// Logisim project basicgates.circ as structural Verilog: 24 circuits, main circuit main
module main (
);

  wire [63:0] multiplier_1_cout, multiplier_1_out;

  // Probe on multiplier_1_out
  Multiplier #(.width(64)) multiplier_1 (
    .a(64'hfffffffff), .b(64'hffffffffffffffee), .out(multiplier_1_out), .cin(64'h1234),
    .cout(multiplier_1_cout));
  // Probe on multiplier_1_cout
  // Probe on nothing
  // Probe on nothing
endmodule

module adder64bit (
  input  inflow,
  input  [63:0] input1,
  input  [63:0] input2,
  output overflow,
  output [63:0] output1
);

  wire and_1_out, and_2_out, and_3_out, and_4_out, and_5_out, and_6_out, and_7_out, and_8_out, and_9_out,
       and_10_out, and_11_out, and_12_out, and_13_out, and_14_out, and_15_out, and_16_out, and_17_out,
       and_18_out, and_19_out, and_20_out, and_21_out, and_22_out, and_23_out, and_24_out, and_25_out,
       and_26_out, and_27_out, and_28_out, and_29_out, and_30_out, and_31_out, and_32_out, and_33_out,
       and_34_out, and_35_out, and_36_out, and_37_out, and_38_out, and_39_out, and_40_out, and_41_out,
       and_42_out, and_43_out, and_44_out, and_45_out, and_46_out, and_47_out, and_48_out, and_49_out,
       and_50_out, and_51_out, and_52_out, and_53_out, and_54_out, and_55_out, and_56_out, and_57_out,
       and_58_out, and_59_out, and_60_out, and_61_out, and_62_out, and_63_out, and_64_out, and_65_out,
       and_66_out, and_67_out, and_68_out, and_69_out, and_70_out, and_71_out, and_72_out, and_73_out,
       and_74_out, and_75_out, and_76_out, and_77_out, and_78_out, and_79_out, and_80_out, and_81_out,
       and_82_out, and_83_out, and_84_out, and_85_out, and_86_out, and_87_out, and_88_out, and_89_out,
       and_90_out, and_91_out, and_92_out, and_93_out, and_94_out, and_95_out, and_96_out, and_97_out,
       and_98_out, and_99_out, and_100_out, and_101_out, and_102_out, and_103_out, and_104_out, and_105_out,
       and_106_out, and_107_out, and_108_out, and_109_out, and_110_out, and_111_out, and_112_out,
       and_113_out, and_114_out, and_115_out, and_116_out, and_117_out, and_118_out, and_119_out,
       and_120_out, and_121_out, and_122_out, and_123_out, and_124_out, and_125_out, and_126_out,
       and_127_out, and_128_out, or_1_out, or_2_out, or_3_out, or_4_out, or_5_out, or_6_out, or_7_out,
       or_8_out, or_9_out, or_10_out, or_11_out, or_12_out, or_13_out, or_14_out, or_15_out, or_16_out,
       or_17_out, or_18_out, or_19_out, or_20_out, or_21_out, or_22_out, or_23_out, or_24_out, or_25_out,
       or_26_out, or_27_out, or_28_out, or_29_out, or_30_out, or_31_out, or_32_out, or_33_out, or_34_out,
       or_35_out, or_36_out, or_37_out, or_38_out, or_39_out, or_40_out, or_41_out, or_42_out, or_43_out,
       or_44_out, or_45_out, or_46_out, or_47_out, or_48_out, or_49_out, or_50_out, or_51_out, or_52_out,
       or_53_out, or_54_out, or_55_out, or_56_out, or_57_out, or_58_out, or_59_out, or_60_out, or_61_out,
       or_62_out, or_63_out, xor_1_out, xor_2_out, xor_3_out, xor_4_out, xor_5_out, xor_6_out, xor_7_out,
       xor_8_out, xor_17_out, xor_18_out, xor_19_out, xor_20_out, xor_21_out, xor_22_out, xor_23_out,
       xor_24_out, xor_33_out, xor_34_out, xor_35_out, xor_36_out, xor_37_out, xor_38_out, xor_39_out,
       xor_40_out, xor_49_out, xor_50_out, xor_51_out, xor_52_out, xor_53_out, xor_54_out, xor_55_out,
       xor_56_out, xor_65_out, xor_66_out, xor_67_out, xor_68_out, xor_69_out, xor_70_out, xor_71_out,
       xor_72_out, xor_81_out, xor_82_out, xor_83_out, xor_84_out, xor_85_out, xor_86_out, xor_87_out,
       xor_88_out, xor_97_out, xor_99_out, xor_101_out, xor_103_out, xor_105_out, xor_107_out, xor_109_out,
       xor_111_out, xor_113_out, xor_114_out, xor_115_out, xor_116_out, xor_117_out, xor_118_out,
       xor_119_out, xor_120_out;

  and and_1 (and_1_out, input1[0], input2[0]);
  xor xor_1 (xor_1_out, input1[0], input2[0]);
  and and_2 (and_2_out, input1[8], input2[8]);
  xor xor_2 (xor_2_out, input1[8], input2[8]);
  and and_3 (and_3_out, input1[16], input2[16]);
  xor xor_3 (xor_3_out, input1[16], input2[16]);
  and and_4 (and_4_out, input1[24], input2[24]);
  xor xor_4 (xor_4_out, input1[24], input2[24]);
  and and_5 (and_5_out, input1[32], input2[32]);
  xor xor_5 (xor_5_out, input1[32], input2[32]);
  and and_6 (and_6_out, input1[40], input2[40]);
  xor xor_6 (xor_6_out, input1[40], input2[40]);
  and and_7 (and_7_out, input1[48], input2[48]);
  xor xor_7 (xor_7_out, input1[48], input2[48]);
  and and_8 (and_8_out, input1[56], input2[56]);
  xor xor_8 (xor_8_out, input1[56], input2[56]);
  and and_9 (and_9_out, inflow, xor_1_out);
  xor xor_9 (output1[0], inflow, xor_1_out);
  and and_10 (and_10_out, or_57_out, xor_2_out);
  xor xor_10 (output1[8], or_57_out, xor_2_out);
  and and_11 (and_11_out, or_58_out, xor_3_out);
  xor xor_11 (output1[16], or_58_out, xor_3_out);
  and and_12 (and_12_out, or_59_out, xor_4_out);
  xor xor_12 (output1[24], or_59_out, xor_4_out);
  and and_13 (and_13_out, or_60_out, xor_5_out);
  xor xor_13 (output1[32], or_60_out, xor_5_out);
  and and_14 (and_14_out, or_61_out, xor_6_out);
  xor xor_14 (output1[40], or_61_out, xor_6_out);
  and and_15 (and_15_out, or_62_out, xor_7_out);
  xor xor_15 (output1[48], or_62_out, xor_7_out);
  and and_16 (and_16_out, or_63_out, xor_8_out);
  xor xor_16 (output1[56], or_63_out, xor_8_out);
  or or_1 (or_1_out, and_1_out, and_9_out);
  and and_17 (and_17_out, input1[1], input2[1]);
  or or_2 (or_2_out, and_2_out, and_10_out);
  and and_18 (and_18_out, input1[9], input2[9]);
  or or_3 (or_3_out, and_3_out, and_11_out);
  and and_19 (and_19_out, input1[17], input2[17]);
  or or_4 (or_4_out, and_4_out, and_12_out);
  and and_20 (and_20_out, input1[25], input2[25]);
  or or_5 (or_5_out, and_5_out, and_13_out);
  and and_21 (and_21_out, input1[33], input2[33]);
  or or_6 (or_6_out, and_6_out, and_14_out);
  and and_22 (and_22_out, input1[41], input2[41]);
  or or_7 (or_7_out, and_7_out, and_15_out);
  and and_23 (and_23_out, input1[49], input2[49]);
  or or_8 (or_8_out, and_8_out, and_16_out);
  and and_24 (and_24_out, input1[57], input2[57]);
  and and_25 (and_25_out, or_1_out, xor_17_out);
  xor xor_17 (xor_17_out, input1[1], input2[1]);
  and and_26 (and_26_out, or_2_out, xor_18_out);
  xor xor_18 (xor_18_out, input1[9], input2[9]);
  and and_27 (and_27_out, or_3_out, xor_19_out);
  xor xor_19 (xor_19_out, input1[17], input2[17]);
  and and_28 (and_28_out, or_4_out, xor_20_out);
  xor xor_20 (xor_20_out, input1[25], input2[25]);
  and and_29 (and_29_out, or_5_out, xor_21_out);
  xor xor_21 (xor_21_out, input1[33], input2[33]);
  and and_30 (and_30_out, or_6_out, xor_22_out);
  xor xor_22 (xor_22_out, input1[41], input2[41]);
  and and_31 (and_31_out, or_7_out, xor_23_out);
  xor xor_23 (xor_23_out, input1[49], input2[49]);
  and and_32 (and_32_out, or_8_out, xor_24_out);
  xor xor_24 (xor_24_out, input1[57], input2[57]);
  or or_9 (or_9_out, and_17_out, and_25_out);
  xor xor_25 (output1[1], or_1_out, xor_17_out);
  or or_10 (or_10_out, and_18_out, and_26_out);
  xor xor_26 (output1[9], or_2_out, xor_18_out);
  or or_11 (or_11_out, and_19_out, and_27_out);
  xor xor_27 (output1[17], or_3_out, xor_19_out);
  or or_12 (or_12_out, and_20_out, and_28_out);
  xor xor_28 (output1[25], or_4_out, xor_20_out);
  or or_13 (or_13_out, and_21_out, and_29_out);
  xor xor_29 (output1[33], or_5_out, xor_21_out);
  or or_14 (or_14_out, and_22_out, and_30_out);
  xor xor_30 (output1[41], or_6_out, xor_22_out);
  or or_15 (or_15_out, and_23_out, and_31_out);
  xor xor_31 (output1[49], or_7_out, xor_23_out);
  or or_16 (or_16_out, and_24_out, and_32_out);
  xor xor_32 (output1[57], or_8_out, xor_24_out);
  and and_33 (and_33_out, input1[2], input2[2]);
  xor xor_33 (xor_33_out, input1[2], input2[2]);
  and and_34 (and_34_out, input1[10], input2[10]);
  xor xor_34 (xor_34_out, input1[10], input2[10]);
  and and_35 (and_35_out, input1[18], input2[18]);
  xor xor_35 (xor_35_out, input1[18], input2[18]);
  and and_36 (and_36_out, input1[26], input2[26]);
  xor xor_36 (xor_36_out, input1[26], input2[26]);
  and and_37 (and_37_out, input1[34], input2[34]);
  xor xor_37 (xor_37_out, input1[34], input2[34]);
  and and_38 (and_38_out, input1[42], input2[42]);
  xor xor_38 (xor_38_out, input1[42], input2[42]);
  and and_39 (and_39_out, input1[50], input2[50]);
  xor xor_39 (xor_39_out, input1[50], input2[50]);
  and and_40 (and_40_out, input1[58], input2[58]);
  xor xor_40 (xor_40_out, input1[58], input2[58]);
  or or_17 (or_17_out, and_33_out, and_41_out);
  and and_41 (and_41_out, or_9_out, xor_33_out);
  xor xor_41 (output1[2], or_9_out, xor_33_out);
  or or_18 (or_18_out, and_34_out, and_42_out);
  and and_42 (and_42_out, or_10_out, xor_34_out);
  xor xor_42 (output1[10], or_10_out, xor_34_out);
  or or_19 (or_19_out, and_35_out, and_43_out);
  and and_43 (and_43_out, or_11_out, xor_35_out);
  xor xor_43 (output1[18], or_11_out, xor_35_out);
  or or_20 (or_20_out, and_36_out, and_44_out);
  and and_44 (and_44_out, or_12_out, xor_36_out);
  xor xor_44 (output1[26], or_12_out, xor_36_out);
  or or_21 (or_21_out, and_37_out, and_45_out);
  and and_45 (and_45_out, or_13_out, xor_37_out);
  xor xor_45 (output1[34], or_13_out, xor_37_out);
  or or_22 (or_22_out, and_38_out, and_46_out);
  and and_46 (and_46_out, or_14_out, xor_38_out);
  xor xor_46 (output1[42], or_14_out, xor_38_out);
  or or_23 (or_23_out, and_39_out, and_47_out);
  and and_47 (and_47_out, or_15_out, xor_39_out);
  xor xor_47 (output1[50], or_15_out, xor_39_out);
  or or_24 (or_24_out, and_40_out, and_48_out);
  and and_48 (and_48_out, or_16_out, xor_40_out);
  xor xor_48 (output1[58], or_16_out, xor_40_out);
  and and_49 (and_49_out, input1[3], input2[3]);
  xor xor_49 (xor_49_out, input1[3], input2[3]);
  and and_50 (and_50_out, input1[11], input2[11]);
  xor xor_50 (xor_50_out, input1[11], input2[11]);
  and and_51 (and_51_out, input1[19], input2[19]);
  xor xor_51 (xor_51_out, input1[19], input2[19]);
  and and_52 (and_52_out, input1[27], input2[27]);
  xor xor_52 (xor_52_out, input1[27], input2[27]);
  and and_53 (and_53_out, input1[35], input2[35]);
  xor xor_53 (xor_53_out, input1[35], input2[35]);
  and and_54 (and_54_out, input1[43], input2[43]);
  xor xor_54 (xor_54_out, input1[43], input2[43]);
  and and_55 (and_55_out, input1[51], input2[51]);
  xor xor_55 (xor_55_out, input1[51], input2[51]);
  and and_56 (and_56_out, input1[59], input2[59]);
  xor xor_56 (xor_56_out, input1[59], input2[59]);
  and and_57 (and_57_out, or_17_out, xor_49_out);
  xor xor_57 (output1[3], or_17_out, xor_49_out);
  and and_58 (and_58_out, or_18_out, xor_50_out);
  xor xor_58 (output1[11], or_18_out, xor_50_out);
  and and_59 (and_59_out, or_19_out, xor_51_out);
  xor xor_59 (output1[19], or_19_out, xor_51_out);
  and and_60 (and_60_out, or_20_out, xor_52_out);
  xor xor_60 (output1[27], or_20_out, xor_52_out);
  and and_61 (and_61_out, or_21_out, xor_53_out);
  xor xor_61 (output1[35], or_21_out, xor_53_out);
  and and_62 (and_62_out, or_22_out, xor_54_out);
  xor xor_62 (output1[43], or_22_out, xor_54_out);
  and and_63 (and_63_out, or_23_out, xor_55_out);
  xor xor_63 (output1[51], or_23_out, xor_55_out);
  and and_64 (and_64_out, or_24_out, xor_56_out);
  xor xor_64 (output1[59], or_24_out, xor_56_out);
  or or_25 (or_25_out, and_49_out, and_57_out);
  or or_26 (or_26_out, and_50_out, and_58_out);
  or or_27 (or_27_out, and_51_out, and_59_out);
  or or_28 (or_28_out, and_52_out, and_60_out);
  or or_29 (or_29_out, and_53_out, and_61_out);
  or or_30 (or_30_out, and_54_out, and_62_out);
  or or_31 (or_31_out, and_55_out, and_63_out);
  or or_32 (or_32_out, and_56_out, and_64_out);
  and and_65 (and_65_out, input1[4], input2[4]);
  xor xor_65 (xor_65_out, input1[4], input2[4]);
  and and_66 (and_66_out, input1[12], input2[12]);
  xor xor_66 (xor_66_out, input1[12], input2[12]);
  and and_67 (and_67_out, input1[20], input2[20]);
  xor xor_67 (xor_67_out, input1[20], input2[20]);
  and and_68 (and_68_out, input1[28], input2[28]);
  xor xor_68 (xor_68_out, input1[28], input2[28]);
  and and_69 (and_69_out, input1[36], input2[36]);
  xor xor_69 (xor_69_out, input1[36], input2[36]);
  and and_70 (and_70_out, input1[44], input2[44]);
  xor xor_70 (xor_70_out, input1[44], input2[44]);
  and and_71 (and_71_out, input1[52], input2[52]);
  xor xor_71 (xor_71_out, input1[52], input2[52]);
  and and_72 (and_72_out, input1[60], input2[60]);
  xor xor_72 (xor_72_out, input1[60], input2[60]);
  or or_33 (or_33_out, and_65_out, and_73_out);
  and and_73 (and_73_out, or_25_out, xor_65_out);
  xor xor_73 (output1[4], or_25_out, xor_65_out);
  or or_34 (or_34_out, and_66_out, and_74_out);
  and and_74 (and_74_out, or_26_out, xor_66_out);
  xor xor_74 (output1[12], or_26_out, xor_66_out);
  or or_35 (or_35_out, and_67_out, and_75_out);
  and and_75 (and_75_out, or_27_out, xor_67_out);
  xor xor_75 (output1[20], or_27_out, xor_67_out);
  or or_36 (or_36_out, and_68_out, and_76_out);
  and and_76 (and_76_out, or_28_out, xor_68_out);
  xor xor_76 (output1[28], or_28_out, xor_68_out);
  or or_37 (or_37_out, and_69_out, and_77_out);
  and and_77 (and_77_out, or_29_out, xor_69_out);
  xor xor_77 (output1[36], or_29_out, xor_69_out);
  or or_38 (or_38_out, and_70_out, and_78_out);
  and and_78 (and_78_out, or_30_out, xor_70_out);
  xor xor_78 (output1[44], or_30_out, xor_70_out);
  or or_39 (or_39_out, and_71_out, and_79_out);
  and and_79 (and_79_out, or_31_out, xor_71_out);
  xor xor_79 (output1[52], or_31_out, xor_71_out);
  or or_40 (or_40_out, and_72_out, and_80_out);
  and and_80 (and_80_out, or_32_out, xor_72_out);
  xor xor_80 (output1[60], or_32_out, xor_72_out);
  and and_81 (and_81_out, input1[5], input2[5]);
  xor xor_81 (xor_81_out, input1[5], input2[5]);
  and and_82 (and_82_out, input1[13], input2[13]);
  xor xor_82 (xor_82_out, input1[13], input2[13]);
  and and_83 (and_83_out, input1[21], input2[21]);
  xor xor_83 (xor_83_out, input1[21], input2[21]);
  and and_84 (and_84_out, input1[29], input2[29]);
  xor xor_84 (xor_84_out, input1[29], input2[29]);
  and and_85 (and_85_out, input1[37], input2[37]);
  xor xor_85 (xor_85_out, input1[37], input2[37]);
  and and_86 (and_86_out, input1[45], input2[45]);
  xor xor_86 (xor_86_out, input1[45], input2[45]);
  and and_87 (and_87_out, input1[53], input2[53]);
  xor xor_87 (xor_87_out, input1[53], input2[53]);
  and and_88 (and_88_out, input1[61], input2[61]);
  xor xor_88 (xor_88_out, input1[61], input2[61]);
  or or_41 (or_41_out, and_81_out, and_89_out);
  and and_89 (and_89_out, or_33_out, xor_81_out);
  xor xor_89 (output1[5], or_33_out, xor_81_out);
  or or_42 (or_42_out, and_82_out, and_90_out);
  and and_90 (and_90_out, or_34_out, xor_82_out);
  xor xor_90 (output1[13], or_34_out, xor_82_out);
  or or_43 (or_43_out, and_83_out, and_91_out);
  and and_91 (and_91_out, or_35_out, xor_83_out);
  xor xor_91 (output1[21], or_35_out, xor_83_out);
  or or_44 (or_44_out, and_84_out, and_92_out);
  and and_92 (and_92_out, or_36_out, xor_84_out);
  xor xor_92 (output1[29], or_36_out, xor_84_out);
  or or_45 (or_45_out, and_85_out, and_93_out);
  and and_93 (and_93_out, or_37_out, xor_85_out);
  xor xor_93 (output1[37], or_37_out, xor_85_out);
  or or_46 (or_46_out, and_86_out, and_94_out);
  and and_94 (and_94_out, or_38_out, xor_86_out);
  xor xor_94 (output1[45], or_38_out, xor_86_out);
  or or_47 (or_47_out, and_87_out, and_95_out);
  and and_95 (and_95_out, or_39_out, xor_87_out);
  xor xor_95 (output1[53], or_39_out, xor_87_out);
  or or_48 (or_48_out, and_88_out, and_96_out);
  and and_96 (and_96_out, or_40_out, xor_88_out);
  xor xor_96 (output1[61], or_40_out, xor_88_out);
  and and_97 (and_97_out, input1[6], input2[6]);
  and and_98 (and_98_out, input1[14], input2[14]);
  and and_99 (and_99_out, input1[22], input2[22]);
  and and_100 (and_100_out, input1[30], input2[30]);
  and and_101 (and_101_out, input1[38], input2[38]);
  and and_102 (and_102_out, input1[46], input2[46]);
  and and_103 (and_103_out, input1[54], input2[54]);
  and and_104 (and_104_out, input1[62], input2[62]);
  and and_105 (and_105_out, or_41_out, xor_97_out);
  xor xor_97 (xor_97_out, input1[6], input2[6]);
  xor xor_98 (output1[6], or_41_out, xor_97_out);
  and and_106 (and_106_out, or_42_out, xor_99_out);
  xor xor_99 (xor_99_out, input1[14], input2[14]);
  xor xor_100 (output1[14], or_42_out, xor_99_out);
  and and_107 (and_107_out, or_43_out, xor_101_out);
  xor xor_101 (xor_101_out, input1[22], input2[22]);
  xor xor_102 (output1[22], or_43_out, xor_101_out);
  and and_108 (and_108_out, or_44_out, xor_103_out);
  xor xor_103 (xor_103_out, input1[30], input2[30]);
  xor xor_104 (output1[30], or_44_out, xor_103_out);
  and and_109 (and_109_out, or_45_out, xor_105_out);
  xor xor_105 (xor_105_out, input1[38], input2[38]);
  xor xor_106 (output1[38], or_45_out, xor_105_out);
  and and_110 (and_110_out, or_46_out, xor_107_out);
  xor xor_107 (xor_107_out, input1[46], input2[46]);
  xor xor_108 (output1[46], or_46_out, xor_107_out);
  and and_111 (and_111_out, or_47_out, xor_109_out);
  xor xor_109 (xor_109_out, input1[54], input2[54]);
  xor xor_110 (output1[54], or_47_out, xor_109_out);
  and and_112 (and_112_out, or_48_out, xor_111_out);
  xor xor_111 (xor_111_out, input1[62], input2[62]);
  xor xor_112 (output1[62], or_48_out, xor_111_out);
  or or_49 (or_49_out, and_97_out, and_105_out);
  or or_50 (or_50_out, and_98_out, and_106_out);
  or or_51 (or_51_out, and_99_out, and_107_out);
  or or_52 (or_52_out, and_100_out, and_108_out);
  or or_53 (or_53_out, and_101_out, and_109_out);
  or or_54 (or_54_out, and_102_out, and_110_out);
  or or_55 (or_55_out, and_103_out, and_111_out);
  or or_56 (or_56_out, and_104_out, and_112_out);
  and and_113 (and_113_out, input1[7], input2[7]);
  xor xor_113 (xor_113_out, input1[7], input2[7]);
  and and_114 (and_114_out, input1[15], input2[15]);
  xor xor_114 (xor_114_out, input1[15], input2[15]);
  and and_115 (and_115_out, input1[23], input2[23]);
  xor xor_115 (xor_115_out, input1[23], input2[23]);
  and and_116 (and_116_out, input1[31], input2[31]);
  xor xor_116 (xor_116_out, input1[31], input2[31]);
  and and_117 (and_117_out, input1[39], input2[39]);
  xor xor_117 (xor_117_out, input1[39], input2[39]);
  and and_118 (and_118_out, input1[47], input2[47]);
  xor xor_118 (xor_118_out, input1[47], input2[47]);
  and and_119 (and_119_out, input1[55], input2[55]);
  xor xor_119 (xor_119_out, input1[55], input2[55]);
  and and_120 (and_120_out, input1[63], input2[63]);
  xor xor_120 (xor_120_out, input1[63], input2[63]);
  or or_57 (or_57_out, and_113_out, and_121_out);
  and and_121 (and_121_out, or_49_out, xor_113_out);
  xor xor_121 (output1[7], or_49_out, xor_113_out);
  or or_58 (or_58_out, and_114_out, and_122_out);
  and and_122 (and_122_out, or_50_out, xor_114_out);
  xor xor_122 (output1[15], or_50_out, xor_114_out);
  or or_59 (or_59_out, and_115_out, and_123_out);
  and and_123 (and_123_out, or_51_out, xor_115_out);
  xor xor_123 (output1[23], or_51_out, xor_115_out);
  or or_60 (or_60_out, and_116_out, and_124_out);
  and and_124 (and_124_out, or_52_out, xor_116_out);
  xor xor_124 (output1[31], or_52_out, xor_116_out);
  or or_61 (or_61_out, and_117_out, and_125_out);
  and and_125 (and_125_out, or_53_out, xor_117_out);
  xor xor_125 (output1[39], or_53_out, xor_117_out);
  or or_62 (or_62_out, and_118_out, and_126_out);
  and and_126 (and_126_out, or_54_out, xor_118_out);
  xor xor_126 (output1[47], or_54_out, xor_118_out);
  or or_63 (or_63_out, and_119_out, and_127_out);
  and and_127 (and_127_out, or_55_out, xor_119_out);
  xor xor_127 (output1[55], or_55_out, xor_119_out);
  or or_64 (overflow, and_120_out, and_128_out);
  and and_128 (and_128_out, or_56_out, xor_120_out);
  xor xor_128 (output1[63], or_56_out, xor_120_out);

  // Notes on the sheet:
  //   input1: initial=0xffffffffffffff
  //   input2: initial=0x1313131313131313
endmodule

module negate64bit (
  input  [63:0] input1,
  output [63:0] output1
);

  wire [63:0] not_1_out;

  assign not_1_out = ~input1;  // NOT_Gate not_1, 64 bits wide
  adder64bit adder64bit_1 (.input1(64'h1), .input2(not_1_out), .output1(output1));  // open: inflow, overflow
endmodule

module subtractor64bit (
  input  inborrow,
  input  [63:0] input1,
  input  [63:0] input2,
  output borrow,
  output [63:0] output1
);

  wire and_1_out, and_2_out, and_3_out, and_4_out, and_5_out, and_6_out, and_7_out, and_8_out, and_9_out,
       and_10_out, and_11_out, and_12_out, and_13_out, and_14_out, and_15_out, and_16_out, and_17_out,
       and_18_out, and_19_out, and_20_out, and_21_out, and_22_out, and_23_out, and_24_out, and_25_out,
       and_26_out, and_27_out, and_28_out, and_29_out, and_30_out, and_31_out, and_32_out, and_33_out,
       and_34_out, and_35_out, and_36_out, and_37_out, and_38_out, and_39_out, and_40_out, and_41_out,
       and_42_out, and_43_out, and_44_out, and_45_out, and_46_out, and_47_out, and_48_out, and_49_out,
       and_50_out, and_51_out, and_52_out, and_53_out, and_54_out, and_55_out, and_56_out, and_57_out,
       and_58_out, and_59_out, and_60_out, and_61_out, and_62_out, and_63_out, and_64_out, and_65_out,
       and_66_out, and_67_out, and_68_out, and_69_out, and_70_out, and_71_out, and_72_out, and_73_out,
       and_74_out, and_75_out, and_76_out, and_77_out, and_78_out, and_79_out, and_80_out, and_81_out,
       and_82_out, and_83_out, and_84_out, and_85_out, and_86_out, and_87_out, and_88_out, and_89_out,
       and_90_out, and_91_out, and_92_out, and_93_out, and_94_out, and_95_out, and_96_out, and_97_out,
       and_98_out, and_99_out, and_100_out, and_101_out, and_102_out, and_103_out, and_104_out, and_105_out,
       and_106_out, and_107_out, and_108_out, and_109_out, and_110_out, and_111_out, and_112_out,
       and_113_out, and_114_out, and_115_out, and_116_out, and_117_out, and_118_out, and_119_out,
       and_120_out, and_121_out, and_122_out, and_123_out, and_124_out, and_125_out, and_126_out,
       and_127_out, and_128_out, not_1_out, not_2_out, not_3_out, not_4_out, not_5_out, not_6_out, not_7_out,
       not_8_out, not_9_out, not_10_out, not_11_out, not_12_out, not_13_out, not_14_out, not_15_out,
       not_16_out, not_17_out, not_18_out, not_19_out, not_20_out, not_21_out, not_22_out, not_23_out,
       not_24_out, not_25_out, not_26_out, not_27_out, not_28_out, not_29_out, not_30_out, not_31_out,
       not_32_out, not_33_out, not_34_out, not_35_out, not_36_out, not_37_out, not_38_out, not_39_out,
       not_40_out, not_41_out, not_42_out, not_43_out, not_44_out, not_45_out, not_46_out, not_47_out,
       not_48_out, not_49_out, not_50_out, not_51_out, not_52_out, not_53_out, not_54_out, not_55_out,
       not_56_out, not_57_out, not_58_out, not_59_out, not_60_out, not_61_out, not_62_out, not_63_out,
       not_64_out, not_65_out, not_66_out, not_67_out, not_68_out, not_69_out, not_70_out, not_71_out,
       not_72_out, not_73_out, not_74_out, not_75_out, not_76_out, not_77_out, not_78_out, not_79_out,
       not_80_out, not_81_out, not_82_out, not_83_out, not_84_out, not_85_out, not_86_out, not_87_out,
       not_88_out, not_89_out, not_90_out, not_91_out, not_92_out, not_93_out, not_94_out, not_95_out,
       not_96_out, not_97_out, not_98_out, not_99_out, not_100_out, not_101_out, not_102_out, not_103_out,
       not_104_out, not_105_out, not_106_out, not_107_out, not_108_out, not_109_out, not_110_out,
       not_111_out, not_112_out, not_113_out, not_114_out, not_115_out, not_116_out, not_117_out,
       not_118_out, not_119_out, not_120_out, not_121_out, not_122_out, not_123_out, not_124_out,
       not_125_out, not_126_out, not_127_out, not_128_out, or_1_out, or_2_out, or_3_out, or_4_out, or_5_out,
       or_6_out, or_7_out, or_8_out, or_9_out, or_10_out, or_11_out, or_12_out, or_13_out, or_14_out,
       or_15_out, or_16_out, or_17_out, or_18_out, or_19_out, or_20_out, or_21_out, or_22_out, or_23_out,
       or_24_out, or_25_out, or_26_out, or_27_out, or_28_out, or_29_out, or_30_out, or_31_out, or_32_out,
       or_33_out, or_34_out, or_35_out, or_36_out, or_37_out, or_38_out, or_39_out, or_40_out, or_41_out,
       or_42_out, or_43_out, or_44_out, or_45_out, or_46_out, or_47_out, or_48_out, or_49_out, or_50_out,
       or_51_out, or_52_out, or_53_out, or_54_out, or_55_out, or_56_out, or_57_out, or_58_out, or_59_out,
       or_60_out, or_61_out, or_62_out, or_63_out, xor_1_out, xor_2_out, xor_3_out, xor_4_out, xor_5_out,
       xor_6_out, xor_7_out, xor_8_out, xor_17_out, xor_18_out, xor_19_out, xor_20_out, xor_21_out,
       xor_22_out, xor_23_out, xor_24_out, xor_33_out, xor_34_out, xor_35_out, xor_36_out, xor_37_out,
       xor_38_out, xor_39_out, xor_40_out, xor_49_out, xor_50_out, xor_51_out, xor_52_out, xor_53_out,
       xor_54_out, xor_55_out, xor_56_out, xor_65_out, xor_66_out, xor_67_out, xor_68_out, xor_69_out,
       xor_70_out, xor_71_out, xor_72_out, xor_81_out, xor_82_out, xor_83_out, xor_84_out, xor_85_out,
       xor_86_out, xor_87_out, xor_88_out, xor_97_out, xor_99_out, xor_101_out, xor_103_out, xor_105_out,
       xor_107_out, xor_109_out, xor_111_out, xor_113_out, xor_114_out, xor_115_out, xor_116_out,
       xor_117_out, xor_118_out, xor_119_out, xor_120_out;

  not not_1 (not_1_out, input1[0]);
  and and_1 (and_1_out, not_1_out, input2[0]);
  xor xor_1 (xor_1_out, input1[0], input2[0]);
  not not_2 (not_2_out, input1[8]);
  and and_2 (and_2_out, not_2_out, input2[8]);
  xor xor_2 (xor_2_out, input1[8], input2[8]);
  not not_3 (not_3_out, input1[16]);
  and and_3 (and_3_out, not_3_out, input2[16]);
  xor xor_3 (xor_3_out, input1[16], input2[16]);
  not not_4 (not_4_out, input1[24]);
  and and_4 (and_4_out, not_4_out, input2[24]);
  xor xor_4 (xor_4_out, input1[24], input2[24]);
  not not_5 (not_5_out, input1[32]);
  and and_5 (and_5_out, not_5_out, input2[32]);
  xor xor_5 (xor_5_out, input1[32], input2[32]);
  not not_6 (not_6_out, input1[40]);
  and and_6 (and_6_out, not_6_out, input2[40]);
  xor xor_6 (xor_6_out, input1[40], input2[40]);
  not not_7 (not_7_out, input1[48]);
  and and_7 (and_7_out, not_7_out, input2[48]);
  xor xor_7 (xor_7_out, input1[48], input2[48]);
  not not_8 (not_8_out, input1[56]);
  and and_8 (and_8_out, not_8_out, input2[56]);
  xor xor_8 (xor_8_out, input1[56], input2[56]);
  and and_9 (and_9_out, inborrow, not_9_out);
  not not_9 (not_9_out, xor_1_out);
  xor xor_9 (output1[0], inborrow, xor_1_out);
  and and_10 (and_10_out, or_57_out, not_10_out);
  not not_10 (not_10_out, xor_2_out);
  xor xor_10 (output1[8], or_57_out, xor_2_out);
  and and_11 (and_11_out, or_58_out, not_11_out);
  not not_11 (not_11_out, xor_3_out);
  xor xor_11 (output1[16], or_58_out, xor_3_out);
  and and_12 (and_12_out, or_59_out, not_12_out);
  not not_12 (not_12_out, xor_4_out);
  xor xor_12 (output1[24], or_59_out, xor_4_out);
  and and_13 (and_13_out, or_60_out, not_13_out);
  not not_13 (not_13_out, xor_5_out);
  xor xor_13 (output1[32], or_60_out, xor_5_out);
  and and_14 (and_14_out, or_61_out, not_14_out);
  not not_14 (not_14_out, xor_6_out);
  xor xor_14 (output1[40], or_61_out, xor_6_out);
  and and_15 (and_15_out, or_62_out, not_15_out);
  not not_15 (not_15_out, xor_7_out);
  xor xor_15 (output1[48], or_62_out, xor_7_out);
  and and_16 (and_16_out, or_63_out, not_16_out);
  not not_16 (not_16_out, xor_8_out);
  xor xor_16 (output1[56], or_63_out, xor_8_out);
  not not_17 (not_17_out, input1[1]);
  or or_1 (or_1_out, and_1_out, and_9_out);
  and and_17 (and_17_out, not_17_out, input2[1]);
  not not_18 (not_18_out, input1[9]);
  or or_2 (or_2_out, and_2_out, and_10_out);
  and and_18 (and_18_out, not_18_out, input2[9]);
  not not_19 (not_19_out, input1[17]);
  or or_3 (or_3_out, and_3_out, and_11_out);
  and and_19 (and_19_out, not_19_out, input2[17]);
  not not_20 (not_20_out, input1[25]);
  or or_4 (or_4_out, and_4_out, and_12_out);
  and and_20 (and_20_out, not_20_out, input2[25]);
  not not_21 (not_21_out, input1[33]);
  or or_5 (or_5_out, and_5_out, and_13_out);
  and and_21 (and_21_out, not_21_out, input2[33]);
  not not_22 (not_22_out, input1[41]);
  or or_6 (or_6_out, and_6_out, and_14_out);
  and and_22 (and_22_out, not_22_out, input2[41]);
  not not_23 (not_23_out, input1[49]);
  or or_7 (or_7_out, and_7_out, and_15_out);
  and and_23 (and_23_out, not_23_out, input2[49]);
  not not_24 (not_24_out, input1[57]);
  or or_8 (or_8_out, and_8_out, and_16_out);
  and and_24 (and_24_out, not_24_out, input2[57]);
  not not_25 (not_25_out, xor_17_out);
  xor xor_17 (xor_17_out, input1[1], input2[1]);
  not not_26 (not_26_out, xor_18_out);
  xor xor_18 (xor_18_out, input1[9], input2[9]);
  not not_27 (not_27_out, xor_19_out);
  xor xor_19 (xor_19_out, input1[17], input2[17]);
  not not_28 (not_28_out, xor_20_out);
  xor xor_20 (xor_20_out, input1[25], input2[25]);
  not not_29 (not_29_out, xor_21_out);
  xor xor_21 (xor_21_out, input1[33], input2[33]);
  not not_30 (not_30_out, xor_22_out);
  xor xor_22 (xor_22_out, input1[41], input2[41]);
  not not_31 (not_31_out, xor_23_out);
  xor xor_23 (xor_23_out, input1[49], input2[49]);
  not not_32 (not_32_out, xor_24_out);
  xor xor_24 (xor_24_out, input1[57], input2[57]);
  not not_33 (not_33_out, input1[2]);
  or or_9 (or_9_out, and_17_out, and_25_out);
  and and_25 (and_25_out, or_1_out, not_25_out);
  xor xor_25 (output1[1], or_1_out, xor_17_out);
  not not_34 (not_34_out, input1[10]);
  or or_10 (or_10_out, and_18_out, and_26_out);
  and and_26 (and_26_out, or_2_out, not_26_out);
  xor xor_26 (output1[9], or_2_out, xor_18_out);
  not not_35 (not_35_out, input1[18]);
  or or_11 (or_11_out, and_19_out, and_27_out);
  and and_27 (and_27_out, or_3_out, not_27_out);
  xor xor_27 (output1[17], or_3_out, xor_19_out);
  not not_36 (not_36_out, input1[26]);
  or or_12 (or_12_out, and_20_out, and_28_out);
  and and_28 (and_28_out, or_4_out, not_28_out);
  xor xor_28 (output1[25], or_4_out, xor_20_out);
  not not_37 (not_37_out, input1[34]);
  or or_13 (or_13_out, and_21_out, and_29_out);
  and and_29 (and_29_out, or_5_out, not_29_out);
  xor xor_29 (output1[33], or_5_out, xor_21_out);
  not not_38 (not_38_out, input1[42]);
  or or_14 (or_14_out, and_22_out, and_30_out);
  and and_30 (and_30_out, or_6_out, not_30_out);
  xor xor_30 (output1[41], or_6_out, xor_22_out);
  not not_39 (not_39_out, input1[50]);
  or or_15 (or_15_out, and_23_out, and_31_out);
  and and_31 (and_31_out, or_7_out, not_31_out);
  xor xor_31 (output1[49], or_7_out, xor_23_out);
  not not_40 (not_40_out, input1[58]);
  or or_16 (or_16_out, and_24_out, and_32_out);
  and and_32 (and_32_out, or_8_out, not_32_out);
  xor xor_32 (output1[57], or_8_out, xor_24_out);
  and and_33 (and_33_out, not_33_out, input2[2]);
  xor xor_33 (xor_33_out, input1[2], input2[2]);
  and and_34 (and_34_out, not_34_out, input2[10]);
  xor xor_34 (xor_34_out, input1[10], input2[10]);
  and and_35 (and_35_out, not_35_out, input2[18]);
  xor xor_35 (xor_35_out, input1[18], input2[18]);
  and and_36 (and_36_out, not_36_out, input2[26]);
  xor xor_36 (xor_36_out, input1[26], input2[26]);
  and and_37 (and_37_out, not_37_out, input2[34]);
  xor xor_37 (xor_37_out, input1[34], input2[34]);
  and and_38 (and_38_out, not_38_out, input2[42]);
  xor xor_38 (xor_38_out, input1[42], input2[42]);
  and and_39 (and_39_out, not_39_out, input2[50]);
  xor xor_39 (xor_39_out, input1[50], input2[50]);
  and and_40 (and_40_out, not_40_out, input2[58]);
  xor xor_40 (xor_40_out, input1[58], input2[58]);
  or or_17 (or_17_out, and_33_out, and_41_out);
  and and_41 (and_41_out, or_9_out, not_41_out);
  not not_41 (not_41_out, xor_33_out);
  xor xor_41 (output1[2], or_9_out, xor_33_out);
  or or_18 (or_18_out, and_34_out, and_42_out);
  and and_42 (and_42_out, or_10_out, not_42_out);
  not not_42 (not_42_out, xor_34_out);
  xor xor_42 (output1[10], or_10_out, xor_34_out);
  or or_19 (or_19_out, and_35_out, and_43_out);
  and and_43 (and_43_out, or_11_out, not_43_out);
  not not_43 (not_43_out, xor_35_out);
  xor xor_43 (output1[18], or_11_out, xor_35_out);
  or or_20 (or_20_out, and_36_out, and_44_out);
  and and_44 (and_44_out, or_12_out, not_44_out);
  not not_44 (not_44_out, xor_36_out);
  xor xor_44 (output1[26], or_12_out, xor_36_out);
  or or_21 (or_21_out, and_37_out, and_45_out);
  and and_45 (and_45_out, or_13_out, not_45_out);
  not not_45 (not_45_out, xor_37_out);
  xor xor_45 (output1[34], or_13_out, xor_37_out);
  or or_22 (or_22_out, and_38_out, and_46_out);
  and and_46 (and_46_out, or_14_out, not_46_out);
  not not_46 (not_46_out, xor_38_out);
  xor xor_46 (output1[42], or_14_out, xor_38_out);
  or or_23 (or_23_out, and_39_out, and_47_out);
  and and_47 (and_47_out, or_15_out, not_47_out);
  not not_47 (not_47_out, xor_39_out);
  xor xor_47 (output1[50], or_15_out, xor_39_out);
  or or_24 (or_24_out, and_40_out, and_48_out);
  and and_48 (and_48_out, or_16_out, not_48_out);
  not not_48 (not_48_out, xor_40_out);
  xor xor_48 (output1[58], or_16_out, xor_40_out);
  not not_49 (not_49_out, input1[3]);
  and and_49 (and_49_out, not_49_out, input2[3]);
  xor xor_49 (xor_49_out, input1[3], input2[3]);
  not not_50 (not_50_out, input1[11]);
  and and_50 (and_50_out, not_50_out, input2[11]);
  xor xor_50 (xor_50_out, input1[11], input2[11]);
  not not_51 (not_51_out, input1[19]);
  and and_51 (and_51_out, not_51_out, input2[19]);
  xor xor_51 (xor_51_out, input1[19], input2[19]);
  not not_52 (not_52_out, input1[27]);
  and and_52 (and_52_out, not_52_out, input2[27]);
  xor xor_52 (xor_52_out, input1[27], input2[27]);
  not not_53 (not_53_out, input1[35]);
  and and_53 (and_53_out, not_53_out, input2[35]);
  xor xor_53 (xor_53_out, input1[35], input2[35]);
  not not_54 (not_54_out, input1[43]);
  and and_54 (and_54_out, not_54_out, input2[43]);
  xor xor_54 (xor_54_out, input1[43], input2[43]);
  not not_55 (not_55_out, input1[51]);
  and and_55 (and_55_out, not_55_out, input2[51]);
  xor xor_55 (xor_55_out, input1[51], input2[51]);
  not not_56 (not_56_out, input1[59]);
  and and_56 (and_56_out, not_56_out, input2[59]);
  xor xor_56 (xor_56_out, input1[59], input2[59]);
  and and_57 (and_57_out, or_17_out, not_57_out);
  not not_57 (not_57_out, xor_49_out);
  xor xor_57 (output1[3], or_17_out, xor_49_out);
  and and_58 (and_58_out, or_18_out, not_58_out);
  not not_58 (not_58_out, xor_50_out);
  xor xor_58 (output1[11], or_18_out, xor_50_out);
  and and_59 (and_59_out, or_19_out, not_59_out);
  not not_59 (not_59_out, xor_51_out);
  xor xor_59 (output1[19], or_19_out, xor_51_out);
  and and_60 (and_60_out, or_20_out, not_60_out);
  not not_60 (not_60_out, xor_52_out);
  xor xor_60 (output1[27], or_20_out, xor_52_out);
  and and_61 (and_61_out, or_21_out, not_61_out);
  not not_61 (not_61_out, xor_53_out);
  xor xor_61 (output1[35], or_21_out, xor_53_out);
  and and_62 (and_62_out, or_22_out, not_62_out);
  not not_62 (not_62_out, xor_54_out);
  xor xor_62 (output1[43], or_22_out, xor_54_out);
  and and_63 (and_63_out, or_23_out, not_63_out);
  not not_63 (not_63_out, xor_55_out);
  xor xor_63 (output1[51], or_23_out, xor_55_out);
  and and_64 (and_64_out, or_24_out, not_64_out);
  not not_64 (not_64_out, xor_56_out);
  xor xor_64 (output1[59], or_24_out, xor_56_out);
  not not_65 (not_65_out, input1[4]);
  or or_25 (or_25_out, and_49_out, and_57_out);
  not not_66 (not_66_out, input1[12]);
  or or_26 (or_26_out, and_50_out, and_58_out);
  not not_67 (not_67_out, input1[20]);
  or or_27 (or_27_out, and_51_out, and_59_out);
  not not_68 (not_68_out, input1[28]);
  or or_28 (or_28_out, and_52_out, and_60_out);
  not not_69 (not_69_out, input1[36]);
  or or_29 (or_29_out, and_53_out, and_61_out);
  not not_70 (not_70_out, input1[44]);
  or or_30 (or_30_out, and_54_out, and_62_out);
  not not_71 (not_71_out, input1[52]);
  or or_31 (or_31_out, and_55_out, and_63_out);
  not not_72 (not_72_out, input1[60]);
  or or_32 (or_32_out, and_56_out, and_64_out);
  and and_65 (and_65_out, not_65_out, input2[4]);
  not not_73 (not_73_out, xor_65_out);
  xor xor_65 (xor_65_out, input1[4], input2[4]);
  and and_66 (and_66_out, not_66_out, input2[12]);
  not not_74 (not_74_out, xor_66_out);
  xor xor_66 (xor_66_out, input1[12], input2[12]);
  and and_67 (and_67_out, not_67_out, input2[20]);
  not not_75 (not_75_out, xor_67_out);
  xor xor_67 (xor_67_out, input1[20], input2[20]);
  and and_68 (and_68_out, not_68_out, input2[28]);
  not not_76 (not_76_out, xor_68_out);
  xor xor_68 (xor_68_out, input1[28], input2[28]);
  and and_69 (and_69_out, not_69_out, input2[36]);
  not not_77 (not_77_out, xor_69_out);
  xor xor_69 (xor_69_out, input1[36], input2[36]);
  and and_70 (and_70_out, not_70_out, input2[44]);
  not not_78 (not_78_out, xor_70_out);
  xor xor_70 (xor_70_out, input1[44], input2[44]);
  and and_71 (and_71_out, not_71_out, input2[52]);
  not not_79 (not_79_out, xor_71_out);
  xor xor_71 (xor_71_out, input1[52], input2[52]);
  and and_72 (and_72_out, not_72_out, input2[60]);
  not not_80 (not_80_out, xor_72_out);
  xor xor_72 (xor_72_out, input1[60], input2[60]);
  or or_33 (or_33_out, and_65_out, and_73_out);
  and and_73 (and_73_out, or_25_out, not_73_out);
  xor xor_73 (output1[4], or_25_out, xor_65_out);
  or or_34 (or_34_out, and_66_out, and_74_out);
  and and_74 (and_74_out, or_26_out, not_74_out);
  xor xor_74 (output1[12], or_26_out, xor_66_out);
  or or_35 (or_35_out, and_67_out, and_75_out);
  and and_75 (and_75_out, or_27_out, not_75_out);
  xor xor_75 (output1[20], or_27_out, xor_67_out);
  or or_36 (or_36_out, and_68_out, and_76_out);
  and and_76 (and_76_out, or_28_out, not_76_out);
  xor xor_76 (output1[28], or_28_out, xor_68_out);
  or or_37 (or_37_out, and_69_out, and_77_out);
  and and_77 (and_77_out, or_29_out, not_77_out);
  xor xor_77 (output1[36], or_29_out, xor_69_out);
  or or_38 (or_38_out, and_70_out, and_78_out);
  and and_78 (and_78_out, or_30_out, not_78_out);
  xor xor_78 (output1[44], or_30_out, xor_70_out);
  or or_39 (or_39_out, and_71_out, and_79_out);
  and and_79 (and_79_out, or_31_out, not_79_out);
  xor xor_79 (output1[52], or_31_out, xor_71_out);
  or or_40 (or_40_out, and_72_out, and_80_out);
  and and_80 (and_80_out, or_32_out, not_80_out);
  xor xor_80 (output1[60], or_32_out, xor_72_out);
  not not_81 (not_81_out, input1[5]);
  and and_81 (and_81_out, not_81_out, input2[5]);
  xor xor_81 (xor_81_out, input1[5], input2[5]);
  not not_82 (not_82_out, input1[13]);
  and and_82 (and_82_out, not_82_out, input2[13]);
  xor xor_82 (xor_82_out, input1[13], input2[13]);
  not not_83 (not_83_out, input1[21]);
  and and_83 (and_83_out, not_83_out, input2[21]);
  xor xor_83 (xor_83_out, input1[21], input2[21]);
  not not_84 (not_84_out, input1[29]);
  and and_84 (and_84_out, not_84_out, input2[29]);
  xor xor_84 (xor_84_out, input1[29], input2[29]);
  not not_85 (not_85_out, input1[37]);
  and and_85 (and_85_out, not_85_out, input2[37]);
  xor xor_85 (xor_85_out, input1[37], input2[37]);
  not not_86 (not_86_out, input1[45]);
  and and_86 (and_86_out, not_86_out, input2[45]);
  xor xor_86 (xor_86_out, input1[45], input2[45]);
  not not_87 (not_87_out, input1[53]);
  and and_87 (and_87_out, not_87_out, input2[53]);
  xor xor_87 (xor_87_out, input1[53], input2[53]);
  not not_88 (not_88_out, input1[61]);
  and and_88 (and_88_out, not_88_out, input2[61]);
  xor xor_88 (xor_88_out, input1[61], input2[61]);
  and and_89 (and_89_out, or_33_out, not_89_out);
  not not_89 (not_89_out, xor_81_out);
  xor xor_89 (output1[5], or_33_out, xor_81_out);
  and and_90 (and_90_out, or_34_out, not_90_out);
  not not_90 (not_90_out, xor_82_out);
  xor xor_90 (output1[13], or_34_out, xor_82_out);
  and and_91 (and_91_out, or_35_out, not_91_out);
  not not_91 (not_91_out, xor_83_out);
  xor xor_91 (output1[21], or_35_out, xor_83_out);
  and and_92 (and_92_out, or_36_out, not_92_out);
  not not_92 (not_92_out, xor_84_out);
  xor xor_92 (output1[29], or_36_out, xor_84_out);
  and and_93 (and_93_out, or_37_out, not_93_out);
  not not_93 (not_93_out, xor_85_out);
  xor xor_93 (output1[37], or_37_out, xor_85_out);
  and and_94 (and_94_out, or_38_out, not_94_out);
  not not_94 (not_94_out, xor_86_out);
  xor xor_94 (output1[45], or_38_out, xor_86_out);
  and and_95 (and_95_out, or_39_out, not_95_out);
  not not_95 (not_95_out, xor_87_out);
  xor xor_95 (output1[53], or_39_out, xor_87_out);
  and and_96 (and_96_out, or_40_out, not_96_out);
  not not_96 (not_96_out, xor_88_out);
  xor xor_96 (output1[61], or_40_out, xor_88_out);
  not not_97 (not_97_out, input1[6]);
  or or_41 (or_41_out, and_81_out, and_89_out);
  and and_97 (and_97_out, not_97_out, input2[6]);
  not not_98 (not_98_out, input1[14]);
  or or_42 (or_42_out, and_82_out, and_90_out);
  and and_98 (and_98_out, not_98_out, input2[14]);
  not not_99 (not_99_out, input1[22]);
  or or_43 (or_43_out, and_83_out, and_91_out);
  and and_99 (and_99_out, not_99_out, input2[22]);
  not not_100 (not_100_out, input1[30]);
  or or_44 (or_44_out, and_84_out, and_92_out);
  and and_100 (and_100_out, not_100_out, input2[30]);
  not not_101 (not_101_out, input1[38]);
  or or_45 (or_45_out, and_85_out, and_93_out);
  and and_101 (and_101_out, not_101_out, input2[38]);
  not not_102 (not_102_out, input1[46]);
  or or_46 (or_46_out, and_86_out, and_94_out);
  and and_102 (and_102_out, not_102_out, input2[46]);
  not not_103 (not_103_out, input1[54]);
  or or_47 (or_47_out, and_87_out, and_95_out);
  and and_103 (and_103_out, not_103_out, input2[54]);
  not not_104 (not_104_out, input1[62]);
  or or_48 (or_48_out, and_88_out, and_96_out);
  and and_104 (and_104_out, not_104_out, input2[62]);
  and and_105 (and_105_out, or_41_out, not_105_out);
  not not_105 (not_105_out, xor_97_out);
  xor xor_97 (xor_97_out, input1[6], input2[6]);
  xor xor_98 (output1[6], or_41_out, xor_97_out);
  and and_106 (and_106_out, or_42_out, not_106_out);
  not not_106 (not_106_out, xor_99_out);
  xor xor_99 (xor_99_out, input1[14], input2[14]);
  xor xor_100 (output1[14], or_42_out, xor_99_out);
  and and_107 (and_107_out, or_43_out, not_107_out);
  not not_107 (not_107_out, xor_101_out);
  xor xor_101 (xor_101_out, input1[22], input2[22]);
  xor xor_102 (output1[22], or_43_out, xor_101_out);
  and and_108 (and_108_out, or_44_out, not_108_out);
  not not_108 (not_108_out, xor_103_out);
  xor xor_103 (xor_103_out, input1[30], input2[30]);
  xor xor_104 (output1[30], or_44_out, xor_103_out);
  and and_109 (and_109_out, or_45_out, not_109_out);
  not not_109 (not_109_out, xor_105_out);
  xor xor_105 (xor_105_out, input1[38], input2[38]);
  xor xor_106 (output1[38], or_45_out, xor_105_out);
  and and_110 (and_110_out, or_46_out, not_110_out);
  not not_110 (not_110_out, xor_107_out);
  xor xor_107 (xor_107_out, input1[46], input2[46]);
  xor xor_108 (output1[46], or_46_out, xor_107_out);
  and and_111 (and_111_out, or_47_out, not_111_out);
  not not_111 (not_111_out, xor_109_out);
  xor xor_109 (xor_109_out, input1[54], input2[54]);
  xor xor_110 (output1[54], or_47_out, xor_109_out);
  and and_112 (and_112_out, or_48_out, not_112_out);
  not not_112 (not_112_out, xor_111_out);
  xor xor_111 (xor_111_out, input1[62], input2[62]);
  xor xor_112 (output1[62], or_48_out, xor_111_out);
  not not_113 (not_113_out, input1[7]);
  or or_49 (or_49_out, and_97_out, and_105_out);
  not not_114 (not_114_out, input1[15]);
  or or_50 (or_50_out, and_98_out, and_106_out);
  not not_115 (not_115_out, input1[23]);
  or or_51 (or_51_out, and_99_out, and_107_out);
  not not_116 (not_116_out, input1[31]);
  or or_52 (or_52_out, and_100_out, and_108_out);
  not not_117 (not_117_out, input1[39]);
  or or_53 (or_53_out, and_101_out, and_109_out);
  not not_118 (not_118_out, input1[47]);
  or or_54 (or_54_out, and_102_out, and_110_out);
  not not_119 (not_119_out, input1[55]);
  or or_55 (or_55_out, and_103_out, and_111_out);
  not not_120 (not_120_out, input1[63]);
  or or_56 (or_56_out, and_104_out, and_112_out);
  and and_113 (and_113_out, not_113_out, input2[7]);
  not not_121 (not_121_out, xor_113_out);
  xor xor_113 (xor_113_out, input1[7], input2[7]);
  and and_114 (and_114_out, not_114_out, input2[15]);
  not not_122 (not_122_out, xor_114_out);
  xor xor_114 (xor_114_out, input1[15], input2[15]);
  and and_115 (and_115_out, not_115_out, input2[23]);
  not not_123 (not_123_out, xor_115_out);
  xor xor_115 (xor_115_out, input1[23], input2[23]);
  and and_116 (and_116_out, not_116_out, input2[31]);
  not not_124 (not_124_out, xor_116_out);
  xor xor_116 (xor_116_out, input1[31], input2[31]);
  and and_117 (and_117_out, not_117_out, input2[39]);
  not not_125 (not_125_out, xor_117_out);
  xor xor_117 (xor_117_out, input1[39], input2[39]);
  and and_118 (and_118_out, not_118_out, input2[47]);
  not not_126 (not_126_out, xor_118_out);
  xor xor_118 (xor_118_out, input1[47], input2[47]);
  and and_119 (and_119_out, not_119_out, input2[55]);
  not not_127 (not_127_out, xor_119_out);
  xor xor_119 (xor_119_out, input1[55], input2[55]);
  and and_120 (and_120_out, not_120_out, input2[63]);
  not not_128 (not_128_out, xor_120_out);
  xor xor_120 (xor_120_out, input1[63], input2[63]);
  or or_57 (or_57_out, and_113_out, and_121_out);
  and and_121 (and_121_out, or_49_out, not_121_out);
  xor xor_121 (output1[7], or_49_out, xor_113_out);
  or or_58 (or_58_out, and_114_out, and_122_out);
  and and_122 (and_122_out, or_50_out, not_122_out);
  xor xor_122 (output1[15], or_50_out, xor_114_out);
  or or_59 (or_59_out, and_115_out, and_123_out);
  and and_123 (and_123_out, or_51_out, not_123_out);
  xor xor_123 (output1[23], or_51_out, xor_115_out);
  or or_60 (or_60_out, and_116_out, and_124_out);
  and and_124 (and_124_out, or_52_out, not_124_out);
  xor xor_124 (output1[31], or_52_out, xor_116_out);
  or or_61 (or_61_out, and_117_out, and_125_out);
  and and_125 (and_125_out, or_53_out, not_125_out);
  xor xor_125 (output1[39], or_53_out, xor_117_out);
  or or_62 (or_62_out, and_118_out, and_126_out);
  and and_126 (and_126_out, or_54_out, not_126_out);
  xor xor_126 (output1[47], or_54_out, xor_118_out);
  or or_63 (or_63_out, and_119_out, and_127_out);
  and and_127 (and_127_out, or_55_out, not_127_out);
  xor xor_127 (output1[55], or_55_out, xor_119_out);
  or or_64 (borrow, and_120_out, and_128_out);
  and and_128 (and_128_out, or_56_out, not_128_out);
  xor xor_128 (output1[63], or_56_out, xor_120_out);

  // Notes on the sheet:
  //   input1: initial=0x1313131313131313
  //   input2: initial=0xffffffffffffff
endmodule

module adder128bit (
  input  inflow,
  input  [63:0] input1a,
  input  [63:0] input1b,
  input  [63:0] input2a,
  input  [63:0] input2b,
  output overflow,
  output [63:0] output1a,
  output [63:0] output1b
);

  wire adder64bit_1_overflow;

  adder64bit adder64bit_1 (
    .inflow(inflow), .input1(input1a), .input2(input2a), .overflow(adder64bit_1_overflow), .output1(output1a));
  adder64bit adder64bit_2 (
    .inflow(adder64bit_1_overflow), .input1(input1b), .input2(input2b), .overflow(overflow),
    .output1(output1b));
endmodule

module negate128bit (
  input  [63:0] input1a,
  input  [63:0] input1b,
  output [63:0] output1a,
  output [63:0] output1b
);

  wire [63:0] not_1_out, not_2_out;

  assign not_1_out = ~input1a;  // NOT_Gate not_1, 64 bits wide
  assign not_2_out = ~input1b;  // NOT_Gate not_2, 64 bits wide
  adder128bit adder128bit_1 (
    .input1a(64'h1), .input2a(not_1_out), .input2b(not_2_out), .output1a(output1a), .output1b(output1b));  // open: inflow, input1b, overflow
endmodule

module subtractor128bit (
  input  inborrow,
  input  [63:0] input1a,
  input  [63:0] input1b,
  input  [63:0] input2a,
  input  [63:0] input2b,
  output borrow,
  output [63:0] output1a,
  output [63:0] output1b
);

  wire subtractor64bit_1_borrow;

  subtractor64bit subtractor64bit_1 (
    .inborrow(inborrow), .input1(input1a), .input2(input2a), .borrow(subtractor64bit_1_borrow),
    .output1(output1a));
  subtractor64bit subtractor64bit_2 (
    .inborrow(subtractor64bit_1_borrow), .input1(input1b), .input2(input2b), .borrow(borrow),
    .output1(output1b));
endmodule

module cbuffer64bit (
  input  buffer1,
  input  [63:0] input1,
  output [63:0] output1
);

  assign output1 = {64{buffer1}} & input1;  // AND_Gate and_1, 64 bits wide
endmodule

module cbuffer128bit (
  input  buffer1,
  input  [63:0] input1a,
  input  [63:0] input1b,
  output [63:0] output1a,
  output [63:0] output1b
);

  assign output1a = {64{buffer1}} & input1a;  // AND_Gate and_1, 64 bits wide
  assign output1b = {64{buffer1}} & input1b;  // AND_Gate and_2, 64 bits wide
endmodule

module multiplier64bit (
  input  [63:0] inflow,
  input  [63:0] input1,
  input  [63:0] input2,
  output [63:0] overflow,
  output [63:0] output1
);

  wire [63:0] adder128bit_1_output1a, adder128bit_1_output1b, adder128bit_2_output1a, adder128bit_2_output1b,
       adder128bit_3_output1a, adder128bit_3_output1b, adder128bit_4_output1a, adder128bit_4_output1b,
       adder128bit_5_output1a, adder128bit_5_output1b, adder128bit_6_output1a, adder128bit_6_output1b,
       adder128bit_7_output1a, adder128bit_7_output1b, adder128bit_8_output1a, adder128bit_8_output1b,
       adder128bit_9_output1a, adder128bit_9_output1b, adder128bit_10_output1a, adder128bit_10_output1b,
       adder128bit_11_output1a, adder128bit_11_output1b, adder128bit_12_output1a, adder128bit_12_output1b,
       adder128bit_13_output1a, adder128bit_13_output1b, adder128bit_14_output1a, adder128bit_14_output1b,
       adder128bit_15_output1a, adder128bit_15_output1b, adder128bit_16_output1a, adder128bit_16_output1b,
       adder128bit_17_output1a, adder128bit_17_output1b, adder128bit_18_output1a, adder128bit_18_output1b,
       adder128bit_19_output1a, adder128bit_19_output1b, adder128bit_20_output1a, adder128bit_20_output1b,
       adder128bit_21_output1a, adder128bit_21_output1b, adder128bit_22_output1a, adder128bit_22_output1b,
       adder128bit_23_output1a, adder128bit_23_output1b, adder128bit_24_output1a, adder128bit_24_output1b,
       adder128bit_25_output1a, adder128bit_25_output1b, adder128bit_26_output1a, adder128bit_26_output1b,
       adder128bit_27_output1a, adder128bit_27_output1b, adder128bit_28_output1a, adder128bit_28_output1b,
       adder128bit_29_output1a, adder128bit_29_output1b, adder128bit_30_output1a, adder128bit_30_output1b,
       adder128bit_31_output1a, adder128bit_31_output1b, adder128bit_33_output1a, adder128bit_33_output1b,
       adder128bit_34_output1a, adder128bit_34_output1b, adder128bit_35_output1a, adder128bit_35_output1b,
       adder128bit_36_output1a, adder128bit_36_output1b, adder128bit_37_output1a, adder128bit_37_output1b,
       adder128bit_38_output1a, adder128bit_38_output1b, adder128bit_39_output1a, adder128bit_39_output1b,
       adder128bit_40_output1a, adder128bit_40_output1b, adder128bit_41_output1a, adder128bit_41_output1b,
       adder128bit_42_output1a, adder128bit_42_output1b, adder128bit_43_output1a, adder128bit_43_output1b,
       adder128bit_44_output1a, adder128bit_44_output1b, adder128bit_45_output1a, adder128bit_45_output1b,
       adder128bit_46_output1a, adder128bit_46_output1b, adder128bit_47_output1a, adder128bit_47_output1b,
       adder128bit_48_output1a, adder128bit_48_output1b, adder128bit_49_output1a, adder128bit_49_output1b,
       adder128bit_50_output1a, adder128bit_50_output1b, adder128bit_51_output1a, adder128bit_51_output1b,
       adder128bit_52_output1a, adder128bit_52_output1b, adder128bit_53_output1a, adder128bit_53_output1b,
       adder128bit_54_output1a, adder128bit_54_output1b, adder128bit_55_output1a, adder128bit_55_output1b,
       adder128bit_56_output1a, adder128bit_56_output1b, adder128bit_57_output1a, adder128bit_57_output1b,
       adder128bit_58_output1a, adder128bit_58_output1b, adder128bit_59_output1a, adder128bit_59_output1b,
       adder128bit_60_output1a, adder128bit_60_output1b, adder128bit_61_output1a, adder128bit_61_output1b,
       adder128bit_62_output1a, adder128bit_62_output1b, adder128bit_63_output1a, adder128bit_63_output1b,
       adder128bit_64_output1a, adder128bit_64_output1b, controlled_buffer_1_out, controlled_buffer_8_out,
       controlled_buffer_16_out, controlled_buffer_24_out, controlled_buffer_32_out,
       controlled_buffer_40_out, controlled_buffer_48_out, controlled_buffer_56_out, pull_resistor_1_node,
       pull_resistor_2_node, pull_resistor_3_node, pull_resistor_5_node, pull_resistor_6_node,
       pull_resistor_7_node, pull_resistor_8_node, pull_resistor_9_node, pull_resistor_10_node,
       pull_resistor_11_node, pull_resistor_13_node, pull_resistor_14_node, pull_resistor_15_node,
       pull_resistor_16_node, pull_resistor_17_node, pull_resistor_18_node, pull_resistor_19_node,
       pull_resistor_21_node, pull_resistor_22_node, pull_resistor_23_node, pull_resistor_24_node,
       pull_resistor_25_node, pull_resistor_26_node, pull_resistor_27_node, pull_resistor_29_node,
       pull_resistor_30_node, pull_resistor_31_node, pull_resistor_32_node, pull_resistor_33_node,
       pull_resistor_34_node, pull_resistor_35_node, pull_resistor_37_node, pull_resistor_38_node,
       pull_resistor_39_node, pull_resistor_40_node, pull_resistor_41_node, pull_resistor_42_node,
       pull_resistor_43_node, pull_resistor_45_node, pull_resistor_46_node, pull_resistor_47_node,
       pull_resistor_48_node, pull_resistor_49_node, pull_resistor_50_node, pull_resistor_51_node,
       pull_resistor_53_node, pull_resistor_54_node, pull_resistor_55_node, pull_resistor_56_node,
       pull_resistor_57_node, pull_resistor_58_node, pull_resistor_59_node, pull_resistor_61_node,
       pull_resistor_62_node, pull_resistor_63_node, pull_resistor_64_node, pull_resistor_65_node,
       pull_resistor_66_node, pull_resistor_67_node, pull_resistor_68_node, pull_resistor_69_node,
       pull_resistor_70_node, pull_resistor_71_node, pull_resistor_72_node, pull_resistor_73_node,
       pull_resistor_74_node, pull_resistor_75_node, pull_resistor_76_node, pull_resistor_77_node,
       pull_resistor_78_node, pull_resistor_79_node, pull_resistor_80_node, pull_resistor_81_node,
       pull_resistor_82_node, pull_resistor_83_node, pull_resistor_84_node, pull_resistor_85_node,
       pull_resistor_86_node, pull_resistor_87_node, pull_resistor_88_node, pull_resistor_89_node,
       pull_resistor_90_node, pull_resistor_91_node, pull_resistor_92_node, pull_resistor_93_node,
       pull_resistor_94_node, pull_resistor_95_node, pull_resistor_96_node, pull_resistor_97_node,
       pull_resistor_98_node, pull_resistor_99_node, pull_resistor_100_node, pull_resistor_101_node,
       pull_resistor_102_node, pull_resistor_103_node, pull_resistor_104_node, pull_resistor_105_node,
       pull_resistor_106_node, pull_resistor_107_node, pull_resistor_108_node, pull_resistor_109_node,
       pull_resistor_110_node, pull_resistor_111_node, pull_resistor_112_node, pull_resistor_113_node,
       pull_resistor_114_node, pull_resistor_115_node, pull_resistor_116_node, pull_resistor_117_node,
       pull_resistor_118_node, pull_resistor_119_node, pull_resistor_120_node, pull_resistor_121_node,
       pull_resistor_122_node, pull_resistor_123_node, pull_resistor_124_node, pull_resistor_125_node,
       pull_resistor_126_node, pull_resistor_127_node;

  adder128bit adder128bit_1 (
    .input1a(pull_resistor_64_node), .input1b(pull_resistor_1_node), .input2a(pull_resistor_65_node),
    .input2b(controlled_buffer_1_out), .output1a(adder128bit_1_output1a), .output1b(adder128bit_1_output1b));  // open: inflow, overflow
  Pull_Resistor pull_resistor_1 (.node(pull_resistor_1_node));
  assign controlled_buffer_1_out = input1[62] ? {2'b00, input2[63:2]} : 64'bz;  // Controlled_Buffer controlled_buffer_1
  assign pull_resistor_1_node = input1[63] ? {1'b0, input2[63:1]} : 64'bz;  // Controlled_Buffer controlled_buffer_2
  adder128bit adder128bit_2 (
    .input1a(pull_resistor_66_node), .input1b(pull_resistor_3_node), .input2a(pull_resistor_67_node),
    .input2b(pull_resistor_2_node), .output1a(adder128bit_2_output1a), .output1b(adder128bit_2_output1b));  // open: inflow, overflow
  Pull_Resistor pull_resistor_2 (.node(pull_resistor_2_node));
  Pull_Resistor pull_resistor_3 (.node(pull_resistor_3_node));
  Pull_Resistor pull_resistor_4 (.node(controlled_buffer_1_out));
  assign pull_resistor_2_node = input1[60] ? {4'b0000, input2[63:4]} : 64'bz;  // Controlled_Buffer controlled_buffer_3
  assign pull_resistor_3_node = input1[61] ? {3'b000, input2[63:3]} : 64'bz;  // Controlled_Buffer controlled_buffer_4
  adder128bit adder128bit_3 (
    .input1a(pull_resistor_68_node), .input1b(pull_resistor_7_node), .input2a(pull_resistor_69_node),
    .input2b(pull_resistor_6_node), .output1a(adder128bit_3_output1a), .output1b(adder128bit_3_output1b));  // open: inflow, overflow
  Pull_Resistor pull_resistor_5 (.node(pull_resistor_5_node));
  Pull_Resistor pull_resistor_6 (.node(pull_resistor_6_node));
  Pull_Resistor pull_resistor_7 (.node(pull_resistor_7_node));
  assign pull_resistor_5_node = input1[57] ? {{7{1'b0}}, input2[63:7]} : 64'bz;  // Controlled_Buffer controlled_buffer_5
  assign pull_resistor_6_node = input1[58] ? {{6{1'b0}}, input2[63:6]} : 64'bz;  // Controlled_Buffer controlled_buffer_6
  assign pull_resistor_7_node = input1[59] ? {{5{1'b0}}, input2[63:5]} : 64'bz;  // Controlled_Buffer controlled_buffer_7
  Pull_Resistor pull_resistor_8 (.node(pull_resistor_8_node));
  Pull_Resistor pull_resistor_9 (.node(pull_resistor_9_node));
  assign controlled_buffer_8_out = input1[54] ? {{10{1'b0}}, input2[63:10]} : 64'bz;  // Controlled_Buffer controlled_buffer_8
  assign pull_resistor_8_node = input1[55] ? {{9{1'b0}}, input2[63:9]} : 64'bz;  // Controlled_Buffer controlled_buffer_9
  assign pull_resistor_9_node = input1[56] ? {{8{1'b0}}, input2[63:8]} : 64'bz;  // Controlled_Buffer controlled_buffer_10
  adder128bit adder128bit_4 (
    .input1a(pull_resistor_70_node), .input1b(pull_resistor_5_node), .input2a(pull_resistor_71_node),
    .input2b(pull_resistor_9_node), .output1a(adder128bit_4_output1a), .output1b(adder128bit_4_output1b));  // open: inflow, overflow
  Pull_Resistor pull_resistor_10 (.node(pull_resistor_10_node));
  Pull_Resistor pull_resistor_11 (.node(pull_resistor_11_node));
  Pull_Resistor pull_resistor_12 (.node(controlled_buffer_8_out));
  assign pull_resistor_10_node = input1[52] ? {{12{1'b0}}, input2[63:12]} : 64'bz;  // Controlled_Buffer controlled_buffer_11
  assign pull_resistor_11_node = input1[53] ? {{11{1'b0}}, input2[63:11]} : 64'bz;  // Controlled_Buffer controlled_buffer_12
  adder128bit adder128bit_5 (
    .input1a(pull_resistor_72_node), .input1b(pull_resistor_8_node), .input2a(pull_resistor_73_node),
    .input2b(controlled_buffer_8_out), .output1a(adder128bit_5_output1a), .output1b(adder128bit_5_output1b));  // open: inflow, overflow
  Pull_Resistor pull_resistor_13 (.node(pull_resistor_13_node));
  Pull_Resistor pull_resistor_14 (.node(pull_resistor_14_node));
  Pull_Resistor pull_resistor_15 (.node(pull_resistor_15_node));
  assign pull_resistor_13_node = input1[49] ? {{15{1'b0}}, input2[63:15]} : 64'bz;  // Controlled_Buffer controlled_buffer_13
  assign pull_resistor_14_node = input1[50] ? {{14{1'b0}}, input2[63:14]} : 64'bz;  // Controlled_Buffer controlled_buffer_14
  assign pull_resistor_15_node = input1[51] ? {{13{1'b0}}, input2[63:13]} : 64'bz;  // Controlled_Buffer controlled_buffer_15
  Pull_Resistor pull_resistor_16 (.node(pull_resistor_16_node));
  Pull_Resistor pull_resistor_17 (.node(pull_resistor_17_node));
  assign controlled_buffer_16_out = input1[46] ? {{18{1'b0}}, input2[63:18]} : 64'bz;  // Controlled_Buffer controlled_buffer_16
  assign pull_resistor_16_node = input1[47] ? {{17{1'b0}}, input2[63:17]} : 64'bz;  // Controlled_Buffer controlled_buffer_17
  assign pull_resistor_17_node = input1[48] ? {{16{1'b0}}, input2[63:16]} : 64'bz;  // Controlled_Buffer controlled_buffer_18
  adder128bit adder128bit_6 (
    .input1a(pull_resistor_74_node), .input1b(pull_resistor_11_node), .input2a(pull_resistor_75_node),
    .input2b(pull_resistor_10_node), .output1a(adder128bit_6_output1a), .output1b(adder128bit_6_output1b));  // open: inflow, overflow
  Pull_Resistor pull_resistor_18 (.node(pull_resistor_18_node));
  Pull_Resistor pull_resistor_19 (.node(pull_resistor_19_node));
  Pull_Resistor pull_resistor_20 (.node(controlled_buffer_16_out));
  assign pull_resistor_18_node = input1[44] ? {{20{1'b0}}, input2[63:20]} : 64'bz;  // Controlled_Buffer controlled_buffer_19
  assign pull_resistor_19_node = input1[45] ? {{19{1'b0}}, input2[63:19]} : 64'bz;  // Controlled_Buffer controlled_buffer_20
  Pull_Resistor pull_resistor_21 (.node(pull_resistor_21_node));
  Pull_Resistor pull_resistor_22 (.node(pull_resistor_22_node));
  Pull_Resistor pull_resistor_23 (.node(pull_resistor_23_node));
  assign pull_resistor_21_node = input1[41] ? {{23{1'b0}}, input2[63:23]} : 64'bz;  // Controlled_Buffer controlled_buffer_21
  assign pull_resistor_22_node = input1[42] ? {{22{1'b0}}, input2[63:22]} : 64'bz;  // Controlled_Buffer controlled_buffer_22
  assign pull_resistor_23_node = input1[43] ? {{21{1'b0}}, input2[63:21]} : 64'bz;  // Controlled_Buffer controlled_buffer_23
  adder128bit adder128bit_7 (
    .input1a(pull_resistor_76_node), .input1b(pull_resistor_15_node), .input2a(pull_resistor_77_node),
    .input2b(pull_resistor_14_node), .output1a(adder128bit_7_output1a), .output1b(adder128bit_7_output1b));  // open: inflow, overflow
  Pull_Resistor pull_resistor_24 (.node(pull_resistor_24_node));
  Pull_Resistor pull_resistor_25 (.node(pull_resistor_25_node));
  assign controlled_buffer_24_out = input1[38] ? {{26{1'b0}}, input2[63:26]} : 64'bz;  // Controlled_Buffer controlled_buffer_24
  assign pull_resistor_24_node = input1[39] ? {{25{1'b0}}, input2[63:25]} : 64'bz;  // Controlled_Buffer controlled_buffer_25
  assign pull_resistor_25_node = input1[40] ? {{24{1'b0}}, input2[63:24]} : 64'bz;  // Controlled_Buffer controlled_buffer_26
  adder128bit adder128bit_8 (
    .input1a(pull_resistor_78_node), .input1b(pull_resistor_13_node), .input2a(pull_resistor_79_node),
    .input2b(pull_resistor_17_node), .output1a(adder128bit_8_output1a), .output1b(adder128bit_8_output1b));  // open: inflow, overflow
  Pull_Resistor pull_resistor_26 (.node(pull_resistor_26_node));
  Pull_Resistor pull_resistor_27 (.node(pull_resistor_27_node));
  Pull_Resistor pull_resistor_28 (.node(controlled_buffer_24_out));
  assign pull_resistor_26_node = input1[36] ? {{28{1'b0}}, input2[63:28]} : 64'bz;  // Controlled_Buffer controlled_buffer_27
  assign pull_resistor_27_node = input1[37] ? {{27{1'b0}}, input2[63:27]} : 64'bz;  // Controlled_Buffer controlled_buffer_28
  Pull_Resistor pull_resistor_29 (.node(pull_resistor_29_node));
  Pull_Resistor pull_resistor_30 (.node(pull_resistor_30_node));
  Pull_Resistor pull_resistor_31 (.node(pull_resistor_31_node));
  assign pull_resistor_29_node = input1[33] ? {{31{1'b0}}, input2[63:31]} : 64'bz;  // Controlled_Buffer controlled_buffer_29
  assign pull_resistor_30_node = input1[34] ? {{30{1'b0}}, input2[63:30]} : 64'bz;  // Controlled_Buffer controlled_buffer_30
  assign pull_resistor_31_node = input1[35] ? {{29{1'b0}}, input2[63:29]} : 64'bz;  // Controlled_Buffer controlled_buffer_31
  adder128bit adder128bit_9 (
    .input1a(adder128bit_1_output1a), .input1b(adder128bit_1_output1b), .input2a(adder128bit_2_output1a),
    .input2b(adder128bit_2_output1b), .output1a(adder128bit_9_output1a), .output1b(adder128bit_9_output1b));  // open: inflow, overflow
  adder128bit adder128bit_10 (
    .input1a(pull_resistor_80_node), .input1b(pull_resistor_16_node), .input2a(pull_resistor_81_node),
    .input2b(controlled_buffer_16_out), .output1a(adder128bit_10_output1a), .output1b(adder128bit_10_output1b));  // open: inflow, overflow
  Pull_Resistor pull_resistor_32 (.node(pull_resistor_32_node));
  Pull_Resistor pull_resistor_33 (.node(pull_resistor_33_node));
  assign controlled_buffer_32_out = input1[30] ? {{34{1'b0}}, input2[63:34]} : 64'bz;  // Controlled_Buffer controlled_buffer_32
  assign pull_resistor_32_node = input1[31] ? {{33{1'b0}}, input2[63:33]} : 64'bz;  // Controlled_Buffer controlled_buffer_33
  assign pull_resistor_33_node = input1[32] ? {{32{1'b0}}, input2[63:32]} : 64'bz;  // Controlled_Buffer controlled_buffer_34
  Pull_Resistor pull_resistor_34 (.node(pull_resistor_34_node));
  Pull_Resistor pull_resistor_35 (.node(pull_resistor_35_node));
  Pull_Resistor pull_resistor_36 (.node(controlled_buffer_32_out));
  assign pull_resistor_34_node = input1[28] ? {{36{1'b0}}, input2[63:36]} : 64'bz;  // Controlled_Buffer controlled_buffer_35
  assign pull_resistor_35_node = input1[29] ? {{35{1'b0}}, input2[63:35]} : 64'bz;  // Controlled_Buffer controlled_buffer_36
  adder128bit adder128bit_11 (
    .input1a(adder128bit_3_output1a), .input1b(adder128bit_3_output1b), .input2a(adder128bit_4_output1a),
    .input2b(adder128bit_4_output1b), .output1a(adder128bit_11_output1a), .output1b(adder128bit_11_output1b));  // open: inflow, overflow
  adder128bit adder128bit_12 (
    .input1a(pull_resistor_82_node), .input1b(pull_resistor_19_node), .input2a(pull_resistor_83_node),
    .input2b(pull_resistor_18_node), .output1a(adder128bit_12_output1a), .output1b(adder128bit_12_output1b));  // open: inflow, overflow
  Pull_Resistor pull_resistor_37 (.node(pull_resistor_37_node));
  Pull_Resistor pull_resistor_38 (.node(pull_resistor_38_node));
  Pull_Resistor pull_resistor_39 (.node(pull_resistor_39_node));
  assign pull_resistor_37_node = input1[25] ? {{39{1'b0}}, input2[63:39]} : 64'bz;  // Controlled_Buffer controlled_buffer_37
  assign pull_resistor_38_node = input1[26] ? {{38{1'b0}}, input2[63:38]} : 64'bz;  // Controlled_Buffer controlled_buffer_38
  assign pull_resistor_39_node = input1[27] ? {{37{1'b0}}, input2[63:37]} : 64'bz;  // Controlled_Buffer controlled_buffer_39
  adder128bit adder128bit_13 (
    .input1a(adder128bit_5_output1a), .input1b(adder128bit_5_output1b), .input2a(adder128bit_6_output1a),
    .input2b(adder128bit_6_output1b), .output1a(adder128bit_13_output1a), .output1b(adder128bit_13_output1b));  // open: inflow, overflow
  adder128bit adder128bit_14 (
    .input1a(pull_resistor_84_node), .input1b(pull_resistor_23_node), .input2a(pull_resistor_85_node),
    .input2b(pull_resistor_22_node), .output1a(adder128bit_14_output1a), .output1b(adder128bit_14_output1b));  // open: inflow, overflow
  Pull_Resistor pull_resistor_40 (.node(pull_resistor_40_node));
  Pull_Resistor pull_resistor_41 (.node(pull_resistor_41_node));
  assign controlled_buffer_40_out = input1[22] ? {{42{1'b0}}, input2[63:42]} : 64'bz;  // Controlled_Buffer controlled_buffer_40
  assign pull_resistor_40_node = input1[23] ? {{41{1'b0}}, input2[63:41]} : 64'bz;  // Controlled_Buffer controlled_buffer_41
  assign pull_resistor_41_node = input1[24] ? {{40{1'b0}}, input2[63:40]} : 64'bz;  // Controlled_Buffer controlled_buffer_42
  Pull_Resistor pull_resistor_42 (.node(pull_resistor_42_node));
  Pull_Resistor pull_resistor_43 (.node(pull_resistor_43_node));
  Pull_Resistor pull_resistor_44 (.node(controlled_buffer_40_out));
  assign pull_resistor_42_node = input1[20] ? {{44{1'b0}}, input2[63:44]} : 64'bz;  // Controlled_Buffer controlled_buffer_43
  assign pull_resistor_43_node = input1[21] ? {{43{1'b0}}, input2[63:43]} : 64'bz;  // Controlled_Buffer controlled_buffer_44
  adder128bit adder128bit_15 (
    .input1a(adder128bit_7_output1a), .input1b(adder128bit_7_output1b), .input2a(adder128bit_8_output1a),
    .input2b(adder128bit_8_output1b), .output1a(adder128bit_15_output1a), .output1b(adder128bit_15_output1b));  // open: inflow, overflow
  adder128bit adder128bit_16 (
    .input1a(pull_resistor_86_node), .input1b(pull_resistor_21_node), .input2a(pull_resistor_87_node),
    .input2b(pull_resistor_25_node), .output1a(adder128bit_16_output1a), .output1b(adder128bit_16_output1b));  // open: inflow, overflow
  Pull_Resistor pull_resistor_45 (.node(pull_resistor_45_node));
  Pull_Resistor pull_resistor_46 (.node(pull_resistor_46_node));
  Pull_Resistor pull_resistor_47 (.node(pull_resistor_47_node));
  assign pull_resistor_45_node = input1[17] ? {{47{1'b0}}, input2[63:47]} : 64'bz;  // Controlled_Buffer controlled_buffer_45
  assign pull_resistor_46_node = input1[18] ? {{46{1'b0}}, input2[63:46]} : 64'bz;  // Controlled_Buffer controlled_buffer_46
  assign pull_resistor_47_node = input1[19] ? {{45{1'b0}}, input2[63:45]} : 64'bz;  // Controlled_Buffer controlled_buffer_47
  adder128bit adder128bit_17 (
    .input1a(adder128bit_9_output1a), .input1b(adder128bit_9_output1b), .input2a(adder128bit_11_output1a),
    .input2b(adder128bit_11_output1b), .output1a(adder128bit_17_output1a), .output1b(adder128bit_17_output1b));  // open: inflow, overflow
  adder128bit adder128bit_18 (
    .input1a(adder128bit_10_output1a), .input1b(adder128bit_10_output1b), .input2a(adder128bit_12_output1a),
    .input2b(adder128bit_12_output1b), .output1a(adder128bit_18_output1a), .output1b(adder128bit_18_output1b));  // open: inflow, overflow
  adder128bit adder128bit_19 (
    .input1a(pull_resistor_88_node), .input1b(pull_resistor_24_node), .input2a(pull_resistor_89_node),
    .input2b(controlled_buffer_24_out), .output1a(adder128bit_19_output1a), .output1b(adder128bit_19_output1b));  // open: inflow, overflow
  Pull_Resistor pull_resistor_48 (.node(pull_resistor_48_node));
  Pull_Resistor pull_resistor_49 (.node(pull_resistor_49_node));
  assign controlled_buffer_48_out = input1[14] ? {{50{1'b0}}, input2[63:50]} : 64'bz;  // Controlled_Buffer controlled_buffer_48
  assign pull_resistor_48_node = input1[15] ? {{49{1'b0}}, input2[63:49]} : 64'bz;  // Controlled_Buffer controlled_buffer_49
  assign pull_resistor_49_node = input1[16] ? {{48{1'b0}}, input2[63:48]} : 64'bz;  // Controlled_Buffer controlled_buffer_50
  Pull_Resistor pull_resistor_50 (.node(pull_resistor_50_node));
  Pull_Resistor pull_resistor_51 (.node(pull_resistor_51_node));
  Pull_Resistor pull_resistor_52 (.node(controlled_buffer_48_out));
  assign pull_resistor_50_node = input1[12] ? {{52{1'b0}}, input2[63:52]} : 64'bz;  // Controlled_Buffer controlled_buffer_51
  assign pull_resistor_51_node = input1[13] ? {{51{1'b0}}, input2[63:51]} : 64'bz;  // Controlled_Buffer controlled_buffer_52
  adder128bit adder128bit_20 (
    .input1a(adder128bit_13_output1a), .input1b(adder128bit_13_output1b), .input2a(adder128bit_15_output1a),
    .input2b(adder128bit_15_output1b), .output1a(adder128bit_20_output1a), .output1b(adder128bit_20_output1b));  // open: inflow, overflow
  adder128bit adder128bit_21 (
    .input1a(adder128bit_14_output1a), .input1b(adder128bit_14_output1b), .input2a(adder128bit_16_output1a),
    .input2b(adder128bit_16_output1b), .output1a(adder128bit_21_output1a), .output1b(adder128bit_21_output1b));  // open: inflow, overflow
  adder128bit adder128bit_22 (
    .input1a(pull_resistor_90_node), .input1b(pull_resistor_27_node), .input2a(pull_resistor_91_node),
    .input2b(pull_resistor_26_node), .output1a(adder128bit_22_output1a), .output1b(adder128bit_22_output1b));  // open: inflow, overflow
  Pull_Resistor pull_resistor_53 (.node(pull_resistor_53_node));
  Pull_Resistor pull_resistor_54 (.node(pull_resistor_54_node));
  Pull_Resistor pull_resistor_55 (.node(pull_resistor_55_node));
  assign pull_resistor_53_node = input1[9] ? {{55{1'b0}}, input2[63:55]} : 64'bz;  // Controlled_Buffer controlled_buffer_53
  assign pull_resistor_54_node = input1[10] ? {{54{1'b0}}, input2[63:54]} : 64'bz;  // Controlled_Buffer controlled_buffer_54
  assign pull_resistor_55_node = input1[11] ? {{53{1'b0}}, input2[63:53]} : 64'bz;  // Controlled_Buffer controlled_buffer_55
  Pull_Resistor pull_resistor_56 (.node(pull_resistor_56_node));
  Pull_Resistor pull_resistor_57 (.node(pull_resistor_57_node));
  assign controlled_buffer_56_out = input1[6] ? {{58{1'b0}}, input2[63:58]} : 64'bz;  // Controlled_Buffer controlled_buffer_56
  assign pull_resistor_56_node = input1[7] ? {{57{1'b0}}, input2[63:57]} : 64'bz;  // Controlled_Buffer controlled_buffer_57
  assign pull_resistor_57_node = input1[8] ? {{56{1'b0}}, input2[63:56]} : 64'bz;  // Controlled_Buffer controlled_buffer_58
  adder128bit adder128bit_23 (
    .input1a(adder128bit_17_output1a), .input1b(adder128bit_17_output1b), .input2a(adder128bit_20_output1a),
    .input2b(adder128bit_20_output1b), .output1a(adder128bit_23_output1a), .output1b(adder128bit_23_output1b));  // open: inflow, overflow
  adder128bit adder128bit_24 (
    .input1a(adder128bit_18_output1a), .input1b(adder128bit_18_output1b), .input2a(adder128bit_21_output1a),
    .input2b(adder128bit_21_output1b), .output1a(adder128bit_24_output1a), .output1b(adder128bit_24_output1b));  // open: inflow, overflow
  adder128bit adder128bit_25 (
    .input1a(adder128bit_19_output1a), .input1b(adder128bit_19_output1b), .input2a(adder128bit_22_output1a),
    .input2b(adder128bit_22_output1b), .output1a(adder128bit_25_output1a), .output1b(adder128bit_25_output1b));  // open: inflow, overflow
  adder128bit adder128bit_26 (
    .input1a(pull_resistor_92_node), .input1b(pull_resistor_31_node), .input2a(pull_resistor_93_node),
    .input2b(pull_resistor_30_node), .output1a(adder128bit_26_output1a), .output1b(adder128bit_26_output1b));  // open: inflow, overflow
  Pull_Resistor pull_resistor_58 (.node(pull_resistor_58_node));
  Pull_Resistor pull_resistor_59 (.node(pull_resistor_59_node));
  Pull_Resistor pull_resistor_60 (.node(controlled_buffer_56_out));
  assign pull_resistor_58_node = input1[4] ? {{60{1'b0}}, input2[63:60]} : 64'bz;  // Controlled_Buffer controlled_buffer_59
  assign pull_resistor_59_node = input1[5] ? {{59{1'b0}}, input2[63:59]} : 64'bz;  // Controlled_Buffer controlled_buffer_60
  adder128bit adder128bit_27 (
    .input1a(adder128bit_23_output1a), .input1b(adder128bit_23_output1b), .input2a(adder128bit_28_output1a),
    .input2b(adder128bit_28_output1b), .output1a(adder128bit_27_output1a), .output1b(adder128bit_27_output1b));  // open: inflow, overflow
  adder128bit adder128bit_28 (
    .input1a(adder128bit_24_output1a), .input1b(adder128bit_24_output1b), .input2a(adder128bit_29_output1a),
    .input2b(adder128bit_29_output1b), .output1a(adder128bit_28_output1a), .output1b(adder128bit_28_output1b));  // open: inflow, overflow
  adder128bit adder128bit_29 (
    .input1a(adder128bit_25_output1a), .input1b(adder128bit_25_output1b), .input2a(adder128bit_30_output1a),
    .input2b(adder128bit_30_output1b), .output1a(adder128bit_29_output1a), .output1b(adder128bit_29_output1b));  // open: inflow, overflow
  adder128bit adder128bit_30 (
    .input1a(adder128bit_26_output1a), .input1b(adder128bit_26_output1b), .input2a(adder128bit_31_output1a),
    .input2b(adder128bit_31_output1b), .output1a(adder128bit_30_output1a), .output1b(adder128bit_30_output1b));  // open: inflow, overflow
  adder128bit adder128bit_31 (
    .input1a(pull_resistor_94_node), .input1b(pull_resistor_29_node), .input2a(pull_resistor_95_node),
    .input2b(pull_resistor_33_node), .output1a(adder128bit_31_output1a), .output1b(adder128bit_31_output1b));  // open: inflow, overflow
  Pull_Resistor pull_resistor_61 (.node(pull_resistor_61_node));
  Pull_Resistor pull_resistor_62 (.node(pull_resistor_62_node));
  Pull_Resistor pull_resistor_63 (.node(pull_resistor_63_node));
  assign pull_resistor_61_node = input1[1] ? {{63{1'b0}}, input2[63]} : 64'bz;  // Controlled_Buffer controlled_buffer_61
  assign pull_resistor_62_node = input1[2] ? {{62{1'b0}}, input2[63:62]} : 64'bz;  // Controlled_Buffer controlled_buffer_62
  assign pull_resistor_63_node = input1[3] ? {{61{1'b0}}, input2[63:61]} : 64'bz;  // Controlled_Buffer controlled_buffer_63
  adder128bit adder128bit_32 (
    .input1a(adder128bit_27_output1a), .input1b(adder128bit_27_output1b), .input2a(adder128bit_33_output1a),
    .input2b(adder128bit_33_output1b), .output1a(output1), .output1b(overflow));  // open: inflow, overflow
  adder128bit adder128bit_33 (
    .input1a(adder128bit_34_output1a), .input1b(adder128bit_34_output1b), .input2a(adder128bit_38_output1a),
    .input2b(adder128bit_38_output1b), .output1a(adder128bit_33_output1a), .output1b(adder128bit_33_output1b));  // open: inflow, overflow
  adder128bit adder128bit_34 (
    .input1a(adder128bit_35_output1a), .input1b(adder128bit_35_output1b), .input2a(adder128bit_39_output1a),
    .input2b(adder128bit_39_output1b), .output1a(adder128bit_34_output1a), .output1b(adder128bit_34_output1b));  // open: inflow, overflow
  adder128bit adder128bit_35 (
    .input1a(adder128bit_36_output1a), .input1b(adder128bit_36_output1b), .input2a(adder128bit_40_output1a),
    .input2b(adder128bit_40_output1b), .output1a(adder128bit_35_output1a), .output1b(adder128bit_35_output1b));  // open: inflow, overflow
  adder128bit adder128bit_36 (
    .input1a(adder128bit_37_output1a), .input1b(adder128bit_37_output1b), .input2a(adder128bit_41_output1a),
    .input2b(adder128bit_41_output1b), .output1a(adder128bit_36_output1a), .output1b(adder128bit_36_output1b));  // open: inflow, overflow
  adder128bit adder128bit_37 (
    .input1a(pull_resistor_96_node), .input1b(pull_resistor_32_node), .input2a(pull_resistor_97_node),
    .input2b(controlled_buffer_32_out), .output1a(adder128bit_37_output1a), .output1b(adder128bit_37_output1b));  // open: inflow, overflow
  Pull_Resistor pull_resistor_64 (.node(pull_resistor_64_node));
  Pull_Resistor pull_resistor_65 (.node(pull_resistor_65_node));
  Pull_Resistor pull_resistor_66 (.node(pull_resistor_66_node));
  assign pull_resistor_64_node = input1[0] ? input2 : 64'bz;  // Controlled_Buffer controlled_buffer_64
  assign pull_resistor_65_node = input1[1] ? {input2[62:0], 1'b0} : 64'bz;  // Controlled_Buffer controlled_buffer_65
  Pull_Resistor pull_resistor_67 (.node(pull_resistor_67_node));
  Pull_Resistor pull_resistor_68 (.node(pull_resistor_68_node));
  assign pull_resistor_66_node = input1[2] ? {input2[61:0], 2'b00} : 64'bz;  // Controlled_Buffer controlled_buffer_66
  assign pull_resistor_67_node = input1[3] ? {input2[60:0], 3'b000} : 64'bz;  // Controlled_Buffer controlled_buffer_67
  assign pull_resistor_68_node = input1[4] ? {input2[59:0], 4'b0000} : 64'bz;  // Controlled_Buffer controlled_buffer_68
  adder128bit adder128bit_38 (
    .input1a(adder128bit_42_output1a), .input1b(adder128bit_42_output1b), .input2a(adder128bit_45_output1a),
    .input2b(adder128bit_45_output1b), .output1a(adder128bit_38_output1a), .output1b(adder128bit_38_output1b));  // open: inflow, overflow
  adder128bit adder128bit_39 (
    .input1a(adder128bit_43_output1a), .input1b(adder128bit_43_output1b), .input2a(adder128bit_46_output1a),
    .input2b(adder128bit_46_output1b), .output1a(adder128bit_39_output1a), .output1b(adder128bit_39_output1b));  // open: inflow, overflow
  adder128bit adder128bit_40 (
    .input1a(adder128bit_44_output1a), .input1b(adder128bit_44_output1b), .input2a(adder128bit_47_output1a),
    .input2b(adder128bit_47_output1b), .output1a(adder128bit_40_output1a), .output1b(adder128bit_40_output1b));  // open: inflow, overflow
  adder128bit adder128bit_41 (
    .input1a(pull_resistor_98_node), .input1b(pull_resistor_35_node), .input2a(pull_resistor_99_node),
    .input2b(pull_resistor_34_node), .output1a(adder128bit_41_output1a), .output1b(adder128bit_41_output1b));  // open: inflow, overflow
  Pull_Resistor pull_resistor_69 (.node(pull_resistor_69_node));
  Pull_Resistor pull_resistor_70 (.node(pull_resistor_70_node));
  Pull_Resistor pull_resistor_71 (.node(pull_resistor_71_node));
  assign pull_resistor_69_node = input1[5] ? {input2[58:0], {5{1'b0}}} : 64'bz;  // Controlled_Buffer controlled_buffer_69
  assign pull_resistor_70_node = input1[6] ? {input2[57:0], {6{1'b0}}} : 64'bz;  // Controlled_Buffer controlled_buffer_70
  assign pull_resistor_71_node = input1[7] ? {input2[56:0], {7{1'b0}}} : 64'bz;  // Controlled_Buffer controlled_buffer_71
  adder128bit adder128bit_42 (
    .input1a(adder128bit_48_output1a), .input1b(adder128bit_48_output1b), .input2a(adder128bit_50_output1a),
    .input2b(adder128bit_50_output1b), .output1a(adder128bit_42_output1a), .output1b(adder128bit_42_output1b));  // open: inflow, overflow
  adder128bit adder128bit_43 (
    .input1a(adder128bit_49_output1a), .input1b(adder128bit_49_output1b), .input2a(adder128bit_51_output1a),
    .input2b(adder128bit_51_output1b), .output1a(adder128bit_43_output1a), .output1b(adder128bit_43_output1b));  // open: inflow, overflow
  adder128bit adder128bit_44 (
    .input1a(pull_resistor_100_node), .input1b(pull_resistor_39_node), .input2a(pull_resistor_101_node),
    .input2b(pull_resistor_38_node), .output1a(adder128bit_44_output1a), .output1b(adder128bit_44_output1b));  // open: inflow, overflow
  Pull_Resistor pull_resistor_72 (.node(pull_resistor_72_node));
  Pull_Resistor pull_resistor_73 (.node(pull_resistor_73_node));
  Pull_Resistor pull_resistor_74 (.node(pull_resistor_74_node));
  assign pull_resistor_72_node = input1[8] ? {input2[55:0], {8{1'b0}}} : 64'bz;  // Controlled_Buffer controlled_buffer_72
  assign pull_resistor_73_node = input1[9] ? {input2[54:0], {9{1'b0}}} : 64'bz;  // Controlled_Buffer controlled_buffer_73
  Pull_Resistor pull_resistor_75 (.node(pull_resistor_75_node));
  Pull_Resistor pull_resistor_76 (.node(pull_resistor_76_node));
  assign pull_resistor_74_node = input1[10] ? {input2[53:0], {10{1'b0}}} : 64'bz;  // Controlled_Buffer controlled_buffer_74
  assign pull_resistor_75_node = input1[11] ? {input2[52:0], {11{1'b0}}} : 64'bz;  // Controlled_Buffer controlled_buffer_75
  assign pull_resistor_76_node = input1[12] ? {input2[51:0], {12{1'b0}}} : 64'bz;  // Controlled_Buffer controlled_buffer_76
  adder128bit adder128bit_45 (
    .input1a(adder128bit_52_output1a), .input1b(adder128bit_52_output1b), .input2a(adder128bit_54_output1a),
    .input2b(adder128bit_54_output1b), .output1a(adder128bit_45_output1a), .output1b(adder128bit_45_output1b));  // open: inflow, overflow
  adder128bit adder128bit_46 (
    .input1a(adder128bit_53_output1a), .input1b(adder128bit_53_output1b), .input2a(adder128bit_55_output1a),
    .input2b(adder128bit_55_output1b), .output1a(adder128bit_46_output1a), .output1b(adder128bit_46_output1b));  // open: inflow, overflow
  adder128bit adder128bit_47 (
    .input1a(pull_resistor_102_node), .input1b(pull_resistor_37_node), .input2a(pull_resistor_103_node),
    .input2b(pull_resistor_41_node), .output1a(adder128bit_47_output1a), .output1b(adder128bit_47_output1b));  // open: inflow, overflow
  Pull_Resistor pull_resistor_77 (.node(pull_resistor_77_node));
  Pull_Resistor pull_resistor_78 (.node(pull_resistor_78_node));
  Pull_Resistor pull_resistor_79 (.node(pull_resistor_79_node));
  assign pull_resistor_77_node = input1[13] ? {input2[50:0], {13{1'b0}}} : 64'bz;  // Controlled_Buffer controlled_buffer_77
  assign pull_resistor_78_node = input1[14] ? {input2[49:0], {14{1'b0}}} : 64'bz;  // Controlled_Buffer controlled_buffer_78
  assign pull_resistor_79_node = input1[15] ? {input2[48:0], {15{1'b0}}} : 64'bz;  // Controlled_Buffer controlled_buffer_79
  adder128bit adder128bit_48 (
    .input1a(adder128bit_56_output1a), .input1b(adder128bit_56_output1b), .input2a(adder128bit_57_output1a),
    .input2b(adder128bit_57_output1b), .output1a(adder128bit_48_output1a), .output1b(adder128bit_48_output1b));  // open: inflow, overflow
  adder128bit adder128bit_49 (
    .input1a(pull_resistor_104_node), .input1b(pull_resistor_40_node), .input2a(pull_resistor_105_node),
    .input2b(controlled_buffer_40_out), .output1a(adder128bit_49_output1a), .output1b(adder128bit_49_output1b));  // open: inflow, overflow
  Pull_Resistor pull_resistor_80 (.node(pull_resistor_80_node));
  Pull_Resistor pull_resistor_81 (.node(pull_resistor_81_node));
  Pull_Resistor pull_resistor_82 (.node(pull_resistor_82_node));
  assign pull_resistor_80_node = input1[16] ? {input2[47:0], {16{1'b0}}} : 64'bz;  // Controlled_Buffer controlled_buffer_80
  assign pull_resistor_81_node = input1[17] ? {input2[46:0], {17{1'b0}}} : 64'bz;  // Controlled_Buffer controlled_buffer_81
  Pull_Resistor pull_resistor_83 (.node(pull_resistor_83_node));
  Pull_Resistor pull_resistor_84 (.node(pull_resistor_84_node));
  assign pull_resistor_82_node = input1[18] ? {input2[45:0], {18{1'b0}}} : 64'bz;  // Controlled_Buffer controlled_buffer_82
  assign pull_resistor_83_node = input1[19] ? {input2[44:0], {19{1'b0}}} : 64'bz;  // Controlled_Buffer controlled_buffer_83
  assign pull_resistor_84_node = input1[20] ? {input2[43:0], {20{1'b0}}} : 64'bz;  // Controlled_Buffer controlled_buffer_84
  adder128bit adder128bit_50 (
    .input1a(adder128bit_58_output1a), .input1b(adder128bit_58_output1b), .input2a(adder128bit_59_output1a),
    .input2b(adder128bit_59_output1b), .output1a(adder128bit_50_output1a), .output1b(adder128bit_50_output1b));  // open: inflow, overflow
  adder128bit adder128bit_51 (
    .input1a(pull_resistor_106_node), .input1b(pull_resistor_43_node), .input2a(pull_resistor_107_node),
    .input2b(pull_resistor_42_node), .output1a(adder128bit_51_output1a), .output1b(adder128bit_51_output1b));  // open: inflow, overflow
  Pull_Resistor pull_resistor_85 (.node(pull_resistor_85_node));
  Pull_Resistor pull_resistor_86 (.node(pull_resistor_86_node));
  Pull_Resistor pull_resistor_87 (.node(pull_resistor_87_node));
  assign pull_resistor_85_node = input1[21] ? {input2[42:0], {21{1'b0}}} : 64'bz;  // Controlled_Buffer controlled_buffer_85
  assign pull_resistor_86_node = input1[22] ? {input2[41:0], {22{1'b0}}} : 64'bz;  // Controlled_Buffer controlled_buffer_86
  assign pull_resistor_87_node = input1[23] ? {input2[40:0], {23{1'b0}}} : 64'bz;  // Controlled_Buffer controlled_buffer_87
  Pull_Resistor pull_resistor_88 (.node(pull_resistor_88_node));
  Pull_Resistor pull_resistor_89 (.node(pull_resistor_89_node));
  Pull_Resistor pull_resistor_90 (.node(pull_resistor_90_node));
  assign pull_resistor_88_node = input1[24] ? {input2[39:0], {24{1'b0}}} : 64'bz;  // Controlled_Buffer controlled_buffer_88
  assign pull_resistor_89_node = input1[25] ? {input2[38:0], {25{1'b0}}} : 64'bz;  // Controlled_Buffer controlled_buffer_89
  adder128bit adder128bit_52 (
    .input1a(adder128bit_60_output1a), .input1b(adder128bit_60_output1b), .input2a(adder128bit_61_output1a),
    .input2b(adder128bit_61_output1b), .output1a(adder128bit_52_output1a), .output1b(adder128bit_52_output1b));  // open: inflow, overflow
  adder128bit adder128bit_53 (
    .input1a(pull_resistor_108_node), .input1b(pull_resistor_47_node), .input2a(pull_resistor_109_node),
    .input2b(pull_resistor_46_node), .output1a(adder128bit_53_output1a), .output1b(adder128bit_53_output1b));  // open: inflow, overflow
  Pull_Resistor pull_resistor_91 (.node(pull_resistor_91_node));
  Pull_Resistor pull_resistor_92 (.node(pull_resistor_92_node));
  assign pull_resistor_90_node = input1[26] ? {input2[37:0], {26{1'b0}}} : 64'bz;  // Controlled_Buffer controlled_buffer_90
  assign pull_resistor_91_node = input1[27] ? {input2[36:0], {27{1'b0}}} : 64'bz;  // Controlled_Buffer controlled_buffer_91
  assign pull_resistor_92_node = input1[28] ? {input2[35:0], {28{1'b0}}} : 64'bz;  // Controlled_Buffer controlled_buffer_92
  adder128bit adder128bit_54 (
    .input1a(adder128bit_62_output1a), .input1b(adder128bit_62_output1b), .input2a(adder128bit_63_output1a),
    .input2b(adder128bit_63_output1b), .output1a(adder128bit_54_output1a), .output1b(adder128bit_54_output1b));  // open: inflow, overflow
  adder128bit adder128bit_55 (
    .input1a(pull_resistor_110_node), .input1b(pull_resistor_45_node), .input2a(pull_resistor_111_node),
    .input2b(pull_resistor_49_node), .output1a(adder128bit_55_output1a), .output1b(adder128bit_55_output1b));  // open: inflow, overflow
  Pull_Resistor pull_resistor_93 (.node(pull_resistor_93_node));
  Pull_Resistor pull_resistor_94 (.node(pull_resistor_94_node));
  Pull_Resistor pull_resistor_95 (.node(pull_resistor_95_node));
  assign pull_resistor_93_node = input1[29] ? {input2[34:0], {29{1'b0}}} : 64'bz;  // Controlled_Buffer controlled_buffer_93
  assign pull_resistor_94_node = input1[30] ? {input2[33:0], {30{1'b0}}} : 64'bz;  // Controlled_Buffer controlled_buffer_94
  assign pull_resistor_95_node = input1[31] ? {input2[32:0], {31{1'b0}}} : 64'bz;  // Controlled_Buffer controlled_buffer_95
  Pull_Resistor pull_resistor_96 (.node(pull_resistor_96_node));
  Pull_Resistor pull_resistor_97 (.node(pull_resistor_97_node));
  Pull_Resistor pull_resistor_98 (.node(pull_resistor_98_node));
  assign pull_resistor_96_node = input1[32] ? {input2[31:0], {32{1'b0}}} : 64'bz;  // Controlled_Buffer controlled_buffer_96
  assign pull_resistor_97_node = input1[33] ? {input2[30:0], {33{1'b0}}} : 64'bz;  // Controlled_Buffer controlled_buffer_97
  adder128bit adder128bit_56 (
    .input1a(pull_resistor_112_node), .input1b(pull_resistor_48_node), .input2a(pull_resistor_113_node),
    .input2b(controlled_buffer_48_out), .output1a(adder128bit_56_output1a), .output1b(adder128bit_56_output1b));  // open: inflow, overflow
  Pull_Resistor pull_resistor_99 (.node(pull_resistor_99_node));
  Pull_Resistor pull_resistor_100 (.node(pull_resistor_100_node));
  assign pull_resistor_98_node = input1[34] ? {input2[29:0], {34{1'b0}}} : 64'bz;  // Controlled_Buffer controlled_buffer_98
  assign pull_resistor_99_node = input1[35] ? {input2[28:0], {35{1'b0}}} : 64'bz;  // Controlled_Buffer controlled_buffer_99
  assign pull_resistor_100_node = input1[36] ? {input2[27:0], {36{1'b0}}} : 64'bz;  // Controlled_Buffer controlled_buffer_100
  Pull_Resistor pull_resistor_101 (.node(pull_resistor_101_node));
  Pull_Resistor pull_resistor_102 (.node(pull_resistor_102_node));
  Pull_Resistor pull_resistor_103 (.node(pull_resistor_103_node));
  assign pull_resistor_101_node = input1[37] ? {input2[26:0], {37{1'b0}}} : 64'bz;  // Controlled_Buffer controlled_buffer_101
  assign pull_resistor_102_node = input1[38] ? {input2[25:0], {38{1'b0}}} : 64'bz;  // Controlled_Buffer controlled_buffer_102
  assign pull_resistor_103_node = input1[39] ? {input2[24:0], {39{1'b0}}} : 64'bz;  // Controlled_Buffer controlled_buffer_103
  adder128bit adder128bit_57 (
    .input1a(pull_resistor_114_node), .input1b(pull_resistor_51_node), .input2a(pull_resistor_115_node),
    .input2b(pull_resistor_50_node), .output1a(adder128bit_57_output1a), .output1b(adder128bit_57_output1b));  // open: inflow, overflow
  Pull_Resistor pull_resistor_104 (.node(pull_resistor_104_node));
  Pull_Resistor pull_resistor_105 (.node(pull_resistor_105_node));
  Pull_Resistor pull_resistor_106 (.node(pull_resistor_106_node));
  assign pull_resistor_104_node = input1[40] ? {input2[23:0], {40{1'b0}}} : 64'bz;  // Controlled_Buffer controlled_buffer_104
  assign pull_resistor_105_node = input1[41] ? {input2[22:0], {41{1'b0}}} : 64'bz;  // Controlled_Buffer controlled_buffer_105
  adder128bit adder128bit_58 (
    .input1a(pull_resistor_116_node), .input1b(pull_resistor_55_node), .input2a(pull_resistor_117_node),
    .input2b(pull_resistor_54_node), .output1a(adder128bit_58_output1a), .output1b(adder128bit_58_output1b));  // open: inflow, overflow
  Pull_Resistor pull_resistor_107 (.node(pull_resistor_107_node));
  Pull_Resistor pull_resistor_108 (.node(pull_resistor_108_node));
  assign pull_resistor_106_node = input1[42] ? {input2[21:0], {42{1'b0}}} : 64'bz;  // Controlled_Buffer controlled_buffer_106
  assign pull_resistor_107_node = input1[43] ? {input2[20:0], {43{1'b0}}} : 64'bz;  // Controlled_Buffer controlled_buffer_107
  assign pull_resistor_108_node = input1[44] ? {input2[19:0], {44{1'b0}}} : 64'bz;  // Controlled_Buffer controlled_buffer_108
  Pull_Resistor pull_resistor_109 (.node(pull_resistor_109_node));
  Pull_Resistor pull_resistor_110 (.node(pull_resistor_110_node));
  Pull_Resistor pull_resistor_111 (.node(pull_resistor_111_node));
  assign pull_resistor_109_node = input1[45] ? {input2[18:0], {45{1'b0}}} : 64'bz;  // Controlled_Buffer controlled_buffer_109
  assign pull_resistor_110_node = input1[46] ? {input2[17:0], {46{1'b0}}} : 64'bz;  // Controlled_Buffer controlled_buffer_110
  assign pull_resistor_111_node = input1[47] ? {input2[16:0], {47{1'b0}}} : 64'bz;  // Controlled_Buffer controlled_buffer_111
  adder128bit adder128bit_59 (
    .input1a(pull_resistor_118_node), .input1b(pull_resistor_53_node), .input2a(pull_resistor_119_node),
    .input2b(pull_resistor_57_node), .output1a(adder128bit_59_output1a), .output1b(adder128bit_59_output1b));  // open: inflow, overflow
  Pull_Resistor pull_resistor_112 (.node(pull_resistor_112_node));
  Pull_Resistor pull_resistor_113 (.node(pull_resistor_113_node));
  Pull_Resistor pull_resistor_114 (.node(pull_resistor_114_node));
  assign pull_resistor_112_node = input1[48] ? {input2[15:0], {48{1'b0}}} : 64'bz;  // Controlled_Buffer controlled_buffer_112
  assign pull_resistor_113_node = input1[49] ? {input2[14:0], {49{1'b0}}} : 64'bz;  // Controlled_Buffer controlled_buffer_113
  adder128bit adder128bit_60 (
    .input1a(pull_resistor_120_node), .input1b(pull_resistor_56_node), .input2a(pull_resistor_121_node),
    .input2b(controlled_buffer_56_out), .output1a(adder128bit_60_output1a), .output1b(adder128bit_60_output1b));  // open: inflow, overflow
  Pull_Resistor pull_resistor_115 (.node(pull_resistor_115_node));
  Pull_Resistor pull_resistor_116 (.node(pull_resistor_116_node));
  assign pull_resistor_114_node = input1[50] ? {input2[13:0], {50{1'b0}}} : 64'bz;  // Controlled_Buffer controlled_buffer_114
  assign pull_resistor_115_node = input1[51] ? {input2[12:0], {51{1'b0}}} : 64'bz;  // Controlled_Buffer controlled_buffer_115
  assign pull_resistor_116_node = input1[52] ? {input2[11:0], {52{1'b0}}} : 64'bz;  // Controlled_Buffer controlled_buffer_116
  Pull_Resistor pull_resistor_117 (.node(pull_resistor_117_node));
  Pull_Resistor pull_resistor_118 (.node(pull_resistor_118_node));
  Pull_Resistor pull_resistor_119 (.node(pull_resistor_119_node));
  assign pull_resistor_117_node = input1[53] ? {input2[10:0], {53{1'b0}}} : 64'bz;  // Controlled_Buffer controlled_buffer_117
  assign pull_resistor_118_node = input1[54] ? {input2[9:0], {54{1'b0}}} : 64'bz;  // Controlled_Buffer controlled_buffer_118
  assign pull_resistor_119_node = input1[55] ? {input2[8:0], {55{1'b0}}} : 64'bz;  // Controlled_Buffer controlled_buffer_119
  adder128bit adder128bit_61 (
    .input1a(pull_resistor_122_node), .input1b(pull_resistor_59_node), .input2a(pull_resistor_123_node),
    .input2b(pull_resistor_58_node), .output1a(adder128bit_61_output1a), .output1b(adder128bit_61_output1b));  // open: inflow, overflow
  Pull_Resistor pull_resistor_120 (.node(pull_resistor_120_node));
  Pull_Resistor pull_resistor_121 (.node(pull_resistor_121_node));
  Pull_Resistor pull_resistor_122 (.node(pull_resistor_122_node));
  assign pull_resistor_120_node = input1[56] ? {input2[7:0], {56{1'b0}}} : 64'bz;  // Controlled_Buffer controlled_buffer_120
  assign pull_resistor_121_node = input1[57] ? {input2[6:0], {57{1'b0}}} : 64'bz;  // Controlled_Buffer controlled_buffer_121
  Pull_Resistor pull_resistor_123 (.node(pull_resistor_123_node));
  Pull_Resistor pull_resistor_124 (.node(pull_resistor_124_node));
  assign pull_resistor_122_node = input1[58] ? {input2[5:0], {58{1'b0}}} : 64'bz;  // Controlled_Buffer controlled_buffer_122
  assign pull_resistor_123_node = input1[59] ? {input2[4:0], {59{1'b0}}} : 64'bz;  // Controlled_Buffer controlled_buffer_123
  assign pull_resistor_124_node = input1[60] ? {input2[3:0], {60{1'b0}}} : 64'bz;  // Controlled_Buffer controlled_buffer_124
  adder128bit adder128bit_62 (
    .input1a(pull_resistor_124_node), .input1b(pull_resistor_63_node), .input2a(pull_resistor_125_node),
    .input2b(pull_resistor_62_node), .output1a(adder128bit_62_output1a), .output1b(adder128bit_62_output1b));  // open: inflow, overflow
  Pull_Resistor pull_resistor_125 (.node(pull_resistor_125_node));
  Pull_Resistor pull_resistor_126 (.node(pull_resistor_126_node));
  Pull_Resistor pull_resistor_127 (.node(pull_resistor_127_node));
  assign pull_resistor_125_node = input1[61] ? {input2[2:0], {61{1'b0}}} : 64'bz;  // Controlled_Buffer controlled_buffer_125
  assign pull_resistor_126_node = input1[62] ? {input2[1:0], {62{1'b0}}} : 64'bz;  // Controlled_Buffer controlled_buffer_126
  assign pull_resistor_127_node = input1[63] ? {input2[0], {63{1'b0}}} : 64'bz;  // Controlled_Buffer controlled_buffer_127
  adder128bit adder128bit_63 (
    .input1a(adder128bit_64_output1a), .input1b(adder128bit_64_output1b), .input2a(inflow),
    .output1a(adder128bit_63_output1a), .output1b(adder128bit_63_output1b));  // open: inflow, input2b, overflow
  adder128bit adder128bit_64 (
    .input1a(pull_resistor_126_node), .input1b(pull_resistor_61_node), .input2a(pull_resistor_127_node),
    .output1a(adder128bit_64_output1a), .output1b(adder128bit_64_output1b));  // open: inflow, input2b, overflow
endmodule
module comparatoru64bit (
  input  [63:0] input1,
  input  [63:0] input2,
  output greater1,
  output equal1,
  output less1
);

  wire and_1_out, and_2_out, and_3_out, and_4_out, and_5_out, and_6_out, and_7_out, and_8_out, and_9_out,
       and_10_out, and_11_out, and_12_out, and_13_out, and_14_out, and_15_out, and_16_out, and_17_out,
       and_18_out, and_19_out, and_20_out, and_21_out, and_22_out, and_23_out, and_24_out, and_25_out,
       and_26_out, and_27_out, and_28_out, and_29_out, and_30_out, and_31_out, and_32_out, and_33_out,
       and_34_out, and_35_out, and_36_out, and_37_out, and_38_out, and_39_out, and_40_out, and_41_out,
       and_42_out, and_43_out, and_44_out, and_45_out, and_46_out, and_47_out, and_48_out, and_49_out,
       and_50_out, and_51_out, and_52_out, and_53_out, and_54_out, and_55_out, and_56_out, and_57_out,
       and_58_out, and_59_out, and_60_out, and_61_out, and_62_out, and_63_out, and_64_out, and_66_out,
       and_67_out, and_68_out, and_69_out, and_70_out, and_71_out, and_72_out, and_73_out, and_74_out,
       and_75_out, and_76_out, and_77_out, and_78_out, and_79_out, and_80_out, and_81_out, and_82_out,
       and_83_out, and_84_out, and_85_out, and_86_out, and_87_out, and_88_out, and_89_out, and_90_out,
       and_91_out, and_92_out, and_93_out, and_94_out, and_95_out, and_96_out, and_97_out, and_98_out,
       and_99_out, and_100_out, and_101_out, and_102_out, and_103_out, and_104_out, and_105_out, and_106_out,
       and_107_out, and_108_out, and_109_out, and_110_out, and_111_out, and_112_out, and_113_out,
       and_114_out, and_115_out, and_116_out, and_117_out, and_118_out, and_119_out, and_120_out,
       and_121_out, and_122_out, and_123_out, and_124_out, and_125_out, and_126_out, and_127_out,
       and_128_out, and_129_out, and_130_out, and_131_out, and_132_out, and_133_out, and_134_out,
       and_135_out, and_136_out, and_137_out, and_138_out, and_139_out, and_140_out, and_141_out,
       and_142_out, and_143_out, and_144_out, and_145_out, and_146_out, and_147_out, and_148_out,
       and_149_out, and_150_out, and_151_out, and_152_out, and_153_out, and_154_out, and_155_out,
       and_156_out, and_157_out, and_158_out, and_159_out, and_160_out, and_161_out, and_162_out,
       and_163_out, and_164_out, and_165_out, and_166_out, and_167_out, and_168_out, and_169_out,
       and_170_out, and_171_out, and_172_out, and_173_out, and_174_out, and_175_out, and_176_out,
       and_177_out, and_178_out, and_179_out, and_180_out, and_181_out, and_182_out, and_183_out,
       and_184_out, and_185_out, and_186_out, and_187_out, and_188_out, and_189_out, and_190_out,
       and_191_out, not_1_out, not_2_out, not_3_out, not_4_out, not_5_out, not_6_out, not_7_out, not_8_out,
       not_9_out, not_10_out, not_11_out, not_12_out, not_13_out, not_14_out, not_15_out, not_16_out,
       not_17_out, not_18_out, not_19_out, not_20_out, not_21_out, not_22_out, not_23_out, not_24_out,
       not_25_out, not_26_out, not_27_out, not_28_out, not_29_out, not_30_out, not_31_out, not_32_out,
       not_33_out, not_34_out, not_35_out, not_36_out, not_37_out, not_38_out, not_39_out, not_40_out,
       not_41_out, not_42_out, not_43_out, not_44_out, not_45_out, not_46_out, not_47_out, not_48_out,
       not_49_out, not_50_out, not_51_out, not_52_out, not_53_out, not_54_out, not_55_out, not_56_out,
       not_57_out, not_58_out, not_59_out, not_60_out, not_61_out, not_62_out, not_63_out, not_64_out,
       not_65_out, not_66_out, not_67_out, not_68_out, not_69_out, not_70_out, not_71_out, not_72_out,
       not_73_out, not_74_out, not_75_out, not_76_out, not_77_out, not_78_out, not_79_out, not_80_out,
       not_81_out, not_82_out, not_83_out, not_84_out, not_85_out, not_86_out, not_87_out, not_88_out,
       not_89_out, not_90_out, not_91_out, not_92_out, not_93_out, not_94_out, not_95_out, not_96_out,
       not_97_out, not_98_out, not_99_out, not_100_out, not_101_out, not_102_out, not_103_out, not_104_out,
       not_105_out, not_106_out, not_107_out, not_108_out, not_109_out, not_110_out, not_111_out,
       not_112_out, not_113_out, not_114_out, not_115_out, not_116_out, not_117_out, not_118_out,
       not_119_out, not_120_out, not_121_out, not_122_out, not_123_out, not_124_out, not_125_out,
       not_126_out, not_127_out, not_128_out, or_2_out, or_3_out, or_4_out, or_5_out, or_6_out, or_7_out,
       or_8_out, or_9_out, or_10_out, or_11_out, or_12_out, or_13_out, or_14_out, or_15_out, or_16_out,
       or_17_out, or_18_out, or_19_out, or_20_out, or_21_out, or_22_out, or_23_out, or_24_out, or_25_out,
       or_26_out, or_27_out, or_28_out, or_29_out, or_30_out, or_31_out, or_32_out, or_33_out, or_34_out,
       or_35_out, or_36_out, or_37_out, or_38_out, or_39_out, or_40_out, or_41_out, or_42_out, or_43_out,
       or_44_out, or_45_out, or_46_out, or_47_out, or_48_out, or_49_out, or_50_out, or_51_out, or_52_out,
       or_53_out, or_54_out, or_55_out, or_56_out, or_57_out, or_58_out, or_59_out, or_60_out, or_61_out,
       or_62_out, or_63_out, or_65_out, or_66_out, or_67_out, or_68_out, or_69_out, or_70_out, or_71_out,
       or_72_out, or_73_out, or_74_out, or_75_out, or_76_out, or_77_out, or_78_out, or_79_out, or_80_out,
       or_81_out, or_82_out, or_83_out, or_84_out, or_85_out, or_86_out, or_87_out, or_88_out, or_89_out,
       or_90_out, or_91_out, or_92_out, or_93_out, or_94_out, or_95_out, or_96_out, or_97_out, or_98_out,
       or_99_out, or_100_out, or_101_out, or_102_out, or_103_out, or_104_out, or_105_out, or_106_out,
       or_107_out, or_108_out, or_109_out, or_110_out, or_111_out, or_112_out, or_113_out, or_114_out,
       or_115_out, or_116_out, or_117_out, or_118_out, or_119_out, or_120_out, or_121_out, or_122_out,
       or_123_out, or_124_out, or_125_out, or_126_out, xnor_1_out, xnor_2_out, xnor_3_out, xnor_4_out,
       xnor_5_out, xnor_6_out, xnor_7_out, xnor_8_out, xnor_9_out, xnor_10_out, xnor_11_out, xnor_12_out,
       xnor_13_out, xnor_14_out, xnor_15_out, xnor_16_out, xnor_17_out, xnor_18_out, xnor_19_out,
       xnor_20_out, xnor_21_out, xnor_22_out, xnor_23_out, xnor_24_out, xnor_25_out, xnor_26_out,
       xnor_27_out, xnor_28_out, xnor_29_out, xnor_30_out, xnor_31_out, xnor_32_out, xnor_33_out,
       xnor_34_out, xnor_35_out, xnor_36_out, xnor_37_out, xnor_38_out, xnor_39_out, xnor_40_out,
       xnor_41_out, xnor_42_out, xnor_43_out, xnor_44_out, xnor_45_out, xnor_46_out, xnor_47_out,
       xnor_48_out, xnor_49_out, xnor_50_out, xnor_51_out, xnor_52_out, xnor_53_out, xnor_54_out,
       xnor_55_out, xnor_56_out, xnor_57_out, xnor_58_out, xnor_59_out, xnor_60_out, xnor_61_out,
       xnor_62_out, xnor_63_out, xnor_64_out;

  or or_1 (greater1, or_2_out, and_1_out);
  or or_2 (or_2_out, or_3_out, and_2_out);
  or or_3 (or_3_out, or_4_out, and_3_out);
  or or_4 (or_4_out, or_5_out, and_4_out);
  or or_5 (or_5_out, or_6_out, and_5_out);
  or or_6 (or_6_out, or_7_out, and_6_out);
  or or_7 (or_7_out, or_8_out, and_7_out);
  or or_8 (or_8_out, or_9_out, and_8_out);
  or or_9 (or_9_out, or_10_out, and_9_out);
  or or_10 (or_10_out, or_11_out, and_10_out);
  or or_11 (or_11_out, or_12_out, and_11_out);
  or or_12 (or_12_out, or_13_out, and_12_out);
  or or_13 (or_13_out, or_14_out, and_13_out);
  or or_14 (or_14_out, or_15_out, and_14_out);
  or or_15 (or_15_out, or_16_out, and_15_out);
  or or_16 (or_16_out, or_17_out, and_16_out);
  or or_17 (or_17_out, or_18_out, and_17_out);
  or or_18 (or_18_out, or_19_out, and_18_out);
  or or_19 (or_19_out, or_20_out, and_19_out);
  or or_20 (or_20_out, or_21_out, and_20_out);
  or or_21 (or_21_out, or_22_out, and_21_out);
  or or_22 (or_22_out, or_23_out, and_22_out);
  or or_23 (or_23_out, or_24_out, and_23_out);
  or or_24 (or_24_out, or_25_out, and_24_out);
  or or_25 (or_25_out, or_26_out, and_25_out);
  or or_26 (or_26_out, or_27_out, and_26_out);
  or or_27 (or_27_out, or_28_out, and_27_out);
  or or_28 (or_28_out, or_29_out, and_28_out);
  or or_29 (or_29_out, or_30_out, and_29_out);
  or or_30 (or_30_out, or_31_out, and_30_out);
  or or_31 (or_31_out, or_32_out, and_31_out);
  or or_32 (or_32_out, or_33_out, and_32_out);
  or or_33 (or_33_out, or_34_out, and_33_out);
  or or_34 (or_34_out, or_35_out, and_34_out);
  or or_35 (or_35_out, or_36_out, and_35_out);
  or or_36 (or_36_out, or_37_out, and_36_out);
  or or_37 (or_37_out, or_38_out, and_37_out);
  or or_38 (or_38_out, or_39_out, and_38_out);
  or or_39 (or_39_out, or_40_out, and_39_out);
  or or_40 (or_40_out, or_41_out, and_40_out);
  or or_41 (or_41_out, or_42_out, and_41_out);
  or or_42 (or_42_out, or_43_out, and_42_out);
  or or_43 (or_43_out, or_44_out, and_43_out);
  or or_44 (or_44_out, or_45_out, and_44_out);
  or or_45 (or_45_out, or_46_out, and_45_out);
  or or_46 (or_46_out, or_47_out, and_46_out);
  or or_47 (or_47_out, or_48_out, and_47_out);
  or or_48 (or_48_out, or_49_out, and_48_out);
  or or_49 (or_49_out, or_50_out, and_49_out);
  or or_50 (or_50_out, or_51_out, and_50_out);
  or or_51 (or_51_out, or_52_out, and_51_out);
  or or_52 (or_52_out, or_53_out, and_52_out);
  or or_53 (or_53_out, or_54_out, and_53_out);
  or or_54 (or_54_out, or_55_out, and_54_out);
  or or_55 (or_55_out, or_56_out, and_55_out);
  or or_56 (or_56_out, or_57_out, and_56_out);
  or or_57 (or_57_out, or_58_out, and_57_out);
  or or_58 (or_58_out, or_59_out, and_58_out);
  or or_59 (or_59_out, or_60_out, and_59_out);
  or or_60 (or_60_out, or_61_out, and_60_out);
  or or_61 (or_61_out, or_62_out, and_61_out);
  or or_62 (or_62_out, or_63_out, and_62_out);
  or or_63 (or_63_out, and_64_out, and_63_out);
  and and_1 (and_1_out, input1[0], and_66_out, not_1_out);
  and and_2 (and_2_out, input1[1], and_67_out, not_2_out);
  and and_3 (and_3_out, input1[2], and_68_out, not_3_out);
  and and_4 (and_4_out, input1[3], and_69_out, not_4_out);
  and and_5 (and_5_out, input1[4], and_70_out, not_5_out);
  and and_6 (and_6_out, input1[5], and_71_out, not_6_out);
  and and_7 (and_7_out, input1[6], and_72_out, not_7_out);
  and and_8 (and_8_out, input1[7], and_73_out, not_8_out);
  and and_9 (and_9_out, input1[8], and_74_out, not_9_out);
  and and_10 (and_10_out, input1[9], and_75_out, not_10_out);
  and and_11 (and_11_out, input1[10], and_76_out, not_11_out);
  and and_12 (and_12_out, input1[11], and_77_out, not_12_out);
  and and_13 (and_13_out, input1[12], and_78_out, not_13_out);
  and and_14 (and_14_out, input1[13], and_79_out, not_14_out);
  and and_15 (and_15_out, input1[14], and_80_out, not_15_out);
  and and_16 (and_16_out, input1[15], and_81_out, not_16_out);
  and and_17 (and_17_out, input1[16], and_82_out, not_17_out);
  and and_18 (and_18_out, input1[17], and_83_out, not_18_out);
  and and_19 (and_19_out, input1[18], and_84_out, not_19_out);
  and and_20 (and_20_out, input1[19], and_85_out, not_20_out);
  and and_21 (and_21_out, input1[20], and_86_out, not_21_out);
  and and_22 (and_22_out, input1[21], and_87_out, not_22_out);
  and and_23 (and_23_out, input1[22], and_88_out, not_23_out);
  and and_24 (and_24_out, input1[23], and_89_out, not_24_out);
  and and_25 (and_25_out, input1[24], and_90_out, not_25_out);
  and and_26 (and_26_out, input1[25], and_91_out, not_26_out);
  and and_27 (and_27_out, input1[26], and_92_out, not_27_out);
  and and_28 (and_28_out, input1[27], and_93_out, not_28_out);
  and and_29 (and_29_out, input1[28], and_94_out, not_29_out);
  and and_30 (and_30_out, input1[29], and_95_out, not_30_out);
  and and_31 (and_31_out, input1[30], and_96_out, not_31_out);
  and and_32 (and_32_out, input1[31], and_97_out, not_32_out);
  and and_33 (and_33_out, input1[32], and_98_out, not_33_out);
  and and_34 (and_34_out, input1[33], and_99_out, not_34_out);
  and and_35 (and_35_out, input1[34], and_100_out, not_35_out);
  and and_36 (and_36_out, input1[35], and_101_out, not_36_out);
  and and_37 (and_37_out, input1[36], and_102_out, not_37_out);
  and and_38 (and_38_out, input1[37], and_103_out, not_38_out);
  and and_39 (and_39_out, input1[38], and_104_out, not_39_out);
  and and_40 (and_40_out, input1[39], and_105_out, not_40_out);
  and and_41 (and_41_out, input1[40], and_106_out, not_41_out);
  and and_42 (and_42_out, input1[41], and_107_out, not_42_out);
  and and_43 (and_43_out, input1[42], and_108_out, not_43_out);
  and and_44 (and_44_out, input1[43], and_109_out, not_44_out);
  and and_45 (and_45_out, input1[44], and_110_out, not_45_out);
  and and_46 (and_46_out, input1[45], and_111_out, not_46_out);
  and and_47 (and_47_out, input1[46], and_112_out, not_47_out);
  and and_48 (and_48_out, input1[47], and_113_out, not_48_out);
  and and_49 (and_49_out, input1[48], and_114_out, not_49_out);
  and and_50 (and_50_out, input1[49], and_115_out, not_50_out);
  and and_51 (and_51_out, input1[50], and_116_out, not_51_out);
  and and_52 (and_52_out, input1[51], and_117_out, not_52_out);
  and and_53 (and_53_out, input1[52], and_118_out, not_53_out);
  and and_54 (and_54_out, input1[53], and_119_out, not_54_out);
  and and_55 (and_55_out, input1[54], and_120_out, not_55_out);
  and and_56 (and_56_out, input1[55], and_121_out, not_56_out);
  and and_57 (and_57_out, input1[56], and_122_out, not_57_out);
  and and_58 (and_58_out, input1[57], and_123_out, not_58_out);
  and and_59 (and_59_out, input1[58], and_124_out, not_59_out);
  and and_60 (and_60_out, input1[59], and_125_out, not_60_out);
  and and_61 (and_61_out, input1[60], and_126_out, not_61_out);
  and and_62 (and_62_out, input1[61], and_127_out, not_62_out);
  and and_63 (and_63_out, input1[62], xnor_64_out, not_63_out);
  and and_64 (and_64_out, input1[63], not_64_out);
  not not_1 (not_1_out, input2[0]);
  not not_2 (not_2_out, input2[1]);
  not not_3 (not_3_out, input2[2]);
  not not_4 (not_4_out, input2[3]);
  not not_5 (not_5_out, input2[4]);
  not not_6 (not_6_out, input2[5]);
  not not_7 (not_7_out, input2[6]);
  not not_8 (not_8_out, input2[7]);
  not not_9 (not_9_out, input2[8]);
  not not_10 (not_10_out, input2[9]);
  not not_11 (not_11_out, input2[10]);
  not not_12 (not_12_out, input2[11]);
  not not_13 (not_13_out, input2[12]);
  not not_14 (not_14_out, input2[13]);
  not not_15 (not_15_out, input2[14]);
  not not_16 (not_16_out, input2[15]);
  not not_17 (not_17_out, input2[16]);
  not not_18 (not_18_out, input2[17]);
  not not_19 (not_19_out, input2[18]);
  not not_20 (not_20_out, input2[19]);
  not not_21 (not_21_out, input2[20]);
  not not_22 (not_22_out, input2[21]);
  not not_23 (not_23_out, input2[22]);
  not not_24 (not_24_out, input2[23]);
  not not_25 (not_25_out, input2[24]);
  not not_26 (not_26_out, input2[25]);
  not not_27 (not_27_out, input2[26]);
  not not_28 (not_28_out, input2[27]);
  not not_29 (not_29_out, input2[28]);
  not not_30 (not_30_out, input2[29]);
  not not_31 (not_31_out, input2[30]);
  not not_32 (not_32_out, input2[31]);
  not not_33 (not_33_out, input2[32]);
  not not_34 (not_34_out, input2[33]);
  not not_35 (not_35_out, input2[34]);
  not not_36 (not_36_out, input2[35]);
  not not_37 (not_37_out, input2[36]);
  not not_38 (not_38_out, input2[37]);
  not not_39 (not_39_out, input2[38]);
  not not_40 (not_40_out, input2[39]);
  not not_41 (not_41_out, input2[40]);
  not not_42 (not_42_out, input2[41]);
  not not_43 (not_43_out, input2[42]);
  not not_44 (not_44_out, input2[43]);
  not not_45 (not_45_out, input2[44]);
  not not_46 (not_46_out, input2[45]);
  not not_47 (not_47_out, input2[46]);
  not not_48 (not_48_out, input2[47]);
  not not_49 (not_49_out, input2[48]);
  not not_50 (not_50_out, input2[49]);
  not not_51 (not_51_out, input2[50]);
  not not_52 (not_52_out, input2[51]);
  not not_53 (not_53_out, input2[52]);
  not not_54 (not_54_out, input2[53]);
  not not_55 (not_55_out, input2[54]);
  not not_56 (not_56_out, input2[55]);
  not not_57 (not_57_out, input2[56]);
  not not_58 (not_58_out, input2[57]);
  not not_59 (not_59_out, input2[58]);
  not not_60 (not_60_out, input2[59]);
  not not_61 (not_61_out, input2[60]);
  not not_62 (not_62_out, input2[61]);
  not not_63 (not_63_out, input2[62]);
  not not_64 (not_64_out, input2[63]);
  and and_65 (equal1, xnor_1_out, and_66_out);
  xnor xnor_1 (xnor_1_out, input1[0], input2[0]);
  and and_66 (and_66_out, xnor_2_out, and_67_out);
  xnor xnor_2 (xnor_2_out, input1[1], input2[1]);
  and and_67 (and_67_out, xnor_3_out, and_68_out);
  xnor xnor_3 (xnor_3_out, input1[2], input2[2]);
  and and_68 (and_68_out, xnor_4_out, and_69_out);
  xnor xnor_4 (xnor_4_out, input1[3], input2[3]);
  and and_69 (and_69_out, xnor_5_out, and_70_out);
  xnor xnor_5 (xnor_5_out, input1[4], input2[4]);
  and and_70 (and_70_out, xnor_6_out, and_71_out);
  xnor xnor_6 (xnor_6_out, input1[5], input2[5]);
  and and_71 (and_71_out, xnor_7_out, and_72_out);
  xnor xnor_7 (xnor_7_out, input1[6], input2[6]);
  and and_72 (and_72_out, xnor_8_out, and_73_out);
  xnor xnor_8 (xnor_8_out, input1[7], input2[7]);
  and and_73 (and_73_out, xnor_9_out, and_74_out);
  xnor xnor_9 (xnor_9_out, input1[8], input2[8]);
  and and_74 (and_74_out, xnor_10_out, and_75_out);
  xnor xnor_10 (xnor_10_out, input1[9], input2[9]);
  and and_75 (and_75_out, xnor_11_out, and_76_out);
  xnor xnor_11 (xnor_11_out, input1[10], input2[10]);
  and and_76 (and_76_out, xnor_12_out, and_77_out);
  xnor xnor_12 (xnor_12_out, input1[11], input2[11]);
  and and_77 (and_77_out, xnor_13_out, and_78_out);
  xnor xnor_13 (xnor_13_out, input1[12], input2[12]);
  and and_78 (and_78_out, xnor_14_out, and_79_out);
  xnor xnor_14 (xnor_14_out, input1[13], input2[13]);
  and and_79 (and_79_out, xnor_15_out, and_80_out);
  xnor xnor_15 (xnor_15_out, input1[14], input2[14]);
  and and_80 (and_80_out, xnor_16_out, and_81_out);
  xnor xnor_16 (xnor_16_out, input1[15], input2[15]);
  and and_81 (and_81_out, xnor_17_out, and_82_out);
  xnor xnor_17 (xnor_17_out, input1[16], input2[16]);
  and and_82 (and_82_out, xnor_18_out, and_83_out);
  xnor xnor_18 (xnor_18_out, input1[17], input2[17]);
  and and_83 (and_83_out, xnor_19_out, and_84_out);
  xnor xnor_19 (xnor_19_out, input1[18], input2[18]);
  and and_84 (and_84_out, xnor_20_out, and_85_out);
  xnor xnor_20 (xnor_20_out, input1[19], input2[19]);
  and and_85 (and_85_out, xnor_21_out, and_86_out);
  xnor xnor_21 (xnor_21_out, input1[20], input2[20]);
  and and_86 (and_86_out, xnor_22_out, and_87_out);
  xnor xnor_22 (xnor_22_out, input1[21], input2[21]);
  and and_87 (and_87_out, xnor_23_out, and_88_out);
  xnor xnor_23 (xnor_23_out, input1[22], input2[22]);
  and and_88 (and_88_out, xnor_24_out, and_89_out);
  xnor xnor_24 (xnor_24_out, input1[23], input2[23]);
  and and_89 (and_89_out, xnor_25_out, and_90_out);
  xnor xnor_25 (xnor_25_out, input1[24], input2[24]);
  and and_90 (and_90_out, xnor_26_out, and_91_out);
  xnor xnor_26 (xnor_26_out, input1[25], input2[25]);
  and and_91 (and_91_out, xnor_27_out, and_92_out);
  xnor xnor_27 (xnor_27_out, input1[26], input2[26]);
  and and_92 (and_92_out, xnor_28_out, and_93_out);
  xnor xnor_28 (xnor_28_out, input1[27], input2[27]);
  and and_93 (and_93_out, xnor_29_out, and_94_out);
  xnor xnor_29 (xnor_29_out, input1[28], input2[28]);
  and and_94 (and_94_out, xnor_30_out, and_95_out);
  xnor xnor_30 (xnor_30_out, input1[29], input2[29]);
  and and_95 (and_95_out, xnor_31_out, and_96_out);
  xnor xnor_31 (xnor_31_out, input1[30], input2[30]);
  and and_96 (and_96_out, xnor_32_out, and_97_out);
  xnor xnor_32 (xnor_32_out, input1[31], input2[31]);
  and and_97 (and_97_out, xnor_33_out, and_98_out);
  xnor xnor_33 (xnor_33_out, input1[32], input2[32]);
  and and_98 (and_98_out, xnor_34_out, and_99_out);
  xnor xnor_34 (xnor_34_out, input1[33], input2[33]);
  and and_99 (and_99_out, xnor_35_out, and_100_out);
  xnor xnor_35 (xnor_35_out, input1[34], input2[34]);
  and and_100 (and_100_out, xnor_36_out, and_101_out);
  xnor xnor_36 (xnor_36_out, input1[35], input2[35]);
  and and_101 (and_101_out, xnor_37_out, and_102_out);
  xnor xnor_37 (xnor_37_out, input1[36], input2[36]);
  and and_102 (and_102_out, xnor_38_out, and_103_out);
  xnor xnor_38 (xnor_38_out, input1[37], input2[37]);
  and and_103 (and_103_out, xnor_39_out, and_104_out);
  xnor xnor_39 (xnor_39_out, input1[38], input2[38]);
  and and_104 (and_104_out, xnor_40_out, and_105_out);
  xnor xnor_40 (xnor_40_out, input1[39], input2[39]);
  and and_105 (and_105_out, xnor_41_out, and_106_out);
  xnor xnor_41 (xnor_41_out, input1[40], input2[40]);
  and and_106 (and_106_out, xnor_42_out, and_107_out);
  xnor xnor_42 (xnor_42_out, input1[41], input2[41]);
  and and_107 (and_107_out, xnor_43_out, and_108_out);
  xnor xnor_43 (xnor_43_out, input1[42], input2[42]);
  and and_108 (and_108_out, xnor_44_out, and_109_out);
  xnor xnor_44 (xnor_44_out, input1[43], input2[43]);
  and and_109 (and_109_out, xnor_45_out, and_110_out);
  xnor xnor_45 (xnor_45_out, input1[44], input2[44]);
  and and_110 (and_110_out, xnor_46_out, and_111_out);
  xnor xnor_46 (xnor_46_out, input1[45], input2[45]);
  and and_111 (and_111_out, xnor_47_out, and_112_out);
  xnor xnor_47 (xnor_47_out, input1[46], input2[46]);
  and and_112 (and_112_out, xnor_48_out, and_113_out);
  xnor xnor_48 (xnor_48_out, input1[47], input2[47]);
  and and_113 (and_113_out, xnor_49_out, and_114_out);
  xnor xnor_49 (xnor_49_out, input1[48], input2[48]);
  and and_114 (and_114_out, xnor_50_out, and_115_out);
  xnor xnor_50 (xnor_50_out, input1[49], input2[49]);
  and and_115 (and_115_out, xnor_51_out, and_116_out);
  xnor xnor_51 (xnor_51_out, input1[50], input2[50]);
  and and_116 (and_116_out, xnor_52_out, and_117_out);
  xnor xnor_52 (xnor_52_out, input1[51], input2[51]);
  and and_117 (and_117_out, xnor_53_out, and_118_out);
  xnor xnor_53 (xnor_53_out, input1[52], input2[52]);
  and and_118 (and_118_out, xnor_54_out, and_119_out);
  xnor xnor_54 (xnor_54_out, input1[53], input2[53]);
  and and_119 (and_119_out, xnor_55_out, and_120_out);
  xnor xnor_55 (xnor_55_out, input1[54], input2[54]);
  and and_120 (and_120_out, xnor_56_out, and_121_out);
  xnor xnor_56 (xnor_56_out, input1[55], input2[55]);
  and and_121 (and_121_out, xnor_57_out, and_122_out);
  xnor xnor_57 (xnor_57_out, input1[56], input2[56]);
  and and_122 (and_122_out, xnor_58_out, and_123_out);
  xnor xnor_58 (xnor_58_out, input1[57], input2[57]);
  and and_123 (and_123_out, xnor_59_out, and_124_out);
  xnor xnor_59 (xnor_59_out, input1[58], input2[58]);
  and and_124 (and_124_out, xnor_60_out, and_125_out);
  xnor xnor_60 (xnor_60_out, input1[59], input2[59]);
  and and_125 (and_125_out, xnor_61_out, and_126_out);
  xnor xnor_61 (xnor_61_out, input1[60], input2[60]);
  and and_126 (and_126_out, xnor_62_out, and_127_out);
  xnor xnor_62 (xnor_62_out, input1[61], input2[61]);
  and and_127 (and_127_out, xnor_63_out, xnor_64_out);
  xnor xnor_63 (xnor_63_out, input1[62], input2[62]);
  xnor xnor_64 (xnor_64_out, input1[63], input2[63]);
  not not_65 (not_65_out, input1[0]);
  not not_66 (not_66_out, input1[1]);
  not not_67 (not_67_out, input1[2]);
  not not_68 (not_68_out, input1[3]);
  not not_69 (not_69_out, input1[4]);
  not not_70 (not_70_out, input1[5]);
  not not_71 (not_71_out, input1[6]);
  not not_72 (not_72_out, input1[7]);
  not not_73 (not_73_out, input1[8]);
  not not_74 (not_74_out, input1[9]);
  not not_75 (not_75_out, input1[10]);
  not not_76 (not_76_out, input1[11]);
  not not_77 (not_77_out, input1[12]);
  not not_78 (not_78_out, input1[13]);
  not not_79 (not_79_out, input1[14]);
  not not_80 (not_80_out, input1[15]);
  not not_81 (not_81_out, input1[16]);
  not not_82 (not_82_out, input1[17]);
  not not_83 (not_83_out, input1[18]);
  not not_84 (not_84_out, input1[19]);
  not not_85 (not_85_out, input1[20]);
  not not_86 (not_86_out, input1[21]);
  not not_87 (not_87_out, input1[22]);
  not not_88 (not_88_out, input1[23]);
  not not_89 (not_89_out, input1[24]);
  not not_90 (not_90_out, input1[25]);
  not not_91 (not_91_out, input1[26]);
  not not_92 (not_92_out, input1[27]);
  not not_93 (not_93_out, input1[28]);
  not not_94 (not_94_out, input1[29]);
  not not_95 (not_95_out, input1[30]);
  not not_96 (not_96_out, input1[31]);
  not not_97 (not_97_out, input1[32]);
  not not_98 (not_98_out, input1[33]);
  not not_99 (not_99_out, input1[34]);
  not not_100 (not_100_out, input1[35]);
  not not_101 (not_101_out, input1[36]);
  not not_102 (not_102_out, input1[37]);
  not not_103 (not_103_out, input1[38]);
  not not_104 (not_104_out, input1[39]);
  not not_105 (not_105_out, input1[40]);
  not not_106 (not_106_out, input1[41]);
  not not_107 (not_107_out, input1[42]);
  not not_108 (not_108_out, input1[43]);
  not not_109 (not_109_out, input1[44]);
  not not_110 (not_110_out, input1[45]);
  not not_111 (not_111_out, input1[46]);
  not not_112 (not_112_out, input1[47]);
  not not_113 (not_113_out, input1[48]);
  not not_114 (not_114_out, input1[49]);
  not not_115 (not_115_out, input1[50]);
  not not_116 (not_116_out, input1[51]);
  not not_117 (not_117_out, input1[52]);
  not not_118 (not_118_out, input1[53]);
  not not_119 (not_119_out, input1[54]);
  not not_120 (not_120_out, input1[55]);
  not not_121 (not_121_out, input1[56]);
  not not_122 (not_122_out, input1[57]);
  not not_123 (not_123_out, input1[58]);
  not not_124 (not_124_out, input1[59]);
  not not_125 (not_125_out, input1[60]);
  not not_126 (not_126_out, input1[61]);
  not not_127 (not_127_out, input1[62]);
  not not_128 (not_128_out, input1[63]);
  and and_128 (and_128_out, not_65_out, input2[0]);
  and and_129 (and_129_out, not_66_out, input2[1]);
  and and_130 (and_130_out, not_67_out, input2[2]);
  and and_131 (and_131_out, not_68_out, input2[3]);
  and and_132 (and_132_out, not_69_out, input2[4]);
  and and_133 (and_133_out, not_70_out, input2[5]);
  and and_134 (and_134_out, not_71_out, input2[6]);
  and and_135 (and_135_out, not_72_out, input2[7]);
  and and_136 (and_136_out, not_73_out, input2[8]);
  and and_137 (and_137_out, not_74_out, input2[9]);
  and and_138 (and_138_out, not_75_out, input2[10]);
  and and_139 (and_139_out, not_76_out, input2[11]);
  and and_140 (and_140_out, not_77_out, input2[12]);
  and and_141 (and_141_out, not_78_out, input2[13]);
  and and_142 (and_142_out, not_79_out, input2[14]);
  and and_143 (and_143_out, not_80_out, input2[15]);
  and and_144 (and_144_out, not_81_out, input2[16]);
  and and_145 (and_145_out, not_82_out, input2[17]);
  and and_146 (and_146_out, not_83_out, input2[18]);
  and and_147 (and_147_out, not_84_out, input2[19]);
  and and_148 (and_148_out, not_85_out, input2[20]);
  and and_149 (and_149_out, not_86_out, input2[21]);
  and and_150 (and_150_out, not_87_out, input2[22]);
  and and_151 (and_151_out, not_88_out, input2[23]);
  and and_152 (and_152_out, not_89_out, input2[24]);
  and and_153 (and_153_out, not_90_out, input2[25]);
  and and_154 (and_154_out, not_91_out, input2[26]);
  and and_155 (and_155_out, not_92_out, input2[27]);
  and and_156 (and_156_out, not_93_out, input2[28]);
  and and_157 (and_157_out, not_94_out, input2[29]);
  and and_158 (and_158_out, not_95_out, input2[30]);
  and and_159 (and_159_out, not_96_out, input2[31]);
  and and_160 (and_160_out, not_97_out, input2[32]);
  and and_161 (and_161_out, not_98_out, input2[33]);
  and and_162 (and_162_out, not_99_out, input2[34]);
  and and_163 (and_163_out, not_100_out, input2[35]);
  and and_164 (and_164_out, not_101_out, input2[36]);
  and and_165 (and_165_out, not_102_out, input2[37]);
  and and_166 (and_166_out, not_103_out, input2[38]);
  and and_167 (and_167_out, not_104_out, input2[39]);
  and and_168 (and_168_out, not_105_out, input2[40]);
  and and_169 (and_169_out, not_106_out, input2[41]);
  and and_170 (and_170_out, not_107_out, and_108_out, input2[42]);
  and and_171 (and_171_out, not_108_out, and_109_out, input2[43]);
  and and_172 (and_172_out, not_109_out, and_110_out, input2[44]);
  and and_173 (and_173_out, not_110_out, and_111_out, input2[45]);
  and and_174 (and_174_out, not_111_out, and_112_out, input2[46]);
  and and_175 (and_175_out, not_112_out, and_113_out, input2[47]);
  and and_176 (and_176_out, not_113_out, and_114_out, input2[48]);
  and and_177 (and_177_out, not_114_out, and_115_out, input2[49]);
  and and_178 (and_178_out, not_115_out, and_116_out, input2[50]);
  and and_179 (and_179_out, not_116_out, and_117_out, input2[51]);
  and and_180 (and_180_out, not_117_out, and_118_out, input2[52]);
  and and_181 (and_181_out, not_118_out, and_119_out, input2[53]);
  and and_182 (and_182_out, not_119_out, and_120_out, input2[54]);
  and and_183 (and_183_out, not_120_out, and_121_out, input2[55]);
  and and_184 (and_184_out, not_121_out, and_122_out, input2[56]);
  and and_185 (and_185_out, not_122_out, and_123_out, input2[57]);
  and and_186 (and_186_out, not_123_out, and_124_out, input2[58]);
  and and_187 (and_187_out, not_124_out, and_125_out, input2[59]);
  and and_188 (and_188_out, not_125_out, and_126_out, input2[60]);
  and and_189 (and_189_out, not_126_out, and_127_out, input2[61]);
  and and_190 (and_190_out, not_127_out, xnor_64_out, input2[62]);
  and and_191 (and_191_out, not_128_out, input2[63]);
  or or_64 (less1, and_128_out, or_65_out);
  or or_65 (or_65_out, and_129_out, or_66_out);
  or or_66 (or_66_out, and_130_out, or_67_out);
  or or_67 (or_67_out, and_131_out, or_68_out);
  or or_68 (or_68_out, and_132_out, or_69_out);
  or or_69 (or_69_out, and_133_out, or_70_out);
  or or_70 (or_70_out, and_134_out, or_71_out);
  or or_71 (or_71_out, and_135_out, or_72_out);
  or or_72 (or_72_out, and_136_out, or_73_out);
  or or_73 (or_73_out, and_137_out, or_74_out);
  or or_74 (or_74_out, and_138_out, or_75_out);
  or or_75 (or_75_out, and_139_out, or_76_out);
  or or_76 (or_76_out, and_140_out, or_77_out);
  or or_77 (or_77_out, and_141_out, or_78_out);
  or or_78 (or_78_out, and_142_out, or_79_out);
  or or_79 (or_79_out, and_143_out, or_80_out);
  or or_80 (or_80_out, and_144_out, or_81_out);
  or or_81 (or_81_out, and_145_out, or_82_out);
  or or_82 (or_82_out, and_146_out, or_83_out);
  or or_83 (or_83_out, and_147_out, or_84_out);
  or or_84 (or_84_out, and_148_out, or_85_out);
  or or_85 (or_85_out, and_149_out, or_86_out);
  or or_86 (or_86_out, and_150_out, or_87_out);
  or or_87 (or_87_out, and_151_out, or_88_out);
  or or_88 (or_88_out, and_152_out, or_89_out);
  or or_89 (or_89_out, and_153_out, or_90_out);
  or or_90 (or_90_out, and_154_out, or_91_out);
  or or_91 (or_91_out, and_155_out, or_92_out);
  or or_92 (or_92_out, and_156_out, or_93_out);
  or or_93 (or_93_out, and_157_out, or_94_out);
  or or_94 (or_94_out, and_158_out, or_95_out);
  or or_95 (or_95_out, and_159_out, or_96_out);
  or or_96 (or_96_out, and_160_out, or_97_out);
  or or_97 (or_97_out, and_161_out, or_98_out);
  or or_98 (or_98_out, and_162_out, or_99_out);
  or or_99 (or_99_out, and_163_out, or_100_out);
  or or_100 (or_100_out, and_164_out, or_101_out);
  or or_101 (or_101_out, and_165_out, or_102_out);
  or or_102 (or_102_out, and_166_out, or_103_out);
  or or_103 (or_103_out, and_167_out, or_104_out);
  or or_104 (or_104_out, and_168_out, or_105_out);
  or or_105 (or_105_out, and_169_out, or_106_out);
  or or_106 (or_106_out, and_170_out, or_107_out);
  or or_107 (or_107_out, and_171_out, or_108_out);
  or or_108 (or_108_out, and_172_out, or_109_out);
  or or_109 (or_109_out, and_173_out, or_110_out);
  or or_110 (or_110_out, and_174_out, or_111_out);
  or or_111 (or_111_out, and_175_out, or_112_out);
  or or_112 (or_112_out, and_176_out, or_113_out);
  or or_113 (or_113_out, and_177_out, or_114_out);
  or or_114 (or_114_out, and_178_out, or_115_out);
  or or_115 (or_115_out, and_179_out, or_116_out);
  or or_116 (or_116_out, and_180_out, or_117_out);
  or or_117 (or_117_out, and_181_out, or_118_out);
  or or_118 (or_118_out, and_182_out, or_119_out);
  or or_119 (or_119_out, and_183_out, or_120_out);
  or or_120 (or_120_out, and_184_out, or_121_out);
  or or_121 (or_121_out, and_185_out, or_122_out);
  or or_122 (or_122_out, and_186_out, or_123_out);
  or or_123 (or_123_out, and_187_out, or_124_out);
  or or_124 (or_124_out, and_188_out, or_125_out);
  or or_125 (or_125_out, and_189_out, or_126_out);
  or or_126 (or_126_out, and_190_out, and_191_out);

  // Notes on the sheet:
  //   input1: initial=0xbdfffff2ffffff15
  //   input2: initial=0xbdfffff2ffffff16
endmodule

module cbuffer256bit (
  input  buffer1,
  input  [63:0] input1a,
  input  [63:0] input1b,
  input  [63:0] input1c,
  input  [63:0] input1d,
  output [63:0] output1a,
  output [63:0] output1b,
  output [63:0] output1c,
  output [63:0] output1d
);

  assign output1a = {64{buffer1}} & input1a;  // AND_Gate and_1, 64 bits wide
  assign output1b = {64{buffer1}} & input1b;  // AND_Gate and_2, 64 bits wide
  assign output1c = {64{buffer1}} & input1c;  // AND_Gate and_3, 64 bits wide
  assign output1d = {64{buffer1}} & input1d;  // AND_Gate and_4, 64 bits wide
endmodule

module subtractor256bit (
  input  inborrow,
  input  [63:0] input1a,
  input  [63:0] input1b,
  input  [63:0] input1c,
  input  [63:0] input1d,
  input  [63:0] input2a,
  input  [63:0] input2b,
  input  [63:0] input2c,
  input  [63:0] input2d,
  output borrow,
  output [63:0] output1a,
  output [63:0] output1b,
  output [63:0] output1c,
  output [63:0] output1d
);

  wire subtractor128bit_1_borrow;

  subtractor128bit subtractor128bit_1 (
    .inborrow(inborrow), .input1a(input1a), .input1b(input1b), .input2a(input2a), .input2b(input2b),
    .borrow(subtractor128bit_1_borrow), .output1a(output1a), .output1b(output1b));
  subtractor128bit subtractor128bit_2 (
    .inborrow(subtractor128bit_1_borrow), .input1a(input1c), .input1b(input1d), .input2a(input2c),
    .input2b(input2d), .borrow(borrow), .output1a(output1c), .output1b(output1d));
endmodule

module negate256bit (
  input  [63:0] input1a,
  input  [63:0] input1b,
  input  [63:0] input1c,
  input  [63:0] input1d,
  output [63:0] output1a,
  output [63:0] output1b,
  output [63:0] output1c,
  output [63:0] output1d
);

  wire [63:0] not_1_out, not_2_out, not_3_out, not_4_out;

  assign not_1_out = ~input1a;  // NOT_Gate not_1, 64 bits wide
  assign not_2_out = ~input1b;  // NOT_Gate not_2, 64 bits wide
  assign not_3_out = ~input1c;  // NOT_Gate not_3, 64 bits wide
  assign not_4_out = ~input1d;  // NOT_Gate not_4, 64 bits wide
  adder256bit adder256bit_1 (
    .input1a(64'h1), .input2a(not_1_out), .input2b(not_2_out), .input2c(not_3_out), .input2d(not_4_out),
    .output1a(output1a), .output1b(output1b), .output1c(output1c), .output1d(output1d));  // open: inflow, input1b, input1c, input1d, overflow
endmodule

module adder256bit (
  input  inflow,
  input  [63:0] input1a,
  input  [63:0] input1b,
  input  [63:0] input1c,
  input  [63:0] input1d,
  input  [63:0] input2a,
  input  [63:0] input2b,
  input  [63:0] input2c,
  input  [63:0] input2d,
  output overflow,
  output [63:0] output1a,
  output [63:0] output1b,
  output [63:0] output1c,
  output [63:0] output1d
);

  wire adder128bit_1_overflow;

  adder128bit adder128bit_1 (
    .inflow(inflow), .input1a(input1a), .input1b(input1b), .input2a(input2a), .input2b(input2b),
    .overflow(adder128bit_1_overflow), .output1a(output1a), .output1b(output1b));
  adder128bit adder128bit_2 (
    .inflow(adder128bit_1_overflow), .input1a(input1c), .input1b(input1d), .input2a(input2c),
    .input2b(input2d), .overflow(overflow), .output1a(output1c), .output1b(output1d));
endmodule

module shiftleft64bit (
  input  [63:0] input1,
  input  [7:0] shiftleft1,
  output [63:0] output1
);

  wire [63:8] undriven;

  mux6x64bit mux6x64bit_1 (
    .select1({undriven, shiftleft1}), .input0(input1), .input1({input1[62:0], 1'b0}),
    .input2({input1[61:0], 2'b00}), .input3({input1[60:0], 3'b000}), .input4({input1[59:0], 4'b0000}),
    .input5({input1[58:0], {5{1'b0}}}), .input6({input1[57:0], {6{1'b0}}}),
    .input7({input1[56:0], {7{1'b0}}}), .input8({input1[55:0], {8{1'b0}}}),
    .input9({input1[54:0], {9{1'b0}}}), .input10({input1[53:0], {10{1'b0}}}),
    .input11({input1[52:0], {11{1'b0}}}), .input12({input1[51:0], {12{1'b0}}}),
    .input13({input1[50:0], {13{1'b0}}}), .input14({input1[49:0], {14{1'b0}}}),
    .input15({input1[48:0], {15{1'b0}}}), .input16({input1[47:0], {16{1'b0}}}),
    .input17({input1[46:0], {17{1'b0}}}), .input18({input1[45:0], {18{1'b0}}}),
    .input19({input1[44:0], {19{1'b0}}}), .input20({input1[43:0], {20{1'b0}}}),
    .input21({input1[42:0], {21{1'b0}}}), .input22({input1[41:0], {22{1'b0}}}),
    .input23({input1[40:0], {23{1'b0}}}), .input24({input1[39:0], {24{1'b0}}}),
    .input25({input1[38:0], {25{1'b0}}}), .input26({input1[37:0], {26{1'b0}}}),
    .input27({input1[36:0], {27{1'b0}}}), .input28({input1[35:0], {28{1'b0}}}),
    .input29({input1[34:0], {29{1'b0}}}), .input30({input1[33:0], {30{1'b0}}}),
    .input31({input1[32:0], {31{1'b0}}}), .input32({input1[31:0], {32{1'b0}}}),
    .input33({input1[30:0], {33{1'b0}}}), .input34({input1[29:0], {34{1'b0}}}),
    .input35({input1[28:0], {35{1'b0}}}), .input36({input1[27:0], {36{1'b0}}}),
    .input37({input1[26:0], {37{1'b0}}}), .input38({input1[25:0], {38{1'b0}}}),
    .input39({input1[24:0], {39{1'b0}}}), .input40({input1[23:0], {40{1'b0}}}),
    .input41({input1[22:0], {41{1'b0}}}), .input42({input1[21:0], {42{1'b0}}}),
    .input43({input1[20:0], {43{1'b0}}}), .input44({input1[19:0], {44{1'b0}}}),
    .input45({input1[18:0], {45{1'b0}}}), .input46({input1[17:0], {46{1'b0}}}),
    .input47({input1[16:0], {47{1'b0}}}), .input48({input1[15:0], {48{1'b0}}}),
    .input49({input1[14:0], {49{1'b0}}}), .input50({input1[13:0], {50{1'b0}}}),
    .input51({input1[12:0], {51{1'b0}}}), .input52({input1[11:0], {52{1'b0}}}),
    .input53({input1[10:0], {53{1'b0}}}), .input54({input1[9:0], {54{1'b0}}}),
    .input55({input1[8:0], {55{1'b0}}}), .input56({input1[7:0], {56{1'b0}}}),
    .input57({input1[6:0], {57{1'b0}}}), .input58({input1[5:0], {58{1'b0}}}),
    .input59({input1[4:0], {59{1'b0}}}), .input60({input1[3:0], {60{1'b0}}}),
    .input61({input1[2:0], {61{1'b0}}}), .input62({input1[1:0], {62{1'b0}}}),
    .input63({input1[0], {63{1'b0}}}), .output1(output1));
  // Pins of 8 and 64 bits meet at {undriven, shiftleft1}

  // Notes on the sheet:
  //   shiftleft1: initial=0x30
  //   input1: initial=0xcafebabecafebabe
endmodule

module mux6x64bit (
  input  [63:0] select1,
  input  [63:0] input0,
  input  [63:0] input1,
  input  [63:0] input2,
  input  [63:0] input3,
  input  [63:0] input4,
  input  [63:0] input5,
  input  [63:0] input6,
  input  [63:0] input7,
  input  [63:0] input8,
  input  [63:0] input9,
  input  [63:0] input10,
  input  [63:0] input11,
  input  [63:0] input12,
  input  [63:0] input13,
  input  [63:0] input14,
  input  [63:0] input15,
  input  [63:0] input16,
  input  [63:0] input17,
  input  [63:0] input18,
  input  [63:0] input19,
  input  [63:0] input20,
  input  [63:0] input21,
  input  [63:0] input22,
  input  [63:0] input23,
  input  [63:0] input24,
  input  [63:0] input25,
  input  [63:0] input26,
  input  [63:0] input27,
  input  [63:0] input28,
  input  [63:0] input29,
  input  [63:0] input30,
  input  [63:0] input31,
  input  [63:0] input32,
  input  [63:0] input33,
  input  [63:0] input34,
  input  [63:0] input35,
  input  [63:0] input36,
  input  [63:0] input37,
  input  [63:0] input38,
  input  [63:0] input39,
  input  [63:0] input40,
  input  [63:0] input41,
  input  [63:0] input42,
  input  [63:0] input43,
  input  [63:0] input44,
  input  [63:0] input45,
  input  [63:0] input46,
  input  [63:0] input47,
  input  [63:0] input48,
  input  [63:0] input49,
  input  [63:0] input50,
  input  [63:0] input51,
  input  [63:0] input52,
  input  [63:0] input53,
  input  [63:0] input54,
  input  [63:0] input55,
  input  [63:0] input56,
  input  [63:0] input57,
  input  [63:0] input58,
  input  [63:0] input59,
  input  [63:0] input60,
  input  [63:0] input61,
  input  [63:0] input62,
  input  [63:0] input63,
  output [63:0] output1
);

  wire comparatoru64bit_1_equal1, comparatoru64bit_2_equal1, comparatoru64bit_3_equal1,
       comparatoru64bit_4_equal1, comparatoru64bit_5_equal1, comparatoru64bit_6_equal1,
       comparatoru64bit_7_equal1, comparatoru64bit_8_equal1, comparatoru64bit_9_equal1,
       comparatoru64bit_10_equal1, comparatoru64bit_11_equal1, comparatoru64bit_12_equal1,
       comparatoru64bit_13_equal1, comparatoru64bit_14_equal1, comparatoru64bit_15_equal1,
       comparatoru64bit_16_equal1, comparatoru64bit_17_equal1, comparatoru64bit_18_equal1,
       comparatoru64bit_19_equal1, comparatoru64bit_20_equal1, comparatoru64bit_21_equal1,
       comparatoru64bit_22_equal1, comparatoru64bit_23_equal1, comparatoru64bit_24_equal1,
       comparatoru64bit_25_equal1, comparatoru64bit_26_equal1, comparatoru64bit_27_equal1,
       comparatoru64bit_28_equal1, comparatoru64bit_29_equal1, comparatoru64bit_30_equal1,
       comparatoru64bit_31_equal1, comparatoru64bit_32_equal1, comparatoru64bit_33_equal1,
       comparatoru64bit_34_equal1, comparatoru64bit_35_equal1, comparatoru64bit_36_equal1,
       comparatoru64bit_37_equal1, comparatoru64bit_38_equal1, comparatoru64bit_39_equal1,
       comparatoru64bit_40_equal1, comparatoru64bit_41_equal1, comparatoru64bit_42_equal1,
       comparatoru64bit_43_equal1, comparatoru64bit_44_equal1, comparatoru64bit_45_equal1,
       comparatoru64bit_46_equal1, comparatoru64bit_47_equal1, comparatoru64bit_48_equal1,
       comparatoru64bit_49_equal1, comparatoru64bit_50_equal1, comparatoru64bit_51_equal1,
       comparatoru64bit_52_equal1, comparatoru64bit_53_equal1, comparatoru64bit_54_equal1,
       comparatoru64bit_55_equal1, comparatoru64bit_56_equal1, comparatoru64bit_57_equal1,
       comparatoru64bit_58_equal1, comparatoru64bit_59_equal1, comparatoru64bit_60_equal1,
       comparatoru64bit_61_equal1, comparatoru64bit_62_equal1, comparatoru64bit_63_equal1,
       comparatoru64bit_64_equal1;
  wire [63:0] cbuffer64bit_1_output1, cbuffer64bit_2_output1, cbuffer64bit_3_output1, cbuffer64bit_4_output1,
       cbuffer64bit_5_output1, cbuffer64bit_6_output1, cbuffer64bit_7_output1, cbuffer64bit_8_output1,
       cbuffer64bit_9_output1, cbuffer64bit_10_output1, cbuffer64bit_11_output1, cbuffer64bit_12_output1,
       cbuffer64bit_13_output1, cbuffer64bit_14_output1, cbuffer64bit_15_output1, cbuffer64bit_16_output1,
       cbuffer64bit_17_output1, cbuffer64bit_18_output1, cbuffer64bit_19_output1, cbuffer64bit_20_output1,
       cbuffer64bit_21_output1, cbuffer64bit_22_output1, cbuffer64bit_23_output1, cbuffer64bit_24_output1,
       cbuffer64bit_25_output1, cbuffer64bit_26_output1, cbuffer64bit_27_output1, cbuffer64bit_28_output1,
       cbuffer64bit_29_output1, cbuffer64bit_30_output1, cbuffer64bit_31_output1, cbuffer64bit_32_output1,
       cbuffer64bit_33_output1, cbuffer64bit_34_output1, cbuffer64bit_35_output1, cbuffer64bit_36_output1,
       cbuffer64bit_37_output1, cbuffer64bit_38_output1, cbuffer64bit_39_output1, cbuffer64bit_40_output1,
       cbuffer64bit_41_output1, cbuffer64bit_42_output1, cbuffer64bit_43_output1, cbuffer64bit_44_output1,
       cbuffer64bit_45_output1, cbuffer64bit_46_output1, cbuffer64bit_47_output1, cbuffer64bit_48_output1,
       cbuffer64bit_49_output1, cbuffer64bit_50_output1, cbuffer64bit_51_output1, cbuffer64bit_52_output1,
       cbuffer64bit_53_output1, cbuffer64bit_54_output1, cbuffer64bit_55_output1, cbuffer64bit_56_output1,
       cbuffer64bit_57_output1, cbuffer64bit_58_output1, cbuffer64bit_59_output1, cbuffer64bit_60_output1,
       cbuffer64bit_61_output1, cbuffer64bit_62_output1, cbuffer64bit_63_output1, cbuffer64bit_64_output1;

  comparatoru64bit comparatoru64bit_1 (
    .input1(select1), .input2({64{1'b0}}), .equal1(comparatoru64bit_1_equal1));  // open: greater1, less1
  comparatoru64bit comparatoru64bit_2 (
    .input1(select1), .input2(64'h1), .equal1(comparatoru64bit_2_equal1));  // open: greater1, less1
  comparatoru64bit comparatoru64bit_3 (
    .input1(select1), .input2(64'h2), .equal1(comparatoru64bit_3_equal1));  // open: greater1, less1
  comparatoru64bit comparatoru64bit_4 (
    .input1(select1), .input2(64'h3), .equal1(comparatoru64bit_4_equal1));  // open: greater1, less1
  comparatoru64bit comparatoru64bit_5 (
    .input1(select1), .input2(64'h4), .equal1(comparatoru64bit_5_equal1));  // open: greater1, less1
  comparatoru64bit comparatoru64bit_6 (
    .input1(select1), .input2(64'h5), .equal1(comparatoru64bit_6_equal1));  // open: greater1, less1
  comparatoru64bit comparatoru64bit_7 (
    .input1(select1), .input2(64'h6), .equal1(comparatoru64bit_7_equal1));  // open: greater1, less1
  comparatoru64bit comparatoru64bit_8 (
    .input1(select1), .input2(64'h7), .equal1(comparatoru64bit_8_equal1));  // open: greater1, less1
  comparatoru64bit comparatoru64bit_9 (
    .input1(select1), .input2(64'h8), .equal1(comparatoru64bit_9_equal1));  // open: greater1, less1
  comparatoru64bit comparatoru64bit_10 (
    .input1(select1), .input2(64'h9), .equal1(comparatoru64bit_10_equal1));  // open: greater1, less1
  comparatoru64bit comparatoru64bit_11 (
    .input1(select1), .input2(64'ha), .equal1(comparatoru64bit_11_equal1));  // open: greater1, less1
  comparatoru64bit comparatoru64bit_12 (
    .input1(select1), .input2(64'hb), .equal1(comparatoru64bit_12_equal1));  // open: greater1, less1
  comparatoru64bit comparatoru64bit_13 (
    .input1(select1), .input2(64'hc), .equal1(comparatoru64bit_13_equal1));  // open: greater1, less1
  comparatoru64bit comparatoru64bit_14 (
    .input1(select1), .input2(64'hd), .equal1(comparatoru64bit_14_equal1));  // open: greater1, less1
  comparatoru64bit comparatoru64bit_15 (
    .input1(select1), .input2(64'he), .equal1(comparatoru64bit_15_equal1));  // open: greater1, less1
  comparatoru64bit comparatoru64bit_16 (
    .input1(select1), .input2(64'hf), .equal1(comparatoru64bit_16_equal1));  // open: greater1, less1
  comparatoru64bit comparatoru64bit_17 (
    .input1(select1), .input2(64'h10), .equal1(comparatoru64bit_17_equal1));  // open: greater1, less1
  comparatoru64bit comparatoru64bit_18 (
    .input1(select1), .input2(64'h11), .equal1(comparatoru64bit_18_equal1));  // open: greater1, less1
  comparatoru64bit comparatoru64bit_19 (
    .input1(select1), .input2(64'h12), .equal1(comparatoru64bit_19_equal1));  // open: greater1, less1
  comparatoru64bit comparatoru64bit_20 (
    .input1(select1), .input2(64'h13), .equal1(comparatoru64bit_20_equal1));  // open: greater1, less1
  comparatoru64bit comparatoru64bit_21 (
    .input1(select1), .input2(64'h14), .equal1(comparatoru64bit_21_equal1));  // open: greater1, less1
  comparatoru64bit comparatoru64bit_22 (
    .input1(select1), .input2(64'h15), .equal1(comparatoru64bit_22_equal1));  // open: greater1, less1
  comparatoru64bit comparatoru64bit_23 (
    .input1(select1), .input2(64'h16), .equal1(comparatoru64bit_23_equal1));  // open: greater1, less1
  comparatoru64bit comparatoru64bit_24 (
    .input1(select1), .input2(64'h17), .equal1(comparatoru64bit_24_equal1));  // open: greater1, less1
  comparatoru64bit comparatoru64bit_25 (
    .input1(select1), .input2(64'h18), .equal1(comparatoru64bit_25_equal1));  // open: greater1, less1
  comparatoru64bit comparatoru64bit_26 (
    .input1(select1), .input2(64'h19), .equal1(comparatoru64bit_26_equal1));  // open: greater1, less1
  comparatoru64bit comparatoru64bit_27 (
    .input1(select1), .input2(64'h1a), .equal1(comparatoru64bit_27_equal1));  // open: greater1, less1
  comparatoru64bit comparatoru64bit_28 (
    .input1(select1), .input2(64'h1b), .equal1(comparatoru64bit_28_equal1));  // open: greater1, less1
  comparatoru64bit comparatoru64bit_29 (
    .input1(select1), .input2(64'h1c), .equal1(comparatoru64bit_29_equal1));  // open: greater1, less1
  comparatoru64bit comparatoru64bit_30 (
    .input1(select1), .input2(64'h1d), .equal1(comparatoru64bit_30_equal1));  // open: greater1, less1
  comparatoru64bit comparatoru64bit_31 (
    .input1(select1), .input2(64'h1e), .equal1(comparatoru64bit_31_equal1));  // open: greater1, less1
  comparatoru64bit comparatoru64bit_32 (
    .input1(select1), .input2(64'h1f), .equal1(comparatoru64bit_32_equal1));  // open: greater1, less1
  comparatoru64bit comparatoru64bit_33 (
    .input1(select1), .input2(64'h20), .equal1(comparatoru64bit_33_equal1));  // open: greater1, less1
  comparatoru64bit comparatoru64bit_34 (
    .input1(select1), .input2(64'h21), .equal1(comparatoru64bit_34_equal1));  // open: greater1, less1
  comparatoru64bit comparatoru64bit_35 (
    .input1(select1), .input2(64'h22), .equal1(comparatoru64bit_35_equal1));  // open: greater1, less1
  comparatoru64bit comparatoru64bit_36 (
    .input1(select1), .input2(64'h23), .equal1(comparatoru64bit_36_equal1));  // open: greater1, less1
  comparatoru64bit comparatoru64bit_37 (
    .input1(select1), .input2(64'h24), .equal1(comparatoru64bit_37_equal1));  // open: greater1, less1
  comparatoru64bit comparatoru64bit_38 (
    .input1(select1), .input2(64'h25), .equal1(comparatoru64bit_38_equal1));  // open: greater1, less1
  comparatoru64bit comparatoru64bit_39 (
    .input1(select1), .input2(64'h26), .equal1(comparatoru64bit_39_equal1));  // open: greater1, less1
  comparatoru64bit comparatoru64bit_40 (
    .input1(select1), .input2(64'h27), .equal1(comparatoru64bit_40_equal1));  // open: greater1, less1
  comparatoru64bit comparatoru64bit_41 (
    .input1(select1), .input2(64'h28), .equal1(comparatoru64bit_41_equal1));  // open: greater1, less1
  comparatoru64bit comparatoru64bit_42 (
    .input1(select1), .input2(64'h29), .equal1(comparatoru64bit_42_equal1));  // open: greater1, less1
  comparatoru64bit comparatoru64bit_43 (
    .input1(select1), .input2(64'h2a), .equal1(comparatoru64bit_43_equal1));  // open: greater1, less1
  comparatoru64bit comparatoru64bit_44 (
    .input1(select1), .input2(64'h2b), .equal1(comparatoru64bit_44_equal1));  // open: greater1, less1
  comparatoru64bit comparatoru64bit_45 (
    .input1(select1), .input2(64'h2c), .equal1(comparatoru64bit_45_equal1));  // open: greater1, less1
  comparatoru64bit comparatoru64bit_46 (
    .input1(select1), .input2(64'h2d), .equal1(comparatoru64bit_46_equal1));  // open: greater1, less1
  comparatoru64bit comparatoru64bit_47 (
    .input1(select1), .input2(64'h2e), .equal1(comparatoru64bit_47_equal1));  // open: greater1, less1
  comparatoru64bit comparatoru64bit_48 (
    .input1(select1), .input2(64'h2f), .equal1(comparatoru64bit_48_equal1));  // open: greater1, less1
  comparatoru64bit comparatoru64bit_49 (
    .input1(select1), .input2(64'h30), .equal1(comparatoru64bit_49_equal1));  // open: greater1, less1
  comparatoru64bit comparatoru64bit_50 (
    .input1(select1), .input2(64'h31), .equal1(comparatoru64bit_50_equal1));  // open: greater1, less1
  comparatoru64bit comparatoru64bit_51 (
    .input1(select1), .input2(64'h32), .equal1(comparatoru64bit_51_equal1));  // open: greater1, less1
  comparatoru64bit comparatoru64bit_52 (
    .input1(select1), .input2(64'h33), .equal1(comparatoru64bit_52_equal1));  // open: greater1, less1
  comparatoru64bit comparatoru64bit_53 (
    .input1(select1), .input2(64'h34), .equal1(comparatoru64bit_53_equal1));  // open: greater1, less1
  comparatoru64bit comparatoru64bit_54 (
    .input1(select1), .input2(64'h35), .equal1(comparatoru64bit_54_equal1));  // open: greater1, less1
  comparatoru64bit comparatoru64bit_55 (
    .input1(select1), .input2(64'h36), .equal1(comparatoru64bit_55_equal1));  // open: greater1, less1
  comparatoru64bit comparatoru64bit_56 (
    .input1(select1), .input2(64'h37), .equal1(comparatoru64bit_56_equal1));  // open: greater1, less1
  comparatoru64bit comparatoru64bit_57 (
    .input1(select1), .input2(64'h38), .equal1(comparatoru64bit_57_equal1));  // open: greater1, less1
  comparatoru64bit comparatoru64bit_58 (
    .input1(select1), .input2(64'h39), .equal1(comparatoru64bit_58_equal1));  // open: greater1, less1
  comparatoru64bit comparatoru64bit_59 (
    .input1(select1), .input2(64'h3a), .equal1(comparatoru64bit_59_equal1));  // open: greater1, less1
  comparatoru64bit comparatoru64bit_60 (
    .input1(select1), .input2(64'h3b), .equal1(comparatoru64bit_60_equal1));  // open: greater1, less1
  comparatoru64bit comparatoru64bit_61 (
    .input1(select1), .input2(64'h3c), .equal1(comparatoru64bit_61_equal1));  // open: greater1, less1
  comparatoru64bit comparatoru64bit_62 (
    .input1(select1), .input2(64'h3d), .equal1(comparatoru64bit_62_equal1));  // open: greater1, less1
  comparatoru64bit comparatoru64bit_63 (
    .input1(select1), .input2(64'h3e), .equal1(comparatoru64bit_63_equal1));  // open: greater1, less1
  comparatoru64bit comparatoru64bit_64 (
    .input1(select1), .input2(64'h3f), .equal1(comparatoru64bit_64_equal1));  // open: greater1, less1
  cbuffer64bit cbuffer64bit_1 (.buffer1(comparatoru64bit_1_equal1), .input1(input0), .output1(cbuffer64bit_1_output1));
  cbuffer64bit cbuffer64bit_2 (.buffer1(comparatoru64bit_2_equal1), .input1(input1), .output1(cbuffer64bit_2_output1));
  cbuffer64bit cbuffer64bit_3 (.buffer1(comparatoru64bit_3_equal1), .input1(input2), .output1(cbuffer64bit_3_output1));
  cbuffer64bit cbuffer64bit_4 (.buffer1(comparatoru64bit_4_equal1), .input1(input3), .output1(cbuffer64bit_4_output1));
  cbuffer64bit cbuffer64bit_5 (.buffer1(comparatoru64bit_5_equal1), .input1(input4), .output1(cbuffer64bit_5_output1));
  cbuffer64bit cbuffer64bit_6 (.buffer1(comparatoru64bit_6_equal1), .input1(input5), .output1(cbuffer64bit_6_output1));
  cbuffer64bit cbuffer64bit_7 (.buffer1(comparatoru64bit_7_equal1), .input1(input6), .output1(cbuffer64bit_7_output1));
  cbuffer64bit cbuffer64bit_8 (.buffer1(comparatoru64bit_8_equal1), .input1(input7), .output1(cbuffer64bit_8_output1));
  cbuffer64bit cbuffer64bit_9 (.buffer1(comparatoru64bit_9_equal1), .input1(input8), .output1(cbuffer64bit_9_output1));
  cbuffer64bit cbuffer64bit_10 (
    .buffer1(comparatoru64bit_10_equal1), .input1(input9), .output1(cbuffer64bit_10_output1));
  cbuffer64bit cbuffer64bit_11 (
    .buffer1(comparatoru64bit_11_equal1), .input1(input10), .output1(cbuffer64bit_11_output1));
  cbuffer64bit cbuffer64bit_12 (
    .buffer1(comparatoru64bit_12_equal1), .input1(input11), .output1(cbuffer64bit_12_output1));
  cbuffer64bit cbuffer64bit_13 (
    .buffer1(comparatoru64bit_13_equal1), .input1(input12), .output1(cbuffer64bit_13_output1));
  cbuffer64bit cbuffer64bit_14 (
    .buffer1(comparatoru64bit_14_equal1), .input1(input13), .output1(cbuffer64bit_14_output1));
  cbuffer64bit cbuffer64bit_15 (
    .buffer1(comparatoru64bit_15_equal1), .input1(input14), .output1(cbuffer64bit_15_output1));
  cbuffer64bit cbuffer64bit_16 (
    .buffer1(comparatoru64bit_16_equal1), .input1(input15), .output1(cbuffer64bit_16_output1));
  cbuffer64bit cbuffer64bit_17 (
    .buffer1(comparatoru64bit_17_equal1), .input1(input16), .output1(cbuffer64bit_17_output1));
  cbuffer64bit cbuffer64bit_18 (
    .buffer1(comparatoru64bit_18_equal1), .input1(input17), .output1(cbuffer64bit_18_output1));
  cbuffer64bit cbuffer64bit_19 (
    .buffer1(comparatoru64bit_19_equal1), .input1(input18), .output1(cbuffer64bit_19_output1));
  cbuffer64bit cbuffer64bit_20 (
    .buffer1(comparatoru64bit_20_equal1), .input1(input19), .output1(cbuffer64bit_20_output1));
  cbuffer64bit cbuffer64bit_21 (
    .buffer1(comparatoru64bit_21_equal1), .input1(input20), .output1(cbuffer64bit_21_output1));
  cbuffer64bit cbuffer64bit_22 (
    .buffer1(comparatoru64bit_22_equal1), .input1(input21), .output1(cbuffer64bit_22_output1));
  cbuffer64bit cbuffer64bit_23 (
    .buffer1(comparatoru64bit_23_equal1), .input1(input22), .output1(cbuffer64bit_23_output1));
  cbuffer64bit cbuffer64bit_24 (
    .buffer1(comparatoru64bit_24_equal1), .input1(input23), .output1(cbuffer64bit_24_output1));
  cbuffer64bit cbuffer64bit_25 (
    .buffer1(comparatoru64bit_25_equal1), .input1(input24), .output1(cbuffer64bit_25_output1));
  cbuffer64bit cbuffer64bit_26 (
    .buffer1(comparatoru64bit_26_equal1), .input1(input25), .output1(cbuffer64bit_26_output1));
  cbuffer64bit cbuffer64bit_27 (
    .buffer1(comparatoru64bit_27_equal1), .input1(input26), .output1(cbuffer64bit_27_output1));
  cbuffer64bit cbuffer64bit_28 (
    .buffer1(comparatoru64bit_28_equal1), .input1(input27), .output1(cbuffer64bit_28_output1));
  cbuffer64bit cbuffer64bit_29 (
    .buffer1(comparatoru64bit_29_equal1), .input1(input28), .output1(cbuffer64bit_29_output1));
  cbuffer64bit cbuffer64bit_30 (
    .buffer1(comparatoru64bit_30_equal1), .input1(input29), .output1(cbuffer64bit_30_output1));
  cbuffer64bit cbuffer64bit_31 (
    .buffer1(comparatoru64bit_31_equal1), .input1(input30), .output1(cbuffer64bit_31_output1));
  cbuffer64bit cbuffer64bit_32 (
    .buffer1(comparatoru64bit_32_equal1), .input1(input31), .output1(cbuffer64bit_32_output1));
  cbuffer64bit cbuffer64bit_33 (
    .buffer1(comparatoru64bit_33_equal1), .input1(input32), .output1(cbuffer64bit_33_output1));
  cbuffer64bit cbuffer64bit_34 (
    .buffer1(comparatoru64bit_34_equal1), .input1(input33), .output1(cbuffer64bit_34_output1));
  cbuffer64bit cbuffer64bit_35 (
    .buffer1(comparatoru64bit_35_equal1), .input1(input34), .output1(cbuffer64bit_35_output1));
  cbuffer64bit cbuffer64bit_36 (
    .buffer1(comparatoru64bit_36_equal1), .input1(input35), .output1(cbuffer64bit_36_output1));
  cbuffer64bit cbuffer64bit_37 (
    .buffer1(comparatoru64bit_37_equal1), .input1(input36), .output1(cbuffer64bit_37_output1));
  cbuffer64bit cbuffer64bit_38 (
    .buffer1(comparatoru64bit_38_equal1), .input1(input37), .output1(cbuffer64bit_38_output1));
  cbuffer64bit cbuffer64bit_39 (
    .buffer1(comparatoru64bit_39_equal1), .input1(input38), .output1(cbuffer64bit_39_output1));
  cbuffer64bit cbuffer64bit_40 (
    .buffer1(comparatoru64bit_40_equal1), .input1(input39), .output1(cbuffer64bit_40_output1));
  cbuffer64bit cbuffer64bit_41 (
    .buffer1(comparatoru64bit_41_equal1), .input1(input40), .output1(cbuffer64bit_41_output1));
  cbuffer64bit cbuffer64bit_42 (
    .buffer1(comparatoru64bit_42_equal1), .input1(input41), .output1(cbuffer64bit_42_output1));
  cbuffer64bit cbuffer64bit_43 (
    .buffer1(comparatoru64bit_43_equal1), .input1(input42), .output1(cbuffer64bit_43_output1));
  cbuffer64bit cbuffer64bit_44 (
    .buffer1(comparatoru64bit_44_equal1), .input1(input43), .output1(cbuffer64bit_44_output1));
  cbuffer64bit cbuffer64bit_45 (
    .buffer1(comparatoru64bit_45_equal1), .input1(input44), .output1(cbuffer64bit_45_output1));
  cbuffer64bit cbuffer64bit_46 (
    .buffer1(comparatoru64bit_46_equal1), .input1(input45), .output1(cbuffer64bit_46_output1));
  cbuffer64bit cbuffer64bit_47 (
    .buffer1(comparatoru64bit_47_equal1), .input1(input46), .output1(cbuffer64bit_47_output1));
  cbuffer64bit cbuffer64bit_48 (
    .buffer1(comparatoru64bit_48_equal1), .input1(input47), .output1(cbuffer64bit_48_output1));
  cbuffer64bit cbuffer64bit_49 (
    .buffer1(comparatoru64bit_49_equal1), .input1(input48), .output1(cbuffer64bit_49_output1));
  cbuffer64bit cbuffer64bit_50 (
    .buffer1(comparatoru64bit_50_equal1), .input1(input49), .output1(cbuffer64bit_50_output1));
  cbuffer64bit cbuffer64bit_51 (
    .buffer1(comparatoru64bit_51_equal1), .input1(input50), .output1(cbuffer64bit_51_output1));
  cbuffer64bit cbuffer64bit_52 (
    .buffer1(comparatoru64bit_52_equal1), .input1(input51), .output1(cbuffer64bit_52_output1));
  cbuffer64bit cbuffer64bit_53 (
    .buffer1(comparatoru64bit_53_equal1), .input1(input52), .output1(cbuffer64bit_53_output1));
  cbuffer64bit cbuffer64bit_54 (
    .buffer1(comparatoru64bit_54_equal1), .input1(input53), .output1(cbuffer64bit_54_output1));
  cbuffer64bit cbuffer64bit_55 (
    .buffer1(comparatoru64bit_55_equal1), .input1(input54), .output1(cbuffer64bit_55_output1));
  cbuffer64bit cbuffer64bit_56 (
    .buffer1(comparatoru64bit_56_equal1), .input1(input55), .output1(cbuffer64bit_56_output1));
  cbuffer64bit cbuffer64bit_57 (
    .buffer1(comparatoru64bit_57_equal1), .input1(input56), .output1(cbuffer64bit_57_output1));
  cbuffer64bit cbuffer64bit_58 (
    .buffer1(comparatoru64bit_58_equal1), .input1(input57), .output1(cbuffer64bit_58_output1));
  cbuffer64bit cbuffer64bit_59 (
    .buffer1(comparatoru64bit_59_equal1), .input1(input58), .output1(cbuffer64bit_59_output1));
  cbuffer64bit cbuffer64bit_60 (
    .buffer1(comparatoru64bit_60_equal1), .input1(input59), .output1(cbuffer64bit_60_output1));
  cbuffer64bit cbuffer64bit_61 (
    .buffer1(comparatoru64bit_61_equal1), .input1(input60), .output1(cbuffer64bit_61_output1));
  cbuffer64bit cbuffer64bit_62 (
    .buffer1(comparatoru64bit_62_equal1), .input1(input61), .output1(cbuffer64bit_62_output1));
  cbuffer64bit cbuffer64bit_63 (
    .buffer1(comparatoru64bit_63_equal1), .input1(input62), .output1(cbuffer64bit_63_output1));
  cbuffer64bit cbuffer64bit_64 (
    .buffer1(comparatoru64bit_64_equal1), .input1(input63), .output1(cbuffer64bit_64_output1));
  assign output1 = cbuffer64bit_1_output1 | cbuffer64bit_2_output1 | cbuffer64bit_3_output1 | cbuffer64bit_4_output1 | cbuffer64bit_5_output1 | cbuffer64bit_6_output1 | cbuffer64bit_7_output1 | cbuffer64bit_8_output1 | cbuffer64bit_9_output1 | cbuffer64bit_10_output1 | cbuffer64bit_11_output1 | cbuffer64bit_12_output1 | cbuffer64bit_13_output1 | cbuffer64bit_14_output1 | cbuffer64bit_15_output1 | cbuffer64bit_16_output1 | cbuffer64bit_17_output1 | cbuffer64bit_18_output1 | cbuffer64bit_19_output1 | cbuffer64bit_20_output1 | cbuffer64bit_21_output1 | cbuffer64bit_22_output1 | cbuffer64bit_23_output1 | cbuffer64bit_24_output1 | cbuffer64bit_25_output1 | cbuffer64bit_26_output1 | cbuffer64bit_27_output1 | cbuffer64bit_28_output1 | cbuffer64bit_29_output1 | cbuffer64bit_30_output1 | cbuffer64bit_31_output1 | cbuffer64bit_32_output1 | cbuffer64bit_33_output1 | cbuffer64bit_34_output1 | cbuffer64bit_35_output1 | cbuffer64bit_36_output1 | cbuffer64bit_37_output1 | cbuffer64bit_38_output1 | cbuffer64bit_39_output1 | cbuffer64bit_40_output1 | cbuffer64bit_41_output1 | cbuffer64bit_42_output1 | cbuffer64bit_43_output1 | cbuffer64bit_44_output1 | cbuffer64bit_45_output1 | cbuffer64bit_46_output1 | cbuffer64bit_47_output1 | cbuffer64bit_48_output1 | cbuffer64bit_49_output1 | cbuffer64bit_50_output1 | cbuffer64bit_51_output1 | cbuffer64bit_52_output1 | cbuffer64bit_53_output1 | cbuffer64bit_54_output1 | cbuffer64bit_55_output1 | cbuffer64bit_56_output1 | cbuffer64bit_57_output1 | cbuffer64bit_58_output1 | cbuffer64bit_59_output1 | cbuffer64bit_60_output1 | cbuffer64bit_61_output1 | cbuffer64bit_62_output1 | cbuffer64bit_63_output1 | cbuffer64bit_64_output1;  // OR_Gate or_1, 64 bits wide
endmodule

module shiftright64bit (
  input  [63:0] input1,
  input  [7:0] shiftright1,
  output [63:0] output1
);

  wire [63:8] undriven;

  mux6x64bit mux6x64bit_1 (
    .select1({undriven, shiftright1}), .input0(input1), .input1({1'b0, input1[63:1]}),
    .input2({2'b00, input1[63:2]}), .input3({3'b000, input1[63:3]}), .input4({4'b0000, input1[63:4]}),
    .input5({{5{1'b0}}, input1[63:5]}), .input6({{6{1'b0}}, input1[63:6]}),
    .input7({{7{1'b0}}, input1[63:7]}), .input8({{8{1'b0}}, input1[63:8]}),
    .input9({{9{1'b0}}, input1[63:9]}), .input10({{10{1'b0}}, input1[63:10]}),
    .input11({{11{1'b0}}, input1[63:11]}), .input12({{12{1'b0}}, input1[63:12]}),
    .input13({{13{1'b0}}, input1[63:13]}), .input14({{14{1'b0}}, input1[63:14]}),
    .input15({{15{1'b0}}, input1[63:15]}), .input16({{16{1'b0}}, input1[63:16]}),
    .input17({{17{1'b0}}, input1[63:17]}), .input18({{18{1'b0}}, input1[63:18]}),
    .input19({{19{1'b0}}, input1[63:19]}), .input20({{20{1'b0}}, input1[63:20]}),
    .input21({{21{1'b0}}, input1[63:21]}), .input22({{22{1'b0}}, input1[63:22]}),
    .input23({{23{1'b0}}, input1[63:23]}), .input24({{24{1'b0}}, input1[63:24]}),
    .input25({{25{1'b0}}, input1[63:25]}), .input26({{26{1'b0}}, input1[63:26]}),
    .input27({{27{1'b0}}, input1[63:27]}), .input28({{28{1'b0}}, input1[63:28]}),
    .input29({{29{1'b0}}, input1[63:29]}), .input30({{30{1'b0}}, input1[63:30]}),
    .input31({{31{1'b0}}, input1[63:31]}), .input32({{32{1'b0}}, input1[63:32]}),
    .input33({{33{1'b0}}, input1[63:33]}), .input34({{34{1'b0}}, input1[63:34]}),
    .input35({{35{1'b0}}, input1[63:35]}), .input36({{36{1'b0}}, input1[63:36]}),
    .input37({{37{1'b0}}, input1[63:37]}), .input38({{38{1'b0}}, input1[63:38]}),
    .input39({{39{1'b0}}, input1[63:39]}), .input40({{40{1'b0}}, input1[63:40]}),
    .input41({{41{1'b0}}, input1[63:41]}), .input42({{42{1'b0}}, input1[63:42]}),
    .input43({{43{1'b0}}, input1[63:43]}), .input44({{44{1'b0}}, input1[63:44]}),
    .input45({{45{1'b0}}, input1[63:45]}), .input46({{46{1'b0}}, input1[63:46]}),
    .input47({{47{1'b0}}, input1[63:47]}), .input48({{48{1'b0}}, input1[63:48]}),
    .input49({{49{1'b0}}, input1[63:49]}), .input50({{50{1'b0}}, input1[63:50]}),
    .input51({{51{1'b0}}, input1[63:51]}), .input52({{52{1'b0}}, input1[63:52]}),
    .input53({{53{1'b0}}, input1[63:53]}), .input54({{54{1'b0}}, input1[63:54]}),
    .input55({{55{1'b0}}, input1[63:55]}), .input56({{56{1'b0}}, input1[63:56]}),
    .input57({{57{1'b0}}, input1[63:57]}), .input58({{58{1'b0}}, input1[63:58]}),
    .input59({{59{1'b0}}, input1[63:59]}), .input60({{60{1'b0}}, input1[63:60]}),
    .input61({{61{1'b0}}, input1[63:61]}), .input62({{62{1'b0}}, input1[63:62]}),
    .input63({{63{1'b0}}, input1[63]}), .output1(output1));
  // Pins of 8 and 64 bits meet at {undriven, shiftright1}

  // Notes on the sheet:
  //   shiftright1: initial=0x30
  //   input1: initial=0xcafebabecafebabe
endmodule

module ashiftright64bit (
  input  [63:0] input1,
  input  [7:0] ashiftright1,
  output [63:0] output1
);

  wire [63:8] undriven;

  mux6x64bit mux6x64bit_1 (
    .select1({undriven, ashiftright1}), .input0(input1), .input1({1'b1, input1[63:1]}),
    .input2({2'b11, input1[63:2]}), .input3({3'b111, input1[63:3]}), .input4({4'b1111, input1[63:4]}),
    .input5({{5{1'b1}}, input1[63:5]}), .input6({{6{1'b1}}, input1[63:6]}),
    .input7({{7{1'b1}}, input1[63:7]}), .input8({{8{1'b1}}, input1[63:8]}),
    .input9({{9{1'b1}}, input1[63:9]}), .input10({{10{1'b1}}, input1[63:10]}),
    .input11({{11{1'b1}}, input1[63:11]}), .input12({{12{1'b1}}, input1[63:12]}),
    .input13({{13{1'b1}}, input1[63:13]}), .input14({{14{1'b1}}, input1[63:14]}),
    .input15({{15{1'b1}}, input1[63:15]}), .input16({{16{1'b1}}, input1[63:16]}),
    .input17({{17{1'b1}}, input1[63:17]}), .input18({{18{1'b1}}, input1[63:18]}),
    .input19({{19{1'b1}}, input1[63:19]}), .input20({{20{1'b1}}, input1[63:20]}),
    .input21({{21{1'b1}}, input1[63:21]}), .input22({{22{1'b1}}, input1[63:22]}),
    .input23({{23{1'b1}}, input1[63:23]}), .input24({{24{1'b1}}, input1[63:24]}),
    .input25({{25{1'b1}}, input1[63:25]}), .input26({{26{1'b1}}, input1[63:26]}),
    .input27({{27{1'b1}}, input1[63:27]}), .input28({{28{1'b1}}, input1[63:28]}),
    .input29({{29{1'b1}}, input1[63:29]}), .input30({{30{1'b1}}, input1[63:30]}),
    .input31({{31{1'b1}}, input1[63:31]}), .input32({{32{1'b1}}, input1[63:32]}),
    .input33({{33{1'b1}}, input1[63:33]}), .input34({{34{1'b1}}, input1[63:34]}),
    .input35({{35{1'b1}}, input1[63:35]}), .input36({{36{1'b1}}, input1[63:36]}),
    .input37({{37{1'b1}}, input1[63:37]}), .input38({{38{1'b1}}, input1[63:38]}),
    .input39({{39{1'b1}}, input1[63:39]}), .input40({{40{1'b1}}, input1[63:40]}),
    .input41({{41{1'b1}}, input1[63:41]}), .input42({{42{1'b1}}, input1[63:42]}),
    .input43({{43{1'b1}}, input1[63:43]}), .input44({{44{1'b1}}, input1[63:44]}),
    .input45({{45{1'b1}}, input1[63:45]}), .input46({{46{1'b1}}, input1[63:46]}),
    .input47({{47{1'b1}}, input1[63:47]}), .input48({{48{1'b1}}, input1[63:48]}),
    .input49({{49{1'b1}}, input1[63:49]}), .input50({{50{1'b1}}, input1[63:50]}),
    .input51({{51{1'b1}}, input1[63:51]}), .input52({{52{1'b1}}, input1[63:52]}),
    .input53({{53{1'b1}}, input1[63:53]}), .input54({{54{1'b1}}, input1[63:54]}),
    .input55({{55{1'b1}}, input1[63:55]}), .input56({{56{1'b1}}, input1[63:56]}),
    .input57({{57{1'b1}}, input1[63:57]}), .input58({{58{1'b1}}, input1[63:58]}),
    .input59({{59{1'b1}}, input1[63:59]}), .input60({{60{1'b1}}, input1[63:60]}),
    .input61({{61{1'b1}}, input1[63:61]}), .input62({{62{1'b1}}, input1[63:62]}),
    .input63({{63{1'b1}}, input1[63]}), .output1(output1));
  // Pins of 8 and 64 bits meet at {undriven, ashiftright1}

  // Notes on the sheet:
  //   ashiftright1: initial=0x30
  //   input1: initial=0xcafebabecafebabe
endmodule

module rotateleft64bit (
  input  [63:0] input1,
  input  [7:0] rotateleft1,
  output [63:0] output1
);

  wire [63:8] undriven;

  mux6x64bit mux6x64bit_1 (
    .select1({undriven, rotateleft1}), .input0(input1), .input1({input1[62:0], input1[63]}),
    .input2({input1[61:0], input1[63:62]}), .input3({input1[60:0], input1[63:61]}),
    .input4({input1[59:0], input1[63:60]}), .input5({input1[58:0], input1[63:59]}),
    .input6({input1[57:0], input1[63:58]}), .input7({input1[56:0], input1[63:57]}),
    .input8({input1[55:0], input1[63:56]}), .input9({input1[54:0], input1[63:55]}),
    .input10({input1[53:0], input1[63:54]}), .input11({input1[52:0], input1[63:53]}),
    .input12({input1[51:0], input1[63:52]}), .input13({input1[50:0], input1[63:51]}),
    .input14({input1[49:0], input1[63:50]}), .input15({input1[48:0], input1[63:49]}),
    .input16({input1[47:0], input1[63:48]}), .input17({input1[46:0], input1[63:47]}),
    .input18({input1[45:0], input1[63:46]}), .input19({input1[44:0], input1[63:45]}),
    .input20({input1[43:0], input1[63:44]}), .input21({input1[42:0], input1[63:43]}),
    .input22({input1[41:0], input1[63:42]}), .input23({input1[40:0], input1[63:41]}),
    .input24({input1[39:0], input1[63:40]}), .input25({input1[38:0], input1[63:39]}),
    .input26({input1[37:0], input1[63:38]}), .input27({input1[36:0], input1[63:37]}),
    .input28({input1[35:0], input1[63:36]}), .input29({input1[34:0], input1[63:35]}),
    .input30({input1[33:0], input1[63:34]}), .input31({input1[32:0], input1[63:33]}),
    .input32({input1[31:0], input1[63:32]}), .input33({input1[30:0], input1[63:31]}),
    .input34({input1[29:0], input1[63:30]}), .input35({input1[28:0], input1[63:29]}),
    .input36({input1[27:0], input1[63:28]}), .input37({input1[26:0], input1[63:27]}),
    .input38({input1[25:0], input1[63:26]}), .input39({input1[24:0], input1[63:25]}),
    .input40({input1[23:0], input1[63:24]}), .input41({input1[22:0], input1[63:23]}),
    .input42({input1[21:0], input1[63:22]}), .input43({input1[20:0], input1[63:21]}),
    .input44({input1[19:0], input1[63:20]}), .input45({input1[18:0], input1[63:19]}),
    .input46({input1[17:0], input1[63:18]}), .input47({input1[16:0], input1[63:17]}),
    .input48({input1[15:0], input1[63:16]}), .input49({input1[14:0], input1[63:15]}),
    .input50({input1[13:0], input1[63:14]}), .input51({input1[12:0], input1[63:13]}),
    .input52({input1[11:0], input1[63:12]}), .input53({input1[10:0], input1[63:11]}),
    .input54({input1[9:0], input1[63:10]}), .input55({input1[8:0], input1[63:9]}),
    .input56({input1[7:0], input1[63:8]}), .input57({input1[6:0], input1[63:7]}),
    .input58({input1[5:0], input1[63:6]}), .input59({input1[4:0], input1[63:5]}),
    .input60({input1[3:0], input1[63:4]}), .input61({input1[2:0], input1[63:3]}),
    .input62({input1[1:0], input1[63:2]}), .input63({input1[0], input1[63:1]}), .output1(output1));
  // Pins of 8 and 64 bits meet at {undriven, rotateleft1}

  // Notes on the sheet:
  //   rotateleft1: initial=0x30
  //   input1: initial=0xcafebabecafebabe
endmodule

module rotateright64bit (
  input  [63:0] input1,
  input  [7:0] rotateright1,
  output [63:0] output1
);

  wire [63:8] undriven;

  mux6x64bit mux6x64bit_1 (
    .select1({undriven, rotateright1}), .input0(input1), .input1({input1[0], input1[63:1]}),
    .input2({input1[1:0], input1[63:2]}), .input3({input1[2:0], input1[63:3]}),
    .input4({input1[3:0], input1[63:4]}), .input5({input1[4:0], input1[63:5]}),
    .input6({input1[5:0], input1[63:6]}), .input7({input1[6:0], input1[63:7]}),
    .input8({input1[7:0], input1[63:8]}), .input9({input1[8:0], input1[63:9]}),
    .input10({input1[9:0], input1[63:10]}), .input11({input1[10:0], input1[63:11]}),
    .input12({input1[11:0], input1[63:12]}), .input13({input1[12:0], input1[63:13]}),
    .input14({input1[13:0], input1[63:14]}), .input15({input1[14:0], input1[63:15]}),
    .input16({input1[15:0], input1[63:16]}), .input17({input1[16:0], input1[63:17]}),
    .input18({input1[17:0], input1[63:18]}), .input19({input1[18:0], input1[63:19]}),
    .input20({input1[19:0], input1[63:20]}), .input21({input1[20:0], input1[63:21]}),
    .input22({input1[21:0], input1[63:22]}), .input23({input1[22:0], input1[63:23]}),
    .input24({input1[23:0], input1[63:24]}), .input25({input1[24:0], input1[63:25]}),
    .input26({input1[25:0], input1[63:26]}), .input27({input1[26:0], input1[63:27]}),
    .input28({input1[27:0], input1[63:28]}), .input29({input1[28:0], input1[63:29]}),
    .input30({input1[29:0], input1[63:30]}), .input31({input1[30:0], input1[63:31]}),
    .input32({input1[31:0], input1[63:32]}), .input33({input1[32:0], input1[63:33]}),
    .input34({input1[33:0], input1[63:34]}), .input35({input1[34:0], input1[63:35]}),
    .input36({input1[35:0], input1[63:36]}), .input37({input1[36:0], input1[63:37]}),
    .input38({input1[37:0], input1[63:38]}), .input39({input1[38:0], input1[63:39]}),
    .input40({input1[39:0], input1[63:40]}), .input41({input1[40:0], input1[63:41]}),
    .input42({input1[41:0], input1[63:42]}), .input43({input1[42:0], input1[63:43]}),
    .input44({input1[43:0], input1[63:44]}), .input45({input1[44:0], input1[63:45]}),
    .input46({input1[45:0], input1[63:46]}), .input47({input1[46:0], input1[63:47]}),
    .input48({input1[47:0], input1[63:48]}), .input49({input1[48:0], input1[63:49]}),
    .input50({input1[49:0], input1[63:50]}), .input51({input1[50:0], input1[63:51]}),
    .input52({input1[51:0], input1[63:52]}), .input53({input1[52:0], input1[63:53]}),
    .input54({input1[53:0], input1[63:54]}), .input55({input1[54:0], input1[63:55]}),
    .input56({input1[55:0], input1[63:56]}), .input57({input1[56:0], input1[63:57]}),
    .input58({input1[57:0], input1[63:58]}), .input59({input1[58:0], input1[63:59]}),
    .input60({input1[59:0], input1[63:60]}), .input61({input1[60:0], input1[63:61]}),
    .input62({input1[61:0], input1[63:62]}), .input63({input1[62:0], input1[63]}), .output1(output1));
  // Pins of 8 and 64 bits meet at {undriven, rotateright1}

  // Notes on the sheet:
  //   rotateright1: initial=0x30
  //   input1: initial=0xcafebabecafebabe
endmodule
module divideru64bit (
  input  [63:0] inupper,
  input  [63:0] input1,
  input  [63:0] input2,
  output [63:0] remainder,
  output [63:0] output1
);

  wire comparatoru64bit_1_equal1, comparatoru256bit_1_equal1, comparatoru256bit_1_greater1,
       comparatoru256bit_2_equal1, comparatoru256bit_2_greater1, comparatoru256bit_3_equal1,
       comparatoru256bit_3_greater1, comparatoru256bit_4_equal1, comparatoru256bit_4_greater1,
       comparatoru256bit_5_equal1, comparatoru256bit_5_greater1, comparatoru256bit_6_equal1,
       comparatoru256bit_6_greater1, comparatoru256bit_7_equal1, comparatoru256bit_7_greater1,
       comparatoru256bit_8_equal1, comparatoru256bit_8_greater1, comparatoru256bit_9_equal1,
       comparatoru256bit_9_greater1, comparatoru256bit_10_equal1, comparatoru256bit_10_greater1,
       comparatoru256bit_11_equal1, comparatoru256bit_11_greater1, comparatoru256bit_12_equal1,
       comparatoru256bit_12_greater1, comparatoru256bit_13_equal1, comparatoru256bit_13_greater1,
       comparatoru256bit_14_equal1, comparatoru256bit_14_greater1, comparatoru256bit_15_equal1,
       comparatoru256bit_15_greater1, comparatoru256bit_16_equal1, comparatoru256bit_16_greater1,
       comparatoru256bit_17_equal1, comparatoru256bit_17_greater1, comparatoru256bit_18_equal1,
       comparatoru256bit_18_greater1, comparatoru256bit_19_equal1, comparatoru256bit_19_greater1,
       comparatoru256bit_20_equal1, comparatoru256bit_20_greater1, comparatoru256bit_21_equal1,
       comparatoru256bit_21_greater1, comparatoru256bit_22_equal1, comparatoru256bit_22_greater1,
       comparatoru256bit_23_equal1, comparatoru256bit_23_greater1, comparatoru256bit_24_equal1,
       comparatoru256bit_24_greater1, comparatoru256bit_25_equal1, comparatoru256bit_25_greater1,
       comparatoru256bit_26_equal1, comparatoru256bit_26_greater1, comparatoru256bit_27_equal1,
       comparatoru256bit_27_greater1, comparatoru256bit_28_equal1, comparatoru256bit_28_greater1,
       comparatoru256bit_29_equal1, comparatoru256bit_29_greater1, comparatoru256bit_30_equal1,
       comparatoru256bit_30_greater1, comparatoru256bit_31_equal1, comparatoru256bit_31_greater1,
       comparatoru256bit_32_equal1, comparatoru256bit_32_greater1, comparatoru256bit_33_equal1,
       comparatoru256bit_33_greater1, comparatoru256bit_34_equal1, comparatoru256bit_34_greater1,
       comparatoru256bit_35_equal1, comparatoru256bit_35_greater1, comparatoru256bit_36_equal1,
       comparatoru256bit_36_greater1, comparatoru256bit_37_equal1, comparatoru256bit_37_greater1,
       comparatoru256bit_38_equal1, comparatoru256bit_38_greater1, comparatoru256bit_39_equal1,
       comparatoru256bit_39_greater1, comparatoru256bit_40_equal1, comparatoru256bit_40_greater1,
       comparatoru256bit_41_equal1, comparatoru256bit_41_greater1, comparatoru256bit_42_equal1,
       comparatoru256bit_42_greater1, comparatoru256bit_43_equal1, comparatoru256bit_43_greater1,
       comparatoru256bit_44_equal1, comparatoru256bit_44_greater1, comparatoru256bit_45_equal1,
       comparatoru256bit_45_greater1, comparatoru256bit_46_equal1, comparatoru256bit_46_greater1,
       comparatoru256bit_47_equal1, comparatoru256bit_47_greater1, comparatoru256bit_48_equal1,
       comparatoru256bit_48_greater1, comparatoru256bit_49_equal1, comparatoru256bit_49_greater1,
       comparatoru256bit_50_equal1, comparatoru256bit_50_greater1, comparatoru256bit_51_equal1,
       comparatoru256bit_51_greater1, comparatoru256bit_52_equal1, comparatoru256bit_52_greater1,
       comparatoru256bit_53_equal1, comparatoru256bit_53_greater1, comparatoru256bit_54_equal1,
       comparatoru256bit_54_greater1, comparatoru256bit_55_equal1, comparatoru256bit_55_greater1,
       comparatoru256bit_56_equal1, comparatoru256bit_56_greater1, comparatoru256bit_57_equal1,
       comparatoru256bit_57_greater1, comparatoru256bit_58_equal1, comparatoru256bit_58_greater1,
       comparatoru256bit_59_equal1, comparatoru256bit_59_greater1, comparatoru256bit_60_equal1,
       comparatoru256bit_60_greater1, comparatoru256bit_61_equal1, comparatoru256bit_61_greater1,
       comparatoru256bit_62_equal1, comparatoru256bit_62_greater1, comparatoru256bit_63_equal1,
       comparatoru256bit_63_greater1, comparatoru256bit_64_equal1, comparatoru256bit_64_greater1,
       comparatoru256bit_65_equal1, comparatoru256bit_65_greater1, comparatoru256bit_66_equal1,
       comparatoru256bit_66_greater1, comparatoru256bit_67_equal1, comparatoru256bit_67_greater1,
       comparatoru256bit_68_equal1, comparatoru256bit_68_greater1, comparatoru256bit_69_equal1,
       comparatoru256bit_69_greater1, comparatoru256bit_70_equal1, comparatoru256bit_70_greater1,
       comparatoru256bit_71_equal1, comparatoru256bit_71_greater1, comparatoru256bit_72_equal1,
       comparatoru256bit_72_greater1, comparatoru256bit_73_equal1, comparatoru256bit_73_greater1,
       comparatoru256bit_74_equal1, comparatoru256bit_74_greater1, comparatoru256bit_75_equal1,
       comparatoru256bit_75_greater1, comparatoru256bit_76_equal1, comparatoru256bit_76_greater1,
       comparatoru256bit_77_equal1, comparatoru256bit_77_greater1, comparatoru256bit_78_equal1,
       comparatoru256bit_78_greater1, comparatoru256bit_79_equal1, comparatoru256bit_79_greater1,
       comparatoru256bit_80_equal1, comparatoru256bit_80_greater1, comparatoru256bit_81_equal1,
       comparatoru256bit_81_greater1, comparatoru256bit_82_equal1, comparatoru256bit_82_greater1,
       comparatoru256bit_83_equal1, comparatoru256bit_83_greater1, comparatoru256bit_84_equal1,
       comparatoru256bit_84_greater1, comparatoru256bit_85_equal1, comparatoru256bit_85_greater1,
       comparatoru256bit_86_equal1, comparatoru256bit_86_greater1, comparatoru256bit_87_equal1,
       comparatoru256bit_87_greater1, comparatoru256bit_88_equal1, comparatoru256bit_88_greater1,
       comparatoru256bit_89_equal1, comparatoru256bit_89_greater1, comparatoru256bit_90_equal1,
       comparatoru256bit_90_greater1, comparatoru256bit_91_equal1, comparatoru256bit_91_greater1,
       comparatoru256bit_92_equal1, comparatoru256bit_92_greater1, comparatoru256bit_93_equal1,
       comparatoru256bit_93_greater1, comparatoru256bit_94_equal1, comparatoru256bit_94_greater1,
       comparatoru256bit_95_equal1, comparatoru256bit_95_greater1, comparatoru256bit_96_equal1,
       comparatoru256bit_96_greater1, comparatoru256bit_97_equal1, comparatoru256bit_97_greater1,
       comparatoru256bit_98_equal1, comparatoru256bit_98_greater1, comparatoru256bit_99_equal1,
       comparatoru256bit_99_greater1, comparatoru256bit_100_equal1, comparatoru256bit_100_greater1,
       comparatoru256bit_101_equal1, comparatoru256bit_101_greater1, comparatoru256bit_102_equal1,
       comparatoru256bit_102_greater1, comparatoru256bit_103_equal1, comparatoru256bit_103_greater1,
       comparatoru256bit_104_equal1, comparatoru256bit_104_greater1, comparatoru256bit_105_equal1,
       comparatoru256bit_105_greater1, comparatoru256bit_106_equal1, comparatoru256bit_106_greater1,
       comparatoru256bit_107_equal1, comparatoru256bit_107_greater1, comparatoru256bit_108_equal1,
       comparatoru256bit_108_greater1, comparatoru256bit_109_equal1, comparatoru256bit_109_greater1,
       comparatoru256bit_110_equal1, comparatoru256bit_110_greater1, comparatoru256bit_111_equal1,
       comparatoru256bit_111_greater1, comparatoru256bit_112_equal1, comparatoru256bit_112_greater1,
       comparatoru256bit_113_equal1, comparatoru256bit_113_greater1, comparatoru256bit_114_equal1,
       comparatoru256bit_114_greater1, comparatoru256bit_115_equal1, comparatoru256bit_115_greater1,
       comparatoru256bit_116_equal1, comparatoru256bit_116_greater1, comparatoru256bit_117_equal1,
       comparatoru256bit_117_greater1, comparatoru256bit_118_equal1, comparatoru256bit_118_greater1,
       comparatoru256bit_119_equal1, comparatoru256bit_119_greater1, comparatoru256bit_120_equal1,
       comparatoru256bit_120_greater1, comparatoru256bit_121_equal1, comparatoru256bit_121_greater1,
       comparatoru256bit_122_equal1, comparatoru256bit_122_greater1, comparatoru256bit_123_equal1,
       comparatoru256bit_123_greater1, comparatoru256bit_124_equal1, comparatoru256bit_124_greater1,
       comparatoru256bit_125_equal1, comparatoru256bit_125_greater1, comparatoru256bit_126_equal1,
       comparatoru256bit_126_greater1, comparatoru256bit_127_equal1, comparatoru256bit_127_greater1,
       comparatoru256bit_128_equal1, comparatoru256bit_128_greater1, not_1_out, or_1_out, or_2_out, or_3_out,
       or_4_out, or_5_out, or_6_out, or_7_out, or_8_out, or_9_out, or_10_out, or_11_out, or_12_out,
       or_13_out, or_14_out, or_15_out, or_16_out, or_17_out, or_18_out, or_19_out, or_20_out, or_21_out,
       or_22_out, or_23_out, or_24_out, or_25_out, or_26_out, or_27_out, or_28_out, or_29_out, or_30_out,
       or_31_out, or_32_out, or_33_out, or_34_out, or_35_out, or_36_out, or_37_out, or_38_out, or_39_out,
       or_40_out, or_41_out, or_42_out, or_43_out, or_44_out, or_45_out, or_46_out, or_47_out, or_48_out,
       or_49_out, or_50_out, or_51_out, or_52_out, or_53_out, or_54_out, or_55_out, or_56_out, or_57_out,
       or_58_out, or_59_out, or_60_out, or_61_out, or_62_out, or_63_out, or_64_out, or_65_out, or_66_out,
       or_67_out, or_68_out, or_69_out, or_70_out, or_71_out, or_72_out, or_73_out, or_74_out, or_75_out,
       or_76_out, or_77_out, or_78_out, or_79_out, or_80_out, or_81_out, or_82_out, or_83_out, or_84_out,
       or_85_out, or_86_out, or_87_out, or_88_out, or_89_out, or_90_out, or_91_out, or_92_out, or_93_out,
       or_94_out, or_95_out, or_96_out, or_97_out, or_98_out, or_99_out, or_100_out, or_101_out, or_102_out,
       or_103_out, or_104_out, or_105_out, or_106_out, or_107_out, or_108_out, or_109_out, or_110_out,
       or_111_out, or_112_out, or_113_out, or_114_out, or_115_out, or_116_out, or_117_out, or_118_out,
       or_119_out, or_120_out, or_121_out, or_122_out, or_123_out, or_124_out, or_125_out, or_126_out,
       or_127_out, or_128_out;
  wire [63:0] and_127_out, cbuffer256bit_1_output1a, cbuffer256bit_1_output1b, cbuffer256bit_1_output1c,
       cbuffer256bit_1_output1d, cbuffer256bit_2_output1a, cbuffer256bit_2_output1b,
       cbuffer256bit_2_output1c, cbuffer256bit_2_output1d, cbuffer256bit_3_output1a,
       cbuffer256bit_3_output1b, cbuffer256bit_3_output1c, cbuffer256bit_3_output1d,
       cbuffer256bit_4_output1a, cbuffer256bit_4_output1b, cbuffer256bit_4_output1c,
       cbuffer256bit_4_output1d, cbuffer256bit_5_output1a, cbuffer256bit_5_output1b,
       cbuffer256bit_5_output1c, cbuffer256bit_5_output1d, cbuffer256bit_6_output1a,
       cbuffer256bit_6_output1b, cbuffer256bit_6_output1c, cbuffer256bit_6_output1d,
       cbuffer256bit_7_output1a, cbuffer256bit_7_output1b, cbuffer256bit_7_output1c,
       cbuffer256bit_7_output1d, cbuffer256bit_8_output1a, cbuffer256bit_8_output1b,
       cbuffer256bit_8_output1c, cbuffer256bit_8_output1d, cbuffer256bit_9_output1a,
       cbuffer256bit_9_output1b, cbuffer256bit_9_output1c, cbuffer256bit_9_output1d,
       cbuffer256bit_10_output1a, cbuffer256bit_10_output1b, cbuffer256bit_10_output1c,
       cbuffer256bit_10_output1d, cbuffer256bit_11_output1a, cbuffer256bit_11_output1b,
       cbuffer256bit_11_output1c, cbuffer256bit_11_output1d, cbuffer256bit_12_output1a,
       cbuffer256bit_12_output1b, cbuffer256bit_12_output1c, cbuffer256bit_12_output1d,
       cbuffer256bit_13_output1a, cbuffer256bit_13_output1b, cbuffer256bit_13_output1c,
       cbuffer256bit_13_output1d, cbuffer256bit_14_output1a, cbuffer256bit_14_output1b,
       cbuffer256bit_14_output1c, cbuffer256bit_14_output1d, cbuffer256bit_15_output1a,
       cbuffer256bit_15_output1b, cbuffer256bit_15_output1c, cbuffer256bit_15_output1d,
       cbuffer256bit_16_output1a, cbuffer256bit_16_output1b, cbuffer256bit_16_output1c,
       cbuffer256bit_16_output1d, cbuffer256bit_17_output1a, cbuffer256bit_17_output1b,
       cbuffer256bit_17_output1c, cbuffer256bit_17_output1d, cbuffer256bit_18_output1a,
       cbuffer256bit_18_output1b, cbuffer256bit_18_output1c, cbuffer256bit_18_output1d,
       cbuffer256bit_19_output1a, cbuffer256bit_19_output1b, cbuffer256bit_19_output1c,
       cbuffer256bit_19_output1d, cbuffer256bit_20_output1a, cbuffer256bit_20_output1b,
       cbuffer256bit_20_output1c, cbuffer256bit_20_output1d, cbuffer256bit_21_output1a,
       cbuffer256bit_21_output1b, cbuffer256bit_21_output1c, cbuffer256bit_21_output1d,
       cbuffer256bit_22_output1a, cbuffer256bit_22_output1b, cbuffer256bit_22_output1c,
       cbuffer256bit_22_output1d, cbuffer256bit_23_output1a, cbuffer256bit_23_output1b,
       cbuffer256bit_23_output1c, cbuffer256bit_23_output1d, cbuffer256bit_24_output1a,
       cbuffer256bit_24_output1b, cbuffer256bit_24_output1c, cbuffer256bit_24_output1d,
       cbuffer256bit_25_output1a, cbuffer256bit_25_output1b, cbuffer256bit_25_output1c,
       cbuffer256bit_25_output1d, cbuffer256bit_26_output1a, cbuffer256bit_26_output1b,
       cbuffer256bit_26_output1c, cbuffer256bit_26_output1d, cbuffer256bit_27_output1a,
       cbuffer256bit_27_output1b, cbuffer256bit_27_output1c, cbuffer256bit_27_output1d,
       cbuffer256bit_28_output1a, cbuffer256bit_28_output1b, cbuffer256bit_28_output1c,
       cbuffer256bit_28_output1d, cbuffer256bit_29_output1a, cbuffer256bit_29_output1b,
       cbuffer256bit_29_output1c, cbuffer256bit_29_output1d, cbuffer256bit_30_output1a,
       cbuffer256bit_30_output1b, cbuffer256bit_30_output1c, cbuffer256bit_30_output1d,
       cbuffer256bit_31_output1a, cbuffer256bit_31_output1b, cbuffer256bit_31_output1c,
       cbuffer256bit_31_output1d, cbuffer256bit_32_output1a, cbuffer256bit_32_output1b,
       cbuffer256bit_32_output1c, cbuffer256bit_32_output1d, cbuffer256bit_33_output1a,
       cbuffer256bit_33_output1b, cbuffer256bit_33_output1c, cbuffer256bit_33_output1d,
       cbuffer256bit_34_output1a, cbuffer256bit_34_output1b, cbuffer256bit_34_output1c,
       cbuffer256bit_34_output1d, cbuffer256bit_35_output1a, cbuffer256bit_35_output1b,
       cbuffer256bit_35_output1c, cbuffer256bit_35_output1d, cbuffer256bit_36_output1a,
       cbuffer256bit_36_output1b, cbuffer256bit_36_output1c, cbuffer256bit_36_output1d,
       cbuffer256bit_37_output1a, cbuffer256bit_37_output1b, cbuffer256bit_37_output1c,
       cbuffer256bit_37_output1d, cbuffer256bit_38_output1a, cbuffer256bit_38_output1b,
       cbuffer256bit_38_output1c, cbuffer256bit_38_output1d, cbuffer256bit_39_output1a,
       cbuffer256bit_39_output1b, cbuffer256bit_39_output1c, cbuffer256bit_39_output1d,
       cbuffer256bit_40_output1a, cbuffer256bit_40_output1b, cbuffer256bit_40_output1c,
       cbuffer256bit_40_output1d, cbuffer256bit_41_output1a, cbuffer256bit_41_output1b,
       cbuffer256bit_41_output1c, cbuffer256bit_41_output1d, cbuffer256bit_42_output1a,
       cbuffer256bit_42_output1b, cbuffer256bit_42_output1c, cbuffer256bit_42_output1d,
       cbuffer256bit_43_output1a, cbuffer256bit_43_output1b, cbuffer256bit_43_output1c,
       cbuffer256bit_43_output1d, cbuffer256bit_44_output1a, cbuffer256bit_44_output1b,
       cbuffer256bit_44_output1c, cbuffer256bit_44_output1d, cbuffer256bit_45_output1a,
       cbuffer256bit_45_output1b, cbuffer256bit_45_output1c, cbuffer256bit_45_output1d,
       cbuffer256bit_46_output1a, cbuffer256bit_46_output1b, cbuffer256bit_46_output1c,
       cbuffer256bit_46_output1d, cbuffer256bit_47_output1a, cbuffer256bit_47_output1b,
       cbuffer256bit_47_output1c, cbuffer256bit_47_output1d, cbuffer256bit_48_output1a,
       cbuffer256bit_48_output1b, cbuffer256bit_48_output1c, cbuffer256bit_48_output1d,
       cbuffer256bit_49_output1a, cbuffer256bit_49_output1b, cbuffer256bit_49_output1c,
       cbuffer256bit_49_output1d, cbuffer256bit_50_output1a, cbuffer256bit_50_output1b,
       cbuffer256bit_50_output1c, cbuffer256bit_50_output1d, cbuffer256bit_51_output1a,
       cbuffer256bit_51_output1b, cbuffer256bit_51_output1c, cbuffer256bit_51_output1d,
       cbuffer256bit_52_output1a, cbuffer256bit_52_output1b, cbuffer256bit_52_output1c,
       cbuffer256bit_52_output1d, cbuffer256bit_53_output1a, cbuffer256bit_53_output1b,
       cbuffer256bit_53_output1c, cbuffer256bit_53_output1d, cbuffer256bit_54_output1a,
       cbuffer256bit_54_output1b, cbuffer256bit_54_output1c, cbuffer256bit_54_output1d,
       cbuffer256bit_55_output1a, cbuffer256bit_55_output1b, cbuffer256bit_55_output1c,
       cbuffer256bit_55_output1d, cbuffer256bit_56_output1a, cbuffer256bit_56_output1b,
       cbuffer256bit_56_output1c, cbuffer256bit_56_output1d, cbuffer256bit_57_output1a,
       cbuffer256bit_57_output1b, cbuffer256bit_57_output1c, cbuffer256bit_57_output1d,
       cbuffer256bit_58_output1a, cbuffer256bit_58_output1b, cbuffer256bit_58_output1c,
       cbuffer256bit_58_output1d, cbuffer256bit_59_output1a, cbuffer256bit_59_output1b,
       cbuffer256bit_59_output1c, cbuffer256bit_59_output1d, cbuffer256bit_60_output1a,
       cbuffer256bit_60_output1b, cbuffer256bit_60_output1c, cbuffer256bit_60_output1d,
       cbuffer256bit_61_output1a, cbuffer256bit_61_output1b, cbuffer256bit_61_output1c,
       cbuffer256bit_61_output1d, cbuffer256bit_62_output1a, cbuffer256bit_62_output1b,
       cbuffer256bit_62_output1c, cbuffer256bit_62_output1d, cbuffer256bit_63_output1a,
       cbuffer256bit_63_output1b, cbuffer256bit_63_output1c, cbuffer256bit_63_output1d,
       cbuffer256bit_64_output1a, cbuffer256bit_64_output1b, cbuffer256bit_64_output1c,
       cbuffer256bit_64_output1d, cbuffer256bit_65_output1a, cbuffer256bit_65_output1b,
       cbuffer256bit_65_output1c, cbuffer256bit_65_output1d, cbuffer256bit_66_output1a,
       cbuffer256bit_66_output1b, cbuffer256bit_66_output1c, cbuffer256bit_66_output1d,
       cbuffer256bit_67_output1a, cbuffer256bit_67_output1b, cbuffer256bit_67_output1c,
       cbuffer256bit_67_output1d, cbuffer256bit_68_output1a, cbuffer256bit_68_output1b,
       cbuffer256bit_68_output1c, cbuffer256bit_68_output1d, cbuffer256bit_69_output1a,
       cbuffer256bit_69_output1b, cbuffer256bit_69_output1c, cbuffer256bit_69_output1d,
       cbuffer256bit_70_output1a, cbuffer256bit_70_output1b, cbuffer256bit_70_output1c,
       cbuffer256bit_70_output1d, cbuffer256bit_71_output1a, cbuffer256bit_71_output1b,
       cbuffer256bit_71_output1c, cbuffer256bit_71_output1d, cbuffer256bit_72_output1a,
       cbuffer256bit_72_output1b, cbuffer256bit_72_output1c, cbuffer256bit_72_output1d,
       cbuffer256bit_73_output1a, cbuffer256bit_73_output1b, cbuffer256bit_73_output1c,
       cbuffer256bit_73_output1d, cbuffer256bit_74_output1a, cbuffer256bit_74_output1b,
       cbuffer256bit_74_output1c, cbuffer256bit_74_output1d, cbuffer256bit_75_output1a,
       cbuffer256bit_75_output1b, cbuffer256bit_75_output1c, cbuffer256bit_75_output1d,
       cbuffer256bit_76_output1a, cbuffer256bit_76_output1b, cbuffer256bit_76_output1c,
       cbuffer256bit_76_output1d, cbuffer256bit_77_output1a, cbuffer256bit_77_output1b,
       cbuffer256bit_77_output1c, cbuffer256bit_77_output1d, cbuffer256bit_78_output1a,
       cbuffer256bit_78_output1b, cbuffer256bit_78_output1c, cbuffer256bit_78_output1d,
       cbuffer256bit_79_output1a, cbuffer256bit_79_output1b, cbuffer256bit_79_output1c,
       cbuffer256bit_79_output1d, cbuffer256bit_80_output1a, cbuffer256bit_80_output1b,
       cbuffer256bit_80_output1c, cbuffer256bit_80_output1d, cbuffer256bit_81_output1a,
       cbuffer256bit_81_output1b, cbuffer256bit_81_output1c, cbuffer256bit_81_output1d,
       cbuffer256bit_82_output1a, cbuffer256bit_82_output1b, cbuffer256bit_82_output1c,
       cbuffer256bit_82_output1d, cbuffer256bit_83_output1a, cbuffer256bit_83_output1b,
       cbuffer256bit_83_output1c, cbuffer256bit_83_output1d, cbuffer256bit_84_output1a,
       cbuffer256bit_84_output1b, cbuffer256bit_84_output1c, cbuffer256bit_84_output1d,
       cbuffer256bit_85_output1a, cbuffer256bit_85_output1b, cbuffer256bit_85_output1c,
       cbuffer256bit_85_output1d, cbuffer256bit_86_output1a, cbuffer256bit_86_output1b,
       cbuffer256bit_86_output1c, cbuffer256bit_86_output1d, cbuffer256bit_87_output1a,
       cbuffer256bit_87_output1b, cbuffer256bit_87_output1c, cbuffer256bit_87_output1d,
       cbuffer256bit_88_output1a, cbuffer256bit_88_output1b, cbuffer256bit_88_output1c,
       cbuffer256bit_88_output1d, cbuffer256bit_89_output1a, cbuffer256bit_89_output1b,
       cbuffer256bit_89_output1c, cbuffer256bit_89_output1d, cbuffer256bit_90_output1a,
       cbuffer256bit_90_output1b, cbuffer256bit_90_output1c, cbuffer256bit_90_output1d,
       cbuffer256bit_91_output1a, cbuffer256bit_91_output1b, cbuffer256bit_91_output1c,
       cbuffer256bit_91_output1d, cbuffer256bit_92_output1a, cbuffer256bit_92_output1b,
       cbuffer256bit_92_output1c, cbuffer256bit_92_output1d, cbuffer256bit_93_output1a,
       cbuffer256bit_93_output1b, cbuffer256bit_93_output1c, cbuffer256bit_93_output1d,
       cbuffer256bit_94_output1a, cbuffer256bit_94_output1b, cbuffer256bit_94_output1c,
       cbuffer256bit_94_output1d, cbuffer256bit_95_output1a, cbuffer256bit_95_output1b,
       cbuffer256bit_95_output1c, cbuffer256bit_95_output1d, cbuffer256bit_96_output1a,
       cbuffer256bit_96_output1b, cbuffer256bit_96_output1c, cbuffer256bit_96_output1d,
       cbuffer256bit_97_output1a, cbuffer256bit_97_output1b, cbuffer256bit_97_output1c,
       cbuffer256bit_97_output1d, cbuffer256bit_98_output1a, cbuffer256bit_98_output1b,
       cbuffer256bit_98_output1c, cbuffer256bit_98_output1d, cbuffer256bit_99_output1a,
       cbuffer256bit_99_output1b, cbuffer256bit_99_output1c, cbuffer256bit_99_output1d,
       cbuffer256bit_100_output1a, cbuffer256bit_100_output1b, cbuffer256bit_100_output1c,
       cbuffer256bit_100_output1d, cbuffer256bit_101_output1a, cbuffer256bit_101_output1b,
       cbuffer256bit_101_output1c, cbuffer256bit_101_output1d, cbuffer256bit_102_output1a,
       cbuffer256bit_102_output1b, cbuffer256bit_102_output1c, cbuffer256bit_102_output1d,
       cbuffer256bit_103_output1a, cbuffer256bit_103_output1b, cbuffer256bit_103_output1c,
       cbuffer256bit_103_output1d, cbuffer256bit_104_output1a, cbuffer256bit_104_output1b,
       cbuffer256bit_104_output1c, cbuffer256bit_104_output1d, cbuffer256bit_105_output1a,
       cbuffer256bit_105_output1b, cbuffer256bit_105_output1c, cbuffer256bit_105_output1d,
       cbuffer256bit_106_output1a, cbuffer256bit_106_output1b, cbuffer256bit_106_output1c,
       cbuffer256bit_106_output1d, cbuffer256bit_107_output1a, cbuffer256bit_107_output1b,
       cbuffer256bit_107_output1c, cbuffer256bit_107_output1d, cbuffer256bit_108_output1a,
       cbuffer256bit_108_output1b, cbuffer256bit_108_output1c, cbuffer256bit_108_output1d,
       cbuffer256bit_109_output1a, cbuffer256bit_109_output1b, cbuffer256bit_109_output1c,
       cbuffer256bit_109_output1d, cbuffer256bit_110_output1a, cbuffer256bit_110_output1b,
       cbuffer256bit_110_output1c, cbuffer256bit_110_output1d, cbuffer256bit_111_output1a,
       cbuffer256bit_111_output1b, cbuffer256bit_111_output1c, cbuffer256bit_111_output1d,
       cbuffer256bit_112_output1a, cbuffer256bit_112_output1b, cbuffer256bit_112_output1c,
       cbuffer256bit_112_output1d, cbuffer256bit_113_output1a, cbuffer256bit_113_output1b,
       cbuffer256bit_113_output1c, cbuffer256bit_113_output1d, cbuffer256bit_114_output1a,
       cbuffer256bit_114_output1b, cbuffer256bit_114_output1c, cbuffer256bit_114_output1d,
       cbuffer256bit_115_output1a, cbuffer256bit_115_output1b, cbuffer256bit_115_output1c,
       cbuffer256bit_115_output1d, cbuffer256bit_116_output1a, cbuffer256bit_116_output1b,
       cbuffer256bit_116_output1c, cbuffer256bit_116_output1d, cbuffer256bit_117_output1a,
       cbuffer256bit_117_output1b, cbuffer256bit_117_output1c, cbuffer256bit_117_output1d,
       cbuffer256bit_118_output1a, cbuffer256bit_118_output1b, cbuffer256bit_118_output1c,
       cbuffer256bit_118_output1d, cbuffer256bit_119_output1a, cbuffer256bit_119_output1b,
       cbuffer256bit_119_output1c, cbuffer256bit_119_output1d, cbuffer256bit_120_output1a,
       cbuffer256bit_120_output1b, cbuffer256bit_120_output1c, cbuffer256bit_120_output1d,
       cbuffer256bit_121_output1a, cbuffer256bit_121_output1b, cbuffer256bit_121_output1c,
       cbuffer256bit_121_output1d, cbuffer256bit_122_output1a, cbuffer256bit_122_output1b,
       cbuffer256bit_122_output1c, cbuffer256bit_122_output1d, cbuffer256bit_123_output1a,
       cbuffer256bit_123_output1b, cbuffer256bit_123_output1c, cbuffer256bit_123_output1d,
       cbuffer256bit_124_output1a, cbuffer256bit_124_output1b, cbuffer256bit_124_output1c,
       cbuffer256bit_124_output1d, cbuffer256bit_125_output1a, cbuffer256bit_125_output1b,
       cbuffer256bit_125_output1c, cbuffer256bit_125_output1d, cbuffer256bit_126_output1a,
       cbuffer256bit_126_output1b, cbuffer256bit_126_output1c, cbuffer256bit_126_output1d,
       cbuffer256bit_127_output1a, cbuffer256bit_127_output1b, cbuffer256bit_127_output1c,
       cbuffer256bit_127_output1d, cbuffer256bit_128_output1a, cbuffer256bit_128_output1b,
       cbuffer256bit_128_output1c, cbuffer256bit_128_output1d, divider_1_out, divider_1_rem,
       subtractor256bit_1_output1a, subtractor256bit_1_output1b, subtractor256bit_1_output1c,
       subtractor256bit_1_output1d, subtractor256bit_2_output1a, subtractor256bit_2_output1b,
       subtractor256bit_2_output1c, subtractor256bit_2_output1d, subtractor256bit_3_output1a,
       subtractor256bit_3_output1b, subtractor256bit_3_output1c, subtractor256bit_3_output1d,
       subtractor256bit_4_output1a, subtractor256bit_4_output1b, subtractor256bit_4_output1c,
       subtractor256bit_4_output1d, subtractor256bit_5_output1a, subtractor256bit_5_output1b,
       subtractor256bit_5_output1c, subtractor256bit_5_output1d, subtractor256bit_6_output1a,
       subtractor256bit_6_output1b, subtractor256bit_6_output1c, subtractor256bit_6_output1d,
       subtractor256bit_7_output1a, subtractor256bit_7_output1b, subtractor256bit_7_output1c,
       subtractor256bit_7_output1d, subtractor256bit_8_output1a, subtractor256bit_8_output1b,
       subtractor256bit_8_output1c, subtractor256bit_8_output1d, subtractor256bit_9_output1a,
       subtractor256bit_9_output1b, subtractor256bit_9_output1c, subtractor256bit_9_output1d,
       subtractor256bit_10_output1a, subtractor256bit_10_output1b, subtractor256bit_10_output1c,
       subtractor256bit_10_output1d, subtractor256bit_11_output1a, subtractor256bit_11_output1b,
       subtractor256bit_11_output1c, subtractor256bit_11_output1d, subtractor256bit_12_output1a,
       subtractor256bit_12_output1b, subtractor256bit_12_output1c, subtractor256bit_12_output1d,
       subtractor256bit_13_output1a, subtractor256bit_13_output1b, subtractor256bit_13_output1c,
       subtractor256bit_13_output1d, subtractor256bit_14_output1a, subtractor256bit_14_output1b,
       subtractor256bit_14_output1c, subtractor256bit_14_output1d, subtractor256bit_15_output1a,
       subtractor256bit_15_output1b, subtractor256bit_15_output1c, subtractor256bit_15_output1d,
       subtractor256bit_16_output1a, subtractor256bit_16_output1b, subtractor256bit_16_output1c,
       subtractor256bit_16_output1d, subtractor256bit_17_output1a, subtractor256bit_17_output1b,
       subtractor256bit_17_output1c, subtractor256bit_17_output1d, subtractor256bit_18_output1a,
       subtractor256bit_18_output1b, subtractor256bit_18_output1c, subtractor256bit_18_output1d,
       subtractor256bit_19_output1a, subtractor256bit_19_output1b, subtractor256bit_19_output1c,
       subtractor256bit_19_output1d, subtractor256bit_20_output1a, subtractor256bit_20_output1b,
       subtractor256bit_20_output1c, subtractor256bit_20_output1d, subtractor256bit_21_output1a,
       subtractor256bit_21_output1b, subtractor256bit_21_output1c, subtractor256bit_21_output1d,
       subtractor256bit_22_output1a, subtractor256bit_22_output1b, subtractor256bit_22_output1c,
       subtractor256bit_22_output1d, subtractor256bit_23_output1a, subtractor256bit_23_output1b,
       subtractor256bit_23_output1c, subtractor256bit_23_output1d, subtractor256bit_24_output1a,
       subtractor256bit_24_output1b, subtractor256bit_24_output1c, subtractor256bit_24_output1d,
       subtractor256bit_25_output1a, subtractor256bit_25_output1b, subtractor256bit_25_output1c,
       subtractor256bit_25_output1d, subtractor256bit_26_output1a, subtractor256bit_26_output1b,
       subtractor256bit_26_output1c, subtractor256bit_26_output1d, subtractor256bit_27_output1a,
       subtractor256bit_27_output1b, subtractor256bit_27_output1c, subtractor256bit_27_output1d,
       subtractor256bit_28_output1a, subtractor256bit_28_output1b, subtractor256bit_28_output1c,
       subtractor256bit_28_output1d, subtractor256bit_29_output1a, subtractor256bit_29_output1b,
       subtractor256bit_29_output1c, subtractor256bit_29_output1d, subtractor256bit_30_output1a,
       subtractor256bit_30_output1b, subtractor256bit_30_output1c, subtractor256bit_30_output1d,
       subtractor256bit_31_output1a, subtractor256bit_31_output1b, subtractor256bit_31_output1c,
       subtractor256bit_31_output1d, subtractor256bit_32_output1a, subtractor256bit_32_output1b,
       subtractor256bit_32_output1c, subtractor256bit_32_output1d, subtractor256bit_33_output1a,
       subtractor256bit_33_output1b, subtractor256bit_33_output1c, subtractor256bit_33_output1d,
       subtractor256bit_34_output1a, subtractor256bit_34_output1b, subtractor256bit_34_output1c,
       subtractor256bit_34_output1d, subtractor256bit_35_output1a, subtractor256bit_35_output1b,
       subtractor256bit_35_output1c, subtractor256bit_35_output1d, subtractor256bit_36_output1a,
       subtractor256bit_36_output1b, subtractor256bit_36_output1c, subtractor256bit_36_output1d,
       subtractor256bit_37_output1a, subtractor256bit_37_output1b, subtractor256bit_37_output1c,
       subtractor256bit_37_output1d, subtractor256bit_38_output1a, subtractor256bit_38_output1b,
       subtractor256bit_38_output1c, subtractor256bit_38_output1d, subtractor256bit_39_output1a,
       subtractor256bit_39_output1b, subtractor256bit_39_output1c, subtractor256bit_39_output1d,
       subtractor256bit_40_output1a, subtractor256bit_40_output1b, subtractor256bit_40_output1c,
       subtractor256bit_40_output1d, subtractor256bit_41_output1a, subtractor256bit_41_output1b,
       subtractor256bit_41_output1c, subtractor256bit_41_output1d, subtractor256bit_42_output1a,
       subtractor256bit_42_output1b, subtractor256bit_42_output1c, subtractor256bit_42_output1d,
       subtractor256bit_43_output1a, subtractor256bit_43_output1b, subtractor256bit_43_output1c,
       subtractor256bit_43_output1d, subtractor256bit_44_output1a, subtractor256bit_44_output1b,
       subtractor256bit_44_output1c, subtractor256bit_44_output1d, subtractor256bit_45_output1a,
       subtractor256bit_45_output1b, subtractor256bit_45_output1c, subtractor256bit_45_output1d,
       subtractor256bit_46_output1a, subtractor256bit_46_output1b, subtractor256bit_46_output1c,
       subtractor256bit_46_output1d, subtractor256bit_47_output1a, subtractor256bit_47_output1b,
       subtractor256bit_47_output1c, subtractor256bit_47_output1d, subtractor256bit_48_output1a,
       subtractor256bit_48_output1b, subtractor256bit_48_output1c, subtractor256bit_48_output1d,
       subtractor256bit_49_output1a, subtractor256bit_49_output1b, subtractor256bit_49_output1c,
       subtractor256bit_49_output1d, subtractor256bit_50_output1a, subtractor256bit_50_output1b,
       subtractor256bit_50_output1c, subtractor256bit_50_output1d, subtractor256bit_51_output1a,
       subtractor256bit_51_output1b, subtractor256bit_51_output1c, subtractor256bit_51_output1d,
       subtractor256bit_52_output1a, subtractor256bit_52_output1b, subtractor256bit_52_output1c,
       subtractor256bit_52_output1d, subtractor256bit_53_output1a, subtractor256bit_53_output1b,
       subtractor256bit_53_output1c, subtractor256bit_53_output1d, subtractor256bit_54_output1a,
       subtractor256bit_54_output1b, subtractor256bit_54_output1c, subtractor256bit_54_output1d,
       subtractor256bit_55_output1a, subtractor256bit_55_output1b, subtractor256bit_55_output1c,
       subtractor256bit_55_output1d, subtractor256bit_56_output1a, subtractor256bit_56_output1b,
       subtractor256bit_56_output1c, subtractor256bit_56_output1d, subtractor256bit_57_output1a,
       subtractor256bit_57_output1b, subtractor256bit_57_output1c, subtractor256bit_57_output1d,
       subtractor256bit_58_output1a, subtractor256bit_58_output1b, subtractor256bit_58_output1c,
       subtractor256bit_58_output1d, subtractor256bit_59_output1a, subtractor256bit_59_output1b,
       subtractor256bit_59_output1c, subtractor256bit_59_output1d, subtractor256bit_60_output1a,
       subtractor256bit_60_output1b, subtractor256bit_60_output1c, subtractor256bit_60_output1d,
       subtractor256bit_61_output1a, subtractor256bit_61_output1b, subtractor256bit_61_output1c,
       subtractor256bit_61_output1d, subtractor256bit_62_output1a, subtractor256bit_62_output1b,
       subtractor256bit_62_output1c, subtractor256bit_62_output1d, subtractor256bit_63_output1a,
       subtractor256bit_63_output1b, subtractor256bit_63_output1c, subtractor256bit_63_output1d,
       subtractor256bit_64_output1a, subtractor256bit_64_output1b, subtractor256bit_64_output1c,
       subtractor256bit_64_output1d, subtractor256bit_65_output1a, subtractor256bit_65_output1b,
       subtractor256bit_65_output1c, subtractor256bit_65_output1d, subtractor256bit_66_output1a,
       subtractor256bit_66_output1b, subtractor256bit_66_output1c, subtractor256bit_66_output1d,
       subtractor256bit_67_output1a, subtractor256bit_67_output1b, subtractor256bit_67_output1c,
       subtractor256bit_67_output1d, subtractor256bit_68_output1a, subtractor256bit_68_output1b,
       subtractor256bit_68_output1c, subtractor256bit_68_output1d, subtractor256bit_69_output1a,
       subtractor256bit_69_output1b, subtractor256bit_69_output1c, subtractor256bit_69_output1d,
       subtractor256bit_70_output1a, subtractor256bit_70_output1b, subtractor256bit_70_output1c,
       subtractor256bit_70_output1d, subtractor256bit_71_output1a, subtractor256bit_71_output1b,
       subtractor256bit_71_output1c, subtractor256bit_71_output1d, subtractor256bit_72_output1a,
       subtractor256bit_72_output1b, subtractor256bit_72_output1c, subtractor256bit_72_output1d,
       subtractor256bit_73_output1a, subtractor256bit_73_output1b, subtractor256bit_73_output1c,
       subtractor256bit_73_output1d, subtractor256bit_74_output1a, subtractor256bit_74_output1b,
       subtractor256bit_74_output1c, subtractor256bit_74_output1d, subtractor256bit_75_output1a,
       subtractor256bit_75_output1b, subtractor256bit_75_output1c, subtractor256bit_75_output1d,
       subtractor256bit_76_output1a, subtractor256bit_76_output1b, subtractor256bit_76_output1c,
       subtractor256bit_76_output1d, subtractor256bit_77_output1a, subtractor256bit_77_output1b,
       subtractor256bit_77_output1c, subtractor256bit_77_output1d, subtractor256bit_78_output1a,
       subtractor256bit_78_output1b, subtractor256bit_78_output1c, subtractor256bit_78_output1d,
       subtractor256bit_79_output1a, subtractor256bit_79_output1b, subtractor256bit_79_output1c,
       subtractor256bit_79_output1d, subtractor256bit_80_output1a, subtractor256bit_80_output1b,
       subtractor256bit_80_output1c, subtractor256bit_80_output1d, subtractor256bit_81_output1a,
       subtractor256bit_81_output1b, subtractor256bit_81_output1c, subtractor256bit_81_output1d,
       subtractor256bit_82_output1a, subtractor256bit_82_output1b, subtractor256bit_82_output1c,
       subtractor256bit_82_output1d, subtractor256bit_83_output1a, subtractor256bit_83_output1b,
       subtractor256bit_83_output1c, subtractor256bit_83_output1d, subtractor256bit_84_output1a,
       subtractor256bit_84_output1b, subtractor256bit_84_output1c, subtractor256bit_84_output1d,
       subtractor256bit_85_output1a, subtractor256bit_85_output1b, subtractor256bit_85_output1c,
       subtractor256bit_85_output1d, subtractor256bit_86_output1a, subtractor256bit_86_output1b,
       subtractor256bit_86_output1c, subtractor256bit_86_output1d, subtractor256bit_87_output1a,
       subtractor256bit_87_output1b, subtractor256bit_87_output1c, subtractor256bit_87_output1d,
       subtractor256bit_88_output1a, subtractor256bit_88_output1b, subtractor256bit_88_output1c,
       subtractor256bit_88_output1d, subtractor256bit_89_output1a, subtractor256bit_89_output1b,
       subtractor256bit_89_output1c, subtractor256bit_89_output1d, subtractor256bit_90_output1a,
       subtractor256bit_90_output1b, subtractor256bit_90_output1c, subtractor256bit_90_output1d,
       subtractor256bit_91_output1a, subtractor256bit_91_output1b, subtractor256bit_91_output1c,
       subtractor256bit_91_output1d, subtractor256bit_92_output1a, subtractor256bit_92_output1b,
       subtractor256bit_92_output1c, subtractor256bit_92_output1d, subtractor256bit_93_output1a,
       subtractor256bit_93_output1b, subtractor256bit_93_output1c, subtractor256bit_93_output1d,
       subtractor256bit_94_output1a, subtractor256bit_94_output1b, subtractor256bit_94_output1c,
       subtractor256bit_94_output1d, subtractor256bit_95_output1a, subtractor256bit_95_output1b,
       subtractor256bit_95_output1c, subtractor256bit_95_output1d, subtractor256bit_96_output1a,
       subtractor256bit_96_output1b, subtractor256bit_96_output1c, subtractor256bit_96_output1d,
       subtractor256bit_97_output1a, subtractor256bit_97_output1b, subtractor256bit_97_output1c,
       subtractor256bit_97_output1d, subtractor256bit_98_output1a, subtractor256bit_98_output1b,
       subtractor256bit_98_output1c, subtractor256bit_98_output1d, subtractor256bit_99_output1a,
       subtractor256bit_99_output1b, subtractor256bit_99_output1c, subtractor256bit_99_output1d,
       subtractor256bit_100_output1a, subtractor256bit_100_output1b, subtractor256bit_100_output1c,
       subtractor256bit_100_output1d, subtractor256bit_101_output1a, subtractor256bit_101_output1b,
       subtractor256bit_101_output1c, subtractor256bit_101_output1d, subtractor256bit_102_output1a,
       subtractor256bit_102_output1b, subtractor256bit_102_output1c, subtractor256bit_102_output1d,
       subtractor256bit_103_output1a, subtractor256bit_103_output1b, subtractor256bit_103_output1c,
       subtractor256bit_103_output1d, subtractor256bit_104_output1a, subtractor256bit_104_output1b,
       subtractor256bit_104_output1c, subtractor256bit_104_output1d, subtractor256bit_105_output1a,
       subtractor256bit_105_output1b, subtractor256bit_105_output1c, subtractor256bit_105_output1d,
       subtractor256bit_106_output1a, subtractor256bit_106_output1b, subtractor256bit_106_output1c,
       subtractor256bit_106_output1d, subtractor256bit_107_output1a, subtractor256bit_107_output1b,
       subtractor256bit_107_output1c, subtractor256bit_107_output1d, subtractor256bit_108_output1a,
       subtractor256bit_108_output1b, subtractor256bit_108_output1c, subtractor256bit_108_output1d,
       subtractor256bit_109_output1a, subtractor256bit_109_output1b, subtractor256bit_109_output1c,
       subtractor256bit_109_output1d, subtractor256bit_110_output1a, subtractor256bit_110_output1b,
       subtractor256bit_110_output1c, subtractor256bit_110_output1d, subtractor256bit_111_output1a,
       subtractor256bit_111_output1b, subtractor256bit_111_output1c, subtractor256bit_111_output1d,
       subtractor256bit_112_output1a, subtractor256bit_112_output1b, subtractor256bit_112_output1c,
       subtractor256bit_112_output1d, subtractor256bit_113_output1a, subtractor256bit_113_output1b,
       subtractor256bit_113_output1c, subtractor256bit_113_output1d, subtractor256bit_114_output1a,
       subtractor256bit_114_output1b, subtractor256bit_114_output1c, subtractor256bit_114_output1d,
       subtractor256bit_115_output1a, subtractor256bit_115_output1b, subtractor256bit_115_output1c,
       subtractor256bit_115_output1d, subtractor256bit_116_output1a, subtractor256bit_116_output1b,
       subtractor256bit_116_output1c, subtractor256bit_116_output1d, subtractor256bit_117_output1a,
       subtractor256bit_117_output1b, subtractor256bit_117_output1c, subtractor256bit_117_output1d,
       subtractor256bit_118_output1a, subtractor256bit_118_output1b, subtractor256bit_118_output1c,
       subtractor256bit_118_output1d, subtractor256bit_119_output1a, subtractor256bit_119_output1b,
       subtractor256bit_119_output1c, subtractor256bit_119_output1d, subtractor256bit_120_output1a,
       subtractor256bit_120_output1b, subtractor256bit_120_output1c, subtractor256bit_120_output1d,
       subtractor256bit_121_output1a, subtractor256bit_121_output1b, subtractor256bit_121_output1c,
       subtractor256bit_121_output1d, subtractor256bit_122_output1a, subtractor256bit_122_output1b,
       subtractor256bit_122_output1c, subtractor256bit_122_output1d, subtractor256bit_123_output1a,
       subtractor256bit_123_output1b, subtractor256bit_123_output1c, subtractor256bit_123_output1d,
       subtractor256bit_124_output1a, subtractor256bit_124_output1b, subtractor256bit_124_output1c,
       subtractor256bit_124_output1d, subtractor256bit_125_output1a, subtractor256bit_125_output1b,
       subtractor256bit_125_output1c, subtractor256bit_125_output1d, subtractor256bit_126_output1a,
       subtractor256bit_126_output1b, subtractor256bit_126_output1c, subtractor256bit_126_output1d,
       subtractor256bit_127_output1a, subtractor256bit_127_output1b, subtractor256bit_127_output1c,
       subtractor256bit_127_output1d, subtractor256bit_128_output1b, subtractor256bit_128_output1c,
       subtractor256bit_128_output1d;

  // Probe on divider_1_out
  // Probe on divider_1_out
  Divider #(.width(64)) divider_1 (.a(input1), .b(input2), .out(divider_1_out), .upper(inupper), .rem(divider_1_rem));
  // Probe on divider_1_rem
  // Probe on divider_1_rem
  // Probe on input2
  // Probe on input2
  // Probe on inupper
  // Probe on inupper
  // Probe on input1
  // Probe on input1
  not not_1 (not_1_out, comparatoru64bit_1_equal1);
  comparatoru64bit comparatoru64bit_1 (
    .input1(input2), .input2({64{1'b0}}), .equal1(comparatoru64bit_1_equal1));  // open: greater1, less1
  subtractor256bit subtractor256bit_1 (
    .input1a(input1), .input1b(inupper), .input1c({64{1'b0}}), .input1d({64{1'b0}}),
    .input2a(cbuffer256bit_1_output1a), .input2b(cbuffer256bit_1_output1b),
    .input2c(cbuffer256bit_1_output1c), .input2d(cbuffer256bit_1_output1d),
    .output1a(subtractor256bit_1_output1a), .output1b(subtractor256bit_1_output1b),
    .output1c(subtractor256bit_1_output1c), .output1d(subtractor256bit_1_output1d));  // open: inborrow, borrow
  cbuffer256bit cbuffer256bit_1 (
    .buffer1(and_127_out[63]), .input1a({64{1'b0}}), .input1b({input2[0], {63{1'b0}}}),
    .input1c({1'b0, input2[63:1]}), .input1d({64{1'b0}}), .output1a(cbuffer256bit_1_output1a),
    .output1b(cbuffer256bit_1_output1b), .output1c(cbuffer256bit_1_output1c),
    .output1d(cbuffer256bit_1_output1d));
  and and_1 (and_127_out[63], not_1_out, or_1_out);
  or or_1 (or_1_out, comparatoru256bit_1_greater1, comparatoru256bit_1_equal1);
  comparatoru256bit comparatoru256bit_1 (
    .input1a(input1), .input1b(inupper), .input1c({64{1'b0}}), .input1d({64{1'b0}}), .input2a({64{1'b0}}),
    .input2b({input2[0], {63{1'b0}}}), .input2c({1'b0, input2[63:1]}), .input2d({64{1'b0}}),
    .greater1(comparatoru256bit_1_greater1), .equal1(comparatoru256bit_1_equal1));  // open: less1
  subtractor256bit subtractor256bit_2 (
    .input1a(subtractor256bit_127_output1a), .input1b(subtractor256bit_127_output1b),
    .input1c(subtractor256bit_127_output1c), .input1d(subtractor256bit_127_output1d),
    .input2a(cbuffer256bit_2_output1a), .input2b(cbuffer256bit_2_output1b),
    .input2c(cbuffer256bit_2_output1c), .input2d(cbuffer256bit_2_output1d),
    .output1a(subtractor256bit_2_output1a), .output1b(subtractor256bit_2_output1b),
    .output1c(subtractor256bit_2_output1c), .output1d(subtractor256bit_2_output1d));  // open: inborrow, borrow
  cbuffer256bit cbuffer256bit_2 (
    .buffer1(output1[63]), .input1a({input2[0], {63{1'b0}}}), .input1b({1'b0, input2[63:1]}),
    .input1c({64{1'b0}}), .input1d({64{1'b0}}), .output1a(cbuffer256bit_2_output1a),
    .output1b(cbuffer256bit_2_output1b), .output1c(cbuffer256bit_2_output1c),
    .output1d(cbuffer256bit_2_output1d));
  and and_2 (output1[63], not_1_out, or_2_out);
  or or_2 (or_2_out, comparatoru256bit_2_greater1, comparatoru256bit_2_equal1);
  comparatoru256bit comparatoru256bit_2 (
    .input1a(subtractor256bit_127_output1a), .input1b(subtractor256bit_127_output1b),
    .input1c(subtractor256bit_127_output1c), .input1d(subtractor256bit_127_output1d),
    .input2a({input2[0], {63{1'b0}}}), .input2b({1'b0, input2[63:1]}), .input2c({64{1'b0}}),
    .input2d({64{1'b0}}), .greater1(comparatoru256bit_2_greater1), .equal1(comparatoru256bit_2_equal1));  // open: less1
  subtractor256bit subtractor256bit_3 (
    .input1a(subtractor256bit_1_output1a), .input1b(subtractor256bit_1_output1b),
    .input1c(subtractor256bit_1_output1c), .input1d(subtractor256bit_1_output1d),
    .input2a(cbuffer256bit_3_output1a), .input2b(cbuffer256bit_3_output1b),
    .input2c(cbuffer256bit_3_output1c), .input2d(cbuffer256bit_3_output1d),
    .output1a(subtractor256bit_3_output1a), .output1b(subtractor256bit_3_output1b),
    .output1c(subtractor256bit_3_output1c), .output1d(subtractor256bit_3_output1d));  // open: inborrow, borrow
  cbuffer256bit cbuffer256bit_3 (
    .buffer1(and_127_out[62]), .input1a({64{1'b0}}), .input1b({input2[1:0], {62{1'b0}}}),
    .input1c({2'b00, input2[63:2]}), .input1d({64{1'b0}}), .output1a(cbuffer256bit_3_output1a),
    .output1b(cbuffer256bit_3_output1b), .output1c(cbuffer256bit_3_output1c),
    .output1d(cbuffer256bit_3_output1d));
  and and_3 (and_127_out[62], not_1_out, or_3_out);
  or or_3 (or_3_out, comparatoru256bit_3_greater1, comparatoru256bit_3_equal1);
  comparatoru256bit comparatoru256bit_3 (
    .input1a(subtractor256bit_1_output1a), .input1b(subtractor256bit_1_output1b),
    .input1c(subtractor256bit_1_output1c), .input1d(subtractor256bit_1_output1d), .input2a({64{1'b0}}),
    .input2b({input2[1:0], {62{1'b0}}}), .input2c({2'b00, input2[63:2]}), .input2d({64{1'b0}}),
    .greater1(comparatoru256bit_3_greater1), .equal1(comparatoru256bit_3_equal1));  // open: less1
  subtractor256bit subtractor256bit_4 (
    .input1a(subtractor256bit_2_output1a), .input1b(subtractor256bit_2_output1b),
    .input1c(subtractor256bit_2_output1c), .input1d(subtractor256bit_2_output1d),
    .input2a(cbuffer256bit_4_output1a), .input2b(cbuffer256bit_4_output1b),
    .input2c(cbuffer256bit_4_output1c), .input2d(cbuffer256bit_4_output1d),
    .output1a(subtractor256bit_4_output1a), .output1b(subtractor256bit_4_output1b),
    .output1c(subtractor256bit_4_output1c), .output1d(subtractor256bit_4_output1d));  // open: inborrow, borrow
  cbuffer256bit cbuffer256bit_4 (
    .buffer1(output1[62]), .input1a({input2[1:0], {62{1'b0}}}), .input1b({2'b00, input2[63:2]}),
    .input1c({64{1'b0}}), .input1d({64{1'b0}}), .output1a(cbuffer256bit_4_output1a),
    .output1b(cbuffer256bit_4_output1b), .output1c(cbuffer256bit_4_output1c),
    .output1d(cbuffer256bit_4_output1d));
  and and_4 (output1[62], not_1_out, or_4_out);
  comparatoru256bit comparatoru256bit_4 (
    .input1a(subtractor256bit_2_output1a), .input1b(subtractor256bit_2_output1b),
    .input1c(subtractor256bit_2_output1c), .input1d(subtractor256bit_2_output1d),
    .input2a({input2[1:0], {62{1'b0}}}), .input2b({2'b00, input2[63:2]}), .input2c({64{1'b0}}),
    .input2d({64{1'b0}}), .greater1(comparatoru256bit_4_greater1), .equal1(comparatoru256bit_4_equal1));  // open: less1
  or or_4 (or_4_out, comparatoru256bit_4_greater1, comparatoru256bit_4_equal1);
  subtractor256bit subtractor256bit_5 (
    .input1a(subtractor256bit_3_output1a), .input1b(subtractor256bit_3_output1b),
    .input1c(subtractor256bit_3_output1c), .input1d(subtractor256bit_3_output1d),
    .input2a(cbuffer256bit_5_output1a), .input2b(cbuffer256bit_5_output1b),
    .input2c(cbuffer256bit_5_output1c), .input2d(cbuffer256bit_5_output1d),
    .output1a(subtractor256bit_5_output1a), .output1b(subtractor256bit_5_output1b),
    .output1c(subtractor256bit_5_output1c), .output1d(subtractor256bit_5_output1d));  // open: inborrow, borrow
  cbuffer256bit cbuffer256bit_5 (
    .buffer1(and_127_out[61]), .input1a({64{1'b0}}), .input1b({input2[2:0], {61{1'b0}}}),
    .input1c({3'b000, input2[63:3]}), .input1d({64{1'b0}}), .output1a(cbuffer256bit_5_output1a),
    .output1b(cbuffer256bit_5_output1b), .output1c(cbuffer256bit_5_output1c),
    .output1d(cbuffer256bit_5_output1d));
  and and_5 (and_127_out[61], not_1_out, or_5_out);
  or or_5 (or_5_out, comparatoru256bit_5_greater1, comparatoru256bit_5_equal1);
  comparatoru256bit comparatoru256bit_5 (
    .input1a(subtractor256bit_3_output1a), .input1b(subtractor256bit_3_output1b),
    .input1c(subtractor256bit_3_output1c), .input1d(subtractor256bit_3_output1d), .input2a({64{1'b0}}),
    .input2b({input2[2:0], {61{1'b0}}}), .input2c({3'b000, input2[63:3]}), .input2d({64{1'b0}}),
    .greater1(comparatoru256bit_5_greater1), .equal1(comparatoru256bit_5_equal1));  // open: less1
  subtractor256bit subtractor256bit_6 (
    .input1a(subtractor256bit_4_output1a), .input1b(subtractor256bit_4_output1b),
    .input1c(subtractor256bit_4_output1c), .input1d(subtractor256bit_4_output1d),
    .input2a(cbuffer256bit_6_output1a), .input2b(cbuffer256bit_6_output1b),
    .input2c(cbuffer256bit_6_output1c), .input2d(cbuffer256bit_6_output1d),
    .output1a(subtractor256bit_6_output1a), .output1b(subtractor256bit_6_output1b),
    .output1c(subtractor256bit_6_output1c), .output1d(subtractor256bit_6_output1d));  // open: inborrow, borrow
  cbuffer256bit cbuffer256bit_6 (
    .buffer1(output1[61]), .input1a({input2[2:0], {61{1'b0}}}), .input1b({3'b000, input2[63:3]}),
    .input1c({64{1'b0}}), .input1d({64{1'b0}}), .output1a(cbuffer256bit_6_output1a),
    .output1b(cbuffer256bit_6_output1b), .output1c(cbuffer256bit_6_output1c),
    .output1d(cbuffer256bit_6_output1d));
  and and_6 (output1[61], not_1_out, or_6_out);
  or or_6 (or_6_out, comparatoru256bit_6_greater1, comparatoru256bit_6_equal1);
  comparatoru256bit comparatoru256bit_6 (
    .input1a(subtractor256bit_4_output1a), .input1b(subtractor256bit_4_output1b),
    .input1c(subtractor256bit_4_output1c), .input1d(subtractor256bit_4_output1d),
    .input2a({input2[2:0], {61{1'b0}}}), .input2b({3'b000, input2[63:3]}), .input2c({64{1'b0}}),
    .input2d({64{1'b0}}), .greater1(comparatoru256bit_6_greater1), .equal1(comparatoru256bit_6_equal1));  // open: less1
  subtractor256bit subtractor256bit_7 (
    .input1a(subtractor256bit_5_output1a), .input1b(subtractor256bit_5_output1b),
    .input1c(subtractor256bit_5_output1c), .input1d(subtractor256bit_5_output1d),
    .input2a(cbuffer256bit_7_output1a), .input2b(cbuffer256bit_7_output1b),
    .input2c(cbuffer256bit_7_output1c), .input2d(cbuffer256bit_7_output1d),
    .output1a(subtractor256bit_7_output1a), .output1b(subtractor256bit_7_output1b),
    .output1c(subtractor256bit_7_output1c), .output1d(subtractor256bit_7_output1d));  // open: inborrow, borrow
  cbuffer256bit cbuffer256bit_7 (
    .buffer1(and_127_out[60]), .input1a({64{1'b0}}), .input1b({input2[3:0], {60{1'b0}}}),
    .input1c({4'b0000, input2[63:4]}), .input1d({64{1'b0}}), .output1a(cbuffer256bit_7_output1a),
    .output1b(cbuffer256bit_7_output1b), .output1c(cbuffer256bit_7_output1c),
    .output1d(cbuffer256bit_7_output1d));
  and and_7 (and_127_out[60], not_1_out, or_7_out);
  or or_7 (or_7_out, comparatoru256bit_7_greater1, comparatoru256bit_7_equal1);
  comparatoru256bit comparatoru256bit_7 (
    .input1a(subtractor256bit_5_output1a), .input1b(subtractor256bit_5_output1b),
    .input1c(subtractor256bit_5_output1c), .input1d(subtractor256bit_5_output1d), .input2a({64{1'b0}}),
    .input2b({input2[3:0], {60{1'b0}}}), .input2c({4'b0000, input2[63:4]}), .input2d({64{1'b0}}),
    .greater1(comparatoru256bit_7_greater1), .equal1(comparatoru256bit_7_equal1));  // open: less1
  subtractor256bit subtractor256bit_8 (
    .input1a(subtractor256bit_6_output1a), .input1b(subtractor256bit_6_output1b),
    .input1c(subtractor256bit_6_output1c), .input1d(subtractor256bit_6_output1d),
    .input2a(cbuffer256bit_8_output1a), .input2b(cbuffer256bit_8_output1b),
    .input2c(cbuffer256bit_8_output1c), .input2d(cbuffer256bit_8_output1d),
    .output1a(subtractor256bit_8_output1a), .output1b(subtractor256bit_8_output1b),
    .output1c(subtractor256bit_8_output1c), .output1d(subtractor256bit_8_output1d));  // open: inborrow, borrow
  cbuffer256bit cbuffer256bit_8 (
    .buffer1(output1[60]), .input1a({input2[3:0], {60{1'b0}}}), .input1b({4'b0000, input2[63:4]}),
    .input1c({64{1'b0}}), .input1d({64{1'b0}}), .output1a(cbuffer256bit_8_output1a),
    .output1b(cbuffer256bit_8_output1b), .output1c(cbuffer256bit_8_output1c),
    .output1d(cbuffer256bit_8_output1d));
  and and_8 (output1[60], not_1_out, or_8_out);
  or or_8 (or_8_out, comparatoru256bit_8_greater1, comparatoru256bit_8_equal1);
  comparatoru256bit comparatoru256bit_8 (
    .input1a(subtractor256bit_6_output1a), .input1b(subtractor256bit_6_output1b),
    .input1c(subtractor256bit_6_output1c), .input1d(subtractor256bit_6_output1d),
    .input2a({input2[3:0], {60{1'b0}}}), .input2b({4'b0000, input2[63:4]}), .input2c({64{1'b0}}),
    .input2d({64{1'b0}}), .greater1(comparatoru256bit_8_greater1), .equal1(comparatoru256bit_8_equal1));  // open: less1
  subtractor256bit subtractor256bit_9 (
    .input1a(subtractor256bit_7_output1a), .input1b(subtractor256bit_7_output1b),
    .input1c(subtractor256bit_7_output1c), .input1d(subtractor256bit_7_output1d),
    .input2a(cbuffer256bit_9_output1a), .input2b(cbuffer256bit_9_output1b),
    .input2c(cbuffer256bit_9_output1c), .input2d(cbuffer256bit_9_output1d),
    .output1a(subtractor256bit_9_output1a), .output1b(subtractor256bit_9_output1b),
    .output1c(subtractor256bit_9_output1c), .output1d(subtractor256bit_9_output1d));  // open: inborrow, borrow
  cbuffer256bit cbuffer256bit_9 (
    .buffer1(and_127_out[59]), .input1a({64{1'b0}}), .input1b({input2[4:0], {59{1'b0}}}),
    .input1c({{5{1'b0}}, input2[63:5]}), .input1d({64{1'b0}}), .output1a(cbuffer256bit_9_output1a),
    .output1b(cbuffer256bit_9_output1b), .output1c(cbuffer256bit_9_output1c),
    .output1d(cbuffer256bit_9_output1d));
  and and_9 (and_127_out[59], not_1_out, or_9_out);
  or or_9 (or_9_out, comparatoru256bit_9_greater1, comparatoru256bit_9_equal1);
  comparatoru256bit comparatoru256bit_9 (
    .input1a(subtractor256bit_7_output1a), .input1b(subtractor256bit_7_output1b),
    .input1c(subtractor256bit_7_output1c), .input1d(subtractor256bit_7_output1d), .input2a({64{1'b0}}),
    .input2b({input2[4:0], {59{1'b0}}}), .input2c({{5{1'b0}}, input2[63:5]}), .input2d({64{1'b0}}),
    .greater1(comparatoru256bit_9_greater1), .equal1(comparatoru256bit_9_equal1));  // open: less1
  subtractor256bit subtractor256bit_10 (
    .input1a(subtractor256bit_8_output1a), .input1b(subtractor256bit_8_output1b),
    .input1c(subtractor256bit_8_output1c), .input1d(subtractor256bit_8_output1d),
    .input2a(cbuffer256bit_10_output1a), .input2b(cbuffer256bit_10_output1b),
    .input2c(cbuffer256bit_10_output1c), .input2d(cbuffer256bit_10_output1d),
    .output1a(subtractor256bit_10_output1a), .output1b(subtractor256bit_10_output1b),
    .output1c(subtractor256bit_10_output1c), .output1d(subtractor256bit_10_output1d));  // open: inborrow, borrow
  cbuffer256bit cbuffer256bit_10 (
    .buffer1(output1[59]), .input1a({input2[4:0], {59{1'b0}}}), .input1b({{5{1'b0}}, input2[63:5]}),
    .input1c({64{1'b0}}), .input1d({64{1'b0}}), .output1a(cbuffer256bit_10_output1a),
    .output1b(cbuffer256bit_10_output1b), .output1c(cbuffer256bit_10_output1c),
    .output1d(cbuffer256bit_10_output1d));
  and and_10 (output1[59], not_1_out, or_10_out);
  or or_10 (or_10_out, comparatoru256bit_10_greater1, comparatoru256bit_10_equal1);
  comparatoru256bit comparatoru256bit_10 (
    .input1a(subtractor256bit_8_output1a), .input1b(subtractor256bit_8_output1b),
    .input1c(subtractor256bit_8_output1c), .input1d(subtractor256bit_8_output1d),
    .input2a({input2[4:0], {59{1'b0}}}), .input2b({{5{1'b0}}, input2[63:5]}), .input2c({64{1'b0}}),
    .input2d({64{1'b0}}), .greater1(comparatoru256bit_10_greater1), .equal1(comparatoru256bit_10_equal1));  // open: less1
  subtractor256bit subtractor256bit_11 (
    .input1a(subtractor256bit_9_output1a), .input1b(subtractor256bit_9_output1b),
    .input1c(subtractor256bit_9_output1c), .input1d(subtractor256bit_9_output1d),
    .input2a(cbuffer256bit_11_output1a), .input2b(cbuffer256bit_11_output1b),
    .input2c(cbuffer256bit_11_output1c), .input2d(cbuffer256bit_11_output1d),
    .output1a(subtractor256bit_11_output1a), .output1b(subtractor256bit_11_output1b),
    .output1c(subtractor256bit_11_output1c), .output1d(subtractor256bit_11_output1d));  // open: inborrow, borrow
  cbuffer256bit cbuffer256bit_11 (
    .buffer1(and_127_out[58]), .input1a({64{1'b0}}), .input1b({input2[5:0], {58{1'b0}}}),
    .input1c({{6{1'b0}}, input2[63:6]}), .input1d({64{1'b0}}), .output1a(cbuffer256bit_11_output1a),
    .output1b(cbuffer256bit_11_output1b), .output1c(cbuffer256bit_11_output1c),
    .output1d(cbuffer256bit_11_output1d));
  and and_11 (and_127_out[58], not_1_out, or_11_out);
  or or_11 (or_11_out, comparatoru256bit_11_greater1, comparatoru256bit_11_equal1);
  comparatoru256bit comparatoru256bit_11 (
    .input1a(subtractor256bit_9_output1a), .input1b(subtractor256bit_9_output1b),
    .input1c(subtractor256bit_9_output1c), .input1d(subtractor256bit_9_output1d), .input2a({64{1'b0}}),
    .input2b({input2[5:0], {58{1'b0}}}), .input2c({{6{1'b0}}, input2[63:6]}), .input2d({64{1'b0}}),
    .greater1(comparatoru256bit_11_greater1), .equal1(comparatoru256bit_11_equal1));  // open: less1
  subtractor256bit subtractor256bit_12 (
    .input1a(subtractor256bit_10_output1a), .input1b(subtractor256bit_10_output1b),
    .input1c(subtractor256bit_10_output1c), .input1d(subtractor256bit_10_output1d),
    .input2a(cbuffer256bit_12_output1a), .input2b(cbuffer256bit_12_output1b),
    .input2c(cbuffer256bit_12_output1c), .input2d(cbuffer256bit_12_output1d),
    .output1a(subtractor256bit_12_output1a), .output1b(subtractor256bit_12_output1b),
    .output1c(subtractor256bit_12_output1c), .output1d(subtractor256bit_12_output1d));  // open: inborrow, borrow
  cbuffer256bit cbuffer256bit_12 (
    .buffer1(output1[58]), .input1a({input2[5:0], {58{1'b0}}}), .input1b({{6{1'b0}}, input2[63:6]}),
    .input1c({64{1'b0}}), .input1d({64{1'b0}}), .output1a(cbuffer256bit_12_output1a),
    .output1b(cbuffer256bit_12_output1b), .output1c(cbuffer256bit_12_output1c),
    .output1d(cbuffer256bit_12_output1d));
  and and_12 (output1[58], not_1_out, or_12_out);
  or or_12 (or_12_out, comparatoru256bit_12_greater1, comparatoru256bit_12_equal1);
  comparatoru256bit comparatoru256bit_12 (
    .input1a(subtractor256bit_10_output1a), .input1b(subtractor256bit_10_output1b),
    .input1c(subtractor256bit_10_output1c), .input1d(subtractor256bit_10_output1d),
    .input2a({input2[5:0], {58{1'b0}}}), .input2b({{6{1'b0}}, input2[63:6]}), .input2c({64{1'b0}}),
    .input2d({64{1'b0}}), .greater1(comparatoru256bit_12_greater1), .equal1(comparatoru256bit_12_equal1));  // open: less1
  subtractor256bit subtractor256bit_13 (
    .input1a(subtractor256bit_11_output1a), .input1b(subtractor256bit_11_output1b),
    .input1c(subtractor256bit_11_output1c), .input1d(subtractor256bit_11_output1d),
    .input2a(cbuffer256bit_13_output1a), .input2b(cbuffer256bit_13_output1b),
    .input2c(cbuffer256bit_13_output1c), .input2d(cbuffer256bit_13_output1d),
    .output1a(subtractor256bit_13_output1a), .output1b(subtractor256bit_13_output1b),
    .output1c(subtractor256bit_13_output1c), .output1d(subtractor256bit_13_output1d));  // open: inborrow, borrow
  cbuffer256bit cbuffer256bit_13 (
    .buffer1(and_127_out[57]), .input1a({64{1'b0}}), .input1b({input2[6:0], {57{1'b0}}}),
    .input1c({{7{1'b0}}, input2[63:7]}), .input1d({64{1'b0}}), .output1a(cbuffer256bit_13_output1a),
    .output1b(cbuffer256bit_13_output1b), .output1c(cbuffer256bit_13_output1c),
    .output1d(cbuffer256bit_13_output1d));
  and and_13 (and_127_out[57], not_1_out, or_13_out);
  comparatoru256bit comparatoru256bit_13 (
    .input1a(subtractor256bit_11_output1a), .input1b(subtractor256bit_11_output1b),
    .input1c(subtractor256bit_11_output1c), .input1d(subtractor256bit_11_output1d), .input2a({64{1'b0}}),
    .input2b({input2[6:0], {57{1'b0}}}), .input2c({{7{1'b0}}, input2[63:7]}), .input2d({64{1'b0}}),
    .greater1(comparatoru256bit_13_greater1), .equal1(comparatoru256bit_13_equal1));  // open: less1
  subtractor256bit subtractor256bit_14 (
    .input1a(subtractor256bit_12_output1a), .input1b(subtractor256bit_12_output1b),
    .input1c(subtractor256bit_12_output1c), .input1d(subtractor256bit_12_output1d),
    .input2a(cbuffer256bit_14_output1a), .input2b(cbuffer256bit_14_output1b),
    .input2c(cbuffer256bit_14_output1c), .input2d(cbuffer256bit_14_output1d),
    .output1a(subtractor256bit_14_output1a), .output1b(subtractor256bit_14_output1b),
    .output1c(subtractor256bit_14_output1c), .output1d(subtractor256bit_14_output1d));  // open: inborrow, borrow
  cbuffer256bit cbuffer256bit_14 (
    .buffer1(output1[57]), .input1a({input2[6:0], {57{1'b0}}}), .input1b({{7{1'b0}}, input2[63:7]}),
    .input1c({64{1'b0}}), .input1d({64{1'b0}}), .output1a(cbuffer256bit_14_output1a),
    .output1b(cbuffer256bit_14_output1b), .output1c(cbuffer256bit_14_output1c),
    .output1d(cbuffer256bit_14_output1d));
  and and_14 (output1[57], not_1_out, or_14_out);
  or or_13 (or_13_out, comparatoru256bit_13_greater1, comparatoru256bit_13_equal1);
  or or_14 (or_14_out, comparatoru256bit_14_greater1, comparatoru256bit_14_equal1);
  comparatoru256bit comparatoru256bit_14 (
    .input1a(subtractor256bit_12_output1a), .input1b(subtractor256bit_12_output1b),
    .input1c(subtractor256bit_12_output1c), .input1d(subtractor256bit_12_output1d),
    .input2a({input2[6:0], {57{1'b0}}}), .input2b({{7{1'b0}}, input2[63:7]}), .input2c({64{1'b0}}),
    .input2d({64{1'b0}}), .greater1(comparatoru256bit_14_greater1), .equal1(comparatoru256bit_14_equal1));  // open: less1
  subtractor256bit subtractor256bit_15 (
    .input1a(subtractor256bit_13_output1a), .input1b(subtractor256bit_13_output1b),
    .input1c(subtractor256bit_13_output1c), .input1d(subtractor256bit_13_output1d),
    .input2a(cbuffer256bit_15_output1a), .input2b(cbuffer256bit_15_output1b),
    .input2c(cbuffer256bit_15_output1c), .input2d(cbuffer256bit_15_output1d),
    .output1a(subtractor256bit_15_output1a), .output1b(subtractor256bit_15_output1b),
    .output1c(subtractor256bit_15_output1c), .output1d(subtractor256bit_15_output1d));  // open: inborrow, borrow
  cbuffer256bit cbuffer256bit_15 (
    .buffer1(and_127_out[56]), .input1a({64{1'b0}}), .input1b({input2[7:0], {56{1'b0}}}),
    .input1c({{8{1'b0}}, input2[63:8]}), .input1d({64{1'b0}}), .output1a(cbuffer256bit_15_output1a),
    .output1b(cbuffer256bit_15_output1b), .output1c(cbuffer256bit_15_output1c),
    .output1d(cbuffer256bit_15_output1d));
  and and_15 (and_127_out[56], not_1_out, or_15_out);
  or or_15 (or_15_out, comparatoru256bit_15_greater1, comparatoru256bit_15_equal1);
  comparatoru256bit comparatoru256bit_15 (
    .input1a(subtractor256bit_13_output1a), .input1b(subtractor256bit_13_output1b),
    .input1c(subtractor256bit_13_output1c), .input1d(subtractor256bit_13_output1d), .input2a({64{1'b0}}),
    .input2b({input2[7:0], {56{1'b0}}}), .input2c({{8{1'b0}}, input2[63:8]}), .input2d({64{1'b0}}),
    .greater1(comparatoru256bit_15_greater1), .equal1(comparatoru256bit_15_equal1));  // open: less1
  subtractor256bit subtractor256bit_16 (
    .input1a(subtractor256bit_14_output1a), .input1b(subtractor256bit_14_output1b),
    .input1c(subtractor256bit_14_output1c), .input1d(subtractor256bit_14_output1d),
    .input2a(cbuffer256bit_16_output1a), .input2b(cbuffer256bit_16_output1b),
    .input2c(cbuffer256bit_16_output1c), .input2d(cbuffer256bit_16_output1d),
    .output1a(subtractor256bit_16_output1a), .output1b(subtractor256bit_16_output1b),
    .output1c(subtractor256bit_16_output1c), .output1d(subtractor256bit_16_output1d));  // open: inborrow, borrow
  cbuffer256bit cbuffer256bit_16 (
    .buffer1(output1[56]), .input1a({input2[7:0], {56{1'b0}}}), .input1b({{8{1'b0}}, input2[63:8]}),
    .input1c({64{1'b0}}), .input1d({64{1'b0}}), .output1a(cbuffer256bit_16_output1a),
    .output1b(cbuffer256bit_16_output1b), .output1c(cbuffer256bit_16_output1c),
    .output1d(cbuffer256bit_16_output1d));
  and and_16 (output1[56], not_1_out, or_16_out);
  or or_16 (or_16_out, comparatoru256bit_16_greater1, comparatoru256bit_16_equal1);
  comparatoru256bit comparatoru256bit_16 (
    .input1a(subtractor256bit_14_output1a), .input1b(subtractor256bit_14_output1b),
    .input1c(subtractor256bit_14_output1c), .input1d(subtractor256bit_14_output1d),
    .input2a({input2[7:0], {56{1'b0}}}), .input2b({{8{1'b0}}, input2[63:8]}), .input2c({64{1'b0}}),
    .input2d({64{1'b0}}), .greater1(comparatoru256bit_16_greater1), .equal1(comparatoru256bit_16_equal1));  // open: less1
  subtractor256bit subtractor256bit_17 (
    .input1a(subtractor256bit_15_output1a), .input1b(subtractor256bit_15_output1b),
    .input1c(subtractor256bit_15_output1c), .input1d(subtractor256bit_15_output1d),
    .input2a(cbuffer256bit_17_output1a), .input2b(cbuffer256bit_17_output1b),
    .input2c(cbuffer256bit_17_output1c), .input2d(cbuffer256bit_17_output1d),
    .output1a(subtractor256bit_17_output1a), .output1b(subtractor256bit_17_output1b),
    .output1c(subtractor256bit_17_output1c), .output1d(subtractor256bit_17_output1d));  // open: inborrow, borrow
  cbuffer256bit cbuffer256bit_17 (
    .buffer1(and_127_out[55]), .input1a({64{1'b0}}), .input1b({input2[8:0], {55{1'b0}}}),
    .input1c({{9{1'b0}}, input2[63:9]}), .input1d({64{1'b0}}), .output1a(cbuffer256bit_17_output1a),
    .output1b(cbuffer256bit_17_output1b), .output1c(cbuffer256bit_17_output1c),
    .output1d(cbuffer256bit_17_output1d));
  and and_17 (and_127_out[55], not_1_out, or_17_out);
  or or_17 (or_17_out, comparatoru256bit_17_greater1, comparatoru256bit_17_equal1);
  comparatoru256bit comparatoru256bit_17 (
    .input1a(subtractor256bit_15_output1a), .input1b(subtractor256bit_15_output1b),
    .input1c(subtractor256bit_15_output1c), .input1d(subtractor256bit_15_output1d), .input2a({64{1'b0}}),
    .input2b({input2[8:0], {55{1'b0}}}), .input2c({{9{1'b0}}, input2[63:9]}), .input2d({64{1'b0}}),
    .greater1(comparatoru256bit_17_greater1), .equal1(comparatoru256bit_17_equal1));  // open: less1
  subtractor256bit subtractor256bit_18 (
    .input1a(subtractor256bit_16_output1a), .input1b(subtractor256bit_16_output1b),
    .input1c(subtractor256bit_16_output1c), .input1d(subtractor256bit_16_output1d),
    .input2a(cbuffer256bit_18_output1a), .input2b(cbuffer256bit_18_output1b),
    .input2c(cbuffer256bit_18_output1c), .input2d(cbuffer256bit_18_output1d),
    .output1a(subtractor256bit_18_output1a), .output1b(subtractor256bit_18_output1b),
    .output1c(subtractor256bit_18_output1c), .output1d(subtractor256bit_18_output1d));  // open: inborrow, borrow
  cbuffer256bit cbuffer256bit_18 (
    .buffer1(output1[55]), .input1a({input2[8:0], {55{1'b0}}}), .input1b({{9{1'b0}}, input2[63:9]}),
    .input1c({64{1'b0}}), .input1d({64{1'b0}}), .output1a(cbuffer256bit_18_output1a),
    .output1b(cbuffer256bit_18_output1b), .output1c(cbuffer256bit_18_output1c),
    .output1d(cbuffer256bit_18_output1d));
  and and_18 (output1[55], not_1_out, or_18_out);
  or or_18 (or_18_out, comparatoru256bit_18_greater1, comparatoru256bit_18_equal1);
  comparatoru256bit comparatoru256bit_18 (
    .input1a(subtractor256bit_16_output1a), .input1b(subtractor256bit_16_output1b),
    .input1c(subtractor256bit_16_output1c), .input1d(subtractor256bit_16_output1d),
    .input2a({input2[8:0], {55{1'b0}}}), .input2b({{9{1'b0}}, input2[63:9]}), .input2c({64{1'b0}}),
    .input2d({64{1'b0}}), .greater1(comparatoru256bit_18_greater1), .equal1(comparatoru256bit_18_equal1));  // open: less1
  subtractor256bit subtractor256bit_19 (
    .input1a(subtractor256bit_17_output1a), .input1b(subtractor256bit_17_output1b),
    .input1c(subtractor256bit_17_output1c), .input1d(subtractor256bit_17_output1d),
    .input2a(cbuffer256bit_19_output1a), .input2b(cbuffer256bit_19_output1b),
    .input2c(cbuffer256bit_19_output1c), .input2d(cbuffer256bit_19_output1d),
    .output1a(subtractor256bit_19_output1a), .output1b(subtractor256bit_19_output1b),
    .output1c(subtractor256bit_19_output1c), .output1d(subtractor256bit_19_output1d));  // open: inborrow, borrow
  cbuffer256bit cbuffer256bit_19 (
    .buffer1(and_127_out[54]), .input1a({64{1'b0}}), .input1b({input2[9:0], {54{1'b0}}}),
    .input1c({{10{1'b0}}, input2[63:10]}), .input1d({64{1'b0}}), .output1a(cbuffer256bit_19_output1a),
    .output1b(cbuffer256bit_19_output1b), .output1c(cbuffer256bit_19_output1c),
    .output1d(cbuffer256bit_19_output1d));
  and and_19 (and_127_out[54], not_1_out, or_19_out);
  or or_19 (or_19_out, comparatoru256bit_19_greater1, comparatoru256bit_19_equal1);
  comparatoru256bit comparatoru256bit_19 (
    .input1a(subtractor256bit_17_output1a), .input1b(subtractor256bit_17_output1b),
    .input1c(subtractor256bit_17_output1c), .input1d(subtractor256bit_17_output1d), .input2a({64{1'b0}}),
    .input2b({input2[9:0], {54{1'b0}}}), .input2c({{10{1'b0}}, input2[63:10]}), .input2d({64{1'b0}}),
    .greater1(comparatoru256bit_19_greater1), .equal1(comparatoru256bit_19_equal1));  // open: less1
  subtractor256bit subtractor256bit_20 (
    .input1a(subtractor256bit_18_output1a), .input1b(subtractor256bit_18_output1b),
    .input1c(subtractor256bit_18_output1c), .input1d(subtractor256bit_18_output1d),
    .input2a(cbuffer256bit_20_output1a), .input2b(cbuffer256bit_20_output1b),
    .input2c(cbuffer256bit_20_output1c), .input2d(cbuffer256bit_20_output1d),
    .output1a(subtractor256bit_20_output1a), .output1b(subtractor256bit_20_output1b),
    .output1c(subtractor256bit_20_output1c), .output1d(subtractor256bit_20_output1d));  // open: inborrow, borrow
  cbuffer256bit cbuffer256bit_20 (
    .buffer1(output1[54]), .input1a({input2[9:0], {54{1'b0}}}), .input1b({{10{1'b0}}, input2[63:10]}),
    .input1c({64{1'b0}}), .input1d({64{1'b0}}), .output1a(cbuffer256bit_20_output1a),
    .output1b(cbuffer256bit_20_output1b), .output1c(cbuffer256bit_20_output1c),
    .output1d(cbuffer256bit_20_output1d));
  and and_20 (output1[54], not_1_out, or_20_out);
  comparatoru256bit comparatoru256bit_20 (
    .input1a(subtractor256bit_18_output1a), .input1b(subtractor256bit_18_output1b),
    .input1c(subtractor256bit_18_output1c), .input1d(subtractor256bit_18_output1d),
    .input2a({input2[9:0], {54{1'b0}}}), .input2b({{10{1'b0}}, input2[63:10]}), .input2c({64{1'b0}}),
    .input2d({64{1'b0}}), .greater1(comparatoru256bit_20_greater1), .equal1(comparatoru256bit_20_equal1));  // open: less1
  or or_20 (or_20_out, comparatoru256bit_20_greater1, comparatoru256bit_20_equal1);
  subtractor256bit subtractor256bit_21 (
    .input1a(subtractor256bit_19_output1a), .input1b(subtractor256bit_19_output1b),
    .input1c(subtractor256bit_19_output1c), .input1d(subtractor256bit_19_output1d),
    .input2a(cbuffer256bit_21_output1a), .input2b(cbuffer256bit_21_output1b),
    .input2c(cbuffer256bit_21_output1c), .input2d(cbuffer256bit_21_output1d),
    .output1a(subtractor256bit_21_output1a), .output1b(subtractor256bit_21_output1b),
    .output1c(subtractor256bit_21_output1c), .output1d(subtractor256bit_21_output1d));  // open: inborrow, borrow
  cbuffer256bit cbuffer256bit_21 (
    .buffer1(and_127_out[53]), .input1a({64{1'b0}}), .input1b({input2[10:0], {53{1'b0}}}),
    .input1c({{11{1'b0}}, input2[63:11]}), .input1d({64{1'b0}}), .output1a(cbuffer256bit_21_output1a),
    .output1b(cbuffer256bit_21_output1b), .output1c(cbuffer256bit_21_output1c),
    .output1d(cbuffer256bit_21_output1d));
  and and_21 (and_127_out[53], not_1_out, or_21_out);
  or or_21 (or_21_out, comparatoru256bit_21_greater1, comparatoru256bit_21_equal1);
  comparatoru256bit comparatoru256bit_21 (
    .input1a(subtractor256bit_19_output1a), .input1b(subtractor256bit_19_output1b),
    .input1c(subtractor256bit_19_output1c), .input1d(subtractor256bit_19_output1d), .input2a({64{1'b0}}),
    .input2b({input2[10:0], {53{1'b0}}}), .input2c({{11{1'b0}}, input2[63:11]}), .input2d({64{1'b0}}),
    .greater1(comparatoru256bit_21_greater1), .equal1(comparatoru256bit_21_equal1));  // open: less1
  subtractor256bit subtractor256bit_22 (
    .input1a(subtractor256bit_20_output1a), .input1b(subtractor256bit_20_output1b),
    .input1c(subtractor256bit_20_output1c), .input1d(subtractor256bit_20_output1d),
    .input2a(cbuffer256bit_22_output1a), .input2b(cbuffer256bit_22_output1b),
    .input2c(cbuffer256bit_22_output1c), .input2d(cbuffer256bit_22_output1d),
    .output1a(subtractor256bit_22_output1a), .output1b(subtractor256bit_22_output1b),
    .output1c(subtractor256bit_22_output1c), .output1d(subtractor256bit_22_output1d));  // open: inborrow, borrow
  cbuffer256bit cbuffer256bit_22 (
    .buffer1(output1[53]), .input1a({input2[10:0], {53{1'b0}}}), .input1b({{11{1'b0}}, input2[63:11]}),
    .input1c({64{1'b0}}), .input1d({64{1'b0}}), .output1a(cbuffer256bit_22_output1a),
    .output1b(cbuffer256bit_22_output1b), .output1c(cbuffer256bit_22_output1c),
    .output1d(cbuffer256bit_22_output1d));
  and and_22 (output1[53], not_1_out, or_22_out);
  or or_22 (or_22_out, comparatoru256bit_22_greater1, comparatoru256bit_22_equal1);
  comparatoru256bit comparatoru256bit_22 (
    .input1a(subtractor256bit_20_output1a), .input1b(subtractor256bit_20_output1b),
    .input1c(subtractor256bit_20_output1c), .input1d(subtractor256bit_20_output1d),
    .input2a({input2[10:0], {53{1'b0}}}), .input2b({{11{1'b0}}, input2[63:11]}), .input2c({64{1'b0}}),
    .input2d({64{1'b0}}), .greater1(comparatoru256bit_22_greater1), .equal1(comparatoru256bit_22_equal1));  // open: less1
  subtractor256bit subtractor256bit_23 (
    .input1a(subtractor256bit_21_output1a), .input1b(subtractor256bit_21_output1b),
    .input1c(subtractor256bit_21_output1c), .input1d(subtractor256bit_21_output1d),
    .input2a(cbuffer256bit_23_output1a), .input2b(cbuffer256bit_23_output1b),
    .input2c(cbuffer256bit_23_output1c), .input2d(cbuffer256bit_23_output1d),
    .output1a(subtractor256bit_23_output1a), .output1b(subtractor256bit_23_output1b),
    .output1c(subtractor256bit_23_output1c), .output1d(subtractor256bit_23_output1d));  // open: inborrow, borrow
  cbuffer256bit cbuffer256bit_23 (
    .buffer1(and_127_out[52]), .input1a({64{1'b0}}), .input1b({input2[11:0], {52{1'b0}}}),
    .input1c({{12{1'b0}}, input2[63:12]}), .input1d({64{1'b0}}), .output1a(cbuffer256bit_23_output1a),
    .output1b(cbuffer256bit_23_output1b), .output1c(cbuffer256bit_23_output1c),
    .output1d(cbuffer256bit_23_output1d));
  and and_23 (and_127_out[52], not_1_out, or_23_out);
  or or_23 (or_23_out, comparatoru256bit_23_greater1, comparatoru256bit_23_equal1);
  comparatoru256bit comparatoru256bit_23 (
    .input1a(subtractor256bit_21_output1a), .input1b(subtractor256bit_21_output1b),
    .input1c(subtractor256bit_21_output1c), .input1d(subtractor256bit_21_output1d), .input2a({64{1'b0}}),
    .input2b({input2[11:0], {52{1'b0}}}), .input2c({{12{1'b0}}, input2[63:12]}), .input2d({64{1'b0}}),
    .greater1(comparatoru256bit_23_greater1), .equal1(comparatoru256bit_23_equal1));  // open: less1
  subtractor256bit subtractor256bit_24 (
    .input1a(subtractor256bit_22_output1a), .input1b(subtractor256bit_22_output1b),
    .input1c(subtractor256bit_22_output1c), .input1d(subtractor256bit_22_output1d),
    .input2a(cbuffer256bit_24_output1a), .input2b(cbuffer256bit_24_output1b),
    .input2c(cbuffer256bit_24_output1c), .input2d(cbuffer256bit_24_output1d),
    .output1a(subtractor256bit_24_output1a), .output1b(subtractor256bit_24_output1b),
    .output1c(subtractor256bit_24_output1c), .output1d(subtractor256bit_24_output1d));  // open: inborrow, borrow
  cbuffer256bit cbuffer256bit_24 (
    .buffer1(output1[52]), .input1a({input2[11:0], {52{1'b0}}}), .input1b({{12{1'b0}}, input2[63:12]}),
    .input1c({64{1'b0}}), .input1d({64{1'b0}}), .output1a(cbuffer256bit_24_output1a),
    .output1b(cbuffer256bit_24_output1b), .output1c(cbuffer256bit_24_output1c),
    .output1d(cbuffer256bit_24_output1d));
  and and_24 (output1[52], not_1_out, or_24_out);
  or or_24 (or_24_out, comparatoru256bit_24_greater1, comparatoru256bit_24_equal1);
  comparatoru256bit comparatoru256bit_24 (
    .input1a(subtractor256bit_22_output1a), .input1b(subtractor256bit_22_output1b),
    .input1c(subtractor256bit_22_output1c), .input1d(subtractor256bit_22_output1d),
    .input2a({input2[11:0], {52{1'b0}}}), .input2b({{12{1'b0}}, input2[63:12]}), .input2c({64{1'b0}}),
    .input2d({64{1'b0}}), .greater1(comparatoru256bit_24_greater1), .equal1(comparatoru256bit_24_equal1));  // open: less1
  subtractor256bit subtractor256bit_25 (
    .input1a(subtractor256bit_23_output1a), .input1b(subtractor256bit_23_output1b),
    .input1c(subtractor256bit_23_output1c), .input1d(subtractor256bit_23_output1d),
    .input2a(cbuffer256bit_25_output1a), .input2b(cbuffer256bit_25_output1b),
    .input2c(cbuffer256bit_25_output1c), .input2d(cbuffer256bit_25_output1d),
    .output1a(subtractor256bit_25_output1a), .output1b(subtractor256bit_25_output1b),
    .output1c(subtractor256bit_25_output1c), .output1d(subtractor256bit_25_output1d));  // open: inborrow, borrow
  cbuffer256bit cbuffer256bit_25 (
    .buffer1(and_127_out[51]), .input1a({64{1'b0}}), .input1b({input2[12:0], {51{1'b0}}}),
    .input1c({{13{1'b0}}, input2[63:13]}), .input1d({64{1'b0}}), .output1a(cbuffer256bit_25_output1a),
    .output1b(cbuffer256bit_25_output1b), .output1c(cbuffer256bit_25_output1c),
    .output1d(cbuffer256bit_25_output1d));
  and and_25 (and_127_out[51], not_1_out, or_25_out);
  or or_25 (or_25_out, comparatoru256bit_25_greater1, comparatoru256bit_25_equal1);
  comparatoru256bit comparatoru256bit_25 (
    .input1a(subtractor256bit_23_output1a), .input1b(subtractor256bit_23_output1b),
    .input1c(subtractor256bit_23_output1c), .input1d(subtractor256bit_23_output1d), .input2a({64{1'b0}}),
    .input2b({input2[12:0], {51{1'b0}}}), .input2c({{13{1'b0}}, input2[63:13]}), .input2d({64{1'b0}}),
    .greater1(comparatoru256bit_25_greater1), .equal1(comparatoru256bit_25_equal1));  // open: less1
  subtractor256bit subtractor256bit_26 (
    .input1a(subtractor256bit_24_output1a), .input1b(subtractor256bit_24_output1b),
    .input1c(subtractor256bit_24_output1c), .input1d(subtractor256bit_24_output1d),
    .input2a(cbuffer256bit_26_output1a), .input2b(cbuffer256bit_26_output1b),
    .input2c(cbuffer256bit_26_output1c), .input2d(cbuffer256bit_26_output1d),
    .output1a(subtractor256bit_26_output1a), .output1b(subtractor256bit_26_output1b),
    .output1c(subtractor256bit_26_output1c), .output1d(subtractor256bit_26_output1d));  // open: inborrow, borrow
  cbuffer256bit cbuffer256bit_26 (
    .buffer1(output1[51]), .input1a({input2[12:0], {51{1'b0}}}), .input1b({{13{1'b0}}, input2[63:13]}),
    .input1c({64{1'b0}}), .input1d({64{1'b0}}), .output1a(cbuffer256bit_26_output1a),
    .output1b(cbuffer256bit_26_output1b), .output1c(cbuffer256bit_26_output1c),
    .output1d(cbuffer256bit_26_output1d));
  and and_26 (output1[51], not_1_out, or_26_out);
  or or_26 (or_26_out, comparatoru256bit_26_greater1, comparatoru256bit_26_equal1);
  comparatoru256bit comparatoru256bit_26 (
    .input1a(subtractor256bit_24_output1a), .input1b(subtractor256bit_24_output1b),
    .input1c(subtractor256bit_24_output1c), .input1d(subtractor256bit_24_output1d),
    .input2a({input2[12:0], {51{1'b0}}}), .input2b({{13{1'b0}}, input2[63:13]}), .input2c({64{1'b0}}),
    .input2d({64{1'b0}}), .greater1(comparatoru256bit_26_greater1), .equal1(comparatoru256bit_26_equal1));  // open: less1
  subtractor256bit subtractor256bit_27 (
    .input1a(subtractor256bit_25_output1a), .input1b(subtractor256bit_25_output1b),
    .input1c(subtractor256bit_25_output1c), .input1d(subtractor256bit_25_output1d),
    .input2a(cbuffer256bit_27_output1a), .input2b(cbuffer256bit_27_output1b),
    .input2c(cbuffer256bit_27_output1c), .input2d(cbuffer256bit_27_output1d),
    .output1a(subtractor256bit_27_output1a), .output1b(subtractor256bit_27_output1b),
    .output1c(subtractor256bit_27_output1c), .output1d(subtractor256bit_27_output1d));  // open: inborrow, borrow
  cbuffer256bit cbuffer256bit_27 (
    .buffer1(and_127_out[50]), .input1a({64{1'b0}}), .input1b({input2[13:0], {50{1'b0}}}),
    .input1c({{14{1'b0}}, input2[63:14]}), .input1d({64{1'b0}}), .output1a(cbuffer256bit_27_output1a),
    .output1b(cbuffer256bit_27_output1b), .output1c(cbuffer256bit_27_output1c),
    .output1d(cbuffer256bit_27_output1d));
  and and_27 (and_127_out[50], not_1_out, or_27_out);
  or or_27 (or_27_out, comparatoru256bit_27_greater1, comparatoru256bit_27_equal1);
  comparatoru256bit comparatoru256bit_27 (
    .input1a(subtractor256bit_25_output1a), .input1b(subtractor256bit_25_output1b),
    .input1c(subtractor256bit_25_output1c), .input1d(subtractor256bit_25_output1d), .input2a({64{1'b0}}),
    .input2b({input2[13:0], {50{1'b0}}}), .input2c({{14{1'b0}}, input2[63:14]}), .input2d({64{1'b0}}),
    .greater1(comparatoru256bit_27_greater1), .equal1(comparatoru256bit_27_equal1));  // open: less1
  subtractor256bit subtractor256bit_28 (
    .input1a(subtractor256bit_26_output1a), .input1b(subtractor256bit_26_output1b),
    .input1c(subtractor256bit_26_output1c), .input1d(subtractor256bit_26_output1d),
    .input2a(cbuffer256bit_28_output1a), .input2b(cbuffer256bit_28_output1b),
    .input2c(cbuffer256bit_28_output1c), .input2d(cbuffer256bit_28_output1d),
    .output1a(subtractor256bit_28_output1a), .output1b(subtractor256bit_28_output1b),
    .output1c(subtractor256bit_28_output1c), .output1d(subtractor256bit_28_output1d));  // open: inborrow, borrow
  cbuffer256bit cbuffer256bit_28 (
    .buffer1(output1[50]), .input1a({input2[13:0], {50{1'b0}}}), .input1b({{14{1'b0}}, input2[63:14]}),
    .input1c({64{1'b0}}), .input1d({64{1'b0}}), .output1a(cbuffer256bit_28_output1a),
    .output1b(cbuffer256bit_28_output1b), .output1c(cbuffer256bit_28_output1c),
    .output1d(cbuffer256bit_28_output1d));
  and and_28 (output1[50], not_1_out, or_28_out);
  or or_28 (or_28_out, comparatoru256bit_28_greater1, comparatoru256bit_28_equal1);
  comparatoru256bit comparatoru256bit_28 (
    .input1a(subtractor256bit_26_output1a), .input1b(subtractor256bit_26_output1b),
    .input1c(subtractor256bit_26_output1c), .input1d(subtractor256bit_26_output1d),
    .input2a({input2[13:0], {50{1'b0}}}), .input2b({{14{1'b0}}, input2[63:14]}), .input2c({64{1'b0}}),
    .input2d({64{1'b0}}), .greater1(comparatoru256bit_28_greater1), .equal1(comparatoru256bit_28_equal1));  // open: less1
  subtractor256bit subtractor256bit_29 (
    .input1a(subtractor256bit_27_output1a), .input1b(subtractor256bit_27_output1b),
    .input1c(subtractor256bit_27_output1c), .input1d(subtractor256bit_27_output1d),
    .input2a(cbuffer256bit_29_output1a), .input2b(cbuffer256bit_29_output1b),
    .input2c(cbuffer256bit_29_output1c), .input2d(cbuffer256bit_29_output1d),
    .output1a(subtractor256bit_29_output1a), .output1b(subtractor256bit_29_output1b),
    .output1c(subtractor256bit_29_output1c), .output1d(subtractor256bit_29_output1d));  // open: inborrow, borrow
  cbuffer256bit cbuffer256bit_29 (
    .buffer1(and_127_out[49]), .input1a({64{1'b0}}), .input1b({input2[14:0], {49{1'b0}}}),
    .input1c({{15{1'b0}}, input2[63:15]}), .input1d({64{1'b0}}), .output1a(cbuffer256bit_29_output1a),
    .output1b(cbuffer256bit_29_output1b), .output1c(cbuffer256bit_29_output1c),
    .output1d(cbuffer256bit_29_output1d));
  and and_29 (and_127_out[49], not_1_out, or_29_out);
  comparatoru256bit comparatoru256bit_29 (
    .input1a(subtractor256bit_27_output1a), .input1b(subtractor256bit_27_output1b),
    .input1c(subtractor256bit_27_output1c), .input1d(subtractor256bit_27_output1d), .input2a({64{1'b0}}),
    .input2b({input2[14:0], {49{1'b0}}}), .input2c({{15{1'b0}}, input2[63:15]}), .input2d({64{1'b0}}),
    .greater1(comparatoru256bit_29_greater1), .equal1(comparatoru256bit_29_equal1));  // open: less1
  subtractor256bit subtractor256bit_30 (
    .input1a(subtractor256bit_28_output1a), .input1b(subtractor256bit_28_output1b),
    .input1c(subtractor256bit_28_output1c), .input1d(subtractor256bit_28_output1d),
    .input2a(cbuffer256bit_30_output1a), .input2b(cbuffer256bit_30_output1b),
    .input2c(cbuffer256bit_30_output1c), .input2d(cbuffer256bit_30_output1d),
    .output1a(subtractor256bit_30_output1a), .output1b(subtractor256bit_30_output1b),
    .output1c(subtractor256bit_30_output1c), .output1d(subtractor256bit_30_output1d));  // open: inborrow, borrow
  cbuffer256bit cbuffer256bit_30 (
    .buffer1(output1[49]), .input1a({input2[14:0], {49{1'b0}}}), .input1b({{15{1'b0}}, input2[63:15]}),
    .input1c({64{1'b0}}), .input1d({64{1'b0}}), .output1a(cbuffer256bit_30_output1a),
    .output1b(cbuffer256bit_30_output1b), .output1c(cbuffer256bit_30_output1c),
    .output1d(cbuffer256bit_30_output1d));
  and and_30 (output1[49], not_1_out, or_30_out);
  or or_29 (or_29_out, comparatoru256bit_29_greater1, comparatoru256bit_29_equal1);
  or or_30 (or_30_out, comparatoru256bit_30_greater1, comparatoru256bit_30_equal1);
  comparatoru256bit comparatoru256bit_30 (
    .input1a(subtractor256bit_28_output1a), .input1b(subtractor256bit_28_output1b),
    .input1c(subtractor256bit_28_output1c), .input1d(subtractor256bit_28_output1d),
    .input2a({input2[14:0], {49{1'b0}}}), .input2b({{15{1'b0}}, input2[63:15]}), .input2c({64{1'b0}}),
    .input2d({64{1'b0}}), .greater1(comparatoru256bit_30_greater1), .equal1(comparatoru256bit_30_equal1));  // open: less1
  subtractor256bit subtractor256bit_31 (
    .input1a(subtractor256bit_29_output1a), .input1b(subtractor256bit_29_output1b),
    .input1c(subtractor256bit_29_output1c), .input1d(subtractor256bit_29_output1d),
    .input2a(cbuffer256bit_31_output1a), .input2b(cbuffer256bit_31_output1b),
    .input2c(cbuffer256bit_31_output1c), .input2d(cbuffer256bit_31_output1d),
    .output1a(subtractor256bit_31_output1a), .output1b(subtractor256bit_31_output1b),
    .output1c(subtractor256bit_31_output1c), .output1d(subtractor256bit_31_output1d));  // open: inborrow, borrow
  cbuffer256bit cbuffer256bit_31 (
    .buffer1(and_127_out[48]), .input1a({64{1'b0}}), .input1b({input2[15:0], {48{1'b0}}}),
    .input1c({{16{1'b0}}, input2[63:16]}), .input1d({64{1'b0}}), .output1a(cbuffer256bit_31_output1a),
    .output1b(cbuffer256bit_31_output1b), .output1c(cbuffer256bit_31_output1c),
    .output1d(cbuffer256bit_31_output1d));
  and and_31 (and_127_out[48], not_1_out, or_31_out);
  or or_31 (or_31_out, comparatoru256bit_31_greater1, comparatoru256bit_31_equal1);
  comparatoru256bit comparatoru256bit_31 (
    .input1a(subtractor256bit_29_output1a), .input1b(subtractor256bit_29_output1b),
    .input1c(subtractor256bit_29_output1c), .input1d(subtractor256bit_29_output1d), .input2a({64{1'b0}}),
    .input2b({input2[15:0], {48{1'b0}}}), .input2c({{16{1'b0}}, input2[63:16]}), .input2d({64{1'b0}}),
    .greater1(comparatoru256bit_31_greater1), .equal1(comparatoru256bit_31_equal1));  // open: less1
  subtractor256bit subtractor256bit_32 (
    .input1a(subtractor256bit_30_output1a), .input1b(subtractor256bit_30_output1b),
    .input1c(subtractor256bit_30_output1c), .input1d(subtractor256bit_30_output1d),
    .input2a(cbuffer256bit_32_output1a), .input2b(cbuffer256bit_32_output1b),
    .input2c(cbuffer256bit_32_output1c), .input2d(cbuffer256bit_32_output1d),
    .output1a(subtractor256bit_32_output1a), .output1b(subtractor256bit_32_output1b),
    .output1c(subtractor256bit_32_output1c), .output1d(subtractor256bit_32_output1d));  // open: inborrow, borrow
  cbuffer256bit cbuffer256bit_32 (
    .buffer1(output1[48]), .input1a({input2[15:0], {48{1'b0}}}), .input1b({{16{1'b0}}, input2[63:16]}),
    .input1c({64{1'b0}}), .input1d({64{1'b0}}), .output1a(cbuffer256bit_32_output1a),
    .output1b(cbuffer256bit_32_output1b), .output1c(cbuffer256bit_32_output1c),
    .output1d(cbuffer256bit_32_output1d));
  and and_32 (output1[48], not_1_out, or_32_out);
  or or_32 (or_32_out, comparatoru256bit_32_greater1, comparatoru256bit_32_equal1);
  comparatoru256bit comparatoru256bit_32 (
    .input1a(subtractor256bit_30_output1a), .input1b(subtractor256bit_30_output1b),
    .input1c(subtractor256bit_30_output1c), .input1d(subtractor256bit_30_output1d),
    .input2a({input2[15:0], {48{1'b0}}}), .input2b({{16{1'b0}}, input2[63:16]}), .input2c({64{1'b0}}),
    .input2d({64{1'b0}}), .greater1(comparatoru256bit_32_greater1), .equal1(comparatoru256bit_32_equal1));  // open: less1
  subtractor256bit subtractor256bit_33 (
    .input1a(subtractor256bit_31_output1a), .input1b(subtractor256bit_31_output1b),
    .input1c(subtractor256bit_31_output1c), .input1d(subtractor256bit_31_output1d),
    .input2a(cbuffer256bit_33_output1a), .input2b(cbuffer256bit_33_output1b),
    .input2c(cbuffer256bit_33_output1c), .input2d(cbuffer256bit_33_output1d),
    .output1a(subtractor256bit_33_output1a), .output1b(subtractor256bit_33_output1b),
    .output1c(subtractor256bit_33_output1c), .output1d(subtractor256bit_33_output1d));  // open: inborrow, borrow
  cbuffer256bit cbuffer256bit_33 (
    .buffer1(and_127_out[47]), .input1a({64{1'b0}}), .input1b({input2[16:0], {47{1'b0}}}),
    .input1c({{17{1'b0}}, input2[63:17]}), .input1d({64{1'b0}}), .output1a(cbuffer256bit_33_output1a),
    .output1b(cbuffer256bit_33_output1b), .output1c(cbuffer256bit_33_output1c),
    .output1d(cbuffer256bit_33_output1d));
  and and_33 (and_127_out[47], not_1_out, or_33_out);
  or or_33 (or_33_out, comparatoru256bit_33_greater1, comparatoru256bit_33_equal1);
  comparatoru256bit comparatoru256bit_33 (
    .input1a(subtractor256bit_31_output1a), .input1b(subtractor256bit_31_output1b),
    .input1c(subtractor256bit_31_output1c), .input1d(subtractor256bit_31_output1d), .input2a({64{1'b0}}),
    .input2b({input2[16:0], {47{1'b0}}}), .input2c({{17{1'b0}}, input2[63:17]}), .input2d({64{1'b0}}),
    .greater1(comparatoru256bit_33_greater1), .equal1(comparatoru256bit_33_equal1));  // open: less1
  subtractor256bit subtractor256bit_34 (
    .input1a(subtractor256bit_32_output1a), .input1b(subtractor256bit_32_output1b),
    .input1c(subtractor256bit_32_output1c), .input1d(subtractor256bit_32_output1d),
    .input2a(cbuffer256bit_34_output1a), .input2b(cbuffer256bit_34_output1b),
    .input2c(cbuffer256bit_34_output1c), .input2d(cbuffer256bit_34_output1d),
    .output1a(subtractor256bit_34_output1a), .output1b(subtractor256bit_34_output1b),
    .output1c(subtractor256bit_34_output1c), .output1d(subtractor256bit_34_output1d));  // open: inborrow, borrow
  cbuffer256bit cbuffer256bit_34 (
    .buffer1(output1[47]), .input1a({input2[16:0], {47{1'b0}}}), .input1b({{17{1'b0}}, input2[63:17]}),
    .input1c({64{1'b0}}), .input1d({64{1'b0}}), .output1a(cbuffer256bit_34_output1a),
    .output1b(cbuffer256bit_34_output1b), .output1c(cbuffer256bit_34_output1c),
    .output1d(cbuffer256bit_34_output1d));
  and and_34 (output1[47], not_1_out, or_34_out);
  or or_34 (or_34_out, comparatoru256bit_34_greater1, comparatoru256bit_34_equal1);
  comparatoru256bit comparatoru256bit_34 (
    .input1a(subtractor256bit_32_output1a), .input1b(subtractor256bit_32_output1b),
    .input1c(subtractor256bit_32_output1c), .input1d(subtractor256bit_32_output1d),
    .input2a({input2[16:0], {47{1'b0}}}), .input2b({{17{1'b0}}, input2[63:17]}), .input2c({64{1'b0}}),
    .input2d({64{1'b0}}), .greater1(comparatoru256bit_34_greater1), .equal1(comparatoru256bit_34_equal1));  // open: less1
  subtractor256bit subtractor256bit_35 (
    .input1a(subtractor256bit_33_output1a), .input1b(subtractor256bit_33_output1b),
    .input1c(subtractor256bit_33_output1c), .input1d(subtractor256bit_33_output1d),
    .input2a(cbuffer256bit_35_output1a), .input2b(cbuffer256bit_35_output1b),
    .input2c(cbuffer256bit_35_output1c), .input2d(cbuffer256bit_35_output1d),
    .output1a(subtractor256bit_35_output1a), .output1b(subtractor256bit_35_output1b),
    .output1c(subtractor256bit_35_output1c), .output1d(subtractor256bit_35_output1d));  // open: inborrow, borrow
  cbuffer256bit cbuffer256bit_35 (
    .buffer1(and_127_out[46]), .input1a({64{1'b0}}), .input1b({input2[17:0], {46{1'b0}}}),
    .input1c({{18{1'b0}}, input2[63:18]}), .input1d({64{1'b0}}), .output1a(cbuffer256bit_35_output1a),
    .output1b(cbuffer256bit_35_output1b), .output1c(cbuffer256bit_35_output1c),
    .output1d(cbuffer256bit_35_output1d));
  and and_35 (and_127_out[46], not_1_out, or_35_out);
  or or_35 (or_35_out, comparatoru256bit_35_greater1, comparatoru256bit_35_equal1);
  comparatoru256bit comparatoru256bit_35 (
    .input1a(subtractor256bit_33_output1a), .input1b(subtractor256bit_33_output1b),
    .input1c(subtractor256bit_33_output1c), .input1d(subtractor256bit_33_output1d), .input2a({64{1'b0}}),
    .input2b({input2[17:0], {46{1'b0}}}), .input2c({{18{1'b0}}, input2[63:18]}), .input2d({64{1'b0}}),
    .greater1(comparatoru256bit_35_greater1), .equal1(comparatoru256bit_35_equal1));  // open: less1
  subtractor256bit subtractor256bit_36 (
    .input1a(subtractor256bit_34_output1a), .input1b(subtractor256bit_34_output1b),
    .input1c(subtractor256bit_34_output1c), .input1d(subtractor256bit_34_output1d),
    .input2a(cbuffer256bit_36_output1a), .input2b(cbuffer256bit_36_output1b),
    .input2c(cbuffer256bit_36_output1c), .input2d(cbuffer256bit_36_output1d),
    .output1a(subtractor256bit_36_output1a), .output1b(subtractor256bit_36_output1b),
    .output1c(subtractor256bit_36_output1c), .output1d(subtractor256bit_36_output1d));  // open: inborrow, borrow
  cbuffer256bit cbuffer256bit_36 (
    .buffer1(output1[46]), .input1a({input2[17:0], {46{1'b0}}}), .input1b({{18{1'b0}}, input2[63:18]}),
    .input1c({64{1'b0}}), .input1d({64{1'b0}}), .output1a(cbuffer256bit_36_output1a),
    .output1b(cbuffer256bit_36_output1b), .output1c(cbuffer256bit_36_output1c),
    .output1d(cbuffer256bit_36_output1d));
  and and_36 (output1[46], not_1_out, or_36_out);
  comparatoru256bit comparatoru256bit_36 (
    .input1a(subtractor256bit_34_output1a), .input1b(subtractor256bit_34_output1b),
    .input1c(subtractor256bit_34_output1c), .input1d(subtractor256bit_34_output1d),
    .input2a({input2[17:0], {46{1'b0}}}), .input2b({{18{1'b0}}, input2[63:18]}), .input2c({64{1'b0}}),
    .input2d({64{1'b0}}), .greater1(comparatoru256bit_36_greater1), .equal1(comparatoru256bit_36_equal1));  // open: less1
  or or_36 (or_36_out, comparatoru256bit_36_greater1, comparatoru256bit_36_equal1);
  subtractor256bit subtractor256bit_37 (
    .input1a(subtractor256bit_35_output1a), .input1b(subtractor256bit_35_output1b),
    .input1c(subtractor256bit_35_output1c), .input1d(subtractor256bit_35_output1d),
    .input2a(cbuffer256bit_37_output1a), .input2b(cbuffer256bit_37_output1b),
    .input2c(cbuffer256bit_37_output1c), .input2d(cbuffer256bit_37_output1d),
    .output1a(subtractor256bit_37_output1a), .output1b(subtractor256bit_37_output1b),
    .output1c(subtractor256bit_37_output1c), .output1d(subtractor256bit_37_output1d));  // open: inborrow, borrow
  cbuffer256bit cbuffer256bit_37 (
    .buffer1(and_127_out[45]), .input1a({64{1'b0}}), .input1b({input2[18:0], {45{1'b0}}}),
    .input1c({{19{1'b0}}, input2[63:19]}), .input1d({64{1'b0}}), .output1a(cbuffer256bit_37_output1a),
    .output1b(cbuffer256bit_37_output1b), .output1c(cbuffer256bit_37_output1c),
    .output1d(cbuffer256bit_37_output1d));
  and and_37 (and_127_out[45], not_1_out, or_37_out);
  or or_37 (or_37_out, comparatoru256bit_37_greater1, comparatoru256bit_37_equal1);
  comparatoru256bit comparatoru256bit_37 (
    .input1a(subtractor256bit_35_output1a), .input1b(subtractor256bit_35_output1b),
    .input1c(subtractor256bit_35_output1c), .input1d(subtractor256bit_35_output1d), .input2a({64{1'b0}}),
    .input2b({input2[18:0], {45{1'b0}}}), .input2c({{19{1'b0}}, input2[63:19]}), .input2d({64{1'b0}}),
    .greater1(comparatoru256bit_37_greater1), .equal1(comparatoru256bit_37_equal1));  // open: less1
  subtractor256bit subtractor256bit_38 (
    .input1a(subtractor256bit_36_output1a), .input1b(subtractor256bit_36_output1b),
    .input1c(subtractor256bit_36_output1c), .input1d(subtractor256bit_36_output1d),
    .input2a(cbuffer256bit_38_output1a), .input2b(cbuffer256bit_38_output1b),
    .input2c(cbuffer256bit_38_output1c), .input2d(cbuffer256bit_38_output1d),
    .output1a(subtractor256bit_38_output1a), .output1b(subtractor256bit_38_output1b),
    .output1c(subtractor256bit_38_output1c), .output1d(subtractor256bit_38_output1d));  // open: inborrow, borrow
  cbuffer256bit cbuffer256bit_38 (
    .buffer1(output1[45]), .input1a({input2[18:0], {45{1'b0}}}), .input1b({{19{1'b0}}, input2[63:19]}),
    .input1c({64{1'b0}}), .input1d({64{1'b0}}), .output1a(cbuffer256bit_38_output1a),
    .output1b(cbuffer256bit_38_output1b), .output1c(cbuffer256bit_38_output1c),
    .output1d(cbuffer256bit_38_output1d));
  and and_38 (output1[45], not_1_out, or_38_out);
  or or_38 (or_38_out, comparatoru256bit_38_greater1, comparatoru256bit_38_equal1);
  comparatoru256bit comparatoru256bit_38 (
    .input1a(subtractor256bit_36_output1a), .input1b(subtractor256bit_36_output1b),
    .input1c(subtractor256bit_36_output1c), .input1d(subtractor256bit_36_output1d),
    .input2a({input2[18:0], {45{1'b0}}}), .input2b({{19{1'b0}}, input2[63:19]}), .input2c({64{1'b0}}),
    .input2d({64{1'b0}}), .greater1(comparatoru256bit_38_greater1), .equal1(comparatoru256bit_38_equal1));  // open: less1
  subtractor256bit subtractor256bit_39 (
    .input1a(subtractor256bit_37_output1a), .input1b(subtractor256bit_37_output1b),
    .input1c(subtractor256bit_37_output1c), .input1d(subtractor256bit_37_output1d),
    .input2a(cbuffer256bit_39_output1a), .input2b(cbuffer256bit_39_output1b),
    .input2c(cbuffer256bit_39_output1c), .input2d(cbuffer256bit_39_output1d),
    .output1a(subtractor256bit_39_output1a), .output1b(subtractor256bit_39_output1b),
    .output1c(subtractor256bit_39_output1c), .output1d(subtractor256bit_39_output1d));  // open: inborrow, borrow
  cbuffer256bit cbuffer256bit_39 (
    .buffer1(and_127_out[44]), .input1a({64{1'b0}}), .input1b({input2[19:0], {44{1'b0}}}),
    .input1c({{20{1'b0}}, input2[63:20]}), .input1d({64{1'b0}}), .output1a(cbuffer256bit_39_output1a),
    .output1b(cbuffer256bit_39_output1b), .output1c(cbuffer256bit_39_output1c),
    .output1d(cbuffer256bit_39_output1d));
  and and_39 (and_127_out[44], not_1_out, or_39_out);
  or or_39 (or_39_out, comparatoru256bit_39_greater1, comparatoru256bit_39_equal1);
  comparatoru256bit comparatoru256bit_39 (
    .input1a(subtractor256bit_37_output1a), .input1b(subtractor256bit_37_output1b),
    .input1c(subtractor256bit_37_output1c), .input1d(subtractor256bit_37_output1d), .input2a({64{1'b0}}),
    .input2b({input2[19:0], {44{1'b0}}}), .input2c({{20{1'b0}}, input2[63:20]}), .input2d({64{1'b0}}),
    .greater1(comparatoru256bit_39_greater1), .equal1(comparatoru256bit_39_equal1));  // open: less1
  subtractor256bit subtractor256bit_40 (
    .input1a(subtractor256bit_38_output1a), .input1b(subtractor256bit_38_output1b),
    .input1c(subtractor256bit_38_output1c), .input1d(subtractor256bit_38_output1d),
    .input2a(cbuffer256bit_40_output1a), .input2b(cbuffer256bit_40_output1b),
    .input2c(cbuffer256bit_40_output1c), .input2d(cbuffer256bit_40_output1d),
    .output1a(subtractor256bit_40_output1a), .output1b(subtractor256bit_40_output1b),
    .output1c(subtractor256bit_40_output1c), .output1d(subtractor256bit_40_output1d));  // open: inborrow, borrow
  cbuffer256bit cbuffer256bit_40 (
    .buffer1(output1[44]), .input1a({input2[19:0], {44{1'b0}}}), .input1b({{20{1'b0}}, input2[63:20]}),
    .input1c({64{1'b0}}), .input1d({64{1'b0}}), .output1a(cbuffer256bit_40_output1a),
    .output1b(cbuffer256bit_40_output1b), .output1c(cbuffer256bit_40_output1c),
    .output1d(cbuffer256bit_40_output1d));
  and and_40 (output1[44], not_1_out, or_40_out);
  or or_40 (or_40_out, comparatoru256bit_40_greater1, comparatoru256bit_40_equal1);
  comparatoru256bit comparatoru256bit_40 (
    .input1a(subtractor256bit_38_output1a), .input1b(subtractor256bit_38_output1b),
    .input1c(subtractor256bit_38_output1c), .input1d(subtractor256bit_38_output1d),
    .input2a({input2[19:0], {44{1'b0}}}), .input2b({{20{1'b0}}, input2[63:20]}), .input2c({64{1'b0}}),
    .input2d({64{1'b0}}), .greater1(comparatoru256bit_40_greater1), .equal1(comparatoru256bit_40_equal1));  // open: less1
  subtractor256bit subtractor256bit_41 (
    .input1a(subtractor256bit_39_output1a), .input1b(subtractor256bit_39_output1b),
    .input1c(subtractor256bit_39_output1c), .input1d(subtractor256bit_39_output1d),
    .input2a(cbuffer256bit_41_output1a), .input2b(cbuffer256bit_41_output1b),
    .input2c(cbuffer256bit_41_output1c), .input2d(cbuffer256bit_41_output1d),
    .output1a(subtractor256bit_41_output1a), .output1b(subtractor256bit_41_output1b),
    .output1c(subtractor256bit_41_output1c), .output1d(subtractor256bit_41_output1d));  // open: inborrow, borrow
  cbuffer256bit cbuffer256bit_41 (
    .buffer1(and_127_out[43]), .input1a({64{1'b0}}), .input1b({input2[20:0], {43{1'b0}}}),
    .input1c({{21{1'b0}}, input2[63:21]}), .input1d({64{1'b0}}), .output1a(cbuffer256bit_41_output1a),
    .output1b(cbuffer256bit_41_output1b), .output1c(cbuffer256bit_41_output1c),
    .output1d(cbuffer256bit_41_output1d));
  and and_41 (and_127_out[43], not_1_out, or_41_out);
  or or_41 (or_41_out, comparatoru256bit_41_greater1, comparatoru256bit_41_equal1);
  comparatoru256bit comparatoru256bit_41 (
    .input1a(subtractor256bit_39_output1a), .input1b(subtractor256bit_39_output1b),
    .input1c(subtractor256bit_39_output1c), .input1d(subtractor256bit_39_output1d), .input2a({64{1'b0}}),
    .input2b({input2[20:0], {43{1'b0}}}), .input2c({{21{1'b0}}, input2[63:21]}), .input2d({64{1'b0}}),
    .greater1(comparatoru256bit_41_greater1), .equal1(comparatoru256bit_41_equal1));  // open: less1
  subtractor256bit subtractor256bit_42 (
    .input1a(subtractor256bit_40_output1a), .input1b(subtractor256bit_40_output1b),
    .input1c(subtractor256bit_40_output1c), .input1d(subtractor256bit_40_output1d),
    .input2a(cbuffer256bit_42_output1a), .input2b(cbuffer256bit_42_output1b),
    .input2c(cbuffer256bit_42_output1c), .input2d(cbuffer256bit_42_output1d),
    .output1a(subtractor256bit_42_output1a), .output1b(subtractor256bit_42_output1b),
    .output1c(subtractor256bit_42_output1c), .output1d(subtractor256bit_42_output1d));  // open: inborrow, borrow
  cbuffer256bit cbuffer256bit_42 (
    .buffer1(output1[43]), .input1a({input2[20:0], {43{1'b0}}}), .input1b({{21{1'b0}}, input2[63:21]}),
    .input1c({64{1'b0}}), .input1d({64{1'b0}}), .output1a(cbuffer256bit_42_output1a),
    .output1b(cbuffer256bit_42_output1b), .output1c(cbuffer256bit_42_output1c),
    .output1d(cbuffer256bit_42_output1d));
  and and_42 (output1[43], not_1_out, or_42_out);
  or or_42 (or_42_out, comparatoru256bit_42_greater1, comparatoru256bit_42_equal1);
  comparatoru256bit comparatoru256bit_42 (
    .input1a(subtractor256bit_40_output1a), .input1b(subtractor256bit_40_output1b),
    .input1c(subtractor256bit_40_output1c), .input1d(subtractor256bit_40_output1d),
    .input2a({input2[20:0], {43{1'b0}}}), .input2b({{21{1'b0}}, input2[63:21]}), .input2c({64{1'b0}}),
    .input2d({64{1'b0}}), .greater1(comparatoru256bit_42_greater1), .equal1(comparatoru256bit_42_equal1));  // open: less1
  subtractor256bit subtractor256bit_43 (
    .input1a(subtractor256bit_41_output1a), .input1b(subtractor256bit_41_output1b),
    .input1c(subtractor256bit_41_output1c), .input1d(subtractor256bit_41_output1d),
    .input2a(cbuffer256bit_43_output1a), .input2b(cbuffer256bit_43_output1b),
    .input2c(cbuffer256bit_43_output1c), .input2d(cbuffer256bit_43_output1d),
    .output1a(subtractor256bit_43_output1a), .output1b(subtractor256bit_43_output1b),
    .output1c(subtractor256bit_43_output1c), .output1d(subtractor256bit_43_output1d));  // open: inborrow, borrow
  cbuffer256bit cbuffer256bit_43 (
    .buffer1(and_127_out[42]), .input1a({64{1'b0}}), .input1b({input2[21:0], {42{1'b0}}}),
    .input1c({{22{1'b0}}, input2[63:22]}), .input1d({64{1'b0}}), .output1a(cbuffer256bit_43_output1a),
    .output1b(cbuffer256bit_43_output1b), .output1c(cbuffer256bit_43_output1c),
    .output1d(cbuffer256bit_43_output1d));
  and and_43 (and_127_out[42], not_1_out, or_43_out);
  or or_43 (or_43_out, comparatoru256bit_43_greater1, comparatoru256bit_43_equal1);
  comparatoru256bit comparatoru256bit_43 (
    .input1a(subtractor256bit_41_output1a), .input1b(subtractor256bit_41_output1b),
    .input1c(subtractor256bit_41_output1c), .input1d(subtractor256bit_41_output1d), .input2a({64{1'b0}}),
    .input2b({input2[21:0], {42{1'b0}}}), .input2c({{22{1'b0}}, input2[63:22]}), .input2d({64{1'b0}}),
    .greater1(comparatoru256bit_43_greater1), .equal1(comparatoru256bit_43_equal1));  // open: less1
  subtractor256bit subtractor256bit_44 (
    .input1a(subtractor256bit_42_output1a), .input1b(subtractor256bit_42_output1b),
    .input1c(subtractor256bit_42_output1c), .input1d(subtractor256bit_42_output1d),
    .input2a(cbuffer256bit_44_output1a), .input2b(cbuffer256bit_44_output1b),
    .input2c(cbuffer256bit_44_output1c), .input2d(cbuffer256bit_44_output1d),
    .output1a(subtractor256bit_44_output1a), .output1b(subtractor256bit_44_output1b),
    .output1c(subtractor256bit_44_output1c), .output1d(subtractor256bit_44_output1d));  // open: inborrow, borrow
  cbuffer256bit cbuffer256bit_44 (
    .buffer1(output1[42]), .input1a({input2[21:0], {42{1'b0}}}), .input1b({{22{1'b0}}, input2[63:22]}),
    .input1c({64{1'b0}}), .input1d({64{1'b0}}), .output1a(cbuffer256bit_44_output1a),
    .output1b(cbuffer256bit_44_output1b), .output1c(cbuffer256bit_44_output1c),
    .output1d(cbuffer256bit_44_output1d));
  and and_44 (output1[42], not_1_out, or_44_out);
  or or_44 (or_44_out, comparatoru256bit_44_greater1, comparatoru256bit_44_equal1);
  comparatoru256bit comparatoru256bit_44 (
    .input1a(subtractor256bit_42_output1a), .input1b(subtractor256bit_42_output1b),
    .input1c(subtractor256bit_42_output1c), .input1d(subtractor256bit_42_output1d),
    .input2a({input2[21:0], {42{1'b0}}}), .input2b({{22{1'b0}}, input2[63:22]}), .input2c({64{1'b0}}),
    .input2d({64{1'b0}}), .greater1(comparatoru256bit_44_greater1), .equal1(comparatoru256bit_44_equal1));  // open: less1
  subtractor256bit subtractor256bit_45 (
    .input1a(subtractor256bit_43_output1a), .input1b(subtractor256bit_43_output1b),
    .input1c(subtractor256bit_43_output1c), .input1d(subtractor256bit_43_output1d),
    .input2a(cbuffer256bit_45_output1a), .input2b(cbuffer256bit_45_output1b),
    .input2c(cbuffer256bit_45_output1c), .input2d(cbuffer256bit_45_output1d),
    .output1a(subtractor256bit_45_output1a), .output1b(subtractor256bit_45_output1b),
    .output1c(subtractor256bit_45_output1c), .output1d(subtractor256bit_45_output1d));  // open: inborrow, borrow
  cbuffer256bit cbuffer256bit_45 (
    .buffer1(and_127_out[41]), .input1a({64{1'b0}}), .input1b({input2[22:0], {41{1'b0}}}),
    .input1c({{23{1'b0}}, input2[63:23]}), .input1d({64{1'b0}}), .output1a(cbuffer256bit_45_output1a),
    .output1b(cbuffer256bit_45_output1b), .output1c(cbuffer256bit_45_output1c),
    .output1d(cbuffer256bit_45_output1d));
  and and_45 (and_127_out[41], not_1_out, or_45_out);
  comparatoru256bit comparatoru256bit_45 (
    .input1a(subtractor256bit_43_output1a), .input1b(subtractor256bit_43_output1b),
    .input1c(subtractor256bit_43_output1c), .input1d(subtractor256bit_43_output1d), .input2a({64{1'b0}}),
    .input2b({input2[22:0], {41{1'b0}}}), .input2c({{23{1'b0}}, input2[63:23]}), .input2d({64{1'b0}}),
    .greater1(comparatoru256bit_45_greater1), .equal1(comparatoru256bit_45_equal1));  // open: less1
  subtractor256bit subtractor256bit_46 (
    .input1a(subtractor256bit_44_output1a), .input1b(subtractor256bit_44_output1b),
    .input1c(subtractor256bit_44_output1c), .input1d(subtractor256bit_44_output1d),
    .input2a(cbuffer256bit_46_output1a), .input2b(cbuffer256bit_46_output1b),
    .input2c(cbuffer256bit_46_output1c), .input2d(cbuffer256bit_46_output1d),
    .output1a(subtractor256bit_46_output1a), .output1b(subtractor256bit_46_output1b),
    .output1c(subtractor256bit_46_output1c), .output1d(subtractor256bit_46_output1d));  // open: inborrow, borrow
  cbuffer256bit cbuffer256bit_46 (
    .buffer1(output1[41]), .input1a({input2[22:0], {41{1'b0}}}), .input1b({{23{1'b0}}, input2[63:23]}),
    .input1c({64{1'b0}}), .input1d({64{1'b0}}), .output1a(cbuffer256bit_46_output1a),
    .output1b(cbuffer256bit_46_output1b), .output1c(cbuffer256bit_46_output1c),
    .output1d(cbuffer256bit_46_output1d));
  and and_46 (output1[41], not_1_out, or_46_out);
  or or_45 (or_45_out, comparatoru256bit_45_greater1, comparatoru256bit_45_equal1);
  or or_46 (or_46_out, comparatoru256bit_46_greater1, comparatoru256bit_46_equal1);
  comparatoru256bit comparatoru256bit_46 (
    .input1a(subtractor256bit_44_output1a), .input1b(subtractor256bit_44_output1b),
    .input1c(subtractor256bit_44_output1c), .input1d(subtractor256bit_44_output1d),
    .input2a({input2[22:0], {41{1'b0}}}), .input2b({{23{1'b0}}, input2[63:23]}), .input2c({64{1'b0}}),
    .input2d({64{1'b0}}), .greater1(comparatoru256bit_46_greater1), .equal1(comparatoru256bit_46_equal1));  // open: less1
  subtractor256bit subtractor256bit_47 (
    .input1a(subtractor256bit_45_output1a), .input1b(subtractor256bit_45_output1b),
    .input1c(subtractor256bit_45_output1c), .input1d(subtractor256bit_45_output1d),
    .input2a(cbuffer256bit_47_output1a), .input2b(cbuffer256bit_47_output1b),
    .input2c(cbuffer256bit_47_output1c), .input2d(cbuffer256bit_47_output1d),
    .output1a(subtractor256bit_47_output1a), .output1b(subtractor256bit_47_output1b),
    .output1c(subtractor256bit_47_output1c), .output1d(subtractor256bit_47_output1d));  // open: inborrow, borrow
  cbuffer256bit cbuffer256bit_47 (
    .buffer1(and_127_out[40]), .input1a({64{1'b0}}), .input1b({input2[23:0], {40{1'b0}}}),
    .input1c({{24{1'b0}}, input2[63:24]}), .input1d({64{1'b0}}), .output1a(cbuffer256bit_47_output1a),
    .output1b(cbuffer256bit_47_output1b), .output1c(cbuffer256bit_47_output1c),
    .output1d(cbuffer256bit_47_output1d));
  and and_47 (and_127_out[40], not_1_out, or_47_out);
  or or_47 (or_47_out, comparatoru256bit_47_greater1, comparatoru256bit_47_equal1);
  comparatoru256bit comparatoru256bit_47 (
    .input1a(subtractor256bit_45_output1a), .input1b(subtractor256bit_45_output1b),
    .input1c(subtractor256bit_45_output1c), .input1d(subtractor256bit_45_output1d), .input2a({64{1'b0}}),
    .input2b({input2[23:0], {40{1'b0}}}), .input2c({{24{1'b0}}, input2[63:24]}), .input2d({64{1'b0}}),
    .greater1(comparatoru256bit_47_greater1), .equal1(comparatoru256bit_47_equal1));  // open: less1
  subtractor256bit subtractor256bit_48 (
    .input1a(subtractor256bit_46_output1a), .input1b(subtractor256bit_46_output1b),
    .input1c(subtractor256bit_46_output1c), .input1d(subtractor256bit_46_output1d),
    .input2a(cbuffer256bit_48_output1a), .input2b(cbuffer256bit_48_output1b),
    .input2c(cbuffer256bit_48_output1c), .input2d(cbuffer256bit_48_output1d),
    .output1a(subtractor256bit_48_output1a), .output1b(subtractor256bit_48_output1b),
    .output1c(subtractor256bit_48_output1c), .output1d(subtractor256bit_48_output1d));  // open: inborrow, borrow
  cbuffer256bit cbuffer256bit_48 (
    .buffer1(output1[40]), .input1a({input2[23:0], {40{1'b0}}}), .input1b({{24{1'b0}}, input2[63:24]}),
    .input1c({64{1'b0}}), .input1d({64{1'b0}}), .output1a(cbuffer256bit_48_output1a),
    .output1b(cbuffer256bit_48_output1b), .output1c(cbuffer256bit_48_output1c),
    .output1d(cbuffer256bit_48_output1d));
  and and_48 (output1[40], not_1_out, or_48_out);
  or or_48 (or_48_out, comparatoru256bit_48_greater1, comparatoru256bit_48_equal1);
  comparatoru256bit comparatoru256bit_48 (
    .input1a(subtractor256bit_46_output1a), .input1b(subtractor256bit_46_output1b),
    .input1c(subtractor256bit_46_output1c), .input1d(subtractor256bit_46_output1d),
    .input2a({input2[23:0], {40{1'b0}}}), .input2b({{24{1'b0}}, input2[63:24]}), .input2c({64{1'b0}}),
    .input2d({64{1'b0}}), .greater1(comparatoru256bit_48_greater1), .equal1(comparatoru256bit_48_equal1));  // open: less1
  subtractor256bit subtractor256bit_49 (
    .input1a(subtractor256bit_47_output1a), .input1b(subtractor256bit_47_output1b),
    .input1c(subtractor256bit_47_output1c), .input1d(subtractor256bit_47_output1d),
    .input2a(cbuffer256bit_49_output1a), .input2b(cbuffer256bit_49_output1b),
    .input2c(cbuffer256bit_49_output1c), .input2d(cbuffer256bit_49_output1d),
    .output1a(subtractor256bit_49_output1a), .output1b(subtractor256bit_49_output1b),
    .output1c(subtractor256bit_49_output1c), .output1d(subtractor256bit_49_output1d));  // open: inborrow, borrow
  cbuffer256bit cbuffer256bit_49 (
    .buffer1(and_127_out[39]), .input1a({64{1'b0}}), .input1b({input2[24:0], {39{1'b0}}}),
    .input1c({{25{1'b0}}, input2[63:25]}), .input1d({64{1'b0}}), .output1a(cbuffer256bit_49_output1a),
    .output1b(cbuffer256bit_49_output1b), .output1c(cbuffer256bit_49_output1c),
    .output1d(cbuffer256bit_49_output1d));
  and and_49 (and_127_out[39], not_1_out, or_49_out);
  or or_49 (or_49_out, comparatoru256bit_49_greater1, comparatoru256bit_49_equal1);
  comparatoru256bit comparatoru256bit_49 (
    .input1a(subtractor256bit_47_output1a), .input1b(subtractor256bit_47_output1b),
    .input1c(subtractor256bit_47_output1c), .input1d(subtractor256bit_47_output1d), .input2a({64{1'b0}}),
    .input2b({input2[24:0], {39{1'b0}}}), .input2c({{25{1'b0}}, input2[63:25]}), .input2d({64{1'b0}}),
    .greater1(comparatoru256bit_49_greater1), .equal1(comparatoru256bit_49_equal1));  // open: less1
  subtractor256bit subtractor256bit_50 (
    .input1a(subtractor256bit_48_output1a), .input1b(subtractor256bit_48_output1b),
    .input1c(subtractor256bit_48_output1c), .input1d(subtractor256bit_48_output1d),
    .input2a(cbuffer256bit_50_output1a), .input2b(cbuffer256bit_50_output1b),
    .input2c(cbuffer256bit_50_output1c), .input2d(cbuffer256bit_50_output1d),
    .output1a(subtractor256bit_50_output1a), .output1b(subtractor256bit_50_output1b),
    .output1c(subtractor256bit_50_output1c), .output1d(subtractor256bit_50_output1d));  // open: inborrow, borrow
  cbuffer256bit cbuffer256bit_50 (
    .buffer1(output1[39]), .input1a({input2[24:0], {39{1'b0}}}), .input1b({{25{1'b0}}, input2[63:25]}),
    .input1c({64{1'b0}}), .input1d({64{1'b0}}), .output1a(cbuffer256bit_50_output1a),
    .output1b(cbuffer256bit_50_output1b), .output1c(cbuffer256bit_50_output1c),
    .output1d(cbuffer256bit_50_output1d));
  and and_50 (output1[39], not_1_out, or_50_out);
  or or_50 (or_50_out, comparatoru256bit_50_greater1, comparatoru256bit_50_equal1);
  comparatoru256bit comparatoru256bit_50 (
    .input1a(subtractor256bit_48_output1a), .input1b(subtractor256bit_48_output1b),
    .input1c(subtractor256bit_48_output1c), .input1d(subtractor256bit_48_output1d),
    .input2a({input2[24:0], {39{1'b0}}}), .input2b({{25{1'b0}}, input2[63:25]}), .input2c({64{1'b0}}),
    .input2d({64{1'b0}}), .greater1(comparatoru256bit_50_greater1), .equal1(comparatoru256bit_50_equal1));  // open: less1
  subtractor256bit subtractor256bit_51 (
    .input1a(subtractor256bit_49_output1a), .input1b(subtractor256bit_49_output1b),
    .input1c(subtractor256bit_49_output1c), .input1d(subtractor256bit_49_output1d),
    .input2a(cbuffer256bit_51_output1a), .input2b(cbuffer256bit_51_output1b),
    .input2c(cbuffer256bit_51_output1c), .input2d(cbuffer256bit_51_output1d),
    .output1a(subtractor256bit_51_output1a), .output1b(subtractor256bit_51_output1b),
    .output1c(subtractor256bit_51_output1c), .output1d(subtractor256bit_51_output1d));  // open: inborrow, borrow
  cbuffer256bit cbuffer256bit_51 (
    .buffer1(and_127_out[38]), .input1a({64{1'b0}}), .input1b({input2[25:0], {38{1'b0}}}),
    .input1c({{26{1'b0}}, input2[63:26]}), .input1d({64{1'b0}}), .output1a(cbuffer256bit_51_output1a),
    .output1b(cbuffer256bit_51_output1b), .output1c(cbuffer256bit_51_output1c),
    .output1d(cbuffer256bit_51_output1d));
  and and_51 (and_127_out[38], not_1_out, or_51_out);
  or or_51 (or_51_out, comparatoru256bit_51_greater1, comparatoru256bit_51_equal1);
  comparatoru256bit comparatoru256bit_51 (
    .input1a(subtractor256bit_49_output1a), .input1b(subtractor256bit_49_output1b),
    .input1c(subtractor256bit_49_output1c), .input1d(subtractor256bit_49_output1d), .input2a({64{1'b0}}),
    .input2b({input2[25:0], {38{1'b0}}}), .input2c({{26{1'b0}}, input2[63:26]}), .input2d({64{1'b0}}),
    .greater1(comparatoru256bit_51_greater1), .equal1(comparatoru256bit_51_equal1));  // open: less1
  subtractor256bit subtractor256bit_52 (
    .input1a(subtractor256bit_50_output1a), .input1b(subtractor256bit_50_output1b),
    .input1c(subtractor256bit_50_output1c), .input1d(subtractor256bit_50_output1d),
    .input2a(cbuffer256bit_52_output1a), .input2b(cbuffer256bit_52_output1b),
    .input2c(cbuffer256bit_52_output1c), .input2d(cbuffer256bit_52_output1d),
    .output1a(subtractor256bit_52_output1a), .output1b(subtractor256bit_52_output1b),
    .output1c(subtractor256bit_52_output1c), .output1d(subtractor256bit_52_output1d));  // open: inborrow, borrow
  cbuffer256bit cbuffer256bit_52 (
    .buffer1(output1[38]), .input1a({input2[25:0], {38{1'b0}}}), .input1b({{26{1'b0}}, input2[63:26]}),
    .input1c({64{1'b0}}), .input1d({64{1'b0}}), .output1a(cbuffer256bit_52_output1a),
    .output1b(cbuffer256bit_52_output1b), .output1c(cbuffer256bit_52_output1c),
    .output1d(cbuffer256bit_52_output1d));
  and and_52 (output1[38], not_1_out, or_52_out);
  comparatoru256bit comparatoru256bit_52 (
    .input1a(subtractor256bit_50_output1a), .input1b(subtractor256bit_50_output1b),
    .input1c(subtractor256bit_50_output1c), .input1d(subtractor256bit_50_output1d),
    .input2a({input2[25:0], {38{1'b0}}}), .input2b({{26{1'b0}}, input2[63:26]}), .input2c({64{1'b0}}),
    .input2d({64{1'b0}}), .greater1(comparatoru256bit_52_greater1), .equal1(comparatoru256bit_52_equal1));  // open: less1
  or or_52 (or_52_out, comparatoru256bit_52_greater1, comparatoru256bit_52_equal1);
  subtractor256bit subtractor256bit_53 (
    .input1a(subtractor256bit_51_output1a), .input1b(subtractor256bit_51_output1b),
    .input1c(subtractor256bit_51_output1c), .input1d(subtractor256bit_51_output1d),
    .input2a(cbuffer256bit_53_output1a), .input2b(cbuffer256bit_53_output1b),
    .input2c(cbuffer256bit_53_output1c), .input2d(cbuffer256bit_53_output1d),
    .output1a(subtractor256bit_53_output1a), .output1b(subtractor256bit_53_output1b),
    .output1c(subtractor256bit_53_output1c), .output1d(subtractor256bit_53_output1d));  // open: inborrow, borrow
  cbuffer256bit cbuffer256bit_53 (
    .buffer1(and_127_out[37]), .input1a({64{1'b0}}), .input1b({input2[26:0], {37{1'b0}}}),
    .input1c({{27{1'b0}}, input2[63:27]}), .input1d({64{1'b0}}), .output1a(cbuffer256bit_53_output1a),
    .output1b(cbuffer256bit_53_output1b), .output1c(cbuffer256bit_53_output1c),
    .output1d(cbuffer256bit_53_output1d));
  and and_53 (and_127_out[37], not_1_out, or_53_out);
  or or_53 (or_53_out, comparatoru256bit_53_greater1, comparatoru256bit_53_equal1);
  comparatoru256bit comparatoru256bit_53 (
    .input1a(subtractor256bit_51_output1a), .input1b(subtractor256bit_51_output1b),
    .input1c(subtractor256bit_51_output1c), .input1d(subtractor256bit_51_output1d), .input2a({64{1'b0}}),
    .input2b({input2[26:0], {37{1'b0}}}), .input2c({{27{1'b0}}, input2[63:27]}), .input2d({64{1'b0}}),
    .greater1(comparatoru256bit_53_greater1), .equal1(comparatoru256bit_53_equal1));  // open: less1
  subtractor256bit subtractor256bit_54 (
    .input1a(subtractor256bit_52_output1a), .input1b(subtractor256bit_52_output1b),
    .input1c(subtractor256bit_52_output1c), .input1d(subtractor256bit_52_output1d),
    .input2a(cbuffer256bit_54_output1a), .input2b(cbuffer256bit_54_output1b),
    .input2c(cbuffer256bit_54_output1c), .input2d(cbuffer256bit_54_output1d),
    .output1a(subtractor256bit_54_output1a), .output1b(subtractor256bit_54_output1b),
    .output1c(subtractor256bit_54_output1c), .output1d(subtractor256bit_54_output1d));  // open: inborrow, borrow
  cbuffer256bit cbuffer256bit_54 (
    .buffer1(output1[37]), .input1a({input2[26:0], {37{1'b0}}}), .input1b({{27{1'b0}}, input2[63:27]}),
    .input1c({64{1'b0}}), .input1d({64{1'b0}}), .output1a(cbuffer256bit_54_output1a),
    .output1b(cbuffer256bit_54_output1b), .output1c(cbuffer256bit_54_output1c),
    .output1d(cbuffer256bit_54_output1d));
  and and_54 (output1[37], not_1_out, or_54_out);
  or or_54 (or_54_out, comparatoru256bit_54_greater1, comparatoru256bit_54_equal1);
  comparatoru256bit comparatoru256bit_54 (
    .input1a(subtractor256bit_52_output1a), .input1b(subtractor256bit_52_output1b),
    .input1c(subtractor256bit_52_output1c), .input1d(subtractor256bit_52_output1d),
    .input2a({input2[26:0], {37{1'b0}}}), .input2b({{27{1'b0}}, input2[63:27]}), .input2c({64{1'b0}}),
    .input2d({64{1'b0}}), .greater1(comparatoru256bit_54_greater1), .equal1(comparatoru256bit_54_equal1));  // open: less1
  subtractor256bit subtractor256bit_55 (
    .input1a(subtractor256bit_53_output1a), .input1b(subtractor256bit_53_output1b),
    .input1c(subtractor256bit_53_output1c), .input1d(subtractor256bit_53_output1d),
    .input2a(cbuffer256bit_55_output1a), .input2b(cbuffer256bit_55_output1b),
    .input2c(cbuffer256bit_55_output1c), .input2d(cbuffer256bit_55_output1d),
    .output1a(subtractor256bit_55_output1a), .output1b(subtractor256bit_55_output1b),
    .output1c(subtractor256bit_55_output1c), .output1d(subtractor256bit_55_output1d));  // open: inborrow, borrow
  cbuffer256bit cbuffer256bit_55 (
    .buffer1(and_127_out[36]), .input1a({64{1'b0}}), .input1b({input2[27:0], {36{1'b0}}}),
    .input1c({{28{1'b0}}, input2[63:28]}), .input1d({64{1'b0}}), .output1a(cbuffer256bit_55_output1a),
    .output1b(cbuffer256bit_55_output1b), .output1c(cbuffer256bit_55_output1c),
    .output1d(cbuffer256bit_55_output1d));
  and and_55 (and_127_out[36], not_1_out, or_55_out);
  or or_55 (or_55_out, comparatoru256bit_55_greater1, comparatoru256bit_55_equal1);
  comparatoru256bit comparatoru256bit_55 (
    .input1a(subtractor256bit_53_output1a), .input1b(subtractor256bit_53_output1b),
    .input1c(subtractor256bit_53_output1c), .input1d(subtractor256bit_53_output1d), .input2a({64{1'b0}}),
    .input2b({input2[27:0], {36{1'b0}}}), .input2c({{28{1'b0}}, input2[63:28]}), .input2d({64{1'b0}}),
    .greater1(comparatoru256bit_55_greater1), .equal1(comparatoru256bit_55_equal1));  // open: less1
  subtractor256bit subtractor256bit_56 (
    .input1a(subtractor256bit_54_output1a), .input1b(subtractor256bit_54_output1b),
    .input1c(subtractor256bit_54_output1c), .input1d(subtractor256bit_54_output1d),
    .input2a(cbuffer256bit_56_output1a), .input2b(cbuffer256bit_56_output1b),
    .input2c(cbuffer256bit_56_output1c), .input2d(cbuffer256bit_56_output1d),
    .output1a(subtractor256bit_56_output1a), .output1b(subtractor256bit_56_output1b),
    .output1c(subtractor256bit_56_output1c), .output1d(subtractor256bit_56_output1d));  // open: inborrow, borrow
  cbuffer256bit cbuffer256bit_56 (
    .buffer1(output1[36]), .input1a({input2[27:0], {36{1'b0}}}), .input1b({{28{1'b0}}, input2[63:28]}),
    .input1c({64{1'b0}}), .input1d({64{1'b0}}), .output1a(cbuffer256bit_56_output1a),
    .output1b(cbuffer256bit_56_output1b), .output1c(cbuffer256bit_56_output1c),
    .output1d(cbuffer256bit_56_output1d));
  and and_56 (output1[36], not_1_out, or_56_out);
  or or_56 (or_56_out, comparatoru256bit_56_greater1, comparatoru256bit_56_equal1);
  comparatoru256bit comparatoru256bit_56 (
    .input1a(subtractor256bit_54_output1a), .input1b(subtractor256bit_54_output1b),
    .input1c(subtractor256bit_54_output1c), .input1d(subtractor256bit_54_output1d),
    .input2a({input2[27:0], {36{1'b0}}}), .input2b({{28{1'b0}}, input2[63:28]}), .input2c({64{1'b0}}),
    .input2d({64{1'b0}}), .greater1(comparatoru256bit_56_greater1), .equal1(comparatoru256bit_56_equal1));  // open: less1
  subtractor256bit subtractor256bit_57 (
    .input1a(subtractor256bit_55_output1a), .input1b(subtractor256bit_55_output1b),
    .input1c(subtractor256bit_55_output1c), .input1d(subtractor256bit_55_output1d),
    .input2a(cbuffer256bit_57_output1a), .input2b(cbuffer256bit_57_output1b),
    .input2c(cbuffer256bit_57_output1c), .input2d(cbuffer256bit_57_output1d),
    .output1a(subtractor256bit_57_output1a), .output1b(subtractor256bit_57_output1b),
    .output1c(subtractor256bit_57_output1c), .output1d(subtractor256bit_57_output1d));  // open: inborrow, borrow
  cbuffer256bit cbuffer256bit_57 (
    .buffer1(and_127_out[35]), .input1a({64{1'b0}}), .input1b({input2[28:0], {35{1'b0}}}),
    .input1c({{29{1'b0}}, input2[63:29]}), .input1d({64{1'b0}}), .output1a(cbuffer256bit_57_output1a),
    .output1b(cbuffer256bit_57_output1b), .output1c(cbuffer256bit_57_output1c),
    .output1d(cbuffer256bit_57_output1d));
  and and_57 (and_127_out[35], not_1_out, or_57_out);
  or or_57 (or_57_out, comparatoru256bit_57_greater1, comparatoru256bit_57_equal1);
  comparatoru256bit comparatoru256bit_57 (
    .input1a(subtractor256bit_55_output1a), .input1b(subtractor256bit_55_output1b),
    .input1c(subtractor256bit_55_output1c), .input1d(subtractor256bit_55_output1d), .input2a({64{1'b0}}),
    .input2b({input2[28:0], {35{1'b0}}}), .input2c({{29{1'b0}}, input2[63:29]}), .input2d({64{1'b0}}),
    .greater1(comparatoru256bit_57_greater1), .equal1(comparatoru256bit_57_equal1));  // open: less1
  subtractor256bit subtractor256bit_58 (
    .input1a(subtractor256bit_56_output1a), .input1b(subtractor256bit_56_output1b),
    .input1c(subtractor256bit_56_output1c), .input1d(subtractor256bit_56_output1d),
    .input2a(cbuffer256bit_58_output1a), .input2b(cbuffer256bit_58_output1b),
    .input2c(cbuffer256bit_58_output1c), .input2d(cbuffer256bit_58_output1d),
    .output1a(subtractor256bit_58_output1a), .output1b(subtractor256bit_58_output1b),
    .output1c(subtractor256bit_58_output1c), .output1d(subtractor256bit_58_output1d));  // open: inborrow, borrow
  cbuffer256bit cbuffer256bit_58 (
    .buffer1(output1[35]), .input1a({input2[28:0], {35{1'b0}}}), .input1b({{29{1'b0}}, input2[63:29]}),
    .input1c({64{1'b0}}), .input1d({64{1'b0}}), .output1a(cbuffer256bit_58_output1a),
    .output1b(cbuffer256bit_58_output1b), .output1c(cbuffer256bit_58_output1c),
    .output1d(cbuffer256bit_58_output1d));
  and and_58 (output1[35], not_1_out, or_58_out);
  or or_58 (or_58_out, comparatoru256bit_58_greater1, comparatoru256bit_58_equal1);
  comparatoru256bit comparatoru256bit_58 (
    .input1a(subtractor256bit_56_output1a), .input1b(subtractor256bit_56_output1b),
    .input1c(subtractor256bit_56_output1c), .input1d(subtractor256bit_56_output1d),
    .input2a({input2[28:0], {35{1'b0}}}), .input2b({{29{1'b0}}, input2[63:29]}), .input2c({64{1'b0}}),
    .input2d({64{1'b0}}), .greater1(comparatoru256bit_58_greater1), .equal1(comparatoru256bit_58_equal1));  // open: less1
  subtractor256bit subtractor256bit_59 (
    .input1a(subtractor256bit_57_output1a), .input1b(subtractor256bit_57_output1b),
    .input1c(subtractor256bit_57_output1c), .input1d(subtractor256bit_57_output1d),
    .input2a(cbuffer256bit_59_output1a), .input2b(cbuffer256bit_59_output1b),
    .input2c(cbuffer256bit_59_output1c), .input2d(cbuffer256bit_59_output1d),
    .output1a(subtractor256bit_59_output1a), .output1b(subtractor256bit_59_output1b),
    .output1c(subtractor256bit_59_output1c), .output1d(subtractor256bit_59_output1d));  // open: inborrow, borrow
  cbuffer256bit cbuffer256bit_59 (
    .buffer1(and_127_out[34]), .input1a({64{1'b0}}), .input1b({input2[29:0], {34{1'b0}}}),
    .input1c({{30{1'b0}}, input2[63:30]}), .input1d({64{1'b0}}), .output1a(cbuffer256bit_59_output1a),
    .output1b(cbuffer256bit_59_output1b), .output1c(cbuffer256bit_59_output1c),
    .output1d(cbuffer256bit_59_output1d));
  and and_59 (and_127_out[34], not_1_out, or_59_out);
  or or_59 (or_59_out, comparatoru256bit_59_greater1, comparatoru256bit_59_equal1);
  comparatoru256bit comparatoru256bit_59 (
    .input1a(subtractor256bit_57_output1a), .input1b(subtractor256bit_57_output1b),
    .input1c(subtractor256bit_57_output1c), .input1d(subtractor256bit_57_output1d), .input2a({64{1'b0}}),
    .input2b({input2[29:0], {34{1'b0}}}), .input2c({{30{1'b0}}, input2[63:30]}), .input2d({64{1'b0}}),
    .greater1(comparatoru256bit_59_greater1), .equal1(comparatoru256bit_59_equal1));  // open: less1
  subtractor256bit subtractor256bit_60 (
    .input1a(subtractor256bit_58_output1a), .input1b(subtractor256bit_58_output1b),
    .input1c(subtractor256bit_58_output1c), .input1d(subtractor256bit_58_output1d),
    .input2a(cbuffer256bit_60_output1a), .input2b(cbuffer256bit_60_output1b),
    .input2c(cbuffer256bit_60_output1c), .input2d(cbuffer256bit_60_output1d),
    .output1a(subtractor256bit_60_output1a), .output1b(subtractor256bit_60_output1b),
    .output1c(subtractor256bit_60_output1c), .output1d(subtractor256bit_60_output1d));  // open: inborrow, borrow
  cbuffer256bit cbuffer256bit_60 (
    .buffer1(output1[34]), .input1a({input2[29:0], {34{1'b0}}}), .input1b({{30{1'b0}}, input2[63:30]}),
    .input1c({64{1'b0}}), .input1d({64{1'b0}}), .output1a(cbuffer256bit_60_output1a),
    .output1b(cbuffer256bit_60_output1b), .output1c(cbuffer256bit_60_output1c),
    .output1d(cbuffer256bit_60_output1d));
  and and_60 (output1[34], not_1_out, or_60_out);
  or or_60 (or_60_out, comparatoru256bit_60_greater1, comparatoru256bit_60_equal1);
  comparatoru256bit comparatoru256bit_60 (
    .input1a(subtractor256bit_58_output1a), .input1b(subtractor256bit_58_output1b),
    .input1c(subtractor256bit_58_output1c), .input1d(subtractor256bit_58_output1d),
    .input2a({input2[29:0], {34{1'b0}}}), .input2b({{30{1'b0}}, input2[63:30]}), .input2c({64{1'b0}}),
    .input2d({64{1'b0}}), .greater1(comparatoru256bit_60_greater1), .equal1(comparatoru256bit_60_equal1));  // open: less1
  subtractor256bit subtractor256bit_61 (
    .input1a(subtractor256bit_59_output1a), .input1b(subtractor256bit_59_output1b),
    .input1c(subtractor256bit_59_output1c), .input1d(subtractor256bit_59_output1d),
    .input2a(cbuffer256bit_61_output1a), .input2b(cbuffer256bit_61_output1b),
    .input2c(cbuffer256bit_61_output1c), .input2d(cbuffer256bit_61_output1d),
    .output1a(subtractor256bit_61_output1a), .output1b(subtractor256bit_61_output1b),
    .output1c(subtractor256bit_61_output1c), .output1d(subtractor256bit_61_output1d));  // open: inborrow, borrow
  cbuffer256bit cbuffer256bit_61 (
    .buffer1(and_127_out[33]), .input1a({64{1'b0}}), .input1b({input2[30:0], {33{1'b0}}}),
    .input1c({{31{1'b0}}, input2[63:31]}), .input1d({64{1'b0}}), .output1a(cbuffer256bit_61_output1a),
    .output1b(cbuffer256bit_61_output1b), .output1c(cbuffer256bit_61_output1c),
    .output1d(cbuffer256bit_61_output1d));
  and and_61 (and_127_out[33], not_1_out, or_61_out);
  comparatoru256bit comparatoru256bit_61 (
    .input1a(subtractor256bit_59_output1a), .input1b(subtractor256bit_59_output1b),
    .input1c(subtractor256bit_59_output1c), .input1d(subtractor256bit_59_output1d), .input2a({64{1'b0}}),
    .input2b({input2[30:0], {33{1'b0}}}), .input2c({{31{1'b0}}, input2[63:31]}), .input2d({64{1'b0}}),
    .greater1(comparatoru256bit_61_greater1), .equal1(comparatoru256bit_61_equal1));  // open: less1
  subtractor256bit subtractor256bit_62 (
    .input1a(subtractor256bit_60_output1a), .input1b(subtractor256bit_60_output1b),
    .input1c(subtractor256bit_60_output1c), .input1d(subtractor256bit_60_output1d),
    .input2a(cbuffer256bit_62_output1a), .input2b(cbuffer256bit_62_output1b),
    .input2c(cbuffer256bit_62_output1c), .input2d(cbuffer256bit_62_output1d),
    .output1a(subtractor256bit_62_output1a), .output1b(subtractor256bit_62_output1b),
    .output1c(subtractor256bit_62_output1c), .output1d(subtractor256bit_62_output1d));  // open: inborrow, borrow
  cbuffer256bit cbuffer256bit_62 (
    .buffer1(output1[33]), .input1a({input2[30:0], {33{1'b0}}}), .input1b({{31{1'b0}}, input2[63:31]}),
    .input1c({64{1'b0}}), .input1d({64{1'b0}}), .output1a(cbuffer256bit_62_output1a),
    .output1b(cbuffer256bit_62_output1b), .output1c(cbuffer256bit_62_output1c),
    .output1d(cbuffer256bit_62_output1d));
  and and_62 (output1[33], not_1_out, or_62_out);
  or or_61 (or_61_out, comparatoru256bit_61_greater1, comparatoru256bit_61_equal1);
  or or_62 (or_62_out, comparatoru256bit_62_greater1, comparatoru256bit_62_equal1);
  comparatoru256bit comparatoru256bit_62 (
    .input1a(subtractor256bit_60_output1a), .input1b(subtractor256bit_60_output1b),
    .input1c(subtractor256bit_60_output1c), .input1d(subtractor256bit_60_output1d),
    .input2a({input2[30:0], {33{1'b0}}}), .input2b({{31{1'b0}}, input2[63:31]}), .input2c({64{1'b0}}),
    .input2d({64{1'b0}}), .greater1(comparatoru256bit_62_greater1), .equal1(comparatoru256bit_62_equal1));  // open: less1
  subtractor256bit subtractor256bit_63 (
    .input1a(subtractor256bit_61_output1a), .input1b(subtractor256bit_61_output1b),
    .input1c(subtractor256bit_61_output1c), .input1d(subtractor256bit_61_output1d),
    .input2a(cbuffer256bit_63_output1a), .input2b(cbuffer256bit_63_output1b),
    .input2c(cbuffer256bit_63_output1c), .input2d(cbuffer256bit_63_output1d),
    .output1a(subtractor256bit_63_output1a), .output1b(subtractor256bit_63_output1b),
    .output1c(subtractor256bit_63_output1c), .output1d(subtractor256bit_63_output1d));  // open: inborrow, borrow
  cbuffer256bit cbuffer256bit_63 (
    .buffer1(and_127_out[32]), .input1a({64{1'b0}}), .input1b({input2[31:0], {32{1'b0}}}),
    .input1c({{32{1'b0}}, input2[63:32]}), .input1d({64{1'b0}}), .output1a(cbuffer256bit_63_output1a),
    .output1b(cbuffer256bit_63_output1b), .output1c(cbuffer256bit_63_output1c),
    .output1d(cbuffer256bit_63_output1d));
  and and_63 (and_127_out[32], not_1_out, or_63_out);
  or or_63 (or_63_out, comparatoru256bit_63_greater1, comparatoru256bit_63_equal1);
  comparatoru256bit comparatoru256bit_63 (
    .input1a(subtractor256bit_61_output1a), .input1b(subtractor256bit_61_output1b),
    .input1c(subtractor256bit_61_output1c), .input1d(subtractor256bit_61_output1d), .input2a({64{1'b0}}),
    .input2b({input2[31:0], {32{1'b0}}}), .input2c({{32{1'b0}}, input2[63:32]}), .input2d({64{1'b0}}),
    .greater1(comparatoru256bit_63_greater1), .equal1(comparatoru256bit_63_equal1));  // open: less1
  subtractor256bit subtractor256bit_64 (
    .input1a(subtractor256bit_62_output1a), .input1b(subtractor256bit_62_output1b),
    .input1c(subtractor256bit_62_output1c), .input1d(subtractor256bit_62_output1d),
    .input2a(cbuffer256bit_64_output1a), .input2b(cbuffer256bit_64_output1b),
    .input2c(cbuffer256bit_64_output1c), .input2d(cbuffer256bit_64_output1d),
    .output1a(subtractor256bit_64_output1a), .output1b(subtractor256bit_64_output1b),
    .output1c(subtractor256bit_64_output1c), .output1d(subtractor256bit_64_output1d));  // open: inborrow, borrow
  cbuffer256bit cbuffer256bit_64 (
    .buffer1(output1[32]), .input1a({input2[31:0], {32{1'b0}}}), .input1b({{32{1'b0}}, input2[63:32]}),
    .input1c({64{1'b0}}), .input1d({64{1'b0}}), .output1a(cbuffer256bit_64_output1a),
    .output1b(cbuffer256bit_64_output1b), .output1c(cbuffer256bit_64_output1c),
    .output1d(cbuffer256bit_64_output1d));
  and and_64 (output1[32], not_1_out, or_64_out);
  or or_64 (or_64_out, comparatoru256bit_64_greater1, comparatoru256bit_64_equal1);
  comparatoru256bit comparatoru256bit_64 (
    .input1a(subtractor256bit_62_output1a), .input1b(subtractor256bit_62_output1b),
    .input1c(subtractor256bit_62_output1c), .input1d(subtractor256bit_62_output1d),
    .input2a({input2[31:0], {32{1'b0}}}), .input2b({{32{1'b0}}, input2[63:32]}), .input2c({64{1'b0}}),
    .input2d({64{1'b0}}), .greater1(comparatoru256bit_64_greater1), .equal1(comparatoru256bit_64_equal1));  // open: less1
  subtractor256bit subtractor256bit_65 (
    .input1a(subtractor256bit_63_output1a), .input1b(subtractor256bit_63_output1b),
    .input1c(subtractor256bit_63_output1c), .input1d(subtractor256bit_63_output1d),
    .input2a(cbuffer256bit_65_output1a), .input2b(cbuffer256bit_65_output1b),
    .input2c(cbuffer256bit_65_output1c), .input2d(cbuffer256bit_65_output1d),
    .output1a(subtractor256bit_65_output1a), .output1b(subtractor256bit_65_output1b),
    .output1c(subtractor256bit_65_output1c), .output1d(subtractor256bit_65_output1d));  // open: inborrow, borrow
  cbuffer256bit cbuffer256bit_65 (
    .buffer1(and_127_out[31]), .input1a({64{1'b0}}), .input1b({input2[32:0], {31{1'b0}}}),
    .input1c({{33{1'b0}}, input2[63:33]}), .input1d({64{1'b0}}), .output1a(cbuffer256bit_65_output1a),
    .output1b(cbuffer256bit_65_output1b), .output1c(cbuffer256bit_65_output1c),
    .output1d(cbuffer256bit_65_output1d));
  and and_65 (and_127_out[31], not_1_out, or_65_out);
  or or_65 (or_65_out, comparatoru256bit_65_greater1, comparatoru256bit_65_equal1);
  comparatoru256bit comparatoru256bit_65 (
    .input1a(subtractor256bit_63_output1a), .input1b(subtractor256bit_63_output1b),
    .input1c(subtractor256bit_63_output1c), .input1d(subtractor256bit_63_output1d), .input2a({64{1'b0}}),
    .input2b({input2[32:0], {31{1'b0}}}), .input2c({{33{1'b0}}, input2[63:33]}), .input2d({64{1'b0}}),
    .greater1(comparatoru256bit_65_greater1), .equal1(comparatoru256bit_65_equal1));  // open: less1
  subtractor256bit subtractor256bit_66 (
    .input1a(subtractor256bit_64_output1a), .input1b(subtractor256bit_64_output1b),
    .input1c(subtractor256bit_64_output1c), .input1d(subtractor256bit_64_output1d),
    .input2a(cbuffer256bit_66_output1a), .input2b(cbuffer256bit_66_output1b),
    .input2c(cbuffer256bit_66_output1c), .input2d(cbuffer256bit_66_output1d),
    .output1a(subtractor256bit_66_output1a), .output1b(subtractor256bit_66_output1b),
    .output1c(subtractor256bit_66_output1c), .output1d(subtractor256bit_66_output1d));  // open: inborrow, borrow
  cbuffer256bit cbuffer256bit_66 (
    .buffer1(output1[31]), .input1a({input2[32:0], {31{1'b0}}}), .input1b({{33{1'b0}}, input2[63:33]}),
    .input1c({64{1'b0}}), .input1d({64{1'b0}}), .output1a(cbuffer256bit_66_output1a),
    .output1b(cbuffer256bit_66_output1b), .output1c(cbuffer256bit_66_output1c),
    .output1d(cbuffer256bit_66_output1d));
  and and_66 (output1[31], not_1_out, or_66_out);
  or or_66 (or_66_out, comparatoru256bit_66_greater1, comparatoru256bit_66_equal1);
  comparatoru256bit comparatoru256bit_66 (
    .input1a(subtractor256bit_64_output1a), .input1b(subtractor256bit_64_output1b),
    .input1c(subtractor256bit_64_output1c), .input1d(subtractor256bit_64_output1d),
    .input2a({input2[32:0], {31{1'b0}}}), .input2b({{33{1'b0}}, input2[63:33]}), .input2c({64{1'b0}}),
    .input2d({64{1'b0}}), .greater1(comparatoru256bit_66_greater1), .equal1(comparatoru256bit_66_equal1));  // open: less1
  subtractor256bit subtractor256bit_67 (
    .input1a(subtractor256bit_65_output1a), .input1b(subtractor256bit_65_output1b),
    .input1c(subtractor256bit_65_output1c), .input1d(subtractor256bit_65_output1d),
    .input2a(cbuffer256bit_67_output1a), .input2b(cbuffer256bit_67_output1b),
    .input2c(cbuffer256bit_67_output1c), .input2d(cbuffer256bit_67_output1d),
    .output1a(subtractor256bit_67_output1a), .output1b(subtractor256bit_67_output1b),
    .output1c(subtractor256bit_67_output1c), .output1d(subtractor256bit_67_output1d));  // open: inborrow, borrow
  cbuffer256bit cbuffer256bit_67 (
    .buffer1(and_127_out[30]), .input1a({64{1'b0}}), .input1b({input2[33:0], {30{1'b0}}}),
    .input1c({{34{1'b0}}, input2[63:34]}), .input1d({64{1'b0}}), .output1a(cbuffer256bit_67_output1a),
    .output1b(cbuffer256bit_67_output1b), .output1c(cbuffer256bit_67_output1c),
    .output1d(cbuffer256bit_67_output1d));
  and and_67 (and_127_out[30], not_1_out, or_67_out);
  or or_67 (or_67_out, comparatoru256bit_67_greater1, comparatoru256bit_67_equal1);
  comparatoru256bit comparatoru256bit_67 (
    .input1a(subtractor256bit_65_output1a), .input1b(subtractor256bit_65_output1b),
    .input1c(subtractor256bit_65_output1c), .input1d(subtractor256bit_65_output1d), .input2a({64{1'b0}}),
    .input2b({input2[33:0], {30{1'b0}}}), .input2c({{34{1'b0}}, input2[63:34]}), .input2d({64{1'b0}}),
    .greater1(comparatoru256bit_67_greater1), .equal1(comparatoru256bit_67_equal1));  // open: less1
  subtractor256bit subtractor256bit_68 (
    .input1a(subtractor256bit_66_output1a), .input1b(subtractor256bit_66_output1b),
    .input1c(subtractor256bit_66_output1c), .input1d(subtractor256bit_66_output1d),
    .input2a(cbuffer256bit_68_output1a), .input2b(cbuffer256bit_68_output1b),
    .input2c(cbuffer256bit_68_output1c), .input2d(cbuffer256bit_68_output1d),
    .output1a(subtractor256bit_68_output1a), .output1b(subtractor256bit_68_output1b),
    .output1c(subtractor256bit_68_output1c), .output1d(subtractor256bit_68_output1d));  // open: inborrow, borrow
  cbuffer256bit cbuffer256bit_68 (
    .buffer1(output1[30]), .input1a({input2[33:0], {30{1'b0}}}), .input1b({{34{1'b0}}, input2[63:34]}),
    .input1c({64{1'b0}}), .input1d({64{1'b0}}), .output1a(cbuffer256bit_68_output1a),
    .output1b(cbuffer256bit_68_output1b), .output1c(cbuffer256bit_68_output1c),
    .output1d(cbuffer256bit_68_output1d));
  and and_68 (output1[30], not_1_out, or_68_out);
  comparatoru256bit comparatoru256bit_68 (
    .input1a(subtractor256bit_66_output1a), .input1b(subtractor256bit_66_output1b),
    .input1c(subtractor256bit_66_output1c), .input1d(subtractor256bit_66_output1d),
    .input2a({input2[33:0], {30{1'b0}}}), .input2b({{34{1'b0}}, input2[63:34]}), .input2c({64{1'b0}}),
    .input2d({64{1'b0}}), .greater1(comparatoru256bit_68_greater1), .equal1(comparatoru256bit_68_equal1));  // open: less1
  or or_68 (or_68_out, comparatoru256bit_68_greater1, comparatoru256bit_68_equal1);
  subtractor256bit subtractor256bit_69 (
    .input1a(subtractor256bit_67_output1a), .input1b(subtractor256bit_67_output1b),
    .input1c(subtractor256bit_67_output1c), .input1d(subtractor256bit_67_output1d),
    .input2a(cbuffer256bit_69_output1a), .input2b(cbuffer256bit_69_output1b),
    .input2c(cbuffer256bit_69_output1c), .input2d(cbuffer256bit_69_output1d),
    .output1a(subtractor256bit_69_output1a), .output1b(subtractor256bit_69_output1b),
    .output1c(subtractor256bit_69_output1c), .output1d(subtractor256bit_69_output1d));  // open: inborrow, borrow
  cbuffer256bit cbuffer256bit_69 (
    .buffer1(and_127_out[29]), .input1a({64{1'b0}}), .input1b({input2[34:0], {29{1'b0}}}),
    .input1c({{35{1'b0}}, input2[63:35]}), .input1d({64{1'b0}}), .output1a(cbuffer256bit_69_output1a),
    .output1b(cbuffer256bit_69_output1b), .output1c(cbuffer256bit_69_output1c),
    .output1d(cbuffer256bit_69_output1d));
  and and_69 (and_127_out[29], not_1_out, or_69_out);
  or or_69 (or_69_out, comparatoru256bit_69_greater1, comparatoru256bit_69_equal1);
  comparatoru256bit comparatoru256bit_69 (
    .input1a(subtractor256bit_67_output1a), .input1b(subtractor256bit_67_output1b),
    .input1c(subtractor256bit_67_output1c), .input1d(subtractor256bit_67_output1d), .input2a({64{1'b0}}),
    .input2b({input2[34:0], {29{1'b0}}}), .input2c({{35{1'b0}}, input2[63:35]}), .input2d({64{1'b0}}),
    .greater1(comparatoru256bit_69_greater1), .equal1(comparatoru256bit_69_equal1));  // open: less1
  subtractor256bit subtractor256bit_70 (
    .input1a(subtractor256bit_68_output1a), .input1b(subtractor256bit_68_output1b),
    .input1c(subtractor256bit_68_output1c), .input1d(subtractor256bit_68_output1d),
    .input2a(cbuffer256bit_70_output1a), .input2b(cbuffer256bit_70_output1b),
    .input2c(cbuffer256bit_70_output1c), .input2d(cbuffer256bit_70_output1d),
    .output1a(subtractor256bit_70_output1a), .output1b(subtractor256bit_70_output1b),
    .output1c(subtractor256bit_70_output1c), .output1d(subtractor256bit_70_output1d));  // open: inborrow, borrow
  cbuffer256bit cbuffer256bit_70 (
    .buffer1(output1[29]), .input1a({input2[34:0], {29{1'b0}}}), .input1b({{35{1'b0}}, input2[63:35]}),
    .input1c({64{1'b0}}), .input1d({64{1'b0}}), .output1a(cbuffer256bit_70_output1a),
    .output1b(cbuffer256bit_70_output1b), .output1c(cbuffer256bit_70_output1c),
    .output1d(cbuffer256bit_70_output1d));
  and and_70 (output1[29], not_1_out, or_70_out);
  or or_70 (or_70_out, comparatoru256bit_70_greater1, comparatoru256bit_70_equal1);
  comparatoru256bit comparatoru256bit_70 (
    .input1a(subtractor256bit_68_output1a), .input1b(subtractor256bit_68_output1b),
    .input1c(subtractor256bit_68_output1c), .input1d(subtractor256bit_68_output1d),
    .input2a({input2[34:0], {29{1'b0}}}), .input2b({{35{1'b0}}, input2[63:35]}), .input2c({64{1'b0}}),
    .input2d({64{1'b0}}), .greater1(comparatoru256bit_70_greater1), .equal1(comparatoru256bit_70_equal1));  // open: less1
  subtractor256bit subtractor256bit_71 (
    .input1a(subtractor256bit_69_output1a), .input1b(subtractor256bit_69_output1b),
    .input1c(subtractor256bit_69_output1c), .input1d(subtractor256bit_69_output1d),
    .input2a(cbuffer256bit_71_output1a), .input2b(cbuffer256bit_71_output1b),
    .input2c(cbuffer256bit_71_output1c), .input2d(cbuffer256bit_71_output1d),
    .output1a(subtractor256bit_71_output1a), .output1b(subtractor256bit_71_output1b),
    .output1c(subtractor256bit_71_output1c), .output1d(subtractor256bit_71_output1d));  // open: inborrow, borrow
  cbuffer256bit cbuffer256bit_71 (
    .buffer1(and_127_out[28]), .input1a({64{1'b0}}), .input1b({input2[35:0], {28{1'b0}}}),
    .input1c({{36{1'b0}}, input2[63:36]}), .input1d({64{1'b0}}), .output1a(cbuffer256bit_71_output1a),
    .output1b(cbuffer256bit_71_output1b), .output1c(cbuffer256bit_71_output1c),
    .output1d(cbuffer256bit_71_output1d));
  and and_71 (and_127_out[28], not_1_out, or_71_out);
  or or_71 (or_71_out, comparatoru256bit_71_greater1, comparatoru256bit_71_equal1);
  comparatoru256bit comparatoru256bit_71 (
    .input1a(subtractor256bit_69_output1a), .input1b(subtractor256bit_69_output1b),
    .input1c(subtractor256bit_69_output1c), .input1d(subtractor256bit_69_output1d), .input2a({64{1'b0}}),
    .input2b({input2[35:0], {28{1'b0}}}), .input2c({{36{1'b0}}, input2[63:36]}), .input2d({64{1'b0}}),
    .greater1(comparatoru256bit_71_greater1), .equal1(comparatoru256bit_71_equal1));  // open: less1
  subtractor256bit subtractor256bit_72 (
    .input1a(subtractor256bit_70_output1a), .input1b(subtractor256bit_70_output1b),
    .input1c(subtractor256bit_70_output1c), .input1d(subtractor256bit_70_output1d),
    .input2a(cbuffer256bit_72_output1a), .input2b(cbuffer256bit_72_output1b),
    .input2c(cbuffer256bit_72_output1c), .input2d(cbuffer256bit_72_output1d),
    .output1a(subtractor256bit_72_output1a), .output1b(subtractor256bit_72_output1b),
    .output1c(subtractor256bit_72_output1c), .output1d(subtractor256bit_72_output1d));  // open: inborrow, borrow
  cbuffer256bit cbuffer256bit_72 (
    .buffer1(output1[28]), .input1a({input2[35:0], {28{1'b0}}}), .input1b({{36{1'b0}}, input2[63:36]}),
    .input1c({64{1'b0}}), .input1d({64{1'b0}}), .output1a(cbuffer256bit_72_output1a),
    .output1b(cbuffer256bit_72_output1b), .output1c(cbuffer256bit_72_output1c),
    .output1d(cbuffer256bit_72_output1d));
  and and_72 (output1[28], not_1_out, or_72_out);
  or or_72 (or_72_out, comparatoru256bit_72_greater1, comparatoru256bit_72_equal1);
  comparatoru256bit comparatoru256bit_72 (
    .input1a(subtractor256bit_70_output1a), .input1b(subtractor256bit_70_output1b),
    .input1c(subtractor256bit_70_output1c), .input1d(subtractor256bit_70_output1d),
    .input2a({input2[35:0], {28{1'b0}}}), .input2b({{36{1'b0}}, input2[63:36]}), .input2c({64{1'b0}}),
    .input2d({64{1'b0}}), .greater1(comparatoru256bit_72_greater1), .equal1(comparatoru256bit_72_equal1));  // open: less1
  subtractor256bit subtractor256bit_73 (
    .input1a(subtractor256bit_71_output1a), .input1b(subtractor256bit_71_output1b),
    .input1c(subtractor256bit_71_output1c), .input1d(subtractor256bit_71_output1d),
    .input2a(cbuffer256bit_73_output1a), .input2b(cbuffer256bit_73_output1b),
    .input2c(cbuffer256bit_73_output1c), .input2d(cbuffer256bit_73_output1d),
    .output1a(subtractor256bit_73_output1a), .output1b(subtractor256bit_73_output1b),
    .output1c(subtractor256bit_73_output1c), .output1d(subtractor256bit_73_output1d));  // open: inborrow, borrow
  cbuffer256bit cbuffer256bit_73 (
    .buffer1(and_127_out[27]), .input1a({64{1'b0}}), .input1b({input2[36:0], {27{1'b0}}}),
    .input1c({{37{1'b0}}, input2[63:37]}), .input1d({64{1'b0}}), .output1a(cbuffer256bit_73_output1a),
    .output1b(cbuffer256bit_73_output1b), .output1c(cbuffer256bit_73_output1c),
    .output1d(cbuffer256bit_73_output1d));
  and and_73 (and_127_out[27], not_1_out, or_73_out);
  or or_73 (or_73_out, comparatoru256bit_73_greater1, comparatoru256bit_73_equal1);
  comparatoru256bit comparatoru256bit_73 (
    .input1a(subtractor256bit_71_output1a), .input1b(subtractor256bit_71_output1b),
    .input1c(subtractor256bit_71_output1c), .input1d(subtractor256bit_71_output1d), .input2a({64{1'b0}}),
    .input2b({input2[36:0], {27{1'b0}}}), .input2c({{37{1'b0}}, input2[63:37]}), .input2d({64{1'b0}}),
    .greater1(comparatoru256bit_73_greater1), .equal1(comparatoru256bit_73_equal1));  // open: less1
  subtractor256bit subtractor256bit_74 (
    .input1a(subtractor256bit_72_output1a), .input1b(subtractor256bit_72_output1b),
    .input1c(subtractor256bit_72_output1c), .input1d(subtractor256bit_72_output1d),
    .input2a(cbuffer256bit_74_output1a), .input2b(cbuffer256bit_74_output1b),
    .input2c(cbuffer256bit_74_output1c), .input2d(cbuffer256bit_74_output1d),
    .output1a(subtractor256bit_74_output1a), .output1b(subtractor256bit_74_output1b),
    .output1c(subtractor256bit_74_output1c), .output1d(subtractor256bit_74_output1d));  // open: inborrow, borrow
  cbuffer256bit cbuffer256bit_74 (
    .buffer1(output1[27]), .input1a({input2[36:0], {27{1'b0}}}), .input1b({{37{1'b0}}, input2[63:37]}),
    .input1c({64{1'b0}}), .input1d({64{1'b0}}), .output1a(cbuffer256bit_74_output1a),
    .output1b(cbuffer256bit_74_output1b), .output1c(cbuffer256bit_74_output1c),
    .output1d(cbuffer256bit_74_output1d));
  and and_74 (output1[27], not_1_out, or_74_out);
  or or_74 (or_74_out, comparatoru256bit_74_greater1, comparatoru256bit_74_equal1);
  comparatoru256bit comparatoru256bit_74 (
    .input1a(subtractor256bit_72_output1a), .input1b(subtractor256bit_72_output1b),
    .input1c(subtractor256bit_72_output1c), .input1d(subtractor256bit_72_output1d),
    .input2a({input2[36:0], {27{1'b0}}}), .input2b({{37{1'b0}}, input2[63:37]}), .input2c({64{1'b0}}),
    .input2d({64{1'b0}}), .greater1(comparatoru256bit_74_greater1), .equal1(comparatoru256bit_74_equal1));  // open: less1
  subtractor256bit subtractor256bit_75 (
    .input1a(subtractor256bit_73_output1a), .input1b(subtractor256bit_73_output1b),
    .input1c(subtractor256bit_73_output1c), .input1d(subtractor256bit_73_output1d),
    .input2a(cbuffer256bit_75_output1a), .input2b(cbuffer256bit_75_output1b),
    .input2c(cbuffer256bit_75_output1c), .input2d(cbuffer256bit_75_output1d),
    .output1a(subtractor256bit_75_output1a), .output1b(subtractor256bit_75_output1b),
    .output1c(subtractor256bit_75_output1c), .output1d(subtractor256bit_75_output1d));  // open: inborrow, borrow
  cbuffer256bit cbuffer256bit_75 (
    .buffer1(and_127_out[26]), .input1a({64{1'b0}}), .input1b({input2[37:0], {26{1'b0}}}),
    .input1c({{38{1'b0}}, input2[63:38]}), .input1d({64{1'b0}}), .output1a(cbuffer256bit_75_output1a),
    .output1b(cbuffer256bit_75_output1b), .output1c(cbuffer256bit_75_output1c),
    .output1d(cbuffer256bit_75_output1d));
  and and_75 (and_127_out[26], not_1_out, or_75_out);
  or or_75 (or_75_out, comparatoru256bit_75_greater1, comparatoru256bit_75_equal1);
  comparatoru256bit comparatoru256bit_75 (
    .input1a(subtractor256bit_73_output1a), .input1b(subtractor256bit_73_output1b),
    .input1c(subtractor256bit_73_output1c), .input1d(subtractor256bit_73_output1d), .input2a({64{1'b0}}),
    .input2b({input2[37:0], {26{1'b0}}}), .input2c({{38{1'b0}}, input2[63:38]}), .input2d({64{1'b0}}),
    .greater1(comparatoru256bit_75_greater1), .equal1(comparatoru256bit_75_equal1));  // open: less1
  subtractor256bit subtractor256bit_76 (
    .input1a(subtractor256bit_74_output1a), .input1b(subtractor256bit_74_output1b),
    .input1c(subtractor256bit_74_output1c), .input1d(subtractor256bit_74_output1d),
    .input2a(cbuffer256bit_76_output1a), .input2b(cbuffer256bit_76_output1b),
    .input2c(cbuffer256bit_76_output1c), .input2d(cbuffer256bit_76_output1d),
    .output1a(subtractor256bit_76_output1a), .output1b(subtractor256bit_76_output1b),
    .output1c(subtractor256bit_76_output1c), .output1d(subtractor256bit_76_output1d));  // open: inborrow, borrow
  cbuffer256bit cbuffer256bit_76 (
    .buffer1(output1[26]), .input1a({input2[37:0], {26{1'b0}}}), .input1b({{38{1'b0}}, input2[63:38]}),
    .input1c({64{1'b0}}), .input1d({64{1'b0}}), .output1a(cbuffer256bit_76_output1a),
    .output1b(cbuffer256bit_76_output1b), .output1c(cbuffer256bit_76_output1c),
    .output1d(cbuffer256bit_76_output1d));
  and and_76 (output1[26], not_1_out, or_76_out);
  or or_76 (or_76_out, comparatoru256bit_76_greater1, comparatoru256bit_76_equal1);
  comparatoru256bit comparatoru256bit_76 (
    .input1a(subtractor256bit_74_output1a), .input1b(subtractor256bit_74_output1b),
    .input1c(subtractor256bit_74_output1c), .input1d(subtractor256bit_74_output1d),
    .input2a({input2[37:0], {26{1'b0}}}), .input2b({{38{1'b0}}, input2[63:38]}), .input2c({64{1'b0}}),
    .input2d({64{1'b0}}), .greater1(comparatoru256bit_76_greater1), .equal1(comparatoru256bit_76_equal1));  // open: less1
  subtractor256bit subtractor256bit_77 (
    .input1a(subtractor256bit_75_output1a), .input1b(subtractor256bit_75_output1b),
    .input1c(subtractor256bit_75_output1c), .input1d(subtractor256bit_75_output1d),
    .input2a(cbuffer256bit_77_output1a), .input2b(cbuffer256bit_77_output1b),
    .input2c(cbuffer256bit_77_output1c), .input2d(cbuffer256bit_77_output1d),
    .output1a(subtractor256bit_77_output1a), .output1b(subtractor256bit_77_output1b),
    .output1c(subtractor256bit_77_output1c), .output1d(subtractor256bit_77_output1d));  // open: inborrow, borrow
  cbuffer256bit cbuffer256bit_77 (
    .buffer1(and_127_out[25]), .input1a({64{1'b0}}), .input1b({input2[38:0], {25{1'b0}}}),
    .input1c({{39{1'b0}}, input2[63:39]}), .input1d({64{1'b0}}), .output1a(cbuffer256bit_77_output1a),
    .output1b(cbuffer256bit_77_output1b), .output1c(cbuffer256bit_77_output1c),
    .output1d(cbuffer256bit_77_output1d));
  and and_77 (and_127_out[25], not_1_out, or_77_out);
  comparatoru256bit comparatoru256bit_77 (
    .input1a(subtractor256bit_75_output1a), .input1b(subtractor256bit_75_output1b),
    .input1c(subtractor256bit_75_output1c), .input1d(subtractor256bit_75_output1d), .input2a({64{1'b0}}),
    .input2b({input2[38:0], {25{1'b0}}}), .input2c({{39{1'b0}}, input2[63:39]}), .input2d({64{1'b0}}),
    .greater1(comparatoru256bit_77_greater1), .equal1(comparatoru256bit_77_equal1));  // open: less1
  subtractor256bit subtractor256bit_78 (
    .input1a(subtractor256bit_76_output1a), .input1b(subtractor256bit_76_output1b),
    .input1c(subtractor256bit_76_output1c), .input1d(subtractor256bit_76_output1d),
    .input2a(cbuffer256bit_78_output1a), .input2b(cbuffer256bit_78_output1b),
    .input2c(cbuffer256bit_78_output1c), .input2d(cbuffer256bit_78_output1d),
    .output1a(subtractor256bit_78_output1a), .output1b(subtractor256bit_78_output1b),
    .output1c(subtractor256bit_78_output1c), .output1d(subtractor256bit_78_output1d));  // open: inborrow, borrow
  cbuffer256bit cbuffer256bit_78 (
    .buffer1(output1[25]), .input1a({input2[38:0], {25{1'b0}}}), .input1b({{39{1'b0}}, input2[63:39]}),
    .input1c({64{1'b0}}), .input1d({64{1'b0}}), .output1a(cbuffer256bit_78_output1a),
    .output1b(cbuffer256bit_78_output1b), .output1c(cbuffer256bit_78_output1c),
    .output1d(cbuffer256bit_78_output1d));
  and and_78 (output1[25], not_1_out, or_78_out);
  or or_77 (or_77_out, comparatoru256bit_77_greater1, comparatoru256bit_77_equal1);
  or or_78 (or_78_out, comparatoru256bit_78_greater1, comparatoru256bit_78_equal1);
  comparatoru256bit comparatoru256bit_78 (
    .input1a(subtractor256bit_76_output1a), .input1b(subtractor256bit_76_output1b),
    .input1c(subtractor256bit_76_output1c), .input1d(subtractor256bit_76_output1d),
    .input2a({input2[38:0], {25{1'b0}}}), .input2b({{39{1'b0}}, input2[63:39]}), .input2c({64{1'b0}}),
    .input2d({64{1'b0}}), .greater1(comparatoru256bit_78_greater1), .equal1(comparatoru256bit_78_equal1));  // open: less1
  subtractor256bit subtractor256bit_79 (
    .input1a(subtractor256bit_77_output1a), .input1b(subtractor256bit_77_output1b),
    .input1c(subtractor256bit_77_output1c), .input1d(subtractor256bit_77_output1d),
    .input2a(cbuffer256bit_79_output1a), .input2b(cbuffer256bit_79_output1b),
    .input2c(cbuffer256bit_79_output1c), .input2d(cbuffer256bit_79_output1d),
    .output1a(subtractor256bit_79_output1a), .output1b(subtractor256bit_79_output1b),
    .output1c(subtractor256bit_79_output1c), .output1d(subtractor256bit_79_output1d));  // open: inborrow, borrow
  cbuffer256bit cbuffer256bit_79 (
    .buffer1(and_127_out[24]), .input1a({64{1'b0}}), .input1b({input2[39:0], {24{1'b0}}}),
    .input1c({{40{1'b0}}, input2[63:40]}), .input1d({64{1'b0}}), .output1a(cbuffer256bit_79_output1a),
    .output1b(cbuffer256bit_79_output1b), .output1c(cbuffer256bit_79_output1c),
    .output1d(cbuffer256bit_79_output1d));
  and and_79 (and_127_out[24], not_1_out, or_79_out);
  or or_79 (or_79_out, comparatoru256bit_79_greater1, comparatoru256bit_79_equal1);
  comparatoru256bit comparatoru256bit_79 (
    .input1a(subtractor256bit_77_output1a), .input1b(subtractor256bit_77_output1b),
    .input1c(subtractor256bit_77_output1c), .input1d(subtractor256bit_77_output1d), .input2a({64{1'b0}}),
    .input2b({input2[39:0], {24{1'b0}}}), .input2c({{40{1'b0}}, input2[63:40]}), .input2d({64{1'b0}}),
    .greater1(comparatoru256bit_79_greater1), .equal1(comparatoru256bit_79_equal1));  // open: less1
  subtractor256bit subtractor256bit_80 (
    .input1a(subtractor256bit_78_output1a), .input1b(subtractor256bit_78_output1b),
    .input1c(subtractor256bit_78_output1c), .input1d(subtractor256bit_78_output1d),
    .input2a(cbuffer256bit_80_output1a), .input2b(cbuffer256bit_80_output1b),
    .input2c(cbuffer256bit_80_output1c), .input2d(cbuffer256bit_80_output1d),
    .output1a(subtractor256bit_80_output1a), .output1b(subtractor256bit_80_output1b),
    .output1c(subtractor256bit_80_output1c), .output1d(subtractor256bit_80_output1d));  // open: inborrow, borrow
  cbuffer256bit cbuffer256bit_80 (
    .buffer1(output1[24]), .input1a({input2[39:0], {24{1'b0}}}), .input1b({{40{1'b0}}, input2[63:40]}),
    .input1c({64{1'b0}}), .input1d({64{1'b0}}), .output1a(cbuffer256bit_80_output1a),
    .output1b(cbuffer256bit_80_output1b), .output1c(cbuffer256bit_80_output1c),
    .output1d(cbuffer256bit_80_output1d));
  and and_80 (output1[24], not_1_out, or_80_out);
  or or_80 (or_80_out, comparatoru256bit_80_greater1, comparatoru256bit_80_equal1);
  comparatoru256bit comparatoru256bit_80 (
    .input1a(subtractor256bit_78_output1a), .input1b(subtractor256bit_78_output1b),
    .input1c(subtractor256bit_78_output1c), .input1d(subtractor256bit_78_output1d),
    .input2a({input2[39:0], {24{1'b0}}}), .input2b({{40{1'b0}}, input2[63:40]}), .input2c({64{1'b0}}),
    .input2d({64{1'b0}}), .greater1(comparatoru256bit_80_greater1), .equal1(comparatoru256bit_80_equal1));  // open: less1
  subtractor256bit subtractor256bit_81 (
    .input1a(subtractor256bit_79_output1a), .input1b(subtractor256bit_79_output1b),
    .input1c(subtractor256bit_79_output1c), .input1d(subtractor256bit_79_output1d),
    .input2a(cbuffer256bit_81_output1a), .input2b(cbuffer256bit_81_output1b),
    .input2c(cbuffer256bit_81_output1c), .input2d(cbuffer256bit_81_output1d),
    .output1a(subtractor256bit_81_output1a), .output1b(subtractor256bit_81_output1b),
    .output1c(subtractor256bit_81_output1c), .output1d(subtractor256bit_81_output1d));  // open: inborrow, borrow
  cbuffer256bit cbuffer256bit_81 (
    .buffer1(and_127_out[23]), .input1a({64{1'b0}}), .input1b({input2[40:0], {23{1'b0}}}),
    .input1c({{41{1'b0}}, input2[63:41]}), .input1d({64{1'b0}}), .output1a(cbuffer256bit_81_output1a),
    .output1b(cbuffer256bit_81_output1b), .output1c(cbuffer256bit_81_output1c),
    .output1d(cbuffer256bit_81_output1d));
  and and_81 (and_127_out[23], not_1_out, or_81_out);
  or or_81 (or_81_out, comparatoru256bit_81_greater1, comparatoru256bit_81_equal1);
  comparatoru256bit comparatoru256bit_81 (
    .input1a(subtractor256bit_79_output1a), .input1b(subtractor256bit_79_output1b),
    .input1c(subtractor256bit_79_output1c), .input1d(subtractor256bit_79_output1d), .input2a({64{1'b0}}),
    .input2b({input2[40:0], {23{1'b0}}}), .input2c({{41{1'b0}}, input2[63:41]}), .input2d({64{1'b0}}),
    .greater1(comparatoru256bit_81_greater1), .equal1(comparatoru256bit_81_equal1));  // open: less1
  subtractor256bit subtractor256bit_82 (
    .input1a(subtractor256bit_80_output1a), .input1b(subtractor256bit_80_output1b),
    .input1c(subtractor256bit_80_output1c), .input1d(subtractor256bit_80_output1d),
    .input2a(cbuffer256bit_82_output1a), .input2b(cbuffer256bit_82_output1b),
    .input2c(cbuffer256bit_82_output1c), .input2d(cbuffer256bit_82_output1d),
    .output1a(subtractor256bit_82_output1a), .output1b(subtractor256bit_82_output1b),
    .output1c(subtractor256bit_82_output1c), .output1d(subtractor256bit_82_output1d));  // open: inborrow, borrow
  cbuffer256bit cbuffer256bit_82 (
    .buffer1(output1[23]), .input1a({input2[40:0], {23{1'b0}}}), .input1b({{41{1'b0}}, input2[63:41]}),
    .input1c({64{1'b0}}), .input1d({64{1'b0}}), .output1a(cbuffer256bit_82_output1a),
    .output1b(cbuffer256bit_82_output1b), .output1c(cbuffer256bit_82_output1c),
    .output1d(cbuffer256bit_82_output1d));
  and and_82 (output1[23], not_1_out, or_82_out);
  or or_82 (or_82_out, comparatoru256bit_82_greater1, comparatoru256bit_82_equal1);
  comparatoru256bit comparatoru256bit_82 (
    .input1a(subtractor256bit_80_output1a), .input1b(subtractor256bit_80_output1b),
    .input1c(subtractor256bit_80_output1c), .input1d(subtractor256bit_80_output1d),
    .input2a({input2[40:0], {23{1'b0}}}), .input2b({{41{1'b0}}, input2[63:41]}), .input2c({64{1'b0}}),
    .input2d({64{1'b0}}), .greater1(comparatoru256bit_82_greater1), .equal1(comparatoru256bit_82_equal1));  // open: less1
  subtractor256bit subtractor256bit_83 (
    .input1a(subtractor256bit_81_output1a), .input1b(subtractor256bit_81_output1b),
    .input1c(subtractor256bit_81_output1c), .input1d(subtractor256bit_81_output1d),
    .input2a(cbuffer256bit_83_output1a), .input2b(cbuffer256bit_83_output1b),
    .input2c(cbuffer256bit_83_output1c), .input2d(cbuffer256bit_83_output1d),
    .output1a(subtractor256bit_83_output1a), .output1b(subtractor256bit_83_output1b),
    .output1c(subtractor256bit_83_output1c), .output1d(subtractor256bit_83_output1d));  // open: inborrow, borrow
  cbuffer256bit cbuffer256bit_83 (
    .buffer1(and_127_out[22]), .input1a({64{1'b0}}), .input1b({input2[41:0], {22{1'b0}}}),
    .input1c({{42{1'b0}}, input2[63:42]}), .input1d({64{1'b0}}), .output1a(cbuffer256bit_83_output1a),
    .output1b(cbuffer256bit_83_output1b), .output1c(cbuffer256bit_83_output1c),
    .output1d(cbuffer256bit_83_output1d));
  and and_83 (and_127_out[22], not_1_out, or_83_out);
  or or_83 (or_83_out, comparatoru256bit_83_greater1, comparatoru256bit_83_equal1);
  comparatoru256bit comparatoru256bit_83 (
    .input1a(subtractor256bit_81_output1a), .input1b(subtractor256bit_81_output1b),
    .input1c(subtractor256bit_81_output1c), .input1d(subtractor256bit_81_output1d), .input2a({64{1'b0}}),
    .input2b({input2[41:0], {22{1'b0}}}), .input2c({{42{1'b0}}, input2[63:42]}), .input2d({64{1'b0}}),
    .greater1(comparatoru256bit_83_greater1), .equal1(comparatoru256bit_83_equal1));  // open: less1
  subtractor256bit subtractor256bit_84 (
    .input1a(subtractor256bit_82_output1a), .input1b(subtractor256bit_82_output1b),
    .input1c(subtractor256bit_82_output1c), .input1d(subtractor256bit_82_output1d),
    .input2a(cbuffer256bit_84_output1a), .input2b(cbuffer256bit_84_output1b),
    .input2c(cbuffer256bit_84_output1c), .input2d(cbuffer256bit_84_output1d),
    .output1a(subtractor256bit_84_output1a), .output1b(subtractor256bit_84_output1b),
    .output1c(subtractor256bit_84_output1c), .output1d(subtractor256bit_84_output1d));  // open: inborrow, borrow
  cbuffer256bit cbuffer256bit_84 (
    .buffer1(output1[22]), .input1a({input2[41:0], {22{1'b0}}}), .input1b({{42{1'b0}}, input2[63:42]}),
    .input1c({64{1'b0}}), .input1d({64{1'b0}}), .output1a(cbuffer256bit_84_output1a),
    .output1b(cbuffer256bit_84_output1b), .output1c(cbuffer256bit_84_output1c),
    .output1d(cbuffer256bit_84_output1d));
  and and_84 (output1[22], not_1_out, or_84_out);
  comparatoru256bit comparatoru256bit_84 (
    .input1a(subtractor256bit_82_output1a), .input1b(subtractor256bit_82_output1b),
    .input1c(subtractor256bit_82_output1c), .input1d(subtractor256bit_82_output1d),
    .input2a({input2[41:0], {22{1'b0}}}), .input2b({{42{1'b0}}, input2[63:42]}), .input2c({64{1'b0}}),
    .input2d({64{1'b0}}), .greater1(comparatoru256bit_84_greater1), .equal1(comparatoru256bit_84_equal1));  // open: less1
  or or_84 (or_84_out, comparatoru256bit_84_greater1, comparatoru256bit_84_equal1);
  subtractor256bit subtractor256bit_85 (
    .input1a(subtractor256bit_83_output1a), .input1b(subtractor256bit_83_output1b),
    .input1c(subtractor256bit_83_output1c), .input1d(subtractor256bit_83_output1d),
    .input2a(cbuffer256bit_85_output1a), .input2b(cbuffer256bit_85_output1b),
    .input2c(cbuffer256bit_85_output1c), .input2d(cbuffer256bit_85_output1d),
    .output1a(subtractor256bit_85_output1a), .output1b(subtractor256bit_85_output1b),
    .output1c(subtractor256bit_85_output1c), .output1d(subtractor256bit_85_output1d));  // open: inborrow, borrow
  cbuffer256bit cbuffer256bit_85 (
    .buffer1(and_127_out[21]), .input1a({64{1'b0}}), .input1b({input2[42:0], {21{1'b0}}}),
    .input1c({{43{1'b0}}, input2[63:43]}), .input1d({64{1'b0}}), .output1a(cbuffer256bit_85_output1a),
    .output1b(cbuffer256bit_85_output1b), .output1c(cbuffer256bit_85_output1c),
    .output1d(cbuffer256bit_85_output1d));
  and and_85 (and_127_out[21], not_1_out, or_85_out);
  or or_85 (or_85_out, comparatoru256bit_85_greater1, comparatoru256bit_85_equal1);
  comparatoru256bit comparatoru256bit_85 (
    .input1a(subtractor256bit_83_output1a), .input1b(subtractor256bit_83_output1b),
    .input1c(subtractor256bit_83_output1c), .input1d(subtractor256bit_83_output1d), .input2a({64{1'b0}}),
    .input2b({input2[42:0], {21{1'b0}}}), .input2c({{43{1'b0}}, input2[63:43]}), .input2d({64{1'b0}}),
    .greater1(comparatoru256bit_85_greater1), .equal1(comparatoru256bit_85_equal1));  // open: less1
  subtractor256bit subtractor256bit_86 (
    .input1a(subtractor256bit_84_output1a), .input1b(subtractor256bit_84_output1b),
    .input1c(subtractor256bit_84_output1c), .input1d(subtractor256bit_84_output1d),
    .input2a(cbuffer256bit_86_output1a), .input2b(cbuffer256bit_86_output1b),
    .input2c(cbuffer256bit_86_output1c), .input2d(cbuffer256bit_86_output1d),
    .output1a(subtractor256bit_86_output1a), .output1b(subtractor256bit_86_output1b),
    .output1c(subtractor256bit_86_output1c), .output1d(subtractor256bit_86_output1d));  // open: inborrow, borrow
  cbuffer256bit cbuffer256bit_86 (
    .buffer1(output1[21]), .input1a({input2[42:0], {21{1'b0}}}), .input1b({{43{1'b0}}, input2[63:43]}),
    .input1c({64{1'b0}}), .input1d({64{1'b0}}), .output1a(cbuffer256bit_86_output1a),
    .output1b(cbuffer256bit_86_output1b), .output1c(cbuffer256bit_86_output1c),
    .output1d(cbuffer256bit_86_output1d));
  and and_86 (output1[21], not_1_out, or_86_out);
  or or_86 (or_86_out, comparatoru256bit_86_greater1, comparatoru256bit_86_equal1);
  comparatoru256bit comparatoru256bit_86 (
    .input1a(subtractor256bit_84_output1a), .input1b(subtractor256bit_84_output1b),
    .input1c(subtractor256bit_84_output1c), .input1d(subtractor256bit_84_output1d),
    .input2a({input2[42:0], {21{1'b0}}}), .input2b({{43{1'b0}}, input2[63:43]}), .input2c({64{1'b0}}),
    .input2d({64{1'b0}}), .greater1(comparatoru256bit_86_greater1), .equal1(comparatoru256bit_86_equal1));  // open: less1
  subtractor256bit subtractor256bit_87 (
    .input1a(subtractor256bit_85_output1a), .input1b(subtractor256bit_85_output1b),
    .input1c(subtractor256bit_85_output1c), .input1d(subtractor256bit_85_output1d),
    .input2a(cbuffer256bit_87_output1a), .input2b(cbuffer256bit_87_output1b),
    .input2c(cbuffer256bit_87_output1c), .input2d(cbuffer256bit_87_output1d),
    .output1a(subtractor256bit_87_output1a), .output1b(subtractor256bit_87_output1b),
    .output1c(subtractor256bit_87_output1c), .output1d(subtractor256bit_87_output1d));  // open: inborrow, borrow
  cbuffer256bit cbuffer256bit_87 (
    .buffer1(and_127_out[20]), .input1a({64{1'b0}}), .input1b({input2[43:0], {20{1'b0}}}),
    .input1c({{44{1'b0}}, input2[63:44]}), .input1d({64{1'b0}}), .output1a(cbuffer256bit_87_output1a),
    .output1b(cbuffer256bit_87_output1b), .output1c(cbuffer256bit_87_output1c),
    .output1d(cbuffer256bit_87_output1d));
  and and_87 (and_127_out[20], not_1_out, or_87_out);
  or or_87 (or_87_out, comparatoru256bit_87_greater1, comparatoru256bit_87_equal1);
  comparatoru256bit comparatoru256bit_87 (
    .input1a(subtractor256bit_85_output1a), .input1b(subtractor256bit_85_output1b),
    .input1c(subtractor256bit_85_output1c), .input1d(subtractor256bit_85_output1d), .input2a({64{1'b0}}),
    .input2b({input2[43:0], {20{1'b0}}}), .input2c({{44{1'b0}}, input2[63:44]}), .input2d({64{1'b0}}),
    .greater1(comparatoru256bit_87_greater1), .equal1(comparatoru256bit_87_equal1));  // open: less1
  subtractor256bit subtractor256bit_88 (
    .input1a(subtractor256bit_86_output1a), .input1b(subtractor256bit_86_output1b),
    .input1c(subtractor256bit_86_output1c), .input1d(subtractor256bit_86_output1d),
    .input2a(cbuffer256bit_88_output1a), .input2b(cbuffer256bit_88_output1b),
    .input2c(cbuffer256bit_88_output1c), .input2d(cbuffer256bit_88_output1d),
    .output1a(subtractor256bit_88_output1a), .output1b(subtractor256bit_88_output1b),
    .output1c(subtractor256bit_88_output1c), .output1d(subtractor256bit_88_output1d));  // open: inborrow, borrow
  cbuffer256bit cbuffer256bit_88 (
    .buffer1(output1[20]), .input1a({input2[43:0], {20{1'b0}}}), .input1b({{44{1'b0}}, input2[63:44]}),
    .input1c({64{1'b0}}), .input1d({64{1'b0}}), .output1a(cbuffer256bit_88_output1a),
    .output1b(cbuffer256bit_88_output1b), .output1c(cbuffer256bit_88_output1c),
    .output1d(cbuffer256bit_88_output1d));
  and and_88 (output1[20], not_1_out, or_88_out);
  or or_88 (or_88_out, comparatoru256bit_88_greater1, comparatoru256bit_88_equal1);
  comparatoru256bit comparatoru256bit_88 (
    .input1a(subtractor256bit_86_output1a), .input1b(subtractor256bit_86_output1b),
    .input1c(subtractor256bit_86_output1c), .input1d(subtractor256bit_86_output1d),
    .input2a({input2[43:0], {20{1'b0}}}), .input2b({{44{1'b0}}, input2[63:44]}), .input2c({64{1'b0}}),
    .input2d({64{1'b0}}), .greater1(comparatoru256bit_88_greater1), .equal1(comparatoru256bit_88_equal1));  // open: less1
  subtractor256bit subtractor256bit_89 (
    .input1a(subtractor256bit_87_output1a), .input1b(subtractor256bit_87_output1b),
    .input1c(subtractor256bit_87_output1c), .input1d(subtractor256bit_87_output1d),
    .input2a(cbuffer256bit_89_output1a), .input2b(cbuffer256bit_89_output1b),
    .input2c(cbuffer256bit_89_output1c), .input2d(cbuffer256bit_89_output1d),
    .output1a(subtractor256bit_89_output1a), .output1b(subtractor256bit_89_output1b),
    .output1c(subtractor256bit_89_output1c), .output1d(subtractor256bit_89_output1d));  // open: inborrow, borrow
  cbuffer256bit cbuffer256bit_89 (
    .buffer1(and_127_out[19]), .input1a({64{1'b0}}), .input1b({input2[44:0], {19{1'b0}}}),
    .input1c({{45{1'b0}}, input2[63:45]}), .input1d({64{1'b0}}), .output1a(cbuffer256bit_89_output1a),
    .output1b(cbuffer256bit_89_output1b), .output1c(cbuffer256bit_89_output1c),
    .output1d(cbuffer256bit_89_output1d));
  and and_89 (and_127_out[19], not_1_out, or_89_out);
  or or_89 (or_89_out, comparatoru256bit_89_greater1, comparatoru256bit_89_equal1);
  comparatoru256bit comparatoru256bit_89 (
    .input1a(subtractor256bit_87_output1a), .input1b(subtractor256bit_87_output1b),
    .input1c(subtractor256bit_87_output1c), .input1d(subtractor256bit_87_output1d), .input2a({64{1'b0}}),
    .input2b({input2[44:0], {19{1'b0}}}), .input2c({{45{1'b0}}, input2[63:45]}), .input2d({64{1'b0}}),
    .greater1(comparatoru256bit_89_greater1), .equal1(comparatoru256bit_89_equal1));  // open: less1
  subtractor256bit subtractor256bit_90 (
    .input1a(subtractor256bit_88_output1a), .input1b(subtractor256bit_88_output1b),
    .input1c(subtractor256bit_88_output1c), .input1d(subtractor256bit_88_output1d),
    .input2a(cbuffer256bit_90_output1a), .input2b(cbuffer256bit_90_output1b),
    .input2c(cbuffer256bit_90_output1c), .input2d(cbuffer256bit_90_output1d),
    .output1a(subtractor256bit_90_output1a), .output1b(subtractor256bit_90_output1b),
    .output1c(subtractor256bit_90_output1c), .output1d(subtractor256bit_90_output1d));  // open: inborrow, borrow
  cbuffer256bit cbuffer256bit_90 (
    .buffer1(output1[19]), .input1a({input2[44:0], {19{1'b0}}}), .input1b({{45{1'b0}}, input2[63:45]}),
    .input1c({64{1'b0}}), .input1d({64{1'b0}}), .output1a(cbuffer256bit_90_output1a),
    .output1b(cbuffer256bit_90_output1b), .output1c(cbuffer256bit_90_output1c),
    .output1d(cbuffer256bit_90_output1d));
  and and_90 (output1[19], not_1_out, or_90_out);
  or or_90 (or_90_out, comparatoru256bit_90_greater1, comparatoru256bit_90_equal1);
  comparatoru256bit comparatoru256bit_90 (
    .input1a(subtractor256bit_88_output1a), .input1b(subtractor256bit_88_output1b),
    .input1c(subtractor256bit_88_output1c), .input1d(subtractor256bit_88_output1d),
    .input2a({input2[44:0], {19{1'b0}}}), .input2b({{45{1'b0}}, input2[63:45]}), .input2c({64{1'b0}}),
    .input2d({64{1'b0}}), .greater1(comparatoru256bit_90_greater1), .equal1(comparatoru256bit_90_equal1));  // open: less1
  subtractor256bit subtractor256bit_91 (
    .input1a(subtractor256bit_89_output1a), .input1b(subtractor256bit_89_output1b),
    .input1c(subtractor256bit_89_output1c), .input1d(subtractor256bit_89_output1d),
    .input2a(cbuffer256bit_91_output1a), .input2b(cbuffer256bit_91_output1b),
    .input2c(cbuffer256bit_91_output1c), .input2d(cbuffer256bit_91_output1d),
    .output1a(subtractor256bit_91_output1a), .output1b(subtractor256bit_91_output1b),
    .output1c(subtractor256bit_91_output1c), .output1d(subtractor256bit_91_output1d));  // open: inborrow, borrow
  cbuffer256bit cbuffer256bit_91 (
    .buffer1(and_127_out[18]), .input1a({64{1'b0}}), .input1b({input2[45:0], {18{1'b0}}}),
    .input1c({{46{1'b0}}, input2[63:46]}), .input1d({64{1'b0}}), .output1a(cbuffer256bit_91_output1a),
    .output1b(cbuffer256bit_91_output1b), .output1c(cbuffer256bit_91_output1c),
    .output1d(cbuffer256bit_91_output1d));
  and and_91 (and_127_out[18], not_1_out, or_91_out);
  or or_91 (or_91_out, comparatoru256bit_91_greater1, comparatoru256bit_91_equal1);
  comparatoru256bit comparatoru256bit_91 (
    .input1a(subtractor256bit_89_output1a), .input1b(subtractor256bit_89_output1b),
    .input1c(subtractor256bit_89_output1c), .input1d(subtractor256bit_89_output1d), .input2a({64{1'b0}}),
    .input2b({input2[45:0], {18{1'b0}}}), .input2c({{46{1'b0}}, input2[63:46]}), .input2d({64{1'b0}}),
    .greater1(comparatoru256bit_91_greater1), .equal1(comparatoru256bit_91_equal1));  // open: less1
  subtractor256bit subtractor256bit_92 (
    .input1a(subtractor256bit_90_output1a), .input1b(subtractor256bit_90_output1b),
    .input1c(subtractor256bit_90_output1c), .input1d(subtractor256bit_90_output1d),
    .input2a(cbuffer256bit_92_output1a), .input2b(cbuffer256bit_92_output1b),
    .input2c(cbuffer256bit_92_output1c), .input2d(cbuffer256bit_92_output1d),
    .output1a(subtractor256bit_92_output1a), .output1b(subtractor256bit_92_output1b),
    .output1c(subtractor256bit_92_output1c), .output1d(subtractor256bit_92_output1d));  // open: inborrow, borrow
  cbuffer256bit cbuffer256bit_92 (
    .buffer1(output1[18]), .input1a({input2[45:0], {18{1'b0}}}), .input1b({{46{1'b0}}, input2[63:46]}),
    .input1c({64{1'b0}}), .input1d({64{1'b0}}), .output1a(cbuffer256bit_92_output1a),
    .output1b(cbuffer256bit_92_output1b), .output1c(cbuffer256bit_92_output1c),
    .output1d(cbuffer256bit_92_output1d));
  and and_92 (output1[18], not_1_out, or_92_out);
  or or_92 (or_92_out, comparatoru256bit_92_greater1, comparatoru256bit_92_equal1);
  comparatoru256bit comparatoru256bit_92 (
    .input1a(subtractor256bit_90_output1a), .input1b(subtractor256bit_90_output1b),
    .input1c(subtractor256bit_90_output1c), .input1d(subtractor256bit_90_output1d),
    .input2a({input2[45:0], {18{1'b0}}}), .input2b({{46{1'b0}}, input2[63:46]}), .input2c({64{1'b0}}),
    .input2d({64{1'b0}}), .greater1(comparatoru256bit_92_greater1), .equal1(comparatoru256bit_92_equal1));  // open: less1
  subtractor256bit subtractor256bit_93 (
    .input1a(subtractor256bit_91_output1a), .input1b(subtractor256bit_91_output1b),
    .input1c(subtractor256bit_91_output1c), .input1d(subtractor256bit_91_output1d),
    .input2a(cbuffer256bit_93_output1a), .input2b(cbuffer256bit_93_output1b),
    .input2c(cbuffer256bit_93_output1c), .input2d(cbuffer256bit_93_output1d),
    .output1a(subtractor256bit_93_output1a), .output1b(subtractor256bit_93_output1b),
    .output1c(subtractor256bit_93_output1c), .output1d(subtractor256bit_93_output1d));  // open: inborrow, borrow
  cbuffer256bit cbuffer256bit_93 (
    .buffer1(and_127_out[17]), .input1a({64{1'b0}}), .input1b({input2[46:0], {17{1'b0}}}),
    .input1c({{47{1'b0}}, input2[63:47]}), .input1d({64{1'b0}}), .output1a(cbuffer256bit_93_output1a),
    .output1b(cbuffer256bit_93_output1b), .output1c(cbuffer256bit_93_output1c),
    .output1d(cbuffer256bit_93_output1d));
  and and_93 (and_127_out[17], not_1_out, or_93_out);
  comparatoru256bit comparatoru256bit_93 (
    .input1a(subtractor256bit_91_output1a), .input1b(subtractor256bit_91_output1b),
    .input1c(subtractor256bit_91_output1c), .input1d(subtractor256bit_91_output1d), .input2a({64{1'b0}}),
    .input2b({input2[46:0], {17{1'b0}}}), .input2c({{47{1'b0}}, input2[63:47]}), .input2d({64{1'b0}}),
    .greater1(comparatoru256bit_93_greater1), .equal1(comparatoru256bit_93_equal1));  // open: less1
  subtractor256bit subtractor256bit_94 (
    .input1a(subtractor256bit_92_output1a), .input1b(subtractor256bit_92_output1b),
    .input1c(subtractor256bit_92_output1c), .input1d(subtractor256bit_92_output1d),
    .input2a(cbuffer256bit_94_output1a), .input2b(cbuffer256bit_94_output1b),
    .input2c(cbuffer256bit_94_output1c), .input2d(cbuffer256bit_94_output1d),
    .output1a(subtractor256bit_94_output1a), .output1b(subtractor256bit_94_output1b),
    .output1c(subtractor256bit_94_output1c), .output1d(subtractor256bit_94_output1d));  // open: inborrow, borrow
  cbuffer256bit cbuffer256bit_94 (
    .buffer1(output1[17]), .input1a({input2[46:0], {17{1'b0}}}), .input1b({{47{1'b0}}, input2[63:47]}),
    .input1c({64{1'b0}}), .input1d({64{1'b0}}), .output1a(cbuffer256bit_94_output1a),
    .output1b(cbuffer256bit_94_output1b), .output1c(cbuffer256bit_94_output1c),
    .output1d(cbuffer256bit_94_output1d));
  and and_94 (output1[17], not_1_out, or_94_out);
  or or_93 (or_93_out, comparatoru256bit_93_greater1, comparatoru256bit_93_equal1);
  or or_94 (or_94_out, comparatoru256bit_94_greater1, comparatoru256bit_94_equal1);
  comparatoru256bit comparatoru256bit_94 (
    .input1a(subtractor256bit_92_output1a), .input1b(subtractor256bit_92_output1b),
    .input1c(subtractor256bit_92_output1c), .input1d(subtractor256bit_92_output1d),
    .input2a({input2[46:0], {17{1'b0}}}), .input2b({{47{1'b0}}, input2[63:47]}), .input2c({64{1'b0}}),
    .input2d({64{1'b0}}), .greater1(comparatoru256bit_94_greater1), .equal1(comparatoru256bit_94_equal1));  // open: less1
  subtractor256bit subtractor256bit_95 (
    .input1a(subtractor256bit_93_output1a), .input1b(subtractor256bit_93_output1b),
    .input1c(subtractor256bit_93_output1c), .input1d(subtractor256bit_93_output1d),
    .input2a(cbuffer256bit_95_output1a), .input2b(cbuffer256bit_95_output1b),
    .input2c(cbuffer256bit_95_output1c), .input2d(cbuffer256bit_95_output1d),
    .output1a(subtractor256bit_95_output1a), .output1b(subtractor256bit_95_output1b),
    .output1c(subtractor256bit_95_output1c), .output1d(subtractor256bit_95_output1d));  // open: inborrow, borrow
  cbuffer256bit cbuffer256bit_95 (
    .buffer1(and_127_out[16]), .input1a({64{1'b0}}), .input1b({input2[47:0], {16{1'b0}}}),
    .input1c({{48{1'b0}}, input2[63:48]}), .input1d({64{1'b0}}), .output1a(cbuffer256bit_95_output1a),
    .output1b(cbuffer256bit_95_output1b), .output1c(cbuffer256bit_95_output1c),
    .output1d(cbuffer256bit_95_output1d));
  and and_95 (and_127_out[16], not_1_out, or_95_out);
  or or_95 (or_95_out, comparatoru256bit_95_greater1, comparatoru256bit_95_equal1);
  comparatoru256bit comparatoru256bit_95 (
    .input1a(subtractor256bit_93_output1a), .input1b(subtractor256bit_93_output1b),
    .input1c(subtractor256bit_93_output1c), .input1d(subtractor256bit_93_output1d), .input2a({64{1'b0}}),
    .input2b({input2[47:0], {16{1'b0}}}), .input2c({{48{1'b0}}, input2[63:48]}), .input2d({64{1'b0}}),
    .greater1(comparatoru256bit_95_greater1), .equal1(comparatoru256bit_95_equal1));  // open: less1
  subtractor256bit subtractor256bit_96 (
    .input1a(subtractor256bit_94_output1a), .input1b(subtractor256bit_94_output1b),
    .input1c(subtractor256bit_94_output1c), .input1d(subtractor256bit_94_output1d),
    .input2a(cbuffer256bit_96_output1a), .input2b(cbuffer256bit_96_output1b),
    .input2c(cbuffer256bit_96_output1c), .input2d(cbuffer256bit_96_output1d),
    .output1a(subtractor256bit_96_output1a), .output1b(subtractor256bit_96_output1b),
    .output1c(subtractor256bit_96_output1c), .output1d(subtractor256bit_96_output1d));  // open: inborrow, borrow
  cbuffer256bit cbuffer256bit_96 (
    .buffer1(output1[16]), .input1a({input2[47:0], {16{1'b0}}}), .input1b({{48{1'b0}}, input2[63:48]}),
    .input1c({64{1'b0}}), .input1d({64{1'b0}}), .output1a(cbuffer256bit_96_output1a),
    .output1b(cbuffer256bit_96_output1b), .output1c(cbuffer256bit_96_output1c),
    .output1d(cbuffer256bit_96_output1d));
  and and_96 (output1[16], not_1_out, or_96_out);
  or or_96 (or_96_out, comparatoru256bit_96_greater1, comparatoru256bit_96_equal1);
  comparatoru256bit comparatoru256bit_96 (
    .input1a(subtractor256bit_94_output1a), .input1b(subtractor256bit_94_output1b),
    .input1c(subtractor256bit_94_output1c), .input1d(subtractor256bit_94_output1d),
    .input2a({input2[47:0], {16{1'b0}}}), .input2b({{48{1'b0}}, input2[63:48]}), .input2c({64{1'b0}}),
    .input2d({64{1'b0}}), .greater1(comparatoru256bit_96_greater1), .equal1(comparatoru256bit_96_equal1));  // open: less1
  subtractor256bit subtractor256bit_97 (
    .input1a(subtractor256bit_95_output1a), .input1b(subtractor256bit_95_output1b),
    .input1c(subtractor256bit_95_output1c), .input1d(subtractor256bit_95_output1d),
    .input2a(cbuffer256bit_97_output1a), .input2b(cbuffer256bit_97_output1b),
    .input2c(cbuffer256bit_97_output1c), .input2d(cbuffer256bit_97_output1d),
    .output1a(subtractor256bit_97_output1a), .output1b(subtractor256bit_97_output1b),
    .output1c(subtractor256bit_97_output1c), .output1d(subtractor256bit_97_output1d));  // open: inborrow, borrow
  cbuffer256bit cbuffer256bit_97 (
    .buffer1(and_127_out[15]), .input1a({64{1'b0}}), .input1b({input2[48:0], {15{1'b0}}}),
    .input1c({{49{1'b0}}, input2[63:49]}), .input1d({64{1'b0}}), .output1a(cbuffer256bit_97_output1a),
    .output1b(cbuffer256bit_97_output1b), .output1c(cbuffer256bit_97_output1c),
    .output1d(cbuffer256bit_97_output1d));
  and and_97 (and_127_out[15], not_1_out, or_97_out);
  or or_97 (or_97_out, comparatoru256bit_97_greater1, comparatoru256bit_97_equal1);
  comparatoru256bit comparatoru256bit_97 (
    .input1a(subtractor256bit_95_output1a), .input1b(subtractor256bit_95_output1b),
    .input1c(subtractor256bit_95_output1c), .input1d(subtractor256bit_95_output1d), .input2a({64{1'b0}}),
    .input2b({input2[48:0], {15{1'b0}}}), .input2c({{49{1'b0}}, input2[63:49]}), .input2d({64{1'b0}}),
    .greater1(comparatoru256bit_97_greater1), .equal1(comparatoru256bit_97_equal1));  // open: less1
  subtractor256bit subtractor256bit_98 (
    .input1a(subtractor256bit_96_output1a), .input1b(subtractor256bit_96_output1b),
    .input1c(subtractor256bit_96_output1c), .input1d(subtractor256bit_96_output1d),
    .input2a(cbuffer256bit_98_output1a), .input2b(cbuffer256bit_98_output1b),
    .input2c(cbuffer256bit_98_output1c), .input2d(cbuffer256bit_98_output1d),
    .output1a(subtractor256bit_98_output1a), .output1b(subtractor256bit_98_output1b),
    .output1c(subtractor256bit_98_output1c), .output1d(subtractor256bit_98_output1d));  // open: inborrow, borrow
  cbuffer256bit cbuffer256bit_98 (
    .buffer1(output1[15]), .input1a({input2[48:0], {15{1'b0}}}), .input1b({{49{1'b0}}, input2[63:49]}),
    .input1c({64{1'b0}}), .input1d({64{1'b0}}), .output1a(cbuffer256bit_98_output1a),
    .output1b(cbuffer256bit_98_output1b), .output1c(cbuffer256bit_98_output1c),
    .output1d(cbuffer256bit_98_output1d));
  and and_98 (output1[15], not_1_out, or_98_out);
  or or_98 (or_98_out, comparatoru256bit_98_greater1, comparatoru256bit_98_equal1);
  comparatoru256bit comparatoru256bit_98 (
    .input1a(subtractor256bit_96_output1a), .input1b(subtractor256bit_96_output1b),
    .input1c(subtractor256bit_96_output1c), .input1d(subtractor256bit_96_output1d),
    .input2a({input2[48:0], {15{1'b0}}}), .input2b({{49{1'b0}}, input2[63:49]}), .input2c({64{1'b0}}),
    .input2d({64{1'b0}}), .greater1(comparatoru256bit_98_greater1), .equal1(comparatoru256bit_98_equal1));  // open: less1
  subtractor256bit subtractor256bit_99 (
    .input1a(subtractor256bit_97_output1a), .input1b(subtractor256bit_97_output1b),
    .input1c(subtractor256bit_97_output1c), .input1d(subtractor256bit_97_output1d),
    .input2a(cbuffer256bit_99_output1a), .input2b(cbuffer256bit_99_output1b),
    .input2c(cbuffer256bit_99_output1c), .input2d(cbuffer256bit_99_output1d),
    .output1a(subtractor256bit_99_output1a), .output1b(subtractor256bit_99_output1b),
    .output1c(subtractor256bit_99_output1c), .output1d(subtractor256bit_99_output1d));  // open: inborrow, borrow
  cbuffer256bit cbuffer256bit_99 (
    .buffer1(and_127_out[14]), .input1a({64{1'b0}}), .input1b({input2[49:0], {14{1'b0}}}),
    .input1c({{50{1'b0}}, input2[63:50]}), .input1d({64{1'b0}}), .output1a(cbuffer256bit_99_output1a),
    .output1b(cbuffer256bit_99_output1b), .output1c(cbuffer256bit_99_output1c),
    .output1d(cbuffer256bit_99_output1d));
  and and_99 (and_127_out[14], not_1_out, or_99_out);
  or or_99 (or_99_out, comparatoru256bit_99_greater1, comparatoru256bit_99_equal1);
  comparatoru256bit comparatoru256bit_99 (
    .input1a(subtractor256bit_97_output1a), .input1b(subtractor256bit_97_output1b),
    .input1c(subtractor256bit_97_output1c), .input1d(subtractor256bit_97_output1d), .input2a({64{1'b0}}),
    .input2b({input2[49:0], {14{1'b0}}}), .input2c({{50{1'b0}}, input2[63:50]}), .input2d({64{1'b0}}),
    .greater1(comparatoru256bit_99_greater1), .equal1(comparatoru256bit_99_equal1));  // open: less1
  subtractor256bit subtractor256bit_100 (
    .input1a(subtractor256bit_98_output1a), .input1b(subtractor256bit_98_output1b),
    .input1c(subtractor256bit_98_output1c), .input1d(subtractor256bit_98_output1d),
    .input2a(cbuffer256bit_100_output1a), .input2b(cbuffer256bit_100_output1b),
    .input2c(cbuffer256bit_100_output1c), .input2d(cbuffer256bit_100_output1d),
    .output1a(subtractor256bit_100_output1a), .output1b(subtractor256bit_100_output1b),
    .output1c(subtractor256bit_100_output1c), .output1d(subtractor256bit_100_output1d));  // open: inborrow, borrow
  cbuffer256bit cbuffer256bit_100 (
    .buffer1(output1[14]), .input1a({input2[49:0], {14{1'b0}}}), .input1b({{50{1'b0}}, input2[63:50]}),
    .input1c({64{1'b0}}), .input1d({64{1'b0}}), .output1a(cbuffer256bit_100_output1a),
    .output1b(cbuffer256bit_100_output1b), .output1c(cbuffer256bit_100_output1c),
    .output1d(cbuffer256bit_100_output1d));
  and and_100 (output1[14], not_1_out, or_100_out);
  comparatoru256bit comparatoru256bit_100 (
    .input1a(subtractor256bit_98_output1a), .input1b(subtractor256bit_98_output1b),
    .input1c(subtractor256bit_98_output1c), .input1d(subtractor256bit_98_output1d),
    .input2a({input2[49:0], {14{1'b0}}}), .input2b({{50{1'b0}}, input2[63:50]}), .input2c({64{1'b0}}),
    .input2d({64{1'b0}}), .greater1(comparatoru256bit_100_greater1), .equal1(comparatoru256bit_100_equal1));  // open: less1
  or or_100 (or_100_out, comparatoru256bit_100_greater1, comparatoru256bit_100_equal1);
  subtractor256bit subtractor256bit_101 (
    .input1a(subtractor256bit_99_output1a), .input1b(subtractor256bit_99_output1b),
    .input1c(subtractor256bit_99_output1c), .input1d(subtractor256bit_99_output1d),
    .input2a(cbuffer256bit_101_output1a), .input2b(cbuffer256bit_101_output1b),
    .input2c(cbuffer256bit_101_output1c), .input2d(cbuffer256bit_101_output1d),
    .output1a(subtractor256bit_101_output1a), .output1b(subtractor256bit_101_output1b),
    .output1c(subtractor256bit_101_output1c), .output1d(subtractor256bit_101_output1d));  // open: inborrow, borrow
  cbuffer256bit cbuffer256bit_101 (
    .buffer1(and_127_out[13]), .input1a({64{1'b0}}), .input1b({input2[50:0], {13{1'b0}}}),
    .input1c({{51{1'b0}}, input2[63:51]}), .input1d({64{1'b0}}), .output1a(cbuffer256bit_101_output1a),
    .output1b(cbuffer256bit_101_output1b), .output1c(cbuffer256bit_101_output1c),
    .output1d(cbuffer256bit_101_output1d));
  and and_101 (and_127_out[13], not_1_out, or_101_out);
  or or_101 (or_101_out, comparatoru256bit_101_greater1, comparatoru256bit_101_equal1);
  comparatoru256bit comparatoru256bit_101 (
    .input1a(subtractor256bit_99_output1a), .input1b(subtractor256bit_99_output1b),
    .input1c(subtractor256bit_99_output1c), .input1d(subtractor256bit_99_output1d), .input2a({64{1'b0}}),
    .input2b({input2[50:0], {13{1'b0}}}), .input2c({{51{1'b0}}, input2[63:51]}), .input2d({64{1'b0}}),
    .greater1(comparatoru256bit_101_greater1), .equal1(comparatoru256bit_101_equal1));  // open: less1
  subtractor256bit subtractor256bit_102 (
    .input1a(subtractor256bit_100_output1a), .input1b(subtractor256bit_100_output1b),
    .input1c(subtractor256bit_100_output1c), .input1d(subtractor256bit_100_output1d),
    .input2a(cbuffer256bit_102_output1a), .input2b(cbuffer256bit_102_output1b),
    .input2c(cbuffer256bit_102_output1c), .input2d(cbuffer256bit_102_output1d),
    .output1a(subtractor256bit_102_output1a), .output1b(subtractor256bit_102_output1b),
    .output1c(subtractor256bit_102_output1c), .output1d(subtractor256bit_102_output1d));  // open: inborrow, borrow
  cbuffer256bit cbuffer256bit_102 (
    .buffer1(output1[13]), .input1a({input2[50:0], {13{1'b0}}}), .input1b({{51{1'b0}}, input2[63:51]}),
    .input1c({64{1'b0}}), .input1d({64{1'b0}}), .output1a(cbuffer256bit_102_output1a),
    .output1b(cbuffer256bit_102_output1b), .output1c(cbuffer256bit_102_output1c),
    .output1d(cbuffer256bit_102_output1d));
  and and_102 (output1[13], not_1_out, or_102_out);
  or or_102 (or_102_out, comparatoru256bit_102_greater1, comparatoru256bit_102_equal1);
  comparatoru256bit comparatoru256bit_102 (
    .input1a(subtractor256bit_100_output1a), .input1b(subtractor256bit_100_output1b),
    .input1c(subtractor256bit_100_output1c), .input1d(subtractor256bit_100_output1d),
    .input2a({input2[50:0], {13{1'b0}}}), .input2b({{51{1'b0}}, input2[63:51]}), .input2c({64{1'b0}}),
    .input2d({64{1'b0}}), .greater1(comparatoru256bit_102_greater1), .equal1(comparatoru256bit_102_equal1));  // open: less1
  subtractor256bit subtractor256bit_103 (
    .input1a(subtractor256bit_101_output1a), .input1b(subtractor256bit_101_output1b),
    .input1c(subtractor256bit_101_output1c), .input1d(subtractor256bit_101_output1d),
    .input2a(cbuffer256bit_103_output1a), .input2b(cbuffer256bit_103_output1b),
    .input2c(cbuffer256bit_103_output1c), .input2d(cbuffer256bit_103_output1d),
    .output1a(subtractor256bit_103_output1a), .output1b(subtractor256bit_103_output1b),
    .output1c(subtractor256bit_103_output1c), .output1d(subtractor256bit_103_output1d));  // open: inborrow, borrow
  cbuffer256bit cbuffer256bit_103 (
    .buffer1(and_127_out[12]), .input1a({64{1'b0}}), .input1b({input2[51:0], {12{1'b0}}}),
    .input1c({{52{1'b0}}, input2[63:52]}), .input1d({64{1'b0}}), .output1a(cbuffer256bit_103_output1a),
    .output1b(cbuffer256bit_103_output1b), .output1c(cbuffer256bit_103_output1c),
    .output1d(cbuffer256bit_103_output1d));
  and and_103 (and_127_out[12], not_1_out, or_103_out);
  or or_103 (or_103_out, comparatoru256bit_103_greater1, comparatoru256bit_103_equal1);
  comparatoru256bit comparatoru256bit_103 (
    .input1a(subtractor256bit_101_output1a), .input1b(subtractor256bit_101_output1b),
    .input1c(subtractor256bit_101_output1c), .input1d(subtractor256bit_101_output1d), .input2a({64{1'b0}}),
    .input2b({input2[51:0], {12{1'b0}}}), .input2c({{52{1'b0}}, input2[63:52]}), .input2d({64{1'b0}}),
    .greater1(comparatoru256bit_103_greater1), .equal1(comparatoru256bit_103_equal1));  // open: less1
  subtractor256bit subtractor256bit_104 (
    .input1a(subtractor256bit_102_output1a), .input1b(subtractor256bit_102_output1b),
    .input1c(subtractor256bit_102_output1c), .input1d(subtractor256bit_102_output1d),
    .input2a(cbuffer256bit_104_output1a), .input2b(cbuffer256bit_104_output1b),
    .input2c(cbuffer256bit_104_output1c), .input2d(cbuffer256bit_104_output1d),
    .output1a(subtractor256bit_104_output1a), .output1b(subtractor256bit_104_output1b),
    .output1c(subtractor256bit_104_output1c), .output1d(subtractor256bit_104_output1d));  // open: inborrow, borrow
  cbuffer256bit cbuffer256bit_104 (
    .buffer1(output1[12]), .input1a({input2[51:0], {12{1'b0}}}), .input1b({{52{1'b0}}, input2[63:52]}),
    .input1c({64{1'b0}}), .input1d({64{1'b0}}), .output1a(cbuffer256bit_104_output1a),
    .output1b(cbuffer256bit_104_output1b), .output1c(cbuffer256bit_104_output1c),
    .output1d(cbuffer256bit_104_output1d));
  and and_104 (output1[12], not_1_out, or_104_out);
  or or_104 (or_104_out, comparatoru256bit_104_greater1, comparatoru256bit_104_equal1);
  comparatoru256bit comparatoru256bit_104 (
    .input1a(subtractor256bit_102_output1a), .input1b(subtractor256bit_102_output1b),
    .input1c(subtractor256bit_102_output1c), .input1d(subtractor256bit_102_output1d),
    .input2a({input2[51:0], {12{1'b0}}}), .input2b({{52{1'b0}}, input2[63:52]}), .input2c({64{1'b0}}),
    .input2d({64{1'b0}}), .greater1(comparatoru256bit_104_greater1), .equal1(comparatoru256bit_104_equal1));  // open: less1
  subtractor256bit subtractor256bit_105 (
    .input1a(subtractor256bit_103_output1a), .input1b(subtractor256bit_103_output1b),
    .input1c(subtractor256bit_103_output1c), .input1d(subtractor256bit_103_output1d),
    .input2a(cbuffer256bit_105_output1a), .input2b(cbuffer256bit_105_output1b),
    .input2c(cbuffer256bit_105_output1c), .input2d(cbuffer256bit_105_output1d),
    .output1a(subtractor256bit_105_output1a), .output1b(subtractor256bit_105_output1b),
    .output1c(subtractor256bit_105_output1c), .output1d(subtractor256bit_105_output1d));  // open: inborrow, borrow
  cbuffer256bit cbuffer256bit_105 (
    .buffer1(and_127_out[11]), .input1a({64{1'b0}}), .input1b({input2[52:0], {11{1'b0}}}),
    .input1c({{53{1'b0}}, input2[63:53]}), .input1d({64{1'b0}}), .output1a(cbuffer256bit_105_output1a),
    .output1b(cbuffer256bit_105_output1b), .output1c(cbuffer256bit_105_output1c),
    .output1d(cbuffer256bit_105_output1d));
  and and_105 (and_127_out[11], not_1_out, or_105_out);
  or or_105 (or_105_out, comparatoru256bit_105_greater1, comparatoru256bit_105_equal1);
  comparatoru256bit comparatoru256bit_105 (
    .input1a(subtractor256bit_103_output1a), .input1b(subtractor256bit_103_output1b),
    .input1c(subtractor256bit_103_output1c), .input1d(subtractor256bit_103_output1d), .input2a({64{1'b0}}),
    .input2b({input2[52:0], {11{1'b0}}}), .input2c({{53{1'b0}}, input2[63:53]}), .input2d({64{1'b0}}),
    .greater1(comparatoru256bit_105_greater1), .equal1(comparatoru256bit_105_equal1));  // open: less1
  subtractor256bit subtractor256bit_106 (
    .input1a(subtractor256bit_104_output1a), .input1b(subtractor256bit_104_output1b),
    .input1c(subtractor256bit_104_output1c), .input1d(subtractor256bit_104_output1d),
    .input2a(cbuffer256bit_106_output1a), .input2b(cbuffer256bit_106_output1b),
    .input2c(cbuffer256bit_106_output1c), .input2d(cbuffer256bit_106_output1d),
    .output1a(subtractor256bit_106_output1a), .output1b(subtractor256bit_106_output1b),
    .output1c(subtractor256bit_106_output1c), .output1d(subtractor256bit_106_output1d));  // open: inborrow, borrow
  cbuffer256bit cbuffer256bit_106 (
    .buffer1(output1[11]), .input1a({input2[52:0], {11{1'b0}}}), .input1b({{53{1'b0}}, input2[63:53]}),
    .input1c({64{1'b0}}), .input1d({64{1'b0}}), .output1a(cbuffer256bit_106_output1a),
    .output1b(cbuffer256bit_106_output1b), .output1c(cbuffer256bit_106_output1c),
    .output1d(cbuffer256bit_106_output1d));
  and and_106 (output1[11], not_1_out, or_106_out);
  or or_106 (or_106_out, comparatoru256bit_106_greater1, comparatoru256bit_106_equal1);
  comparatoru256bit comparatoru256bit_106 (
    .input1a(subtractor256bit_104_output1a), .input1b(subtractor256bit_104_output1b),
    .input1c(subtractor256bit_104_output1c), .input1d(subtractor256bit_104_output1d),
    .input2a({input2[52:0], {11{1'b0}}}), .input2b({{53{1'b0}}, input2[63:53]}), .input2c({64{1'b0}}),
    .input2d({64{1'b0}}), .greater1(comparatoru256bit_106_greater1), .equal1(comparatoru256bit_106_equal1));  // open: less1
  subtractor256bit subtractor256bit_107 (
    .input1a(subtractor256bit_105_output1a), .input1b(subtractor256bit_105_output1b),
    .input1c(subtractor256bit_105_output1c), .input1d(subtractor256bit_105_output1d),
    .input2a(cbuffer256bit_107_output1a), .input2b(cbuffer256bit_107_output1b),
    .input2c(cbuffer256bit_107_output1c), .input2d(cbuffer256bit_107_output1d),
    .output1a(subtractor256bit_107_output1a), .output1b(subtractor256bit_107_output1b),
    .output1c(subtractor256bit_107_output1c), .output1d(subtractor256bit_107_output1d));  // open: inborrow, borrow
  cbuffer256bit cbuffer256bit_107 (
    .buffer1(and_127_out[10]), .input1a({64{1'b0}}), .input1b({input2[53:0], {10{1'b0}}}),
    .input1c({{54{1'b0}}, input2[63:54]}), .input1d({64{1'b0}}), .output1a(cbuffer256bit_107_output1a),
    .output1b(cbuffer256bit_107_output1b), .output1c(cbuffer256bit_107_output1c),
    .output1d(cbuffer256bit_107_output1d));
  and and_107 (and_127_out[10], not_1_out, or_107_out);
  or or_107 (or_107_out, comparatoru256bit_107_greater1, comparatoru256bit_107_equal1);
  comparatoru256bit comparatoru256bit_107 (
    .input1a(subtractor256bit_105_output1a), .input1b(subtractor256bit_105_output1b),
    .input1c(subtractor256bit_105_output1c), .input1d(subtractor256bit_105_output1d), .input2a({64{1'b0}}),
    .input2b({input2[53:0], {10{1'b0}}}), .input2c({{54{1'b0}}, input2[63:54]}), .input2d({64{1'b0}}),
    .greater1(comparatoru256bit_107_greater1), .equal1(comparatoru256bit_107_equal1));  // open: less1
  subtractor256bit subtractor256bit_108 (
    .input1a(subtractor256bit_106_output1a), .input1b(subtractor256bit_106_output1b),
    .input1c(subtractor256bit_106_output1c), .input1d(subtractor256bit_106_output1d),
    .input2a(cbuffer256bit_108_output1a), .input2b(cbuffer256bit_108_output1b),
    .input2c(cbuffer256bit_108_output1c), .input2d(cbuffer256bit_108_output1d),
    .output1a(subtractor256bit_108_output1a), .output1b(subtractor256bit_108_output1b),
    .output1c(subtractor256bit_108_output1c), .output1d(subtractor256bit_108_output1d));  // open: inborrow, borrow
  cbuffer256bit cbuffer256bit_108 (
    .buffer1(output1[10]), .input1a({input2[53:0], {10{1'b0}}}), .input1b({{54{1'b0}}, input2[63:54]}),
    .input1c({64{1'b0}}), .input1d({64{1'b0}}), .output1a(cbuffer256bit_108_output1a),
    .output1b(cbuffer256bit_108_output1b), .output1c(cbuffer256bit_108_output1c),
    .output1d(cbuffer256bit_108_output1d));
  and and_108 (output1[10], not_1_out, or_108_out);
  or or_108 (or_108_out, comparatoru256bit_108_greater1, comparatoru256bit_108_equal1);
  comparatoru256bit comparatoru256bit_108 (
    .input1a(subtractor256bit_106_output1a), .input1b(subtractor256bit_106_output1b),
    .input1c(subtractor256bit_106_output1c), .input1d(subtractor256bit_106_output1d),
    .input2a({input2[53:0], {10{1'b0}}}), .input2b({{54{1'b0}}, input2[63:54]}), .input2c({64{1'b0}}),
    .input2d({64{1'b0}}), .greater1(comparatoru256bit_108_greater1), .equal1(comparatoru256bit_108_equal1));  // open: less1
  subtractor256bit subtractor256bit_109 (
    .input1a(subtractor256bit_107_output1a), .input1b(subtractor256bit_107_output1b),
    .input1c(subtractor256bit_107_output1c), .input1d(subtractor256bit_107_output1d),
    .input2a(cbuffer256bit_109_output1a), .input2b(cbuffer256bit_109_output1b),
    .input2c(cbuffer256bit_109_output1c), .input2d(cbuffer256bit_109_output1d),
    .output1a(subtractor256bit_109_output1a), .output1b(subtractor256bit_109_output1b),
    .output1c(subtractor256bit_109_output1c), .output1d(subtractor256bit_109_output1d));  // open: inborrow, borrow
  cbuffer256bit cbuffer256bit_109 (
    .buffer1(and_127_out[9]), .input1a({64{1'b0}}), .input1b({input2[54:0], {9{1'b0}}}),
    .input1c({{55{1'b0}}, input2[63:55]}), .input1d({64{1'b0}}), .output1a(cbuffer256bit_109_output1a),
    .output1b(cbuffer256bit_109_output1b), .output1c(cbuffer256bit_109_output1c),
    .output1d(cbuffer256bit_109_output1d));
  and and_109 (and_127_out[9], not_1_out, or_109_out);
  comparatoru256bit comparatoru256bit_109 (
    .input1a(subtractor256bit_107_output1a), .input1b(subtractor256bit_107_output1b),
    .input1c(subtractor256bit_107_output1c), .input1d(subtractor256bit_107_output1d), .input2a({64{1'b0}}),
    .input2b({input2[54:0], {9{1'b0}}}), .input2c({{55{1'b0}}, input2[63:55]}), .input2d({64{1'b0}}),
    .greater1(comparatoru256bit_109_greater1), .equal1(comparatoru256bit_109_equal1));  // open: less1
  subtractor256bit subtractor256bit_110 (
    .input1a(subtractor256bit_108_output1a), .input1b(subtractor256bit_108_output1b),
    .input1c(subtractor256bit_108_output1c), .input1d(subtractor256bit_108_output1d),
    .input2a(cbuffer256bit_110_output1a), .input2b(cbuffer256bit_110_output1b),
    .input2c(cbuffer256bit_110_output1c), .input2d(cbuffer256bit_110_output1d),
    .output1a(subtractor256bit_110_output1a), .output1b(subtractor256bit_110_output1b),
    .output1c(subtractor256bit_110_output1c), .output1d(subtractor256bit_110_output1d));  // open: inborrow, borrow
  cbuffer256bit cbuffer256bit_110 (
    .buffer1(output1[9]), .input1a({input2[54:0], {9{1'b0}}}), .input1b({{55{1'b0}}, input2[63:55]}),
    .input1c({64{1'b0}}), .input1d({64{1'b0}}), .output1a(cbuffer256bit_110_output1a),
    .output1b(cbuffer256bit_110_output1b), .output1c(cbuffer256bit_110_output1c),
    .output1d(cbuffer256bit_110_output1d));
  and and_110 (output1[9], not_1_out, or_110_out);
  or or_109 (or_109_out, comparatoru256bit_109_greater1, comparatoru256bit_109_equal1);
  or or_110 (or_110_out, comparatoru256bit_110_greater1, comparatoru256bit_110_equal1);
  comparatoru256bit comparatoru256bit_110 (
    .input1a(subtractor256bit_108_output1a), .input1b(subtractor256bit_108_output1b),
    .input1c(subtractor256bit_108_output1c), .input1d(subtractor256bit_108_output1d),
    .input2a({input2[54:0], {9{1'b0}}}), .input2b({{55{1'b0}}, input2[63:55]}), .input2c({64{1'b0}}),
    .input2d({64{1'b0}}), .greater1(comparatoru256bit_110_greater1), .equal1(comparatoru256bit_110_equal1));  // open: less1
  subtractor256bit subtractor256bit_111 (
    .input1a(subtractor256bit_109_output1a), .input1b(subtractor256bit_109_output1b),
    .input1c(subtractor256bit_109_output1c), .input1d(subtractor256bit_109_output1d),
    .input2a(cbuffer256bit_111_output1a), .input2b(cbuffer256bit_111_output1b),
    .input2c(cbuffer256bit_111_output1c), .input2d(cbuffer256bit_111_output1d),
    .output1a(subtractor256bit_111_output1a), .output1b(subtractor256bit_111_output1b),
    .output1c(subtractor256bit_111_output1c), .output1d(subtractor256bit_111_output1d));  // open: inborrow, borrow
  cbuffer256bit cbuffer256bit_111 (
    .buffer1(and_127_out[8]), .input1a({64{1'b0}}), .input1b({input2[55:0], {8{1'b0}}}),
    .input1c({{56{1'b0}}, input2[63:56]}), .input1d({64{1'b0}}), .output1a(cbuffer256bit_111_output1a),
    .output1b(cbuffer256bit_111_output1b), .output1c(cbuffer256bit_111_output1c),
    .output1d(cbuffer256bit_111_output1d));
  and and_111 (and_127_out[8], not_1_out, or_111_out);
  or or_111 (or_111_out, comparatoru256bit_111_greater1, comparatoru256bit_111_equal1);
  comparatoru256bit comparatoru256bit_111 (
    .input1a(subtractor256bit_109_output1a), .input1b(subtractor256bit_109_output1b),
    .input1c(subtractor256bit_109_output1c), .input1d(subtractor256bit_109_output1d), .input2a({64{1'b0}}),
    .input2b({input2[55:0], {8{1'b0}}}), .input2c({{56{1'b0}}, input2[63:56]}), .input2d({64{1'b0}}),
    .greater1(comparatoru256bit_111_greater1), .equal1(comparatoru256bit_111_equal1));  // open: less1
  subtractor256bit subtractor256bit_112 (
    .input1a(subtractor256bit_110_output1a), .input1b(subtractor256bit_110_output1b),
    .input1c(subtractor256bit_110_output1c), .input1d(subtractor256bit_110_output1d),
    .input2a(cbuffer256bit_112_output1a), .input2b(cbuffer256bit_112_output1b),
    .input2c(cbuffer256bit_112_output1c), .input2d(cbuffer256bit_112_output1d),
    .output1a(subtractor256bit_112_output1a), .output1b(subtractor256bit_112_output1b),
    .output1c(subtractor256bit_112_output1c), .output1d(subtractor256bit_112_output1d));  // open: inborrow, borrow
  cbuffer256bit cbuffer256bit_112 (
    .buffer1(output1[8]), .input1a({input2[55:0], {8{1'b0}}}), .input1b({{56{1'b0}}, input2[63:56]}),
    .input1c({64{1'b0}}), .input1d({64{1'b0}}), .output1a(cbuffer256bit_112_output1a),
    .output1b(cbuffer256bit_112_output1b), .output1c(cbuffer256bit_112_output1c),
    .output1d(cbuffer256bit_112_output1d));
  and and_112 (output1[8], not_1_out, or_112_out);
  or or_112 (or_112_out, comparatoru256bit_112_greater1, comparatoru256bit_112_equal1);
  comparatoru256bit comparatoru256bit_112 (
    .input1a(subtractor256bit_110_output1a), .input1b(subtractor256bit_110_output1b),
    .input1c(subtractor256bit_110_output1c), .input1d(subtractor256bit_110_output1d),
    .input2a({input2[55:0], {8{1'b0}}}), .input2b({{56{1'b0}}, input2[63:56]}), .input2c({64{1'b0}}),
    .input2d({64{1'b0}}), .greater1(comparatoru256bit_112_greater1), .equal1(comparatoru256bit_112_equal1));  // open: less1
  subtractor256bit subtractor256bit_113 (
    .input1a(subtractor256bit_111_output1a), .input1b(subtractor256bit_111_output1b),
    .input1c(subtractor256bit_111_output1c), .input1d(subtractor256bit_111_output1d),
    .input2a(cbuffer256bit_113_output1a), .input2b(cbuffer256bit_113_output1b),
    .input2c(cbuffer256bit_113_output1c), .input2d(cbuffer256bit_113_output1d),
    .output1a(subtractor256bit_113_output1a), .output1b(subtractor256bit_113_output1b),
    .output1c(subtractor256bit_113_output1c), .output1d(subtractor256bit_113_output1d));  // open: inborrow, borrow
  cbuffer256bit cbuffer256bit_113 (
    .buffer1(and_127_out[7]), .input1a({64{1'b0}}), .input1b({input2[56:0], {7{1'b0}}}),
    .input1c({{57{1'b0}}, input2[63:57]}), .input1d({64{1'b0}}), .output1a(cbuffer256bit_113_output1a),
    .output1b(cbuffer256bit_113_output1b), .output1c(cbuffer256bit_113_output1c),
    .output1d(cbuffer256bit_113_output1d));
  and and_113 (and_127_out[7], not_1_out, or_113_out);
  or or_113 (or_113_out, comparatoru256bit_113_greater1, comparatoru256bit_113_equal1);
  comparatoru256bit comparatoru256bit_113 (
    .input1a(subtractor256bit_111_output1a), .input1b(subtractor256bit_111_output1b),
    .input1c(subtractor256bit_111_output1c), .input1d(subtractor256bit_111_output1d), .input2a({64{1'b0}}),
    .input2b({input2[56:0], {7{1'b0}}}), .input2c({{57{1'b0}}, input2[63:57]}), .input2d({64{1'b0}}),
    .greater1(comparatoru256bit_113_greater1), .equal1(comparatoru256bit_113_equal1));  // open: less1
  subtractor256bit subtractor256bit_114 (
    .input1a(subtractor256bit_112_output1a), .input1b(subtractor256bit_112_output1b),
    .input1c(subtractor256bit_112_output1c), .input1d(subtractor256bit_112_output1d),
    .input2a(cbuffer256bit_114_output1a), .input2b(cbuffer256bit_114_output1b),
    .input2c(cbuffer256bit_114_output1c), .input2d(cbuffer256bit_114_output1d),
    .output1a(subtractor256bit_114_output1a), .output1b(subtractor256bit_114_output1b),
    .output1c(subtractor256bit_114_output1c), .output1d(subtractor256bit_114_output1d));  // open: inborrow, borrow
  cbuffer256bit cbuffer256bit_114 (
    .buffer1(output1[7]), .input1a({input2[56:0], {7{1'b0}}}), .input1b({{57{1'b0}}, input2[63:57]}),
    .input1c({64{1'b0}}), .input1d({64{1'b0}}), .output1a(cbuffer256bit_114_output1a),
    .output1b(cbuffer256bit_114_output1b), .output1c(cbuffer256bit_114_output1c),
    .output1d(cbuffer256bit_114_output1d));
  and and_114 (output1[7], not_1_out, or_114_out);
  or or_114 (or_114_out, comparatoru256bit_114_greater1, comparatoru256bit_114_equal1);
  comparatoru256bit comparatoru256bit_114 (
    .input1a(subtractor256bit_112_output1a), .input1b(subtractor256bit_112_output1b),
    .input1c(subtractor256bit_112_output1c), .input1d(subtractor256bit_112_output1d),
    .input2a({input2[56:0], {7{1'b0}}}), .input2b({{57{1'b0}}, input2[63:57]}), .input2c({64{1'b0}}),
    .input2d({64{1'b0}}), .greater1(comparatoru256bit_114_greater1), .equal1(comparatoru256bit_114_equal1));  // open: less1
  subtractor256bit subtractor256bit_115 (
    .input1a(subtractor256bit_113_output1a), .input1b(subtractor256bit_113_output1b),
    .input1c(subtractor256bit_113_output1c), .input1d(subtractor256bit_113_output1d),
    .input2a(cbuffer256bit_115_output1a), .input2b(cbuffer256bit_115_output1b),
    .input2c(cbuffer256bit_115_output1c), .input2d(cbuffer256bit_115_output1d),
    .output1a(subtractor256bit_115_output1a), .output1b(subtractor256bit_115_output1b),
    .output1c(subtractor256bit_115_output1c), .output1d(subtractor256bit_115_output1d));  // open: inborrow, borrow
  cbuffer256bit cbuffer256bit_115 (
    .buffer1(and_127_out[6]), .input1a({64{1'b0}}), .input1b({input2[57:0], {6{1'b0}}}),
    .input1c({{58{1'b0}}, input2[63:58]}), .input1d({64{1'b0}}), .output1a(cbuffer256bit_115_output1a),
    .output1b(cbuffer256bit_115_output1b), .output1c(cbuffer256bit_115_output1c),
    .output1d(cbuffer256bit_115_output1d));
  and and_115 (and_127_out[6], not_1_out, or_115_out);
  or or_115 (or_115_out, comparatoru256bit_115_greater1, comparatoru256bit_115_equal1);
  comparatoru256bit comparatoru256bit_115 (
    .input1a(subtractor256bit_113_output1a), .input1b(subtractor256bit_113_output1b),
    .input1c(subtractor256bit_113_output1c), .input1d(subtractor256bit_113_output1d), .input2a({64{1'b0}}),
    .input2b({input2[57:0], {6{1'b0}}}), .input2c({{58{1'b0}}, input2[63:58]}), .input2d({64{1'b0}}),
    .greater1(comparatoru256bit_115_greater1), .equal1(comparatoru256bit_115_equal1));  // open: less1
  subtractor256bit subtractor256bit_116 (
    .input1a(subtractor256bit_114_output1a), .input1b(subtractor256bit_114_output1b),
    .input1c(subtractor256bit_114_output1c), .input1d(subtractor256bit_114_output1d),
    .input2a(cbuffer256bit_116_output1a), .input2b(cbuffer256bit_116_output1b),
    .input2c(cbuffer256bit_116_output1c), .input2d(cbuffer256bit_116_output1d),
    .output1a(subtractor256bit_116_output1a), .output1b(subtractor256bit_116_output1b),
    .output1c(subtractor256bit_116_output1c), .output1d(subtractor256bit_116_output1d));  // open: inborrow, borrow
  cbuffer256bit cbuffer256bit_116 (
    .buffer1(output1[6]), .input1a({input2[57:0], {6{1'b0}}}), .input1b({{58{1'b0}}, input2[63:58]}),
    .input1c({64{1'b0}}), .input1d({64{1'b0}}), .output1a(cbuffer256bit_116_output1a),
    .output1b(cbuffer256bit_116_output1b), .output1c(cbuffer256bit_116_output1c),
    .output1d(cbuffer256bit_116_output1d));
  and and_116 (output1[6], not_1_out, or_116_out);
  comparatoru256bit comparatoru256bit_116 (
    .input1a(subtractor256bit_114_output1a), .input1b(subtractor256bit_114_output1b),
    .input1c(subtractor256bit_114_output1c), .input1d(subtractor256bit_114_output1d),
    .input2a({input2[57:0], {6{1'b0}}}), .input2b({{58{1'b0}}, input2[63:58]}), .input2c({64{1'b0}}),
    .input2d({64{1'b0}}), .greater1(comparatoru256bit_116_greater1), .equal1(comparatoru256bit_116_equal1));  // open: less1
  or or_116 (or_116_out, comparatoru256bit_116_greater1, comparatoru256bit_116_equal1);
  subtractor256bit subtractor256bit_117 (
    .input1a(subtractor256bit_115_output1a), .input1b(subtractor256bit_115_output1b),
    .input1c(subtractor256bit_115_output1c), .input1d(subtractor256bit_115_output1d),
    .input2a(cbuffer256bit_117_output1a), .input2b(cbuffer256bit_117_output1b),
    .input2c(cbuffer256bit_117_output1c), .input2d(cbuffer256bit_117_output1d),
    .output1a(subtractor256bit_117_output1a), .output1b(subtractor256bit_117_output1b),
    .output1c(subtractor256bit_117_output1c), .output1d(subtractor256bit_117_output1d));  // open: inborrow, borrow
  cbuffer256bit cbuffer256bit_117 (
    .buffer1(and_127_out[5]), .input1a({64{1'b0}}), .input1b({input2[58:0], {5{1'b0}}}),
    .input1c({{59{1'b0}}, input2[63:59]}), .input1d({64{1'b0}}), .output1a(cbuffer256bit_117_output1a),
    .output1b(cbuffer256bit_117_output1b), .output1c(cbuffer256bit_117_output1c),
    .output1d(cbuffer256bit_117_output1d));
  and and_117 (and_127_out[5], not_1_out, or_117_out);
  or or_117 (or_117_out, comparatoru256bit_117_greater1, comparatoru256bit_117_equal1);
  comparatoru256bit comparatoru256bit_117 (
    .input1a(subtractor256bit_115_output1a), .input1b(subtractor256bit_115_output1b),
    .input1c(subtractor256bit_115_output1c), .input1d(subtractor256bit_115_output1d), .input2a({64{1'b0}}),
    .input2b({input2[58:0], {5{1'b0}}}), .input2c({{59{1'b0}}, input2[63:59]}), .input2d({64{1'b0}}),
    .greater1(comparatoru256bit_117_greater1), .equal1(comparatoru256bit_117_equal1));  // open: less1
  subtractor256bit subtractor256bit_118 (
    .input1a(subtractor256bit_116_output1a), .input1b(subtractor256bit_116_output1b),
    .input1c(subtractor256bit_116_output1c), .input1d(subtractor256bit_116_output1d),
    .input2a(cbuffer256bit_118_output1a), .input2b(cbuffer256bit_118_output1b),
    .input2c(cbuffer256bit_118_output1c), .input2d(cbuffer256bit_118_output1d),
    .output1a(subtractor256bit_118_output1a), .output1b(subtractor256bit_118_output1b),
    .output1c(subtractor256bit_118_output1c), .output1d(subtractor256bit_118_output1d));  // open: inborrow, borrow
  cbuffer256bit cbuffer256bit_118 (
    .buffer1(output1[5]), .input1a({input2[58:0], {5{1'b0}}}), .input1b({{59{1'b0}}, input2[63:59]}),
    .input1c({64{1'b0}}), .input1d({64{1'b0}}), .output1a(cbuffer256bit_118_output1a),
    .output1b(cbuffer256bit_118_output1b), .output1c(cbuffer256bit_118_output1c),
    .output1d(cbuffer256bit_118_output1d));
  and and_118 (output1[5], not_1_out, or_118_out);
  or or_118 (or_118_out, comparatoru256bit_118_greater1, comparatoru256bit_118_equal1);
  comparatoru256bit comparatoru256bit_118 (
    .input1a(subtractor256bit_116_output1a), .input1b(subtractor256bit_116_output1b),
    .input1c(subtractor256bit_116_output1c), .input1d(subtractor256bit_116_output1d),
    .input2a({input2[58:0], {5{1'b0}}}), .input2b({{59{1'b0}}, input2[63:59]}), .input2c({64{1'b0}}),
    .input2d({64{1'b0}}), .greater1(comparatoru256bit_118_greater1), .equal1(comparatoru256bit_118_equal1));  // open: less1
  subtractor256bit subtractor256bit_119 (
    .input1a(subtractor256bit_117_output1a), .input1b(subtractor256bit_117_output1b),
    .input1c(subtractor256bit_117_output1c), .input1d(subtractor256bit_117_output1d),
    .input2a(cbuffer256bit_119_output1a), .input2b(cbuffer256bit_119_output1b),
    .input2c(cbuffer256bit_119_output1c), .input2d(cbuffer256bit_119_output1d),
    .output1a(subtractor256bit_119_output1a), .output1b(subtractor256bit_119_output1b),
    .output1c(subtractor256bit_119_output1c), .output1d(subtractor256bit_119_output1d));  // open: inborrow, borrow
  cbuffer256bit cbuffer256bit_119 (
    .buffer1(and_127_out[4]), .input1a({64{1'b0}}), .input1b({input2[59:0], 4'b0000}),
    .input1c({{60{1'b0}}, input2[63:60]}), .input1d({64{1'b0}}), .output1a(cbuffer256bit_119_output1a),
    .output1b(cbuffer256bit_119_output1b), .output1c(cbuffer256bit_119_output1c),
    .output1d(cbuffer256bit_119_output1d));
  and and_119 (and_127_out[4], not_1_out, or_119_out);
  or or_119 (or_119_out, comparatoru256bit_119_greater1, comparatoru256bit_119_equal1);
  comparatoru256bit comparatoru256bit_119 (
    .input1a(subtractor256bit_117_output1a), .input1b(subtractor256bit_117_output1b),
    .input1c(subtractor256bit_117_output1c), .input1d(subtractor256bit_117_output1d), .input2a({64{1'b0}}),
    .input2b({input2[59:0], 4'b0000}), .input2c({{60{1'b0}}, input2[63:60]}), .input2d({64{1'b0}}),
    .greater1(comparatoru256bit_119_greater1), .equal1(comparatoru256bit_119_equal1));  // open: less1
  subtractor256bit subtractor256bit_120 (
    .input1a(subtractor256bit_118_output1a), .input1b(subtractor256bit_118_output1b),
    .input1c(subtractor256bit_118_output1c), .input1d(subtractor256bit_118_output1d),
    .input2a(cbuffer256bit_120_output1a), .input2b(cbuffer256bit_120_output1b),
    .input2c(cbuffer256bit_120_output1c), .input2d(cbuffer256bit_120_output1d),
    .output1a(subtractor256bit_120_output1a), .output1b(subtractor256bit_120_output1b),
    .output1c(subtractor256bit_120_output1c), .output1d(subtractor256bit_120_output1d));  // open: inborrow, borrow
  cbuffer256bit cbuffer256bit_120 (
    .buffer1(output1[4]), .input1a({input2[59:0], 4'b0000}), .input1b({{60{1'b0}}, input2[63:60]}),
    .input1c({64{1'b0}}), .input1d({64{1'b0}}), .output1a(cbuffer256bit_120_output1a),
    .output1b(cbuffer256bit_120_output1b), .output1c(cbuffer256bit_120_output1c),
    .output1d(cbuffer256bit_120_output1d));
  and and_120 (output1[4], not_1_out, or_120_out);
  or or_120 (or_120_out, comparatoru256bit_120_greater1, comparatoru256bit_120_equal1);
  comparatoru256bit comparatoru256bit_120 (
    .input1a(subtractor256bit_118_output1a), .input1b(subtractor256bit_118_output1b),
    .input1c(subtractor256bit_118_output1c), .input1d(subtractor256bit_118_output1d),
    .input2a({input2[59:0], 4'b0000}), .input2b({{60{1'b0}}, input2[63:60]}), .input2c({64{1'b0}}),
    .input2d({64{1'b0}}), .greater1(comparatoru256bit_120_greater1), .equal1(comparatoru256bit_120_equal1));  // open: less1
  subtractor256bit subtractor256bit_121 (
    .input1a(subtractor256bit_119_output1a), .input1b(subtractor256bit_119_output1b),
    .input1c(subtractor256bit_119_output1c), .input1d(subtractor256bit_119_output1d),
    .input2a(cbuffer256bit_121_output1a), .input2b(cbuffer256bit_121_output1b),
    .input2c(cbuffer256bit_121_output1c), .input2d(cbuffer256bit_121_output1d),
    .output1a(subtractor256bit_121_output1a), .output1b(subtractor256bit_121_output1b),
    .output1c(subtractor256bit_121_output1c), .output1d(subtractor256bit_121_output1d));  // open: inborrow, borrow
  cbuffer256bit cbuffer256bit_121 (
    .buffer1(and_127_out[3]), .input1a({64{1'b0}}), .input1b({input2[60:0], 3'b000}),
    .input1c({{61{1'b0}}, input2[63:61]}), .input1d({64{1'b0}}), .output1a(cbuffer256bit_121_output1a),
    .output1b(cbuffer256bit_121_output1b), .output1c(cbuffer256bit_121_output1c),
    .output1d(cbuffer256bit_121_output1d));
  and and_121 (and_127_out[3], not_1_out, or_121_out);
  or or_121 (or_121_out, comparatoru256bit_121_greater1, comparatoru256bit_121_equal1);
  comparatoru256bit comparatoru256bit_121 (
    .input1a(subtractor256bit_119_output1a), .input1b(subtractor256bit_119_output1b),
    .input1c(subtractor256bit_119_output1c), .input1d(subtractor256bit_119_output1d), .input2a({64{1'b0}}),
    .input2b({input2[60:0], 3'b000}), .input2c({{61{1'b0}}, input2[63:61]}), .input2d({64{1'b0}}),
    .greater1(comparatoru256bit_121_greater1), .equal1(comparatoru256bit_121_equal1));  // open: less1
  subtractor256bit subtractor256bit_122 (
    .input1a(subtractor256bit_120_output1a), .input1b(subtractor256bit_120_output1b),
    .input1c(subtractor256bit_120_output1c), .input1d(subtractor256bit_120_output1d),
    .input2a(cbuffer256bit_122_output1a), .input2b(cbuffer256bit_122_output1b),
    .input2c(cbuffer256bit_122_output1c), .input2d(cbuffer256bit_122_output1d),
    .output1a(subtractor256bit_122_output1a), .output1b(subtractor256bit_122_output1b),
    .output1c(subtractor256bit_122_output1c), .output1d(subtractor256bit_122_output1d));  // open: inborrow, borrow
  cbuffer256bit cbuffer256bit_122 (
    .buffer1(output1[3]), .input1a({input2[60:0], 3'b000}), .input1b({{61{1'b0}}, input2[63:61]}),
    .input1c({64{1'b0}}), .input1d({64{1'b0}}), .output1a(cbuffer256bit_122_output1a),
    .output1b(cbuffer256bit_122_output1b), .output1c(cbuffer256bit_122_output1c),
    .output1d(cbuffer256bit_122_output1d));
  and and_122 (output1[3], not_1_out, or_122_out);
  or or_122 (or_122_out, comparatoru256bit_122_greater1, comparatoru256bit_122_equal1);
  comparatoru256bit comparatoru256bit_122 (
    .input1a(subtractor256bit_120_output1a), .input1b(subtractor256bit_120_output1b),
    .input1c(subtractor256bit_120_output1c), .input1d(subtractor256bit_120_output1d),
    .input2a({input2[60:0], 3'b000}), .input2b({{61{1'b0}}, input2[63:61]}), .input2c({64{1'b0}}),
    .input2d({64{1'b0}}), .greater1(comparatoru256bit_122_greater1), .equal1(comparatoru256bit_122_equal1));  // open: less1
  subtractor256bit subtractor256bit_123 (
    .input1a(subtractor256bit_121_output1a), .input1b(subtractor256bit_121_output1b),
    .input1c(subtractor256bit_121_output1c), .input1d(subtractor256bit_121_output1d),
    .input2a(cbuffer256bit_123_output1a), .input2b(cbuffer256bit_123_output1b),
    .input2c(cbuffer256bit_123_output1c), .input2d(cbuffer256bit_123_output1d),
    .output1a(subtractor256bit_123_output1a), .output1b(subtractor256bit_123_output1b),
    .output1c(subtractor256bit_123_output1c), .output1d(subtractor256bit_123_output1d));  // open: inborrow, borrow
  cbuffer256bit cbuffer256bit_123 (
    .buffer1(and_127_out[2]), .input1a({64{1'b0}}), .input1b({input2[61:0], 2'b00}),
    .input1c({{62{1'b0}}, input2[63:62]}), .input1d({64{1'b0}}), .output1a(cbuffer256bit_123_output1a),
    .output1b(cbuffer256bit_123_output1b), .output1c(cbuffer256bit_123_output1c),
    .output1d(cbuffer256bit_123_output1d));
  and and_123 (and_127_out[2], not_1_out, or_123_out);
  or or_123 (or_123_out, comparatoru256bit_123_greater1, comparatoru256bit_123_equal1);
  comparatoru256bit comparatoru256bit_123 (
    .input1a(subtractor256bit_121_output1a), .input1b(subtractor256bit_121_output1b),
    .input1c(subtractor256bit_121_output1c), .input1d(subtractor256bit_121_output1d), .input2a({64{1'b0}}),
    .input2b({input2[61:0], 2'b00}), .input2c({{62{1'b0}}, input2[63:62]}), .input2d({64{1'b0}}),
    .greater1(comparatoru256bit_123_greater1), .equal1(comparatoru256bit_123_equal1));  // open: less1
  subtractor256bit subtractor256bit_124 (
    .input1a(subtractor256bit_122_output1a), .input1b(subtractor256bit_122_output1b),
    .input1c(subtractor256bit_122_output1c), .input1d(subtractor256bit_122_output1d),
    .input2a(cbuffer256bit_124_output1a), .input2b(cbuffer256bit_124_output1b),
    .input2c(cbuffer256bit_124_output1c), .input2d(cbuffer256bit_124_output1d),
    .output1a(subtractor256bit_124_output1a), .output1b(subtractor256bit_124_output1b),
    .output1c(subtractor256bit_124_output1c), .output1d(subtractor256bit_124_output1d));  // open: inborrow, borrow
  cbuffer256bit cbuffer256bit_124 (
    .buffer1(output1[2]), .input1a({input2[61:0], 2'b00}), .input1b({{62{1'b0}}, input2[63:62]}),
    .input1c({64{1'b0}}), .input1d({64{1'b0}}), .output1a(cbuffer256bit_124_output1a),
    .output1b(cbuffer256bit_124_output1b), .output1c(cbuffer256bit_124_output1c),
    .output1d(cbuffer256bit_124_output1d));
  and and_124 (output1[2], not_1_out, or_124_out);
  or or_124 (or_124_out, comparatoru256bit_124_greater1, comparatoru256bit_124_equal1);
  comparatoru256bit comparatoru256bit_124 (
    .input1a(subtractor256bit_122_output1a), .input1b(subtractor256bit_122_output1b),
    .input1c(subtractor256bit_122_output1c), .input1d(subtractor256bit_122_output1d),
    .input2a({input2[61:0], 2'b00}), .input2b({{62{1'b0}}, input2[63:62]}), .input2c({64{1'b0}}),
    .input2d({64{1'b0}}), .greater1(comparatoru256bit_124_greater1), .equal1(comparatoru256bit_124_equal1));  // open: less1
  subtractor256bit subtractor256bit_125 (
    .input1a(subtractor256bit_123_output1a), .input1b(subtractor256bit_123_output1b),
    .input1c(subtractor256bit_123_output1c), .input1d(subtractor256bit_123_output1d),
    .input2a(cbuffer256bit_125_output1a), .input2b(cbuffer256bit_125_output1b),
    .input2c(cbuffer256bit_125_output1c), .input2d(cbuffer256bit_125_output1d),
    .output1a(subtractor256bit_125_output1a), .output1b(subtractor256bit_125_output1b),
    .output1c(subtractor256bit_125_output1c), .output1d(subtractor256bit_125_output1d));  // open: inborrow, borrow
  cbuffer256bit cbuffer256bit_125 (
    .buffer1(and_127_out[1]), .input1a({64{1'b0}}), .input1b({input2[62:0], 1'b0}),
    .input1c({{63{1'b0}}, input2[63]}), .input1d({64{1'b0}}), .output1a(cbuffer256bit_125_output1a),
    .output1b(cbuffer256bit_125_output1b), .output1c(cbuffer256bit_125_output1c),
    .output1d(cbuffer256bit_125_output1d));
  and and_125 (and_127_out[1], not_1_out, or_125_out);
  comparatoru256bit comparatoru256bit_125 (
    .input1a(subtractor256bit_123_output1a), .input1b(subtractor256bit_123_output1b),
    .input1c(subtractor256bit_123_output1c), .input1d(subtractor256bit_123_output1d), .input2a({64{1'b0}}),
    .input2b({input2[62:0], 1'b0}), .input2c({{63{1'b0}}, input2[63]}), .input2d({64{1'b0}}),
    .greater1(comparatoru256bit_125_greater1), .equal1(comparatoru256bit_125_equal1));  // open: less1
  subtractor256bit subtractor256bit_126 (
    .input1a(subtractor256bit_124_output1a), .input1b(subtractor256bit_124_output1b),
    .input1c(subtractor256bit_124_output1c), .input1d(subtractor256bit_124_output1d),
    .input2a(cbuffer256bit_126_output1a), .input2b(cbuffer256bit_126_output1b),
    .input2c(cbuffer256bit_126_output1c), .input2d(cbuffer256bit_126_output1d),
    .output1a(subtractor256bit_126_output1a), .output1b(subtractor256bit_126_output1b),
    .output1c(subtractor256bit_126_output1c), .output1d(subtractor256bit_126_output1d));  // open: inborrow, borrow
  cbuffer256bit cbuffer256bit_126 (
    .buffer1(output1[1]), .input1a({input2[62:0], 1'b0}), .input1b({{63{1'b0}}, input2[63]}),
    .input1c({64{1'b0}}), .input1d({64{1'b0}}), .output1a(cbuffer256bit_126_output1a),
    .output1b(cbuffer256bit_126_output1b), .output1c(cbuffer256bit_126_output1c),
    .output1d(cbuffer256bit_126_output1d));
  and and_126 (output1[1], not_1_out, or_126_out);
  or or_125 (or_125_out, comparatoru256bit_125_greater1, comparatoru256bit_125_equal1);
  or or_126 (or_126_out, comparatoru256bit_126_greater1, comparatoru256bit_126_equal1);
  comparatoru256bit comparatoru256bit_126 (
    .input1a(subtractor256bit_124_output1a), .input1b(subtractor256bit_124_output1b),
    .input1c(subtractor256bit_124_output1c), .input1d(subtractor256bit_124_output1d),
    .input2a({input2[62:0], 1'b0}), .input2b({{63{1'b0}}, input2[63]}), .input2c({64{1'b0}}),
    .input2d({64{1'b0}}), .greater1(comparatoru256bit_126_greater1), .equal1(comparatoru256bit_126_equal1));  // open: less1
  subtractor256bit subtractor256bit_127 (
    .input1a(subtractor256bit_125_output1a), .input1b(subtractor256bit_125_output1b),
    .input1c(subtractor256bit_125_output1c), .input1d(subtractor256bit_125_output1d),
    .input2a(cbuffer256bit_127_output1a), .input2b(cbuffer256bit_127_output1b),
    .input2c(cbuffer256bit_127_output1c), .input2d(cbuffer256bit_127_output1d),
    .output1a(subtractor256bit_127_output1a), .output1b(subtractor256bit_127_output1b),
    .output1c(subtractor256bit_127_output1c), .output1d(subtractor256bit_127_output1d));  // open: inborrow, borrow
  cbuffer256bit cbuffer256bit_127 (
    .buffer1(and_127_out[0]), .input1a({64{1'b0}}), .input1b(input2), .input1c({64{1'b0}}),
    .input1d({64{1'b0}}), .output1a(cbuffer256bit_127_output1a), .output1b(cbuffer256bit_127_output1b),
    .output1c(cbuffer256bit_127_output1c), .output1d(cbuffer256bit_127_output1d));
  and and_127 (and_127_out[0], not_1_out, or_127_out);
  or or_127 (or_127_out, comparatoru256bit_127_greater1, comparatoru256bit_127_equal1);
  comparatoru256bit comparatoru256bit_127 (
    .input1a(subtractor256bit_125_output1a), .input1b(subtractor256bit_125_output1b),
    .input1c(subtractor256bit_125_output1c), .input1d(subtractor256bit_125_output1d), .input2a({64{1'b0}}),
    .input2b(input2), .input2c({64{1'b0}}), .input2d({64{1'b0}}), .greater1(comparatoru256bit_127_greater1),
    .equal1(comparatoru256bit_127_equal1));  // open: less1
  subtractor256bit subtractor256bit_128 (
    .input1a(subtractor256bit_126_output1a), .input1b(subtractor256bit_126_output1b),
    .input1c(subtractor256bit_126_output1c), .input1d(subtractor256bit_126_output1d),
    .input2a(cbuffer256bit_128_output1a), .input2b(cbuffer256bit_128_output1b),
    .input2c(cbuffer256bit_128_output1c), .input2d(cbuffer256bit_128_output1d), .output1a(remainder),
    .output1b(subtractor256bit_128_output1b), .output1c(subtractor256bit_128_output1c),
    .output1d(subtractor256bit_128_output1d));  // open: inborrow, borrow
  cbuffer256bit cbuffer256bit_128 (
    .buffer1(output1[0]), .input1a(input2), .input1b({64{1'b0}}), .input1c({64{1'b0}}), .input1d({64{1'b0}}),
    .output1a(cbuffer256bit_128_output1a), .output1b(cbuffer256bit_128_output1b),
    .output1c(cbuffer256bit_128_output1c), .output1d(cbuffer256bit_128_output1d));
  and and_128 (output1[0], not_1_out, or_128_out);
  or or_128 (or_128_out, comparatoru256bit_128_greater1, comparatoru256bit_128_equal1);
  comparatoru256bit comparatoru256bit_128 (
    .input1a(subtractor256bit_126_output1a), .input1b(subtractor256bit_126_output1b),
    .input1c(subtractor256bit_126_output1c), .input1d(subtractor256bit_126_output1d), .input2a(input2),
    .input2b({64{1'b0}}), .input2c({64{1'b0}}), .input2d({64{1'b0}}),
    .greater1(comparatoru256bit_128_greater1), .equal1(comparatoru256bit_128_equal1));  // open: less1
  // Probe on and_127_out
  // Probe on and_127_out
  // Probe on remainder
  // Probe on remainder
  // Probe on output1
  // Probe on output1

  // Notes on the sheet:
  //   input2: initial=0xfed14b7a
  //   inupper: initial=0xffbbddaa3b5afedc
  //   input1: initial=0xeeddaabb26ebfa3d
endmodule

module comparatoru128bit (
  input  [63:0] input1a,
  input  [63:0] input1b,
  input  [63:0] input2a,
  input  [63:0] input2b,
  output greater1,
  output equal1,
  output less1
);

  wire and_2_out, and_3_out, comparatoru64bit_1_equal1, comparatoru64bit_1_greater1,
       comparatoru64bit_1_less1, comparatoru64bit_2_equal1, comparatoru64bit_2_greater1,
       comparatoru64bit_2_less1;

  comparatoru64bit comparatoru64bit_1 (
    .input1(input1b), .input2(input2b), .greater1(comparatoru64bit_1_greater1),
    .equal1(comparatoru64bit_1_equal1), .less1(comparatoru64bit_1_less1));
  and and_1 (equal1, comparatoru64bit_1_equal1, comparatoru64bit_2_equal1);
  or or_1 (greater1, comparatoru64bit_1_greater1, and_2_out);
  and and_2 (and_2_out, comparatoru64bit_1_equal1, comparatoru64bit_2_greater1);
  or or_2 (less1, comparatoru64bit_1_less1, and_3_out);
  and and_3 (and_3_out, comparatoru64bit_1_equal1, comparatoru64bit_2_less1);
  comparatoru64bit comparatoru64bit_2 (
    .input1(input1a), .input2(input2a), .greater1(comparatoru64bit_2_greater1),
    .equal1(comparatoru64bit_2_equal1), .less1(comparatoru64bit_2_less1));

  // Notes on the sheet:
  //   input1b: initial=0x2
  //   input2b: initial=0x3
endmodule

module comparatoru256bit (
  input  [63:0] input1a,
  input  [63:0] input1b,
  input  [63:0] input1c,
  input  [63:0] input1d,
  input  [63:0] input2a,
  input  [63:0] input2b,
  input  [63:0] input2c,
  input  [63:0] input2d,
  output greater1,
  output equal1,
  output less1
);

  wire and_2_out, and_3_out, comparatoru128bit_1_equal1, comparatoru128bit_1_greater1,
       comparatoru128bit_1_less1, comparatoru128bit_2_equal1, comparatoru128bit_2_greater1,
       comparatoru128bit_2_less1;

  comparatoru128bit comparatoru128bit_1 (
    .input1a(input1c), .input1b(input1d), .input2a(input2c), .input2b(input2d),
    .greater1(comparatoru128bit_1_greater1), .equal1(comparatoru128bit_1_equal1),
    .less1(comparatoru128bit_1_less1));
  and and_1 (equal1, comparatoru128bit_1_equal1, comparatoru128bit_2_equal1);
  or or_1 (greater1, comparatoru128bit_1_greater1, and_2_out);
  and and_2 (and_2_out, comparatoru128bit_1_equal1, comparatoru128bit_2_greater1);
  or or_2 (less1, comparatoru128bit_1_less1, and_3_out);
  and and_3 (and_3_out, comparatoru128bit_1_equal1, comparatoru128bit_2_less1);
  comparatoru128bit comparatoru128bit_2 (
    .input1a(input1a), .input1b(input1b), .input2a(input2a), .input2b(input2b),
    .greater1(comparatoru128bit_2_greater1), .equal1(comparatoru128bit_2_equal1),
    .less1(comparatoru128bit_2_less1));
endmodule
