// Logisim project fpcomp.circ as structural Verilog
module fneg64 (
  input  [63:0] inval1,
  output [63:0] outval1,
  output isnan1
);

  wire fpnegator_1_p2;

  // Probe on inval1
  // FPNegator #(.fpwidth(64)) fpnegator_1: pin names not known; wires that end beside it: inval1, fpnegator_1_p2
  not not_1 (outval1[63], inval1[63]);
  Comparator #(.width(11)) comparator_1 (.a(inval1[62:52]), .b({11{1'b1}}), .eq(isnan1));  // open: gt, lt
  // Probe on fpnegator_1_p2
  // Probe on {outval1[63], inval1[62:0]}

  assign outval1[62:0] = inval1[62:0];

  // Notes on the sheet:
  //   inval1: initial=0x4040152bd3c36113
endmodule

module fadd64 (
  input  [63:0] in_1,
  input  [63:0] in_2,
  input  [63:0] in_3,
  input  [63:0] inval1,
  input  [63:0] inval2,
  output [63:0] outval1,
  output isnan1
);

  wire comparator_1_eq, comparator_2_eq, comparator_3_gt, subtractor_1_bout;
  wire [5:0] hone64_1_outval1, multiplexer_3_out, subtractor_4_out, subtractor_5_out;
  wire [10:0] bit_extender_3_out, multiplexer_7_out;
  wire [15:0] bit_extender_1_out, bit_extender_2_out, negator_1_out, subtractor_1_out, subtractor_2_out,
       subtractor_3_out;
  wire [15:6] multiplexer_3_out_2;
  wire [63:0] adder_1_out, adder_2_out, fpadder_1_out, multiplexer_1_out, multiplexer_2_out,
       multiplexer_4_out, multiplexer_5_out, multiplexer_6_out, multiplexer_8_out, multiplexer_9_out,
       multiplexer_10_out, multiplexer_11_out, negator_2_out, negator_3_out, negator_4_out, shifter_1_out,
       shifter_2_out;

  // Probe on inval1
  // Probe on inval2
  Comparator #(.width(11)) comparator_1 (.a(inval1[62:52]), .b({11{1'b1}}), .eq(comparator_1_eq));  // open: gt, lt
  Comparator #(.width(11)) comparator_2 (.a(inval2[62:52]), .b({11{1'b1}}), .eq(comparator_2_eq));  // open: gt, lt
  Multiplexer #(.width(64)) multiplexer_1 (
    .in0({3'b001, inval1[51:0], {9{1'b0}}}), .in1({3'b001, inval2[51:0], {9{1'b0}}}),
    .out(multiplexer_1_out), .sel(subtractor_1_bout));
  Multiplexer #(.width(64)) multiplexer_2 (
    .in0({3'b001, inval2[51:0], {9{1'b0}}}), .in1({3'b001, inval1[51:0], {9{1'b0}}}),
    .out(multiplexer_2_out), .sel(subtractor_1_bout));
  Subtractor #(.width(16)) subtractor_1 (
    .a(subtractor_2_out), .b(subtractor_3_out), .out(subtractor_1_out), .bout(subtractor_1_bout));  // open: bin
  Subtractor #(.width(16)) subtractor_2 (
    .a(bit_extender_1_out), .b(16'h3ff), .out(subtractor_2_out));  // open: bin, bout
  assign bit_extender_1_out = {{5{1'b0}}, inval1[62:52]};  // Bit_Extender bit_extender_1
  or or_1 (isnan1, comparator_1_eq, comparator_2_eq);
  FPAdder #(.fpwidth(64)) fpadder_1 (.a(inval1), .b(inval2), .out(fpadder_1_out));
  Shifter #(.shift("lr"), .width(64)) shifter_1 (
    .in(multiplexer_2_out), .\dist (multiplexer_3_out), .out(shifter_1_out));
  Multiplexer #(.width(16)) multiplexer_3 (
    .in0(subtractor_1_out), .in1(negator_1_out), .out({multiplexer_3_out_2, multiplexer_3_out}),
    .sel(subtractor_1_bout));
  Negator #(.width(16)) negator_1 (.in(subtractor_1_out), .out(negator_1_out));
  Subtractor #(.width(16)) subtractor_3 (
    .a(bit_extender_2_out), .b(16'h3ff), .out(subtractor_3_out));  // open: bin, bout
  assign bit_extender_2_out = {{5{1'b0}}, inval2[62:52]};  // Bit_Extender bit_extender_2
  Comparator #(.width(16)) comparator_3 (
    .a({multiplexer_3_out_2, multiplexer_3_out}), .b(16'h3f), .gt(comparator_3_gt));  // open: eq, lt
  Multiplexer #(.width(64)) multiplexer_4 (
    .in0(shifter_1_out), .in1({64{1'b0}}), .out(multiplexer_4_out), .sel(comparator_3_gt));
  Multiplexer #(.width(64)) multiplexer_5 (
    .in0(multiplexer_1_out), .in1(multiplexer_4_out), .out(multiplexer_5_out), .sel(subtractor_1_bout));
  Multiplexer #(.width(64)) multiplexer_6 (
    .in0(multiplexer_4_out), .in1(multiplexer_1_out), .out(multiplexer_6_out), .sel(subtractor_1_bout));
  Multiplexer #(.width(11)) multiplexer_7 (
    .in0(inval1[62:52]), .in1(inval2[62:52]), .out(multiplexer_7_out), .sel(subtractor_1_bout));
  Negator #(.width(64)) negator_2 (.in(multiplexer_6_out), .out(negator_2_out));
  Negator #(.width(64)) negator_3 (.in(multiplexer_5_out), .out(negator_3_out));
  Multiplexer #(.width(64)) multiplexer_8 (
    .in0(multiplexer_6_out), .in1(negator_2_out), .out(multiplexer_8_out), .sel(inval2[63]));
  Multiplexer #(.width(64)) multiplexer_9 (
    .in0(multiplexer_5_out), .in1(negator_3_out), .out(multiplexer_9_out), .sel(inval1[63]));
  Adder #(.width(64)) adder_1 (.a(multiplexer_9_out), .b(multiplexer_8_out), .out(adder_1_out));  // open: cin, cout
  Negator #(.width(64)) negator_4 (.in(adder_1_out), .out(negator_4_out));
  Comparator #(.width(64)) comparator_4 (.a(adder_1_out), .b({64{1'b0}}), .lt(outval1[63]));  // open: gt, eq
  Multiplexer #(.width(64)) multiplexer_10 (
    .in0(adder_1_out), .in1(negator_4_out), .out(multiplexer_10_out), .sel(outval1[63]));
  Shifter #(.width(64)) shifter_2 (.in(multiplexer_10_out), .\dist (subtractor_4_out), .out(shifter_2_out));
  Subtractor #(.width(6)) subtractor_4 (
    .a({6{1'b1}}), .b(hone64_1_outval1), .out(subtractor_4_out));  // open: bin, bout
  Subtractor #(.width(6)) subtractor_5 (
    .a(subtractor_4_out), .b(6'b000010), .out(subtractor_5_out));  // open: bin, bout
  hone64 hone64_1 (.inval1(multiplexer_10_out), .outval1(hone64_1_outval1));  // open: contains1
  assign bit_extender_3_out = {{5{subtractor_5_out[5]}}, subtractor_5_out};  // Bit_Extender bit_extender_3
  Subtractor #(.width(11)) subtractor_6 (
    .a(multiplexer_7_out), .b(bit_extender_3_out), .out(outval1[62:52]));  // open: bin, bout
  Multiplexer #(.width(64)) multiplexer_11 (
    .in0(shifter_2_out), .in1(adder_2_out),
    .out({multiplexer_11_out[63], outval1[51:0], multiplexer_11_out[10:0]}), .sel(shifter_2_out[10]));
  Adder #(.width(64)) adder_2 (.a(64'h800), .b(shifter_2_out), .out(adder_2_out));  // open: cin, cout
  // Probe on fpadder_1_out
  // Probe on fpadder_1_out
  // Probe on outval1

  // Notes on the sheet:
  //   in_1: initial=0x4040152bd3c36113
  //   in_2: initial=0x4061d93f7ced9168
  //   in_3: initial=0xc056ef0d844d013b
  //   inval1: initial=0x4040152bd3c36113
  //   inval2: initial=0x4061d93f7ced9168
endmodule

module fsub64 (
  input  [63:0] inval1,
  input  [63:0] inval2,
  output [63:0] outval1
);
endmodule

module fmul64 (
  input  [63:0] inval1,
  input  [63:0] inval2,
  output [63:0] outval1
);
endmodule

module fdiv64 (
  input  [63:0] inval1,
  input  [63:0] inval2,
  output [63:0] outval1
);
endmodule

module hone64 (
  input  [63:0] inval1,
  output [5:0] outval1,
  output contains1
);

  wire bitfinder_1_found, not_1_out;
  wire [5:0] bitfinder_1_index, priority_encoder_1_out;

  // Probe on priority_encoder_1_out
  Priority_Encoder #(.select(6)) priority_encoder_1 (
    .in0(inval1[0]), .in1(inval1[1]), .in2(inval1[2]), .in3(inval1[3]), .in4(inval1[4]), .in5(inval1[5]),
    .in6(inval1[6]), .in7(inval1[7]), .in8(inval1[8]), .in9(inval1[9]), .in10(inval1[10]), .in11(inval1[11]),
    .in12(inval1[12]), .in13(inval1[13]), .in14(inval1[14]), .in15(inval1[15]), .in16(inval1[16]),
    .in17(inval1[17]), .in18(inval1[18]), .in19(inval1[19]), .in20(inval1[20]), .in21(inval1[21]),
    .in22(inval1[22]), .in23(inval1[23]), .in24(inval1[24]), .in25(inval1[25]), .in26(inval1[26]),
    .in27(inval1[27]), .in28(inval1[28]), .in29(inval1[29]), .in30(inval1[30]), .in31(inval1[31]),
    .in32(inval1[32]), .in33(inval1[33]), .in34(inval1[34]), .in35(inval1[35]), .in36(inval1[36]),
    .in37(inval1[37]), .in38(inval1[38]), .in39(inval1[39]), .in40(inval1[40]), .in41(inval1[41]),
    .in42(inval1[42]), .in43(inval1[43]), .in44(inval1[44]), .in45(inval1[45]), .in46(inval1[46]),
    .in47(inval1[47]), .in48(inval1[48]), .in49(inval1[49]), .in50(inval1[50]), .in51(inval1[51]),
    .in52(inval1[52]), .in53(inval1[53]), .in54(inval1[54]), .in55(inval1[55]), .in56(inval1[56]),
    .in57(inval1[57]), .in58(inval1[58]), .in59(inval1[59]), .in60(inval1[60]), .in61(inval1[61]),
    .in62(inval1[62]), .in63(inval1[63]), .out(priority_encoder_1_out), .gs(contains1));  // open: en_out, en_in
  BitFinder #(.\type ("high1"), .width(64)) bitfinder_1 (
    .in(inval1), .index(bitfinder_1_index), .found(bitfinder_1_found));
  Multiplexer #(.width(6)) multiplexer_1 (
    .in0(priority_encoder_1_out), .in1({6{1'b0}}), .out(outval1), .sel(not_1_out));
  not not_1 (not_1_out, contains1);
  // Probe on bitfinder_1_index
  // Probe on bitfinder_1_found
  // Probe on outval1

  // Notes on the sheet:
  //   inval1: initial=0xb000000003ff
endmodule

module add128 (
  input  [63:0] inval1a,
  input  [63:0] inval1b,
  input  [63:0] inval2a,
  input  [63:0] inval2b,
  input  carryin1,
  output [63:0] outval1a,
  output [63:0] outval1b,
  output carryout1
);

  wire adder_1_cout;

  Adder #(.width(64)) adder_1 (.a(inval1a), .b(inval2a), .out(outval1a), .cin(carryin1), .cout(adder_1_cout));
  Adder #(.width(64)) adder_2 (.a(inval1b), .b(inval2b), .out(outval1b), .cin(adder_1_cout), .cout(carryout1));

  // Notes on the sheet:
  //   inval1a: initial=0xf000b000000003ff
  //   inval1b: initial=0xfff0000bff
  //   inval2a: initial=0x8321000000001234
  //   inval2b: initial=0xb0000a4b2
endmodule

module neg128 (
  input  [63:0] inval1a,
  input  [63:0] inval1b,
  output [63:0] outval1a,
  output [63:0] outval1b
);

  wire adder_1_cout;
  wire [63:0] not_1_out, not_2_out;

  assign not_1_out = ~inval1a;  // NOT_Gate not_1, 64 bits wide
  assign not_2_out = ~inval1b;  // NOT_Gate not_2, 64 bits wide
  Adder #(.width(64)) adder_1 (.a(64'h1), .b(not_1_out), .out(outval1a), .cout(adder_1_cout));  // open: cin
  Adder #(.width(64)) adder_2 (.a(not_2_out), .b({64{1'b0}}), .out(outval1b), .cin(adder_1_cout));  // open: cout

  // Notes on the sheet:
  //   inval1a: initial=0x8000000000000000
  //   inval1b: initial=0xb000000003ff
endmodule

module shl128 (
  input  [63:0] inval1a,
  input  [63:0] inval1b,
  input  [6:0] shift1a,
  output [63:0] outval1a,
  output [63:0] outval1b
);

  wire [63:0] and_1_out, and_2_out, not_1_out, or_1_out, shifter_1_out, shifter_2_out, shifter_3_out,
       shifter_4_out;

  Shifter #(.width(64)) shifter_1 (.in({64{1'b1}}), .\dist (shift1a[5:0]), .out(shifter_1_out));
  Shifter #(.shift("rl"), .width(64)) shifter_2 (.in(inval1a), .\dist (shift1a[5:0]), .out(shifter_2_out));
  Shifter #(.width(64)) shifter_3 (.in(inval1b), .\dist (shift1a[5:0]), .out(shifter_3_out));
  Shifter #(.width(64)) shifter_4 (.in(inval1a), .\dist (shift1a[5:0]), .out(shifter_4_out));
  assign not_1_out = ~shifter_1_out;  // NOT_Gate not_1, 64 bits wide
  assign and_1_out = not_1_out & shifter_2_out;  // AND_Gate and_1, 64 bits wide
  assign and_2_out = shifter_1_out & shifter_2_out;  // AND_Gate and_2, 64 bits wide
  assign or_1_out = and_1_out | shifter_3_out;  // OR_Gate or_1, 64 bits wide
  Multiplexer #(.width(64)) multiplexer_1 (.in0(and_2_out), .in1({64{1'b0}}), .out(outval1a), .sel(shift1a[6]));
  Multiplexer #(.width(64)) multiplexer_2 (.in0(or_1_out), .in1(shifter_4_out), .out(outval1b), .sel(shift1a[6]));

  // Notes on the sheet:
  //   inval1a: initial=0xffff000000000000
  //   inval1b: initial=0xf00000000fff
  //   shift1a: initial=0x10
endmodule

module shr128 (
  input  [63:0] inval1a,
  input  [63:0] inval1b,
  input  [6:0] shift1a,
  output [63:0] outval1a,
  output [63:0] outval1b
);

  wire [63:0] and_1_out, and_2_out, not_1_out, or_1_out, shifter_1_out, shifter_2_out, shifter_3_out,
       shifter_4_out;

  Shifter #(.shift("lr"), .width(64)) shifter_1 (.in(inval1b), .\dist (shift1a[5:0]), .out(shifter_1_out));
  Shifter #(.shift("lr"), .width(64)) shifter_2 (.in(inval1a), .\dist (shift1a[5:0]), .out(shifter_2_out));
  Shifter #(.shift("lr"), .width(64)) shifter_3 (.in({64{1'b1}}), .\dist (shift1a[5:0]), .out(shifter_3_out));
  Shifter #(.shift("rr"), .width(64)) shifter_4 (.in(inval1b), .\dist (shift1a[5:0]), .out(shifter_4_out));
  assign not_1_out = ~shifter_3_out;  // NOT_Gate not_1, 64 bits wide
  assign and_1_out = not_1_out & shifter_4_out;  // AND_Gate and_1, 64 bits wide
  assign and_2_out = shifter_3_out & shifter_4_out;  // AND_Gate and_2, 64 bits wide
  assign or_1_out = shifter_2_out | and_1_out;  // OR_Gate or_1, 64 bits wide
  Multiplexer #(.width(64)) multiplexer_1 (.in0(or_1_out), .in1(shifter_1_out), .out(outval1a), .sel(shift1a[6]));
  Multiplexer #(.width(64)) multiplexer_2 (.in0(and_2_out), .in1({64{1'b0}}), .out(outval1b), .sel(shift1a[6]));

  // Notes on the sheet:
  //   inval1a: initial=0xffff000000000000
  //   inval1b: initial=0xf00000000fff
  //   shift1a: initial=0x10
endmodule

module lone64 (
  input  [63:0] inval1,
  output [5:0] outval1,
  output contains1
);

  wire bitfinder_1_found, not_1_out;
  wire [5:0] bitfinder_1_index, priority_encoder_1_p1, subtractor_1_out;

  BitFinder #(.width(64)) bitfinder_1 (.in(inval1), .index(bitfinder_1_index), .found(bitfinder_1_found));
  // Probe on priority_encoder_1_p1
  // Priority_Encoder #(.select(6)) priority_encoder_1: pin names not known; wires that end beside it: priority_encoder_1_p1, contains1
  Subtractor #(.width(6)) subtractor_1 (
    .a({6{1'b1}}), .b(priority_encoder_1_p1), .out(subtractor_1_out));  // open: bin, bout
  Multiplexer #(.width(6)) multiplexer_1 (.in0(subtractor_1_out), .in1({6{1'b0}}), .out(outval1), .sel(not_1_out));
  not not_1 (not_1_out, contains1);
  // Probe on bitfinder_1_index
  // Probe on bitfinder_1_found
  // Probe on outval1

  // Notes on the sheet:
  //   inval1: initial=0xb0000003ff80
endmodule

module hzero64 (
  input  [63:0] inval1,
  output [5:0] outval1,
  output contains1
);

  wire bitfinder_1_found, not_2_out;
  wire [5:0] bitfinder_1_index, priority_encoder_1_out;
  wire [63:0] not_1_out;

  assign not_1_out = ~inval1;  // NOT_Gate not_1, 64 bits wide
  // Probe on priority_encoder_1_out
  Priority_Encoder #(.select(6)) priority_encoder_1 (
    .in0(not_1_out[0]), .in1(not_1_out[1]), .in2(not_1_out[2]), .in3(not_1_out[3]), .in4(not_1_out[4]),
    .in5(not_1_out[5]), .in6(not_1_out[6]), .in7(not_1_out[7]), .in8(not_1_out[8]), .in9(not_1_out[9]),
    .in10(not_1_out[10]), .in11(not_1_out[11]), .in12(not_1_out[12]), .in13(not_1_out[13]),
    .in14(not_1_out[14]), .in15(not_1_out[15]), .in16(not_1_out[16]), .in17(not_1_out[17]),
    .in18(not_1_out[18]), .in19(not_1_out[19]), .in20(not_1_out[20]), .in21(not_1_out[21]),
    .in22(not_1_out[22]), .in23(not_1_out[23]), .in24(not_1_out[24]), .in25(not_1_out[25]),
    .in26(not_1_out[26]), .in27(not_1_out[27]), .in28(not_1_out[28]), .in29(not_1_out[29]),
    .in30(not_1_out[30]), .in31(not_1_out[31]), .in32(not_1_out[32]), .in33(not_1_out[33]),
    .in34(not_1_out[34]), .in35(not_1_out[35]), .in36(not_1_out[36]), .in37(not_1_out[37]),
    .in38(not_1_out[38]), .in39(not_1_out[39]), .in40(not_1_out[40]), .in41(not_1_out[41]),
    .in42(not_1_out[42]), .in43(not_1_out[43]), .in44(not_1_out[44]), .in45(not_1_out[45]),
    .in46(not_1_out[46]), .in47(not_1_out[47]), .in48(not_1_out[48]), .in49(not_1_out[49]),
    .in50(not_1_out[50]), .in51(not_1_out[51]), .in52(not_1_out[52]), .in53(not_1_out[53]),
    .in54(not_1_out[54]), .in55(not_1_out[55]), .in56(not_1_out[56]), .in57(not_1_out[57]),
    .in58(not_1_out[58]), .in59(not_1_out[59]), .in60(not_1_out[60]), .in61(not_1_out[61]),
    .in62(not_1_out[62]), .in63(not_1_out[63]), .out(priority_encoder_1_out), .gs(contains1));  // open: en_out, en_in
  BitFinder #(.\type ("high0"), .width(64)) bitfinder_1 (
    .in(inval1), .index(bitfinder_1_index), .found(bitfinder_1_found));
  Multiplexer #(.width(6)) multiplexer_1 (
    .in0(priority_encoder_1_out), .in1({6{1'b0}}), .out(outval1), .sel(not_2_out));
  not not_2 (not_2_out, contains1);
  // Probe on bitfinder_1_index
  // Probe on bitfinder_1_found
  // Probe on outval1

  // Notes on the sheet:
  //   inval1: initial=0xffffb000003fffff
endmodule

module lzero64 (
  input  [63:0] inval1,
  output [5:0] outval1,
  output contains1
);

  wire bitfinder_1_found, not_2_out;
  wire [5:0] bitfinder_1_index, priority_encoder_1_p1, subtractor_1_out;
  wire [63:0] not_1_out;

  assign not_1_out = ~inval1;  // NOT_Gate not_1, 64 bits wide
  BitFinder #(.\type ("low0"), .width(64)) bitfinder_1 (
    .in(inval1), .index(bitfinder_1_index), .found(bitfinder_1_found));
  // Probe on priority_encoder_1_p1
  // Priority_Encoder #(.select(6)) priority_encoder_1: pin names not known; wires that end beside it: priority_encoder_1_p1, contains1
  Subtractor #(.width(6)) subtractor_1 (
    .a({6{1'b1}}), .b(priority_encoder_1_p1), .out(subtractor_1_out));  // open: bin, bout
  Multiplexer #(.width(6)) multiplexer_1 (.in0(subtractor_1_out), .in1({6{1'b0}}), .out(outval1), .sel(not_2_out));
  not not_2 (not_2_out, contains1);
  // Probe on bitfinder_1_index
  // Probe on bitfinder_1_found
  // Probe on outval1

  // Notes on the sheet:
  //   inval1: initial=0xffffb0000003ffff
endmodule

module ones64 (
  input  [63:0] inval1,
  output [6:0] outval1
);

  wire [1:0] adder_1_out, adder_2_out, adder_3_out, adder_4_out, adder_5_out, adder_6_out, adder_7_out,
       adder_8_out, adder_9_out, adder_10_out, adder_11_out, adder_12_out, adder_13_out, adder_14_out,
       adder_15_out, adder_16_out, adder_17_out, adder_18_out, adder_19_out, adder_20_out, adder_21_out,
       adder_22_out, adder_23_out, adder_24_out, adder_25_out, adder_26_out, adder_27_out, adder_28_out,
       adder_29_out, adder_30_out, adder_31_out, adder_32_out, adder_33_out, adder_34_out, adder_35_out,
       adder_36_out, adder_37_out, adder_38_out, adder_39_out, adder_40_out, adder_41_out, adder_42_out,
       adder_43_out, adder_44_out, adder_45_out, adder_46_out, adder_47_out, adder_48_out;
  wire [2:0] adder_49_out, adder_50_out, adder_51_out, adder_52_out, adder_53_out, adder_54_out,
       adder_55_out, adder_56_out;
  wire [2:2] adder_33_cout, adder_34_cout, adder_35_cout, adder_36_cout, adder_37_cout, adder_38_cout,
       adder_39_cout, adder_40_cout, adder_41_cout, adder_42_cout, adder_43_cout, adder_44_cout,
       adder_45_cout, adder_46_cout, adder_47_cout, adder_48_cout;
  wire [3:0] adder_57_out, adder_58_out, adder_59_out, adder_60_out;
  wire [3:3] adder_49_cout, adder_50_cout, adder_51_cout, adder_52_cout, adder_53_cout, adder_54_cout,
       adder_55_cout, adder_56_cout;
  wire [4:0] adder_61_out, adder_62_out;
  wire [4:4] adder_57_cout, adder_58_cout, adder_59_cout, adder_60_cout;
  wire [5:5] adder_61_cout, adder_62_cout;
  wire [6:0] bitadder_1_out;

  BitAdder #(.width(64)) bitadder_1 (.in0(inval1), .out(bitadder_1_out));
  Adder #(.width(1)) adder_1 (.a(inval1[0]), .b(inval1[1]), .out(adder_1_out[0]), .cout(adder_1_out[1]));  // open: cin
  Adder #(.width(1)) adder_2 (.a(inval1[2]), .b(inval1[3]), .out(adder_2_out[0]), .cout(adder_2_out[1]));  // open: cin
  Adder #(.width(1)) adder_3 (.a(inval1[4]), .b(inval1[5]), .out(adder_3_out[0]), .cout(adder_3_out[1]));  // open: cin
  Adder #(.width(1)) adder_4 (.a(inval1[6]), .b(inval1[7]), .out(adder_4_out[0]), .cout(adder_4_out[1]));  // open: cin
  Adder #(.width(1)) adder_5 (.a(inval1[8]), .b(inval1[9]), .out(adder_5_out[0]), .cout(adder_5_out[1]));  // open: cin
  Adder #(.width(1)) adder_6 (
    .a(inval1[10]), .b(inval1[11]), .out(adder_6_out[0]), .cout(adder_6_out[1]));  // open: cin
  Adder #(.width(1)) adder_7 (
    .a(inval1[12]), .b(inval1[13]), .out(adder_7_out[0]), .cout(adder_7_out[1]));  // open: cin
  Adder #(.width(1)) adder_8 (
    .a(inval1[14]), .b(inval1[15]), .out(adder_8_out[0]), .cout(adder_8_out[1]));  // open: cin
  Adder #(.width(1)) adder_9 (
    .a(inval1[16]), .b(inval1[17]), .out(adder_9_out[0]), .cout(adder_9_out[1]));  // open: cin
  Adder #(.width(1)) adder_10 (
    .a(inval1[18]), .b(inval1[19]), .out(adder_10_out[0]), .cout(adder_10_out[1]));  // open: cin
  Adder #(.width(1)) adder_11 (
    .a(inval1[20]), .b(inval1[21]), .out(adder_11_out[0]), .cout(adder_11_out[1]));  // open: cin
  Adder #(.width(1)) adder_12 (
    .a(inval1[22]), .b(inval1[23]), .out(adder_12_out[0]), .cout(adder_12_out[1]));  // open: cin
  Adder #(.width(1)) adder_13 (
    .a(inval1[24]), .b(inval1[25]), .out(adder_13_out[0]), .cout(adder_13_out[1]));  // open: cin
  Adder #(.width(1)) adder_14 (
    .a(inval1[26]), .b(inval1[27]), .out(adder_14_out[0]), .cout(adder_14_out[1]));  // open: cin
  Adder #(.width(1)) adder_15 (
    .a(inval1[28]), .b(inval1[29]), .out(adder_15_out[0]), .cout(adder_15_out[1]));  // open: cin
  Adder #(.width(1)) adder_16 (
    .a(inval1[30]), .b(inval1[31]), .out(adder_16_out[0]), .cout(adder_16_out[1]));  // open: cin
  Adder #(.width(1)) adder_17 (
    .a(inval1[32]), .b(inval1[33]), .out(adder_17_out[0]), .cout(adder_17_out[1]));  // open: cin
  Adder #(.width(1)) adder_18 (
    .a(inval1[34]), .b(inval1[35]), .out(adder_18_out[0]), .cout(adder_18_out[1]));  // open: cin
  Adder #(.width(1)) adder_19 (
    .a(inval1[36]), .b(inval1[37]), .out(adder_19_out[0]), .cout(adder_19_out[1]));  // open: cin
  Adder #(.width(1)) adder_20 (
    .a(inval1[38]), .b(inval1[39]), .out(adder_20_out[0]), .cout(adder_20_out[1]));  // open: cin
  Adder #(.width(1)) adder_21 (
    .a(inval1[40]), .b(inval1[41]), .out(adder_21_out[0]), .cout(adder_21_out[1]));  // open: cin
  Adder #(.width(1)) adder_22 (
    .a(inval1[42]), .b(inval1[43]), .out(adder_22_out[0]), .cout(adder_22_out[1]));  // open: cin
  Adder #(.width(1)) adder_23 (
    .a(inval1[44]), .b(inval1[45]), .out(adder_23_out[0]), .cout(adder_23_out[1]));  // open: cin
  Adder #(.width(1)) adder_24 (
    .a(inval1[46]), .b(inval1[47]), .out(adder_24_out[0]), .cout(adder_24_out[1]));  // open: cin
  Adder #(.width(1)) adder_25 (
    .a(inval1[48]), .b(inval1[49]), .out(adder_25_out[0]), .cout(adder_25_out[1]));  // open: cin
  Adder #(.width(1)) adder_26 (
    .a(inval1[50]), .b(inval1[51]), .out(adder_26_out[0]), .cout(adder_26_out[1]));  // open: cin
  Adder #(.width(1)) adder_27 (
    .a(inval1[52]), .b(inval1[53]), .out(adder_27_out[0]), .cout(adder_27_out[1]));  // open: cin
  Adder #(.width(1)) adder_28 (
    .a(inval1[54]), .b(inval1[55]), .out(adder_28_out[0]), .cout(adder_28_out[1]));  // open: cin
  Adder #(.width(1)) adder_29 (
    .a(inval1[56]), .b(inval1[57]), .out(adder_29_out[0]), .cout(adder_29_out[1]));  // open: cin
  Adder #(.width(1)) adder_30 (
    .a(inval1[58]), .b(inval1[59]), .out(adder_30_out[0]), .cout(adder_30_out[1]));  // open: cin
  Adder #(.width(1)) adder_31 (
    .a(inval1[60]), .b(inval1[61]), .out(adder_31_out[0]), .cout(adder_31_out[1]));  // open: cin
  Adder #(.width(1)) adder_32 (
    .a(inval1[62]), .b(inval1[63]), .out(adder_32_out[0]), .cout(adder_32_out[1]));  // open: cin
  Adder #(.width(2)) adder_33 (
    .a(adder_1_out), .b(adder_2_out), .out(adder_33_out), .cout(adder_33_cout[2]));  // open: cin
  Adder #(.width(2)) adder_34 (
    .a(adder_3_out), .b(adder_4_out), .out(adder_34_out), .cout(adder_34_cout[2]));  // open: cin
  Adder #(.width(2)) adder_35 (
    .a(adder_5_out), .b(adder_6_out), .out(adder_35_out), .cout(adder_35_cout[2]));  // open: cin
  Adder #(.width(2)) adder_36 (
    .a(adder_7_out), .b(adder_8_out), .out(adder_36_out), .cout(adder_36_cout[2]));  // open: cin
  Adder #(.width(2)) adder_37 (
    .a(adder_9_out), .b(adder_10_out), .out(adder_37_out), .cout(adder_37_cout[2]));  // open: cin
  Adder #(.width(2)) adder_38 (
    .a(adder_11_out), .b(adder_12_out), .out(adder_38_out), .cout(adder_38_cout[2]));  // open: cin
  Adder #(.width(2)) adder_39 (
    .a(adder_13_out), .b(adder_14_out), .out(adder_39_out), .cout(adder_39_cout[2]));  // open: cin
  Adder #(.width(2)) adder_40 (
    .a(adder_15_out), .b(adder_16_out), .out(adder_40_out), .cout(adder_40_cout[2]));  // open: cin
  Adder #(.width(2)) adder_41 (
    .a(adder_17_out), .b(adder_18_out), .out(adder_41_out), .cout(adder_41_cout[2]));  // open: cin
  Adder #(.width(2)) adder_42 (
    .a(adder_19_out), .b(adder_20_out), .out(adder_42_out), .cout(adder_42_cout[2]));  // open: cin
  Adder #(.width(2)) adder_43 (
    .a(adder_21_out), .b(adder_22_out), .out(adder_43_out), .cout(adder_43_cout[2]));  // open: cin
  Adder #(.width(2)) adder_44 (
    .a(adder_23_out), .b(adder_24_out), .out(adder_44_out), .cout(adder_44_cout[2]));  // open: cin
  Adder #(.width(2)) adder_45 (
    .a(adder_25_out), .b(adder_26_out), .out(adder_45_out), .cout(adder_45_cout[2]));  // open: cin
  Adder #(.width(2)) adder_46 (
    .a(adder_27_out), .b(adder_28_out), .out(adder_46_out), .cout(adder_46_cout[2]));  // open: cin
  Adder #(.width(2)) adder_47 (
    .a(adder_29_out), .b(adder_30_out), .out(adder_47_out), .cout(adder_47_cout[2]));  // open: cin
  Adder #(.width(2)) adder_48 (
    .a(adder_31_out), .b(adder_32_out), .out(adder_48_out), .cout(adder_48_cout[2]));  // open: cin
  Adder #(.width(3)) adder_49 (
    .a({adder_33_cout[2], adder_33_out}), .b({adder_34_cout[2], adder_34_out}), .out(adder_49_out),
    .cout(adder_49_cout[3]));  // open: cin
  Adder #(.width(3)) adder_50 (
    .a({adder_35_cout[2], adder_35_out}), .b({adder_36_cout[2], adder_36_out}), .out(adder_50_out),
    .cout(adder_50_cout[3]));  // open: cin
  Adder #(.width(3)) adder_51 (
    .a({adder_37_cout[2], adder_37_out}), .b({adder_38_cout[2], adder_38_out}), .out(adder_51_out),
    .cout(adder_51_cout[3]));  // open: cin
  Adder #(.width(3)) adder_52 (
    .a({adder_39_cout[2], adder_39_out}), .b({adder_40_cout[2], adder_40_out}), .out(adder_52_out),
    .cout(adder_52_cout[3]));  // open: cin
  Adder #(.width(3)) adder_53 (
    .a({adder_41_cout[2], adder_41_out}), .b({adder_42_cout[2], adder_42_out}), .out(adder_53_out),
    .cout(adder_53_cout[3]));  // open: cin
  Adder #(.width(3)) adder_54 (
    .a({adder_43_cout[2], adder_43_out}), .b({adder_44_cout[2], adder_44_out}), .out(adder_54_out),
    .cout(adder_54_cout[3]));  // open: cin
  Adder #(.width(3)) adder_55 (
    .a({adder_45_cout[2], adder_45_out}), .b({adder_46_cout[2], adder_46_out}), .out(adder_55_out),
    .cout(adder_55_cout[3]));  // open: cin
  Adder #(.width(3)) adder_56 (
    .a({adder_47_cout[2], adder_47_out}), .b({adder_48_cout[2], adder_48_out}), .out(adder_56_out),
    .cout(adder_56_cout[3]));  // open: cin
  Adder #(.width(4)) adder_57 (
    .a({adder_49_cout[3], adder_49_out}), .b({adder_50_cout[3], adder_50_out}), .out(adder_57_out),
    .cout(adder_57_cout[4]));  // open: cin
  Adder #(.width(4)) adder_58 (
    .a({adder_51_cout[3], adder_51_out}), .b({adder_52_cout[3], adder_52_out}), .out(adder_58_out),
    .cout(adder_58_cout[4]));  // open: cin
  Adder #(.width(4)) adder_59 (
    .a({adder_53_cout[3], adder_53_out}), .b({adder_54_cout[3], adder_54_out}), .out(adder_59_out),
    .cout(adder_59_cout[4]));  // open: cin
  Adder #(.width(4)) adder_60 (
    .a({adder_55_cout[3], adder_55_out}), .b({adder_56_cout[3], adder_56_out}), .out(adder_60_out),
    .cout(adder_60_cout[4]));  // open: cin
  Adder #(.width(5)) adder_61 (
    .a({adder_57_cout[4], adder_57_out}), .b({adder_58_cout[4], adder_58_out}), .out(adder_61_out),
    .cout(adder_61_cout[5]));  // open: cin
  Adder #(.width(5)) adder_62 (
    .a({adder_59_cout[4], adder_59_out}), .b({adder_60_cout[4], adder_60_out}), .out(adder_62_out),
    .cout(adder_62_cout[5]));  // open: cin
  Adder #(.width(6)) adder_63 (
    .a({adder_61_cout[5], adder_61_out}), .b({adder_62_cout[5], adder_62_out}), .out(outval1[5:0]),
    .cout(outval1[6]));  // open: cin
  // Probe on bitadder_1_out
  // Probe on outval1

  // Notes on the sheet:
  //   inval1: initial=0xfa04c5873b93dd10
endmodule

module add64 (
  input  [63:0] in_1,
  input  [63:0] in_2,
  input  [63:0] in_3,
  input  [63:0] in_4,
  input  [63:0] in_5,
  input  [63:0] in_6,
  input  [63:0] in_7,
  input  [63:0] inval1,
  input  [63:0] inval2,
  input  carryin1,
  output [63:0] outval1,
  output carryout1
);

  wire adder_1_cout, or_2_out, or_3_out, or_4_out, or_5_out, or_6_out, or_7_out, or_8_out, or_9_out,
       or_10_out, or_11_out, or_12_out, or_13_out, or_14_out, or_15_out, or_16_out, or_17_out, or_18_out,
       or_19_out, or_20_out, or_21_out, or_22_out, or_23_out, or_24_out, or_25_out, or_26_out, or_27_out,
       or_28_out, or_29_out, or_30_out, or_31_out, or_32_out, or_33_out, or_34_out, or_35_out, or_36_out,
       or_37_out, or_38_out, or_39_out, or_40_out, or_41_out, or_42_out, or_43_out, or_44_out, or_45_out,
       or_46_out, or_47_out, or_48_out, or_49_out, or_50_out, or_51_out, or_52_out, or_53_out, or_54_out,
       or_55_out, or_56_out, or_57_out, or_58_out, or_59_out, or_60_out, or_61_out, or_62_out, or_63_out,
       or_64_out;
  wire [7:0] and_63_out, and_63_out_2, and_63_out_3, and_63_out_4, and_63_out_5, and_63_out_6, and_63_out_7,
       and_63_out_8, and_64_out, and_64_out_2, and_64_out_3, and_64_out_4, and_64_out_5, and_64_out_6,
       and_64_out_7, and_64_out_8, and_65_out, and_65_out_2, and_65_out_3, and_65_out_4, and_65_out_5,
       and_65_out_6, and_65_out_7, and_65_out_8;
  wire [63:0] adder_1_out, and_1_out, and_2_out, and_3_out, and_4_out, and_5_out, and_6_out, and_7_out,
       and_8_out, and_9_out, and_10_out, and_11_out, and_12_out, and_13_out, and_14_out, and_15_out,
       and_16_out, and_17_out, and_18_out, and_19_out, and_20_out, and_21_out, and_22_out, and_23_out,
       and_24_out, and_25_out, and_26_out, and_27_out, and_28_out, and_29_out, and_30_out, and_31_out,
       and_32_out, and_33_out, and_34_out, and_35_out, and_36_out, and_37_out, and_38_out, and_39_out,
       and_40_out, and_41_out, and_42_out, and_43_out, and_44_out, and_45_out, and_46_out, and_47_out,
       and_48_out, and_49_out, and_50_out, and_51_out, and_52_out, and_53_out, and_54_out, and_55_out,
       and_56_out, and_57_out, and_58_out, and_59_out, and_60_out, and_61_out, and_62_out, and_66_out,
       bit_extender_1_out, or_1_out, shifter_1_out, shifter_2_out, shifter_3_out, shifter_4_out,
       shifter_5_out, shifter_6_out, shifter_7_out, shifter_8_out, shifter_9_out, shifter_10_out,
       shifter_11_out, shifter_12_out, shifter_13_out, shifter_14_out, shifter_15_out, shifter_16_out,
       shifter_17_out, shifter_18_out, shifter_19_out, shifter_20_out, shifter_21_out, shifter_22_out,
       shifter_23_out, shifter_24_out, shifter_25_out, shifter_26_out, shifter_27_out, shifter_28_out,
       shifter_29_out, shifter_30_out, shifter_31_out, shifter_32_out, shifter_33_out, shifter_34_out,
       shifter_35_out, shifter_36_out, shifter_37_out, shifter_38_out, shifter_39_out, shifter_40_out,
       shifter_41_out, shifter_42_out, shifter_43_out, shifter_44_out, shifter_45_out, shifter_46_out,
       shifter_47_out, shifter_48_out, shifter_49_out, shifter_50_out, shifter_51_out, shifter_52_out,
       shifter_53_out, shifter_54_out, shifter_55_out, shifter_56_out, shifter_57_out, shifter_58_out,
       shifter_59_out, shifter_60_out, shifter_61_out, shifter_62_out, shifter_63_out, shifter_64_out,
       xor_1_out, xor_2_out, xor_3_out, xor_4_out, xor_5_out, xor_6_out, xor_7_out, xor_8_out, xor_9_out,
       xor_10_out, xor_11_out, xor_12_out, xor_13_out, xor_14_out, xor_15_out, xor_16_out, xor_17_out,
       xor_18_out, xor_19_out, xor_20_out, xor_21_out, xor_22_out, xor_23_out, xor_24_out, xor_25_out,
       xor_26_out, xor_27_out, xor_28_out, xor_29_out, xor_30_out, xor_31_out, xor_32_out, xor_33_out,
       xor_34_out, xor_35_out, xor_36_out, xor_37_out, xor_38_out, xor_39_out, xor_40_out, xor_41_out,
       xor_42_out, xor_43_out, xor_44_out, xor_45_out, xor_46_out, xor_47_out, xor_48_out, xor_49_out,
       xor_50_out, xor_51_out, xor_52_out, xor_53_out, xor_54_out, xor_55_out, xor_56_out, xor_57_out,
       xor_58_out, xor_59_out, xor_60_out, xor_61_out, xor_62_out, xor_63_out, xor_64_out, xor_65_out;

  // Probe on inval1
  // Probe on inval2
  assign bit_extender_1_out = {{63{1'b0}}, carryin1};  // Bit_Extender bit_extender_1
  // Probe on inval1
  // Probe on inval2
  assign xor_1_out = inval1 ^ inval2;  // XOR_Gate xor_1, 64 bits wide
  assign and_1_out = xor_1_out & bit_extender_1_out;  // AND_Gate and_1, 64 bits wide
  assign and_2_out = inval1 & inval2;  // AND_Gate and_2, 64 bits wide
  assign xor_2_out = bit_extender_1_out ^ xor_1_out;  // XOR_Gate xor_2, 64 bits wide
  assign or_1_out = and_1_out | and_2_out;  // OR_Gate or_1, 64 bits wide
  Shifter #(.width(64)) shifter_1 (.in(or_1_out), .\dist (6'b000001), .out(shifter_1_out));
  Shifter #(.width(64)) shifter_2 (
    .in({and_63_out_8, and_63_out_7, and_63_out_6, and_63_out_5, and_63_out_4, and_63_out_3, and_63_out_2, and_63_out}),
    .\dist (6'b000001), .out(shifter_2_out));
  Shifter #(.width(64)) shifter_3 (
    .in({and_64_out_8, and_64_out_7, and_64_out_6, and_64_out_5, and_64_out_4, and_64_out_3, and_64_out_2, and_64_out}),
    .\dist (6'b000001), .out(shifter_3_out));
  Shifter #(.width(64)) shifter_4 (
    .in({and_65_out_8, and_65_out_7, and_65_out_6, and_65_out_5, and_65_out_4, and_65_out_3, and_65_out_2, and_65_out}),
    .\dist (6'b000001), .out(shifter_4_out));
  assign xor_3_out = xor_2_out ^ shifter_1_out;  // XOR_Gate xor_3, 64 bits wide
  assign and_3_out = xor_2_out & shifter_1_out;  // AND_Gate and_3, 64 bits wide
  Shifter #(.width(64)) shifter_5 (.in(and_3_out), .\dist (6'b000001), .out(shifter_5_out));
  assign xor_4_out = xor_63_out ^ shifter_2_out;  // XOR_Gate xor_4, 64 bits wide
  assign and_4_out = xor_63_out & shifter_2_out;  // AND_Gate and_4, 64 bits wide
  Shifter #(.width(64)) shifter_6 (.in(and_4_out), .\dist (6'b000001), .out(shifter_6_out));
  assign xor_5_out = xor_64_out ^ shifter_3_out;  // XOR_Gate xor_5, 64 bits wide
  assign and_5_out = xor_64_out & shifter_3_out;  // AND_Gate and_5, 64 bits wide
  Shifter #(.width(64)) shifter_7 (.in(and_5_out), .\dist (6'b000001), .out(shifter_7_out));
  assign xor_6_out = xor_65_out ^ shifter_4_out;  // XOR_Gate xor_6, 64 bits wide
  assign and_6_out = xor_65_out & shifter_4_out;  // AND_Gate and_6, 64 bits wide
  Shifter #(.width(64)) shifter_8 (.in(and_6_out), .\dist (6'b000001), .out(shifter_8_out));
  assign xor_7_out = xor_3_out ^ shifter_5_out;  // XOR_Gate xor_7, 64 bits wide
  assign and_7_out = xor_3_out & shifter_5_out;  // AND_Gate and_7, 64 bits wide
  or or_2 (or_2_out, or_1_out[63], and_3_out[63]);
  assign xor_8_out = xor_4_out ^ shifter_6_out;  // XOR_Gate xor_8, 64 bits wide
  assign and_8_out = xor_4_out & shifter_6_out;  // AND_Gate and_8, 64 bits wide
  or or_3 (or_3_out, or_62_out, and_4_out[63]);
  assign xor_9_out = xor_5_out ^ shifter_7_out;  // XOR_Gate xor_9, 64 bits wide
  assign and_9_out = xor_5_out & shifter_7_out;  // AND_Gate and_9, 64 bits wide
  or or_4 (or_4_out, or_63_out, and_5_out[63]);
  assign xor_10_out = xor_6_out ^ shifter_8_out;  // XOR_Gate xor_10, 64 bits wide
  assign and_10_out = xor_6_out & shifter_8_out;  // AND_Gate and_10, 64 bits wide
  or or_5 (or_5_out, or_64_out, and_6_out[63]);
  Adder #(.width(64)) adder_1 (.a(inval1), .b(inval2), .out(adder_1_out), .cin(carryin1), .cout(adder_1_cout));
  Shifter #(.width(64)) shifter_9 (.in(and_7_out), .\dist (6'b000001), .out(shifter_9_out));
  or or_6 (or_6_out, or_2_out, and_7_out[63]);
  Shifter #(.width(64)) shifter_10 (.in(and_8_out), .\dist (6'b000001), .out(shifter_10_out));
  or or_7 (or_7_out, or_3_out, and_8_out[63]);
  Shifter #(.width(64)) shifter_11 (.in(and_9_out), .\dist (6'b000001), .out(shifter_11_out));
  or or_8 (or_8_out, or_4_out, and_9_out[63]);
  Shifter #(.width(64)) shifter_12 (.in(and_10_out), .\dist (6'b000001), .out(shifter_12_out));
  or or_9 (or_9_out, or_5_out, and_10_out[63]);
  assign xor_11_out = xor_7_out ^ shifter_9_out;  // XOR_Gate xor_11, 64 bits wide
  assign and_11_out = xor_7_out & shifter_9_out;  // AND_Gate and_11, 64 bits wide
  Shifter #(.width(64)) shifter_13 (.in(and_11_out), .\dist (6'b000001), .out(shifter_13_out));
  assign xor_12_out = xor_8_out ^ shifter_10_out;  // XOR_Gate xor_12, 64 bits wide
  assign and_12_out = xor_8_out & shifter_10_out;  // AND_Gate and_12, 64 bits wide
  Shifter #(.width(64)) shifter_14 (.in(and_12_out), .\dist (6'b000001), .out(shifter_14_out));
  assign xor_13_out = xor_9_out ^ shifter_11_out;  // XOR_Gate xor_13, 64 bits wide
  assign and_13_out = xor_9_out & shifter_11_out;  // AND_Gate and_13, 64 bits wide
  Shifter #(.width(64)) shifter_15 (.in(and_13_out), .\dist (6'b000001), .out(shifter_15_out));
  assign xor_14_out = xor_10_out ^ shifter_12_out;  // XOR_Gate xor_14, 64 bits wide
  assign and_14_out = xor_10_out & shifter_12_out;  // AND_Gate and_14, 64 bits wide
  Shifter #(.width(64)) shifter_16 (.in(and_14_out), .\dist (6'b000001), .out(shifter_16_out));
  assign xor_15_out = xor_11_out ^ shifter_13_out;  // XOR_Gate xor_15, 64 bits wide
  assign and_15_out = xor_11_out & shifter_13_out;  // AND_Gate and_15, 64 bits wide
  or or_10 (or_10_out, or_6_out, and_11_out[63]);
  assign xor_16_out = xor_12_out ^ shifter_14_out;  // XOR_Gate xor_16, 64 bits wide
  assign and_16_out = xor_12_out & shifter_14_out;  // AND_Gate and_16, 64 bits wide
  or or_11 (or_11_out, or_7_out, and_12_out[63]);
  assign xor_17_out = xor_13_out ^ shifter_15_out;  // XOR_Gate xor_17, 64 bits wide
  assign and_17_out = xor_13_out & shifter_15_out;  // AND_Gate and_17, 64 bits wide
  or or_12 (or_12_out, or_8_out, and_13_out[63]);
  assign xor_18_out = xor_14_out ^ shifter_16_out;  // XOR_Gate xor_18, 64 bits wide
  assign and_18_out = xor_14_out & shifter_16_out;  // AND_Gate and_18, 64 bits wide
  or or_13 (or_13_out, or_9_out, and_14_out[63]);
  Shifter #(.width(64)) shifter_17 (.in(and_15_out), .\dist (6'b000001), .out(shifter_17_out));
  or or_14 (or_14_out, or_10_out, and_15_out[63]);
  Shifter #(.width(64)) shifter_18 (.in(and_16_out), .\dist (6'b000001), .out(shifter_18_out));
  or or_15 (or_15_out, or_11_out, and_16_out[63]);
  Shifter #(.width(64)) shifter_19 (.in(and_17_out), .\dist (6'b000001), .out(shifter_19_out));
  or or_16 (or_16_out, or_12_out, and_17_out[63]);
  Shifter #(.width(64)) shifter_20 (.in(and_18_out), .\dist (6'b000001), .out(shifter_20_out));
  or or_17 (or_17_out, or_13_out, and_18_out[63]);
  assign xor_19_out = xor_15_out ^ shifter_17_out;  // XOR_Gate xor_19, 64 bits wide
  assign and_19_out = xor_15_out & shifter_17_out;  // AND_Gate and_19, 64 bits wide
  Shifter #(.width(64)) shifter_21 (.in(and_19_out), .\dist (6'b000001), .out(shifter_21_out));
  assign xor_20_out = xor_16_out ^ shifter_18_out;  // XOR_Gate xor_20, 64 bits wide
  assign and_20_out = xor_16_out & shifter_18_out;  // AND_Gate and_20, 64 bits wide
  Shifter #(.width(64)) shifter_22 (.in(and_20_out), .\dist (6'b000001), .out(shifter_22_out));
  assign xor_21_out = xor_17_out ^ shifter_19_out;  // XOR_Gate xor_21, 64 bits wide
  assign and_21_out = xor_17_out & shifter_19_out;  // AND_Gate and_21, 64 bits wide
  Shifter #(.width(64)) shifter_23 (.in(and_21_out), .\dist (6'b000001), .out(shifter_23_out));
  assign xor_22_out = xor_18_out ^ shifter_20_out;  // XOR_Gate xor_22, 64 bits wide
  assign and_22_out = xor_18_out & shifter_20_out;  // AND_Gate and_22, 64 bits wide
  Shifter #(.width(64)) shifter_24 (.in(and_22_out), .\dist (6'b000001), .out(shifter_24_out));
  assign xor_23_out = xor_19_out ^ shifter_21_out;  // XOR_Gate xor_23, 64 bits wide
  assign and_23_out = xor_19_out & shifter_21_out;  // AND_Gate and_23, 64 bits wide
  or or_18 (or_18_out, or_14_out, and_19_out[63]);
  assign xor_24_out = xor_20_out ^ shifter_22_out;  // XOR_Gate xor_24, 64 bits wide
  assign and_24_out = xor_20_out & shifter_22_out;  // AND_Gate and_24, 64 bits wide
  or or_19 (or_19_out, or_15_out, and_20_out[63]);
  assign xor_25_out = xor_21_out ^ shifter_23_out;  // XOR_Gate xor_25, 64 bits wide
  assign and_25_out = xor_21_out & shifter_23_out;  // AND_Gate and_25, 64 bits wide
  or or_20 (or_20_out, or_16_out, and_21_out[63]);
  assign xor_26_out = xor_22_out ^ shifter_24_out;  // XOR_Gate xor_26, 64 bits wide
  assign and_26_out = xor_22_out & shifter_24_out;  // AND_Gate and_26, 64 bits wide
  or or_21 (or_21_out, or_17_out, and_22_out[63]);
  Shifter #(.width(64)) shifter_25 (.in(and_23_out), .\dist (6'b000001), .out(shifter_25_out));
  or or_22 (or_22_out, or_18_out, and_23_out[63]);
  Shifter #(.width(64)) shifter_26 (.in(and_24_out), .\dist (6'b000001), .out(shifter_26_out));
  or or_23 (or_23_out, or_19_out, and_24_out[63]);
  Shifter #(.width(64)) shifter_27 (.in(and_25_out), .\dist (6'b000001), .out(shifter_27_out));
  or or_24 (or_24_out, or_20_out, and_25_out[63]);
  Shifter #(.width(64)) shifter_28 (.in(and_26_out), .\dist (6'b000001), .out(shifter_28_out));
  or or_25 (or_25_out, or_21_out, and_26_out[63]);
  assign xor_27_out = xor_23_out ^ shifter_25_out;  // XOR_Gate xor_27, 64 bits wide
  assign and_27_out = xor_23_out & shifter_25_out;  // AND_Gate and_27, 64 bits wide
  Shifter #(.width(64)) shifter_29 (.in(and_27_out), .\dist (6'b000001), .out(shifter_29_out));
  assign xor_28_out = xor_24_out ^ shifter_26_out;  // XOR_Gate xor_28, 64 bits wide
  assign and_28_out = xor_24_out & shifter_26_out;  // AND_Gate and_28, 64 bits wide
  Shifter #(.width(64)) shifter_30 (.in(and_28_out), .\dist (6'b000001), .out(shifter_30_out));
  assign xor_29_out = xor_25_out ^ shifter_27_out;  // XOR_Gate xor_29, 64 bits wide
  assign and_29_out = xor_25_out & shifter_27_out;  // AND_Gate and_29, 64 bits wide
  Shifter #(.width(64)) shifter_31 (.in(and_29_out), .\dist (6'b000001), .out(shifter_31_out));
  assign xor_30_out = xor_26_out ^ shifter_28_out;  // XOR_Gate xor_30, 64 bits wide
  assign and_30_out = xor_26_out & shifter_28_out;  // AND_Gate and_30, 64 bits wide
  Shifter #(.width(64)) shifter_32 (.in(and_30_out), .\dist (6'b000001), .out(shifter_32_out));
  assign xor_31_out = xor_27_out ^ shifter_29_out;  // XOR_Gate xor_31, 64 bits wide
  assign and_31_out = xor_27_out & shifter_29_out;  // AND_Gate and_31, 64 bits wide
  or or_26 (or_26_out, or_22_out, and_27_out[63]);
  assign xor_32_out = xor_28_out ^ shifter_30_out;  // XOR_Gate xor_32, 64 bits wide
  assign and_32_out = xor_28_out & shifter_30_out;  // AND_Gate and_32, 64 bits wide
  or or_27 (or_27_out, or_23_out, and_28_out[63]);
  assign xor_33_out = xor_29_out ^ shifter_31_out;  // XOR_Gate xor_33, 64 bits wide
  assign and_33_out = xor_29_out & shifter_31_out;  // AND_Gate and_33, 64 bits wide
  or or_28 (or_28_out, or_24_out, and_29_out[63]);
  assign xor_34_out = xor_30_out ^ shifter_32_out;  // XOR_Gate xor_34, 64 bits wide
  assign and_34_out = xor_30_out & shifter_32_out;  // AND_Gate and_34, 64 bits wide
  or or_29 (or_29_out, or_25_out, and_30_out[63]);
  Shifter #(.width(64)) shifter_33 (.in(and_31_out), .\dist (6'b000001), .out(shifter_33_out));
  or or_30 (or_30_out, or_26_out, and_31_out[63]);
  Shifter #(.width(64)) shifter_34 (.in(and_32_out), .\dist (6'b000001), .out(shifter_34_out));
  or or_31 (or_31_out, or_27_out, and_32_out[63]);
  Shifter #(.width(64)) shifter_35 (.in(and_33_out), .\dist (6'b000001), .out(shifter_35_out));
  or or_32 (or_32_out, or_28_out, and_33_out[63]);
  Shifter #(.width(64)) shifter_36 (.in(and_34_out), .\dist (6'b000001), .out(shifter_36_out));
  or or_33 (or_33_out, or_29_out, and_34_out[63]);
  assign xor_35_out = xor_31_out ^ shifter_33_out;  // XOR_Gate xor_35, 64 bits wide
  assign and_35_out = xor_31_out & shifter_33_out;  // AND_Gate and_35, 64 bits wide
  Shifter #(.width(64)) shifter_37 (.in(and_35_out), .\dist (6'b000001), .out(shifter_37_out));
  assign xor_36_out = xor_32_out ^ shifter_34_out;  // XOR_Gate xor_36, 64 bits wide
  assign and_36_out = xor_32_out & shifter_34_out;  // AND_Gate and_36, 64 bits wide
  Shifter #(.width(64)) shifter_38 (.in(and_36_out), .\dist (6'b000001), .out(shifter_38_out));
  assign xor_37_out = xor_33_out ^ shifter_35_out;  // XOR_Gate xor_37, 64 bits wide
  assign and_37_out = xor_33_out & shifter_35_out;  // AND_Gate and_37, 64 bits wide
  Shifter #(.width(64)) shifter_39 (.in(and_37_out), .\dist (6'b000001), .out(shifter_39_out));
  assign xor_38_out = xor_34_out ^ shifter_36_out;  // XOR_Gate xor_38, 64 bits wide
  assign and_38_out = xor_34_out & shifter_36_out;  // AND_Gate and_38, 64 bits wide
  Shifter #(.width(64)) shifter_40 (.in(and_38_out), .\dist (6'b000001), .out(shifter_40_out));
  assign xor_39_out = xor_35_out ^ shifter_37_out;  // XOR_Gate xor_39, 64 bits wide
  assign and_39_out = xor_35_out & shifter_37_out;  // AND_Gate and_39, 64 bits wide
  or or_34 (or_34_out, or_30_out, and_35_out[63]);
  assign xor_40_out = xor_36_out ^ shifter_38_out;  // XOR_Gate xor_40, 64 bits wide
  assign and_40_out = xor_36_out & shifter_38_out;  // AND_Gate and_40, 64 bits wide
  or or_35 (or_35_out, or_31_out, and_36_out[63]);
  assign xor_41_out = xor_37_out ^ shifter_39_out;  // XOR_Gate xor_41, 64 bits wide
  assign and_41_out = xor_37_out & shifter_39_out;  // AND_Gate and_41, 64 bits wide
  or or_36 (or_36_out, or_32_out, and_37_out[63]);
  assign xor_42_out = xor_38_out ^ shifter_40_out;  // XOR_Gate xor_42, 64 bits wide
  assign and_42_out = xor_38_out & shifter_40_out;  // AND_Gate and_42, 64 bits wide
  or or_37 (or_37_out, or_33_out, and_38_out[63]);
  Shifter #(.width(64)) shifter_41 (.in(and_39_out), .\dist (6'b000001), .out(shifter_41_out));
  or or_38 (or_38_out, or_34_out, and_39_out[63]);
  Shifter #(.width(64)) shifter_42 (.in(and_40_out), .\dist (6'b000001), .out(shifter_42_out));
  or or_39 (or_39_out, or_35_out, and_40_out[63]);
  Shifter #(.width(64)) shifter_43 (.in(and_41_out), .\dist (6'b000001), .out(shifter_43_out));
  or or_40 (or_40_out, or_36_out, and_41_out[63]);
  Shifter #(.width(64)) shifter_44 (.in(and_42_out), .\dist (6'b000001), .out(shifter_44_out));
  or or_41 (or_41_out, or_37_out, and_42_out[63]);
  assign xor_43_out = xor_39_out ^ shifter_41_out;  // XOR_Gate xor_43, 64 bits wide
  assign and_43_out = xor_39_out & shifter_41_out;  // AND_Gate and_43, 64 bits wide
  Shifter #(.width(64)) shifter_45 (.in(and_43_out), .\dist (6'b000001), .out(shifter_45_out));
  assign xor_44_out = xor_40_out ^ shifter_42_out;  // XOR_Gate xor_44, 64 bits wide
  assign and_44_out = xor_40_out & shifter_42_out;  // AND_Gate and_44, 64 bits wide
  Shifter #(.width(64)) shifter_46 (.in(and_44_out), .\dist (6'b000001), .out(shifter_46_out));
  assign xor_45_out = xor_41_out ^ shifter_43_out;  // XOR_Gate xor_45, 64 bits wide
  assign and_45_out = xor_41_out & shifter_43_out;  // AND_Gate and_45, 64 bits wide
  Shifter #(.width(64)) shifter_47 (.in(and_45_out), .\dist (6'b000001), .out(shifter_47_out));
  assign xor_46_out = xor_42_out ^ shifter_44_out;  // XOR_Gate xor_46, 64 bits wide
  assign and_46_out = xor_42_out & shifter_44_out;  // AND_Gate and_46, 64 bits wide
  Shifter #(.width(64)) shifter_48 (.in(and_46_out), .\dist (6'b000001), .out(shifter_48_out));
  assign xor_47_out = xor_43_out ^ shifter_45_out;  // XOR_Gate xor_47, 64 bits wide
  assign and_47_out = xor_43_out & shifter_45_out;  // AND_Gate and_47, 64 bits wide
  or or_42 (or_42_out, or_38_out, and_43_out[63]);
  assign xor_48_out = xor_44_out ^ shifter_46_out;  // XOR_Gate xor_48, 64 bits wide
  assign and_48_out = xor_44_out & shifter_46_out;  // AND_Gate and_48, 64 bits wide
  or or_43 (or_43_out, or_39_out, and_44_out[63]);
  assign xor_49_out = xor_45_out ^ shifter_47_out;  // XOR_Gate xor_49, 64 bits wide
  assign and_49_out = xor_45_out & shifter_47_out;  // AND_Gate and_49, 64 bits wide
  or or_44 (or_44_out, or_40_out, and_45_out[63]);
  assign xor_50_out = xor_46_out ^ shifter_48_out;  // XOR_Gate xor_50, 64 bits wide
  assign and_50_out = xor_46_out & shifter_48_out;  // AND_Gate and_50, 64 bits wide
  or or_45 (or_45_out, or_41_out, and_46_out[63]);
  Shifter #(.width(64)) shifter_49 (.in(and_47_out), .\dist (6'b000001), .out(shifter_49_out));
  or or_46 (or_46_out, or_42_out, and_47_out[63]);
  Shifter #(.width(64)) shifter_50 (.in(and_48_out), .\dist (6'b000001), .out(shifter_50_out));
  or or_47 (or_47_out, or_43_out, and_48_out[63]);
  Shifter #(.width(64)) shifter_51 (.in(and_49_out), .\dist (6'b000001), .out(shifter_51_out));
  or or_48 (or_48_out, or_44_out, and_49_out[63]);
  Shifter #(.width(64)) shifter_52 (.in(and_50_out), .\dist (6'b000001), .out(shifter_52_out));
  or or_49 (or_49_out, or_45_out, and_50_out[63]);
  assign xor_51_out = xor_47_out ^ shifter_49_out;  // XOR_Gate xor_51, 64 bits wide
  assign and_51_out = xor_47_out & shifter_49_out;  // AND_Gate and_51, 64 bits wide
  Shifter #(.width(64)) shifter_53 (.in(and_51_out), .\dist (6'b000001), .out(shifter_53_out));
  assign xor_52_out = xor_48_out ^ shifter_50_out;  // XOR_Gate xor_52, 64 bits wide
  assign and_52_out = xor_48_out & shifter_50_out;  // AND_Gate and_52, 64 bits wide
  Shifter #(.width(64)) shifter_54 (.in(and_52_out), .\dist (6'b000001), .out(shifter_54_out));
  assign xor_53_out = xor_49_out ^ shifter_51_out;  // XOR_Gate xor_53, 64 bits wide
  assign and_53_out = xor_49_out & shifter_51_out;  // AND_Gate and_53, 64 bits wide
  Shifter #(.width(64)) shifter_55 (.in(and_53_out), .\dist (6'b000001), .out(shifter_55_out));
  assign xor_54_out = xor_50_out ^ shifter_52_out;  // XOR_Gate xor_54, 64 bits wide
  assign and_54_out = xor_50_out & shifter_52_out;  // AND_Gate and_54, 64 bits wide
  Shifter #(.width(64)) shifter_56 (.in(and_54_out), .\dist (6'b000001), .out(shifter_56_out));
  assign xor_55_out = xor_51_out ^ shifter_53_out;  // XOR_Gate xor_55, 64 bits wide
  assign and_55_out = xor_51_out & shifter_53_out;  // AND_Gate and_55, 64 bits wide
  or or_50 (or_50_out, or_46_out, and_51_out[63]);
  assign xor_56_out = xor_52_out ^ shifter_54_out;  // XOR_Gate xor_56, 64 bits wide
  assign and_56_out = xor_52_out & shifter_54_out;  // AND_Gate and_56, 64 bits wide
  or or_51 (or_51_out, or_47_out, and_52_out[63]);
  assign xor_57_out = xor_53_out ^ shifter_55_out;  // XOR_Gate xor_57, 64 bits wide
  assign and_57_out = xor_53_out & shifter_55_out;  // AND_Gate and_57, 64 bits wide
  or or_52 (or_52_out, or_48_out, and_53_out[63]);
  assign xor_58_out = xor_54_out ^ shifter_56_out;  // XOR_Gate xor_58, 64 bits wide
  assign and_58_out = xor_54_out & shifter_56_out;  // AND_Gate and_58, 64 bits wide
  or or_53 (or_53_out, or_49_out, and_54_out[63]);
  Shifter #(.width(64)) shifter_57 (.in(and_55_out), .\dist (6'b000001), .out(shifter_57_out));
  or or_54 (or_54_out, or_50_out, and_55_out[63]);
  Shifter #(.width(64)) shifter_58 (.in(and_56_out), .\dist (6'b000001), .out(shifter_58_out));
  or or_55 (or_55_out, or_51_out, and_56_out[63]);
  Shifter #(.width(64)) shifter_59 (.in(and_57_out), .\dist (6'b000001), .out(shifter_59_out));
  or or_56 (or_56_out, or_52_out, and_57_out[63]);
  Shifter #(.width(64)) shifter_60 (.in(and_58_out), .\dist (6'b000001), .out(shifter_60_out));
  or or_57 (or_57_out, or_53_out, and_58_out[63]);
  assign xor_59_out = xor_55_out ^ shifter_57_out;  // XOR_Gate xor_59, 64 bits wide
  assign and_59_out = xor_55_out & shifter_57_out;  // AND_Gate and_59, 64 bits wide
  Shifter #(.width(64)) shifter_61 (.in(and_59_out), .\dist (6'b000001), .out(shifter_61_out));
  assign xor_60_out = xor_56_out ^ shifter_58_out;  // XOR_Gate xor_60, 64 bits wide
  assign and_60_out = xor_56_out & shifter_58_out;  // AND_Gate and_60, 64 bits wide
  Shifter #(.width(64)) shifter_62 (.in(and_60_out), .\dist (6'b000001), .out(shifter_62_out));
  assign xor_61_out = xor_57_out ^ shifter_59_out;  // XOR_Gate xor_61, 64 bits wide
  assign and_61_out = xor_57_out & shifter_59_out;  // AND_Gate and_61, 64 bits wide
  Shifter #(.width(64)) shifter_63 (.in(and_61_out), .\dist (6'b000001), .out(shifter_63_out));
  assign xor_62_out = xor_58_out ^ shifter_60_out;  // XOR_Gate xor_62, 64 bits wide
  assign and_62_out = xor_58_out & shifter_60_out;  // AND_Gate and_62, 64 bits wide
  Shifter #(.width(64)) shifter_64 (.in(and_62_out), .\dist (6'b000001), .out(shifter_64_out));
  assign xor_63_out = xor_59_out ^ shifter_61_out;  // XOR_Gate xor_63, 64 bits wide
  assign {and_63_out_8, and_63_out_7, and_63_out_6, and_63_out_5, and_63_out_4, and_63_out_3, and_63_out_2, and_63_out} = xor_59_out & shifter_61_out;  // AND_Gate and_63, 64 bits wide
  or or_58 (or_58_out, or_54_out, and_59_out[63]);
  assign xor_64_out = xor_60_out ^ shifter_62_out;  // XOR_Gate xor_64, 64 bits wide
  assign {and_64_out_8, and_64_out_7, and_64_out_6, and_64_out_5, and_64_out_4, and_64_out_3, and_64_out_2, and_64_out} = xor_60_out & shifter_62_out;  // AND_Gate and_64, 64 bits wide
  or or_59 (or_59_out, or_55_out, and_60_out[63]);
  assign xor_65_out = xor_61_out ^ shifter_63_out;  // XOR_Gate xor_65, 64 bits wide
  assign {and_65_out_8, and_65_out_7, and_65_out_6, and_65_out_5, and_65_out_4, and_65_out_3, and_65_out_2, and_65_out} = xor_61_out & shifter_63_out;  // AND_Gate and_65, 64 bits wide
  or or_60 (or_60_out, or_56_out, and_61_out[63]);
  assign outval1 = xor_62_out ^ shifter_64_out;  // XOR_Gate xor_66, 64 bits wide
  assign and_66_out = xor_62_out & shifter_64_out;  // AND_Gate and_66, 64 bits wide
  or or_61 (or_61_out, or_57_out, and_62_out[63]);
  or or_62 (or_62_out, or_58_out, and_63_out_8[7]);
  or or_63 (or_63_out, or_59_out, and_64_out_8[7]);
  or or_64 (or_64_out, or_60_out, and_65_out_8[7]);
  or or_65 (carryout1, or_61_out, and_66_out[63]);
  // Probe on adder_1_out
  // Probe on adder_1_out
  // Probe on adder_1_cout
  // Probe on outval1
  // Probe on adder_1_out
  // Probe on outval1

  // Notes on the sheet:
  //   carryin1: initial=0x1
  //   inval1: initial=0x7fffffffffffffff
  //   inval2: initial=0x8000000000000001
  //   in_2: initial=0x61d93f7ced9168
  //   in_3: initial=0x80f0c02108e74001
  //   in_4: initial=0x8000000000000001
  //   in_5: initial=0x7ffffffffffffffe
  //   in_6: initial=0x4040152bd3c36113
  //   in_7: initial=0x4061d93f7ced9168
  //   in_1: initial=0x40152bd3c36113
endmodule

module penc64 (
  input  [63:0] in_1,
  input  [63:0] in_2,
  input  [63:0] in_3,
  input  [63:0] in_4,
  input  [63:0] inval1,
  input  enablein1,
  output [5:0] priorityindex1,
  output groupselect1,
  output enableout1
);

  wire and_1_out, and_2_out, and_3_out, and_4_out, and_5_out, and_6_out, and_7_out, and_8_out, and_9_out,
       and_10_out, and_11_out, and_12_out, and_13_out, and_14_out, and_15_out, and_16_out, and_17_out,
       and_18_out, and_19_out, and_20_out, and_21_out, and_22_out, and_23_out, and_24_out, and_25_out,
       and_26_out, and_27_out, and_28_out, and_29_out, and_30_out, and_31_out, and_32_out, and_33_out,
       and_34_out, and_35_out, and_36_out, and_37_out, and_38_out, and_39_out, and_40_out, and_41_out,
       and_42_out, and_43_out, and_44_out, and_45_out, and_46_out, and_47_out, and_48_out, and_49_out,
       and_50_out, and_51_out, and_52_out, and_53_out, and_54_out, and_55_out, and_56_out, and_57_out,
       and_58_out, and_59_out, and_60_out, and_61_out, and_62_out, and_63_out, not_1_out, or_1_out, or_2_out,
       or_3_out, or_4_out, or_5_out, or_6_out, or_7_out, or_8_out, or_9_out, or_10_out, or_11_out, or_12_out,
       or_13_out, or_14_out, or_15_out, or_16_out, or_17_out, or_18_out, or_19_out, or_20_out, or_21_out,
       or_22_out, or_23_out, or_24_out, or_25_out, or_26_out, or_27_out, or_28_out, or_29_out, or_30_out,
       or_31_out, or_32_out, or_33_out, or_34_out, or_35_out, or_36_out, or_37_out, or_38_out, or_39_out,
       or_40_out, or_41_out, or_42_out, or_43_out, or_44_out, or_45_out, or_46_out, or_47_out, or_48_out,
       or_49_out, or_50_out, or_51_out, or_52_out, or_53_out, or_54_out, or_55_out, or_56_out, or_57_out,
       or_58_out, or_59_out, or_60_out, or_61_out, or_62_out, or_63_out, priority_encoder_1_en_out,
       priority_encoder_1_gs;
  wire [5:0] multiplexer_1_out, multiplexer_2_out, multiplexer_3_out, multiplexer_4_out, multiplexer_5_out,
       multiplexer_6_out, multiplexer_7_out, multiplexer_8_out, multiplexer_9_out, multiplexer_10_out,
       multiplexer_11_out, multiplexer_12_out, multiplexer_13_out, multiplexer_14_out, multiplexer_15_out,
       multiplexer_16_out, multiplexer_17_out, multiplexer_18_out, multiplexer_19_out, multiplexer_20_out,
       multiplexer_21_out, multiplexer_22_out, multiplexer_23_out, multiplexer_24_out, multiplexer_25_out,
       multiplexer_26_out, multiplexer_27_out, multiplexer_28_out, multiplexer_29_out, multiplexer_30_out,
       multiplexer_31_out, multiplexer_32_out, multiplexer_33_out, multiplexer_34_out, multiplexer_35_out,
       multiplexer_36_out, multiplexer_37_out, multiplexer_38_out, multiplexer_39_out, multiplexer_40_out,
       multiplexer_41_out, multiplexer_42_out, multiplexer_43_out, multiplexer_44_out, multiplexer_45_out,
       multiplexer_46_out, multiplexer_47_out, multiplexer_48_out, multiplexer_49_out, multiplexer_50_out,
       multiplexer_51_out, multiplexer_52_out, multiplexer_53_out, multiplexer_54_out, multiplexer_55_out,
       multiplexer_56_out, multiplexer_57_out, multiplexer_58_out, multiplexer_59_out, multiplexer_60_out,
       multiplexer_61_out, multiplexer_62_out, multiplexer_63_out, multiplexer_64_out, or_64_out,
       priority_encoder_1_out;

  // Probe on inval1
  Priority_Encoder #(.select(6)) priority_encoder_1 (
    .in0(inval1[0]), .in1(inval1[1]), .in2(inval1[2]), .in3(inval1[3]), .in4(inval1[4]), .in5(inval1[5]),
    .in6(inval1[6]), .in7(inval1[7]), .in8(inval1[8]), .in9(inval1[9]), .in10(inval1[10]), .in11(inval1[11]),
    .in12(inval1[12]), .in13(inval1[13]), .in14(inval1[14]), .in15(inval1[15]), .in16(inval1[16]),
    .in17(inval1[17]), .in18(inval1[18]), .in19(inval1[19]), .in20(inval1[20]), .in21(inval1[21]),
    .in22(inval1[22]), .in23(inval1[23]), .in24(inval1[24]), .in25(inval1[25]), .in26(inval1[26]),
    .in27(inval1[27]), .in28(inval1[28]), .in29(inval1[29]), .in30(inval1[30]), .in31(inval1[31]),
    .in32(inval1[32]), .in33(inval1[33]), .in34(inval1[34]), .in35(inval1[35]), .in36(inval1[36]),
    .in37(inval1[37]), .in38(inval1[38]), .in39(inval1[39]), .in40(inval1[40]), .in41(inval1[41]),
    .in42(inval1[42]), .in43(inval1[43]), .in44(inval1[44]), .in45(inval1[45]), .in46(inval1[46]),
    .in47(inval1[47]), .in48(inval1[48]), .in49(inval1[49]), .in50(inval1[50]), .in51(inval1[51]),
    .in52(inval1[52]), .in53(inval1[53]), .in54(inval1[54]), .in55(inval1[55]), .in56(inval1[56]),
    .in57(inval1[57]), .in58(inval1[58]), .in59(inval1[59]), .in60(inval1[60]), .in61(inval1[61]),
    .in62(inval1[62]), .in63(inval1[63]), .out(priority_encoder_1_out), .gs(priority_encoder_1_gs),
    .en_out(priority_encoder_1_en_out), .en_in(enablein1));
  and and_1 (and_1_out, ~inval1[63], inval1[62]);  // AND_Gate
  or or_1 (or_1_out, inval1[63], and_1_out);
  Multiplexer #(.width(6)) multiplexer_1 (.in0({6{1'b0}}), .in1({6{1'b1}}), .out(multiplexer_1_out), .sel(inval1[63]));
  and and_2 (and_2_out, ~or_1_out, inval1[61]);  // AND_Gate
  or or_2 (or_2_out, or_1_out, and_2_out);
  or or_3 (or_3_out, or_2_out, and_3_out);
  Multiplexer #(.width(6)) multiplexer_2 (.in0({6{1'b0}}), .in1(6'b111101), .out(multiplexer_2_out), .sel(and_2_out));
  Multiplexer #(.width(6)) multiplexer_3 (.in0({6{1'b0}}), .in1(6'b111110), .out(multiplexer_3_out), .sel(and_1_out));
  and and_3 (and_3_out, ~or_2_out, inval1[60]);  // AND_Gate
  and and_4 (and_4_out, ~or_3_out, inval1[59]);  // AND_Gate
  or or_4 (or_4_out, or_3_out, and_4_out);
  Multiplexer #(.width(6)) multiplexer_4 (.in0({6{1'b0}}), .in1(6'b111011), .out(multiplexer_4_out), .sel(and_4_out));
  Multiplexer #(.width(6)) multiplexer_5 (.in0({6{1'b0}}), .in1(6'b111100), .out(multiplexer_5_out), .sel(and_3_out));
  and and_5 (and_5_out, ~or_4_out, inval1[58]);  // AND_Gate
  and and_6 (and_6_out, ~or_5_out, inval1[57]);  // AND_Gate
  or or_5 (or_5_out, or_4_out, and_5_out);
  or or_6 (or_6_out, or_5_out, and_6_out);
  Multiplexer #(.width(6)) multiplexer_6 (.in0({6{1'b0}}), .in1(6'b111010), .out(multiplexer_6_out), .sel(and_5_out));
  and and_7 (and_7_out, ~or_6_out, inval1[56]);  // AND_Gate
  or or_7 (or_7_out, or_6_out, and_7_out);
  or or_8 (or_8_out, or_7_out, and_8_out);
  Multiplexer #(.width(6)) multiplexer_7 (.in0({6{1'b0}}), .in1(6'b111000), .out(multiplexer_7_out), .sel(and_7_out));
  Multiplexer #(.width(6)) multiplexer_8 (.in0({6{1'b0}}), .in1(6'b111001), .out(multiplexer_8_out), .sel(and_6_out));
  and and_8 (and_8_out, ~or_7_out, inval1[55]);  // AND_Gate
  and and_9 (and_9_out, ~or_8_out, inval1[54]);  // AND_Gate
  or or_9 (or_9_out, or_8_out, and_9_out);
  Multiplexer #(.width(6)) multiplexer_9 (.in0({6{1'b0}}), .in1(6'b110111), .out(multiplexer_9_out), .sel(and_8_out));
  and and_10 (and_10_out, ~or_9_out, inval1[53]);  // AND_Gate
  or or_10 (or_10_out, or_11_out, and_11_out);
  or or_11 (or_11_out, or_9_out, and_10_out);
  Multiplexer #(.width(6)) multiplexer_10 (
    .in0({6{1'b0}}), .in1(6'b110101), .out(multiplexer_10_out), .sel(and_10_out));
  Multiplexer #(.width(6)) multiplexer_11 (.in0({6{1'b0}}), .in1(6'b110110), .out(multiplexer_11_out), .sel(and_9_out));
  and and_11 (and_11_out, ~or_11_out, inval1[52]);  // AND_Gate
  and and_12 (and_12_out, ~or_10_out, inval1[51]);  // AND_Gate
  or or_12 (or_12_out, or_10_out, and_12_out);
  Multiplexer #(.width(6)) multiplexer_12 (
    .in0({6{1'b0}}), .in1(6'b110011), .out(multiplexer_12_out), .sel(and_12_out));
  Multiplexer #(.width(6)) multiplexer_13 (
    .in0({6{1'b0}}), .in1(6'b110100), .out(multiplexer_13_out), .sel(and_11_out));
  and and_13 (and_13_out, ~or_12_out, inval1[50]);  // AND_Gate
  and and_14 (and_14_out, ~or_13_out, inval1[49]);  // AND_Gate
  or or_13 (or_13_out, or_12_out, and_13_out);
  or or_14 (or_14_out, or_13_out, and_14_out);
  Multiplexer #(.width(6)) multiplexer_14 (
    .in0({6{1'b0}}), .in1(6'b110010), .out(multiplexer_14_out), .sel(and_13_out));
  and and_15 (and_15_out, ~or_14_out, inval1[48]);  // AND_Gate
  or or_15 (or_15_out, or_14_out, and_15_out);
  or or_16 (or_16_out, or_15_out, and_16_out);
  Multiplexer #(.width(6)) multiplexer_15 (
    .in0({6{1'b0}}), .in1(6'b110000), .out(multiplexer_15_out), .sel(and_15_out));
  Multiplexer #(.width(6)) multiplexer_16 (
    .in0({6{1'b0}}), .in1(6'b110001), .out(multiplexer_16_out), .sel(and_14_out));
  and and_16 (and_16_out, ~or_15_out, inval1[47]);  // AND_Gate
  and and_17 (and_17_out, ~or_16_out, inval1[46]);  // AND_Gate
  or or_17 (or_17_out, or_16_out, and_17_out);
  Multiplexer #(.width(6)) multiplexer_17 (
    .in0({6{1'b0}}), .in1(6'b101111), .out(multiplexer_17_out), .sel(and_16_out));
  and and_18 (and_18_out, ~or_17_out, inval1[45]);  // AND_Gate
  or or_18 (or_18_out, or_17_out, and_18_out);
  or or_19 (or_19_out, or_18_out, and_19_out);
  Multiplexer #(.width(6)) multiplexer_18 (
    .in0({6{1'b0}}), .in1(6'b101101), .out(multiplexer_18_out), .sel(and_18_out));
  Multiplexer #(.width(6)) multiplexer_19 (
    .in0({6{1'b0}}), .in1(6'b101110), .out(multiplexer_19_out), .sel(and_17_out));
  and and_19 (and_19_out, ~or_18_out, inval1[44]);  // AND_Gate
  and and_20 (and_20_out, ~or_19_out, inval1[43]);  // AND_Gate
  or or_20 (or_20_out, or_19_out, and_20_out);
  Multiplexer #(.width(6)) multiplexer_20 (
    .in0({6{1'b0}}), .in1(6'b101011), .out(multiplexer_20_out), .sel(and_20_out));
  Multiplexer #(.width(6)) multiplexer_21 (
    .in0({6{1'b0}}), .in1(6'b101100), .out(multiplexer_21_out), .sel(and_19_out));
  and and_21 (and_21_out, ~or_20_out, inval1[42]);  // AND_Gate
  and and_22 (and_22_out, ~or_21_out, inval1[41]);  // AND_Gate
  or or_21 (or_21_out, or_20_out, and_21_out);
  or or_22 (or_22_out, or_21_out, and_22_out);
  Multiplexer #(.width(6)) multiplexer_22 (
    .in0({6{1'b0}}), .in1(6'b101010), .out(multiplexer_22_out), .sel(and_21_out));
  and and_23 (and_23_out, ~or_22_out, inval1[40]);  // AND_Gate
  or or_23 (or_23_out, or_22_out, and_23_out);
  or or_24 (or_24_out, or_23_out, and_24_out);
  Multiplexer #(.width(6)) multiplexer_23 (
    .in0({6{1'b0}}), .in1(6'b101000), .out(multiplexer_23_out), .sel(and_23_out));
  Multiplexer #(.width(6)) multiplexer_24 (
    .in0({6{1'b0}}), .in1(6'b101001), .out(multiplexer_24_out), .sel(and_22_out));
  and and_24 (and_24_out, ~or_23_out, inval1[39]);  // AND_Gate
  and and_25 (and_25_out, ~or_24_out, inval1[38]);  // AND_Gate
  or or_25 (or_25_out, or_24_out, and_25_out);
  Multiplexer #(.width(6)) multiplexer_25 (
    .in0({6{1'b0}}), .in1(6'b100111), .out(multiplexer_25_out), .sel(and_24_out));
  and and_26 (and_26_out, ~or_25_out, inval1[37]);  // AND_Gate
  or or_26 (or_26_out, or_25_out, and_26_out);
  or or_27 (or_27_out, or_26_out, and_27_out);
  Multiplexer #(.width(6)) multiplexer_26 (
    .in0({6{1'b0}}), .in1(6'b100101), .out(multiplexer_26_out), .sel(and_26_out));
  Multiplexer #(.width(6)) multiplexer_27 (
    .in0({6{1'b0}}), .in1(6'b100110), .out(multiplexer_27_out), .sel(and_25_out));
  and and_27 (and_27_out, ~or_26_out, inval1[36]);  // AND_Gate
  and and_28 (and_28_out, ~or_27_out, inval1[35]);  // AND_Gate
  or or_28 (or_28_out, or_27_out, and_28_out);
  Multiplexer #(.width(6)) multiplexer_28 (
    .in0({6{1'b0}}), .in1(6'b100011), .out(multiplexer_28_out), .sel(and_28_out));
  Multiplexer #(.width(6)) multiplexer_29 (
    .in0({6{1'b0}}), .in1(6'b100100), .out(multiplexer_29_out), .sel(and_27_out));
  and and_29 (and_29_out, ~or_28_out, inval1[34]);  // AND_Gate
  and and_30 (and_30_out, ~or_29_out, inval1[33]);  // AND_Gate
  or or_29 (or_29_out, or_28_out, and_29_out);
  or or_30 (or_30_out, or_29_out, and_30_out);
  Multiplexer #(.width(6)) multiplexer_30 (
    .in0({6{1'b0}}), .in1(6'b100010), .out(multiplexer_30_out), .sel(and_29_out));
  and and_31 (and_31_out, ~or_30_out, inval1[32]);  // AND_Gate
  or or_31 (or_31_out, or_30_out, and_31_out);
  or or_32 (or_32_out, or_31_out, and_32_out);
  Multiplexer #(.width(6)) multiplexer_31 (
    .in0({6{1'b0}}), .in1(6'b100000), .out(multiplexer_31_out), .sel(and_31_out));
  Multiplexer #(.width(6)) multiplexer_32 (
    .in0({6{1'b0}}), .in1(6'b100001), .out(multiplexer_32_out), .sel(and_30_out));
  and and_32 (and_32_out, ~or_31_out, inval1[31]);  // AND_Gate
  and and_33 (and_33_out, ~or_32_out, inval1[30]);  // AND_Gate
  or or_33 (or_33_out, or_32_out, and_33_out);
  Multiplexer #(.width(6)) multiplexer_33 (
    .in0({6{1'b0}}), .in1(6'b011111), .out(multiplexer_33_out), .sel(and_32_out));
  and and_34 (and_34_out, ~or_33_out, inval1[29]);  // AND_Gate
  or or_34 (or_34_out, or_33_out, and_34_out);
  or or_35 (or_35_out, or_34_out, and_35_out);
  Multiplexer #(.width(6)) multiplexer_34 (
    .in0({6{1'b0}}), .in1(6'b011101), .out(multiplexer_34_out), .sel(and_34_out));
  Multiplexer #(.width(6)) multiplexer_35 (
    .in0({6{1'b0}}), .in1(6'b011110), .out(multiplexer_35_out), .sel(and_33_out));
  and and_35 (and_35_out, ~or_34_out, inval1[28]);  // AND_Gate
  and and_36 (and_36_out, ~or_35_out, inval1[27]);  // AND_Gate
  or or_36 (or_36_out, or_35_out, and_36_out);
  Multiplexer #(.width(6)) multiplexer_36 (
    .in0({6{1'b0}}), .in1(6'b011011), .out(multiplexer_36_out), .sel(and_36_out));
  Multiplexer #(.width(6)) multiplexer_37 (
    .in0({6{1'b0}}), .in1(6'b011100), .out(multiplexer_37_out), .sel(and_35_out));
  and and_37 (and_37_out, ~or_36_out, inval1[26]);  // AND_Gate
  and and_38 (and_38_out, ~or_37_out, inval1[25]);  // AND_Gate
  or or_37 (or_37_out, or_36_out, and_37_out);
  or or_38 (or_38_out, or_37_out, and_38_out);
  Multiplexer #(.width(6)) multiplexer_38 (
    .in0({6{1'b0}}), .in1(6'b011010), .out(multiplexer_38_out), .sel(and_37_out));
  and and_39 (and_39_out, ~or_38_out, inval1[24]);  // AND_Gate
  or or_39 (or_39_out, or_38_out, and_39_out);
  or or_40 (or_40_out, or_39_out, and_40_out);
  Multiplexer #(.width(6)) multiplexer_39 (
    .in0({6{1'b0}}), .in1(6'b011000), .out(multiplexer_39_out), .sel(and_39_out));
  Multiplexer #(.width(6)) multiplexer_40 (
    .in0({6{1'b0}}), .in1(6'b011001), .out(multiplexer_40_out), .sel(and_38_out));
  and and_40 (and_40_out, ~or_39_out, inval1[23]);  // AND_Gate
  and and_41 (and_41_out, ~or_40_out, inval1[22]);  // AND_Gate
  or or_41 (or_41_out, or_40_out, and_41_out);
  Multiplexer #(.width(6)) multiplexer_41 (
    .in0({6{1'b0}}), .in1(6'b010111), .out(multiplexer_41_out), .sel(and_40_out));
  and and_42 (and_42_out, ~or_41_out, inval1[21]);  // AND_Gate
  or or_42 (or_42_out, or_41_out, and_42_out);
  or or_43 (or_43_out, or_42_out, and_43_out);
  Multiplexer #(.width(6)) multiplexer_42 (
    .in0({6{1'b0}}), .in1(6'b010101), .out(multiplexer_42_out), .sel(and_42_out));
  Multiplexer #(.width(6)) multiplexer_43 (
    .in0({6{1'b0}}), .in1(6'b010110), .out(multiplexer_43_out), .sel(and_41_out));
  and and_43 (and_43_out, ~or_42_out, inval1[20]);  // AND_Gate
  and and_44 (and_44_out, ~or_43_out, inval1[19]);  // AND_Gate
  or or_44 (or_44_out, or_43_out, and_44_out);
  Multiplexer #(.width(6)) multiplexer_44 (
    .in0({6{1'b0}}), .in1(6'b010011), .out(multiplexer_44_out), .sel(and_44_out));
  Multiplexer #(.width(6)) multiplexer_45 (
    .in0({6{1'b0}}), .in1(6'b010100), .out(multiplexer_45_out), .sel(and_43_out));
  and and_45 (and_45_out, ~or_44_out, inval1[18]);  // AND_Gate
  and and_46 (and_46_out, ~or_45_out, inval1[17]);  // AND_Gate
  or or_45 (or_45_out, or_44_out, and_45_out);
  or or_46 (or_46_out, or_45_out, and_46_out);
  Multiplexer #(.width(6)) multiplexer_46 (
    .in0({6{1'b0}}), .in1(6'b010010), .out(multiplexer_46_out), .sel(and_45_out));
  and and_47 (and_47_out, ~or_46_out, inval1[16]);  // AND_Gate
  or or_47 (or_47_out, or_46_out, and_47_out);
  or or_48 (or_48_out, or_47_out, and_48_out);
  Multiplexer #(.width(6)) multiplexer_47 (
    .in0({6{1'b0}}), .in1(6'b010000), .out(multiplexer_47_out), .sel(and_47_out));
  Multiplexer #(.width(6)) multiplexer_48 (
    .in0({6{1'b0}}), .in1(6'b010001), .out(multiplexer_48_out), .sel(and_46_out));
  and and_48 (and_48_out, ~or_47_out, inval1[15]);  // AND_Gate
  and and_49 (and_49_out, ~or_48_out, inval1[14]);  // AND_Gate
  or or_49 (or_49_out, or_48_out, and_49_out);
  Multiplexer #(.width(6)) multiplexer_49 (
    .in0({6{1'b0}}), .in1(6'b001111), .out(multiplexer_49_out), .sel(and_48_out));
  and and_50 (and_50_out, ~or_49_out, inval1[13]);  // AND_Gate
  or or_50 (or_50_out, or_49_out, and_50_out);
  or or_51 (or_51_out, or_50_out, and_51_out);
  Multiplexer #(.width(6)) multiplexer_50 (
    .in0({6{1'b0}}), .in1(6'b001101), .out(multiplexer_50_out), .sel(and_50_out));
  Multiplexer #(.width(6)) multiplexer_51 (
    .in0({6{1'b0}}), .in1(6'b001110), .out(multiplexer_51_out), .sel(and_49_out));
  and and_51 (and_51_out, ~or_50_out, inval1[12]);  // AND_Gate
  and and_52 (and_52_out, ~or_51_out, inval1[11]);  // AND_Gate
  or or_52 (or_52_out, or_51_out, and_52_out);
  Multiplexer #(.width(6)) multiplexer_52 (
    .in0({6{1'b0}}), .in1(6'b001011), .out(multiplexer_52_out), .sel(and_52_out));
  Multiplexer #(.width(6)) multiplexer_53 (
    .in0({6{1'b0}}), .in1(6'b001100), .out(multiplexer_53_out), .sel(and_51_out));
  and and_53 (and_53_out, ~or_52_out, inval1[10]);  // AND_Gate
  and and_54 (and_54_out, ~or_53_out, inval1[9]);  // AND_Gate
  or or_53 (or_53_out, or_52_out, and_53_out);
  or or_54 (or_54_out, or_53_out, and_54_out);
  Multiplexer #(.width(6)) multiplexer_54 (
    .in0({6{1'b0}}), .in1(6'b001010), .out(multiplexer_54_out), .sel(and_53_out));
  and and_55 (and_55_out, ~or_54_out, inval1[8]);  // AND_Gate
  or or_55 (or_55_out, or_54_out, and_55_out);
  or or_56 (or_56_out, or_55_out, and_56_out);
  Multiplexer #(.width(6)) multiplexer_55 (
    .in0({6{1'b0}}), .in1(6'b001000), .out(multiplexer_55_out), .sel(and_55_out));
  Multiplexer #(.width(6)) multiplexer_56 (
    .in0({6{1'b0}}), .in1(6'b001001), .out(multiplexer_56_out), .sel(and_54_out));
  and and_56 (and_56_out, ~or_55_out, inval1[7]);  // AND_Gate
  and and_57 (and_57_out, ~or_56_out, inval1[6]);  // AND_Gate
  or or_57 (or_57_out, or_56_out, and_57_out);
  Multiplexer #(.width(6)) multiplexer_57 (
    .in0({6{1'b0}}), .in1(6'b000111), .out(multiplexer_57_out), .sel(and_56_out));
  and and_58 (and_58_out, ~or_57_out, inval1[5]);  // AND_Gate
  or or_58 (or_58_out, or_57_out, and_58_out);
  or or_59 (or_59_out, or_58_out, and_59_out);
  Multiplexer #(.width(6)) multiplexer_58 (
    .in0({6{1'b0}}), .in1(6'b000101), .out(multiplexer_58_out), .sel(and_58_out));
  Multiplexer #(.width(6)) multiplexer_59 (
    .in0({6{1'b0}}), .in1(6'b000110), .out(multiplexer_59_out), .sel(and_57_out));
  and and_59 (and_59_out, ~or_58_out, inval1[4]);  // AND_Gate
  and and_60 (and_60_out, ~or_59_out, inval1[3]);  // AND_Gate
  or or_60 (or_60_out, or_59_out, and_60_out);
  Multiplexer #(.width(6)) multiplexer_60 (
    .in0({6{1'b0}}), .in1(6'b000011), .out(multiplexer_60_out), .sel(and_60_out));
  Multiplexer #(.width(6)) multiplexer_61 (
    .in0({6{1'b0}}), .in1(6'b000100), .out(multiplexer_61_out), .sel(and_59_out));
  and and_61 (and_61_out, ~or_60_out, inval1[2]);  // AND_Gate
  and and_62 (and_62_out, ~or_61_out, inval1[1]);  // AND_Gate
  or or_61 (or_61_out, or_60_out, and_61_out);
  or or_62 (or_62_out, or_61_out, and_62_out);
  Multiplexer #(.width(6)) multiplexer_62 (
    .in0({6{1'b0}}), .in1(6'b000010), .out(multiplexer_62_out), .sel(and_61_out));
  and and_63 (and_63_out, ~or_62_out, inval1[0]);  // AND_Gate
  or or_63 (or_63_out, or_62_out, and_63_out);
  Multiplexer #(.width(6)) multiplexer_63 (
    .in0({6{1'b0}}), .in1({6{1'b0}}), .out(multiplexer_63_out), .sel(and_63_out));
  Multiplexer #(.width(6)) multiplexer_64 (
    .in0({6{1'b0}}), .in1(6'b000001), .out(multiplexer_64_out), .sel(and_62_out));
  assign or_64_out = multiplexer_63_out | multiplexer_64_out | multiplexer_62_out | multiplexer_60_out | multiplexer_61_out | multiplexer_58_out | multiplexer_59_out | multiplexer_57_out | multiplexer_55_out | multiplexer_56_out | multiplexer_54_out | multiplexer_52_out | multiplexer_53_out | multiplexer_50_out | multiplexer_51_out | multiplexer_49_out | multiplexer_47_out | multiplexer_48_out | multiplexer_46_out | multiplexer_44_out | multiplexer_45_out | multiplexer_42_out | multiplexer_43_out | multiplexer_41_out | multiplexer_39_out | multiplexer_40_out | multiplexer_38_out | multiplexer_36_out | multiplexer_37_out | multiplexer_34_out | multiplexer_35_out | multiplexer_33_out | multiplexer_31_out | multiplexer_32_out | multiplexer_30_out | multiplexer_28_out | multiplexer_29_out | multiplexer_26_out | multiplexer_27_out | multiplexer_25_out | multiplexer_23_out | multiplexer_24_out | multiplexer_22_out | multiplexer_20_out | multiplexer_21_out | multiplexer_18_out | multiplexer_19_out | multiplexer_17_out | multiplexer_15_out | multiplexer_16_out | multiplexer_14_out | multiplexer_12_out | multiplexer_13_out | multiplexer_10_out | multiplexer_11_out | multiplexer_9_out | multiplexer_7_out | multiplexer_8_out | multiplexer_6_out | multiplexer_4_out | multiplexer_5_out | multiplexer_2_out | multiplexer_3_out | multiplexer_1_out;  // OR_Gate or_64, 6 bits wide
  not not_1 (not_1_out, or_63_out);
  Multiplexer #(.width(6)) multiplexer_65 (.in0({6{1'b0}}), .in1(or_64_out), .out(priorityindex1), .sel(groupselect1));
  and and_64 (groupselect1, or_63_out, enablein1);
  and and_65 (enableout1, not_1_out, enablein1);
  // Probe on priority_encoder_1_out
  // Probe on priority_encoder_1_gs
  // Probe on priority_encoder_1_en_out
  // Probe on priorityindex1

  // Notes on the sheet:
  //   in_1: initial=0x3bf6b2a83cb280
  //   in_2: initial=0x3fffffffffffffff
  //   in_3: initial=0xffffffffffffffff
  //   in_4: initial=0xb48888ff0000
  //   inval1: initial=0xb48888ff0000
  //   enablein1: initial=0x1
endmodule

module fexp64 (
  input  [63:0] inval1,
  output [63:0] outval1,
  output isnan1
);

  wire fpexponentiator_1_p2;
  wire [63:0] fpadder_1_out, fpadder_2_out, fpadder_3_out, fpadder_4_out, fpadder_5_out, fpadder_6_out,
       fpadder_7_out, fpadder_8_out, fpadder_9_out, fpadder_10_out, fpadder_11_out, fpadder_12_out,
       fpadder_13_out, fpadder_14_out, fpadder_15_out, fpadder_16_out, fpadder_17_out, fpadder_18_out,
       fpadder_19_out, fpadder_20_out, fpadder_21_out, fpadder_22_out, fpadder_23_out, fpmultiplier_1_out,
       fpmultiplier_2_out, fpmultiplier_3_out, fpmultiplier_4_out, fpmultiplier_5_out, fpmultiplier_6_out,
       fpmultiplier_7_out, fpmultiplier_8_out, fpmultiplier_9_out, fpmultiplier_10_out, fpmultiplier_11_out,
       fpmultiplier_12_out, fpmultiplier_13_out, fpmultiplier_14_out, fpmultiplier_15_out,
       fpmultiplier_16_out, fpmultiplier_17_out, fpmultiplier_18_out, fpmultiplier_19_out,
       fpmultiplier_20_out, fpmultiplier_21_out, fpmultiplier_22_out, fpmultiplier_23_out,
       fpmultiplier_24_out, fpmultiplier_25_out, fpmultiplier_26_out, fpmultiplier_27_out,
       fpmultiplier_28_out, fpmultiplier_29_out, fpmultiplier_30_out, fpmultiplier_31_out,
       fpmultiplier_32_out, fpmultiplier_33_out, fpmultiplier_34_out, fpmultiplier_35_out,
       fpmultiplier_36_out, fpmultiplier_37_out, fpmultiplier_38_out, fpmultiplier_39_out,
       fpmultiplier_40_out, fpmultiplier_41_out, fpmultiplier_42_out, fpmultiplier_43_out,
       fpmultiplier_44_out, fpmultiplier_45_out, fpmultiplier_46_out;

  // Probe on inval1
  FPMultiplier #(.fpwidth(64)) fpmultiplier_1 (.a(inval1), .b(inval1), .out(fpmultiplier_1_out));
  FPMultiplier #(.fpwidth(64)) fpmultiplier_2 (.a(fpmultiplier_1_out), .b(inval1), .out(fpmultiplier_2_out));
  FPMultiplier #(.fpwidth(64)) fpmultiplier_3 (.a(fpmultiplier_2_out), .b(inval1), .out(fpmultiplier_3_out));
  FPMultiplier #(.fpwidth(64)) fpmultiplier_4 (.a(fpmultiplier_3_out), .b(inval1), .out(fpmultiplier_4_out));
  FPMultiplier #(.fpwidth(64)) fpmultiplier_5 (.a(fpmultiplier_4_out), .b(inval1), .out(fpmultiplier_5_out));
  FPMultiplier #(.fpwidth(64)) fpmultiplier_6 (.a(fpmultiplier_5_out), .b(inval1), .out(fpmultiplier_6_out));
  FPMultiplier #(.fpwidth(64)) fpmultiplier_7 (.a(fpmultiplier_6_out), .b(inval1), .out(fpmultiplier_7_out));
  FPMultiplier #(.fpwidth(64)) fpmultiplier_8 (.a(fpmultiplier_7_out), .b(inval1), .out(fpmultiplier_8_out));
  FPMultiplier #(.fpwidth(64)) fpmultiplier_9 (.a(fpmultiplier_8_out), .b(inval1), .out(fpmultiplier_9_out));
  FPMultiplier #(.fpwidth(64)) fpmultiplier_10 (.a(fpmultiplier_9_out), .b(inval1), .out(fpmultiplier_10_out));
  FPMultiplier #(.fpwidth(64)) fpmultiplier_11 (.a(fpmultiplier_10_out), .b(inval1), .out(fpmultiplier_11_out));
  FPMultiplier #(.fpwidth(64)) fpmultiplier_12 (.a(fpmultiplier_11_out), .b(inval1), .out(fpmultiplier_12_out));
  FPMultiplier #(.fpwidth(64)) fpmultiplier_13 (.a(fpmultiplier_12_out), .b(inval1), .out(fpmultiplier_13_out));
  FPMultiplier #(.fpwidth(64)) fpmultiplier_14 (.a(fpmultiplier_13_out), .b(inval1), .out(fpmultiplier_14_out));
  FPMultiplier #(.fpwidth(64)) fpmultiplier_15 (.a(fpmultiplier_14_out), .b(inval1), .out(fpmultiplier_15_out));
  FPMultiplier #(.fpwidth(64)) fpmultiplier_16 (.a(fpmultiplier_15_out), .b(inval1), .out(fpmultiplier_16_out));
  FPMultiplier #(.fpwidth(64)) fpmultiplier_17 (.a(fpmultiplier_16_out), .b(inval1), .out(fpmultiplier_17_out));
  FPMultiplier #(.fpwidth(64)) fpmultiplier_18 (.a(fpmultiplier_17_out), .b(inval1), .out(fpmultiplier_18_out));
  FPMultiplier #(.fpwidth(64)) fpmultiplier_19 (.a(fpmultiplier_18_out), .b(inval1), .out(fpmultiplier_19_out));
  FPMultiplier #(.fpwidth(64)) fpmultiplier_20 (.a(fpmultiplier_19_out), .b(inval1), .out(fpmultiplier_20_out));
  FPMultiplier #(.fpwidth(64)) fpmultiplier_21 (.a(fpmultiplier_20_out), .b(inval1), .out(fpmultiplier_21_out));
  FPMultiplier #(.fpwidth(64)) fpmultiplier_22 (.a(fpmultiplier_21_out), .b(inval1), .out(fpmultiplier_22_out));
  FPMultiplier #(.fpwidth(64)) fpmultiplier_23 (.a(fpmultiplier_22_out), .b(inval1), .out(fpmultiplier_23_out));
  // FPExponentiator #(.fpwidth(64), .mode("exp")) fpexponentiator_1: pin names not known; wires that end beside it: inval1, fpexponentiator_1_p2
  FPAdder #(.fpwidth(64)) fpadder_1 (.a(inval1), .b(64'h3ff0000000000000), .out(fpadder_1_out));
  FPMultiplier #(.fpwidth(64)) fpmultiplier_24 (
    .a(fpmultiplier_1_out), .b(64'h3fe0000000000000), .out(fpmultiplier_24_out));
  FPAdder #(.fpwidth(64)) fpadder_2 (.a(fpadder_1_out), .b(fpmultiplier_24_out), .out(fpadder_2_out));
  FPMultiplier #(.fpwidth(64)) fpmultiplier_25 (
    .a(fpmultiplier_2_out), .b(64'h3fc5555555555555), .out(fpmultiplier_25_out));
  FPAdder #(.fpwidth(64)) fpadder_3 (.a(fpadder_2_out), .b(fpmultiplier_25_out), .out(fpadder_3_out));
  FPMultiplier #(.fpwidth(64)) fpmultiplier_26 (
    .a(fpmultiplier_3_out), .b(64'h3fa5555555555555), .out(fpmultiplier_26_out));
  FPAdder #(.fpwidth(64)) fpadder_4 (.a(fpadder_3_out), .b(fpmultiplier_26_out), .out(fpadder_4_out));
  FPMultiplier #(.fpwidth(64)) fpmultiplier_27 (
    .a(fpmultiplier_4_out), .b(64'h3f81111111111111), .out(fpmultiplier_27_out));
  FPAdder #(.fpwidth(64)) fpadder_5 (.a(fpadder_4_out), .b(fpmultiplier_27_out), .out(fpadder_5_out));
  FPMultiplier #(.fpwidth(64)) fpmultiplier_28 (
    .a(fpmultiplier_5_out), .b(64'h3f56c16c16c16c17), .out(fpmultiplier_28_out));
  FPAdder #(.fpwidth(64)) fpadder_6 (.a(fpadder_5_out), .b(fpmultiplier_28_out), .out(fpadder_6_out));
  FPMultiplier #(.fpwidth(64)) fpmultiplier_29 (
    .a(fpmultiplier_6_out), .b(64'h3f2a01a01a01a01a), .out(fpmultiplier_29_out));
  FPAdder #(.fpwidth(64)) fpadder_7 (.a(fpadder_6_out), .b(fpmultiplier_29_out), .out(fpadder_7_out));
  FPMultiplier #(.fpwidth(64)) fpmultiplier_30 (
    .a(fpmultiplier_7_out), .b(64'h3efa01a01a01a01a), .out(fpmultiplier_30_out));
  FPAdder #(.fpwidth(64)) fpadder_8 (.a(fpadder_7_out), .b(fpmultiplier_30_out), .out(fpadder_8_out));
  FPMultiplier #(.fpwidth(64)) fpmultiplier_31 (
    .a(fpmultiplier_8_out), .b(64'h3ec71de3a556c734), .out(fpmultiplier_31_out));
  FPAdder #(.fpwidth(64)) fpadder_9 (.a(fpadder_8_out), .b(fpmultiplier_31_out), .out(fpadder_9_out));
  FPMultiplier #(.fpwidth(64)) fpmultiplier_32 (
    .a(fpmultiplier_9_out), .b(64'h3e927e4fb7789f5c), .out(fpmultiplier_32_out));
  FPAdder #(.fpwidth(64)) fpadder_10 (.a(fpadder_9_out), .b(fpmultiplier_32_out), .out(fpadder_10_out));
  FPMultiplier #(.fpwidth(64)) fpmultiplier_33 (
    .a(fpmultiplier_10_out), .b(64'h3e5ae64567f544e4), .out(fpmultiplier_33_out));
  FPAdder #(.fpwidth(64)) fpadder_11 (.a(fpadder_10_out), .b(fpmultiplier_33_out), .out(fpadder_11_out));
  FPMultiplier #(.fpwidth(64)) fpmultiplier_34 (
    .a(fpmultiplier_11_out), .b(64'h3e21eed8eff8d898), .out(fpmultiplier_34_out));
  FPAdder #(.fpwidth(64)) fpadder_12 (.a(fpadder_11_out), .b(fpmultiplier_34_out), .out(fpadder_12_out));
  FPMultiplier #(.fpwidth(64)) fpmultiplier_35 (
    .a(fpmultiplier_12_out), .b(64'h3de6124613a86d09), .out(fpmultiplier_35_out));
  FPAdder #(.fpwidth(64)) fpadder_13 (.a(fpadder_12_out), .b(fpmultiplier_35_out), .out(fpadder_13_out));
  FPMultiplier #(.fpwidth(64)) fpmultiplier_36 (
    .a(fpmultiplier_13_out), .b(64'h3da93974a8c07c9d), .out(fpmultiplier_36_out));
  FPAdder #(.fpwidth(64)) fpadder_14 (.a(fpadder_13_out), .b(fpmultiplier_36_out), .out(fpadder_14_out));
  FPMultiplier #(.fpwidth(64)) fpmultiplier_37 (
    .a(fpmultiplier_14_out), .b(64'h3d6ae7f3e733b81f), .out(fpmultiplier_37_out));
  FPAdder #(.fpwidth(64)) fpadder_15 (.a(fpadder_14_out), .b(fpmultiplier_37_out), .out(fpadder_15_out));
  FPMultiplier #(.fpwidth(64)) fpmultiplier_38 (
    .a(fpmultiplier_15_out), .b(64'h3d2ae7f3e733b81f), .out(fpmultiplier_38_out));
  FPAdder #(.fpwidth(64)) fpadder_16 (.a(fpadder_15_out), .b(fpmultiplier_38_out), .out(fpadder_16_out));
  FPMultiplier #(.fpwidth(64)) fpmultiplier_39 (
    .a(fpmultiplier_16_out), .b(64'h3ce952c77030ad4a), .out(fpmultiplier_39_out));
  FPAdder #(.fpwidth(64)) fpadder_17 (.a(fpadder_16_out), .b(fpmultiplier_39_out), .out(fpadder_17_out));
  FPMultiplier #(.fpwidth(64)) fpmultiplier_40 (
    .a(fpmultiplier_17_out), .b(64'h3ca6827863b97d97), .out(fpmultiplier_40_out));
  FPAdder #(.fpwidth(64)) fpadder_18 (.a(fpadder_17_out), .b(fpmultiplier_40_out), .out(fpadder_18_out));
  FPMultiplier #(.fpwidth(64)) fpmultiplier_41 (
    .a(fpmultiplier_18_out), .b(64'h3c62f49b46814157), .out(fpmultiplier_41_out));
  FPAdder #(.fpwidth(64)) fpadder_19 (.a(fpadder_18_out), .b(fpmultiplier_41_out), .out(fpadder_19_out));
  FPMultiplier #(.fpwidth(64)) fpmultiplier_42 (
    .a(fpmultiplier_19_out), .b(64'h3c1e542ba4020225), .out(fpmultiplier_42_out));
  FPAdder #(.fpwidth(64)) fpadder_20 (.a(fpadder_19_out), .b(fpmultiplier_42_out), .out(fpadder_20_out));
  FPMultiplier #(.fpwidth(64)) fpmultiplier_43 (
    .a(fpmultiplier_20_out), .b(64'h3bd71b8ef6dcf572), .out(fpmultiplier_43_out));
  FPAdder #(.fpwidth(64)) fpadder_21 (.a(fpadder_20_out), .b(fpmultiplier_43_out), .out(fpadder_21_out));
  FPMultiplier #(.fpwidth(64)) fpmultiplier_44 (
    .a(fpmultiplier_21_out), .b(64'h3b90ce396db7f853), .out(fpmultiplier_44_out));
  FPAdder #(.fpwidth(64)) fpadder_22 (.a(fpadder_21_out), .b(fpmultiplier_44_out), .out(fpadder_22_out));
  FPMultiplier #(.fpwidth(64)) fpmultiplier_45 (
    .a(fpmultiplier_22_out), .b(64'h3b4761b41316381a), .out(fpmultiplier_45_out));
  FPAdder #(.fpwidth(64)) fpadder_23 (.a(fpadder_22_out), .b(fpmultiplier_45_out), .out(fpadder_23_out));
  FPMultiplier #(.fpwidth(64)) fpmultiplier_46 (
    .a(fpmultiplier_23_out), .b(64'h3aff2cf01972f578), .out(fpmultiplier_46_out));
  FPAdder #(.fpwidth(64)) fpadder_24 (.a(fpadder_23_out), .b(fpmultiplier_46_out), .out(outval1));
  // Probe on fpexponentiator_1_p2
  // Probe on outval1

  // Notes on the sheet:
  //   inval1: initial=0x4020152bd3c36113
endmodule

module fitf64 (
  input  [63:0] in_1,
  input  [63:0] in_2,
  input  [63:0] in_3,
  input  [63:0] in_4,
  input  [63:0] in_5,
  input  [63:0] in_6,
  input  [63:0] in_7,
  input  [63:0] in_8,
  input  [63:0] in_9,
  input  [63:0] in_10,
  input  [63:0] in_11,
  input  [63:0] in_12,
  input  [63:0] in_13,
  input  [63:0] in_14,
  input  [63:0] in_15,
  input  [63:0] inval1,
  output [63:0] outval1,
  output isnan1
);

  wire adder_2_cout, inttofp_1_p2;
  wire [5:0] hone64_1_outval1, subtractor_1_out;
  wire [15:0] bit_extender_1_out;
  wire [15:11] adder_1_out;
  wire [63:0] adder_2_out, multiplexer_1_out, multiplexer_2_out, negator_1_out, shifter_1_out;

  // Probe on inval1
  // IntToFP #(.fpwidth(64), .width(64)) inttofp_1: pin names not known; wires that end beside it: inval1, inttofp_1_p2
  Negator #(.width(64)) negator_1 (.in(inval1), .out(negator_1_out));
  Multiplexer #(.width(64)) multiplexer_1 (
    .in0(inval1), .in1(negator_1_out), .out(multiplexer_1_out), .sel(outval1[63]));
  Comparator #(.width(64)) comparator_1 (.a(inval1), .b({64{1'b0}}), .lt(outval1[63]));  // open: gt, eq
  Subtractor #(.width(6)) subtractor_1 (
    .a({6{1'b1}}), .b(hone64_1_outval1), .out(subtractor_1_out));  // open: bin, bout
  Shifter #(.width(64)) shifter_1 (.in(multiplexer_1_out), .\dist (subtractor_1_out), .out(shifter_1_out));
  hone64 hone64_1 (.inval1(multiplexer_1_out), .outval1(hone64_1_outval1));  // open: contains1
  assign bit_extender_1_out = {{10{1'b0}}, hone64_1_outval1};  // Bit_Extender bit_extender_1
  Adder #(.width(16)) adder_1 (
    .a(bit_extender_1_out), .b(16'h3ff), .out({adder_1_out, outval1[62:52]}), .cin(adder_2_cout));  // open: cout
  Multiplexer #(.width(64)) multiplexer_2 (
    .in0(shifter_1_out), .in1(adder_2_out),
    .out({multiplexer_2_out[63], outval1[51:0], multiplexer_2_out[10:0]}), .sel(shifter_1_out[10]));
  Adder #(.width(64)) adder_2 (.a(64'h800), .b(shifter_1_out), .out(adder_2_out), .cout(adder_2_cout));  // open: cin
  // Probe on inttofp_1_p2
  // Probe on inttofp_1_p2
  // Probe on outval1

  // Notes on the sheet:
  //   in_1: initial=0xfffffffffff80b3e
  //   in_2: initial=0x408e6d5c28f5c28f
  //   in_3: initial=0xc5b1354992695dcb
  //   in_4: initial=0xc127e50ee147ae14
  //   in_5: initial=0x45b1354992695dcb
  //   in_6: initial=0x4373ec6e44274ce4
  //   in_7: initial=0x4127e50ee147ae14
  //   in_8: initial=0x4020152bd3c36113
  //   in_9: initial=0x4040152bd3c36113
  //   in_10: initial=0x4061d93f7ced9168
  //   in_11: initial=0xc056ef0d844d013b
  //   in_12: initial=0x3bf6b2a83cb280
  //   in_13: initial=0x3fffffffffffffff
  //   in_14: initial=0xffffffffffffffff
  //   in_15: initial=0xb48888ff0000
  //   inval1: initial=0xfffffffffff80b3e
endmodule

module ffti64 (
  input  [63:0] in_1,
  input  [63:0] in_2,
  input  [63:0] in_3,
  input  [63:0] in_4,
  input  [63:0] in_5,
  input  [63:0] in_6,
  input  [63:0] in_7,
  input  [63:0] in_8,
  input  [63:0] in_9,
  input  [63:0] in_10,
  input  [63:0] in_11,
  input  [63:0] in_12,
  input  [63:0] in_13,
  input  [63:0] in_14,
  input  [63:0] inval1,
  output [63:0] nearoutval1,
  output [63:0] downoutval1,
  output [63:0] upoutval1,
  output [63:0] truncoutval1,
  output isnan1
);

  wire and_1_out, and_2_out, comparator_1_gt, comparator_2_lt, comparator_3_gt, comparator_4_lt,
       comparator_5_gt, comparator_6_eq, comparator_6_gt, comparator_7_gt, fptoint_1_p2, fptoint_2_p2,
       fptoint_3_p2, fptoint_4_p2, not_1_out, or_1_out;
  wire [6:0] multiplexer_1_out, multiplexer_2_out;
  wire [15:0] bit_extender_1_out, negator_1_out, subtractor_1_out, subtractor_2_out;
  wire [15:7] multiplexer_1_out_2, multiplexer_2_out_2;
  wire [63:0] adder_1_out, adder_2_out, adder_3_out, bit_extender_2_out, bit_extender_3_out,
       bit_extender_4_out, multiplexer_3_out, multiplexer_4_out, multiplexer_5_out, multiplexer_6_out,
       multiplexer_7_out, multiplexer_8_out, multiplexer_9_out, multiplexer_10_out, multiplexer_11_out,
       negator_2_out, negator_3_out, negator_4_out, shl128_1_outval1a, shl128_1_outval1b, shr128_1_outval1a,
       shr128_1_outval1b;

  // Probe on inval1
  // FPToInt #(.fpwidth(64), .width(64)) fptoint_1: pin names not known; wires that end beside it: inval1, fptoint_1_p2
  // FPToInt #(.fpwidth(64), .mode("floor"), .width(64)) fptoint_2: pin names not known; wires that end beside it: inval1, fptoint_2_p2
  // FPToInt #(.fpwidth(64), .mode("ceil"), .width(64)) fptoint_3: pin names not known; wires that end beside it: inval1, fptoint_3_p2
  // FPToInt #(.fpwidth(64), .mode("truncate"), .width(64)) fptoint_4: pin names not known; wires that end beside it: inval1, fptoint_4_p2
  Multiplexer #(.width(16)) multiplexer_1 (
    .in0(subtractor_1_out), .in1(16'h7f), .out({multiplexer_1_out_2, multiplexer_1_out}),
    .sel(comparator_1_gt));
  Comparator #(.width(16)) comparator_1 (.a(subtractor_1_out), .b(16'h7f), .gt(comparator_1_gt));  // open: eq, lt
  Subtractor #(.width(16)) subtractor_1 (.a(subtractor_2_out), .b(16'h3d), .out(subtractor_1_out));  // open: bin, bout
  Subtractor #(.width(16)) subtractor_2 (
    .a(bit_extender_1_out), .b(16'h3ff), .out(subtractor_2_out));  // open: bin, bout
  assign bit_extender_1_out = {{5{1'b0}}, inval1[62:52]};  // Bit_Extender bit_extender_1
  shl128 shl128_1 (
    .inval1b({3'b001, inval1[51:0], {9{1'b0}}}), .shift1a(multiplexer_1_out), .outval1a(shl128_1_outval1a),
    .outval1b(shl128_1_outval1b));  // open: inval1a
  Negator #(.width(16)) negator_1 (.in(subtractor_1_out), .out(negator_1_out));
  Comparator #(.width(16)) comparator_2 (.a(subtractor_1_out), .b({16{1'b0}}), .lt(comparator_2_lt));  // open: gt, eq
  Comparator #(.width(16)) comparator_3 (.a(subtractor_2_out), .b(16'h3d), .gt(comparator_3_gt));  // open: eq, lt
  Comparator #(.width(16)) comparator_4 (.a(subtractor_2_out), .b({16{1'b0}}), .lt(comparator_4_lt));  // open: gt, eq
  Multiplexer #(.width(16)) multiplexer_2 (
    .in0(negator_1_out), .in1(16'h7f), .out({multiplexer_2_out_2, multiplexer_2_out}), .sel(comparator_5_gt));
  Comparator #(.width(16)) comparator_5 (.a(negator_1_out), .b(16'h7f), .gt(comparator_5_gt));  // open: eq, lt
  shr128 shr128_1 (
    .inval1b({3'b001, inval1[51:0], {9{1'b0}}}), .shift1a(multiplexer_2_out), .outval1a(shr128_1_outval1a),
    .outval1b(shr128_1_outval1b));  // open: inval1a
  Multiplexer #(.width(64)) multiplexer_3 (
    .in0(shl128_1_outval1a), .in1(shr128_1_outval1a), .out(multiplexer_3_out), .sel(comparator_2_lt));
  Multiplexer #(.width(64)) multiplexer_4 (
    .in0(shl128_1_outval1b), .in1(shr128_1_outval1b), .out(multiplexer_4_out), .sel(comparator_2_lt));
  Negator #(.width(64)) negator_2 (.in(multiplexer_4_out), .out(negator_2_out));
  Multiplexer #(.width(64)) multiplexer_5 (
    .in0(multiplexer_4_out), .in1(negator_2_out), .out(multiplexer_5_out), .sel(inval1[63]));
  or or_1 (or_1_out, comparator_6_gt, comparator_6_eq);
  Comparator #(.mode("unsigned"), .width(64)) comparator_6 (
    .a(multiplexer_3_out), .b(64'h8000000000000000), .gt(comparator_6_gt), .eq(comparator_6_eq));  // open: lt
  Comparator #(.mode("unsigned"), .width(64)) comparator_7 (
    .a(multiplexer_3_out), .b({64{1'b0}}), .gt(comparator_7_gt));  // open: eq, lt
  not not_1 (not_1_out, inval1[63]);
  assign bit_extender_2_out = {{63{1'b0}}, or_1_out};  // Bit_Extender bit_extender_2
  assign bit_extender_3_out = {{63{1'b0}}, and_1_out};  // Bit_Extender bit_extender_3
  and and_1 (and_1_out, comparator_7_gt, inval1[63]);
  assign bit_extender_4_out = {{63{1'b0}}, and_2_out};  // Bit_Extender bit_extender_4
  and and_2 (and_2_out, comparator_7_gt, not_1_out);
  Negator #(.width(64)) negator_3 (.in(bit_extender_2_out), .out(negator_3_out));
  Negator #(.width(64)) negator_4 (.in(bit_extender_3_out), .out(negator_4_out));
  Multiplexer #(.width(64)) multiplexer_6 (
    .in0(bit_extender_2_out), .in1(negator_3_out), .out(multiplexer_6_out), .sel(inval1[63]));
  Adder #(.width(64)) adder_1 (.a(multiplexer_5_out), .b(multiplexer_6_out), .out(adder_1_out));  // open: cin, cout
  Adder #(.width(64)) adder_2 (.a(multiplexer_5_out), .b(negator_4_out), .out(adder_2_out));  // open: cin, cout
  Adder #(.width(64)) adder_3 (.a(multiplexer_5_out), .b(bit_extender_4_out), .out(adder_3_out));  // open: cin, cout
  Multiplexer #(.width(64)) multiplexer_7 (
    .in0(adder_1_out), .in1({64{1'b0}}), .out(multiplexer_7_out), .sel(comparator_4_lt));
  Multiplexer #(.width(64)) multiplexer_8 (
    .in0(adder_2_out), .in1({64{1'b0}}), .out(multiplexer_8_out), .sel(comparator_4_lt));
  Multiplexer #(.width(64)) multiplexer_9 (
    .in0(adder_3_out), .in1({64{1'b0}}), .out(multiplexer_9_out), .sel(comparator_4_lt));
  Multiplexer #(.width(64)) multiplexer_10 (
    .in0(multiplexer_5_out), .in1({64{1'b0}}), .out(multiplexer_10_out), .sel(comparator_4_lt));
  Multiplexer #(.width(64)) multiplexer_11 (
    .in0(64'h7fffffffffffffff), .in1(64'h8000000000000000), .out(multiplexer_11_out), .sel(inval1[63]));
  Multiplexer #(.width(64)) multiplexer_12 (
    .in0(multiplexer_7_out), .in1(multiplexer_11_out), .out(nearoutval1), .sel(comparator_3_gt));
  Multiplexer #(.width(64)) multiplexer_13 (
    .in0(multiplexer_8_out), .in1(multiplexer_11_out), .out(downoutval1), .sel(comparator_3_gt));
  Multiplexer #(.width(64)) multiplexer_14 (
    .in0(multiplexer_9_out), .in1(multiplexer_11_out), .out(upoutval1), .sel(comparator_3_gt));
  Multiplexer #(.width(64)) multiplexer_15 (
    .in0(multiplexer_10_out), .in1(multiplexer_11_out), .out(truncoutval1), .sel(comparator_3_gt));
  // Probe on fptoint_1_p2
  // Probe on fptoint_1_p2
  // Probe on fptoint_2_p2
  // Probe on fptoint_2_p2
  // Probe on fptoint_3_p2
  // Probe on fptoint_3_p2
  // Probe on fptoint_4_p2
  // Probe on fptoint_4_p2
  // Probe on nearoutval1
  // Probe on downoutval1
  // Probe on upoutval1
  // Probe on truncoutval1

  // Notes on the sheet:
  //   in_1: initial=0x408e6d5c28f5c28f
  //   in_2: initial=0xc5b1354992695dcb
  //   in_3: initial=0xc127e50ee147ae14
  //   in_4: initial=0x45b1354992695dcb
  //   in_5: initial=0x4373ec6e44274ce4
  //   in_6: initial=0x4127e50ee147ae14
  //   in_7: initial=0x4020152bd3c36113
  //   in_8: initial=0x4040152bd3c36113
  //   in_9: initial=0x4061d93f7ced9168
  //   in_10: initial=0xc056ef0d844d013b
  //   in_11: initial=0x3bf6b2a83cb280
  //   in_12: initial=0x3fffffffffffffff
  //   in_13: initial=0xffffffffffffffff
  //   in_14: initial=0xb48888ff0000
  //   inval1: initial=0x3bf6b2a83cb280
endmodule
module fln64 (
  input  [63:0] inval1,
  output [63:0] outval1,
  output isnan1
);

  wire fplogarithm_1_p2;
  wire [15:0] bit_extender_1_out, inttofp_1_p1;
  wire [63:0] fpadder_1_out, fpadder_2_out, fpadder_3_out, fpadder_4_out, fpadder_5_out, fpadder_6_out,
       fpadder_7_out, fpadder_8_out, fpadder_9_out, fpadder_10_out, fpadder_11_out, fpadder_12_out,
       fpadder_13_out, fpadder_14_out, fpadder_15_out, fpadder_16_out, fpadder_17_out, fpadder_18_out,
       fpadder_19_out, fpadder_20_out, fpadder_21_out, fpadder_22_out, fpadder_23_out, fpadder_24_out,
       fpmultiplier_1_out, fpmultiplier_2_out, fpmultiplier_3_out, fpmultiplier_4_out, fpmultiplier_5_out,
       fpmultiplier_6_out, fpmultiplier_7_out, fpmultiplier_8_out, fpmultiplier_9_out, fpmultiplier_10_out,
       fpmultiplier_11_out, fpmultiplier_12_out, fpmultiplier_13_out, fpmultiplier_14_out,
       fpmultiplier_15_out, fpmultiplier_16_out, fpmultiplier_17_out, fpmultiplier_18_out,
       fpmultiplier_19_out, fpmultiplier_20_out, fpmultiplier_21_out, fpmultiplier_22_out,
       fpmultiplier_23_out, fpmultiplier_24_out, fpmultiplier_25_out, fpmultiplier_26_out,
       fpmultiplier_27_out, fpmultiplier_28_out, fpmultiplier_29_out, fpmultiplier_30_out,
       fpmultiplier_31_out, fpmultiplier_32_out, fpmultiplier_33_out, fpmultiplier_34_out,
       fpmultiplier_35_out, fpmultiplier_36_out, fpmultiplier_37_out, fpmultiplier_38_out,
       fpmultiplier_39_out, fpmultiplier_40_out, fpmultiplier_41_out, fpmultiplier_42_out,
       fpmultiplier_43_out, fpmultiplier_44_out, fpmultiplier_45_out, fpmultiplier_46_out,
       fpmultiplier_47_out, inttofp_1_p2;

  // IntToFP #(.fpwidth(64), .width(16)) inttofp_1: pin names not known; wires that end beside it: inttofp_1_p1, inttofp_1_p2
  Subtractor #(.width(16)) subtractor_1 (.a(bit_extender_1_out), .b(16'h3ff), .out(inttofp_1_p1));  // open: bin, bout
  assign bit_extender_1_out = {{5{1'b0}}, inval1[62:52]};  // Bit_Extender bit_extender_1
  // Probe on inval1
  FPAdder #(.fpwidth(64)) fpadder_1 (
    .a(64'hbff0000000000000), .b({inval1[63], 11'h3ff, inval1[51:0]}), .out(fpadder_1_out));
  FPMultiplier #(.fpwidth(64)) fpmultiplier_1 (.a(64'h3fe62e42fefa39ef), .b(inttofp_1_p2), .out(fpmultiplier_1_out));
  FPMultiplier #(.fpwidth(64)) fpmultiplier_2 (.a(fpadder_1_out), .b(fpadder_1_out), .out(fpmultiplier_2_out));
  FPMultiplier #(.fpwidth(64)) fpmultiplier_3 (.a(fpmultiplier_2_out), .b(fpadder_1_out), .out(fpmultiplier_3_out));
  FPMultiplier #(.fpwidth(64)) fpmultiplier_4 (.a(fpmultiplier_3_out), .b(fpadder_1_out), .out(fpmultiplier_4_out));
  FPMultiplier #(.fpwidth(64)) fpmultiplier_5 (.a(fpmultiplier_4_out), .b(fpadder_1_out), .out(fpmultiplier_5_out));
  FPMultiplier #(.fpwidth(64)) fpmultiplier_6 (.a(fpmultiplier_5_out), .b(fpadder_1_out), .out(fpmultiplier_6_out));
  FPMultiplier #(.fpwidth(64)) fpmultiplier_7 (.a(fpmultiplier_6_out), .b(fpadder_1_out), .out(fpmultiplier_7_out));
  FPMultiplier #(.fpwidth(64)) fpmultiplier_8 (.a(fpmultiplier_7_out), .b(fpadder_1_out), .out(fpmultiplier_8_out));
  FPMultiplier #(.fpwidth(64)) fpmultiplier_9 (.a(fpmultiplier_8_out), .b(fpadder_1_out), .out(fpmultiplier_9_out));
  FPMultiplier #(.fpwidth(64)) fpmultiplier_10 (.a(fpmultiplier_9_out), .b(fpadder_1_out), .out(fpmultiplier_10_out));
  FPMultiplier #(.fpwidth(64)) fpmultiplier_11 (.a(fpmultiplier_10_out), .b(fpadder_1_out), .out(fpmultiplier_11_out));
  FPMultiplier #(.fpwidth(64)) fpmultiplier_12 (.a(fpmultiplier_11_out), .b(fpadder_1_out), .out(fpmultiplier_12_out));
  FPMultiplier #(.fpwidth(64)) fpmultiplier_13 (.a(fpmultiplier_12_out), .b(fpadder_1_out), .out(fpmultiplier_13_out));
  FPMultiplier #(.fpwidth(64)) fpmultiplier_14 (.a(fpmultiplier_13_out), .b(fpadder_1_out), .out(fpmultiplier_14_out));
  FPMultiplier #(.fpwidth(64)) fpmultiplier_15 (.a(fpmultiplier_14_out), .b(fpadder_1_out), .out(fpmultiplier_15_out));
  FPMultiplier #(.fpwidth(64)) fpmultiplier_16 (.a(fpmultiplier_15_out), .b(fpadder_1_out), .out(fpmultiplier_16_out));
  FPMultiplier #(.fpwidth(64)) fpmultiplier_17 (.a(fpmultiplier_16_out), .b(fpadder_1_out), .out(fpmultiplier_17_out));
  FPMultiplier #(.fpwidth(64)) fpmultiplier_18 (.a(fpmultiplier_17_out), .b(fpadder_1_out), .out(fpmultiplier_18_out));
  FPMultiplier #(.fpwidth(64)) fpmultiplier_19 (.a(fpmultiplier_18_out), .b(fpadder_1_out), .out(fpmultiplier_19_out));
  FPMultiplier #(.fpwidth(64)) fpmultiplier_20 (.a(fpmultiplier_19_out), .b(fpadder_1_out), .out(fpmultiplier_20_out));
  FPMultiplier #(.fpwidth(64)) fpmultiplier_21 (.a(fpmultiplier_20_out), .b(fpadder_1_out), .out(fpmultiplier_21_out));
  FPMultiplier #(.fpwidth(64)) fpmultiplier_22 (.a(fpmultiplier_21_out), .b(fpadder_1_out), .out(fpmultiplier_22_out));
  FPMultiplier #(.fpwidth(64)) fpmultiplier_23 (.a(fpmultiplier_22_out), .b(fpadder_1_out), .out(fpmultiplier_23_out));
  FPMultiplier #(.fpwidth(64)) fpmultiplier_24 (.a(fpmultiplier_23_out), .b(fpadder_1_out), .out(fpmultiplier_24_out));
  // FPLogarithm #(.fpwidth(64), .mode("log")) fplogarithm_1: pin names not known; wires that end beside it: inval1, fplogarithm_1_p2
  FPMultiplier #(.fpwidth(64)) fpmultiplier_25 (
    .a(fpmultiplier_2_out), .b(64'hbfe0000000000000), .out(fpmultiplier_25_out));
  FPAdder #(.fpwidth(64)) fpadder_2 (.a(fpadder_1_out), .b(fpmultiplier_25_out), .out(fpadder_2_out));
  FPMultiplier #(.fpwidth(64)) fpmultiplier_26 (
    .a(fpmultiplier_3_out), .b(64'h3fd5555555555555), .out(fpmultiplier_26_out));
  FPAdder #(.fpwidth(64)) fpadder_3 (.a(fpadder_2_out), .b(fpmultiplier_26_out), .out(fpadder_3_out));
  FPMultiplier #(.fpwidth(64)) fpmultiplier_27 (
    .a(fpmultiplier_4_out), .b(64'hbfd0000000000000), .out(fpmultiplier_27_out));
  FPAdder #(.fpwidth(64)) fpadder_4 (.a(fpadder_3_out), .b(fpmultiplier_27_out), .out(fpadder_4_out));
  FPMultiplier #(.fpwidth(64)) fpmultiplier_28 (
    .a(fpmultiplier_5_out), .b(64'h3fc999999999999a), .out(fpmultiplier_28_out));
  FPAdder #(.fpwidth(64)) fpadder_5 (.a(fpadder_4_out), .b(fpmultiplier_28_out), .out(fpadder_5_out));
  FPMultiplier #(.fpwidth(64)) fpmultiplier_29 (
    .a(fpmultiplier_6_out), .b(64'hbfc5555555555555), .out(fpmultiplier_29_out));
  FPAdder #(.fpwidth(64)) fpadder_6 (.a(fpadder_5_out), .b(fpmultiplier_29_out), .out(fpadder_6_out));
  FPMultiplier #(.fpwidth(64)) fpmultiplier_30 (
    .a(fpmultiplier_7_out), .b(64'h3fc2492492492492), .out(fpmultiplier_30_out));
  FPAdder #(.fpwidth(64)) fpadder_7 (.a(fpadder_6_out), .b(fpmultiplier_30_out), .out(fpadder_7_out));
  FPMultiplier #(.fpwidth(64)) fpmultiplier_31 (
    .a(fpmultiplier_8_out), .b(64'hbfc0000000000000), .out(fpmultiplier_31_out));
  FPAdder #(.fpwidth(64)) fpadder_8 (.a(fpadder_7_out), .b(fpmultiplier_31_out), .out(fpadder_8_out));
  FPMultiplier #(.fpwidth(64)) fpmultiplier_32 (
    .a(fpmultiplier_9_out), .b(64'h3fbc71c71c71c71c), .out(fpmultiplier_32_out));
  FPAdder #(.fpwidth(64)) fpadder_9 (.a(fpadder_8_out), .b(fpmultiplier_32_out), .out(fpadder_9_out));
  FPMultiplier #(.fpwidth(64)) fpmultiplier_33 (
    .a(fpmultiplier_10_out), .b(64'hbfb999999999999a), .out(fpmultiplier_33_out));
  FPAdder #(.fpwidth(64)) fpadder_10 (.a(fpadder_9_out), .b(fpmultiplier_33_out), .out(fpadder_10_out));
  FPMultiplier #(.fpwidth(64)) fpmultiplier_34 (
    .a(fpmultiplier_11_out), .b(64'h3fb745d1745d1746), .out(fpmultiplier_34_out));
  FPAdder #(.fpwidth(64)) fpadder_11 (.a(fpadder_10_out), .b(fpmultiplier_34_out), .out(fpadder_11_out));
  FPMultiplier #(.fpwidth(64)) fpmultiplier_35 (
    .a(fpmultiplier_12_out), .b(64'hbfb5555555555555), .out(fpmultiplier_35_out));
  FPAdder #(.fpwidth(64)) fpadder_12 (.a(fpadder_11_out), .b(fpmultiplier_35_out), .out(fpadder_12_out));
  FPMultiplier #(.fpwidth(64)) fpmultiplier_36 (
    .a(fpmultiplier_13_out), .b(64'h3fb3b13b13b13b14), .out(fpmultiplier_36_out));
  FPAdder #(.fpwidth(64)) fpadder_13 (.a(fpadder_12_out), .b(fpmultiplier_36_out), .out(fpadder_13_out));
  FPMultiplier #(.fpwidth(64)) fpmultiplier_37 (
    .a(fpmultiplier_14_out), .b(64'hbfb2492492492492), .out(fpmultiplier_37_out));
  FPAdder #(.fpwidth(64)) fpadder_14 (.a(fpadder_13_out), .b(fpmultiplier_37_out), .out(fpadder_14_out));
  FPMultiplier #(.fpwidth(64)) fpmultiplier_38 (
    .a(fpmultiplier_15_out), .b(64'h3fb1111111111111), .out(fpmultiplier_38_out));
  FPAdder #(.fpwidth(64)) fpadder_15 (.a(fpadder_14_out), .b(fpmultiplier_38_out), .out(fpadder_15_out));
  FPMultiplier #(.fpwidth(64)) fpmultiplier_39 (
    .a(fpmultiplier_16_out), .b(64'hbfb0000000000000), .out(fpmultiplier_39_out));
  FPAdder #(.fpwidth(64)) fpadder_16 (.a(fpadder_15_out), .b(fpmultiplier_39_out), .out(fpadder_16_out));
  FPMultiplier #(.fpwidth(64)) fpmultiplier_40 (
    .a(fpmultiplier_17_out), .b(64'h3fae1e1e1e1e1e1e), .out(fpmultiplier_40_out));
  FPAdder #(.fpwidth(64)) fpadder_17 (.a(fpadder_16_out), .b(fpmultiplier_40_out), .out(fpadder_17_out));
  FPMultiplier #(.fpwidth(64)) fpmultiplier_41 (
    .a(fpmultiplier_18_out), .b(64'hbfac71c71c71c71c), .out(fpmultiplier_41_out));
  FPAdder #(.fpwidth(64)) fpadder_18 (.a(fpadder_17_out), .b(fpmultiplier_41_out), .out(fpadder_18_out));
  FPMultiplier #(.fpwidth(64)) fpmultiplier_42 (
    .a(fpmultiplier_19_out), .b(64'h3faaf286bca1af28), .out(fpmultiplier_42_out));
  FPAdder #(.fpwidth(64)) fpadder_19 (.a(fpadder_18_out), .b(fpmultiplier_42_out), .out(fpadder_19_out));
  FPMultiplier #(.fpwidth(64)) fpmultiplier_43 (
    .a(fpmultiplier_20_out), .b(64'hbfa999999999999a), .out(fpmultiplier_43_out));
  FPAdder #(.fpwidth(64)) fpadder_20 (.a(fpadder_19_out), .b(fpmultiplier_43_out), .out(fpadder_20_out));
  FPMultiplier #(.fpwidth(64)) fpmultiplier_44 (
    .a(fpmultiplier_21_out), .b(64'h3fa8618618618618), .out(fpmultiplier_44_out));
  FPAdder #(.fpwidth(64)) fpadder_21 (.a(fpadder_20_out), .b(fpmultiplier_44_out), .out(fpadder_21_out));
  FPMultiplier #(.fpwidth(64)) fpmultiplier_45 (
    .a(fpmultiplier_22_out), .b(64'hbfa745d1745d1746), .out(fpmultiplier_45_out));
  FPAdder #(.fpwidth(64)) fpadder_22 (.a(fpadder_21_out), .b(fpmultiplier_45_out), .out(fpadder_22_out));
  FPMultiplier #(.fpwidth(64)) fpmultiplier_46 (
    .a(fpmultiplier_23_out), .b(64'h3fa642c8590b2164), .out(fpmultiplier_46_out));
  FPAdder #(.fpwidth(64)) fpadder_23 (.a(fpadder_22_out), .b(fpmultiplier_46_out), .out(fpadder_23_out));
  FPMultiplier #(.fpwidth(64)) fpmultiplier_47 (
    .a(fpmultiplier_24_out), .b(64'hbfa5555555555555), .out(fpmultiplier_47_out));
  FPAdder #(.fpwidth(64)) fpadder_24 (.a(fpadder_23_out), .b(fpmultiplier_47_out), .out(fpadder_24_out));
  FPAdder #(.fpwidth(64)) fpadder_25 (.a(fpmultiplier_1_out), .b(fpadder_24_out), .out(outval1));
  // Probe on fplogarithm_1_p2
  // Probe on outval1

  // Notes on the sheet:
  //   inval1: initial=0x40a84599e363b2d9
endmodule
