// Logisim project microfpgamux.circ as structural Verilog: 4 circuits, main circuit circuittest
module muxalu (
  input  [63:0] input1,
  input  [63:0] input2,
  input  [63:0] extarg1,
  input  [63:0] extarg2,
  input  isdirectval1,
  input  [4:0] opcode1,
  input  [63:0] initval1,
  output [63:0] output1,
  output [63:0] outputpins1,
  output [63:0] outputpins2
);

  wire clock_1_out, clock_2_out, clock_3_out, comparator_1_eq, comparator_2_gt, comparator_3_eq,
       fpcomparator_1_p3, fpcomparator_2_p5, register_1_q;
  wire [5:0] bitselector_2_out, bitselector_3_out, bitselector_4_out, bitselector_5_out, bitselector_6_out;
  wire [15:0] bitselector_1_out;
  wire [63:0] adder_1_out, and_1_out, and_2_out, and_3_out, buffer_1_out, demultiplexer_1_out0,
       demultiplexer_1_out1, demultiplexer_1_out2, demultiplexer_1_out3, demultiplexer_1_out4,
       demultiplexer_1_out5, demultiplexer_1_out6, demultiplexer_1_out7, demultiplexer_1_out8,
       demultiplexer_1_out9, demultiplexer_1_out10, demultiplexer_1_out11, demultiplexer_1_out12,
       demultiplexer_1_out13, demultiplexer_1_out14, demultiplexer_1_out15, demultiplexer_1_out16,
       demultiplexer_1_out17, demultiplexer_1_out18, demultiplexer_1_out19, demultiplexer_1_out20,
       demultiplexer_1_out21, demultiplexer_1_out22, demultiplexer_1_out23, demultiplexer_1_out24,
       demultiplexer_1_out25, demultiplexer_1_out26, demultiplexer_1_out27, demultiplexer_1_out28,
       demultiplexer_1_out29, demultiplexer_1_out31, demultiplexer_2_out0, demultiplexer_2_out1,
       demultiplexer_2_out2, demultiplexer_2_out3, demultiplexer_2_out4, demultiplexer_2_out5,
       demultiplexer_2_out6, demultiplexer_2_out7, demultiplexer_2_out8, demultiplexer_2_out9,
       demultiplexer_2_out10, demultiplexer_2_out11, demultiplexer_2_out12, demultiplexer_2_out13,
       demultiplexer_2_out14, demultiplexer_2_out15, demultiplexer_2_out16, demultiplexer_2_out17,
       demultiplexer_2_out18, demultiplexer_2_out19, demultiplexer_2_out20, demultiplexer_2_out21,
       demultiplexer_2_out22, demultiplexer_2_out23, demultiplexer_2_out24, demultiplexer_2_out25,
       demultiplexer_2_out26, demultiplexer_2_out27, demultiplexer_2_out28, demultiplexer_2_out29,
       demultiplexer_2_out31, divider_1_out, fpadder_1_out, fpdivider_1_out, fpmultiplier_1_out,
       fpnegator_1_p3, fpsubtractor_1_out, fptoint_1_p3, inttofp_1_p6, multiplexer_1_out, multiplexer_2_out,
       multiplexer_3_out, multiplexer_4_out, multiplexer_5_out, multiplexer_6_out, multiplexer_7_out,
       multiplexer_8_out, multiplexer_9_out, multiplier_1_out, nand_1_out, negator_1_out, nor_1_out,
       not_1_out, not_2_out, or_1_out, ram_1_dout, random_1_out, shifter_1_out, shifter_2_out, shifter_3_out,
       shifter_4_out, shifter_5_out, subtractor_1_out, xnor_1_out, xor_1_out;

  Multiplexer #(.width(64)) multiplexer_1 (.in0(input1), .in1(extarg1), .out(multiplexer_1_out), .sel(isdirectval1));
  Demultiplexer #(.select(5), .width(64)) demultiplexer_1 (
    .out0(demultiplexer_1_out0), .out1(demultiplexer_1_out1), .out2(demultiplexer_1_out2),
    .out3(demultiplexer_1_out3), .out4(demultiplexer_1_out4), .out5(demultiplexer_1_out5),
    .out6(demultiplexer_1_out6), .out7(demultiplexer_1_out7), .out8(demultiplexer_1_out8),
    .out9(demultiplexer_1_out9), .out10(demultiplexer_1_out10), .out11(demultiplexer_1_out11),
    .out12(demultiplexer_1_out12), .out13(demultiplexer_1_out13), .out14(demultiplexer_1_out14),
    .out15(demultiplexer_1_out15), .out16(demultiplexer_1_out16), .out17(demultiplexer_1_out17),
    .out18(demultiplexer_1_out18), .out19(demultiplexer_1_out19), .out20(demultiplexer_1_out20),
    .out21(demultiplexer_1_out21), .out22(demultiplexer_1_out22), .out23(demultiplexer_1_out23),
    .out24(demultiplexer_1_out24), .out25(demultiplexer_1_out25), .out26(demultiplexer_1_out26),
    .out27(demultiplexer_1_out27), .out28(demultiplexer_1_out28), .out29(demultiplexer_1_out29),
    .out30(outputpins1), .out31(demultiplexer_1_out31), .in(multiplexer_1_out), .sel(opcode1));
  Multiplexer #(.width(64)) multiplexer_2 (.in0(input2), .in1(extarg2), .out(multiplexer_2_out), .sel(isdirectval1));
  Demultiplexer #(.select(5), .width(64)) demultiplexer_2 (
    .out0(demultiplexer_2_out0), .out1(demultiplexer_2_out1), .out2(demultiplexer_2_out2),
    .out3(demultiplexer_2_out3), .out4(demultiplexer_2_out4), .out5(demultiplexer_2_out5),
    .out6(demultiplexer_2_out6), .out7(demultiplexer_2_out7), .out8(demultiplexer_2_out8),
    .out9(demultiplexer_2_out9), .out10(demultiplexer_2_out10), .out11(demultiplexer_2_out11),
    .out12(demultiplexer_2_out12), .out13(demultiplexer_2_out13), .out14(demultiplexer_2_out14),
    .out15(demultiplexer_2_out15), .out16(demultiplexer_2_out16), .out17(demultiplexer_2_out17),
    .out18(demultiplexer_2_out18), .out19(demultiplexer_2_out19), .out20(demultiplexer_2_out20),
    .out21(demultiplexer_2_out21), .out22(demultiplexer_2_out22), .out23(demultiplexer_2_out23),
    .out24(demultiplexer_2_out24), .out25(demultiplexer_2_out25), .out26(demultiplexer_2_out26),
    .out27(demultiplexer_2_out27), .out28(demultiplexer_2_out28), .out29(demultiplexer_2_out29),
    .out30(outputpins2), .out31(demultiplexer_2_out31), .in(multiplexer_2_out), .sel(opcode1));
  assign not_1_out = ~64'h8000000000000000;  // NOT_Gate not_1, 64 bits wide
  assign and_1_out = demultiplexer_2_out31 & 64'h8000000000000000;  // AND_Gate and_1, 64 bits wide
  Multiplexer #(.width(64)) multiplexer_3 (
    .in0(demultiplexer_2_out31), .in1(and_2_out), .out(multiplexer_3_out), .sel(comparator_1_eq));
  assign and_2_out = demultiplexer_2_out31 & not_1_out;  // AND_Gate and_2, 64 bits wide
  Comparator #(.width(64)) comparator_1 (
    .a(and_1_out), .b(64'h8000000000000000), .eq(comparator_1_eq));  // open: gt, lt
  BitSelector #(.group(16), .width(64)) bitselector_1 (.in(multiplexer_3_out), .out(bitselector_1_out), .sel(2'b00));
  RAM #(.addrWidth(16), .dataWidth(64), .enables("line"), .trigger("falling")) ram_1 (
    .addr(bitselector_1_out), .we(comparator_1_eq), .clk(clock_1_out), .din(demultiplexer_1_out31),
    .dout(ram_1_dout));
  Clock clock_1 (.out(clock_1_out));
  Comparator #(.width(64)) comparator_2 (
    .a(demultiplexer_1_out25), .b(demultiplexer_2_out25), .gt(comparator_2_gt));  // open: eq, lt
  Comparator #(.width(64)) comparator_3 (
    .a(demultiplexer_1_out26), .b(demultiplexer_2_out26), .eq(comparator_3_eq));  // open: gt, lt
  // FPComparator #(.fpwidth(64)) fpcomparator_1: pin names not known; wires that end beside it: demultiplexer_1_out27, demultiplexer_2_out27, fpcomparator_1_p3
  // FPComparator #(.fpwidth(64)) fpcomparator_2: pin names not known; wires that end beside it: demultiplexer_1_out28, demultiplexer_2_out28, demultiplexer_1_out29, demultiplexer_2_out29, fpcomparator_2_p5
  Random #(.seed(69420), .trigger("falling"), .width(64)) random_1 (
    .clk(clock_2_out), .out(random_1_out));  // open: clr, next
  Clock clock_2 (.out(clock_2_out));
  FPAdder #(.fpwidth(64)) fpadder_1 (.a(demultiplexer_1_out0), .b(demultiplexer_2_out0), .out(fpadder_1_out));
  FPSubtractor #(.fpwidth(64)) fpsubtractor_1 (
    .a(demultiplexer_1_out1), .b(demultiplexer_2_out1), .out(fpsubtractor_1_out));
  FPMultiplier #(.fpwidth(64)) fpmultiplier_1 (
    .a(demultiplexer_1_out2), .b(demultiplexer_2_out2), .out(fpmultiplier_1_out));
  FPDivider #(.fpwidth(64)) fpdivider_1 (.a(demultiplexer_1_out3), .b(demultiplexer_2_out3), .out(fpdivider_1_out));
  // FPNegator #(.fpwidth(64)) fpnegator_1: pin names not known; wires that end beside it: demultiplexer_2_out4, demultiplexer_1_out4, fpnegator_1_p3
  // FPToInt #(.fpwidth(64), .width(64)) fptoint_1: pin names not known; wires that end beside it: demultiplexer_2_out5, demultiplexer_1_out5, fptoint_1_p3
  Adder #(.width(64)) adder_1 (
    .a(demultiplexer_1_out6), .b(demultiplexer_2_out6), .out(adder_1_out));  // open: cin, cout
  Subtractor #(.width(64)) subtractor_1 (
    .a(demultiplexer_1_out7), .b(demultiplexer_2_out7), .out(subtractor_1_out));  // open: bin, bout
  Multiplier #(.mode("twosComplement"), .width(64)) multiplier_1 (
    .a(demultiplexer_1_out8), .b(demultiplexer_2_out8), .out(multiplier_1_out));  // open: cin, cout
  Divider #(.mode("twosComplement"), .width(64)) divider_1 (
    .a(demultiplexer_1_out9), .b(demultiplexer_2_out9), .out(divider_1_out));  // open: upper, rem
  Negator #(.width(64)) negator_1 (.in(demultiplexer_1_out10), .out(negator_1_out));
  // IntToFP #(.fpwidth(64), .width(64)) inttofp_1: pin names not known; wires that end beside it: demultiplexer_2_out10, demultiplexer_2_out11, demultiplexer_2_out12, demultiplexer_2_out13, demultiplexer_1_out11, inttofp_1_p6
  assign buffer_1_out = demultiplexer_1_out12;  // Buffer buffer_1, 64 bits wide
  assign not_2_out = ~demultiplexer_1_out13;  // NOT_Gate not_2, 64 bits wide
  assign and_3_out = demultiplexer_1_out14 & demultiplexer_2_out14;  // AND_Gate and_3, 64 bits wide
  assign or_1_out = demultiplexer_1_out15 | demultiplexer_2_out15;  // OR_Gate or_1, 64 bits wide
  assign xor_1_out = demultiplexer_1_out16 ^ demultiplexer_2_out16;  // XOR_Gate xor_1, 64 bits wide
  assign nand_1_out = ~(demultiplexer_1_out17 & demultiplexer_2_out17);  // NAND_Gate nand_1, 64 bits wide
  assign nor_1_out = ~(demultiplexer_1_out18 | demultiplexer_2_out18);  // NOR_Gate nor_1, 64 bits wide
  assign xnor_1_out = ~(demultiplexer_1_out19 ^ demultiplexer_2_out19);  // XNOR_Gate xnor_1, 64 bits wide
  Shifter #(.width(64)) shifter_1 (.in(demultiplexer_1_out20), .\dist (bitselector_2_out), .out(shifter_1_out));
  BitSelector #(.group(6), .width(64)) bitselector_2 (
    .in(demultiplexer_2_out20), .out(bitselector_2_out), .sel(4'b0000));
  Shifter #(.shift("lr"), .width(64)) shifter_2 (
    .in(demultiplexer_1_out21), .\dist (bitselector_3_out), .out(shifter_2_out));
  BitSelector #(.group(6), .width(64)) bitselector_3 (
    .in(demultiplexer_2_out21), .out(bitselector_3_out), .sel(4'b0000));
  Shifter #(.shift("ar"), .width(64)) shifter_3 (
    .in(demultiplexer_1_out22), .\dist (bitselector_4_out), .out(shifter_3_out));
  BitSelector #(.group(6), .width(64)) bitselector_4 (
    .in(demultiplexer_2_out22), .out(bitselector_4_out), .sel(4'b0000));
  Shifter #(.shift("rl"), .width(64)) shifter_4 (
    .in(demultiplexer_1_out23), .\dist (bitselector_5_out), .out(shifter_4_out));
  BitSelector #(.group(6), .width(64)) bitselector_5 (
    .in(demultiplexer_2_out23), .out(bitselector_5_out), .sel(4'b0000));
  Shifter #(.shift("rr"), .width(64)) shifter_5 (
    .in(demultiplexer_1_out24), .\dist (bitselector_6_out), .out(shifter_5_out));
  BitSelector #(.group(6), .width(64)) bitselector_6 (
    .in(demultiplexer_2_out24), .out(bitselector_6_out), .sel(4'b0000));
  Multiplexer #(.width(64)) multiplexer_4 (
    .in0({64{1'b0}}), .in1(64'h1), .out(multiplexer_4_out), .sel(comparator_2_gt));
  Multiplexer #(.width(64)) multiplexer_5 (
    .in0({64{1'b0}}), .in1(64'h1), .out(multiplexer_5_out), .sel(comparator_3_eq));
  Multiplexer #(.width(64)) multiplexer_6 (
    .in0({64{1'b0}}), .in1(64'h1), .out(multiplexer_6_out), .sel(fpcomparator_1_p3));
  Multiplexer #(.width(64)) multiplexer_7 (
    .in0({64{1'b0}}), .in1(64'h1), .out(multiplexer_7_out), .sel(fpcomparator_2_p5));
  Multiplexer #(.select(5), .width(64)) multiplexer_8 (
    .in0(fpadder_1_out), .in1(fpsubtractor_1_out), .in2(fpmultiplier_1_out), .in3(fpdivider_1_out),
    .in4(fpnegator_1_p3), .in5(fptoint_1_p3), .in6(adder_1_out), .in7(subtractor_1_out),
    .in8(multiplier_1_out), .in9(divider_1_out), .in10(negator_1_out), .in11(inttofp_1_p6),
    .in12(buffer_1_out), .in13(not_2_out), .in14(and_3_out), .in15(or_1_out), .in16(xor_1_out),
    .in17(nand_1_out), .in18(nor_1_out), .in19(xnor_1_out), .in20(shifter_1_out), .in21(shifter_2_out),
    .in22(shifter_3_out), .in23(shifter_4_out), .in24(shifter_5_out), .in25(multiplexer_4_out),
    .in26(multiplexer_5_out), .in27(multiplexer_6_out), .in28(multiplexer_7_out), .in29(random_1_out),
    .in30(extarg1), .in31(ram_1_dout), .out(multiplexer_8_out), .sel(opcode1));
  Register #(.width(1)) register_1 (.D(1'b1), .clk(clock_3_out), .Q(register_1_q));  // open: en, clr
  Clock clock_3 (.out(clock_3_out));
  Register #(.width(64)) register_2 (.D(multiplexer_9_out), .clk(clock_3_out), .Q(output1));  // open: en, clr
  Multiplexer #(.width(64)) multiplexer_9 (
    .in0(initval1), .in1(multiplexer_8_out), .out(multiplexer_9_out), .sel(register_1_q));
endmodule
module muxfpga (
  input  [63:0] direct1A,
  input  [63:0] direct1B,
  input  isdirect1,
  input  [4:0] opcode1,
  input  [63:0] initval1,
  input  [63:0] direct2A,
  input  [63:0] direct2B,
  input  isdirect2,
  input  [4:0] opcode2,
  input  [63:0] initval2,
  input  [63:0] direct3A,
  input  [63:0] direct3B,
  input  isdirect3,
  input  [4:0] opcode3,
  input  [63:0] initval3,
  input  [63:0] direct4A,
  input  [63:0] direct4B,
  input  isdirect4,
  input  [4:0] opcode4,
  input  [63:0] initval4,
  input  [63:0] direct5A,
  input  [63:0] direct5B,
  input  isdirect5,
  input  [4:0] opcode5,
  input  [63:0] initval5,
  input  [63:0] direct6A,
  input  [63:0] direct6B,
  input  isdirect6,
  input  [4:0] opcode6,
  input  [63:0] initval6,
  input  [63:0] direct7A,
  input  [63:0] direct7B,
  input  isdirect7,
  input  [4:0] opcode7,
  input  [63:0] initval7,
  input  [63:0] direct8A,
  input  [63:0] direct8B,
  input  isdirect8,
  input  [4:0] opcode8,
  input  [63:0] initval8,
  input  [63:0] direct9A,
  input  [63:0] direct9B,
  input  isdirect9,
  input  [4:0] opcode9,
  input  [63:0] initval9,
  input  [63:0] direct10A,
  input  [63:0] direct10B,
  input  isdirect10,
  input  [4:0] opcode10,
  input  [63:0] initval10,
  input  [63:0] direct11A,
  input  [63:0] direct11B,
  input  isdirect11,
  input  [4:0] opcode11,
  input  [63:0] initval11,
  input  [63:0] direct12A,
  input  [63:0] direct12B,
  input  isdirect12,
  input  [4:0] opcode12,
  input  [63:0] initval12,
  input  [63:0] direct13A,
  input  [63:0] direct13B,
  input  isdirect13,
  input  [4:0] opcode13,
  input  [63:0] initval13,
  input  [63:0] direct14A,
  input  [63:0] direct14B,
  input  isdirect14,
  input  [4:0] opcode14,
  input  [63:0] initval14,
  input  [63:0] direct15A,
  input  [63:0] direct15B,
  input  isdirect15,
  input  [4:0] opcode15,
  input  [63:0] initval15,
  input  [63:0] direct16A,
  input  [63:0] direct16B,
  input  isdirect16,
  input  [4:0] opcode16,
  input  [63:0] initval16,
  input  [63:0] direct17A,
  input  [63:0] direct17B,
  input  isdirect17,
  input  [4:0] opcode17,
  input  [63:0] initval17,
  input  [63:0] direct18A,
  input  [63:0] direct18B,
  input  isdirect18,
  input  [4:0] opcode18,
  input  [63:0] initval18,
  input  [63:0] direct19A,
  input  [63:0] direct19B,
  input  isdirect19,
  input  [4:0] opcode19,
  input  [63:0] initval19,
  input  [63:0] direct20A,
  input  [63:0] direct20B,
  input  isdirect20,
  input  [4:0] opcode20,
  input  [63:0] initval20,
  input  [63:0] direct21A,
  input  [63:0] direct21B,
  input  isdirect21,
  input  [4:0] opcode21,
  input  [63:0] initval21,
  input  [63:0] direct22A,
  input  [63:0] direct22B,
  input  isdirect22,
  input  [4:0] opcode22,
  input  [63:0] initval22,
  input  [63:0] direct23A,
  input  [63:0] direct23B,
  input  isdirect23,
  input  [4:0] opcode23,
  input  [63:0] initval23,
  input  [63:0] direct24A,
  input  [63:0] direct24B,
  input  isdirect24,
  input  [4:0] opcode24,
  input  [63:0] initval24,
  input  [63:0] direct25A,
  input  [63:0] direct25B,
  input  isdirect25,
  input  [4:0] opcode25,
  input  [63:0] initval25,
  input  [63:0] direct26A,
  input  [63:0] direct26B,
  input  isdirect26,
  input  [4:0] opcode26,
  input  [63:0] initval26,
  input  [63:0] direct27A,
  input  [63:0] direct27B,
  input  isdirect27,
  input  [4:0] opcode27,
  input  [63:0] initval27,
  input  [63:0] direct28A,
  input  [63:0] direct28B,
  input  isdirect28,
  input  [4:0] opcode28,
  input  [63:0] initval28,
  input  [63:0] direct29A,
  input  [63:0] direct29B,
  input  isdirect29,
  input  [4:0] opcode29,
  input  [63:0] initval29,
  input  [63:0] direct30A,
  input  [63:0] direct30B,
  input  isdirect30,
  input  [4:0] opcode30,
  input  [63:0] initval30,
  input  [63:0] direct31A,
  input  [63:0] direct31B,
  input  isdirect31,
  input  [4:0] opcode31,
  input  [63:0] initval31,
  input  [63:0] direct32A,
  input  [63:0] direct32B,
  input  isdirect32,
  input  [4:0] opcode32,
  input  [63:0] initval32,
  input  [63:0] direct33A,
  input  [63:0] direct33B,
  input  isdirect33,
  input  [4:0] opcode33,
  input  [63:0] initval33,
  input  [63:0] direct34A,
  input  [63:0] direct34B,
  input  isdirect34,
  input  [4:0] opcode34,
  input  [63:0] initval34,
  input  [63:0] direct35A,
  input  [63:0] direct35B,
  input  isdirect35,
  input  [4:0] opcode35,
  input  [63:0] initval35,
  input  [63:0] direct36A,
  input  [63:0] direct36B,
  input  isdirect36,
  input  [4:0] opcode36,
  input  [63:0] initval36,
  input  [63:0] direct37A,
  input  [63:0] direct37B,
  input  isdirect37,
  input  [4:0] opcode37,
  input  [63:0] initval37,
  input  [63:0] direct38A,
  input  [63:0] direct38B,
  input  isdirect38,
  input  [4:0] opcode38,
  input  [63:0] initval38,
  input  [63:0] direct39A,
  input  [63:0] direct39B,
  input  isdirect39,
  input  [4:0] opcode39,
  input  [63:0] initval39,
  input  [63:0] direct40A,
  input  [63:0] direct40B,
  input  isdirect40,
  input  [4:0] opcode40,
  input  [63:0] initval40,
  input  [63:0] direct41A,
  input  [63:0] direct41B,
  input  isdirect41,
  input  [4:0] opcode41,
  input  [63:0] initval41,
  input  [63:0] direct42A,
  input  [63:0] direct42B,
  input  isdirect42,
  input  [4:0] opcode42,
  input  [63:0] initval42,
  input  [63:0] direct43A,
  input  [63:0] direct43B,
  input  isdirect43,
  input  [4:0] opcode43,
  input  [63:0] initval43,
  input  [63:0] direct44A,
  input  [63:0] direct44B,
  input  isdirect44,
  input  [4:0] opcode44,
  input  [63:0] initval44,
  input  [63:0] direct45A,
  input  [63:0] direct45B,
  input  isdirect45,
  input  [4:0] opcode45,
  input  [63:0] initval45,
  input  [63:0] direct46A,
  input  [63:0] direct46B,
  input  isdirect46,
  input  [4:0] opcode46,
  input  [63:0] initval46,
  input  [63:0] direct47A,
  input  [63:0] direct47B,
  input  isdirect47,
  input  [4:0] opcode47,
  input  [63:0] initval47,
  input  [63:0] direct48A,
  input  [63:0] direct48B,
  input  isdirect48,
  input  [4:0] opcode48,
  input  [63:0] initval48,
  input  [63:0] direct49A,
  input  [63:0] direct49B,
  input  isdirect49,
  input  [4:0] opcode49,
  input  [63:0] initval49,
  input  [63:0] direct50A,
  input  [63:0] direct50B,
  input  isdirect50,
  input  [4:0] opcode50,
  input  [63:0] initval50,
  input  [63:0] direct51A,
  input  [63:0] direct51B,
  input  isdirect51,
  input  [4:0] opcode51,
  input  [63:0] initval51,
  input  [63:0] direct52A,
  input  [63:0] direct52B,
  input  isdirect52,
  input  [4:0] opcode52,
  input  [63:0] initval52,
  input  [63:0] direct53A,
  input  [63:0] direct53B,
  input  isdirect53,
  input  [4:0] opcode53,
  input  [63:0] initval53,
  input  [63:0] direct54A,
  input  [63:0] direct54B,
  input  isdirect54,
  input  [4:0] opcode54,
  input  [63:0] initval54,
  input  [63:0] direct55A,
  input  [63:0] direct55B,
  input  isdirect55,
  input  [4:0] opcode55,
  input  [63:0] initval55,
  input  [63:0] direct56A,
  input  [63:0] direct56B,
  input  isdirect56,
  input  [4:0] opcode56,
  input  [63:0] initval56,
  input  [63:0] direct57A,
  input  [63:0] direct57B,
  input  isdirect57,
  input  [4:0] opcode57,
  input  [63:0] initval57,
  input  [63:0] direct58A,
  input  [63:0] direct58B,
  input  isdirect58,
  input  [4:0] opcode58,
  input  [63:0] initval58,
  input  [63:0] direct59A,
  input  [63:0] direct59B,
  input  isdirect59,
  input  [4:0] opcode59,
  input  [63:0] initval59,
  input  [63:0] direct60A,
  input  [63:0] direct60B,
  input  isdirect60,
  input  [4:0] opcode60,
  input  [63:0] initval60,
  input  [63:0] direct61A,
  input  [63:0] direct61B,
  input  isdirect61,
  input  [4:0] opcode61,
  input  [63:0] initval61,
  input  [63:0] direct62A,
  input  [63:0] direct62B,
  input  isdirect62,
  input  [4:0] opcode62,
  input  [63:0] initval62,
  input  [63:0] direct63A,
  input  [63:0] direct63B,
  input  isdirect63,
  input  [4:0] opcode63,
  input  [63:0] initval63,
  input  [63:0] direct64A,
  input  [63:0] direct64B,
  input  isdirect64,
  input  [4:0] opcode64,
  input  [63:0] initval64,
  output [63:0] argval1A,
  output [63:0] argval1B,
  output [63:0] gateval1,
  output [63:0] outpins1A,
  output [63:0] outpins1B,
  output [63:0] argval2A,
  output [63:0] argval2B,
  output [63:0] gateval2,
  output [63:0] outpins2A,
  output [63:0] outpins2B,
  output [63:0] argval3A,
  output [63:0] argval3B,
  output [63:0] gateval3,
  output [63:0] outpins3A,
  output [63:0] outpins3B,
  output [63:0] argval4A,
  output [63:0] argval4B,
  output [63:0] gateval4,
  output [63:0] outpins4A,
  output [63:0] outpins4B,
  output [63:0] argval5A,
  output [63:0] argval5B,
  output [63:0] gateval5,
  output [63:0] outpins5A,
  output [63:0] outpins5B,
  output [63:0] argval6A,
  output [63:0] argval6B,
  output [63:0] gateval6,
  output [63:0] outpins6A,
  output [63:0] outpins6B,
  output [63:0] argval7A,
  output [63:0] argval7B,
  output [63:0] gateval7,
  output [63:0] outpins7A,
  output [63:0] outpins7B,
  output [63:0] argval8A,
  output [63:0] argval8B,
  output [63:0] gateval8,
  output [63:0] outpins8A,
  output [63:0] outpins8B,
  output [63:0] argval9A,
  output [63:0] argval9B,
  output [63:0] gateval9,
  output [63:0] outpins9A,
  output [63:0] outpins9B,
  output [63:0] argval10A,
  output [63:0] argval10B,
  output [63:0] gateval10,
  output [63:0] outpins10A,
  output [63:0] outpins10B,
  output [63:0] argval11A,
  output [63:0] argval11B,
  output [63:0] gateval11,
  output [63:0] outpins11A,
  output [63:0] outpins11B,
  output [63:0] argval12A,
  output [63:0] argval12B,
  output [63:0] gateval12,
  output [63:0] outpins12A,
  output [63:0] outpins12B,
  output [63:0] argval13A,
  output [63:0] argval13B,
  output [63:0] gateval13,
  output [63:0] outpins13A,
  output [63:0] outpins13B,
  output [63:0] argval14A,
  output [63:0] argval14B,
  output [63:0] gateval14,
  output [63:0] outpins14A,
  output [63:0] outpins14B,
  output [63:0] argval15A,
  output [63:0] argval15B,
  output [63:0] gateval15,
  output [63:0] outpins15A,
  output [63:0] outpins15B,
  output [63:0] argval16A,
  output [63:0] argval16B,
  output [63:0] gateval16,
  output [63:0] outpins16A,
  output [63:0] outpins16B,
  output [63:0] argval17A,
  output [63:0] argval17B,
  output [63:0] gateval17,
  output [63:0] outpins17A,
  output [63:0] outpins17B,
  output [63:0] argval18A,
  output [63:0] argval18B,
  output [63:0] gateval18,
  output [63:0] outpins18A,
  output [63:0] outpins18B,
  output [63:0] argval19A,
  output [63:0] argval19B,
  output [63:0] gateval19,
  output [63:0] outpins19A,
  output [63:0] outpins19B,
  output [63:0] argval20A,
  output [63:0] argval20B,
  output [63:0] gateval20,
  output [63:0] outpins20A,
  output [63:0] outpins20B,
  output [63:0] argval21A,
  output [63:0] argval21B,
  output [63:0] gateval21,
  output [63:0] outpins21A,
  output [63:0] outpins21B,
  output [63:0] argval22A,
  output [63:0] argval22B,
  output [63:0] gateval22,
  output [63:0] outpins22A,
  output [63:0] outpins22B,
  output [63:0] argval23A,
  output [63:0] argval23B,
  output [63:0] gateval23,
  output [63:0] outpins23A,
  output [63:0] outpins23B,
  output [63:0] argval24A,
  output [63:0] argval24B,
  output [63:0] gateval24,
  output [63:0] outpins24A,
  output [63:0] outpins24B,
  output [63:0] argval25A,
  output [63:0] argval25B,
  output [63:0] gateval25,
  output [63:0] outpins25A,
  output [63:0] outpins25B,
  output [63:0] argval26A,
  output [63:0] argval26B,
  output [63:0] gateval26,
  output [63:0] outpins26A,
  output [63:0] outpins26B,
  output [63:0] argval27A,
  output [63:0] argval27B,
  output [63:0] gateval27,
  output [63:0] outpins27A,
  output [63:0] outpins27B,
  output [63:0] argval28A,
  output [63:0] argval28B,
  output [63:0] gateval28,
  output [63:0] outpins28A,
  output [63:0] outpins28B,
  output [63:0] argval29A,
  output [63:0] argval29B,
  output [63:0] gateval29,
  output [63:0] outpins29A,
  output [63:0] outpins29B,
  output [63:0] argval30A,
  output [63:0] argval30B,
  output [63:0] gateval30,
  output [63:0] outpins30A,
  output [63:0] outpins30B,
  output [63:0] argval31A,
  output [63:0] argval31B,
  output [63:0] gateval31,
  output [63:0] outpins31A,
  output [63:0] outpins31B,
  output [63:0] argval32A,
  output [63:0] argval32B,
  output [63:0] gateval32,
  output [63:0] outpins32A,
  output [63:0] outpins32B,
  output [63:0] argval33A,
  output [63:0] argval33B,
  output [63:0] gateval33,
  output [63:0] outpins33A,
  output [63:0] outpins33B,
  output [63:0] argval34A,
  output [63:0] argval34B,
  output [63:0] gateval34,
  output [63:0] outpins34A,
  output [63:0] outpins34B,
  output [63:0] argval35A,
  output [63:0] argval35B,
  output [63:0] gateval35,
  output [63:0] outpins35A,
  output [63:0] outpins35B,
  output [63:0] argval36A,
  output [63:0] argval36B,
  output [63:0] gateval36,
  output [63:0] outpins36A,
  output [63:0] outpins36B,
  output [63:0] argval37A,
  output [63:0] argval37B,
  output [63:0] gateval37,
  output [63:0] outpins37A,
  output [63:0] outpins37B,
  output [63:0] argval38A,
  output [63:0] argval38B,
  output [63:0] gateval38,
  output [63:0] outpins38A,
  output [63:0] outpins38B,
  output [63:0] argval39A,
  output [63:0] argval39B,
  output [63:0] gateval39,
  output [63:0] outpins39A,
  output [63:0] outpins39B,
  output [63:0] argval40A,
  output [63:0] argval40B,
  output [63:0] gateval40,
  output [63:0] outpins40A,
  output [63:0] outpins40B,
  output [63:0] argval41A,
  output [63:0] argval41B,
  output [63:0] gateval41,
  output [63:0] outpins41A,
  output [63:0] outpins41B,
  output [63:0] argval42A,
  output [63:0] argval42B,
  output [63:0] gateval42,
  output [63:0] outpins42A,
  output [63:0] outpins42B,
  output [63:0] argval43A,
  output [63:0] argval43B,
  output [63:0] gateval43,
  output [63:0] outpins43A,
  output [63:0] outpins43B,
  output [63:0] argval44A,
  output [63:0] argval44B,
  output [63:0] gateval44,
  output [63:0] outpins44A,
  output [63:0] outpins44B,
  output [63:0] argval45A,
  output [63:0] argval45B,
  output [63:0] gateval45,
  output [63:0] outpins45A,
  output [63:0] outpins45B,
  output [63:0] argval46A,
  output [63:0] argval46B,
  output [63:0] gateval46,
  output [63:0] outpins46A,
  output [63:0] outpins46B,
  output [63:0] argval47A,
  output [63:0] argval47B,
  output [63:0] gateval47,
  output [63:0] outpins47A,
  output [63:0] outpins47B,
  output [63:0] argval48A,
  output [63:0] argval48B,
  output [63:0] gateval48,
  output [63:0] outpins48A,
  output [63:0] outpins48B,
  output [63:0] argval49A,
  output [63:0] argval49B,
  output [63:0] gateval49,
  output [63:0] outpins49A,
  output [63:0] outpins49B,
  output [63:0] argval50A,
  output [63:0] argval50B,
  output [63:0] gateval50,
  output [63:0] outpins50A,
  output [63:0] outpins50B,
  output [63:0] argval51A,
  output [63:0] argval51B,
  output [63:0] gateval51,
  output [63:0] outpins51A,
  output [63:0] outpins51B,
  output [63:0] argval52A,
  output [63:0] argval52B,
  output [63:0] gateval52,
  output [63:0] outpins52A,
  output [63:0] outpins52B,
  output [63:0] argval53A,
  output [63:0] argval53B,
  output [63:0] gateval53,
  output [63:0] outpins53A,
  output [63:0] outpins53B,
  output [63:0] argval54A,
  output [63:0] argval54B,
  output [63:0] gateval54,
  output [63:0] outpins54A,
  output [63:0] outpins54B,
  output [63:0] argval55A,
  output [63:0] argval55B,
  output [63:0] gateval55,
  output [63:0] outpins55A,
  output [63:0] outpins55B,
  output [63:0] argval56A,
  output [63:0] argval56B,
  output [63:0] gateval56,
  output [63:0] outpins56A,
  output [63:0] outpins56B,
  output [63:0] argval57A,
  output [63:0] argval57B,
  output [63:0] gateval57,
  output [63:0] outpins57A,
  output [63:0] outpins57B,
  output [63:0] argval58A,
  output [63:0] argval58B,
  output [63:0] gateval58,
  output [63:0] outpins58A,
  output [63:0] outpins58B,
  output [63:0] argval59A,
  output [63:0] argval59B,
  output [63:0] gateval59,
  output [63:0] outpins59A,
  output [63:0] outpins59B,
  output [63:0] argval60A,
  output [63:0] argval60B,
  output [63:0] gateval60,
  output [63:0] outpins60A,
  output [63:0] outpins60B,
  output [63:0] argval61A,
  output [63:0] argval61B,
  output [63:0] gateval61,
  output [63:0] outpins61A,
  output [63:0] outpins61B,
  output [63:0] argval62A,
  output [63:0] argval62B,
  output [63:0] gateval62,
  output [63:0] outpins62A,
  output [63:0] outpins62B,
  output [63:0] argval63A,
  output [63:0] argval63B,
  output [63:0] gateval63,
  output [63:0] outpins63A,
  output [63:0] outpins63B,
  output [63:0] argval64A,
  output [63:0] argval64B,
  output [63:0] gateval64,
  output [63:0] outpins64A,
  output [63:0] outpins64B
);

  Clock clock_1 ();  // open: out
  muxalu muxalu_1 (
    .input1(argval1A), .input2(argval1B), .extarg1(direct1A), .extarg2(direct1B), .isdirectval1(isdirect1),
    .opcode1(opcode1), .initval1(initval1), .output1(gateval1), .outputpins1(outpins1A),
    .outputpins2(outpins1B));
  muxalu muxalu_2 (
    .input1(argval2A), .input2(argval2B), .extarg1(direct2A), .extarg2(direct2B), .isdirectval1(isdirect2),
    .opcode1(opcode2), .initval1(initval2), .output1(gateval2), .outputpins1(outpins2A),
    .outputpins2(outpins2B));
  muxalu muxalu_3 (
    .input1(argval3A), .input2(argval3B), .extarg1(direct3A), .extarg2(direct3B), .isdirectval1(isdirect3),
    .opcode1(opcode3), .initval1(initval3), .output1(gateval3), .outputpins1(outpins3A),
    .outputpins2(outpins3B));
  muxalu muxalu_4 (
    .input1(argval4A), .input2(argval4B), .extarg1(direct4A), .extarg2(direct4B), .isdirectval1(isdirect4),
    .opcode1(opcode4), .initval1(initval4), .output1(gateval4), .outputpins1(outpins4A),
    .outputpins2(outpins4B));
  muxalu muxalu_5 (
    .input1(argval5A), .input2(argval5B), .extarg1(direct5A), .extarg2(direct5B), .isdirectval1(isdirect5),
    .opcode1(opcode5), .initval1(initval5), .output1(gateval5), .outputpins1(outpins5A),
    .outputpins2(outpins5B));
  muxalu muxalu_6 (
    .input1(argval6A), .input2(argval6B), .extarg1(direct6A), .extarg2(direct6B), .isdirectval1(isdirect6),
    .opcode1(opcode6), .initval1(initval6), .output1(gateval6), .outputpins1(outpins6A),
    .outputpins2(outpins6B));
  muxalu muxalu_7 (
    .input1(argval7A), .input2(argval7B), .extarg1(direct7A), .extarg2(direct7B), .isdirectval1(isdirect7),
    .opcode1(opcode7), .initval1(initval7), .output1(gateval7), .outputpins1(outpins7A),
    .outputpins2(outpins7B));
  muxalu muxalu_8 (
    .input1(argval8A), .input2(argval8B), .extarg1(direct8A), .extarg2(direct8B), .isdirectval1(isdirect8),
    .opcode1(opcode8), .initval1(initval8), .output1(gateval8), .outputpins1(outpins8A),
    .outputpins2(outpins8B));
  muxalu muxalu_9 (
    .input1(argval9A), .input2(argval9B), .extarg1(direct9A), .extarg2(direct9B), .isdirectval1(isdirect9),
    .opcode1(opcode9), .initval1(initval9), .output1(gateval9), .outputpins1(outpins9A),
    .outputpins2(outpins9B));
  muxalu muxalu_10 (
    .input1(argval10A), .input2(argval10B), .extarg1(direct10A), .extarg2(direct10B),
    .isdirectval1(isdirect10), .opcode1(opcode10), .initval1(initval10), .output1(gateval10),
    .outputpins1(outpins10A), .outputpins2(outpins10B));
  muxalu muxalu_11 (
    .input1(argval11A), .input2(argval11B), .extarg1(direct11A), .extarg2(direct11B),
    .isdirectval1(isdirect11), .opcode1(opcode11), .initval1(initval11), .output1(gateval11),
    .outputpins1(outpins11A), .outputpins2(outpins11B));
  muxalu muxalu_12 (
    .input1(argval12A), .input2(argval12B), .extarg1(direct12A), .extarg2(direct12B),
    .isdirectval1(isdirect12), .opcode1(opcode12), .initval1(initval12), .output1(gateval12),
    .outputpins1(outpins12A), .outputpins2(outpins12B));
  muxalu muxalu_13 (
    .input1(argval13A), .input2(argval13B), .extarg1(direct13A), .extarg2(direct13B),
    .isdirectval1(isdirect13), .opcode1(opcode13), .initval1(initval13), .output1(gateval13),
    .outputpins1(outpins13A), .outputpins2(outpins13B));
  muxalu muxalu_14 (
    .input1(argval14A), .input2(argval14B), .extarg1(direct14A), .extarg2(direct14B),
    .isdirectval1(isdirect14), .opcode1(opcode14), .initval1(initval14), .output1(gateval14),
    .outputpins1(outpins14A), .outputpins2(outpins14B));
  muxalu muxalu_15 (
    .input1(argval15A), .input2(argval15B), .extarg1(direct15A), .extarg2(direct15B),
    .isdirectval1(isdirect15), .opcode1(opcode15), .initval1(initval15), .output1(gateval15),
    .outputpins1(outpins15A), .outputpins2(outpins15B));
  muxalu muxalu_16 (
    .input1(argval16A), .input2(argval16B), .extarg1(direct16A), .extarg2(direct16B),
    .isdirectval1(isdirect16), .opcode1(opcode16), .initval1(initval16), .output1(gateval16),
    .outputpins1(outpins16A), .outputpins2(outpins16B));
  muxalu muxalu_17 (
    .input1(argval17A), .input2(argval17B), .extarg1(direct17A), .extarg2(direct17B),
    .isdirectval1(isdirect17), .opcode1(opcode17), .initval1(initval17), .output1(gateval17),
    .outputpins1(outpins17A), .outputpins2(outpins17B));
  muxalu muxalu_18 (
    .input1(argval18A), .input2(argval18B), .extarg1(direct18A), .extarg2(direct18B),
    .isdirectval1(isdirect18), .opcode1(opcode18), .initval1(initval18), .output1(gateval18),
    .outputpins1(outpins18A), .outputpins2(outpins18B));
  muxalu muxalu_19 (
    .input1(argval19A), .input2(argval19B), .extarg1(direct19A), .extarg2(direct19B),
    .isdirectval1(isdirect19), .opcode1(opcode19), .initval1(initval19), .output1(gateval19),
    .outputpins1(outpins19A), .outputpins2(outpins19B));
  muxalu muxalu_20 (
    .input1(argval20A), .input2(argval20B), .extarg1(direct20A), .extarg2(direct20B),
    .isdirectval1(isdirect20), .opcode1(opcode20), .initval1(initval20), .output1(gateval20),
    .outputpins1(outpins20A), .outputpins2(outpins20B));
  muxalu muxalu_21 (
    .input1(argval21A), .input2(argval21B), .extarg1(direct21A), .extarg2(direct21B),
    .isdirectval1(isdirect21), .opcode1(opcode21), .initval1(initval21), .output1(gateval21),
    .outputpins1(outpins21A), .outputpins2(outpins21B));
  muxalu muxalu_22 (
    .input1(argval22A), .input2(argval22B), .extarg1(direct22A), .extarg2(direct22B),
    .isdirectval1(isdirect22), .opcode1(opcode22), .initval1(initval22), .output1(gateval22),
    .outputpins1(outpins22A), .outputpins2(outpins22B));
  muxalu muxalu_23 (
    .input1(argval23A), .input2(argval23B), .extarg1(direct23A), .extarg2(direct23B),
    .isdirectval1(isdirect23), .opcode1(opcode23), .initval1(initval23), .output1(gateval23),
    .outputpins1(outpins23A), .outputpins2(outpins23B));
  muxalu muxalu_24 (
    .input1(argval24A), .input2(argval24B), .extarg1(direct24A), .extarg2(direct24B),
    .isdirectval1(isdirect24), .opcode1(opcode24), .initval1(initval24), .output1(gateval24),
    .outputpins1(outpins24A), .outputpins2(outpins24B));
  muxalu muxalu_25 (
    .input1(argval25A), .input2(argval25B), .extarg1(direct25A), .extarg2(direct25B),
    .isdirectval1(isdirect25), .opcode1(opcode25), .initval1(initval25), .output1(gateval25),
    .outputpins1(outpins25A), .outputpins2(outpins25B));
  muxalu muxalu_26 (
    .input1(argval26A), .input2(argval26B), .extarg1(direct26A), .extarg2(direct26B),
    .isdirectval1(isdirect26), .opcode1(opcode26), .initval1(initval26), .output1(gateval26),
    .outputpins1(outpins26A), .outputpins2(outpins26B));
  muxalu muxalu_27 (
    .input1(argval27A), .input2(argval27B), .extarg1(direct27A), .extarg2(direct27B),
    .isdirectval1(isdirect27), .opcode1(opcode27), .initval1(initval27), .output1(gateval27),
    .outputpins1(outpins27A), .outputpins2(outpins27B));
  muxalu muxalu_28 (
    .input1(argval28A), .input2(argval28B), .extarg1(direct28A), .extarg2(direct28B),
    .isdirectval1(isdirect28), .opcode1(opcode28), .initval1(initval28), .output1(gateval28),
    .outputpins1(outpins28A), .outputpins2(outpins28B));
  muxalu muxalu_29 (
    .input1(argval29A), .input2(argval29B), .extarg1(direct29A), .extarg2(direct29B),
    .isdirectval1(isdirect29), .opcode1(opcode29), .initval1(initval29), .output1(gateval29),
    .outputpins1(outpins29A), .outputpins2(outpins29B));
  muxalu muxalu_30 (
    .input1(argval30A), .input2(argval30B), .extarg1(direct30A), .extarg2(direct30B),
    .isdirectval1(isdirect30), .opcode1(opcode30), .initval1(initval30), .output1(gateval30),
    .outputpins1(outpins30A), .outputpins2(outpins30B));
  muxalu muxalu_31 (
    .input1(argval31A), .input2(argval31B), .extarg1(direct31A), .extarg2(direct31B),
    .isdirectval1(isdirect31), .opcode1(opcode31), .initval1(initval31), .output1(gateval31),
    .outputpins1(outpins31A), .outputpins2(outpins31B));
  muxalu muxalu_32 (
    .input1(argval32A), .input2(argval32B), .extarg1(direct32A), .extarg2(direct32B),
    .isdirectval1(isdirect32), .opcode1(opcode32), .initval1(initval32), .output1(gateval32),
    .outputpins1(outpins32A), .outputpins2(outpins32B));
  muxalu muxalu_33 (
    .input1(argval33A), .input2(argval33B), .extarg1(direct33A), .extarg2(direct33B),
    .isdirectval1(isdirect33), .opcode1(opcode33), .initval1(initval33), .output1(gateval33),
    .outputpins1(outpins33A), .outputpins2(outpins33B));
  muxalu muxalu_34 (
    .input1(argval34A), .input2(argval34B), .extarg1(direct34A), .extarg2(direct34B),
    .isdirectval1(isdirect34), .opcode1(opcode34), .initval1(initval34), .output1(gateval34),
    .outputpins1(outpins34A), .outputpins2(outpins34B));
  muxalu muxalu_35 (
    .input1(argval35A), .input2(argval35B), .extarg1(direct35A), .extarg2(direct35B),
    .isdirectval1(isdirect35), .opcode1(opcode35), .initval1(initval35), .output1(gateval35),
    .outputpins1(outpins35A), .outputpins2(outpins35B));
  muxalu muxalu_36 (
    .input1(argval36A), .input2(argval36B), .extarg1(direct36A), .extarg2(direct36B),
    .isdirectval1(isdirect36), .opcode1(opcode36), .initval1(initval36), .output1(gateval36),
    .outputpins1(outpins36A), .outputpins2(outpins36B));
  muxalu muxalu_37 (
    .input1(argval37A), .input2(argval37B), .extarg1(direct37A), .extarg2(direct37B),
    .isdirectval1(isdirect37), .opcode1(opcode37), .initval1(initval37), .output1(gateval37),
    .outputpins1(outpins37A), .outputpins2(outpins37B));
  muxalu muxalu_38 (
    .input1(argval38A), .input2(argval38B), .extarg1(direct38A), .extarg2(direct38B),
    .isdirectval1(isdirect38), .opcode1(opcode38), .initval1(initval38), .output1(gateval38),
    .outputpins1(outpins38A), .outputpins2(outpins38B));
  muxalu muxalu_39 (
    .input1(argval39A), .input2(argval39B), .extarg1(direct39A), .extarg2(direct39B),
    .isdirectval1(isdirect39), .opcode1(opcode39), .initval1(initval39), .output1(gateval39),
    .outputpins1(outpins39A), .outputpins2(outpins39B));
  muxalu muxalu_40 (
    .input1(argval40A), .input2(argval40B), .extarg1(direct40A), .extarg2(direct40B),
    .isdirectval1(isdirect40), .opcode1(opcode40), .initval1(initval40), .output1(gateval40),
    .outputpins1(outpins40A), .outputpins2(outpins40B));
  muxalu muxalu_41 (
    .input1(argval41A), .input2(argval41B), .extarg1(direct41A), .extarg2(direct41B),
    .isdirectval1(isdirect41), .opcode1(opcode41), .initval1(initval41), .output1(gateval41),
    .outputpins1(outpins41A), .outputpins2(outpins41B));
  muxalu muxalu_42 (
    .input1(argval42A), .input2(argval42B), .extarg1(direct42A), .extarg2(direct42B),
    .isdirectval1(isdirect42), .opcode1(opcode42), .initval1(initval42), .output1(gateval42),
    .outputpins1(outpins42A), .outputpins2(outpins42B));
  muxalu muxalu_43 (
    .input1(argval43A), .input2(argval43B), .extarg1(direct43A), .extarg2(direct43B),
    .isdirectval1(isdirect43), .opcode1(opcode43), .initval1(initval43), .output1(gateval43),
    .outputpins1(outpins43A), .outputpins2(outpins43B));
  muxalu muxalu_44 (
    .input1(argval44A), .input2(argval44B), .extarg1(direct44A), .extarg2(direct44B),
    .isdirectval1(isdirect44), .opcode1(opcode44), .initval1(initval44), .output1(gateval44),
    .outputpins1(outpins44A), .outputpins2(outpins44B));
  muxalu muxalu_45 (
    .input1(argval45A), .input2(argval45B), .extarg1(direct45A), .extarg2(direct45B),
    .isdirectval1(isdirect45), .opcode1(opcode45), .initval1(initval45), .output1(gateval45),
    .outputpins1(outpins45A), .outputpins2(outpins45B));
  muxalu muxalu_46 (
    .input1(argval46A), .input2(argval46B), .extarg1(direct46A), .extarg2(direct46B),
    .isdirectval1(isdirect46), .opcode1(opcode46), .initval1(initval46), .output1(gateval46),
    .outputpins1(outpins46A), .outputpins2(outpins46B));
  muxalu muxalu_47 (
    .input1(argval47A), .input2(argval47B), .extarg1(direct47A), .extarg2(direct47B),
    .isdirectval1(isdirect47), .opcode1(opcode47), .initval1(initval47), .output1(gateval47),
    .outputpins1(outpins47A), .outputpins2(outpins47B));
  muxalu muxalu_48 (
    .input1(argval48A), .input2(argval48B), .extarg1(direct48A), .extarg2(direct48B),
    .isdirectval1(isdirect48), .opcode1(opcode48), .initval1(initval48), .output1(gateval48),
    .outputpins1(outpins48A), .outputpins2(outpins48B));
  muxalu muxalu_49 (
    .input1(argval49A), .input2(argval49B), .extarg1(direct49A), .extarg2(direct49B),
    .isdirectval1(isdirect49), .opcode1(opcode49), .initval1(initval49), .output1(gateval49),
    .outputpins1(outpins49A), .outputpins2(outpins49B));
  muxalu muxalu_50 (
    .input1(argval50A), .input2(argval50B), .extarg1(direct50A), .extarg2(direct50B),
    .isdirectval1(isdirect50), .opcode1(opcode50), .initval1(initval50), .output1(gateval50),
    .outputpins1(outpins50A), .outputpins2(outpins50B));
  muxalu muxalu_51 (
    .input1(argval51A), .input2(argval51B), .extarg1(direct51A), .extarg2(direct51B),
    .isdirectval1(isdirect51), .opcode1(opcode51), .initval1(initval51), .output1(gateval51),
    .outputpins1(outpins51A), .outputpins2(outpins51B));
  muxalu muxalu_52 (
    .input1(argval52A), .input2(argval52B), .extarg1(direct52A), .extarg2(direct52B),
    .isdirectval1(isdirect52), .opcode1(opcode52), .initval1(initval52), .output1(gateval52),
    .outputpins1(outpins52A), .outputpins2(outpins52B));
  muxalu muxalu_53 (
    .input1(argval53A), .input2(argval53B), .extarg1(direct53A), .extarg2(direct53B),
    .isdirectval1(isdirect53), .opcode1(opcode53), .initval1(initval53), .output1(gateval53),
    .outputpins1(outpins53A), .outputpins2(outpins53B));
  muxalu muxalu_54 (
    .input1(argval54A), .input2(argval54B), .extarg1(direct54A), .extarg2(direct54B),
    .isdirectval1(isdirect54), .opcode1(opcode54), .initval1(initval54), .output1(gateval54),
    .outputpins1(outpins54A), .outputpins2(outpins54B));
  muxalu muxalu_55 (
    .input1(argval55A), .input2(argval55B), .extarg1(direct55A), .extarg2(direct55B),
    .isdirectval1(isdirect55), .opcode1(opcode55), .initval1(initval55), .output1(gateval55),
    .outputpins1(outpins55A), .outputpins2(outpins55B));
  muxalu muxalu_56 (
    .input1(argval56A), .input2(argval56B), .extarg1(direct56A), .extarg2(direct56B),
    .isdirectval1(isdirect56), .opcode1(opcode56), .initval1(initval56), .output1(gateval56),
    .outputpins1(outpins56A), .outputpins2(outpins56B));
  muxalu muxalu_57 (
    .input1(argval57A), .input2(argval57B), .extarg1(direct57A), .extarg2(direct57B),
    .isdirectval1(isdirect57), .opcode1(opcode57), .initval1(initval57), .output1(gateval57),
    .outputpins1(outpins57A), .outputpins2(outpins57B));
  muxalu muxalu_58 (
    .input1(argval58A), .input2(argval58B), .extarg1(direct58A), .extarg2(direct58B),
    .isdirectval1(isdirect58), .opcode1(opcode58), .initval1(initval58), .output1(gateval58),
    .outputpins1(outpins58A), .outputpins2(outpins58B));
  muxalu muxalu_59 (
    .input1(argval59A), .input2(argval59B), .extarg1(direct59A), .extarg2(direct59B),
    .isdirectval1(isdirect59), .opcode1(opcode59), .initval1(initval59), .output1(gateval59),
    .outputpins1(outpins59A), .outputpins2(outpins59B));
  muxalu muxalu_60 (
    .input1(argval60A), .input2(argval60B), .extarg1(direct60A), .extarg2(direct60B),
    .isdirectval1(isdirect60), .opcode1(opcode60), .initval1(initval60), .output1(gateval60),
    .outputpins1(outpins60A), .outputpins2(outpins60B));
  muxalu muxalu_61 (
    .input1(argval61A), .input2(argval61B), .extarg1(direct61A), .extarg2(direct61B),
    .isdirectval1(isdirect61), .opcode1(opcode61), .initval1(initval61), .output1(gateval61),
    .outputpins1(outpins61A), .outputpins2(outpins61B));
  muxalu muxalu_62 (
    .input1(argval62A), .input2(argval62B), .extarg1(direct62A), .extarg2(direct62B),
    .isdirectval1(isdirect62), .opcode1(opcode62), .initval1(initval62), .output1(gateval62),
    .outputpins1(outpins62A), .outputpins2(outpins62B));
  muxalu muxalu_63 (
    .input1(argval63A), .input2(argval63B), .extarg1(direct63A), .extarg2(direct63B),
    .isdirectval1(isdirect63), .opcode1(opcode63), .initval1(initval63), .output1(gateval63),
    .outputpins1(outpins63A), .outputpins2(outpins63B));
  muxalu muxalu_64 (
    .input1(argval64A), .input2(argval64B), .extarg1(direct64A), .extarg2(direct64B),
    .isdirectval1(isdirect64), .opcode1(opcode64), .initval1(initval64), .output1(gateval64),
    .outputpins1(outpins64A), .outputpins2(outpins64B));
  muxselector muxselector_1 (
    .direct1(direct1A), .direct2(direct1B), .input1(gateval1), .input2(gateval2), .input3(gateval3),
    .input4(gateval4), .input5(gateval5), .input6(gateval6), .input7(gateval7), .input8(gateval8),
    .input9(gateval9), .input10(gateval10), .input11(gateval11), .input12(gateval12), .input13(gateval13),
    .input14(gateval14), .input15(gateval15), .input16(gateval16), .input17(gateval17), .input18(gateval18),
    .input19(gateval19), .input20(gateval20), .input21(gateval21), .input22(gateval22), .input23(gateval23),
    .input24(gateval24), .input25(gateval25), .input26(gateval26), .input27(gateval27), .input28(gateval28),
    .input29(gateval29), .input30(gateval30), .input31(gateval31), .input32(gateval32), .input33(gateval33),
    .input34(gateval34), .input35(gateval35), .input36(gateval36), .input37(gateval37), .input38(gateval38),
    .input39(gateval39), .input40(gateval40), .input41(gateval41), .input42(gateval42), .input43(gateval43),
    .input44(gateval44), .input45(gateval45), .input46(gateval46), .input47(gateval47), .input48(gateval48),
    .input49(gateval49), .input50(gateval50), .input51(gateval51), .input52(gateval52), .input53(gateval53),
    .input54(gateval54), .input55(gateval55), .input56(gateval56), .input57(gateval57), .input58(gateval58),
    .input59(gateval59), .input60(gateval60), .input61(gateval61), .input62(gateval62), .input63(gateval63),
    .input64(gateval64), .output1(argval1A), .output2(argval1B));
  muxselector muxselector_2 (
    .direct1(direct2A), .direct2(direct2B), .input1(gateval1), .input2(gateval2), .input3(gateval3),
    .input4(gateval4), .input5(gateval5), .input6(gateval6), .input7(gateval7), .input8(gateval8),
    .input9(gateval9), .input10(gateval10), .input11(gateval11), .input12(gateval12), .input13(gateval13),
    .input14(gateval14), .input15(gateval15), .input16(gateval16), .input17(gateval17), .input18(gateval18),
    .input19(gateval19), .input20(gateval20), .input21(gateval21), .input22(gateval22), .input23(gateval23),
    .input24(gateval24), .input25(gateval25), .input26(gateval26), .input27(gateval27), .input28(gateval28),
    .input29(gateval29), .input30(gateval30), .input31(gateval31), .input32(gateval32), .input33(gateval33),
    .input34(gateval34), .input35(gateval35), .input36(gateval36), .input37(gateval37), .input38(gateval38),
    .input39(gateval39), .input40(gateval40), .input41(gateval41), .input42(gateval42), .input43(gateval43),
    .input44(gateval44), .input45(gateval45), .input46(gateval46), .input47(gateval47), .input48(gateval48),
    .input49(gateval49), .input50(gateval50), .input51(gateval51), .input52(gateval52), .input53(gateval53),
    .input54(gateval54), .input55(gateval55), .input56(gateval56), .input57(gateval57), .input58(gateval58),
    .input59(gateval59), .input60(gateval60), .input61(gateval61), .input62(gateval62), .input63(gateval63),
    .input64(gateval64), .output1(argval2A), .output2(argval2B));
  muxselector muxselector_3 (
    .direct1(direct3A), .direct2(direct3B), .input1(gateval1), .input2(gateval2), .input3(gateval3),
    .input4(gateval4), .input5(gateval5), .input6(gateval6), .input7(gateval7), .input8(gateval8),
    .input9(gateval9), .input10(gateval10), .input11(gateval11), .input12(gateval12), .input13(gateval13),
    .input14(gateval14), .input15(gateval15), .input16(gateval16), .input17(gateval17), .input18(gateval18),
    .input19(gateval19), .input20(gateval20), .input21(gateval21), .input22(gateval22), .input23(gateval23),
    .input24(gateval24), .input25(gateval25), .input26(gateval26), .input27(gateval27), .input28(gateval28),
    .input29(gateval29), .input30(gateval30), .input31(gateval31), .input32(gateval32), .input33(gateval33),
    .input34(gateval34), .input35(gateval35), .input36(gateval36), .input37(gateval37), .input38(gateval38),
    .input39(gateval39), .input40(gateval40), .input41(gateval41), .input42(gateval42), .input43(gateval43),
    .input44(gateval44), .input45(gateval45), .input46(gateval46), .input47(gateval47), .input48(gateval48),
    .input49(gateval49), .input50(gateval50), .input51(gateval51), .input52(gateval52), .input53(gateval53),
    .input54(gateval54), .input55(gateval55), .input56(gateval56), .input57(gateval57), .input58(gateval58),
    .input59(gateval59), .input60(gateval60), .input61(gateval61), .input62(gateval62), .input63(gateval63),
    .input64(gateval64), .output1(argval3A), .output2(argval3B));
  muxselector muxselector_4 (
    .direct1(direct4A), .direct2(direct4B), .input1(gateval1), .input2(gateval2), .input3(gateval3),
    .input4(gateval4), .input5(gateval5), .input6(gateval6), .input7(gateval7), .input8(gateval8),
    .input9(gateval9), .input10(gateval10), .input11(gateval11), .input12(gateval12), .input13(gateval13),
    .input14(gateval14), .input15(gateval15), .input16(gateval16), .input17(gateval17), .input18(gateval18),
    .input19(gateval19), .input20(gateval20), .input21(gateval21), .input22(gateval22), .input23(gateval23),
    .input24(gateval24), .input25(gateval25), .input26(gateval26), .input27(gateval27), .input28(gateval28),
    .input29(gateval29), .input30(gateval30), .input31(gateval31), .input32(gateval32), .input33(gateval33),
    .input34(gateval34), .input35(gateval35), .input36(gateval36), .input37(gateval37), .input38(gateval38),
    .input39(gateval39), .input40(gateval40), .input41(gateval41), .input42(gateval42), .input43(gateval43),
    .input44(gateval44), .input45(gateval45), .input46(gateval46), .input47(gateval47), .input48(gateval48),
    .input49(gateval49), .input50(gateval50), .input51(gateval51), .input52(gateval52), .input53(gateval53),
    .input54(gateval54), .input55(gateval55), .input56(gateval56), .input57(gateval57), .input58(gateval58),
    .input59(gateval59), .input60(gateval60), .input61(gateval61), .input62(gateval62), .input63(gateval63),
    .input64(gateval64), .output1(argval4A), .output2(argval4B));
  muxselector muxselector_5 (
    .direct1(direct5A), .direct2(direct5B), .input1(gateval1), .input2(gateval2), .input3(gateval3),
    .input4(gateval4), .input5(gateval5), .input6(gateval6), .input7(gateval7), .input8(gateval8),
    .input9(gateval9), .input10(gateval10), .input11(gateval11), .input12(gateval12), .input13(gateval13),
    .input14(gateval14), .input15(gateval15), .input16(gateval16), .input17(gateval17), .input18(gateval18),
    .input19(gateval19), .input20(gateval20), .input21(gateval21), .input22(gateval22), .input23(gateval23),
    .input24(gateval24), .input25(gateval25), .input26(gateval26), .input27(gateval27), .input28(gateval28),
    .input29(gateval29), .input30(gateval30), .input31(gateval31), .input32(gateval32), .input33(gateval33),
    .input34(gateval34), .input35(gateval35), .input36(gateval36), .input37(gateval37), .input38(gateval38),
    .input39(gateval39), .input40(gateval40), .input41(gateval41), .input42(gateval42), .input43(gateval43),
    .input44(gateval44), .input45(gateval45), .input46(gateval46), .input47(gateval47), .input48(gateval48),
    .input49(gateval49), .input50(gateval50), .input51(gateval51), .input52(gateval52), .input53(gateval53),
    .input54(gateval54), .input55(gateval55), .input56(gateval56), .input57(gateval57), .input58(gateval58),
    .input59(gateval59), .input60(gateval60), .input61(gateval61), .input62(gateval62), .input63(gateval63),
    .input64(gateval64), .output1(argval5A), .output2(argval5B));
  muxselector muxselector_6 (
    .direct1(direct6A), .direct2(direct6B), .input1(gateval1), .input2(gateval2), .input3(gateval3),
    .input4(gateval4), .input5(gateval5), .input6(gateval6), .input7(gateval7), .input8(gateval8),
    .input9(gateval9), .input10(gateval10), .input11(gateval11), .input12(gateval12), .input13(gateval13),
    .input14(gateval14), .input15(gateval15), .input16(gateval16), .input17(gateval17), .input18(gateval18),
    .input19(gateval19), .input20(gateval20), .input21(gateval21), .input22(gateval22), .input23(gateval23),
    .input24(gateval24), .input25(gateval25), .input26(gateval26), .input27(gateval27), .input28(gateval28),
    .input29(gateval29), .input30(gateval30), .input31(gateval31), .input32(gateval32), .input33(gateval33),
    .input34(gateval34), .input35(gateval35), .input36(gateval36), .input37(gateval37), .input38(gateval38),
    .input39(gateval39), .input40(gateval40), .input41(gateval41), .input42(gateval42), .input43(gateval43),
    .input44(gateval44), .input45(gateval45), .input46(gateval46), .input47(gateval47), .input48(gateval48),
    .input49(gateval49), .input50(gateval50), .input51(gateval51), .input52(gateval52), .input53(gateval53),
    .input54(gateval54), .input55(gateval55), .input56(gateval56), .input57(gateval57), .input58(gateval58),
    .input59(gateval59), .input60(gateval60), .input61(gateval61), .input62(gateval62), .input63(gateval63),
    .input64(gateval64), .output1(argval6A), .output2(argval6B));
  muxselector muxselector_7 (
    .direct1(direct7A), .direct2(direct7B), .input1(gateval1), .input2(gateval2), .input3(gateval3),
    .input4(gateval4), .input5(gateval5), .input6(gateval6), .input7(gateval7), .input8(gateval8),
    .input9(gateval9), .input10(gateval10), .input11(gateval11), .input12(gateval12), .input13(gateval13),
    .input14(gateval14), .input15(gateval15), .input16(gateval16), .input17(gateval17), .input18(gateval18),
    .input19(gateval19), .input20(gateval20), .input21(gateval21), .input22(gateval22), .input23(gateval23),
    .input24(gateval24), .input25(gateval25), .input26(gateval26), .input27(gateval27), .input28(gateval28),
    .input29(gateval29), .input30(gateval30), .input31(gateval31), .input32(gateval32), .input33(gateval33),
    .input34(gateval34), .input35(gateval35), .input36(gateval36), .input37(gateval37), .input38(gateval38),
    .input39(gateval39), .input40(gateval40), .input41(gateval41), .input42(gateval42), .input43(gateval43),
    .input44(gateval44), .input45(gateval45), .input46(gateval46), .input47(gateval47), .input48(gateval48),
    .input49(gateval49), .input50(gateval50), .input51(gateval51), .input52(gateval52), .input53(gateval53),
    .input54(gateval54), .input55(gateval55), .input56(gateval56), .input57(gateval57), .input58(gateval58),
    .input59(gateval59), .input60(gateval60), .input61(gateval61), .input62(gateval62), .input63(gateval63),
    .input64(gateval64), .output1(argval7A), .output2(argval7B));
  muxselector muxselector_8 (
    .direct1(direct8A), .direct2(direct8B), .input1(gateval1), .input2(gateval2), .input3(gateval3),
    .input4(gateval4), .input5(gateval5), .input6(gateval6), .input7(gateval7), .input8(gateval8),
    .input9(gateval9), .input10(gateval10), .input11(gateval11), .input12(gateval12), .input13(gateval13),
    .input14(gateval14), .input15(gateval15), .input16(gateval16), .input17(gateval17), .input18(gateval18),
    .input19(gateval19), .input20(gateval20), .input21(gateval21), .input22(gateval22), .input23(gateval23),
    .input24(gateval24), .input25(gateval25), .input26(gateval26), .input27(gateval27), .input28(gateval28),
    .input29(gateval29), .input30(gateval30), .input31(gateval31), .input32(gateval32), .input33(gateval33),
    .input34(gateval34), .input35(gateval35), .input36(gateval36), .input37(gateval37), .input38(gateval38),
    .input39(gateval39), .input40(gateval40), .input41(gateval41), .input42(gateval42), .input43(gateval43),
    .input44(gateval44), .input45(gateval45), .input46(gateval46), .input47(gateval47), .input48(gateval48),
    .input49(gateval49), .input50(gateval50), .input51(gateval51), .input52(gateval52), .input53(gateval53),
    .input54(gateval54), .input55(gateval55), .input56(gateval56), .input57(gateval57), .input58(gateval58),
    .input59(gateval59), .input60(gateval60), .input61(gateval61), .input62(gateval62), .input63(gateval63),
    .input64(gateval64), .output1(argval8A), .output2(argval8B));
  muxselector muxselector_9 (
    .direct1(direct9A), .direct2(direct9B), .input1(gateval1), .input2(gateval2), .input3(gateval3),
    .input4(gateval4), .input5(gateval5), .input6(gateval6), .input7(gateval7), .input8(gateval8),
    .input9(gateval9), .input10(gateval10), .input11(gateval11), .input12(gateval12), .input13(gateval13),
    .input14(gateval14), .input15(gateval15), .input16(gateval16), .input17(gateval17), .input18(gateval18),
    .input19(gateval19), .input20(gateval20), .input21(gateval21), .input22(gateval22), .input23(gateval23),
    .input24(gateval24), .input25(gateval25), .input26(gateval26), .input27(gateval27), .input28(gateval28),
    .input29(gateval29), .input30(gateval30), .input31(gateval31), .input32(gateval32), .input33(gateval33),
    .input34(gateval34), .input35(gateval35), .input36(gateval36), .input37(gateval37), .input38(gateval38),
    .input39(gateval39), .input40(gateval40), .input41(gateval41), .input42(gateval42), .input43(gateval43),
    .input44(gateval44), .input45(gateval45), .input46(gateval46), .input47(gateval47), .input48(gateval48),
    .input49(gateval49), .input50(gateval50), .input51(gateval51), .input52(gateval52), .input53(gateval53),
    .input54(gateval54), .input55(gateval55), .input56(gateval56), .input57(gateval57), .input58(gateval58),
    .input59(gateval59), .input60(gateval60), .input61(gateval61), .input62(gateval62), .input63(gateval63),
    .input64(gateval64), .output1(argval9A), .output2(argval9B));
  muxselector muxselector_10 (
    .direct1(direct10A), .direct2(direct10B), .input1(gateval1), .input2(gateval2), .input3(gateval3),
    .input4(gateval4), .input5(gateval5), .input6(gateval6), .input7(gateval7), .input8(gateval8),
    .input9(gateval9), .input10(gateval10), .input11(gateval11), .input12(gateval12), .input13(gateval13),
    .input14(gateval14), .input15(gateval15), .input16(gateval16), .input17(gateval17), .input18(gateval18),
    .input19(gateval19), .input20(gateval20), .input21(gateval21), .input22(gateval22), .input23(gateval23),
    .input24(gateval24), .input25(gateval25), .input26(gateval26), .input27(gateval27), .input28(gateval28),
    .input29(gateval29), .input30(gateval30), .input31(gateval31), .input32(gateval32), .input33(gateval33),
    .input34(gateval34), .input35(gateval35), .input36(gateval36), .input37(gateval37), .input38(gateval38),
    .input39(gateval39), .input40(gateval40), .input41(gateval41), .input42(gateval42), .input43(gateval43),
    .input44(gateval44), .input45(gateval45), .input46(gateval46), .input47(gateval47), .input48(gateval48),
    .input49(gateval49), .input50(gateval50), .input51(gateval51), .input52(gateval52), .input53(gateval53),
    .input54(gateval54), .input55(gateval55), .input56(gateval56), .input57(gateval57), .input58(gateval58),
    .input59(gateval59), .input60(gateval60), .input61(gateval61), .input62(gateval62), .input63(gateval63),
    .input64(gateval64), .output1(argval10A), .output2(argval10B));
  muxselector muxselector_11 (
    .direct1(direct11A), .direct2(direct11B), .input1(gateval1), .input2(gateval2), .input3(gateval3),
    .input4(gateval4), .input5(gateval5), .input6(gateval6), .input7(gateval7), .input8(gateval8),
    .input9(gateval9), .input10(gateval10), .input11(gateval11), .input12(gateval12), .input13(gateval13),
    .input14(gateval14), .input15(gateval15), .input16(gateval16), .input17(gateval17), .input18(gateval18),
    .input19(gateval19), .input20(gateval20), .input21(gateval21), .input22(gateval22), .input23(gateval23),
    .input24(gateval24), .input25(gateval25), .input26(gateval26), .input27(gateval27), .input28(gateval28),
    .input29(gateval29), .input30(gateval30), .input31(gateval31), .input32(gateval32), .input33(gateval33),
    .input34(gateval34), .input35(gateval35), .input36(gateval36), .input37(gateval37), .input38(gateval38),
    .input39(gateval39), .input40(gateval40), .input41(gateval41), .input42(gateval42), .input43(gateval43),
    .input44(gateval44), .input45(gateval45), .input46(gateval46), .input47(gateval47), .input48(gateval48),
    .input49(gateval49), .input50(gateval50), .input51(gateval51), .input52(gateval52), .input53(gateval53),
    .input54(gateval54), .input55(gateval55), .input56(gateval56), .input57(gateval57), .input58(gateval58),
    .input59(gateval59), .input60(gateval60), .input61(gateval61), .input62(gateval62), .input63(gateval63),
    .input64(gateval64), .output1(argval11A), .output2(argval11B));
  muxselector muxselector_12 (
    .direct1(direct12A), .direct2(direct12B), .input1(gateval1), .input2(gateval2), .input3(gateval3),
    .input4(gateval4), .input5(gateval5), .input6(gateval6), .input7(gateval7), .input8(gateval8),
    .input9(gateval9), .input10(gateval10), .input11(gateval11), .input12(gateval12), .input13(gateval13),
    .input14(gateval14), .input15(gateval15), .input16(gateval16), .input17(gateval17), .input18(gateval18),
    .input19(gateval19), .input20(gateval20), .input21(gateval21), .input22(gateval22), .input23(gateval23),
    .input24(gateval24), .input25(gateval25), .input26(gateval26), .input27(gateval27), .input28(gateval28),
    .input29(gateval29), .input30(gateval30), .input31(gateval31), .input32(gateval32), .input33(gateval33),
    .input34(gateval34), .input35(gateval35), .input36(gateval36), .input37(gateval37), .input38(gateval38),
    .input39(gateval39), .input40(gateval40), .input41(gateval41), .input42(gateval42), .input43(gateval43),
    .input44(gateval44), .input45(gateval45), .input46(gateval46), .input47(gateval47), .input48(gateval48),
    .input49(gateval49), .input50(gateval50), .input51(gateval51), .input52(gateval52), .input53(gateval53),
    .input54(gateval54), .input55(gateval55), .input56(gateval56), .input57(gateval57), .input58(gateval58),
    .input59(gateval59), .input60(gateval60), .input61(gateval61), .input62(gateval62), .input63(gateval63),
    .input64(gateval64), .output1(argval12A), .output2(argval12B));
  muxselector muxselector_13 (
    .direct1(direct13A), .direct2(direct13B), .input1(gateval1), .input2(gateval2), .input3(gateval3),
    .input4(gateval4), .input5(gateval5), .input6(gateval6), .input7(gateval7), .input8(gateval8),
    .input9(gateval9), .input10(gateval10), .input11(gateval11), .input12(gateval12), .input13(gateval13),
    .input14(gateval14), .input15(gateval15), .input16(gateval16), .input17(gateval17), .input18(gateval18),
    .input19(gateval19), .input20(gateval20), .input21(gateval21), .input22(gateval22), .input23(gateval23),
    .input24(gateval24), .input25(gateval25), .input26(gateval26), .input27(gateval27), .input28(gateval28),
    .input29(gateval29), .input30(gateval30), .input31(gateval31), .input32(gateval32), .input33(gateval33),
    .input34(gateval34), .input35(gateval35), .input36(gateval36), .input37(gateval37), .input38(gateval38),
    .input39(gateval39), .input40(gateval40), .input41(gateval41), .input42(gateval42), .input43(gateval43),
    .input44(gateval44), .input45(gateval45), .input46(gateval46), .input47(gateval47), .input48(gateval48),
    .input49(gateval49), .input50(gateval50), .input51(gateval51), .input52(gateval52), .input53(gateval53),
    .input54(gateval54), .input55(gateval55), .input56(gateval56), .input57(gateval57), .input58(gateval58),
    .input59(gateval59), .input60(gateval60), .input61(gateval61), .input62(gateval62), .input63(gateval63),
    .input64(gateval64), .output1(argval13A), .output2(argval13B));
  muxselector muxselector_14 (
    .direct1(direct14A), .direct2(direct14B), .input1(gateval1), .input2(gateval2), .input3(gateval3),
    .input4(gateval4), .input5(gateval5), .input6(gateval6), .input7(gateval7), .input8(gateval8),
    .input9(gateval9), .input10(gateval10), .input11(gateval11), .input12(gateval12), .input13(gateval13),
    .input14(gateval14), .input15(gateval15), .input16(gateval16), .input17(gateval17), .input18(gateval18),
    .input19(gateval19), .input20(gateval20), .input21(gateval21), .input22(gateval22), .input23(gateval23),
    .input24(gateval24), .input25(gateval25), .input26(gateval26), .input27(gateval27), .input28(gateval28),
    .input29(gateval29), .input30(gateval30), .input31(gateval31), .input32(gateval32), .input33(gateval33),
    .input34(gateval34), .input35(gateval35), .input36(gateval36), .input37(gateval37), .input38(gateval38),
    .input39(gateval39), .input40(gateval40), .input41(gateval41), .input42(gateval42), .input43(gateval43),
    .input44(gateval44), .input45(gateval45), .input46(gateval46), .input47(gateval47), .input48(gateval48),
    .input49(gateval49), .input50(gateval50), .input51(gateval51), .input52(gateval52), .input53(gateval53),
    .input54(gateval54), .input55(gateval55), .input56(gateval56), .input57(gateval57), .input58(gateval58),
    .input59(gateval59), .input60(gateval60), .input61(gateval61), .input62(gateval62), .input63(gateval63),
    .input64(gateval64), .output1(argval14A), .output2(argval14B));
  muxselector muxselector_15 (
    .direct1(direct15A), .direct2(direct15B), .input1(gateval1), .input2(gateval2), .input3(gateval3),
    .input4(gateval4), .input5(gateval5), .input6(gateval6), .input7(gateval7), .input8(gateval8),
    .input9(gateval9), .input10(gateval10), .input11(gateval11), .input12(gateval12), .input13(gateval13),
    .input14(gateval14), .input15(gateval15), .input16(gateval16), .input17(gateval17), .input18(gateval18),
    .input19(gateval19), .input20(gateval20), .input21(gateval21), .input22(gateval22), .input23(gateval23),
    .input24(gateval24), .input25(gateval25), .input26(gateval26), .input27(gateval27), .input28(gateval28),
    .input29(gateval29), .input30(gateval30), .input31(gateval31), .input32(gateval32), .input33(gateval33),
    .input34(gateval34), .input35(gateval35), .input36(gateval36), .input37(gateval37), .input38(gateval38),
    .input39(gateval39), .input40(gateval40), .input41(gateval41), .input42(gateval42), .input43(gateval43),
    .input44(gateval44), .input45(gateval45), .input46(gateval46), .input47(gateval47), .input48(gateval48),
    .input49(gateval49), .input50(gateval50), .input51(gateval51), .input52(gateval52), .input53(gateval53),
    .input54(gateval54), .input55(gateval55), .input56(gateval56), .input57(gateval57), .input58(gateval58),
    .input59(gateval59), .input60(gateval60), .input61(gateval61), .input62(gateval62), .input63(gateval63),
    .input64(gateval64), .output1(argval15A), .output2(argval15B));
  muxselector muxselector_16 (
    .direct1(direct16A), .direct2(direct16B), .input1(gateval1), .input2(gateval2), .input3(gateval3),
    .input4(gateval4), .input5(gateval5), .input6(gateval6), .input7(gateval7), .input8(gateval8),
    .input9(gateval9), .input10(gateval10), .input11(gateval11), .input12(gateval12), .input13(gateval13),
    .input14(gateval14), .input15(gateval15), .input16(gateval16), .input17(gateval17), .input18(gateval18),
    .input19(gateval19), .input20(gateval20), .input21(gateval21), .input22(gateval22), .input23(gateval23),
    .input24(gateval24), .input25(gateval25), .input26(gateval26), .input27(gateval27), .input28(gateval28),
    .input29(gateval29), .input30(gateval30), .input31(gateval31), .input32(gateval32), .input33(gateval33),
    .input34(gateval34), .input35(gateval35), .input36(gateval36), .input37(gateval37), .input38(gateval38),
    .input39(gateval39), .input40(gateval40), .input41(gateval41), .input42(gateval42), .input43(gateval43),
    .input44(gateval44), .input45(gateval45), .input46(gateval46), .input47(gateval47), .input48(gateval48),
    .input49(gateval49), .input50(gateval50), .input51(gateval51), .input52(gateval52), .input53(gateval53),
    .input54(gateval54), .input55(gateval55), .input56(gateval56), .input57(gateval57), .input58(gateval58),
    .input59(gateval59), .input60(gateval60), .input61(gateval61), .input62(gateval62), .input63(gateval63),
    .input64(gateval64), .output1(argval16A), .output2(argval16B));
  muxselector muxselector_17 (
    .direct1(direct17A), .direct2(direct17B), .input1(gateval1), .input2(gateval2), .input3(gateval3),
    .input4(gateval4), .input5(gateval5), .input6(gateval6), .input7(gateval7), .input8(gateval8),
    .input9(gateval9), .input10(gateval10), .input11(gateval11), .input12(gateval12), .input13(gateval13),
    .input14(gateval14), .input15(gateval15), .input16(gateval16), .input17(gateval17), .input18(gateval18),
    .input19(gateval19), .input20(gateval20), .input21(gateval21), .input22(gateval22), .input23(gateval23),
    .input24(gateval24), .input25(gateval25), .input26(gateval26), .input27(gateval27), .input28(gateval28),
    .input29(gateval29), .input30(gateval30), .input31(gateval31), .input32(gateval32), .input33(gateval33),
    .input34(gateval34), .input35(gateval35), .input36(gateval36), .input37(gateval37), .input38(gateval38),
    .input39(gateval39), .input40(gateval40), .input41(gateval41), .input42(gateval42), .input43(gateval43),
    .input44(gateval44), .input45(gateval45), .input46(gateval46), .input47(gateval47), .input48(gateval48),
    .input49(gateval49), .input50(gateval50), .input51(gateval51), .input52(gateval52), .input53(gateval53),
    .input54(gateval54), .input55(gateval55), .input56(gateval56), .input57(gateval57), .input58(gateval58),
    .input59(gateval59), .input60(gateval60), .input61(gateval61), .input62(gateval62), .input63(gateval63),
    .input64(gateval64), .output1(argval17A), .output2(argval17B));
  muxselector muxselector_18 (
    .direct1(direct18A), .direct2(direct18B), .input1(gateval1), .input2(gateval2), .input3(gateval3),
    .input4(gateval4), .input5(gateval5), .input6(gateval6), .input7(gateval7), .input8(gateval8),
    .input9(gateval9), .input10(gateval10), .input11(gateval11), .input12(gateval12), .input13(gateval13),
    .input14(gateval14), .input15(gateval15), .input16(gateval16), .input17(gateval17), .input18(gateval18),
    .input19(gateval19), .input20(gateval20), .input21(gateval21), .input22(gateval22), .input23(gateval23),
    .input24(gateval24), .input25(gateval25), .input26(gateval26), .input27(gateval27), .input28(gateval28),
    .input29(gateval29), .input30(gateval30), .input31(gateval31), .input32(gateval32), .input33(gateval33),
    .input34(gateval34), .input35(gateval35), .input36(gateval36), .input37(gateval37), .input38(gateval38),
    .input39(gateval39), .input40(gateval40), .input41(gateval41), .input42(gateval42), .input43(gateval43),
    .input44(gateval44), .input45(gateval45), .input46(gateval46), .input47(gateval47), .input48(gateval48),
    .input49(gateval49), .input50(gateval50), .input51(gateval51), .input52(gateval52), .input53(gateval53),
    .input54(gateval54), .input55(gateval55), .input56(gateval56), .input57(gateval57), .input58(gateval58),
    .input59(gateval59), .input60(gateval60), .input61(gateval61), .input62(gateval62), .input63(gateval63),
    .input64(gateval64), .output1(argval18A), .output2(argval18B));
  muxselector muxselector_19 (
    .direct1(direct19A), .direct2(direct19B), .input1(gateval1), .input2(gateval2), .input3(gateval3),
    .input4(gateval4), .input5(gateval5), .input6(gateval6), .input7(gateval7), .input8(gateval8),
    .input9(gateval9), .input10(gateval10), .input11(gateval11), .input12(gateval12), .input13(gateval13),
    .input14(gateval14), .input15(gateval15), .input16(gateval16), .input17(gateval17), .input18(gateval18),
    .input19(gateval19), .input20(gateval20), .input21(gateval21), .input22(gateval22), .input23(gateval23),
    .input24(gateval24), .input25(gateval25), .input26(gateval26), .input27(gateval27), .input28(gateval28),
    .input29(gateval29), .input30(gateval30), .input31(gateval31), .input32(gateval32), .input33(gateval33),
    .input34(gateval34), .input35(gateval35), .input36(gateval36), .input37(gateval37), .input38(gateval38),
    .input39(gateval39), .input40(gateval40), .input41(gateval41), .input42(gateval42), .input43(gateval43),
    .input44(gateval44), .input45(gateval45), .input46(gateval46), .input47(gateval47), .input48(gateval48),
    .input49(gateval49), .input50(gateval50), .input51(gateval51), .input52(gateval52), .input53(gateval53),
    .input54(gateval54), .input55(gateval55), .input56(gateval56), .input57(gateval57), .input58(gateval58),
    .input59(gateval59), .input60(gateval60), .input61(gateval61), .input62(gateval62), .input63(gateval63),
    .input64(gateval64), .output1(argval19A), .output2(argval19B));
  muxselector muxselector_20 (
    .direct1(direct20A), .direct2(direct20B), .input1(gateval1), .input2(gateval2), .input3(gateval3),
    .input4(gateval4), .input5(gateval5), .input6(gateval6), .input7(gateval7), .input8(gateval8),
    .input9(gateval9), .input10(gateval10), .input11(gateval11), .input12(gateval12), .input13(gateval13),
    .input14(gateval14), .input15(gateval15), .input16(gateval16), .input17(gateval17), .input18(gateval18),
    .input19(gateval19), .input20(gateval20), .input21(gateval21), .input22(gateval22), .input23(gateval23),
    .input24(gateval24), .input25(gateval25), .input26(gateval26), .input27(gateval27), .input28(gateval28),
    .input29(gateval29), .input30(gateval30), .input31(gateval31), .input32(gateval32), .input33(gateval33),
    .input34(gateval34), .input35(gateval35), .input36(gateval36), .input37(gateval37), .input38(gateval38),
    .input39(gateval39), .input40(gateval40), .input41(gateval41), .input42(gateval42), .input43(gateval43),
    .input44(gateval44), .input45(gateval45), .input46(gateval46), .input47(gateval47), .input48(gateval48),
    .input49(gateval49), .input50(gateval50), .input51(gateval51), .input52(gateval52), .input53(gateval53),
    .input54(gateval54), .input55(gateval55), .input56(gateval56), .input57(gateval57), .input58(gateval58),
    .input59(gateval59), .input60(gateval60), .input61(gateval61), .input62(gateval62), .input63(gateval63),
    .input64(gateval64), .output1(argval20A), .output2(argval20B));
  muxselector muxselector_21 (
    .direct1(direct21A), .direct2(direct21B), .input1(gateval1), .input2(gateval2), .input3(gateval3),
    .input4(gateval4), .input5(gateval5), .input6(gateval6), .input7(gateval7), .input8(gateval8),
    .input9(gateval9), .input10(gateval10), .input11(gateval11), .input12(gateval12), .input13(gateval13),
    .input14(gateval14), .input15(gateval15), .input16(gateval16), .input17(gateval17), .input18(gateval18),
    .input19(gateval19), .input20(gateval20), .input21(gateval21), .input22(gateval22), .input23(gateval23),
    .input24(gateval24), .input25(gateval25), .input26(gateval26), .input27(gateval27), .input28(gateval28),
    .input29(gateval29), .input30(gateval30), .input31(gateval31), .input32(gateval32), .input33(gateval33),
    .input34(gateval34), .input35(gateval35), .input36(gateval36), .input37(gateval37), .input38(gateval38),
    .input39(gateval39), .input40(gateval40), .input41(gateval41), .input42(gateval42), .input43(gateval43),
    .input44(gateval44), .input45(gateval45), .input46(gateval46), .input47(gateval47), .input48(gateval48),
    .input49(gateval49), .input50(gateval50), .input51(gateval51), .input52(gateval52), .input53(gateval53),
    .input54(gateval54), .input55(gateval55), .input56(gateval56), .input57(gateval57), .input58(gateval58),
    .input59(gateval59), .input60(gateval60), .input61(gateval61), .input62(gateval62), .input63(gateval63),
    .input64(gateval64), .output1(argval21A), .output2(argval21B));
  muxselector muxselector_22 (
    .direct1(direct22A), .direct2(direct22B), .input1(gateval1), .input2(gateval2), .input3(gateval3),
    .input4(gateval4), .input5(gateval5), .input6(gateval6), .input7(gateval7), .input8(gateval8),
    .input9(gateval9), .input10(gateval10), .input11(gateval11), .input12(gateval12), .input13(gateval13),
    .input14(gateval14), .input15(gateval15), .input16(gateval16), .input17(gateval17), .input18(gateval18),
    .input19(gateval19), .input20(gateval20), .input21(gateval21), .input22(gateval22), .input23(gateval23),
    .input24(gateval24), .input25(gateval25), .input26(gateval26), .input27(gateval27), .input28(gateval28),
    .input29(gateval29), .input30(gateval30), .input31(gateval31), .input32(gateval32), .input33(gateval33),
    .input34(gateval34), .input35(gateval35), .input36(gateval36), .input37(gateval37), .input38(gateval38),
    .input39(gateval39), .input40(gateval40), .input41(gateval41), .input42(gateval42), .input43(gateval43),
    .input44(gateval44), .input45(gateval45), .input46(gateval46), .input47(gateval47), .input48(gateval48),
    .input49(gateval49), .input50(gateval50), .input51(gateval51), .input52(gateval52), .input53(gateval53),
    .input54(gateval54), .input55(gateval55), .input56(gateval56), .input57(gateval57), .input58(gateval58),
    .input59(gateval59), .input60(gateval60), .input61(gateval61), .input62(gateval62), .input63(gateval63),
    .input64(gateval64), .output1(argval22A), .output2(argval22B));
  muxselector muxselector_23 (
    .direct1(direct23A), .direct2(direct23B), .input1(gateval1), .input2(gateval2), .input3(gateval3),
    .input4(gateval4), .input5(gateval5), .input6(gateval6), .input7(gateval7), .input8(gateval8),
    .input9(gateval9), .input10(gateval10), .input11(gateval11), .input12(gateval12), .input13(gateval13),
    .input14(gateval14), .input15(gateval15), .input16(gateval16), .input17(gateval17), .input18(gateval18),
    .input19(gateval19), .input20(gateval20), .input21(gateval21), .input22(gateval22), .input23(gateval23),
    .input24(gateval24), .input25(gateval25), .input26(gateval26), .input27(gateval27), .input28(gateval28),
    .input29(gateval29), .input30(gateval30), .input31(gateval31), .input32(gateval32), .input33(gateval33),
    .input34(gateval34), .input35(gateval35), .input36(gateval36), .input37(gateval37), .input38(gateval38),
    .input39(gateval39), .input40(gateval40), .input41(gateval41), .input42(gateval42), .input43(gateval43),
    .input44(gateval44), .input45(gateval45), .input46(gateval46), .input47(gateval47), .input48(gateval48),
    .input49(gateval49), .input50(gateval50), .input51(gateval51), .input52(gateval52), .input53(gateval53),
    .input54(gateval54), .input55(gateval55), .input56(gateval56), .input57(gateval57), .input58(gateval58),
    .input59(gateval59), .input60(gateval60), .input61(gateval61), .input62(gateval62), .input63(gateval63),
    .input64(gateval64), .output1(argval23A), .output2(argval23B));
  muxselector muxselector_24 (
    .direct1(direct24A), .direct2(direct24B), .input1(gateval1), .input2(gateval2), .input3(gateval3),
    .input4(gateval4), .input5(gateval5), .input6(gateval6), .input7(gateval7), .input8(gateval8),
    .input9(gateval9), .input10(gateval10), .input11(gateval11), .input12(gateval12), .input13(gateval13),
    .input14(gateval14), .input15(gateval15), .input16(gateval16), .input17(gateval17), .input18(gateval18),
    .input19(gateval19), .input20(gateval20), .input21(gateval21), .input22(gateval22), .input23(gateval23),
    .input24(gateval24), .input25(gateval25), .input26(gateval26), .input27(gateval27), .input28(gateval28),
    .input29(gateval29), .input30(gateval30), .input31(gateval31), .input32(gateval32), .input33(gateval33),
    .input34(gateval34), .input35(gateval35), .input36(gateval36), .input37(gateval37), .input38(gateval38),
    .input39(gateval39), .input40(gateval40), .input41(gateval41), .input42(gateval42), .input43(gateval43),
    .input44(gateval44), .input45(gateval45), .input46(gateval46), .input47(gateval47), .input48(gateval48),
    .input49(gateval49), .input50(gateval50), .input51(gateval51), .input52(gateval52), .input53(gateval53),
    .input54(gateval54), .input55(gateval55), .input56(gateval56), .input57(gateval57), .input58(gateval58),
    .input59(gateval59), .input60(gateval60), .input61(gateval61), .input62(gateval62), .input63(gateval63),
    .input64(gateval64), .output1(argval24A), .output2(argval24B));
  muxselector muxselector_25 (
    .direct1(direct25A), .direct2(direct25B), .input1(gateval1), .input2(gateval2), .input3(gateval3),
    .input4(gateval4), .input5(gateval5), .input6(gateval6), .input7(gateval7), .input8(gateval8),
    .input9(gateval9), .input10(gateval10), .input11(gateval11), .input12(gateval12), .input13(gateval13),
    .input14(gateval14), .input15(gateval15), .input16(gateval16), .input17(gateval17), .input18(gateval18),
    .input19(gateval19), .input20(gateval20), .input21(gateval21), .input22(gateval22), .input23(gateval23),
    .input24(gateval24), .input25(gateval25), .input26(gateval26), .input27(gateval27), .input28(gateval28),
    .input29(gateval29), .input30(gateval30), .input31(gateval31), .input32(gateval32), .input33(gateval33),
    .input34(gateval34), .input35(gateval35), .input36(gateval36), .input37(gateval37), .input38(gateval38),
    .input39(gateval39), .input40(gateval40), .input41(gateval41), .input42(gateval42), .input43(gateval43),
    .input44(gateval44), .input45(gateval45), .input46(gateval46), .input47(gateval47), .input48(gateval48),
    .input49(gateval49), .input50(gateval50), .input51(gateval51), .input52(gateval52), .input53(gateval53),
    .input54(gateval54), .input55(gateval55), .input56(gateval56), .input57(gateval57), .input58(gateval58),
    .input59(gateval59), .input60(gateval60), .input61(gateval61), .input62(gateval62), .input63(gateval63),
    .input64(gateval64), .output1(argval25A), .output2(argval25B));
  muxselector muxselector_26 (
    .direct1(direct26A), .direct2(direct26B), .input1(gateval1), .input2(gateval2), .input3(gateval3),
    .input4(gateval4), .input5(gateval5), .input6(gateval6), .input7(gateval7), .input8(gateval8),
    .input9(gateval9), .input10(gateval10), .input11(gateval11), .input12(gateval12), .input13(gateval13),
    .input14(gateval14), .input15(gateval15), .input16(gateval16), .input17(gateval17), .input18(gateval18),
    .input19(gateval19), .input20(gateval20), .input21(gateval21), .input22(gateval22), .input23(gateval23),
    .input24(gateval24), .input25(gateval25), .input26(gateval26), .input27(gateval27), .input28(gateval28),
    .input29(gateval29), .input30(gateval30), .input31(gateval31), .input32(gateval32), .input33(gateval33),
    .input34(gateval34), .input35(gateval35), .input36(gateval36), .input37(gateval37), .input38(gateval38),
    .input39(gateval39), .input40(gateval40), .input41(gateval41), .input42(gateval42), .input43(gateval43),
    .input44(gateval44), .input45(gateval45), .input46(gateval46), .input47(gateval47), .input48(gateval48),
    .input49(gateval49), .input50(gateval50), .input51(gateval51), .input52(gateval52), .input53(gateval53),
    .input54(gateval54), .input55(gateval55), .input56(gateval56), .input57(gateval57), .input58(gateval58),
    .input59(gateval59), .input60(gateval60), .input61(gateval61), .input62(gateval62), .input63(gateval63),
    .input64(gateval64), .output1(argval26A), .output2(argval26B));
  muxselector muxselector_27 (
    .direct1(direct27A), .direct2(direct27B), .input1(gateval1), .input2(gateval2), .input3(gateval3),
    .input4(gateval4), .input5(gateval5), .input6(gateval6), .input7(gateval7), .input8(gateval8),
    .input9(gateval9), .input10(gateval10), .input11(gateval11), .input12(gateval12), .input13(gateval13),
    .input14(gateval14), .input15(gateval15), .input16(gateval16), .input17(gateval17), .input18(gateval18),
    .input19(gateval19), .input20(gateval20), .input21(gateval21), .input22(gateval22), .input23(gateval23),
    .input24(gateval24), .input25(gateval25), .input26(gateval26), .input27(gateval27), .input28(gateval28),
    .input29(gateval29), .input30(gateval30), .input31(gateval31), .input32(gateval32), .input33(gateval33),
    .input34(gateval34), .input35(gateval35), .input36(gateval36), .input37(gateval37), .input38(gateval38),
    .input39(gateval39), .input40(gateval40), .input41(gateval41), .input42(gateval42), .input43(gateval43),
    .input44(gateval44), .input45(gateval45), .input46(gateval46), .input47(gateval47), .input48(gateval48),
    .input49(gateval49), .input50(gateval50), .input51(gateval51), .input52(gateval52), .input53(gateval53),
    .input54(gateval54), .input55(gateval55), .input56(gateval56), .input57(gateval57), .input58(gateval58),
    .input59(gateval59), .input60(gateval60), .input61(gateval61), .input62(gateval62), .input63(gateval63),
    .input64(gateval64), .output1(argval27A), .output2(argval27B));
  muxselector muxselector_28 (
    .direct1(direct28A), .direct2(direct28B), .input1(gateval1), .input2(gateval2), .input3(gateval3),
    .input4(gateval4), .input5(gateval5), .input6(gateval6), .input7(gateval7), .input8(gateval8),
    .input9(gateval9), .input10(gateval10), .input11(gateval11), .input12(gateval12), .input13(gateval13),
    .input14(gateval14), .input15(gateval15), .input16(gateval16), .input17(gateval17), .input18(gateval18),
    .input19(gateval19), .input20(gateval20), .input21(gateval21), .input22(gateval22), .input23(gateval23),
    .input24(gateval24), .input25(gateval25), .input26(gateval26), .input27(gateval27), .input28(gateval28),
    .input29(gateval29), .input30(gateval30), .input31(gateval31), .input32(gateval32), .input33(gateval33),
    .input34(gateval34), .input35(gateval35), .input36(gateval36), .input37(gateval37), .input38(gateval38),
    .input39(gateval39), .input40(gateval40), .input41(gateval41), .input42(gateval42), .input43(gateval43),
    .input44(gateval44), .input45(gateval45), .input46(gateval46), .input47(gateval47), .input48(gateval48),
    .input49(gateval49), .input50(gateval50), .input51(gateval51), .input52(gateval52), .input53(gateval53),
    .input54(gateval54), .input55(gateval55), .input56(gateval56), .input57(gateval57), .input58(gateval58),
    .input59(gateval59), .input60(gateval60), .input61(gateval61), .input62(gateval62), .input63(gateval63),
    .input64(gateval64), .output1(argval28A), .output2(argval28B));
  muxselector muxselector_29 (
    .direct1(direct29A), .direct2(direct29B), .input1(gateval1), .input2(gateval2), .input3(gateval3),
    .input4(gateval4), .input5(gateval5), .input6(gateval6), .input7(gateval7), .input8(gateval8),
    .input9(gateval9), .input10(gateval10), .input11(gateval11), .input12(gateval12), .input13(gateval13),
    .input14(gateval14), .input15(gateval15), .input16(gateval16), .input17(gateval17), .input18(gateval18),
    .input19(gateval19), .input20(gateval20), .input21(gateval21), .input22(gateval22), .input23(gateval23),
    .input24(gateval24), .input25(gateval25), .input26(gateval26), .input27(gateval27), .input28(gateval28),
    .input29(gateval29), .input30(gateval30), .input31(gateval31), .input32(gateval32), .input33(gateval33),
    .input34(gateval34), .input35(gateval35), .input36(gateval36), .input37(gateval37), .input38(gateval38),
    .input39(gateval39), .input40(gateval40), .input41(gateval41), .input42(gateval42), .input43(gateval43),
    .input44(gateval44), .input45(gateval45), .input46(gateval46), .input47(gateval47), .input48(gateval48),
    .input49(gateval49), .input50(gateval50), .input51(gateval51), .input52(gateval52), .input53(gateval53),
    .input54(gateval54), .input55(gateval55), .input56(gateval56), .input57(gateval57), .input58(gateval58),
    .input59(gateval59), .input60(gateval60), .input61(gateval61), .input62(gateval62), .input63(gateval63),
    .input64(gateval64), .output1(argval29A), .output2(argval29B));
  muxselector muxselector_30 (
    .direct1(direct30A), .direct2(direct30B), .input1(gateval1), .input2(gateval2), .input3(gateval3),
    .input4(gateval4), .input5(gateval5), .input6(gateval6), .input7(gateval7), .input8(gateval8),
    .input9(gateval9), .input10(gateval10), .input11(gateval11), .input12(gateval12), .input13(gateval13),
    .input14(gateval14), .input15(gateval15), .input16(gateval16), .input17(gateval17), .input18(gateval18),
    .input19(gateval19), .input20(gateval20), .input21(gateval21), .input22(gateval22), .input23(gateval23),
    .input24(gateval24), .input25(gateval25), .input26(gateval26), .input27(gateval27), .input28(gateval28),
    .input29(gateval29), .input30(gateval30), .input31(gateval31), .input32(gateval32), .input33(gateval33),
    .input34(gateval34), .input35(gateval35), .input36(gateval36), .input37(gateval37), .input38(gateval38),
    .input39(gateval39), .input40(gateval40), .input41(gateval41), .input42(gateval42), .input43(gateval43),
    .input44(gateval44), .input45(gateval45), .input46(gateval46), .input47(gateval47), .input48(gateval48),
    .input49(gateval49), .input50(gateval50), .input51(gateval51), .input52(gateval52), .input53(gateval53),
    .input54(gateval54), .input55(gateval55), .input56(gateval56), .input57(gateval57), .input58(gateval58),
    .input59(gateval59), .input60(gateval60), .input61(gateval61), .input62(gateval62), .input63(gateval63),
    .input64(gateval64), .output1(argval30A), .output2(argval30B));
  muxselector muxselector_31 (
    .direct1(direct31A), .direct2(direct31B), .input1(gateval1), .input2(gateval2), .input3(gateval3),
    .input4(gateval4), .input5(gateval5), .input6(gateval6), .input7(gateval7), .input8(gateval8),
    .input9(gateval9), .input10(gateval10), .input11(gateval11), .input12(gateval12), .input13(gateval13),
    .input14(gateval14), .input15(gateval15), .input16(gateval16), .input17(gateval17), .input18(gateval18),
    .input19(gateval19), .input20(gateval20), .input21(gateval21), .input22(gateval22), .input23(gateval23),
    .input24(gateval24), .input25(gateval25), .input26(gateval26), .input27(gateval27), .input28(gateval28),
    .input29(gateval29), .input30(gateval30), .input31(gateval31), .input32(gateval32), .input33(gateval33),
    .input34(gateval34), .input35(gateval35), .input36(gateval36), .input37(gateval37), .input38(gateval38),
    .input39(gateval39), .input40(gateval40), .input41(gateval41), .input42(gateval42), .input43(gateval43),
    .input44(gateval44), .input45(gateval45), .input46(gateval46), .input47(gateval47), .input48(gateval48),
    .input49(gateval49), .input50(gateval50), .input51(gateval51), .input52(gateval52), .input53(gateval53),
    .input54(gateval54), .input55(gateval55), .input56(gateval56), .input57(gateval57), .input58(gateval58),
    .input59(gateval59), .input60(gateval60), .input61(gateval61), .input62(gateval62), .input63(gateval63),
    .input64(gateval64), .output1(argval31A), .output2(argval31B));
  muxselector muxselector_32 (
    .direct1(direct32A), .direct2(direct32B), .input1(gateval1), .input2(gateval2), .input3(gateval3),
    .input4(gateval4), .input5(gateval5), .input6(gateval6), .input7(gateval7), .input8(gateval8),
    .input9(gateval9), .input10(gateval10), .input11(gateval11), .input12(gateval12), .input13(gateval13),
    .input14(gateval14), .input15(gateval15), .input16(gateval16), .input17(gateval17), .input18(gateval18),
    .input19(gateval19), .input20(gateval20), .input21(gateval21), .input22(gateval22), .input23(gateval23),
    .input24(gateval24), .input25(gateval25), .input26(gateval26), .input27(gateval27), .input28(gateval28),
    .input29(gateval29), .input30(gateval30), .input31(gateval31), .input32(gateval32), .input33(gateval33),
    .input34(gateval34), .input35(gateval35), .input36(gateval36), .input37(gateval37), .input38(gateval38),
    .input39(gateval39), .input40(gateval40), .input41(gateval41), .input42(gateval42), .input43(gateval43),
    .input44(gateval44), .input45(gateval45), .input46(gateval46), .input47(gateval47), .input48(gateval48),
    .input49(gateval49), .input50(gateval50), .input51(gateval51), .input52(gateval52), .input53(gateval53),
    .input54(gateval54), .input55(gateval55), .input56(gateval56), .input57(gateval57), .input58(gateval58),
    .input59(gateval59), .input60(gateval60), .input61(gateval61), .input62(gateval62), .input63(gateval63),
    .input64(gateval64), .output1(argval32A), .output2(argval32B));
  muxselector muxselector_33 (
    .direct1(direct33A), .direct2(direct33B), .input1(gateval1), .input2(gateval2), .input3(gateval3),
    .input4(gateval4), .input5(gateval5), .input6(gateval6), .input7(gateval7), .input8(gateval8),
    .input9(gateval9), .input10(gateval10), .input11(gateval11), .input12(gateval12), .input13(gateval13),
    .input14(gateval14), .input15(gateval15), .input16(gateval16), .input17(gateval17), .input18(gateval18),
    .input19(gateval19), .input20(gateval20), .input21(gateval21), .input22(gateval22), .input23(gateval23),
    .input24(gateval24), .input25(gateval25), .input26(gateval26), .input27(gateval27), .input28(gateval28),
    .input29(gateval29), .input30(gateval30), .input31(gateval31), .input32(gateval32), .input33(gateval33),
    .input34(gateval34), .input35(gateval35), .input36(gateval36), .input37(gateval37), .input38(gateval38),
    .input39(gateval39), .input40(gateval40), .input41(gateval41), .input42(gateval42), .input43(gateval43),
    .input44(gateval44), .input45(gateval45), .input46(gateval46), .input47(gateval47), .input48(gateval48),
    .input49(gateval49), .input50(gateval50), .input51(gateval51), .input52(gateval52), .input53(gateval53),
    .input54(gateval54), .input55(gateval55), .input56(gateval56), .input57(gateval57), .input58(gateval58),
    .input59(gateval59), .input60(gateval60), .input61(gateval61), .input62(gateval62), .input63(gateval63),
    .input64(gateval64), .output1(argval33A), .output2(argval33B));
  muxselector muxselector_34 (
    .direct1(direct34A), .direct2(direct34B), .input1(gateval1), .input2(gateval2), .input3(gateval3),
    .input4(gateval4), .input5(gateval5), .input6(gateval6), .input7(gateval7), .input8(gateval8),
    .input9(gateval9), .input10(gateval10), .input11(gateval11), .input12(gateval12), .input13(gateval13),
    .input14(gateval14), .input15(gateval15), .input16(gateval16), .input17(gateval17), .input18(gateval18),
    .input19(gateval19), .input20(gateval20), .input21(gateval21), .input22(gateval22), .input23(gateval23),
    .input24(gateval24), .input25(gateval25), .input26(gateval26), .input27(gateval27), .input28(gateval28),
    .input29(gateval29), .input30(gateval30), .input31(gateval31), .input32(gateval32), .input33(gateval33),
    .input34(gateval34), .input35(gateval35), .input36(gateval36), .input37(gateval37), .input38(gateval38),
    .input39(gateval39), .input40(gateval40), .input41(gateval41), .input42(gateval42), .input43(gateval43),
    .input44(gateval44), .input45(gateval45), .input46(gateval46), .input47(gateval47), .input48(gateval48),
    .input49(gateval49), .input50(gateval50), .input51(gateval51), .input52(gateval52), .input53(gateval53),
    .input54(gateval54), .input55(gateval55), .input56(gateval56), .input57(gateval57), .input58(gateval58),
    .input59(gateval59), .input60(gateval60), .input61(gateval61), .input62(gateval62), .input63(gateval63),
    .input64(gateval64), .output1(argval34A), .output2(argval34B));
  muxselector muxselector_35 (
    .direct1(direct35A), .direct2(direct35B), .input1(gateval1), .input2(gateval2), .input3(gateval3),
    .input4(gateval4), .input5(gateval5), .input6(gateval6), .input7(gateval7), .input8(gateval8),
    .input9(gateval9), .input10(gateval10), .input11(gateval11), .input12(gateval12), .input13(gateval13),
    .input14(gateval14), .input15(gateval15), .input16(gateval16), .input17(gateval17), .input18(gateval18),
    .input19(gateval19), .input20(gateval20), .input21(gateval21), .input22(gateval22), .input23(gateval23),
    .input24(gateval24), .input25(gateval25), .input26(gateval26), .input27(gateval27), .input28(gateval28),
    .input29(gateval29), .input30(gateval30), .input31(gateval31), .input32(gateval32), .input33(gateval33),
    .input34(gateval34), .input35(gateval35), .input36(gateval36), .input37(gateval37), .input38(gateval38),
    .input39(gateval39), .input40(gateval40), .input41(gateval41), .input42(gateval42), .input43(gateval43),
    .input44(gateval44), .input45(gateval45), .input46(gateval46), .input47(gateval47), .input48(gateval48),
    .input49(gateval49), .input50(gateval50), .input51(gateval51), .input52(gateval52), .input53(gateval53),
    .input54(gateval54), .input55(gateval55), .input56(gateval56), .input57(gateval57), .input58(gateval58),
    .input59(gateval59), .input60(gateval60), .input61(gateval61), .input62(gateval62), .input63(gateval63),
    .input64(gateval64), .output1(argval35A), .output2(argval35B));
  muxselector muxselector_36 (
    .direct1(direct36A), .direct2(direct36B), .input1(gateval1), .input2(gateval2), .input3(gateval3),
    .input4(gateval4), .input5(gateval5), .input6(gateval6), .input7(gateval7), .input8(gateval8),
    .input9(gateval9), .input10(gateval10), .input11(gateval11), .input12(gateval12), .input13(gateval13),
    .input14(gateval14), .input15(gateval15), .input16(gateval16), .input17(gateval17), .input18(gateval18),
    .input19(gateval19), .input20(gateval20), .input21(gateval21), .input22(gateval22), .input23(gateval23),
    .input24(gateval24), .input25(gateval25), .input26(gateval26), .input27(gateval27), .input28(gateval28),
    .input29(gateval29), .input30(gateval30), .input31(gateval31), .input32(gateval32), .input33(gateval33),
    .input34(gateval34), .input35(gateval35), .input36(gateval36), .input37(gateval37), .input38(gateval38),
    .input39(gateval39), .input40(gateval40), .input41(gateval41), .input42(gateval42), .input43(gateval43),
    .input44(gateval44), .input45(gateval45), .input46(gateval46), .input47(gateval47), .input48(gateval48),
    .input49(gateval49), .input50(gateval50), .input51(gateval51), .input52(gateval52), .input53(gateval53),
    .input54(gateval54), .input55(gateval55), .input56(gateval56), .input57(gateval57), .input58(gateval58),
    .input59(gateval59), .input60(gateval60), .input61(gateval61), .input62(gateval62), .input63(gateval63),
    .input64(gateval64), .output1(argval36A), .output2(argval36B));
  muxselector muxselector_37 (
    .direct1(direct37A), .direct2(direct37B), .input1(gateval1), .input2(gateval2), .input3(gateval3),
    .input4(gateval4), .input5(gateval5), .input6(gateval6), .input7(gateval7), .input8(gateval8),
    .input9(gateval9), .input10(gateval10), .input11(gateval11), .input12(gateval12), .input13(gateval13),
    .input14(gateval14), .input15(gateval15), .input16(gateval16), .input17(gateval17), .input18(gateval18),
    .input19(gateval19), .input20(gateval20), .input21(gateval21), .input22(gateval22), .input23(gateval23),
    .input24(gateval24), .input25(gateval25), .input26(gateval26), .input27(gateval27), .input28(gateval28),
    .input29(gateval29), .input30(gateval30), .input31(gateval31), .input32(gateval32), .input33(gateval33),
    .input34(gateval34), .input35(gateval35), .input36(gateval36), .input37(gateval37), .input38(gateval38),
    .input39(gateval39), .input40(gateval40), .input41(gateval41), .input42(gateval42), .input43(gateval43),
    .input44(gateval44), .input45(gateval45), .input46(gateval46), .input47(gateval47), .input48(gateval48),
    .input49(gateval49), .input50(gateval50), .input51(gateval51), .input52(gateval52), .input53(gateval53),
    .input54(gateval54), .input55(gateval55), .input56(gateval56), .input57(gateval57), .input58(gateval58),
    .input59(gateval59), .input60(gateval60), .input61(gateval61), .input62(gateval62), .input63(gateval63),
    .input64(gateval64), .output1(argval37A), .output2(argval37B));
  muxselector muxselector_38 (
    .direct1(direct38A), .direct2(direct38B), .input1(gateval1), .input2(gateval2), .input3(gateval3),
    .input4(gateval4), .input5(gateval5), .input6(gateval6), .input7(gateval7), .input8(gateval8),
    .input9(gateval9), .input10(gateval10), .input11(gateval11), .input12(gateval12), .input13(gateval13),
    .input14(gateval14), .input15(gateval15), .input16(gateval16), .input17(gateval17), .input18(gateval18),
    .input19(gateval19), .input20(gateval20), .input21(gateval21), .input22(gateval22), .input23(gateval23),
    .input24(gateval24), .input25(gateval25), .input26(gateval26), .input27(gateval27), .input28(gateval28),
    .input29(gateval29), .input30(gateval30), .input31(gateval31), .input32(gateval32), .input33(gateval33),
    .input34(gateval34), .input35(gateval35), .input36(gateval36), .input37(gateval37), .input38(gateval38),
    .input39(gateval39), .input40(gateval40), .input41(gateval41), .input42(gateval42), .input43(gateval43),
    .input44(gateval44), .input45(gateval45), .input46(gateval46), .input47(gateval47), .input48(gateval48),
    .input49(gateval49), .input50(gateval50), .input51(gateval51), .input52(gateval52), .input53(gateval53),
    .input54(gateval54), .input55(gateval55), .input56(gateval56), .input57(gateval57), .input58(gateval58),
    .input59(gateval59), .input60(gateval60), .input61(gateval61), .input62(gateval62), .input63(gateval63),
    .input64(gateval64), .output1(argval38A), .output2(argval38B));
  muxselector muxselector_39 (
    .direct1(direct39A), .direct2(direct39B), .input1(gateval1), .input2(gateval2), .input3(gateval3),
    .input4(gateval4), .input5(gateval5), .input6(gateval6), .input7(gateval7), .input8(gateval8),
    .input9(gateval9), .input10(gateval10), .input11(gateval11), .input12(gateval12), .input13(gateval13),
    .input14(gateval14), .input15(gateval15), .input16(gateval16), .input17(gateval17), .input18(gateval18),
    .input19(gateval19), .input20(gateval20), .input21(gateval21), .input22(gateval22), .input23(gateval23),
    .input24(gateval24), .input25(gateval25), .input26(gateval26), .input27(gateval27), .input28(gateval28),
    .input29(gateval29), .input30(gateval30), .input31(gateval31), .input32(gateval32), .input33(gateval33),
    .input34(gateval34), .input35(gateval35), .input36(gateval36), .input37(gateval37), .input38(gateval38),
    .input39(gateval39), .input40(gateval40), .input41(gateval41), .input42(gateval42), .input43(gateval43),
    .input44(gateval44), .input45(gateval45), .input46(gateval46), .input47(gateval47), .input48(gateval48),
    .input49(gateval49), .input50(gateval50), .input51(gateval51), .input52(gateval52), .input53(gateval53),
    .input54(gateval54), .input55(gateval55), .input56(gateval56), .input57(gateval57), .input58(gateval58),
    .input59(gateval59), .input60(gateval60), .input61(gateval61), .input62(gateval62), .input63(gateval63),
    .input64(gateval64), .output1(argval39A), .output2(argval39B));
  muxselector muxselector_40 (
    .direct1(direct40A), .direct2(direct40B), .input1(gateval1), .input2(gateval2), .input3(gateval3),
    .input4(gateval4), .input5(gateval5), .input6(gateval6), .input7(gateval7), .input8(gateval8),
    .input9(gateval9), .input10(gateval10), .input11(gateval11), .input12(gateval12), .input13(gateval13),
    .input14(gateval14), .input15(gateval15), .input16(gateval16), .input17(gateval17), .input18(gateval18),
    .input19(gateval19), .input20(gateval20), .input21(gateval21), .input22(gateval22), .input23(gateval23),
    .input24(gateval24), .input25(gateval25), .input26(gateval26), .input27(gateval27), .input28(gateval28),
    .input29(gateval29), .input30(gateval30), .input31(gateval31), .input32(gateval32), .input33(gateval33),
    .input34(gateval34), .input35(gateval35), .input36(gateval36), .input37(gateval37), .input38(gateval38),
    .input39(gateval39), .input40(gateval40), .input41(gateval41), .input42(gateval42), .input43(gateval43),
    .input44(gateval44), .input45(gateval45), .input46(gateval46), .input47(gateval47), .input48(gateval48),
    .input49(gateval49), .input50(gateval50), .input51(gateval51), .input52(gateval52), .input53(gateval53),
    .input54(gateval54), .input55(gateval55), .input56(gateval56), .input57(gateval57), .input58(gateval58),
    .input59(gateval59), .input60(gateval60), .input61(gateval61), .input62(gateval62), .input63(gateval63),
    .input64(gateval64), .output1(argval40A), .output2(argval40B));
  muxselector muxselector_41 (
    .direct1(direct41A), .direct2(direct41B), .input1(gateval1), .input2(gateval2), .input3(gateval3),
    .input4(gateval4), .input5(gateval5), .input6(gateval6), .input7(gateval7), .input8(gateval8),
    .input9(gateval9), .input10(gateval10), .input11(gateval11), .input12(gateval12), .input13(gateval13),
    .input14(gateval14), .input15(gateval15), .input16(gateval16), .input17(gateval17), .input18(gateval18),
    .input19(gateval19), .input20(gateval20), .input21(gateval21), .input22(gateval22), .input23(gateval23),
    .input24(gateval24), .input25(gateval25), .input26(gateval26), .input27(gateval27), .input28(gateval28),
    .input29(gateval29), .input30(gateval30), .input31(gateval31), .input32(gateval32), .input33(gateval33),
    .input34(gateval34), .input35(gateval35), .input36(gateval36), .input37(gateval37), .input38(gateval38),
    .input39(gateval39), .input40(gateval40), .input41(gateval41), .input42(gateval42), .input43(gateval43),
    .input44(gateval44), .input45(gateval45), .input46(gateval46), .input47(gateval47), .input48(gateval48),
    .input49(gateval49), .input50(gateval50), .input51(gateval51), .input52(gateval52), .input53(gateval53),
    .input54(gateval54), .input55(gateval55), .input56(gateval56), .input57(gateval57), .input58(gateval58),
    .input59(gateval59), .input60(gateval60), .input61(gateval61), .input62(gateval62), .input63(gateval63),
    .input64(gateval64), .output1(argval41A), .output2(argval41B));
  muxselector muxselector_42 (
    .direct1(direct42A), .direct2(direct42B), .input1(gateval1), .input2(gateval2), .input3(gateval3),
    .input4(gateval4), .input5(gateval5), .input6(gateval6), .input7(gateval7), .input8(gateval8),
    .input9(gateval9), .input10(gateval10), .input11(gateval11), .input12(gateval12), .input13(gateval13),
    .input14(gateval14), .input15(gateval15), .input16(gateval16), .input17(gateval17), .input18(gateval18),
    .input19(gateval19), .input20(gateval20), .input21(gateval21), .input22(gateval22), .input23(gateval23),
    .input24(gateval24), .input25(gateval25), .input26(gateval26), .input27(gateval27), .input28(gateval28),
    .input29(gateval29), .input30(gateval30), .input31(gateval31), .input32(gateval32), .input33(gateval33),
    .input34(gateval34), .input35(gateval35), .input36(gateval36), .input37(gateval37), .input38(gateval38),
    .input39(gateval39), .input40(gateval40), .input41(gateval41), .input42(gateval42), .input43(gateval43),
    .input44(gateval44), .input45(gateval45), .input46(gateval46), .input47(gateval47), .input48(gateval48),
    .input49(gateval49), .input50(gateval50), .input51(gateval51), .input52(gateval52), .input53(gateval53),
    .input54(gateval54), .input55(gateval55), .input56(gateval56), .input57(gateval57), .input58(gateval58),
    .input59(gateval59), .input60(gateval60), .input61(gateval61), .input62(gateval62), .input63(gateval63),
    .input64(gateval64), .output1(argval42A), .output2(argval42B));
  muxselector muxselector_43 (
    .direct1(direct43A), .direct2(direct43B), .input1(gateval1), .input2(gateval2), .input3(gateval3),
    .input4(gateval4), .input5(gateval5), .input6(gateval6), .input7(gateval7), .input8(gateval8),
    .input9(gateval9), .input10(gateval10), .input11(gateval11), .input12(gateval12), .input13(gateval13),
    .input14(gateval14), .input15(gateval15), .input16(gateval16), .input17(gateval17), .input18(gateval18),
    .input19(gateval19), .input20(gateval20), .input21(gateval21), .input22(gateval22), .input23(gateval23),
    .input24(gateval24), .input25(gateval25), .input26(gateval26), .input27(gateval27), .input28(gateval28),
    .input29(gateval29), .input30(gateval30), .input31(gateval31), .input32(gateval32), .input33(gateval33),
    .input34(gateval34), .input35(gateval35), .input36(gateval36), .input37(gateval37), .input38(gateval38),
    .input39(gateval39), .input40(gateval40), .input41(gateval41), .input42(gateval42), .input43(gateval43),
    .input44(gateval44), .input45(gateval45), .input46(gateval46), .input47(gateval47), .input48(gateval48),
    .input49(gateval49), .input50(gateval50), .input51(gateval51), .input52(gateval52), .input53(gateval53),
    .input54(gateval54), .input55(gateval55), .input56(gateval56), .input57(gateval57), .input58(gateval58),
    .input59(gateval59), .input60(gateval60), .input61(gateval61), .input62(gateval62), .input63(gateval63),
    .input64(gateval64), .output1(argval43A), .output2(argval43B));
  muxselector muxselector_44 (
    .direct1(direct44A), .direct2(direct44B), .input1(gateval1), .input2(gateval2), .input3(gateval3),
    .input4(gateval4), .input5(gateval5), .input6(gateval6), .input7(gateval7), .input8(gateval8),
    .input9(gateval9), .input10(gateval10), .input11(gateval11), .input12(gateval12), .input13(gateval13),
    .input14(gateval14), .input15(gateval15), .input16(gateval16), .input17(gateval17), .input18(gateval18),
    .input19(gateval19), .input20(gateval20), .input21(gateval21), .input22(gateval22), .input23(gateval23),
    .input24(gateval24), .input25(gateval25), .input26(gateval26), .input27(gateval27), .input28(gateval28),
    .input29(gateval29), .input30(gateval30), .input31(gateval31), .input32(gateval32), .input33(gateval33),
    .input34(gateval34), .input35(gateval35), .input36(gateval36), .input37(gateval37), .input38(gateval38),
    .input39(gateval39), .input40(gateval40), .input41(gateval41), .input42(gateval42), .input43(gateval43),
    .input44(gateval44), .input45(gateval45), .input46(gateval46), .input47(gateval47), .input48(gateval48),
    .input49(gateval49), .input50(gateval50), .input51(gateval51), .input52(gateval52), .input53(gateval53),
    .input54(gateval54), .input55(gateval55), .input56(gateval56), .input57(gateval57), .input58(gateval58),
    .input59(gateval59), .input60(gateval60), .input61(gateval61), .input62(gateval62), .input63(gateval63),
    .input64(gateval64), .output1(argval44A), .output2(argval44B));
  muxselector muxselector_45 (
    .direct1(direct45A), .direct2(direct45B), .input1(gateval1), .input2(gateval2), .input3(gateval3),
    .input4(gateval4), .input5(gateval5), .input6(gateval6), .input7(gateval7), .input8(gateval8),
    .input9(gateval9), .input10(gateval10), .input11(gateval11), .input12(gateval12), .input13(gateval13),
    .input14(gateval14), .input15(gateval15), .input16(gateval16), .input17(gateval17), .input18(gateval18),
    .input19(gateval19), .input20(gateval20), .input21(gateval21), .input22(gateval22), .input23(gateval23),
    .input24(gateval24), .input25(gateval25), .input26(gateval26), .input27(gateval27), .input28(gateval28),
    .input29(gateval29), .input30(gateval30), .input31(gateval31), .input32(gateval32), .input33(gateval33),
    .input34(gateval34), .input35(gateval35), .input36(gateval36), .input37(gateval37), .input38(gateval38),
    .input39(gateval39), .input40(gateval40), .input41(gateval41), .input42(gateval42), .input43(gateval43),
    .input44(gateval44), .input45(gateval45), .input46(gateval46), .input47(gateval47), .input48(gateval48),
    .input49(gateval49), .input50(gateval50), .input51(gateval51), .input52(gateval52), .input53(gateval53),
    .input54(gateval54), .input55(gateval55), .input56(gateval56), .input57(gateval57), .input58(gateval58),
    .input59(gateval59), .input60(gateval60), .input61(gateval61), .input62(gateval62), .input63(gateval63),
    .input64(gateval64), .output1(argval45A), .output2(argval45B));
  muxselector muxselector_46 (
    .direct1(direct46A), .direct2(direct46B), .input1(gateval1), .input2(gateval2), .input3(gateval3),
    .input4(gateval4), .input5(gateval5), .input6(gateval6), .input7(gateval7), .input8(gateval8),
    .input9(gateval9), .input10(gateval10), .input11(gateval11), .input12(gateval12), .input13(gateval13),
    .input14(gateval14), .input15(gateval15), .input16(gateval16), .input17(gateval17), .input18(gateval18),
    .input19(gateval19), .input20(gateval20), .input21(gateval21), .input22(gateval22), .input23(gateval23),
    .input24(gateval24), .input25(gateval25), .input26(gateval26), .input27(gateval27), .input28(gateval28),
    .input29(gateval29), .input30(gateval30), .input31(gateval31), .input32(gateval32), .input33(gateval33),
    .input34(gateval34), .input35(gateval35), .input36(gateval36), .input37(gateval37), .input38(gateval38),
    .input39(gateval39), .input40(gateval40), .input41(gateval41), .input42(gateval42), .input43(gateval43),
    .input44(gateval44), .input45(gateval45), .input46(gateval46), .input47(gateval47), .input48(gateval48),
    .input49(gateval49), .input50(gateval50), .input51(gateval51), .input52(gateval52), .input53(gateval53),
    .input54(gateval54), .input55(gateval55), .input56(gateval56), .input57(gateval57), .input58(gateval58),
    .input59(gateval59), .input60(gateval60), .input61(gateval61), .input62(gateval62), .input63(gateval63),
    .input64(gateval64), .output1(argval46A), .output2(argval46B));
  muxselector muxselector_47 (
    .direct1(direct47A), .direct2(direct47B), .input1(gateval1), .input2(gateval2), .input3(gateval3),
    .input4(gateval4), .input5(gateval5), .input6(gateval6), .input7(gateval7), .input8(gateval8),
    .input9(gateval9), .input10(gateval10), .input11(gateval11), .input12(gateval12), .input13(gateval13),
    .input14(gateval14), .input15(gateval15), .input16(gateval16), .input17(gateval17), .input18(gateval18),
    .input19(gateval19), .input20(gateval20), .input21(gateval21), .input22(gateval22), .input23(gateval23),
    .input24(gateval24), .input25(gateval25), .input26(gateval26), .input27(gateval27), .input28(gateval28),
    .input29(gateval29), .input30(gateval30), .input31(gateval31), .input32(gateval32), .input33(gateval33),
    .input34(gateval34), .input35(gateval35), .input36(gateval36), .input37(gateval37), .input38(gateval38),
    .input39(gateval39), .input40(gateval40), .input41(gateval41), .input42(gateval42), .input43(gateval43),
    .input44(gateval44), .input45(gateval45), .input46(gateval46), .input47(gateval47), .input48(gateval48),
    .input49(gateval49), .input50(gateval50), .input51(gateval51), .input52(gateval52), .input53(gateval53),
    .input54(gateval54), .input55(gateval55), .input56(gateval56), .input57(gateval57), .input58(gateval58),
    .input59(gateval59), .input60(gateval60), .input61(gateval61), .input62(gateval62), .input63(gateval63),
    .input64(gateval64), .output1(argval47A), .output2(argval47B));
  muxselector muxselector_48 (
    .direct1(direct48A), .direct2(direct48B), .input1(gateval1), .input2(gateval2), .input3(gateval3),
    .input4(gateval4), .input5(gateval5), .input6(gateval6), .input7(gateval7), .input8(gateval8),
    .input9(gateval9), .input10(gateval10), .input11(gateval11), .input12(gateval12), .input13(gateval13),
    .input14(gateval14), .input15(gateval15), .input16(gateval16), .input17(gateval17), .input18(gateval18),
    .input19(gateval19), .input20(gateval20), .input21(gateval21), .input22(gateval22), .input23(gateval23),
    .input24(gateval24), .input25(gateval25), .input26(gateval26), .input27(gateval27), .input28(gateval28),
    .input29(gateval29), .input30(gateval30), .input31(gateval31), .input32(gateval32), .input33(gateval33),
    .input34(gateval34), .input35(gateval35), .input36(gateval36), .input37(gateval37), .input38(gateval38),
    .input39(gateval39), .input40(gateval40), .input41(gateval41), .input42(gateval42), .input43(gateval43),
    .input44(gateval44), .input45(gateval45), .input46(gateval46), .input47(gateval47), .input48(gateval48),
    .input49(gateval49), .input50(gateval50), .input51(gateval51), .input52(gateval52), .input53(gateval53),
    .input54(gateval54), .input55(gateval55), .input56(gateval56), .input57(gateval57), .input58(gateval58),
    .input59(gateval59), .input60(gateval60), .input61(gateval61), .input62(gateval62), .input63(gateval63),
    .input64(gateval64), .output1(argval48A), .output2(argval48B));
  muxselector muxselector_49 (
    .direct1(direct49A), .direct2(direct49B), .input1(gateval1), .input2(gateval2), .input3(gateval3),
    .input4(gateval4), .input5(gateval5), .input6(gateval6), .input7(gateval7), .input8(gateval8),
    .input9(gateval9), .input10(gateval10), .input11(gateval11), .input12(gateval12), .input13(gateval13),
    .input14(gateval14), .input15(gateval15), .input16(gateval16), .input17(gateval17), .input18(gateval18),
    .input19(gateval19), .input20(gateval20), .input21(gateval21), .input22(gateval22), .input23(gateval23),
    .input24(gateval24), .input25(gateval25), .input26(gateval26), .input27(gateval27), .input28(gateval28),
    .input29(gateval29), .input30(gateval30), .input31(gateval31), .input32(gateval32), .input33(gateval33),
    .input34(gateval34), .input35(gateval35), .input36(gateval36), .input37(gateval37), .input38(gateval38),
    .input39(gateval39), .input40(gateval40), .input41(gateval41), .input42(gateval42), .input43(gateval43),
    .input44(gateval44), .input45(gateval45), .input46(gateval46), .input47(gateval47), .input48(gateval48),
    .input49(gateval49), .input50(gateval50), .input51(gateval51), .input52(gateval52), .input53(gateval53),
    .input54(gateval54), .input55(gateval55), .input56(gateval56), .input57(gateval57), .input58(gateval58),
    .input59(gateval59), .input60(gateval60), .input61(gateval61), .input62(gateval62), .input63(gateval63),
    .input64(gateval64), .output1(argval49A), .output2(argval49B));
  muxselector muxselector_50 (
    .direct1(direct50A), .direct2(direct50B), .input1(gateval1), .input2(gateval2), .input3(gateval3),
    .input4(gateval4), .input5(gateval5), .input6(gateval6), .input7(gateval7), .input8(gateval8),
    .input9(gateval9), .input10(gateval10), .input11(gateval11), .input12(gateval12), .input13(gateval13),
    .input14(gateval14), .input15(gateval15), .input16(gateval16), .input17(gateval17), .input18(gateval18),
    .input19(gateval19), .input20(gateval20), .input21(gateval21), .input22(gateval22), .input23(gateval23),
    .input24(gateval24), .input25(gateval25), .input26(gateval26), .input27(gateval27), .input28(gateval28),
    .input29(gateval29), .input30(gateval30), .input31(gateval31), .input32(gateval32), .input33(gateval33),
    .input34(gateval34), .input35(gateval35), .input36(gateval36), .input37(gateval37), .input38(gateval38),
    .input39(gateval39), .input40(gateval40), .input41(gateval41), .input42(gateval42), .input43(gateval43),
    .input44(gateval44), .input45(gateval45), .input46(gateval46), .input47(gateval47), .input48(gateval48),
    .input49(gateval49), .input50(gateval50), .input51(gateval51), .input52(gateval52), .input53(gateval53),
    .input54(gateval54), .input55(gateval55), .input56(gateval56), .input57(gateval57), .input58(gateval58),
    .input59(gateval59), .input60(gateval60), .input61(gateval61), .input62(gateval62), .input63(gateval63),
    .input64(gateval64), .output1(argval50A), .output2(argval50B));
  muxselector muxselector_51 (
    .direct1(direct51A), .direct2(direct51B), .input1(gateval1), .input2(gateval2), .input3(gateval3),
    .input4(gateval4), .input5(gateval5), .input6(gateval6), .input7(gateval7), .input8(gateval8),
    .input9(gateval9), .input10(gateval10), .input11(gateval11), .input12(gateval12), .input13(gateval13),
    .input14(gateval14), .input15(gateval15), .input16(gateval16), .input17(gateval17), .input18(gateval18),
    .input19(gateval19), .input20(gateval20), .input21(gateval21), .input22(gateval22), .input23(gateval23),
    .input24(gateval24), .input25(gateval25), .input26(gateval26), .input27(gateval27), .input28(gateval28),
    .input29(gateval29), .input30(gateval30), .input31(gateval31), .input32(gateval32), .input33(gateval33),
    .input34(gateval34), .input35(gateval35), .input36(gateval36), .input37(gateval37), .input38(gateval38),
    .input39(gateval39), .input40(gateval40), .input41(gateval41), .input42(gateval42), .input43(gateval43),
    .input44(gateval44), .input45(gateval45), .input46(gateval46), .input47(gateval47), .input48(gateval48),
    .input49(gateval49), .input50(gateval50), .input51(gateval51), .input52(gateval52), .input53(gateval53),
    .input54(gateval54), .input55(gateval55), .input56(gateval56), .input57(gateval57), .input58(gateval58),
    .input59(gateval59), .input60(gateval60), .input61(gateval61), .input62(gateval62), .input63(gateval63),
    .input64(gateval64), .output1(argval51A), .output2(argval51B));
  muxselector muxselector_52 (
    .direct1(direct52A), .direct2(direct52B), .input1(gateval1), .input2(gateval2), .input3(gateval3),
    .input4(gateval4), .input5(gateval5), .input6(gateval6), .input7(gateval7), .input8(gateval8),
    .input9(gateval9), .input10(gateval10), .input11(gateval11), .input12(gateval12), .input13(gateval13),
    .input14(gateval14), .input15(gateval15), .input16(gateval16), .input17(gateval17), .input18(gateval18),
    .input19(gateval19), .input20(gateval20), .input21(gateval21), .input22(gateval22), .input23(gateval23),
    .input24(gateval24), .input25(gateval25), .input26(gateval26), .input27(gateval27), .input28(gateval28),
    .input29(gateval29), .input30(gateval30), .input31(gateval31), .input32(gateval32), .input33(gateval33),
    .input34(gateval34), .input35(gateval35), .input36(gateval36), .input37(gateval37), .input38(gateval38),
    .input39(gateval39), .input40(gateval40), .input41(gateval41), .input42(gateval42), .input43(gateval43),
    .input44(gateval44), .input45(gateval45), .input46(gateval46), .input47(gateval47), .input48(gateval48),
    .input49(gateval49), .input50(gateval50), .input51(gateval51), .input52(gateval52), .input53(gateval53),
    .input54(gateval54), .input55(gateval55), .input56(gateval56), .input57(gateval57), .input58(gateval58),
    .input59(gateval59), .input60(gateval60), .input61(gateval61), .input62(gateval62), .input63(gateval63),
    .input64(gateval64), .output1(argval52A), .output2(argval52B));
  muxselector muxselector_53 (
    .direct1(direct53A), .direct2(direct53B), .input1(gateval1), .input2(gateval2), .input3(gateval3),
    .input4(gateval4), .input5(gateval5), .input6(gateval6), .input7(gateval7), .input8(gateval8),
    .input9(gateval9), .input10(gateval10), .input11(gateval11), .input12(gateval12), .input13(gateval13),
    .input14(gateval14), .input15(gateval15), .input16(gateval16), .input17(gateval17), .input18(gateval18),
    .input19(gateval19), .input20(gateval20), .input21(gateval21), .input22(gateval22), .input23(gateval23),
    .input24(gateval24), .input25(gateval25), .input26(gateval26), .input27(gateval27), .input28(gateval28),
    .input29(gateval29), .input30(gateval30), .input31(gateval31), .input32(gateval32), .input33(gateval33),
    .input34(gateval34), .input35(gateval35), .input36(gateval36), .input37(gateval37), .input38(gateval38),
    .input39(gateval39), .input40(gateval40), .input41(gateval41), .input42(gateval42), .input43(gateval43),
    .input44(gateval44), .input45(gateval45), .input46(gateval46), .input47(gateval47), .input48(gateval48),
    .input49(gateval49), .input50(gateval50), .input51(gateval51), .input52(gateval52), .input53(gateval53),
    .input54(gateval54), .input55(gateval55), .input56(gateval56), .input57(gateval57), .input58(gateval58),
    .input59(gateval59), .input60(gateval60), .input61(gateval61), .input62(gateval62), .input63(gateval63),
    .input64(gateval64), .output1(argval53A), .output2(argval53B));
  muxselector muxselector_54 (
    .direct1(direct54A), .direct2(direct54B), .input1(gateval1), .input2(gateval2), .input3(gateval3),
    .input4(gateval4), .input5(gateval5), .input6(gateval6), .input7(gateval7), .input8(gateval8),
    .input9(gateval9), .input10(gateval10), .input11(gateval11), .input12(gateval12), .input13(gateval13),
    .input14(gateval14), .input15(gateval15), .input16(gateval16), .input17(gateval17), .input18(gateval18),
    .input19(gateval19), .input20(gateval20), .input21(gateval21), .input22(gateval22), .input23(gateval23),
    .input24(gateval24), .input25(gateval25), .input26(gateval26), .input27(gateval27), .input28(gateval28),
    .input29(gateval29), .input30(gateval30), .input31(gateval31), .input32(gateval32), .input33(gateval33),
    .input34(gateval34), .input35(gateval35), .input36(gateval36), .input37(gateval37), .input38(gateval38),
    .input39(gateval39), .input40(gateval40), .input41(gateval41), .input42(gateval42), .input43(gateval43),
    .input44(gateval44), .input45(gateval45), .input46(gateval46), .input47(gateval47), .input48(gateval48),
    .input49(gateval49), .input50(gateval50), .input51(gateval51), .input52(gateval52), .input53(gateval53),
    .input54(gateval54), .input55(gateval55), .input56(gateval56), .input57(gateval57), .input58(gateval58),
    .input59(gateval59), .input60(gateval60), .input61(gateval61), .input62(gateval62), .input63(gateval63),
    .input64(gateval64), .output1(argval54A), .output2(argval54B));
  muxselector muxselector_55 (
    .direct1(direct55A), .direct2(direct55B), .input1(gateval1), .input2(gateval2), .input3(gateval3),
    .input4(gateval4), .input5(gateval5), .input6(gateval6), .input7(gateval7), .input8(gateval8),
    .input9(gateval9), .input10(gateval10), .input11(gateval11), .input12(gateval12), .input13(gateval13),
    .input14(gateval14), .input15(gateval15), .input16(gateval16), .input17(gateval17), .input18(gateval18),
    .input19(gateval19), .input20(gateval20), .input21(gateval21), .input22(gateval22), .input23(gateval23),
    .input24(gateval24), .input25(gateval25), .input26(gateval26), .input27(gateval27), .input28(gateval28),
    .input29(gateval29), .input30(gateval30), .input31(gateval31), .input32(gateval32), .input33(gateval33),
    .input34(gateval34), .input35(gateval35), .input36(gateval36), .input37(gateval37), .input38(gateval38),
    .input39(gateval39), .input40(gateval40), .input41(gateval41), .input42(gateval42), .input43(gateval43),
    .input44(gateval44), .input45(gateval45), .input46(gateval46), .input47(gateval47), .input48(gateval48),
    .input49(gateval49), .input50(gateval50), .input51(gateval51), .input52(gateval52), .input53(gateval53),
    .input54(gateval54), .input55(gateval55), .input56(gateval56), .input57(gateval57), .input58(gateval58),
    .input59(gateval59), .input60(gateval60), .input61(gateval61), .input62(gateval62), .input63(gateval63),
    .input64(gateval64), .output1(argval55A), .output2(argval55B));
  muxselector muxselector_56 (
    .direct1(direct56A), .direct2(direct56B), .input1(gateval1), .input2(gateval2), .input3(gateval3),
    .input4(gateval4), .input5(gateval5), .input6(gateval6), .input7(gateval7), .input8(gateval8),
    .input9(gateval9), .input10(gateval10), .input11(gateval11), .input12(gateval12), .input13(gateval13),
    .input14(gateval14), .input15(gateval15), .input16(gateval16), .input17(gateval17), .input18(gateval18),
    .input19(gateval19), .input20(gateval20), .input21(gateval21), .input22(gateval22), .input23(gateval23),
    .input24(gateval24), .input25(gateval25), .input26(gateval26), .input27(gateval27), .input28(gateval28),
    .input29(gateval29), .input30(gateval30), .input31(gateval31), .input32(gateval32), .input33(gateval33),
    .input34(gateval34), .input35(gateval35), .input36(gateval36), .input37(gateval37), .input38(gateval38),
    .input39(gateval39), .input40(gateval40), .input41(gateval41), .input42(gateval42), .input43(gateval43),
    .input44(gateval44), .input45(gateval45), .input46(gateval46), .input47(gateval47), .input48(gateval48),
    .input49(gateval49), .input50(gateval50), .input51(gateval51), .input52(gateval52), .input53(gateval53),
    .input54(gateval54), .input55(gateval55), .input56(gateval56), .input57(gateval57), .input58(gateval58),
    .input59(gateval59), .input60(gateval60), .input61(gateval61), .input62(gateval62), .input63(gateval63),
    .input64(gateval64), .output1(argval56A), .output2(argval56B));
  muxselector muxselector_57 (
    .direct1(direct57A), .direct2(direct57B), .input1(gateval1), .input2(gateval2), .input3(gateval3),
    .input4(gateval4), .input5(gateval5), .input6(gateval6), .input7(gateval7), .input8(gateval8),
    .input9(gateval9), .input10(gateval10), .input11(gateval11), .input12(gateval12), .input13(gateval13),
    .input14(gateval14), .input15(gateval15), .input16(gateval16), .input17(gateval17), .input18(gateval18),
    .input19(gateval19), .input20(gateval20), .input21(gateval21), .input22(gateval22), .input23(gateval23),
    .input24(gateval24), .input25(gateval25), .input26(gateval26), .input27(gateval27), .input28(gateval28),
    .input29(gateval29), .input30(gateval30), .input31(gateval31), .input32(gateval32), .input33(gateval33),
    .input34(gateval34), .input35(gateval35), .input36(gateval36), .input37(gateval37), .input38(gateval38),
    .input39(gateval39), .input40(gateval40), .input41(gateval41), .input42(gateval42), .input43(gateval43),
    .input44(gateval44), .input45(gateval45), .input46(gateval46), .input47(gateval47), .input48(gateval48),
    .input49(gateval49), .input50(gateval50), .input51(gateval51), .input52(gateval52), .input53(gateval53),
    .input54(gateval54), .input55(gateval55), .input56(gateval56), .input57(gateval57), .input58(gateval58),
    .input59(gateval59), .input60(gateval60), .input61(gateval61), .input62(gateval62), .input63(gateval63),
    .input64(gateval64), .output1(argval57A), .output2(argval57B));
  muxselector muxselector_58 (
    .direct1(direct58A), .direct2(direct58B), .input1(gateval1), .input2(gateval2), .input3(gateval3),
    .input4(gateval4), .input5(gateval5), .input6(gateval6), .input7(gateval7), .input8(gateval8),
    .input9(gateval9), .input10(gateval10), .input11(gateval11), .input12(gateval12), .input13(gateval13),
    .input14(gateval14), .input15(gateval15), .input16(gateval16), .input17(gateval17), .input18(gateval18),
    .input19(gateval19), .input20(gateval20), .input21(gateval21), .input22(gateval22), .input23(gateval23),
    .input24(gateval24), .input25(gateval25), .input26(gateval26), .input27(gateval27), .input28(gateval28),
    .input29(gateval29), .input30(gateval30), .input31(gateval31), .input32(gateval32), .input33(gateval33),
    .input34(gateval34), .input35(gateval35), .input36(gateval36), .input37(gateval37), .input38(gateval38),
    .input39(gateval39), .input40(gateval40), .input41(gateval41), .input42(gateval42), .input43(gateval43),
    .input44(gateval44), .input45(gateval45), .input46(gateval46), .input47(gateval47), .input48(gateval48),
    .input49(gateval49), .input50(gateval50), .input51(gateval51), .input52(gateval52), .input53(gateval53),
    .input54(gateval54), .input55(gateval55), .input56(gateval56), .input57(gateval57), .input58(gateval58),
    .input59(gateval59), .input60(gateval60), .input61(gateval61), .input62(gateval62), .input63(gateval63),
    .input64(gateval64), .output1(argval58A), .output2(argval58B));
  muxselector muxselector_59 (
    .direct1(direct59A), .direct2(direct59B), .input1(gateval1), .input2(gateval2), .input3(gateval3),
    .input4(gateval4), .input5(gateval5), .input6(gateval6), .input7(gateval7), .input8(gateval8),
    .input9(gateval9), .input10(gateval10), .input11(gateval11), .input12(gateval12), .input13(gateval13),
    .input14(gateval14), .input15(gateval15), .input16(gateval16), .input17(gateval17), .input18(gateval18),
    .input19(gateval19), .input20(gateval20), .input21(gateval21), .input22(gateval22), .input23(gateval23),
    .input24(gateval24), .input25(gateval25), .input26(gateval26), .input27(gateval27), .input28(gateval28),
    .input29(gateval29), .input30(gateval30), .input31(gateval31), .input32(gateval32), .input33(gateval33),
    .input34(gateval34), .input35(gateval35), .input36(gateval36), .input37(gateval37), .input38(gateval38),
    .input39(gateval39), .input40(gateval40), .input41(gateval41), .input42(gateval42), .input43(gateval43),
    .input44(gateval44), .input45(gateval45), .input46(gateval46), .input47(gateval47), .input48(gateval48),
    .input49(gateval49), .input50(gateval50), .input51(gateval51), .input52(gateval52), .input53(gateval53),
    .input54(gateval54), .input55(gateval55), .input56(gateval56), .input57(gateval57), .input58(gateval58),
    .input59(gateval59), .input60(gateval60), .input61(gateval61), .input62(gateval62), .input63(gateval63),
    .input64(gateval64), .output1(argval59A), .output2(argval59B));
  muxselector muxselector_60 (
    .direct1(direct60A), .direct2(direct60B), .input1(gateval1), .input2(gateval2), .input3(gateval3),
    .input4(gateval4), .input5(gateval5), .input6(gateval6), .input7(gateval7), .input8(gateval8),
    .input9(gateval9), .input10(gateval10), .input11(gateval11), .input12(gateval12), .input13(gateval13),
    .input14(gateval14), .input15(gateval15), .input16(gateval16), .input17(gateval17), .input18(gateval18),
    .input19(gateval19), .input20(gateval20), .input21(gateval21), .input22(gateval22), .input23(gateval23),
    .input24(gateval24), .input25(gateval25), .input26(gateval26), .input27(gateval27), .input28(gateval28),
    .input29(gateval29), .input30(gateval30), .input31(gateval31), .input32(gateval32), .input33(gateval33),
    .input34(gateval34), .input35(gateval35), .input36(gateval36), .input37(gateval37), .input38(gateval38),
    .input39(gateval39), .input40(gateval40), .input41(gateval41), .input42(gateval42), .input43(gateval43),
    .input44(gateval44), .input45(gateval45), .input46(gateval46), .input47(gateval47), .input48(gateval48),
    .input49(gateval49), .input50(gateval50), .input51(gateval51), .input52(gateval52), .input53(gateval53),
    .input54(gateval54), .input55(gateval55), .input56(gateval56), .input57(gateval57), .input58(gateval58),
    .input59(gateval59), .input60(gateval60), .input61(gateval61), .input62(gateval62), .input63(gateval63),
    .input64(gateval64), .output1(argval60A), .output2(argval60B));
  muxselector muxselector_61 (
    .direct1(direct61A), .direct2(direct61B), .input1(gateval1), .input2(gateval2), .input3(gateval3),
    .input4(gateval4), .input5(gateval5), .input6(gateval6), .input7(gateval7), .input8(gateval8),
    .input9(gateval9), .input10(gateval10), .input11(gateval11), .input12(gateval12), .input13(gateval13),
    .input14(gateval14), .input15(gateval15), .input16(gateval16), .input17(gateval17), .input18(gateval18),
    .input19(gateval19), .input20(gateval20), .input21(gateval21), .input22(gateval22), .input23(gateval23),
    .input24(gateval24), .input25(gateval25), .input26(gateval26), .input27(gateval27), .input28(gateval28),
    .input29(gateval29), .input30(gateval30), .input31(gateval31), .input32(gateval32), .input33(gateval33),
    .input34(gateval34), .input35(gateval35), .input36(gateval36), .input37(gateval37), .input38(gateval38),
    .input39(gateval39), .input40(gateval40), .input41(gateval41), .input42(gateval42), .input43(gateval43),
    .input44(gateval44), .input45(gateval45), .input46(gateval46), .input47(gateval47), .input48(gateval48),
    .input49(gateval49), .input50(gateval50), .input51(gateval51), .input52(gateval52), .input53(gateval53),
    .input54(gateval54), .input55(gateval55), .input56(gateval56), .input57(gateval57), .input58(gateval58),
    .input59(gateval59), .input60(gateval60), .input61(gateval61), .input62(gateval62), .input63(gateval63),
    .input64(gateval64), .output1(argval61A), .output2(argval61B));
  muxselector muxselector_62 (
    .direct1(direct62A), .direct2(direct62B), .input1(gateval1), .input2(gateval2), .input3(gateval3),
    .input4(gateval4), .input5(gateval5), .input6(gateval6), .input7(gateval7), .input8(gateval8),
    .input9(gateval9), .input10(gateval10), .input11(gateval11), .input12(gateval12), .input13(gateval13),
    .input14(gateval14), .input15(gateval15), .input16(gateval16), .input17(gateval17), .input18(gateval18),
    .input19(gateval19), .input20(gateval20), .input21(gateval21), .input22(gateval22), .input23(gateval23),
    .input24(gateval24), .input25(gateval25), .input26(gateval26), .input27(gateval27), .input28(gateval28),
    .input29(gateval29), .input30(gateval30), .input31(gateval31), .input32(gateval32), .input33(gateval33),
    .input34(gateval34), .input35(gateval35), .input36(gateval36), .input37(gateval37), .input38(gateval38),
    .input39(gateval39), .input40(gateval40), .input41(gateval41), .input42(gateval42), .input43(gateval43),
    .input44(gateval44), .input45(gateval45), .input46(gateval46), .input47(gateval47), .input48(gateval48),
    .input49(gateval49), .input50(gateval50), .input51(gateval51), .input52(gateval52), .input53(gateval53),
    .input54(gateval54), .input55(gateval55), .input56(gateval56), .input57(gateval57), .input58(gateval58),
    .input59(gateval59), .input60(gateval60), .input61(gateval61), .input62(gateval62), .input63(gateval63),
    .input64(gateval64), .output1(argval62A), .output2(argval62B));
  muxselector muxselector_63 (
    .direct1(direct63A), .direct2(direct63B), .input1(gateval1), .input2(gateval2), .input3(gateval3),
    .input4(gateval4), .input5(gateval5), .input6(gateval6), .input7(gateval7), .input8(gateval8),
    .input9(gateval9), .input10(gateval10), .input11(gateval11), .input12(gateval12), .input13(gateval13),
    .input14(gateval14), .input15(gateval15), .input16(gateval16), .input17(gateval17), .input18(gateval18),
    .input19(gateval19), .input20(gateval20), .input21(gateval21), .input22(gateval22), .input23(gateval23),
    .input24(gateval24), .input25(gateval25), .input26(gateval26), .input27(gateval27), .input28(gateval28),
    .input29(gateval29), .input30(gateval30), .input31(gateval31), .input32(gateval32), .input33(gateval33),
    .input34(gateval34), .input35(gateval35), .input36(gateval36), .input37(gateval37), .input38(gateval38),
    .input39(gateval39), .input40(gateval40), .input41(gateval41), .input42(gateval42), .input43(gateval43),
    .input44(gateval44), .input45(gateval45), .input46(gateval46), .input47(gateval47), .input48(gateval48),
    .input49(gateval49), .input50(gateval50), .input51(gateval51), .input52(gateval52), .input53(gateval53),
    .input54(gateval54), .input55(gateval55), .input56(gateval56), .input57(gateval57), .input58(gateval58),
    .input59(gateval59), .input60(gateval60), .input61(gateval61), .input62(gateval62), .input63(gateval63),
    .input64(gateval64), .output1(argval63A), .output2(argval63B));
  muxselector muxselector_64 (
    .direct1(direct64A), .direct2(direct64B), .input1(gateval1), .input2(gateval2), .input3(gateval3),
    .input4(gateval4), .input5(gateval5), .input6(gateval6), .input7(gateval7), .input8(gateval8),
    .input9(gateval9), .input10(gateval10), .input11(gateval11), .input12(gateval12), .input13(gateval13),
    .input14(gateval14), .input15(gateval15), .input16(gateval16), .input17(gateval17), .input18(gateval18),
    .input19(gateval19), .input20(gateval20), .input21(gateval21), .input22(gateval22), .input23(gateval23),
    .input24(gateval24), .input25(gateval25), .input26(gateval26), .input27(gateval27), .input28(gateval28),
    .input29(gateval29), .input30(gateval30), .input31(gateval31), .input32(gateval32), .input33(gateval33),
    .input34(gateval34), .input35(gateval35), .input36(gateval36), .input37(gateval37), .input38(gateval38),
    .input39(gateval39), .input40(gateval40), .input41(gateval41), .input42(gateval42), .input43(gateval43),
    .input44(gateval44), .input45(gateval45), .input46(gateval46), .input47(gateval47), .input48(gateval48),
    .input49(gateval49), .input50(gateval50), .input51(gateval51), .input52(gateval52), .input53(gateval53),
    .input54(gateval54), .input55(gateval55), .input56(gateval56), .input57(gateval57), .input58(gateval58),
    .input59(gateval59), .input60(gateval60), .input61(gateval61), .input62(gateval62), .input63(gateval63),
    .input64(gateval64), .output1(argval64A), .output2(argval64B));

  // Other names for the same wires on the sheet: i1[63:0] = gateval1; i2[63:0] = gateval2; i3[63:0] = gateval3;
  //   i4[63:0] = gateval4; i5[63:0] = gateval5; i6[63:0] = gateval6; i7[63:0] = gateval7; i8[63:0] = gateval8;
  //   i9[63:0] = gateval9; i10[63:0] = gateval10; i11[63:0] = gateval11; i12[63:0] = gateval12; i13[63:0] = gateval13;
  //   i14[63:0] = gateval14; i15[63:0] = gateval15; i16[63:0] = gateval16; i17[63:0] = gateval17;
  //   i18[63:0] = gateval18; i19[63:0] = gateval19; i20[63:0] = gateval20; i21[63:0] = gateval21;
  //   i22[63:0] = gateval22; i23[63:0] = gateval23; i24[63:0] = gateval24; i25[63:0] = gateval25;
  //   i26[63:0] = gateval26; i27[63:0] = gateval27; i28[63:0] = gateval28; i29[63:0] = gateval29;
  //   i30[63:0] = gateval30; i31[63:0] = gateval31; i32[63:0] = gateval32; i33[63:0] = gateval33;
  //   i34[63:0] = gateval34; i35[63:0] = gateval35; i36[63:0] = gateval36; i37[63:0] = gateval37;
  //   i38[63:0] = gateval38; i39[63:0] = gateval39; i40[63:0] = gateval40; i41[63:0] = gateval41;
  //   i42[63:0] = gateval42; i43[63:0] = gateval43; i44[63:0] = gateval44; i45[63:0] = gateval45;
  //   i46[63:0] = gateval46; i47[63:0] = gateval47; i48[63:0] = gateval48; i49[63:0] = gateval49;
  //   i50[63:0] = gateval50; i51[63:0] = gateval51; i52[63:0] = gateval52; i53[63:0] = gateval53;
  //   i54[63:0] = gateval54; i55[63:0] = gateval55; i56[63:0] = gateval56; i57[63:0] = gateval57;
  //   i58[63:0] = gateval58; i59[63:0] = gateval59; i60[63:0] = gateval60; i61[63:0] = gateval61;
  //   i62[63:0] = gateval62; i63[63:0] = gateval63; i64[63:0] = gateval64; o1A[63:0] = argval1A; o1B[63:0] = argval1B;
  //   o2A[63:0] = argval2A; o2B[63:0] = argval2B; o3A[63:0] = argval3A; o3B[63:0] = argval3B; o4A[63:0] = argval4A;
  //   o4B[63:0] = argval4B; o5A[63:0] = argval5A; o5B[63:0] = argval5B; o6A[63:0] = argval6A; o6B[63:0] = argval6B;
  //   o7A[63:0] = argval7A; o7B[63:0] = argval7B; o8A[63:0] = argval8A; o8B[63:0] = argval8B; o9A[63:0] = argval9A;
  //   o9B[63:0] = argval9B; o10A[63:0] = argval10A; o10B[63:0] = argval10B; o11A[63:0] = argval11A;
  //   o11B[63:0] = argval11B; o12A[63:0] = argval12A; o12B[63:0] = argval12B; o13A[63:0] = argval13A;
  //   o13B[63:0] = argval13B; o14A[63:0] = argval14A; o14B[63:0] = argval14B; o15A[63:0] = argval15A;
  //   o15B[63:0] = argval15B; o16A[63:0] = argval16A; o16B[63:0] = argval16B; o17A[63:0] = argval17A;
  //   o17B[63:0] = argval17B; o18A[63:0] = argval18A; o18B[63:0] = argval18B; o19A[63:0] = argval19A;
  //   o19B[63:0] = argval19B; o20A[63:0] = argval20A; o20B[63:0] = argval20B; o21A[63:0] = argval21A;
  //   o21B[63:0] = argval21B; o22A[63:0] = argval22A; o22B[63:0] = argval22B; o23A[63:0] = argval23A;
  //   o23B[63:0] = argval23B; o24A[63:0] = argval24A; o24B[63:0] = argval24B; o25A[63:0] = argval25A;
  //   o25B[63:0] = argval25B; o26A[63:0] = argval26A; o26B[63:0] = argval26B; o27A[63:0] = argval27A;
  //   o27B[63:0] = argval27B; o28A[63:0] = argval28A; o28B[63:0] = argval28B; o29A[63:0] = argval29A;
  //   o29B[63:0] = argval29B; o30A[63:0] = argval30A; o30B[63:0] = argval30B; o31A[63:0] = argval31A;
  //   o31B[63:0] = argval31B; o32A[63:0] = argval32A; o32B[63:0] = argval32B; o33A[63:0] = argval33A;
  //   o33B[63:0] = argval33B; o34A[63:0] = argval34A; o34B[63:0] = argval34B; o35A[63:0] = argval35A;
  //   o35B[63:0] = argval35B; o36A[63:0] = argval36A; o36B[63:0] = argval36B; o37A[63:0] = argval37A;
  //   o37B[63:0] = argval37B; o38A[63:0] = argval38A; o38B[63:0] = argval38B; o39A[63:0] = argval39A;
  //   o39B[63:0] = argval39B; o40A[63:0] = argval40A; o40B[63:0] = argval40B; o41A[63:0] = argval41A;
  //   o41B[63:0] = argval41B; o42A[63:0] = argval42A; o42B[63:0] = argval42B; o43A[63:0] = argval43A;
  //   o43B[63:0] = argval43B; o44A[63:0] = argval44A; o44B[63:0] = argval44B; o45A[63:0] = argval45A;
  //   o45B[63:0] = argval45B; o46A[63:0] = argval46A; o46B[63:0] = argval46B; o47A[63:0] = argval47A;
  //   o47B[63:0] = argval47B; o48A[63:0] = argval48A; o48B[63:0] = argval48B; o49A[63:0] = argval49A;
  //   o49B[63:0] = argval49B; o50A[63:0] = argval50A; o50B[63:0] = argval50B; o51A[63:0] = argval51A;
  //   o51B[63:0] = argval51B; o52A[63:0] = argval52A; o52B[63:0] = argval52B; o53A[63:0] = argval53A;
  //   o53B[63:0] = argval53B; o54A[63:0] = argval54A; o54B[63:0] = argval54B; o55A[63:0] = argval55A;
  //   o55B[63:0] = argval55B; o56A[63:0] = argval56A; o56B[63:0] = argval56B; o57A[63:0] = argval57A;
  //   o57B[63:0] = argval57B; o58A[63:0] = argval58A; o58B[63:0] = argval58B; o59A[63:0] = argval59A;
  //   o59B[63:0] = argval59B; o60A[63:0] = argval60A; o60B[63:0] = argval60B; o61A[63:0] = argval61A;
  //   o61B[63:0] = argval61B; o62A[63:0] = argval62A; o62B[63:0] = argval62B; o63A[63:0] = argval63A;
  //   o63B[63:0] = argval63B; o64A[63:0] = argval64A; o64B[63:0] = argval64B
endmodule

module muxselector (
  input  [63:0] direct1,
  input  [63:0] direct2,
  input  [63:0] input1,
  input  [63:0] input2,
  input  [63:0] input3,
  input  [63:0] input4,
  input  [63:0] input5,
  input  [63:0] input6,
  input  [63:0] input7,
  input  [63:0] input8,
  input  [63:0] input9,
  input  [63:0] input10,
  input  [63:0] input11,
  input  [63:0] input12,
  input  [63:0] input13,
  input  [63:0] input14,
  input  [63:0] input15,
  input  [63:0] input16,
  input  [63:0] input17,
  input  [63:0] input18,
  input  [63:0] input19,
  input  [63:0] input20,
  input  [63:0] input21,
  input  [63:0] input22,
  input  [63:0] input23,
  input  [63:0] input24,
  input  [63:0] input25,
  input  [63:0] input26,
  input  [63:0] input27,
  input  [63:0] input28,
  input  [63:0] input29,
  input  [63:0] input30,
  input  [63:0] input31,
  input  [63:0] input32,
  input  [63:0] input33,
  input  [63:0] input34,
  input  [63:0] input35,
  input  [63:0] input36,
  input  [63:0] input37,
  input  [63:0] input38,
  input  [63:0] input39,
  input  [63:0] input40,
  input  [63:0] input41,
  input  [63:0] input42,
  input  [63:0] input43,
  input  [63:0] input44,
  input  [63:0] input45,
  input  [63:0] input46,
  input  [63:0] input47,
  input  [63:0] input48,
  input  [63:0] input49,
  input  [63:0] input50,
  input  [63:0] input51,
  input  [63:0] input52,
  input  [63:0] input53,
  input  [63:0] input54,
  input  [63:0] input55,
  input  [63:0] input56,
  input  [63:0] input57,
  input  [63:0] input58,
  input  [63:0] input59,
  input  [63:0] input60,
  input  [63:0] input61,
  input  [63:0] input62,
  input  [63:0] input63,
  input  [63:0] input64,
  output [63:0] output1,
  output [63:0] output2
);

  wire comparator_1_eq, comparator_2_eq;
  wire [5:0] bitselector_1_out, bitselector_2_out, bitselector_3_out, bitselector_4_out;
  wire [63:0] and_1_out, and_2_out, and_3_out, and_4_out, multiplexer_1_out, multiplexer_2_out,
       multiplexer_3_out, multiplexer_4_out, multiplexer_6_out, multiplexer_8_out, not_1_out, not_2_out;

  assign not_1_out = ~64'h8000000000000000;  // NOT_Gate not_1, 64 bits wide
  assign and_1_out = direct1 & 64'h8000000000000000;  // AND_Gate and_1, 64 bits wide
  assign not_2_out = ~64'h8000000000000000;  // NOT_Gate not_2, 64 bits wide
  assign and_2_out = direct2 & 64'h8000000000000000;  // AND_Gate and_2, 64 bits wide
  Multiplexer #(.width(64)) multiplexer_1 (
    .in0(direct1), .in1(and_3_out), .out(multiplexer_1_out), .sel(comparator_1_eq));
  assign and_3_out = direct1 & not_1_out;  // AND_Gate and_3, 64 bits wide
  Comparator #(.width(64)) comparator_1 (
    .a(and_1_out), .b(64'h8000000000000000), .eq(comparator_1_eq));  // open: gt, lt
  Multiplexer #(.width(64)) multiplexer_2 (
    .in0(direct2), .in1(and_4_out), .out(multiplexer_2_out), .sel(comparator_2_eq));
  assign and_4_out = direct2 & not_2_out;  // AND_Gate and_4, 64 bits wide
  Comparator #(.width(64)) comparator_2 (
    .a(and_2_out), .b(64'h8000000000000000), .eq(comparator_2_eq));  // open: gt, lt
  Multiplexer #(.width(64)) multiplexer_3 (
    .in0(multiplexer_1_out), .in1(multiplexer_6_out), .out(multiplexer_3_out), .sel(comparator_1_eq));
  BitSelector #(.group(6), .width(64)) bitselector_1 (.in(multiplexer_3_out), .out(bitselector_1_out), .sel(4'b0000));
  BitSelector #(.group(6), .width(64)) bitselector_2 (.in(multiplexer_1_out), .out(bitselector_2_out), .sel(4'b0000));
  Multiplexer #(.width(64)) multiplexer_4 (
    .in0(multiplexer_2_out), .in1(multiplexer_8_out), .out(multiplexer_4_out), .sel(comparator_2_eq));
  BitSelector #(.group(6), .width(64)) bitselector_3 (.in(multiplexer_4_out), .out(bitselector_3_out), .sel(4'b0000));
  BitSelector #(.group(6), .width(64)) bitselector_4 (.in(multiplexer_2_out), .out(bitselector_4_out), .sel(4'b0000));
  Multiplexer #(.select(6), .width(64)) multiplexer_5 (
    .in0(input1), .in1(input2), .in2(input3), .in3(input4), .in4(input5), .in5(input6), .in6(input7),
    .in7(input8), .in8(input9), .in9(input10), .in10(input11), .in11(input12), .in12(input13),
    .in13(input14), .in14(input15), .in15(input16), .in16(input17), .in17(input18), .in18(input19),
    .in19(input20), .in20(input21), .in21(input22), .in22(input23), .in23(input24), .in24(input25),
    .in25(input26), .in26(input27), .in27(input28), .in28(input29), .in29(input30), .in30(input31),
    .in31(input32), .in32(input33), .in33(input34), .in34(input35), .in35(input36), .in36(input37),
    .in37(input38), .in38(input39), .in39(input40), .in40(input41), .in41(input42), .in42(input43),
    .in43(input44), .in44(input45), .in45(input46), .in46(input47), .in47(input48), .in48(input49),
    .in49(input50), .in50(input51), .in51(input52), .in52(input53), .in53(input54), .in54(input55),
    .in55(input56), .in56(input57), .in57(input58), .in58(input59), .in59(input60), .in60(input61),
    .in61(input62), .in62(input63), .in63(input64), .out(output1), .sel(bitselector_1_out));
  Multiplexer #(.select(6), .width(64)) multiplexer_6 (
    .in0(input1), .in1(input2), .in2(input3), .in3(input4), .in4(input5), .in5(input6), .in6(input7),
    .in7(input8), .in8(input9), .in9(input10), .in10(input11), .in11(input12), .in12(input13),
    .in13(input14), .in14(input15), .in15(input16), .in16(input17), .in17(input18), .in18(input19),
    .in19(input20), .in20(input21), .in21(input22), .in22(input23), .in23(input24), .in24(input25),
    .in25(input26), .in26(input27), .in27(input28), .in28(input29), .in29(input30), .in30(input31),
    .in31(input32), .in32(input33), .in33(input34), .in34(input35), .in35(input36), .in36(input37),
    .in37(input38), .in38(input39), .in39(input40), .in40(input41), .in41(input42), .in42(input43),
    .in43(input44), .in44(input45), .in45(input46), .in46(input47), .in47(input48), .in48(input49),
    .in49(input50), .in50(input51), .in51(input52), .in52(input53), .in53(input54), .in54(input55),
    .in55(input56), .in56(input57), .in57(input58), .in58(input59), .in59(input60), .in60(input61),
    .in61(input62), .in62(input63), .in63(input64), .out(multiplexer_6_out), .sel(bitselector_2_out));
  Multiplexer #(.select(6), .width(64)) multiplexer_7 (
    .in0(input1), .in1(input2), .in2(input3), .in3(input4), .in4(input5), .in5(input6), .in6(input7),
    .in7(input8), .in8(input9), .in9(input10), .in10(input11), .in11(input12), .in12(input13),
    .in13(input14), .in14(input15), .in15(input16), .in16(input17), .in17(input18), .in18(input19),
    .in19(input20), .in20(input21), .in21(input22), .in22(input23), .in23(input24), .in24(input25),
    .in25(input26), .in26(input27), .in27(input28), .in28(input29), .in29(input30), .in30(input31),
    .in31(input32), .in32(input33), .in33(input34), .in34(input35), .in35(input36), .in36(input37),
    .in37(input38), .in38(input39), .in39(input40), .in40(input41), .in41(input42), .in42(input43),
    .in43(input44), .in44(input45), .in45(input46), .in46(input47), .in47(input48), .in48(input49),
    .in49(input50), .in50(input51), .in51(input52), .in52(input53), .in53(input54), .in54(input55),
    .in55(input56), .in56(input57), .in57(input58), .in58(input59), .in59(input60), .in60(input61),
    .in61(input62), .in62(input63), .in63(input64), .out(output2), .sel(bitselector_3_out));
  Multiplexer #(.select(6), .width(64)) multiplexer_8 (
    .in0(input1), .in1(input2), .in2(input3), .in3(input4), .in4(input5), .in5(input6), .in6(input7),
    .in7(input8), .in8(input9), .in9(input10), .in10(input11), .in11(input12), .in12(input13),
    .in13(input14), .in14(input15), .in15(input16), .in16(input17), .in17(input18), .in18(input19),
    .in19(input20), .in20(input21), .in21(input22), .in22(input23), .in23(input24), .in24(input25),
    .in25(input26), .in26(input27), .in27(input28), .in28(input29), .in29(input30), .in30(input31),
    .in31(input32), .in32(input33), .in33(input34), .in34(input35), .in35(input36), .in36(input37),
    .in37(input38), .in38(input39), .in39(input40), .in40(input41), .in41(input42), .in42(input43),
    .in43(input44), .in44(input45), .in45(input46), .in46(input47), .in47(input48), .in48(input49),
    .in49(input50), .in50(input51), .in51(input52), .in52(input53), .in53(input54), .in54(input55),
    .in55(input56), .in56(input57), .in57(input58), .in58(input59), .in59(input60), .in60(input61),
    .in61(input62), .in62(input63), .in63(input64), .out(multiplexer_8_out), .sel(bitselector_4_out));

  // Other names for the same wires on the sheet: i1[63:0] = input1; i2[63:0] = input2; i3[63:0] = input3;
  //   i4[63:0] = input4; i5[63:0] = input5; i6[63:0] = input6; i7[63:0] = input7; i8[63:0] = input8;
  //   i9[63:0] = input9; i10[63:0] = input10; i11[63:0] = input11; i12[63:0] = input12; i13[63:0] = input13;
  //   i14[63:0] = input14; i15[63:0] = input15; i16[63:0] = input16; i17[63:0] = input17; i18[63:0] = input18;
  //   i19[63:0] = input19; i20[63:0] = input20; i21[63:0] = input21; i22[63:0] = input22; i23[63:0] = input23;
  //   i24[63:0] = input24; i25[63:0] = input25; i26[63:0] = input26; i27[63:0] = input27; i28[63:0] = input28;
  //   i29[63:0] = input29; i30[63:0] = input30; i31[63:0] = input31; i32[63:0] = input32; i33[63:0] = input33;
  //   i34[63:0] = input34; i35[63:0] = input35; i36[63:0] = input36; i37[63:0] = input37; i38[63:0] = input38;
  //   i39[63:0] = input39; i40[63:0] = input40; i41[63:0] = input41; i42[63:0] = input42; i43[63:0] = input43;
  //   i44[63:0] = input44; i45[63:0] = input45; i46[63:0] = input46; i47[63:0] = input47; i48[63:0] = input48;
  //   i49[63:0] = input49; i50[63:0] = input50; i51[63:0] = input51; i52[63:0] = input52; i53[63:0] = input53;
  //   i54[63:0] = input54; i55[63:0] = input55; i56[63:0] = input56; i57[63:0] = input57; i58[63:0] = input58;
  //   i59[63:0] = input59; i60[63:0] = input60; i61[63:0] = input61; i62[63:0] = input62; i63[63:0] = input63;
  //   i64[63:0] = input64
endmodule

module circuittest (
);

  wire [63:0] muxfpga_1_gateval1, muxfpga_1_gateval2, muxfpga_1_gateval3, muxfpga_1_gateval4,
       muxfpga_1_gateval5, muxfpga_1_gateval6;

  Clock clock_1 ();  // open: out
  muxfpga muxfpga_1 (
    .direct1A({64{1'b0}}), .direct1B(64'h1), .isdirect1(1'b0), .opcode1(5'b00110), .initval1(64'h1),
    .direct2A({64{1'b0}}), .isdirect2(1'b0), .opcode2(5'b01100), .direct3A(64'h2), .direct3B(64'h3),
    .isdirect3(1'b0), .opcode3(5'b00110), .initval3(64'h8000000000000000), .direct4A(64'h1),
    .isdirect4(1'b0), .opcode4(5'b11110), .initval4(64'h1), .direct5A(64'h1), .direct5B(64'h2),
    .isdirect5(1'b0), .opcode5({5{1'b1}}), .direct6A(muxfpga_1_gateval1), .direct6B(64'h1), .isdirect6(1'b1),
    .opcode6(5'b00110), .initval6(64'h1), .gateval1(muxfpga_1_gateval1), .gateval2(muxfpga_1_gateval2),
    .gateval3(muxfpga_1_gateval3), .gateval4(muxfpga_1_gateval4), .gateval5(muxfpga_1_gateval5),
    .gateval6(muxfpga_1_gateval6));  // open: direct2B, initval2, direct4B, initval5, direct7A, direct7B, isdirect7, opcode7, initval7, direct8A, direct8B, isdirect8, opcode8, initval8, direct9A, direct9B, isdirect9, opcode9, initval9, direct10A, direct10B, isdirect10, opcode10, initval10, direct11A, direct11B, isdirect11, opcode11, initval11, direct12A, direct12B, isdirect12, opcode12, initval12, direct13A, direct13B, isdirect13, opcode13, initval13, direct14A, direct14B, isdirect14, opcode14, initval14, direct15A, direct15B, isdirect15, opcode15, initval15, direct16A, direct16B, isdirect16, opcode16, initval16, direct17A, direct17B, isdirect17, opcode17, initval17, direct18A, direct18B, isdirect18, opcode18, initval18, direct19A, direct19B, isdirect19, opcode19, initval19, direct20A, direct20B, isdirect20, opcode20, initval20, direct21A, direct21B, isdirect21, opcode21, initval21, direct22A, direct22B, isdirect22, opcode22, initval22, direct23A, direct23B, isdirect23, opcode23, initval23, direct24A, direct24B, isdirect24, opcode24, initval24, direct25A, direct25B, isdirect25, opcode25, initval25, direct26A, direct26B, isdirect26, opcode26, initval26, direct27A, direct27B, isdirect27, opcode27, initval27, direct28A, direct28B, isdirect28, opcode28, initval28, direct29A, direct29B, isdirect29, opcode29, initval29, direct30A, direct30B, isdirect30, opcode30, initval30, direct31A, direct31B, isdirect31, opcode31, initval31, direct32A, direct32B, isdirect32, opcode32, initval32, direct33A, direct33B, isdirect33, opcode33, initval33, direct34A, direct34B, isdirect34, opcode34, initval34, direct35A, direct35B, isdirect35, opcode35, initval35, direct36A, direct36B, isdirect36, opcode36, initval36, direct37A, direct37B, isdirect37, opcode37, initval37, direct38A, direct38B, isdirect38, opcode38, initval38, direct39A, direct39B, isdirect39, opcode39, initval39, direct40A, direct40B, isdirect40, opcode40, initval40, direct41A, direct41B, isdirect41, opcode41, initval41, direct42A, direct42B, isdirect42, opcode42, initval42, direct43A, direct43B, isdirect43, opcode43, initval43, direct44A, direct44B, isdirect44, opcode44, initval44, direct45A, direct45B, isdirect45, opcode45, initval45, direct46A, direct46B, isdirect46, opcode46, initval46, direct47A, direct47B, isdirect47, opcode47, initval47, direct48A, direct48B, isdirect48, opcode48, initval48, direct49A, direct49B, isdirect49, opcode49, initval49, direct50A, direct50B, isdirect50, opcode50, initval50, direct51A, direct51B, isdirect51, opcode51, initval51, direct52A, direct52B, isdirect52, opcode52, initval52, direct53A, direct53B, isdirect53, opcode53, initval53, direct54A, direct54B, isdirect54, opcode54, initval54, direct55A, direct55B, isdirect55, opcode55, initval55, direct56A, direct56B, isdirect56, opcode56, initval56, direct57A, direct57B, isdirect57, opcode57, initval57, direct58A, direct58B, isdirect58, opcode58, initval58, direct59A, direct59B, isdirect59, opcode59, initval59, direct60A, direct60B, isdirect60, opcode60, initval60, direct61A, direct61B, isdirect61, opcode61, initval61, direct62A, direct62B, isdirect62, opcode62, initval62, direct63A, direct63B, isdirect63, opcode63, initval63, direct64A, direct64B, isdirect64, opcode64, initval64, argval1A, argval1B, outpins1A, outpins1B, argval2A, argval2B, outpins2A, outpins2B, argval3A, argval3B, outpins3A, outpins3B, argval4A, argval4B, outpins4A, outpins4B, argval5A, argval5B, outpins5A, outpins5B, argval6A, argval6B, outpins6A, outpins6B, argval7A, argval7B, gateval7, outpins7A, outpins7B, argval8A, argval8B, gateval8, outpins8A, outpins8B, argval9A, argval9B, gateval9, outpins9A, outpins9B, argval10A, argval10B, gateval10, outpins10A, outpins10B, argval11A, argval11B, gateval11, outpins11A, outpins11B, argval12A, argval12B, gateval12, outpins12A, outpins12B, argval13A, argval13B, gateval13, outpins13A, outpins13B, argval14A, argval14B, gateval14, outpins14A, outpins14B, argval15A, argval15B, gateval15, outpins15A, outpins15B, argval16A, argval16B, gateval16, outpins16A, outpins16B, argval17A, argval17B, gateval17, outpins17A, outpins17B, argval18A, argval18B, gateval18, outpins18A, outpins18B, argval19A, argval19B, gateval19, outpins19A, outpins19B, argval20A, argval20B, gateval20, outpins20A, outpins20B, argval21A, argval21B, gateval21, outpins21A, outpins21B, argval22A, argval22B, gateval22, outpins22A, outpins22B, argval23A, argval23B, gateval23, outpins23A, outpins23B, argval24A, argval24B, gateval24, outpins24A, outpins24B, argval25A, argval25B, gateval25, outpins25A, outpins25B, argval26A, argval26B, gateval26, outpins26A, outpins26B, argval27A, argval27B, gateval27, outpins27A, outpins27B, argval28A, argval28B, gateval28, outpins28A, outpins28B, argval29A, argval29B, gateval29, outpins29A, outpins29B, argval30A, argval30B, gateval30, outpins30A, outpins30B, argval31A, argval31B, gateval31, outpins31A, outpins31B, argval32A, argval32B, gateval32, outpins32A, outpins32B, argval33A, argval33B, gateval33, outpins33A, outpins33B, argval34A, argval34B, gateval34, outpins34A, outpins34B, argval35A, argval35B, gateval35, outpins35A, outpins35B, argval36A, argval36B, gateval36, outpins36A, outpins36B, argval37A, argval37B, gateval37, outpins37A, outpins37B, argval38A, argval38B, gateval38, outpins38A, outpins38B, argval39A, argval39B, gateval39, outpins39A, outpins39B, argval40A, argval40B, gateval40, outpins40A, outpins40B, argval41A, argval41B, gateval41, outpins41A, outpins41B, argval42A, argval42B, gateval42, outpins42A, outpins42B, argval43A, argval43B, gateval43, outpins43A, outpins43B, argval44A, argval44B, gateval44, outpins44A, outpins44B, argval45A, argval45B, gateval45, outpins45A, outpins45B, argval46A, argval46B, gateval46, outpins46A, outpins46B, argval47A, argval47B, gateval47, outpins47A, outpins47B, argval48A, argval48B, gateval48, outpins48A, outpins48B, argval49A, argval49B, gateval49, outpins49A, outpins49B, argval50A, argval50B, gateval50, outpins50A, outpins50B, argval51A, argval51B, gateval51, outpins51A, outpins51B, argval52A, argval52B, gateval52, outpins52A, outpins52B, argval53A, argval53B, gateval53, outpins53A, outpins53B, argval54A, argval54B, gateval54, outpins54A, outpins54B, argval55A, argval55B, gateval55, outpins55A, outpins55B, argval56A, argval56B, gateval56, outpins56A, outpins56B, argval57A, argval57B, gateval57, outpins57A, outpins57B, argval58A, argval58B, gateval58, outpins58A, outpins58B, argval59A, argval59B, gateval59, outpins59A, outpins59B, argval60A, argval60B, gateval60, outpins60A, outpins60B, argval61A, argval61B, gateval61, outpins61A, outpins61B, argval62A, argval62B, gateval62, outpins62A, outpins62B, argval63A, argval63B, gateval63, outpins63A, outpins63B, argval64A, argval64B, gateval64, outpins64A, outpins64B
  // Probe on muxfpga_1_gateval1
  // Probe on muxfpga_1_gateval2
  // Probe on muxfpga_1_gateval3
  // Probe on muxfpga_1_gateval4
  // Probe on muxfpga_1_gateval5
  // Probe on muxfpga_1_gateval6
endmodule
