// Logisim project muxflpalu.circ as structural Verilog: 2 circuits, main circuit main
module main (
);

  wire fpcomparator_1_p3;
  wire [63:0] flpadd64_1_output1, fpadder_1_out;

  // Probe on 64'hc01c7d495182a993
  // Probe on 64'h407c83851eb851ec
  FPAdder #(.fpwidth(64)) fpadder_1 (.a(64'hc01c7d495182a993), .b(64'h407c83851eb851ec), .out(fpadder_1_out));
  flpadd64 flpadd64_1 (.input1(64'hc01c7d495182a993), .input2(64'h407c83851eb851ec), .output1(flpadd64_1_output1));
  // Probe on fpadder_1_out
  // Probe on flpadd64_1_output1
  // FPComparator #(.fpwidth(64)) fpcomparator_1: pin names not known; wires that end beside it: fpadder_1_out, flpadd64_1_output1, fpcomparator_1_p3
  LED led_1 (.in(fpcomparator_1_p3));
endmodule

module flpadd64 (
  input  [63:0] input1,
  input  [63:0] input2,
  output [63:0] output1
);

  wire bitfinder_1_found, comparator_1_lt, comparator_3_lt, not_1_out;
  wire [5:0] bitfinder_1_index, bitselector_1_out, bitselector_2_out, negator_4_out, subtractor_3_out;
  wire [10:0] adder_2_out, bit_extender_3_out, multiplexer_3_out, subtractor_1_out, subtractor_2_out;
  wire [51:0] bitselector_3_out;
  wire [52:0] multiplexer_1_out, multiplexer_2_out, shifter_1_out, shifter_2_out;
  wire [63:0] adder_1_out, bit_extender_1_out, bit_extender_2_out, multiplexer_4_out, multiplexer_5_out,
       multiplexer_6_out, multiplexer_7_out, negator_1_out, negator_2_out, negator_3_out, shifter_3_out,
       shifter_4_out;
  wire [63:63] comparator_2_lt;

  // Probe on input1
  // Probe on input2
  BitSelector #(.group(6), .width(11)) bitselector_1 (.in(subtractor_1_out), .out(bitselector_1_out), .sel(1'b0));
  Subtractor #(.width(11)) subtractor_1 (
    .a(input2[62:52]), .b(input1[62:52]), .out(subtractor_1_out));  // open: bin, bout
  Comparator #(.mode("unsigned"), .width(11)) comparator_1 (
    .a(input1[62:52]), .b(input2[62:52]), .lt(comparator_1_lt));  // open: gt, eq
  Subtractor #(.width(11)) subtractor_2 (
    .a(input1[62:52]), .b(input2[62:52]), .out(subtractor_2_out));  // open: bin, bout
  BitSelector #(.group(6), .width(11)) bitselector_2 (.in(subtractor_2_out), .out(bitselector_2_out), .sel(1'b0));
  Multiplexer #(.width(53)) multiplexer_1 (
    .in0({1'b1, input1[51:0]}), .in1(shifter_1_out), .out(multiplexer_1_out), .sel(comparator_1_lt));
  Shifter #(.shift("lr"), .width(53)) shifter_1 (
    .in({1'b1, input1[51:0]}), .\dist (bitselector_1_out), .out(shifter_1_out));
  Shifter #(.shift("lr"), .width(53)) shifter_2 (
    .in({1'b1, input2[51:0]}), .\dist (bitselector_2_out), .out(shifter_2_out));
  Multiplexer #(.width(53)) multiplexer_2 (
    .in0(shifter_2_out), .in1({1'b1, input2[51:0]}), .out(multiplexer_2_out), .sel(comparator_1_lt));
  assign bit_extender_1_out = {{11{1'b0}}, multiplexer_1_out};  // Bit_Extender bit_extender_1
  Multiplexer #(.width(11)) multiplexer_3 (
    .in0(input1[62:52]), .in1(input2[62:52]), .out(multiplexer_3_out), .sel(comparator_1_lt));
  assign bit_extender_2_out = {{11{1'b0}}, multiplexer_2_out};  // Bit_Extender bit_extender_2
  Negator #(.width(64)) negator_1 (.in(bit_extender_1_out), .out(negator_1_out));
  Negator #(.width(64)) negator_2 (.in(bit_extender_2_out), .out(negator_2_out));
  Multiplexer #(.width(64)) multiplexer_4 (
    .in0(bit_extender_1_out), .in1(negator_1_out), .out(multiplexer_4_out), .sel(input1[63]));
  Multiplexer #(.width(64)) multiplexer_5 (
    .in0(bit_extender_2_out), .in1(negator_2_out), .out(multiplexer_5_out), .sel(input2[63]));
  Adder #(.width(64)) adder_1 (.a(multiplexer_4_out), .b(multiplexer_5_out), .out(adder_1_out));  // open: cin, cout
  Multiplexer #(.width(64)) multiplexer_6 (
    .in0(adder_1_out), .in1(negator_3_out), .out(multiplexer_6_out), .sel(comparator_2_lt[63]));
  Negator #(.width(64)) negator_3 (.in(adder_1_out), .out(negator_3_out));
  Comparator #(.width(64)) comparator_2 (.a(adder_1_out), .b({64{1'b0}}), .lt(comparator_2_lt[63]));  // open: gt, eq
  BitFinder #(.\type ("high1"), .width(64)) bitfinder_1 (
    .in(multiplexer_6_out), .index(bitfinder_1_index), .found(bitfinder_1_found));
  not not_1 (not_1_out, bitfinder_1_found);
  Subtractor #(.width(6)) subtractor_3 (
    .a(bitfinder_1_index), .b(6'b110100), .out(subtractor_3_out));  // open: bin, bout
  Comparator #(.width(6)) comparator_3 (.a(subtractor_3_out), .b({6{1'b0}}), .lt(comparator_3_lt));  // open: gt, eq
  Negator #(.width(6)) negator_4 (.in(subtractor_3_out), .out(negator_4_out));
  Shifter #(.shift("lr"), .width(64)) shifter_3 (
    .in(multiplexer_6_out), .\dist (subtractor_3_out), .out(shifter_3_out));
  Shifter #(.width(64)) shifter_4 (.in(multiplexer_6_out), .\dist (negator_4_out), .out(shifter_4_out));
  assign bit_extender_3_out = {{5{subtractor_3_out[5]}}, subtractor_3_out};  // Bit_Extender bit_extender_3
  Multiplexer #(.width(64)) multiplexer_7 (
    .in0(shifter_3_out), .in1(shifter_4_out), .out(multiplexer_7_out), .sel(comparator_3_lt));
  Adder #(.width(11)) adder_2 (.a(multiplexer_3_out), .b(bit_extender_3_out), .out(adder_2_out));  // open: cin, cout
  BitSelector #(.group(52), .width(64)) bitselector_3 (.in(multiplexer_7_out), .out(bitselector_3_out), .sel(1'b0));
  Multiplexer #(.width(64)) multiplexer_8 (
    .in0({comparator_2_lt[63], adder_2_out, bitselector_3_out}), .in1({64{1'b0}}), .out(output1),
    .sel(not_1_out));
  // Probe on output1
endmodule
