// Logisim project muxfpga.circ as structural Verilog: 3 circuits, main circuit main
module main (
);

  wire clock_1_out;
  wire [63:0] fpgaram_1_dx;

  Clock clock_1 (.out(clock_1_out));
  // Probe on fpgaram_1_dx
  fpgaram fpgaram_1 (
    .A(4'b1111), .WE(1'b1), .D(64'hffff), .RY(64'h1), .RZ(64'h2), .OP(4'b1011), .OE(1'b1), .CLK(clock_1_out),
    .DX(fpgaram_1_dx));
endmodule

module logicelement (
  input  [63:0] DY,
  input  [63:0] DZ,
  input  [63:0] RY,
  input  [63:0] RZ,
  input  [3:0] OP,
  input  OE,
  input  [63:0] DX,
  input  WE,
  input  CLK,
  output [63:0] AY,
  output [63:0] AZ,
  output [63:0] D
);

  wire [3:0] register_1_q;
  wire [63:0] and_1_out, nand_1_out, nor_1_out, not_1_out, or_1_out, register_2_q, register_3_q, xnor_1_out,
       xor_1_out;

  Register #(.width(4)) register_1 (.D(OP), .en(OE), .clk(CLK), .Q(register_1_q));  // open: clr
  Register #(.width(64)) register_2 (.D(DX), .en(WE), .clk(CLK), .Q(register_2_q));  // open: clr
  assign xnor_1_out = ~(DZ ^ DY);  // XNOR_Gate xnor_1, 64 bits wide
  assign xor_1_out = DZ ^ DY;  // XOR_Gate xor_1, 64 bits wide
  assign nor_1_out = ~(DZ | DY);  // NOR_Gate nor_1, 64 bits wide
  Register #(.width(64)) register_3 (.D(DY), .en(1'b1), .clk(CLK), .Q(register_3_q));  // open: clr
  assign or_1_out = DZ | DY;  // OR_Gate or_1, 64 bits wide
  assign nand_1_out = ~(DZ & DY);  // NAND_Gate nand_1, 64 bits wide
  assign not_1_out = ~DY;  // NOT_Gate not_1, 64 bits wide
  assign and_1_out = DZ & DY;  // AND_Gate and_1, 64 bits wide
  Multiplexer #(.select(4), .width(64)) multiplexer_1 (
    .in0(register_2_q), .in1(not_1_out), .in2(and_1_out), .in3(or_1_out), .in4(nand_1_out), .in5(nor_1_out),
    .in6(xor_1_out), .in7(xnor_1_out), .in8({64{1'b0}}), .in9(64'h1), .in10(64'hf), .in11(64'hff),
    .in12(64'hffff), .in13(64'hffffffff), .in14({64{1'b1}}), .in15(register_3_q), .out(D), .sel(register_1_q));
  Register #(.width(64)) Y (.D(RY), .en(OE), .clk(CLK), .Q(AY));  // open: clr
  Register #(.width(64)) Z (.D(RZ), .en(OE), .clk(CLK), .Q(AZ));  // open: clr
endmodule

module fpgaram (
  input  [3:0] A,
  input  WE,
  input  [63:0] D,
  input  [63:0] RY,
  input  [63:0] RZ,
  input  [3:0] OP,
  input  OE,
  input  CLK,
  output [63:0] DX
);

  wire demultiplexer_1_out0, demultiplexer_1_out1, demultiplexer_1_out2, demultiplexer_1_out3,
       demultiplexer_1_out4, demultiplexer_1_out5, demultiplexer_1_out6, demultiplexer_1_out7,
       demultiplexer_1_out8, demultiplexer_1_out9, demultiplexer_1_out10, demultiplexer_1_out11,
       demultiplexer_1_out12, demultiplexer_1_out13, demultiplexer_1_out14, demultiplexer_1_out15,
       demultiplexer_2_out0, demultiplexer_2_out1, demultiplexer_2_out2, demultiplexer_2_out3,
       demultiplexer_2_out4, demultiplexer_2_out5, demultiplexer_2_out6, demultiplexer_2_out7,
       demultiplexer_2_out8, demultiplexer_2_out9, demultiplexer_2_out10, demultiplexer_2_out11,
       demultiplexer_2_out12, demultiplexer_2_out13, demultiplexer_2_out14, demultiplexer_2_out15;
  wire [3:0] bitselector_1_out, bitselector_2_out, bitselector_3_out, bitselector_4_out, bitselector_5_out,
       bitselector_6_out, bitselector_7_out, bitselector_8_out, bitselector_9_out, bitselector_10_out,
       bitselector_11_out, bitselector_12_out, bitselector_13_out, bitselector_14_out, bitselector_15_out,
       bitselector_16_out, bitselector_17_out, bitselector_18_out, bitselector_19_out, bitselector_20_out,
       bitselector_21_out, bitselector_22_out, bitselector_23_out, bitselector_24_out, bitselector_25_out,
       bitselector_26_out, bitselector_27_out, bitselector_28_out, bitselector_29_out, bitselector_30_out,
       bitselector_31_out, bitselector_32_out;
  wire [63:0] D00, D0A, D0B, D0C, D0D, D0E, D0F, D01, D02, D03, D04, D05, D06, D07, D08, D09,
       multiplexer_1_out, multiplexer_2_out, multiplexer_3_out, multiplexer_4_out, multiplexer_5_out,
       multiplexer_6_out, multiplexer_7_out, multiplexer_8_out, multiplexer_9_out, multiplexer_10_out,
       multiplexer_11_out, multiplexer_12_out, multiplexer_13_out, multiplexer_14_out, multiplexer_15_out,
       multiplexer_16_out, multiplexer_17_out, multiplexer_18_out, multiplexer_19_out, multiplexer_20_out,
       multiplexer_21_out, multiplexer_22_out, multiplexer_23_out, multiplexer_24_out, multiplexer_25_out,
       multiplexer_26_out, multiplexer_27_out, multiplexer_28_out, multiplexer_29_out, multiplexer_30_out,
       multiplexer_31_out, multiplexer_32_out, R0_ay, R0_az, R1_ay, R1_az, R2_ay, R2_az, R3_ay, R3_az, R4_ay,
       R4_az, R5_ay, R5_az, R6_ay, R6_az, R7_ay, R7_az, R8_ay, R8_az, R9_ay, R9_az, RA_ay, RA_az, RB_ay,
       RB_az, RC_ay, RC_az, RD_ay, RD_az, RE_ay, RE_az, RF_ay, RF_az;

  Demultiplexer #(.select(4)) demultiplexer_1 (
    .out0(demultiplexer_1_out0), .out1(demultiplexer_1_out1), .out2(demultiplexer_1_out2),
    .out3(demultiplexer_1_out3), .out4(demultiplexer_1_out4), .out5(demultiplexer_1_out5),
    .out6(demultiplexer_1_out6), .out7(demultiplexer_1_out7), .out8(demultiplexer_1_out8),
    .out9(demultiplexer_1_out9), .out10(demultiplexer_1_out10), .out11(demultiplexer_1_out11),
    .out12(demultiplexer_1_out12), .out13(demultiplexer_1_out13), .out14(demultiplexer_1_out14),
    .out15(demultiplexer_1_out15), .in(WE), .sel(A));
  Demultiplexer #(.select(4)) demultiplexer_2 (
    .out0(demultiplexer_2_out0), .out1(demultiplexer_2_out1), .out2(demultiplexer_2_out2),
    .out3(demultiplexer_2_out3), .out4(demultiplexer_2_out4), .out5(demultiplexer_2_out5),
    .out6(demultiplexer_2_out6), .out7(demultiplexer_2_out7), .out8(demultiplexer_2_out8),
    .out9(demultiplexer_2_out9), .out10(demultiplexer_2_out10), .out11(demultiplexer_2_out11),
    .out12(demultiplexer_2_out12), .out13(demultiplexer_2_out13), .out14(demultiplexer_2_out14),
    .out15(demultiplexer_2_out15), .in(OE), .sel(A));
  // Probe on D00
  // Probe on D01
  // Probe on D02
  // Probe on D03
  // Probe on D04
  // Probe on D05
  // Probe on D06
  // Probe on D07
  // Probe on D08
  // Probe on D09
  // Probe on D0A
  // Probe on D0B
  // Probe on D0C
  // Probe on D0D
  // Probe on D0E
  // Probe on D0F
  logicelement R0 (
    .DY(multiplexer_1_out), .DZ(multiplexer_17_out), .RY(RY), .RZ(RZ), .OP(OP), .OE(demultiplexer_2_out0),
    .DX(D), .WE(demultiplexer_1_out0), .CLK(CLK), .AY(R0_ay), .AZ(R0_az), .D(D00));
  logicelement R1 (
    .DY(multiplexer_2_out), .DZ(multiplexer_18_out), .RY(RY), .RZ(RZ), .OP(OP), .OE(demultiplexer_2_out1),
    .DX(D), .WE(demultiplexer_1_out1), .CLK(CLK), .AY(R1_ay), .AZ(R1_az), .D(D01));
  logicelement R2 (
    .DY(multiplexer_3_out), .DZ(multiplexer_19_out), .RY(RY), .RZ(RZ), .OP(OP), .OE(demultiplexer_2_out2),
    .DX(D), .WE(demultiplexer_1_out2), .CLK(CLK), .AY(R2_ay), .AZ(R2_az), .D(D02));
  logicelement R3 (
    .DY(multiplexer_4_out), .DZ(multiplexer_20_out), .RY(RY), .RZ(RZ), .OP(OP), .OE(demultiplexer_2_out3),
    .DX(D), .WE(demultiplexer_1_out3), .CLK(CLK), .AY(R3_ay), .AZ(R3_az), .D(D03));
  logicelement R4 (
    .DY(multiplexer_5_out), .DZ(multiplexer_21_out), .RY(RY), .RZ(RZ), .OP(OP), .OE(demultiplexer_2_out4),
    .DX(D), .WE(demultiplexer_1_out4), .CLK(CLK), .AY(R4_ay), .AZ(R4_az), .D(D04));
  logicelement R5 (
    .DY(multiplexer_6_out), .DZ(multiplexer_22_out), .RY(RY), .RZ(RZ), .OP(OP), .OE(demultiplexer_2_out5),
    .DX(D), .WE(demultiplexer_1_out5), .CLK(CLK), .AY(R5_ay), .AZ(R5_az), .D(D05));
  logicelement R6 (
    .DY(multiplexer_7_out), .DZ(multiplexer_23_out), .RY(RY), .RZ(RZ), .OP(OP), .OE(demultiplexer_2_out6),
    .DX(D), .WE(demultiplexer_1_out6), .CLK(CLK), .AY(R6_ay), .AZ(R6_az), .D(D06));
  logicelement R7 (
    .DY(multiplexer_8_out), .DZ(multiplexer_24_out), .RY(RY), .RZ(RZ), .OP(OP), .OE(demultiplexer_2_out7),
    .DX(D), .WE(demultiplexer_1_out7), .CLK(CLK), .AY(R7_ay), .AZ(R7_az), .D(D07));
  logicelement R8 (
    .DY(multiplexer_9_out), .DZ(multiplexer_25_out), .RY(RY), .RZ(RZ), .OP(OP), .OE(demultiplexer_2_out8),
    .DX(D), .WE(demultiplexer_1_out8), .CLK(CLK), .AY(R8_ay), .AZ(R8_az), .D(D08));
  logicelement R9 (
    .DY(multiplexer_10_out), .DZ(multiplexer_26_out), .RY(RY), .RZ(RZ), .OP(OP), .OE(demultiplexer_2_out9),
    .DX(D), .WE(demultiplexer_1_out9), .CLK(CLK), .AY(R9_ay), .AZ(R9_az), .D(D09));
  logicelement RA (
    .DY(multiplexer_11_out), .DZ(multiplexer_27_out), .RY(RY), .RZ(RZ), .OP(OP), .OE(demultiplexer_2_out10),
    .DX(D), .WE(demultiplexer_1_out10), .CLK(CLK), .AY(RA_ay), .AZ(RA_az), .D(D0A));
  logicelement RB (
    .DY(multiplexer_12_out), .DZ(multiplexer_28_out), .RY(RY), .RZ(RZ), .OP(OP), .OE(demultiplexer_2_out11),
    .DX(D), .WE(demultiplexer_1_out11), .CLK(CLK), .AY(RB_ay), .AZ(RB_az), .D(D0B));
  logicelement RC (
    .DY(multiplexer_13_out), .DZ(multiplexer_29_out), .RY(RY), .RZ(RZ), .OP(OP), .OE(demultiplexer_2_out12),
    .DX(D), .WE(demultiplexer_1_out12), .CLK(CLK), .AY(RC_ay), .AZ(RC_az), .D(D0C));
  logicelement RD (
    .DY(multiplexer_14_out), .DZ(multiplexer_30_out), .RY(RY), .RZ(RZ), .OP(OP), .OE(demultiplexer_2_out13),
    .DX(D), .WE(demultiplexer_1_out13), .CLK(CLK), .AY(RD_ay), .AZ(RD_az), .D(D0D));
  logicelement RE (
    .DY(multiplexer_15_out), .DZ(multiplexer_31_out), .RY(RY), .RZ(RZ), .OP(OP), .OE(demultiplexer_2_out14),
    .DX(D), .WE(demultiplexer_1_out14), .CLK(CLK), .AY(RE_ay), .AZ(RE_az), .D(D0E));
  logicelement RF (
    .DY(multiplexer_16_out), .DZ(multiplexer_32_out), .RY(RY), .RZ(RZ), .OP(OP), .OE(demultiplexer_2_out15),
    .DX(D), .WE(demultiplexer_1_out15), .CLK(CLK), .AY(RF_ay), .AZ(RF_az), .D(D0F));
  Multiplexer #(.select(4), .width(64)) multiplexer_1 (
    .in0(D00), .in1(D01), .in2(D02), .in3(D03), .in4(D04), .in5(D05), .in6(D06), .in7(D07), .in8(D08),
    .in9(D09), .in10(D0A), .in11(D0B), .in12(D0C), .in13(D0D), .in14(D0E), .in15(D0F),
    .out(multiplexer_1_out), .sel(bitselector_1_out));
  BitSelector #(.group(4), .width(64)) bitselector_1 (.in(R0_ay), .out(bitselector_1_out), .sel(4'b0000));
  Multiplexer #(.select(4), .width(64)) multiplexer_2 (
    .in0(D00), .in1(D01), .in2(D02), .in3(D03), .in4(D04), .in5(D05), .in6(D06), .in7(D07), .in8(D08),
    .in9(D09), .in10(D0A), .in11(D0B), .in12(D0C), .in13(D0D), .in14(D0E), .in15(D0F),
    .out(multiplexer_2_out), .sel(bitselector_2_out));
  BitSelector #(.group(4), .width(64)) bitselector_2 (.in(R1_ay), .out(bitselector_2_out), .sel(4'b0000));
  Multiplexer #(.select(4), .width(64)) multiplexer_3 (
    .in0(D00), .in1(D01), .in2(D02), .in3(D03), .in4(D04), .in5(D05), .in6(D06), .in7(D07), .in8(D08),
    .in9(D09), .in10(D0A), .in11(D0B), .in12(D0C), .in13(D0D), .in14(D0E), .in15(D0F),
    .out(multiplexer_3_out), .sel(bitselector_3_out));
  BitSelector #(.group(4), .width(64)) bitselector_3 (.in(R2_ay), .out(bitselector_3_out), .sel(4'b0000));
  Multiplexer #(.select(4), .width(64)) multiplexer_4 (
    .in0(D00), .in1(D01), .in2(D02), .in3(D03), .in4(D04), .in5(D05), .in6(D06), .in7(D07), .in8(D08),
    .in9(D09), .in10(D0A), .in11(D0B), .in12(D0C), .in13(D0D), .in14(D0E), .in15(D0F),
    .out(multiplexer_4_out), .sel(bitselector_4_out));
  BitSelector #(.group(4), .width(64)) bitselector_4 (.in(R3_ay), .out(bitselector_4_out), .sel(4'b0000));
  Multiplexer #(.select(4), .width(64)) multiplexer_5 (
    .in0(D00), .in1(D01), .in2(D02), .in3(D03), .in4(D04), .in5(D05), .in6(D06), .in7(D07), .in8(D08),
    .in9(D09), .in10(D0A), .in11(D0B), .in12(D0C), .in13(D0D), .in14(D0E), .in15(D0F),
    .out(multiplexer_5_out), .sel(bitselector_5_out));
  BitSelector #(.group(4), .width(64)) bitselector_5 (.in(R4_ay), .out(bitselector_5_out), .sel(4'b0000));
  Multiplexer #(.select(4), .width(64)) multiplexer_6 (
    .in0(D00), .in1(D01), .in2(D02), .in3(D03), .in4(D04), .in5(D05), .in6(D06), .in7(D07), .in8(D08),
    .in9(D09), .in10(D0A), .in11(D0B), .in12(D0C), .in13(D0D), .in14(D0E), .in15(D0F),
    .out(multiplexer_6_out), .sel(bitselector_6_out));
  BitSelector #(.group(4), .width(64)) bitselector_6 (.in(R5_ay), .out(bitselector_6_out), .sel(4'b0000));
  Multiplexer #(.select(4), .width(64)) multiplexer_7 (
    .in0(D00), .in1(D01), .in2(D02), .in3(D03), .in4(D04), .in5(D05), .in6(D06), .in7(D07), .in8(D08),
    .in9(D09), .in10(D0A), .in11(D0B), .in12(D0C), .in13(D0D), .in14(D0E), .in15(D0F),
    .out(multiplexer_7_out), .sel(bitselector_7_out));
  BitSelector #(.group(4), .width(64)) bitselector_7 (.in(R6_ay), .out(bitselector_7_out), .sel(4'b0000));
  Multiplexer #(.select(4), .width(64)) multiplexer_8 (
    .in0(D00), .in1(D01), .in2(D02), .in3(D03), .in4(D04), .in5(D05), .in6(D06), .in7(D07), .in8(D08),
    .in9(D09), .in10(D0A), .in11(D0B), .in12(D0C), .in13(D0D), .in14(D0E), .in15(D0F),
    .out(multiplexer_8_out), .sel(bitselector_8_out));
  BitSelector #(.group(4), .width(64)) bitselector_8 (.in(R7_ay), .out(bitselector_8_out), .sel(4'b0000));
  Multiplexer #(.select(4), .width(64)) multiplexer_9 (
    .in0(D00), .in1(D01), .in2(D02), .in3(D03), .in4(D04), .in5(D05), .in6(D06), .in7(D07), .in8(D08),
    .in9(D09), .in10(D0A), .in11(D0B), .in12(D0C), .in13(D0D), .in14(D0E), .in15(D0F),
    .out(multiplexer_9_out), .sel(bitselector_9_out));
  BitSelector #(.group(4), .width(64)) bitselector_9 (.in(R8_ay), .out(bitselector_9_out), .sel(4'b0000));
  Multiplexer #(.select(4), .width(64)) multiplexer_10 (
    .in0(D00), .in1(D01), .in2(D02), .in3(D03), .in4(D04), .in5(D05), .in6(D06), .in7(D07), .in8(D08),
    .in9(D09), .in10(D0A), .in11(D0B), .in12(D0C), .in13(D0D), .in14(D0E), .in15(D0F),
    .out(multiplexer_10_out), .sel(bitselector_10_out));
  BitSelector #(.group(4), .width(64)) bitselector_10 (.in(R9_ay), .out(bitselector_10_out), .sel(4'b0000));
  Multiplexer #(.select(4), .width(64)) multiplexer_11 (
    .in0(D00), .in1(D01), .in2(D02), .in3(D03), .in4(D04), .in5(D05), .in6(D06), .in7(D07), .in8(D08),
    .in9(D09), .in10(D0A), .in11(D0B), .in12(D0C), .in13(D0D), .in14(D0E), .in15(D0F),
    .out(multiplexer_11_out), .sel(bitselector_11_out));
  BitSelector #(.group(4), .width(64)) bitselector_11 (.in(RA_ay), .out(bitselector_11_out), .sel(4'b0000));
  Multiplexer #(.select(4), .width(64)) multiplexer_12 (
    .in0(D00), .in1(D01), .in2(D02), .in3(D03), .in4(D04), .in5(D05), .in6(D06), .in7(D07), .in8(D08),
    .in9(D09), .in10(D0A), .in11(D0B), .in12(D0C), .in13(D0D), .in14(D0E), .in15(D0F),
    .out(multiplexer_12_out), .sel(bitselector_12_out));
  BitSelector #(.group(4), .width(64)) bitselector_12 (.in(RB_ay), .out(bitselector_12_out), .sel(4'b0000));
  Multiplexer #(.select(4), .width(64)) multiplexer_13 (
    .in0(D00), .in1(D01), .in2(D02), .in3(D03), .in4(D04), .in5(D05), .in6(D06), .in7(D07), .in8(D08),
    .in9(D09), .in10(D0A), .in11(D0B), .in12(D0C), .in13(D0D), .in14(D0E), .in15(D0F),
    .out(multiplexer_13_out), .sel(bitselector_13_out));
  BitSelector #(.group(4), .width(64)) bitselector_13 (.in(RC_ay), .out(bitselector_13_out), .sel(4'b0000));
  Multiplexer #(.select(4), .width(64)) multiplexer_14 (
    .in0(D00), .in1(D01), .in2(D02), .in3(D03), .in4(D04), .in5(D05), .in6(D06), .in7(D07), .in8(D08),
    .in9(D09), .in10(D0A), .in11(D0B), .in12(D0C), .in13(D0D), .in14(D0E), .in15(D0F),
    .out(multiplexer_14_out), .sel(bitselector_14_out));
  BitSelector #(.group(4), .width(64)) bitselector_14 (.in(RD_ay), .out(bitselector_14_out), .sel(4'b0000));
  Multiplexer #(.select(4), .width(64)) multiplexer_15 (
    .in0(D00), .in1(D01), .in2(D02), .in3(D03), .in4(D04), .in5(D05), .in6(D06), .in7(D07), .in8(D08),
    .in9(D09), .in10(D0A), .in11(D0B), .in12(D0C), .in13(D0D), .in14(D0E), .in15(D0F),
    .out(multiplexer_15_out), .sel(bitselector_15_out));
  BitSelector #(.group(4), .width(64)) bitselector_15 (.in(RE_ay), .out(bitselector_15_out), .sel(4'b0000));
  Multiplexer #(.select(4), .width(64)) multiplexer_16 (
    .in0(D00), .in1(D01), .in2(D02), .in3(D03), .in4(D04), .in5(D05), .in6(D06), .in7(D07), .in8(D08),
    .in9(D09), .in10(D0A), .in11(D0B), .in12(D0C), .in13(D0D), .in14(D0E), .in15(D0F),
    .out(multiplexer_16_out), .sel(bitselector_16_out));
  BitSelector #(.group(4), .width(64)) bitselector_16 (.in(RF_ay), .out(bitselector_16_out), .sel(4'b0000));
  Multiplexer #(.select(4), .width(64)) multiplexer_17 (
    .in0(D00), .in1(D01), .in2(D02), .in3(D03), .in4(D04), .in5(D05), .in6(D06), .in7(D07), .in8(D08),
    .in9(D09), .in10(D0A), .in11(D0B), .in12(D0C), .in13(D0D), .in14(D0E), .in15(D0F),
    .out(multiplexer_17_out), .sel(bitselector_17_out));
  BitSelector #(.group(4), .width(64)) bitselector_17 (.in(R0_az), .out(bitselector_17_out), .sel(4'b0000));
  Multiplexer #(.select(4), .width(64)) multiplexer_18 (
    .in0(D00), .in1(D01), .in2(D02), .in3(D03), .in4(D04), .in5(D05), .in6(D06), .in7(D07), .in8(D08),
    .in9(D09), .in10(D0A), .in11(D0B), .in12(D0C), .in13(D0D), .in14(D0E), .in15(D0F),
    .out(multiplexer_18_out), .sel(bitselector_18_out));
  BitSelector #(.group(4), .width(64)) bitselector_18 (.in(R1_az), .out(bitselector_18_out), .sel(4'b0000));
  Multiplexer #(.select(4), .width(64)) multiplexer_19 (
    .in0(D00), .in1(D01), .in2(D02), .in3(D03), .in4(D04), .in5(D05), .in6(D06), .in7(D07), .in8(D08),
    .in9(D09), .in10(D0A), .in11(D0B), .in12(D0C), .in13(D0D), .in14(D0E), .in15(D0F),
    .out(multiplexer_19_out), .sel(bitselector_19_out));
  BitSelector #(.group(4), .width(64)) bitselector_19 (.in(R2_az), .out(bitselector_19_out), .sel(4'b0000));
  Multiplexer #(.select(4), .width(64)) multiplexer_20 (
    .in0(D00), .in1(D01), .in2(D02), .in3(D03), .in4(D04), .in5(D05), .in6(D06), .in7(D07), .in8(D08),
    .in9(D09), .in10(D0A), .in11(D0B), .in12(D0C), .in13(D0D), .in14(D0E), .in15(D0F),
    .out(multiplexer_20_out), .sel(bitselector_20_out));
  BitSelector #(.group(4), .width(64)) bitselector_20 (.in(R3_az), .out(bitselector_20_out), .sel(4'b0000));
  Multiplexer #(.select(4), .width(64)) multiplexer_21 (
    .in0(D00), .in1(D01), .in2(D02), .in3(D03), .in4(D04), .in5(D05), .in6(D06), .in7(D07), .in8(D08),
    .in9(D09), .in10(D0A), .in11(D0B), .in12(D0C), .in13(D0D), .in14(D0E), .in15(D0F),
    .out(multiplexer_21_out), .sel(bitselector_21_out));
  BitSelector #(.group(4), .width(64)) bitselector_21 (.in(R4_az), .out(bitselector_21_out), .sel(4'b0000));
  Multiplexer #(.select(4), .width(64)) multiplexer_22 (
    .in0(D00), .in1(D01), .in2(D02), .in3(D03), .in4(D04), .in5(D05), .in6(D06), .in7(D07), .in8(D08),
    .in9(D09), .in10(D0A), .in11(D0B), .in12(D0C), .in13(D0D), .in14(D0E), .in15(D0F),
    .out(multiplexer_22_out), .sel(bitselector_22_out));
  BitSelector #(.group(4), .width(64)) bitselector_22 (.in(R5_az), .out(bitselector_22_out), .sel(4'b0000));
  Multiplexer #(.select(4), .width(64)) multiplexer_23 (
    .in0(D00), .in1(D01), .in2(D02), .in3(D03), .in4(D04), .in5(D05), .in6(D06), .in7(D07), .in8(D08),
    .in9(D09), .in10(D0A), .in11(D0B), .in12(D0C), .in13(D0D), .in14(D0E), .in15(D0F),
    .out(multiplexer_23_out), .sel(bitselector_23_out));
  BitSelector #(.group(4), .width(64)) bitselector_23 (.in(R6_az), .out(bitselector_23_out), .sel(4'b0000));
  Multiplexer #(.select(4), .width(64)) multiplexer_24 (
    .in0(D00), .in1(D01), .in2(D02), .in3(D03), .in4(D04), .in5(D05), .in6(D06), .in7(D07), .in8(D08),
    .in9(D09), .in10(D0A), .in11(D0B), .in12(D0C), .in13(D0D), .in14(D0E), .in15(D0F),
    .out(multiplexer_24_out), .sel(bitselector_24_out));
  BitSelector #(.group(4), .width(64)) bitselector_24 (.in(R7_az), .out(bitselector_24_out), .sel(4'b0000));
  Multiplexer #(.select(4), .width(64)) multiplexer_25 (
    .in0(D00), .in1(D01), .in2(D02), .in3(D03), .in4(D04), .in5(D05), .in6(D06), .in7(D07), .in8(D08),
    .in9(D09), .in10(D0A), .in11(D0B), .in12(D0C), .in13(D0D), .in14(D0E), .in15(D0F),
    .out(multiplexer_25_out), .sel(bitselector_25_out));
  BitSelector #(.group(4), .width(64)) bitselector_25 (.in(R8_az), .out(bitselector_25_out), .sel(4'b0000));
  Multiplexer #(.select(4), .width(64)) multiplexer_26 (
    .in0(D00), .in1(D01), .in2(D02), .in3(D03), .in4(D04), .in5(D05), .in6(D06), .in7(D07), .in8(D08),
    .in9(D09), .in10(D0A), .in11(D0B), .in12(D0C), .in13(D0D), .in14(D0E), .in15(D0F),
    .out(multiplexer_26_out), .sel(bitselector_26_out));
  BitSelector #(.group(4), .width(64)) bitselector_26 (.in(R9_az), .out(bitselector_26_out), .sel(4'b0000));
  Multiplexer #(.select(4), .width(64)) multiplexer_27 (
    .in0(D00), .in1(D01), .in2(D02), .in3(D03), .in4(D04), .in5(D05), .in6(D06), .in7(D07), .in8(D08),
    .in9(D09), .in10(D0A), .in11(D0B), .in12(D0C), .in13(D0D), .in14(D0E), .in15(D0F),
    .out(multiplexer_27_out), .sel(bitselector_27_out));
  BitSelector #(.group(4), .width(64)) bitselector_27 (.in(RA_az), .out(bitselector_27_out), .sel(4'b0000));
  Multiplexer #(.select(4), .width(64)) multiplexer_28 (
    .in0(D00), .in1(D01), .in2(D02), .in3(D03), .in4(D04), .in5(D05), .in6(D06), .in7(D07), .in8(D08),
    .in9(D09), .in10(D0A), .in11(D0B), .in12(D0C), .in13(D0D), .in14(D0E), .in15(D0F),
    .out(multiplexer_28_out), .sel(bitselector_28_out));
  BitSelector #(.group(4), .width(64)) bitselector_28 (.in(RB_az), .out(bitselector_28_out), .sel(4'b0000));
  Multiplexer #(.select(4), .width(64)) multiplexer_29 (
    .in0(D00), .in1(D01), .in2(D02), .in3(D03), .in4(D04), .in5(D05), .in6(D06), .in7(D07), .in8(D08),
    .in9(D09), .in10(D0A), .in11(D0B), .in12(D0C), .in13(D0D), .in14(D0E), .in15(D0F),
    .out(multiplexer_29_out), .sel(bitselector_29_out));
  BitSelector #(.group(4), .width(64)) bitselector_29 (.in(RC_az), .out(bitselector_29_out), .sel(4'b0000));
  Multiplexer #(.select(4), .width(64)) multiplexer_30 (
    .in0(D00), .in1(D01), .in2(D02), .in3(D03), .in4(D04), .in5(D05), .in6(D06), .in7(D07), .in8(D08),
    .in9(D09), .in10(D0A), .in11(D0B), .in12(D0C), .in13(D0D), .in14(D0E), .in15(D0F),
    .out(multiplexer_30_out), .sel(bitselector_30_out));
  BitSelector #(.group(4), .width(64)) bitselector_30 (.in(RD_az), .out(bitselector_30_out), .sel(4'b0000));
  Multiplexer #(.select(4), .width(64)) multiplexer_31 (
    .in0(D00), .in1(D01), .in2(D02), .in3(D03), .in4(D04), .in5(D05), .in6(D06), .in7(D07), .in8(D08),
    .in9(D09), .in10(D0A), .in11(D0B), .in12(D0C), .in13(D0D), .in14(D0E), .in15(D0F),
    .out(multiplexer_31_out), .sel(bitselector_31_out));
  BitSelector #(.group(4), .width(64)) bitselector_31 (.in(RE_az), .out(bitselector_31_out), .sel(4'b0000));
  Multiplexer #(.select(4), .width(64)) multiplexer_32 (
    .in0(D00), .in1(D01), .in2(D02), .in3(D03), .in4(D04), .in5(D05), .in6(D06), .in7(D07), .in8(D08),
    .in9(D09), .in10(D0A), .in11(D0B), .in12(D0C), .in13(D0D), .in14(D0E), .in15(D0F),
    .out(multiplexer_32_out), .sel(bitselector_32_out));
  BitSelector #(.group(4), .width(64)) bitselector_32 (.in(RF_az), .out(bitselector_32_out), .sel(4'b0000));
  Multiplexer #(.select(4), .width(64)) multiplexer_33 (
    .in0(D00), .in1(D01), .in2(D02), .in3(D03), .in4(D04), .in5(D05), .in6(D06), .in7(D07), .in8(D08),
    .in9(D09), .in10(D0A), .in11(D0B), .in12(D0C), .in13(D0D), .in14(D0E), .in15(D0F), .out(DX), .sel(A));
endmodule
